// Logisim project 2.circ as structural Verilog: 22 circuits, main circuit ◇单周期RISC-V
// 单周期硬布线控制器
module \单周期硬布线控制器  (
  input  [4:0] OP,
  input  [4:0] Funct,
  input  in_3,
  output [3:0] ALU_OP,
  output uret,
  output MemToReg,
  output ecall,
  output MemWrite,
  output ALU_SRC,
  output RegWrite,
  output S_type,
  output Beq,
  output Bne,
  output Jalr,
  output JAL,
  output sb,
  output auipc,
  output bltu,
  output sltiu,
  output rs1,
  output rs2,
  output CSRRSI,
  output CSRRCI
);

  wire \控制信号自动生成_1_ecall ;

  \运算控制器自动生成  \u_运算控制器自动生成_1  (
    .OP2(OP[0]), .OP3(OP[1]), .OP4(OP[2]), .OP5(OP[3]), .OP6(OP[4]), .F12(Funct[0]), .F13(Funct[1]),
    .F14(Funct[2]), .F25(Funct[3]), .F30(Funct[4]), .S0(ALU_OP[0]), .S1(ALU_OP[1]), .S2(ALU_OP[2]),
    .S3(ALU_OP[3]));
  \控制信号自动生成  \u_控制信号自动生成_1  (
    .OP2(OP[0]), .OP3(OP[1]), .MemToReg(MemToReg), .OP4(OP[2]), .OP5(OP[3]), .OP6(OP[4]), .F12(Funct[0]),
    .MemWrite(MemWrite), .F13(Funct[1]), .F14(Funct[2]), .F25(Funct[3]), .F30(Funct[4]), .ALU_SRC(ALU_SRC),
    .RegWrite(RegWrite), .ecall(\控制信号自动生成_1_ecall ), .S_Type(S_type), .BEQ(Beq), .BNE(Bne), .JALR(Jalr),
    .JAL(JAL), .sb(sb), .auipc(auipc), .bltu(bltu), .sltiu(sltiu), .rs1(rs1), .rs2(rs2), .CSRRSI(CSRRSI),
    .CSRRCI(CSRRCI));
  and and_1 (uret, in_3, \控制信号自动生成_1_ecall );
  and and_2 (ecall, ~in_3, \控制信号自动生成_1_ecall );  // AND_Gate

  // Other names for the same wires on the sheet: IR21 = in_3; OP_CODE[4:0] = OP

  // Notes on the sheet:
  //   运算器控制器，根据指令生成运算器功能选择信号
  //   控制信号生成，产生数据通路需要的其他控制信号
endmodule

// 运算器控制器
module \运算控制器自动生成  (
  input  OP2,
  input  OP3,
  input  OP4,
  input  OP5,
  input  OP6,
  input  F12,
  input  F13,
  input  F14,
  input  F25,
  input  F30,
  output S0,
  output S1,
  output S2,
  output S3
);

  wire and_1_out, and_2_out, and_3_out, and_4_out, and_5_out, and_6_out, and_7_out, and_8_out, and_9_out,
       and_10_out, and_11_out, and_12_out, and_13_out, and_14_out, and_15_out, and_16_out, and_17_out,
       and_18_out, and_19_out, and_20_out, and_21_out, and_22_out, and_23_out, and_24_out, and_25_out,
       and_26_out, and_27_out, and_28_out, and_29_out, and_30_out, and_31_out, and_32_out, and_33_out,
       and_34_out, and_35_out, and_36_out, and_37_out, and_38_out, and_39_out, and_40_out, and_41_out,
       and_42_out, and_43_out, and_44_out, and_45_out, and_46_out, and_47_out, and_48_out, and_49_out,
       not_1_out, not_2_out, not_3_out, not_4_out, not_5_out, not_6_out, not_7_out, not_8_out, not_9_out,
       not_10_out, not_11_out, not_12_out, not_13_out, not_14_out, not_15_out, not_16_out, not_17_out,
       not_18_out, not_19_out, not_20_out, not_21_out, not_22_out, not_23_out, not_24_out, not_25_out,
       not_26_out, not_27_out, not_28_out, not_29_out, not_30_out, not_31_out, not_32_out, not_33_out,
       not_34_out, not_35_out, not_36_out, not_37_out, not_38_out, not_39_out, not_40_out, not_41_out,
       not_42_out, not_43_out, not_44_out, not_45_out, not_46_out, not_47_out, not_48_out, not_49_out,
       not_50_out, not_51_out, not_52_out, not_53_out, not_54_out, not_55_out, not_56_out, not_57_out,
       not_58_out, not_59_out, not_60_out, not_61_out, not_62_out, not_63_out, not_64_out, not_65_out,
       not_66_out, not_67_out, not_68_out, not_69_out, not_70_out, not_71_out, not_72_out, not_73_out,
       not_74_out, not_75_out, not_76_out, not_77_out, not_78_out, not_79_out, not_80_out, not_81_out,
       not_82_out, not_83_out, not_84_out, not_85_out, not_86_out, not_87_out, not_88_out, not_89_out,
       not_90_out, not_91_out, not_92_out, not_93_out, not_94_out, not_95_out, not_96_out, not_97_out,
       not_98_out, not_99_out, not_100_out, not_101_out, not_102_out, not_103_out, not_104_out, not_105_out,
       not_106_out, not_107_out, not_108_out, not_109_out, not_110_out, not_111_out, not_112_out,
       not_113_out, not_114_out, not_115_out, not_116_out, not_117_out, not_118_out, not_119_out,
       not_120_out, not_121_out, not_122_out, not_123_out, not_124_out, not_125_out, not_126_out,
       not_127_out, not_128_out, not_129_out, not_130_out, not_131_out, not_132_out, not_133_out,
       not_134_out, not_135_out, not_136_out, not_137_out, not_138_out, not_139_out, not_140_out,
       not_141_out, not_142_out, not_143_out, not_144_out, not_145_out, not_146_out, not_147_out,
       not_148_out, not_149_out, not_150_out, not_151_out, not_152_out, not_153_out, not_154_out,
       not_155_out, not_156_out, not_157_out, not_158_out, not_159_out, not_160_out, not_161_out,
       not_162_out, not_163_out, not_164_out, not_165_out, not_166_out, not_167_out, not_168_out,
       not_169_out, not_170_out, not_171_out, not_172_out, not_173_out, not_174_out, not_175_out,
       not_176_out, not_177_out, not_178_out, not_179_out, not_180_out, not_181_out, not_182_out,
       not_183_out, not_184_out, not_185_out, not_186_out, not_187_out, not_188_out, not_189_out,
       not_190_out, not_191_out, not_192_out, not_193_out, not_194_out, not_195_out, not_196_out,
       not_197_out, not_198_out, not_199_out, not_200_out, not_201_out, not_202_out, not_203_out,
       not_204_out, not_205_out, not_206_out, not_207_out, not_208_out, not_209_out, not_210_out,
       not_211_out, not_212_out, not_213_out, not_214_out, not_215_out, not_216_out, not_217_out,
       not_218_out, not_219_out, not_220_out, not_221_out, not_222_out, not_223_out, not_224_out,
       not_225_out, not_226_out, not_227_out, not_228_out, not_229_out, not_230_out, not_231_out,
       not_232_out, not_233_out, not_234_out, not_235_out, not_236_out, not_237_out, not_238_out,
       not_239_out, not_240_out, not_241_out, not_242_out, not_243_out, not_244_out, not_245_out,
       not_246_out, not_247_out, not_248_out, not_249_out, not_250_out, not_251_out, not_252_out,
       not_253_out, not_254_out, not_255_out, not_256_out, not_257_out, not_258_out, not_259_out,
       not_260_out, not_261_out, not_262_out, not_263_out, not_264_out, not_265_out, not_266_out,
       not_267_out, not_268_out, not_269_out, not_270_out, not_271_out, not_272_out, not_273_out,
       not_274_out, not_275_out, not_276_out, not_277_out, not_278_out, not_279_out, not_280_out;

  not not_1 (not_1_out, F30);
  not not_2 (not_2_out, F25);
  not not_3 (not_3_out, F14);
  not not_4 (not_4_out, F13);
  not not_5 (not_5_out, F12);
  not not_6 (not_6_out, OP6);
  not not_7 (not_7_out, OP3);
  not not_8 (not_8_out, OP2);
  not not_9 (not_9_out, F30);
  not not_10 (not_10_out, F25);
  not not_11 (not_11_out, OP6);
  not not_12 (not_12_out, OP3);
  not not_13 (not_13_out, OP2);
  not not_14 (not_14_out, F30);
  not not_15 (not_15_out, F25);
  not not_16 (not_16_out, F14);
  not not_17 (not_17_out, F12);
  not not_18 (not_18_out, OP6);
  not not_19 (not_19_out, OP3);
  not not_20 (not_20_out, OP2);
  not not_21 (not_21_out, F14);
  not not_22 (not_22_out, F13);
  not not_23 (not_23_out, F12);
  not not_24 (not_24_out, OP6);
  not not_25 (not_25_out, OP5);
  not not_26 (not_26_out, OP3);
  not not_27 (not_27_out, OP2);
  not not_28 (not_28_out, OP6);
  not not_29 (not_29_out, OP5);
  not not_30 (not_30_out, OP3);
  not not_31 (not_31_out, OP2);
  not not_32 (not_32_out, F13);
  not not_33 (not_33_out, F12);
  not not_34 (not_34_out, OP6);
  not not_35 (not_35_out, OP5);
  not not_36 (not_36_out, OP3);
  not not_37 (not_37_out, OP2);
  not not_38 (not_38_out, F14);
  not not_39 (not_39_out, F12);
  not not_40 (not_40_out, OP6);
  not not_41 (not_41_out, OP5);
  not not_42 (not_42_out, OP3);
  not not_43 (not_43_out, OP2);
  not not_44 (not_44_out, F25);
  not not_45 (not_45_out, F13);
  not not_46 (not_46_out, OP6);
  not not_47 (not_47_out, OP5);
  not not_48 (not_48_out, OP3);
  not not_49 (not_49_out, OP2);
  not not_50 (not_50_out, F14);
  not not_51 (not_51_out, F12);
  not not_52 (not_52_out, OP6);
  not not_53 (not_53_out, OP5);
  not not_54 (not_54_out, OP4);
  not not_55 (not_55_out, OP3);
  not not_56 (not_56_out, OP2);
  not not_57 (not_57_out, F14);
  not not_58 (not_58_out, F12);
  not not_59 (not_59_out, OP6);
  not not_60 (not_60_out, OP4);
  not not_61 (not_61_out, OP3);
  not not_62 (not_62_out, OP2);
  not not_63 (not_63_out, F14);
  not not_64 (not_64_out, F13);
  not not_65 (not_65_out, F12);
  not not_66 (not_66_out, OP3);
  not not_67 (not_67_out, OP2);
  not not_68 (not_68_out, F14);
  not not_69 (not_69_out, F13);
  not not_70 (not_70_out, F12);
  not not_71 (not_71_out, OP4);
  not not_72 (not_72_out, OP3);
  not not_73 (not_73_out, OP2);
  not not_74 (not_74_out, F14);
  not not_75 (not_75_out, F13);
  not not_76 (not_76_out, OP4);
  not not_77 (not_77_out, OP3);
  not not_78 (not_78_out, OP2);
  not not_79 (not_79_out, F14);
  not not_80 (not_80_out, F13);
  not not_81 (not_81_out, F12);
  not not_82 (not_82_out, OP4);
  not not_83 (not_83_out, OP3);
  not not_84 (not_84_out, F14);
  not not_85 (not_85_out, F13);
  not not_86 (not_86_out, F12);
  not not_87 (not_87_out, OP6);
  not not_88 (not_88_out, OP4);
  not not_89 (not_89_out, OP3);
  not not_90 (not_90_out, OP2);
  not not_91 (not_91_out, OP6);
  not not_92 (not_92_out, OP5);
  not not_93 (not_93_out, OP3);
  not not_94 (not_94_out, F25);
  not not_95 (not_95_out, F14);
  not not_96 (not_96_out, F13);
  not not_97 (not_97_out, F12);
  not not_98 (not_98_out, OP6);
  not not_99 (not_99_out, OP3);
  not not_100 (not_100_out, OP2);
  not not_101 (not_101_out, F30);
  not not_102 (not_102_out, F25);
  not not_103 (not_103_out, OP6);
  not not_104 (not_104_out, OP3);
  not not_105 (not_105_out, OP2);
  not not_106 (not_106_out, F30);
  not not_107 (not_107_out, F25);
  not not_108 (not_108_out, F14);
  not not_109 (not_109_out, F12);
  not not_110 (not_110_out, OP6);
  not not_111 (not_111_out, OP3);
  not not_112 (not_112_out, OP2);
  not not_113 (not_113_out, OP6);
  not not_114 (not_114_out, OP5);
  not not_115 (not_115_out, OP3);
  not not_116 (not_116_out, OP2);
  not not_117 (not_117_out, F14);
  not not_118 (not_118_out, F12);
  not not_119 (not_119_out, OP6);
  not not_120 (not_120_out, OP5);
  not not_121 (not_121_out, OP3);
  not not_122 (not_122_out, OP2);
  not not_123 (not_123_out, F30);
  not not_124 (not_124_out, F25);
  not not_125 (not_125_out, F13);
  not not_126 (not_126_out, OP6);
  not not_127 (not_127_out, OP5);
  not not_128 (not_128_out, OP3);
  not not_129 (not_129_out, OP2);
  not not_130 (not_130_out, F14);
  not not_131 (not_131_out, F13);
  not not_132 (not_132_out, F12);
  not not_133 (not_133_out, OP3);
  not not_134 (not_134_out, OP2);
  not not_135 (not_135_out, F14);
  not not_136 (not_136_out, F13);
  not not_137 (not_137_out, F12);
  not not_138 (not_138_out, OP4);
  not not_139 (not_139_out, OP3);
  not not_140 (not_140_out, OP2);
  not not_141 (not_141_out, F14);
  not not_142 (not_142_out, F13);
  not not_143 (not_143_out, OP4);
  not not_144 (not_144_out, OP3);
  not not_145 (not_145_out, OP2);
  not not_146 (not_146_out, F30);
  not not_147 (not_147_out, F25);
  not not_148 (not_148_out, F14);
  not not_149 (not_149_out, F13);
  not not_150 (not_150_out, F12);
  not not_151 (not_151_out, OP6);
  not not_152 (not_152_out, OP3);
  not not_153 (not_153_out, OP2);
  not not_154 (not_154_out, F25);
  not not_155 (not_155_out, F14);
  not not_156 (not_156_out, F13);
  not not_157 (not_157_out, F12);
  not not_158 (not_158_out, OP6);
  not not_159 (not_159_out, OP3);
  not not_160 (not_160_out, OP2);
  not not_161 (not_161_out, F30);
  not not_162 (not_162_out, F25);
  not not_163 (not_163_out, OP6);
  not not_164 (not_164_out, OP3);
  not not_165 (not_165_out, OP2);
  not not_166 (not_166_out, F30);
  not not_167 (not_167_out, F25);
  not not_168 (not_168_out, F14);
  not not_169 (not_169_out, OP6);
  not not_170 (not_170_out, OP3);
  not not_171 (not_171_out, OP2);
  not not_172 (not_172_out, F14);
  not not_173 (not_173_out, F13);
  not not_174 (not_174_out, F12);
  not not_175 (not_175_out, OP6);
  not not_176 (not_176_out, OP5);
  not not_177 (not_177_out, OP3);
  not not_178 (not_178_out, OP2);
  not not_179 (not_179_out, OP6);
  not not_180 (not_180_out, OP5);
  not not_181 (not_181_out, OP3);
  not not_182 (not_182_out, OP2);
  not not_183 (not_183_out, F14);
  not not_184 (not_184_out, F12);
  not not_185 (not_185_out, OP6);
  not not_186 (not_186_out, OP5);
  not not_187 (not_187_out, OP4);
  not not_188 (not_188_out, OP3);
  not not_189 (not_189_out, OP2);
  not not_190 (not_190_out, F14);
  not not_191 (not_191_out, F12);
  not not_192 (not_192_out, OP6);
  not not_193 (not_193_out, OP4);
  not not_194 (not_194_out, OP3);
  not not_195 (not_195_out, OP2);
  not not_196 (not_196_out, F14);
  not not_197 (not_197_out, F13);
  not not_198 (not_198_out, F12);
  not not_199 (not_199_out, OP4);
  not not_200 (not_200_out, OP3);
  not not_201 (not_201_out, F14);
  not not_202 (not_202_out, F13);
  not not_203 (not_203_out, F12);
  not not_204 (not_204_out, OP6);
  not not_205 (not_205_out, OP4);
  not not_206 (not_206_out, OP3);
  not not_207 (not_207_out, OP2);
  not not_208 (not_208_out, OP6);
  not not_209 (not_209_out, OP5);
  not not_210 (not_210_out, OP3);
  not not_211 (not_211_out, F14);
  not not_212 (not_212_out, OP6);
  not not_213 (not_213_out, OP5);
  not not_214 (not_214_out, OP3);
  not not_215 (not_215_out, OP2);
  not not_216 (not_216_out, F12);
  not not_217 (not_217_out, OP4);
  not not_218 (not_218_out, OP3);
  not not_219 (not_219_out, OP2);
  not not_220 (not_220_out, F30);
  not not_221 (not_221_out, F25);
  not not_222 (not_222_out, F12);
  not not_223 (not_223_out, OP6);
  not not_224 (not_224_out, OP3);
  not not_225 (not_225_out, OP2);
  not not_226 (not_226_out, F30);
  not not_227 (not_227_out, F25);
  not not_228 (not_228_out, F14);
  not not_229 (not_229_out, F12);
  not not_230 (not_230_out, OP6);
  not not_231 (not_231_out, OP3);
  not not_232 (not_232_out, OP2);
  not not_233 (not_233_out, F30);
  not not_234 (not_234_out, F25);
  not not_235 (not_235_out, F14);
  not not_236 (not_236_out, OP6);
  not not_237 (not_237_out, OP3);
  not not_238 (not_238_out, OP2);
  not not_239 (not_239_out, F12);
  not not_240 (not_240_out, OP6);
  not not_241 (not_241_out, OP5);
  not not_242 (not_242_out, OP3);
  not not_243 (not_243_out, OP2);
  not not_244 (not_244_out, F13);
  not not_245 (not_245_out, F12);
  not not_246 (not_246_out, OP6);
  not not_247 (not_247_out, OP5);
  not not_248 (not_248_out, OP3);
  not not_249 (not_249_out, OP2);
  not not_250 (not_250_out, F14);
  not not_251 (not_251_out, F12);
  not not_252 (not_252_out, OP6);
  not not_253 (not_253_out, OP5);
  not not_254 (not_254_out, OP3);
  not not_255 (not_255_out, OP2);
  not not_256 (not_256_out, F14);
  not not_257 (not_257_out, F13);
  not not_258 (not_258_out, F12);
  not not_259 (not_259_out, OP3);
  not not_260 (not_260_out, OP2);
  not not_261 (not_261_out, F14);
  not not_262 (not_262_out, F13);
  not not_263 (not_263_out, F12);
  not not_264 (not_264_out, OP4);
  not not_265 (not_265_out, OP3);
  not not_266 (not_266_out, OP2);
  not not_267 (not_267_out, F14);
  not not_268 (not_268_out, F13);
  not not_269 (not_269_out, OP4);
  not not_270 (not_270_out, OP3);
  not not_271 (not_271_out, OP2);
  not not_272 (not_272_out, F14);
  not not_273 (not_273_out, OP6);
  not not_274 (not_274_out, OP5);
  not not_275 (not_275_out, OP3);
  not not_276 (not_276_out, OP2);
  not not_277 (not_277_out, F12);
  not not_278 (not_278_out, OP4);
  not not_279 (not_279_out, OP3);
  not not_280 (not_280_out, OP2);
  and and_1 (and_1_out, not_1_out, not_2_out, not_3_out, not_4_out, not_5_out, not_6_out, OP5, OP4, not_7_out, not_8_out);
  and and_2 (and_2_out, not_9_out, not_10_out, F14, F13, F12, not_11_out, OP5, OP4, not_12_out, not_13_out);
  and and_3 (and_3_out, not_14_out, not_15_out, not_16_out, F13, not_17_out, not_18_out, OP5, OP4, not_19_out, not_20_out);
  and and_4 (and_4_out, not_21_out, not_22_out, not_23_out, not_24_out, not_25_out, OP4, not_26_out, not_27_out);
  and and_5 (and_5_out, F14, F13, F12, not_28_out, not_29_out, OP4, not_30_out, not_31_out);
  and and_6 (and_6_out, F14, not_32_out, not_33_out, not_34_out, not_35_out, OP4, not_36_out, not_37_out);
  and and_7 (and_7_out, not_38_out, F13, not_39_out, not_40_out, not_41_out, OP4, not_42_out, not_43_out);
  and and_8 (and_8_out, F30, not_44_out, F14, not_45_out, F12, not_46_out, not_47_out, OP4, not_48_out, not_49_out);
  and and_9 (and_9_out, not_50_out, F13, not_51_out, not_52_out, not_53_out, not_54_out, not_55_out, not_56_out);
  and and_10 (and_10_out, not_57_out, F13, not_58_out, not_59_out, OP5, not_60_out, not_61_out, not_62_out);
  and and_11 (and_11_out, not_63_out, not_64_out, not_65_out, OP6, OP5, OP4, not_66_out, not_67_out);
  and and_12 (and_12_out, not_68_out, not_69_out, not_70_out, OP6, OP5, not_71_out, not_72_out, not_73_out);
  and and_13 (and_13_out, not_74_out, not_75_out, F12, OP6, OP5, not_76_out, not_77_out, not_78_out);
  and and_14 (and_14_out, not_79_out, not_80_out, not_81_out, OP6, OP5, not_82_out, not_83_out, OP2);
  and and_15 (and_15_out, not_84_out, not_85_out, not_86_out, not_87_out, OP5, not_88_out, not_89_out, not_90_out);
  and and_16 (and_16_out, not_91_out, not_92_out, OP4, not_93_out, OP2);
  and and_17 (and_17_out, F30, not_94_out, not_95_out, not_96_out, not_97_out, not_98_out, OP5, OP4, not_99_out, not_100_out);
  and and_18 (and_18_out, not_101_out, not_102_out, F14, F13, F12, not_103_out, OP5, OP4, not_104_out, not_105_out);
  and and_19 (and_19_out, not_106_out, not_107_out, not_108_out, F13, not_109_out, not_110_out, OP5, OP4, not_111_out, not_112_out);
  and and_20 (and_20_out, F14, F13, F12, not_113_out, not_114_out, OP4, not_115_out, not_116_out);
  and and_21 (and_21_out, not_117_out, F13, not_118_out, not_119_out, not_120_out, OP4, not_121_out, not_122_out);
  and and_22 (and_22_out, not_123_out, not_124_out, F14, not_125_out, F12, not_126_out, not_127_out, OP4, not_128_out, not_129_out);
  and and_23 (and_23_out, not_130_out, not_131_out, not_132_out, OP6, OP5, OP4, not_133_out, not_134_out);
  and and_24 (and_24_out, not_135_out, not_136_out, not_137_out, OP6, OP5, not_138_out, not_139_out, not_140_out);
  and and_25 (and_25_out, not_141_out, not_142_out, F12, OP6, OP5, not_143_out, not_144_out, not_145_out);
  and and_26 (and_26_out, not_146_out, not_147_out, not_148_out, not_149_out, not_150_out, not_151_out, OP5, OP4, not_152_out, not_153_out);
  and and_27 (and_27_out, F30, not_154_out, not_155_out, not_156_out, not_157_out, not_158_out, OP5, OP4, not_159_out, not_160_out);
  and and_28 (and_28_out, not_161_out, not_162_out, F14, F13, F12, not_163_out, OP5, OP4, not_164_out, not_165_out);
  and and_29 (and_29_out, not_166_out, not_167_out, not_168_out, F13, F12, not_169_out, OP5, OP4, not_170_out, not_171_out);
  and and_30 (and_30_out, not_172_out, not_173_out, not_174_out, not_175_out, not_176_out, OP4, not_177_out, not_178_out);
  and and_31 (and_31_out, F14, F13, F12, not_179_out, not_180_out, OP4, not_181_out, not_182_out);
  and and_32 (and_32_out, not_183_out, F13, not_184_out, not_185_out, not_186_out, not_187_out, not_188_out, not_189_out);
  and and_33 (and_33_out, not_190_out, F13, not_191_out, not_192_out, OP5, not_193_out, not_194_out, not_195_out);
  and and_34 (and_34_out, not_196_out, not_197_out, not_198_out, OP6, OP5, not_199_out, not_200_out, OP2);
  and and_35 (and_35_out, not_201_out, not_202_out, not_203_out, not_204_out, OP5, not_205_out, not_206_out, not_207_out);
  and and_36 (and_36_out, not_208_out, not_209_out, OP4, not_210_out, OP2);
  and and_37 (and_37_out, not_211_out, F13, F12, not_212_out, not_213_out, OP4, not_214_out, not_215_out);
  and and_38 (and_38_out, F14, F13, not_216_out, OP6, OP5, not_217_out, not_218_out, not_219_out);
  and and_39 (and_39_out, not_220_out, not_221_out, F14, F13, not_222_out, not_223_out, OP5, OP4, not_224_out, not_225_out);
  and and_40 (and_40_out, not_226_out, not_227_out, not_228_out, F13, not_229_out, not_230_out, OP5, OP4, not_231_out, not_232_out);
  and and_41 (and_41_out, not_233_out, not_234_out, not_235_out, F13, F12, not_236_out, OP5, OP4, not_237_out, not_238_out);
  and and_42 (and_42_out, F14, F13, not_239_out, not_240_out, not_241_out, OP4, not_242_out, not_243_out);
  and and_43 (and_43_out, F14, not_244_out, not_245_out, not_246_out, not_247_out, OP4, not_248_out, not_249_out);
  and and_44 (and_44_out, not_250_out, F13, not_251_out, not_252_out, not_253_out, OP4, not_254_out, not_255_out);
  and and_45 (and_45_out, not_256_out, not_257_out, not_258_out, OP6, OP5, OP4, not_259_out, not_260_out);
  and and_46 (and_46_out, not_261_out, not_262_out, not_263_out, OP6, OP5, not_264_out, not_265_out, not_266_out);
  and and_47 (and_47_out, not_267_out, not_268_out, F12, OP6, OP5, not_269_out, not_270_out, not_271_out);
  and and_48 (and_48_out, not_272_out, F13, F12, not_273_out, not_274_out, OP4, not_275_out, not_276_out);
  and and_49 (and_49_out, F14, F13, not_277_out, OP6, OP5, not_278_out, not_279_out, not_280_out);
  or or_1 (S0, and_1_out, and_2_out, and_3_out, and_4_out, and_5_out, and_6_out, and_7_out, and_8_out, and_9_out, and_10_out, and_11_out, and_12_out, and_13_out, and_14_out, and_15_out, and_16_out);
  or or_2 (S1, and_17_out, and_18_out, and_19_out, and_20_out, and_21_out, and_22_out, and_23_out, and_24_out, and_25_out);
  or or_3 (S2, and_26_out, and_27_out, and_28_out, and_29_out, and_30_out, and_31_out, and_32_out, and_33_out, and_34_out, and_35_out, and_36_out, and_37_out, and_38_out);
  or or_4 (S3, and_39_out, and_40_out, and_41_out, and_42_out, and_43_out, and_44_out, and_45_out, and_46_out, and_47_out, and_48_out, and_49_out);
endmodule

// 控制信号生成
module \控制信号自动生成  (
  input  OP2,
  input  OP3,
  input  OP4,
  input  OP5,
  input  OP6,
  input  F12,
  input  F13,
  input  F14,
  input  F25,
  input  F30,
  output MemToReg,
  output MemWrite,
  output ALU_SRC,
  output RegWrite,
  output ecall,
  output S_Type,
  output BEQ,
  output BNE,
  output JALR,
  output JAL,
  output sb,
  output auipc,
  output bltu,
  output sltiu,
  output rs1,
  output rs2,
  output CSRRSI,
  output CSRRCI
);

  wire and_3_out, and_4_out, and_5_out, and_6_out, and_7_out, and_8_out, and_9_out, and_10_out, and_11_out,
       and_12_out, and_13_out, and_14_out, and_15_out, and_16_out, and_17_out, and_18_out, and_19_out,
       and_20_out, and_21_out, and_22_out, and_23_out, and_24_out, and_25_out, and_26_out, and_27_out,
       and_28_out, and_29_out, and_30_out, and_41_out, and_42_out, and_43_out, and_44_out, and_45_out,
       and_46_out, and_47_out, and_48_out, and_49_out, and_50_out, and_51_out, and_52_out, and_53_out,
       and_54_out, and_55_out, and_56_out, and_57_out, not_1_out, not_2_out, not_3_out, not_4_out, not_5_out,
       not_6_out, not_7_out, not_8_out, not_9_out, not_10_out, not_11_out, not_12_out, not_13_out,
       not_14_out, not_15_out, not_16_out, not_17_out, not_18_out, not_19_out, not_20_out, not_21_out,
       not_22_out, not_23_out, not_24_out, not_25_out, not_26_out, not_27_out, not_28_out, not_29_out,
       not_30_out, not_31_out, not_32_out, not_33_out, not_34_out, not_35_out, not_36_out, not_37_out,
       not_38_out, not_39_out, not_40_out, not_41_out, not_42_out, not_43_out, not_44_out, not_45_out,
       not_46_out, not_47_out, not_48_out, not_49_out, not_50_out, not_51_out, not_52_out, not_53_out,
       not_54_out, not_55_out, not_56_out, not_57_out, not_58_out, not_59_out, not_60_out, not_61_out,
       not_62_out, not_63_out, not_64_out, not_65_out, not_66_out, not_67_out, not_68_out, not_69_out,
       not_70_out, not_71_out, not_72_out, not_73_out, not_74_out, not_75_out, not_76_out, not_77_out,
       not_78_out, not_79_out, not_80_out, not_81_out, not_82_out, not_83_out, not_84_out, not_85_out,
       not_86_out, not_87_out, not_88_out, not_89_out, not_90_out, not_91_out, not_92_out, not_93_out,
       not_94_out, not_95_out, not_96_out, not_97_out, not_98_out, not_99_out, not_100_out, not_101_out,
       not_102_out, not_103_out, not_104_out, not_105_out, not_106_out, not_107_out, not_108_out,
       not_109_out, not_110_out, not_111_out, not_112_out, not_113_out, not_114_out, not_115_out,
       not_116_out, not_117_out, not_118_out, not_119_out, not_120_out, not_121_out, not_122_out,
       not_123_out, not_124_out, not_125_out, not_126_out, not_127_out, not_128_out, not_129_out,
       not_130_out, not_131_out, not_132_out, not_133_out, not_134_out, not_135_out, not_136_out,
       not_137_out, not_138_out, not_139_out, not_140_out, not_141_out, not_142_out, not_143_out,
       not_144_out, not_145_out, not_146_out, not_147_out, not_148_out, not_149_out, not_150_out,
       not_151_out, not_152_out, not_153_out, not_154_out, not_155_out, not_156_out, not_157_out,
       not_158_out, not_159_out, not_160_out, not_161_out, not_162_out, not_163_out, not_164_out,
       not_165_out, not_166_out, not_167_out, not_168_out, not_169_out, not_170_out, not_171_out,
       not_172_out, not_173_out, not_174_out, not_175_out, not_176_out, not_177_out, not_178_out,
       not_179_out, not_180_out, not_181_out, not_182_out, not_183_out, not_184_out, not_185_out,
       not_186_out, not_187_out, not_188_out, not_189_out, not_190_out, not_191_out, not_192_out,
       not_193_out, not_194_out, not_195_out, not_196_out, not_197_out, not_198_out, not_199_out,
       not_200_out, not_201_out, not_202_out, not_203_out, not_204_out, not_205_out, not_206_out,
       not_207_out, not_208_out, not_209_out, not_210_out, not_211_out, not_212_out, not_213_out,
       not_214_out, not_215_out, not_216_out, not_217_out, not_218_out, not_219_out, not_220_out,
       not_221_out, not_222_out, not_223_out, not_224_out, not_225_out, not_226_out, not_227_out,
       not_228_out, not_229_out, not_230_out, not_231_out, not_232_out, not_233_out, not_234_out,
       not_235_out, not_236_out, not_237_out, not_238_out, not_239_out, not_240_out, not_241_out,
       not_242_out, not_243_out, not_244_out, not_245_out, not_246_out, not_247_out, not_248_out,
       not_249_out, not_250_out, not_251_out, not_252_out, not_253_out, not_254_out, not_255_out,
       not_256_out, not_257_out, not_258_out, not_259_out, not_260_out, not_261_out, not_262_out,
       not_263_out, not_264_out, not_265_out, not_266_out, not_267_out, not_268_out, not_269_out,
       not_270_out, not_271_out, not_272_out, not_273_out, not_274_out, not_275_out, not_276_out,
       not_277_out, not_278_out, not_279_out, not_280_out, not_281_out, not_282_out, not_283_out,
       not_284_out, not_285_out, not_286_out, not_287_out, not_288_out, not_289_out, not_290_out,
       not_291_out, not_292_out, not_293_out, not_294_out, not_295_out;

  not not_1 (not_1_out, OP2);
  not not_2 (not_2_out, OP3);
  not not_3 (not_3_out, OP4);
  not not_4 (not_4_out, OP5);
  not not_5 (not_5_out, OP6);
  not not_6 (not_6_out, F12);
  not not_7 (not_7_out, F14);
  not not_8 (not_8_out, OP2);
  not not_9 (not_9_out, OP3);
  not not_10 (not_10_out, OP4);
  not not_11 (not_11_out, OP6);
  not not_12 (not_12_out, F12);
  not not_13 (not_13_out, F14);
  not not_14 (not_14_out, OP2);
  not not_15 (not_15_out, OP3);
  not not_16 (not_16_out, OP4);
  not not_17 (not_17_out, OP6);
  not not_18 (not_18_out, F12);
  not not_19 (not_19_out, F14);
  not not_20 (not_20_out, OP2);
  not not_21 (not_21_out, OP3);
  not not_22 (not_22_out, OP4);
  not not_23 (not_23_out, OP6);
  not not_24 (not_24_out, F12);
  not not_25 (not_25_out, F14);
  not not_26 (not_26_out, OP3);
  not not_27 (not_27_out, OP5);
  not not_28 (not_28_out, OP6);
  not not_29 (not_29_out, F12);
  not not_30 (not_30_out, OP3);
  not not_31 (not_31_out, OP5);
  not not_32 (not_32_out, OP6);
  not not_33 (not_33_out, F25);
  not not_34 (not_34_out, F30);
  not not_35 (not_35_out, OP3);
  not not_36 (not_36_out, OP5);
  not not_37 (not_37_out, OP6);
  not not_38 (not_38_out, F25);
  not not_39 (not_39_out, OP3);
  not not_40 (not_40_out, OP5);
  not not_41 (not_41_out, OP6);
  not not_42 (not_42_out, OP2);
  not not_43 (not_43_out, OP3);
  not not_44 (not_44_out, OP3);
  not not_45 (not_45_out, OP4);
  not not_46 (not_46_out, F12);
  not not_47 (not_47_out, F13);
  not not_48 (not_48_out, F14);
  not not_49 (not_49_out, OP3);
  not not_50 (not_50_out, OP5);
  not not_51 (not_51_out, OP6);
  not not_52 (not_52_out, F30);
  not not_53 (not_53_out, F25);
  not not_54 (not_54_out, F14);
  not not_55 (not_55_out, F13);
  not not_56 (not_56_out, F12);
  not not_57 (not_57_out, OP6);
  not not_58 (not_58_out, OP3);
  not not_59 (not_59_out, OP2);
  not not_60 (not_60_out, F25);
  not not_61 (not_61_out, F14);
  not not_62 (not_62_out, F13);
  not not_63 (not_63_out, F12);
  not not_64 (not_64_out, OP6);
  not not_65 (not_65_out, OP3);
  not not_66 (not_66_out, OP2);
  not not_67 (not_67_out, F30);
  not not_68 (not_68_out, F25);
  not not_69 (not_69_out, OP6);
  not not_70 (not_70_out, OP3);
  not not_71 (not_71_out, OP2);
  not not_72 (not_72_out, F30);
  not not_73 (not_73_out, F25);
  not not_74 (not_74_out, F12);
  not not_75 (not_75_out, OP6);
  not not_76 (not_76_out, OP3);
  not not_77 (not_77_out, OP2);
  not not_78 (not_78_out, F30);
  not not_79 (not_79_out, F25);
  not not_80 (not_80_out, F14);
  not not_81 (not_81_out, F12);
  not not_82 (not_82_out, OP6);
  not not_83 (not_83_out, OP3);
  not not_84 (not_84_out, OP2);
  not not_85 (not_85_out, F30);
  not not_86 (not_86_out, F25);
  not not_87 (not_87_out, F14);
  not not_88 (not_88_out, OP6);
  not not_89 (not_89_out, OP3);
  not not_90 (not_90_out, OP2);
  not not_91 (not_91_out, F14);
  not not_92 (not_92_out, F13);
  not not_93 (not_93_out, F12);
  not not_94 (not_94_out, OP6);
  not not_95 (not_95_out, OP5);
  not not_96 (not_96_out, OP3);
  not not_97 (not_97_out, OP2);
  not not_98 (not_98_out, OP6);
  not not_99 (not_99_out, OP5);
  not not_100 (not_100_out, OP3);
  not not_101 (not_101_out, OP2);
  not not_102 (not_102_out, F12);
  not not_103 (not_103_out, OP6);
  not not_104 (not_104_out, OP5);
  not not_105 (not_105_out, OP3);
  not not_106 (not_106_out, OP2);
  not not_107 (not_107_out, F13);
  not not_108 (not_108_out, F12);
  not not_109 (not_109_out, OP6);
  not not_110 (not_110_out, OP5);
  not not_111 (not_111_out, OP3);
  not not_112 (not_112_out, OP2);
  not not_113 (not_113_out, F14);
  not not_114 (not_114_out, F12);
  not not_115 (not_115_out, OP6);
  not not_116 (not_116_out, OP5);
  not not_117 (not_117_out, OP3);
  not not_118 (not_118_out, OP2);
  not not_119 (not_119_out, F30);
  not not_120 (not_120_out, F25);
  not not_121 (not_121_out, F14);
  not not_122 (not_122_out, F13);
  not not_123 (not_123_out, OP6);
  not not_124 (not_124_out, OP5);
  not not_125 (not_125_out, OP3);
  not not_126 (not_126_out, OP2);
  not not_127 (not_127_out, F30);
  not not_128 (not_128_out, F25);
  not not_129 (not_129_out, F13);
  not not_130 (not_130_out, OP6);
  not not_131 (not_131_out, OP5);
  not not_132 (not_132_out, OP3);
  not not_133 (not_133_out, OP2);
  not not_134 (not_134_out, F25);
  not not_135 (not_135_out, F13);
  not not_136 (not_136_out, OP6);
  not not_137 (not_137_out, OP5);
  not not_138 (not_138_out, OP3);
  not not_139 (not_139_out, OP2);
  not not_140 (not_140_out, F14);
  not not_141 (not_141_out, F12);
  not not_142 (not_142_out, OP6);
  not not_143 (not_143_out, OP5);
  not not_144 (not_144_out, OP4);
  not not_145 (not_145_out, OP3);
  not not_146 (not_146_out, OP2);
  not not_147 (not_147_out, OP4);
  not not_148 (not_148_out, F14);
  not not_149 (not_149_out, F13);
  not not_150 (not_150_out, F12);
  not not_151 (not_151_out, OP4);
  not not_152 (not_152_out, OP3);
  not not_153 (not_153_out, OP6);
  not not_154 (not_154_out, OP5);
  not not_155 (not_155_out, OP3);
  not not_156 (not_156_out, F14);
  not not_157 (not_157_out, OP6);
  not not_158 (not_158_out, OP5);
  not not_159 (not_159_out, OP3);
  not not_160 (not_160_out, OP2);
  not not_161 (not_161_out, OP2);
  not not_162 (not_162_out, OP3);
  not not_163 (not_163_out, F12);
  not not_164 (not_164_out, F13);
  not not_165 (not_165_out, F14);
  not not_166 (not_166_out, OP2);
  not not_167 (not_167_out, OP3);
  not not_168 (not_168_out, OP4);
  not not_169 (not_169_out, OP6);
  not not_170 (not_170_out, F12);
  not not_171 (not_171_out, F14);
  not not_172 (not_172_out, OP2);
  not not_173 (not_173_out, OP3);
  not not_174 (not_174_out, OP4);
  not not_175 (not_175_out, F12);
  not not_176 (not_176_out, F13);
  not not_177 (not_177_out, F14);
  not not_178 (not_178_out, OP2);
  not not_179 (not_179_out, OP3);
  not not_180 (not_180_out, OP4);
  not not_181 (not_181_out, F13);
  not not_182 (not_182_out, F14);
  not not_183 (not_183_out, OP3);
  not not_184 (not_184_out, OP4);
  not not_185 (not_185_out, F12);
  not not_186 (not_186_out, F13);
  not not_187 (not_187_out, F14);
  not not_188 (not_188_out, OP4);
  not not_189 (not_189_out, OP2);
  not not_190 (not_190_out, OP3);
  not not_191 (not_191_out, OP4);
  not not_192 (not_192_out, OP6);
  not not_193 (not_193_out, F12);
  not not_194 (not_194_out, F13);
  not not_195 (not_195_out, F14);
  not not_196 (not_196_out, OP3);
  not not_197 (not_197_out, OP5);
  not not_198 (not_198_out, OP6);
  not not_199 (not_199_out, OP2);
  not not_200 (not_200_out, OP3);
  not not_201 (not_201_out, OP4);
  not not_202 (not_202_out, F12);
  not not_203 (not_203_out, OP2);
  not not_204 (not_204_out, OP3);
  not not_205 (not_205_out, OP5);
  not not_206 (not_206_out, OP6);
  not not_207 (not_207_out, F14);
  not not_208 (not_208_out, OP2);
  not not_209 (not_209_out, OP3);
  not not_210 (not_210_out, OP4);
  not not_211 (not_211_out, OP6);
  not not_212 (not_212_out, F12);
  not not_213 (not_213_out, F14);
  not not_214 (not_214_out, OP2);
  not not_215 (not_215_out, OP3);
  not not_216 (not_216_out, OP4);
  not not_217 (not_217_out, F13);
  not not_218 (not_218_out, F14);
  not not_219 (not_219_out, OP2);
  not not_220 (not_220_out, OP3);
  not not_221 (not_221_out, F12);
  not not_222 (not_222_out, F13);
  not not_223 (not_223_out, F14);
  not not_224 (not_224_out, OP3);
  not not_225 (not_225_out, OP4);
  not not_226 (not_226_out, F12);
  not not_227 (not_227_out, F13);
  not not_228 (not_228_out, F14);
  not not_229 (not_229_out, OP2);
  not not_230 (not_230_out, OP3);
  not not_231 (not_231_out, OP4);
  not not_232 (not_232_out, F12);
  not not_233 (not_233_out, OP2);
  not not_234 (not_234_out, OP3);
  not not_235 (not_235_out, OP6);
  not not_236 (not_236_out, F12);
  not not_237 (not_237_out, F13);
  not not_238 (not_238_out, F14);
  not not_239 (not_239_out, F25);
  not not_240 (not_240_out, OP3);
  not not_241 (not_241_out, OP5);
  not not_242 (not_242_out, OP6);
  not not_243 (not_243_out, F12);
  not not_244 (not_244_out, OP3);
  not not_245 (not_245_out, OP5);
  not not_246 (not_246_out, OP6);
  not not_247 (not_247_out, F13);
  not not_248 (not_248_out, F25);
  not not_249 (not_249_out, F30);
  not not_250 (not_250_out, OP3);
  not not_251 (not_251_out, OP5);
  not not_252 (not_252_out, OP6);
  not not_253 (not_253_out, F25);
  not not_254 (not_254_out, OP3);
  not not_255 (not_255_out, OP5);
  not not_256 (not_256_out, OP6);
  not not_257 (not_257_out, OP2);
  not not_258 (not_258_out, OP3);
  not not_259 (not_259_out, OP6);
  not not_260 (not_260_out, F25);
  not not_261 (not_261_out, F30);
  not not_262 (not_262_out, OP3);
  not not_263 (not_263_out, OP5);
  not not_264 (not_264_out, OP6);
  not not_265 (not_265_out, OP2);
  not not_266 (not_266_out, OP3);
  not not_267 (not_267_out, OP4);
  not not_268 (not_268_out, OP6);
  not not_269 (not_269_out, F12);
  not not_270 (not_270_out, F14);
  not not_271 (not_271_out, OP2);
  not not_272 (not_272_out, OP3);
  not not_273 (not_273_out, OP4);
  not not_274 (not_274_out, F13);
  not not_275 (not_275_out, F14);
  not not_276 (not_276_out, OP2);
  not not_277 (not_277_out, OP3);
  not not_278 (not_278_out, OP6);
  not not_279 (not_279_out, F12);
  not not_280 (not_280_out, F13);
  not not_281 (not_281_out, F14);
  not not_282 (not_282_out, F25);
  not not_283 (not_283_out, OP2);
  not not_284 (not_284_out, OP3);
  not not_285 (not_285_out, OP6);
  not not_286 (not_286_out, F25);
  not not_287 (not_287_out, F30);
  not not_288 (not_288_out, OP3);
  not not_289 (not_289_out, OP5);
  not not_290 (not_290_out, OP6);
  not not_291 (not_291_out, OP2);
  not not_292 (not_292_out, OP3);
  not not_293 (not_293_out, F12);
  not not_294 (not_294_out, OP2);
  not not_295 (not_295_out, OP3);
  and and_1 (MemToReg, not_1_out, not_2_out, not_3_out, not_4_out, not_5_out, not_6_out, F13, not_7_out);
  and and_2 (MemWrite, not_8_out, not_9_out, not_10_out, OP5, not_11_out, not_12_out, not_13_out);
  and and_3 (and_3_out, not_14_out, not_15_out, not_16_out, not_17_out, not_18_out, F13, not_19_out);
  and and_4 (and_4_out, not_20_out, not_21_out, not_22_out, OP5, not_23_out, not_24_out, not_25_out);
  and and_5 (and_5_out, not_26_out, OP4, not_27_out, not_28_out, not_29_out);
  and and_6 (and_6_out, not_30_out, OP4, not_31_out, not_32_out, not_33_out, not_34_out);
  and and_7 (and_7_out, not_35_out, OP4, not_36_out, not_37_out, F14, not_38_out);
  and and_8 (and_8_out, not_39_out, OP4, not_40_out, not_41_out, F13);
  and and_9 (and_9_out, not_42_out, not_43_out, OP4, OP5, OP6, F13, F14);
  and and_10 (and_10_out, OP2, not_44_out, not_45_out, OP5, OP6, not_46_out, not_47_out, not_48_out);
  and and_11 (and_11_out, OP2, not_49_out, OP4, not_50_out, not_51_out);
  and and_12 (and_12_out, not_52_out, not_53_out, not_54_out, not_55_out, not_56_out, not_57_out, OP5, OP4, not_58_out, not_59_out);
  and and_13 (and_13_out, F30, not_60_out, not_61_out, not_62_out, not_63_out, not_64_out, OP5, OP4, not_65_out, not_66_out);
  and and_14 (and_14_out, not_67_out, not_68_out, F14, F13, F12, not_69_out, OP5, OP4, not_70_out, not_71_out);
  and and_15 (and_15_out, not_72_out, not_73_out, F14, F13, not_74_out, not_75_out, OP5, OP4, not_76_out, not_77_out);
  and and_16 (and_16_out, not_78_out, not_79_out, not_80_out, F13, not_81_out, not_82_out, OP5, OP4, not_83_out, not_84_out);
  and and_17 (and_17_out, not_85_out, not_86_out, not_87_out, F13, F12, not_88_out, OP5, OP4, not_89_out, not_90_out);
  and and_18 (and_18_out, not_91_out, not_92_out, not_93_out, not_94_out, not_95_out, OP4, not_96_out, not_97_out);
  and and_19 (and_19_out, F14, F13, F12, not_98_out, not_99_out, OP4, not_100_out, not_101_out);
  and and_20 (and_20_out, F14, F13, not_102_out, not_103_out, not_104_out, OP4, not_105_out, not_106_out);
  and and_21 (and_21_out, F14, not_107_out, not_108_out, not_109_out, not_110_out, OP4, not_111_out, not_112_out);
  and and_22 (and_22_out, not_113_out, F13, not_114_out, not_115_out, not_116_out, OP4, not_117_out, not_118_out);
  and and_23 (and_23_out, not_119_out, not_120_out, not_121_out, not_122_out, F12, not_123_out, not_124_out, OP4, not_125_out, not_126_out);
  and and_24 (and_24_out, not_127_out, not_128_out, F14, not_129_out, F12, not_130_out, not_131_out, OP4, not_132_out, not_133_out);
  and and_25 (and_25_out, F30, not_134_out, F14, not_135_out, F12, not_136_out, not_137_out, OP4, not_138_out, not_139_out);
  and and_26 (and_26_out, not_140_out, F13, not_141_out, not_142_out, not_143_out, not_144_out, not_145_out, not_146_out);
  and and_27 (and_27_out, OP6, OP5, not_147_out, OP3, OP2);
  and and_28 (and_28_out, not_148_out, not_149_out, not_150_out, OP6, OP5, not_151_out, not_152_out, OP2);
  and and_29 (and_29_out, not_153_out, not_154_out, OP4, not_155_out, OP2);
  and and_30 (and_30_out, not_156_out, F13, F12, not_157_out, not_158_out, OP4, not_159_out, not_160_out);
  and and_31 (ecall, not_161_out, not_162_out, OP4, OP5, OP6, not_163_out, not_164_out, not_165_out);
  and and_32 (S_Type, not_166_out, not_167_out, not_168_out, OP5, not_169_out, not_170_out, not_171_out);
  and and_33 (BEQ, not_172_out, not_173_out, not_174_out, OP5, OP6, not_175_out, not_176_out, not_177_out);
  and and_34 (BNE, not_178_out, not_179_out, not_180_out, OP5, OP6, F12, not_181_out, not_182_out);
  and and_35 (JALR, OP2, not_183_out, not_184_out, OP5, OP6, not_185_out, not_186_out, not_187_out);
  and and_36 (JAL, OP2, OP3, not_188_out, OP5, OP6);
  and and_37 (sb, not_189_out, not_190_out, not_191_out, OP5, not_192_out, not_193_out, not_194_out, not_195_out);
  and and_38 (auipc, OP2, not_196_out, OP4, not_197_out, not_198_out);
  and and_39 (bltu, not_199_out, not_200_out, not_201_out, OP5, OP6, not_202_out, F13, F14);
  and and_40 (sltiu, not_203_out, not_204_out, OP4, not_205_out, not_206_out, F12, F13, not_207_out);
  and and_41 (and_41_out, not_208_out, not_209_out, not_210_out, not_211_out, not_212_out, F13, not_213_out);
  and and_42 (and_42_out, not_214_out, not_215_out, not_216_out, OP5, OP6, not_217_out, not_218_out);
  and and_43 (and_43_out, not_219_out, not_220_out, OP5, OP6, not_221_out, not_222_out, not_223_out);
  and and_44 (and_44_out, not_224_out, not_225_out, OP5, OP6, not_226_out, not_227_out, not_228_out);
  and and_45 (and_45_out, not_229_out, not_230_out, not_231_out, OP5, OP6, not_232_out, F13, F14);
  and and_46 (and_46_out, not_233_out, not_234_out, OP4, not_235_out, not_236_out, not_237_out, not_238_out, not_239_out);
  and and_47 (and_47_out, not_240_out, OP4, not_241_out, not_242_out, not_243_out);
  and and_48 (and_48_out, not_244_out, OP4, not_245_out, not_246_out, not_247_out, not_248_out, not_249_out);
  and and_49 (and_49_out, not_250_out, OP4, not_251_out, not_252_out, F14, not_253_out);
  and and_50 (and_50_out, not_254_out, OP4, not_255_out, not_256_out, F13, F14);
  and and_51 (and_51_out, not_257_out, not_258_out, OP4, OP5, not_259_out, F13, not_260_out, not_261_out);
  and and_52 (and_52_out, OP2, not_262_out, OP4, not_263_out, not_264_out);
  and and_53 (and_53_out, not_265_out, not_266_out, not_267_out, OP5, not_268_out, not_269_out, F13, not_270_out);
  and and_54 (and_54_out, not_271_out, not_272_out, not_273_out, OP5, OP6, not_274_out, not_275_out);
  and and_55 (and_55_out, not_276_out, not_277_out, OP4, OP5, not_278_out, not_279_out, not_280_out, not_281_out, not_282_out);
  and and_56 (and_56_out, not_283_out, not_284_out, OP4, OP5, not_285_out, F13, not_286_out, not_287_out);
  and and_57 (and_57_out, OP2, not_288_out, OP4, not_289_out, not_290_out);
  and and_58 (CSRRSI, not_291_out, not_292_out, OP4, OP5, OP6, not_293_out, F13, F14);
  and and_59 (CSRRCI, not_294_out, not_295_out, OP4, OP5, OP6, F12, F13, F14);
  or or_1 (rs2, and_53_out, and_54_out, and_55_out, and_56_out, and_57_out);
  or or_2 (ALU_SRC, and_3_out, and_4_out, and_5_out, and_6_out, and_7_out, and_8_out, and_9_out, and_10_out, and_11_out);
  or or_3 (RegWrite, and_12_out, and_13_out, and_14_out, and_15_out, and_16_out, and_17_out, and_18_out, and_19_out, and_20_out, and_21_out, and_22_out, and_23_out, and_24_out, and_25_out, and_26_out, and_27_out, and_28_out, and_29_out, and_30_out);
  or or_4 (rs1, and_41_out, and_42_out, and_43_out, and_44_out, and_45_out, and_46_out, and_47_out, and_48_out, and_49_out, and_50_out, and_51_out, and_52_out);
endmodule

module \单周期RISC_V  (
  input  IR1,
  input  IR2,
  input  IR3,
  output RegWrite,
  output MemWrite,
  output [31:0] PC,
  output [31:0] IR,
  output [31:0] RDin,
  output [31:0] MDin,
  output [31:0] LedData
);

  wire alu_1_equal, alu_1_out_6, and_1_out, and_2_out, and_3_out, and_5_out, and_6_out, auipc, bltu, Branch,
       CLK, clock_1_out, comparator_1_eq, comparator_1_lt, comparator_2_eq, d_ff_1_q, ecall, Go, halt, IR1_t,
       IR2_t, IR3_t, IRA, IRB, IRC, JAL, JALR, MemToReg, nand_1_out, not_1_out, not_2_out, not_3_out,
       not_4_out, or_4_out, or_6_out, riscv_probe_1_p3, RST, sb, sltiu, W1, W2, W3, \单周期硬布线控制器_1_alu_src ,
       \单周期硬布线控制器_1_beq , \单周期硬布线控制器_1_bne , \单周期硬布线控制器_1_s_type ;
  wire [3:0] sb_1_out_3, \单周期硬布线控制器_1_alu_op ;
  wire [4:0] multiplexer_4_out, multiplexer_5_out;
  wire [11:0] multiplexer_6_out;
  wire [12:0] CNT_num;
  wire [15:0] \总周期数 ;
  wire [31:0] adder_1_out, adder_5_out, ALU_result, bit_extender_1_out, bit_extender_2_out,
       bit_extender_3_out, bit_extender_4_out, Branch_Adress, JAL_Adress, JALR_Adress, less, mips_ram_1_p7,
       multiplexer_1_out, multiplexer_2_out, multiplexer_3_out, multiplexer_7_out, multiplexer_8_out,
       multiplexer_10_out, multiplexer_11_out, r1, r2, sb_1_darta, shifter_1_out, shifter_2_out,
       shifter_3_out, U_adress;

  Button \u_继续运行  (.out(Go));
  Button _1 (.out(IRA));
  Button _2 (.out(IRB));
  Button _3 (.out(IRC));
  Multiplexer #(.select(1), .width(32), .disabled("Z"), .enable("false")) multiplexer_1 (
    .in0(multiplexer_2_out), .in1(JALR_Adress), .out(multiplexer_1_out), .sel(JALR));
  Multiplexer #(.select(1), .width(32), .disabled("Z"), .enable("false")) multiplexer_2 (
    .in0(adder_1_out), .in1(Branch_Adress), .out(multiplexer_2_out), .sel(Branch));
  LED #(.active("true")) led_1 (.in(W1));
  LED #(.active("true")) led_2 (.in(W2));
  LED #(.active("true")) led_3 (.in(W3));
  Button button_1 (.out(RST));
  Multiplexer #(.select(1), .width(32), .disabled("Z"), .enable("false")) multiplexer_3 (
    .in0(multiplexer_1_out), .in1(JAL_Adress), .out(multiplexer_3_out), .sel(JAL));
  Hex_Digit_Display hex_digit_display_1 (.value(LedData[31:28]));  // open: dp
  Register #(.width(32), .trigger("rising"), .Select("low")) u_PC (
    .D(multiplexer_3_out), .en(not_1_out), .Q(PC), .clk(CLK), .clr(RST));
  not not_1 (not_1_out, halt);
  Hex_Digit_Display hex_digit_display_2 (.value(LedData[27:24]));  // open: dp
  Hex_Digit_Display hex_digit_display_3 (.value(LedData[23:20]));  // open: dp
  Hex_Digit_Display hex_digit_display_4 (.value(LedData[15:12]));  // open: dp
  Hex_Digit_Display hex_digit_display_5 (.value(LedData[19:16]));  // open: dp
  // RiscV_Probe riscv_probe_1: pin names not known; wires that end beside it: Branch, IR, riscv_probe_1_p3, ecall
  Adder #(.width(32)) adder_1 (.a(PC), .b(32'h4), .out(adder_1_out));  // open: cin, cout
  Hex_Digit_Display hex_digit_display_6 (.value(LedData[11:8]));  // open: dp
  Hex_Digit_Display hex_digit_display_7 (.value(LedData[7:4]));  // open: dp
  // Probe on \总周期数 
  ROM #(.addrWidth(10), .dataWidth(32), .Select("high")) rom_1 (.addr(PC[11:2]), .data(IR));
  Hex_Digit_Display hex_digit_display_8 (.value(LedData[3:0]));  // open: dp
  \单周期硬布线控制器  \u_单周期硬布线控制器_1  (
    .Funct({IR[30], IR[25], IR[14:12]}), .OP(IR[6:2]), .ALU_OP(\单周期硬布线控制器_1_alu_op ), .MemToReg(MemToReg),
    .MemWrite(MemWrite), .ALU_SRC(\单周期硬布线控制器_1_alu_src ), .RegWrite(RegWrite), .ecall(ecall),
    .S_type(\单周期硬布线控制器_1_s_type ), .Jalr(JALR), .Beq(\单周期硬布线控制器_1_beq ), .JAL(JAL), .Bne(\单周期硬布线控制器_1_bne ),
    .in_3(IR[21]), .uret(riscv_probe_1_p3), .sb(sb), .auipc(auipc), .bltu(bltu), .sltiu(sltiu));  // open: rs1, rs2, CSRRSI, CSRRCI
  Multiplexer #(.select(1), .width(5), .disabled("Z"), .enable("false")) multiplexer_4 (
    .in0(IR[19:15]), .in1(5'b10001), .out(multiplexer_4_out), .sel(ecall));
  Multiplexer #(.select(1), .width(5), .disabled("Z"), .enable("false")) multiplexer_5 (
    .in0(IR[24:20]), .in1(5'b01010), .out(multiplexer_5_out), .sel(ecall));
  or or_1 (IR1_t, IR1, IRA);
  Multiplexer #(.select(1), .width(12), .disabled("Z"), .enable("false")) multiplexer_6 (
    .in0(IR[31:20]), .in1({IR[31:25], IR[11:7]}), .out(multiplexer_6_out), .sel(\单周期硬布线控制器_1_s_type ));
  assign bit_extender_1_out = {{20{IR[31]}}, {IR[31], IR[7], IR[30:25], IR[11:8]}};  // Bit_Extender bit_extender_1
  assign bit_extender_2_out = {{12{IR[31]}}, {IR[31], IR[19:12], IR[20], IR[30:21]}};  // Bit_Extender bit_extender_2
  assign bit_extender_3_out = {{12{1'b0}}, IR[31:12]};  // Bit_Extender bit_extender_3
  or or_2 (IR2_t, IR2, IRB);
  assign bit_extender_4_out = {{20{multiplexer_6_out[11]}}, multiplexer_6_out};  // Bit_Extender bit_extender_4
  Multiplexer #(.select(1), .width(32), .disabled("Z"), .enable("false")) multiplexer_7 (
    .in0({32{1'b0}}), .in1(bit_extender_3_out), .out(multiplexer_7_out), .sel(auipc));
  Regifile regifile_1 (
    .Din(RDin), .Clk(CLK), .R1(r1), .R2(r2), .WE(RegWrite), .W_num(IR[11:7]), .R1_num(multiplexer_4_out),
    .R2_num(multiplexer_5_out));
  Shifter #(.width(32), .shift("ll")) shifter_1 (.in(bit_extender_1_out), .\dist (5'b00001), .out(shifter_1_out));
  Shifter #(.width(32), .shift("ll")) shifter_2 (.in(bit_extender_2_out), .\dist (5'b00001), .out(shifter_2_out));
  or or_3 (IR3_t, IR3, IRC);
  Multiplexer #(.select(1), .width(32), .disabled("Z"), .enable("false")) multiplexer_8 (
    .in0(r2), .in1(bit_extender_4_out), .out(multiplexer_8_out), .sel(\单周期硬布线控制器_1_alu_src ));
  Adder #(.width(32)) adder_2 (.a(shifter_1_out), .b(PC), .out(Branch_Adress));  // open: cin, cout
  Adder #(.width(32)) adder_3 (.a(shifter_2_out), .b(PC), .out(JAL_Adress));  // open: cin, cout
  Shifter #(.width(32), .shift("ll")) shifter_3 (.in(multiplexer_7_out), .\dist (5'b01100), .out(shifter_3_out));
  Adder #(.width(32)) adder_4 (.a(shifter_3_out), .b(PC), .out(U_adress));  // open: cin, cout
  ALU alu_1 (
    .X(r1), .Y(multiplexer_8_out), .AluOP(\单周期硬布线控制器_1_alu_op ), .Equal(alu_1_equal), .Result(ALU_result),
    .out_6(alu_1_out_6));  // open: Result_2, out_4
  sb sb_1 (.in_1(sb), .R2(r2), .out_3(sb_1_out_3), .darta(sb_1_darta));
  Multiplexer #(.select(1), .width(32), .disabled("Z"), .enable("false")) multiplexer_9 (
    .in0(r2), .in1(sb_1_darta), .out(MDin), .sel(sb));
  and and_1 (and_1_out, \单周期硬布线控制器_1_beq , alu_1_equal);
  and and_2 (and_2_out, \单周期硬布线控制器_1_bne , not_2_out);
  not not_2 (not_2_out, alu_1_equal);
  and and_3 (and_3_out, bltu, alu_1_out_6);
  assign less = {{31{1'b0}}, alu_1_out_6};  // Bit_Extender bit_extender_5
  D_Flip_Flop #(.trigger("high"), .Pre_Clr_Positions("LEGACY"), .NegatePresetClear("false"), .enable("true"), .NewFFLayout("false")) d_ff_1 (.Q(d_ff_1_q));  // open: clk, D, Qn, preset, en, reset
  // Probe on 13'hc
  or or_4 (or_4_out, and_1_out, and_2_out);
  // MIPS_RAM mips_ram_1: pin names not known; wires that end beside it: ALU_result[11:2], MDin, MemWrite, sb_1_out_3, CLK, RST, mips_ram_1_p7
  Comparator #(.width(13), .mode("twosComplement")) comparator_1 (
    .a(CNT_num), .b(13'hc), .eq(comparator_1_eq), .lt(comparator_1_lt));  // open: gt
  Clock #(.highDuration(1), .lowDuration(1)) clock_1 (.out(clock_1_out));
  or or_5 (Branch, or_4_out, and_3_out);
  Counter #(.width(13), .max('h1fff), .ongoal("stay"), .trigger("rising"), .behavior("old")) counter_1 (
    .count(comparator_1_lt), .Q(CNT_num), .clk(clock_1_out));  // open: load, D, carry, clr, preset
  Multiplexer #(.select(1), .width(32), .disabled("Z"), .enable("false")) multiplexer_10 (
    .in0(ALU_result), .in1(mips_ram_1_p7), .out(multiplexer_10_out), .sel(MemToReg));
  Adder #(.width(32)) adder_5 (.a(PC), .b(32'h4), .out(adder_5_out));  // open: cin, cout
  assign JALR_Adress = ALU_result & 32'hfffffffe;  // AND_Gate and_4, 32 bits wide
  nand nand_1 (nand_1_out, d_ff_1_q, comparator_1_eq);
  or or_6 (or_6_out, JAL, JALR);
  Multiplexer #(.select(1), .width(32), .disabled("Z"), .enable("false")) multiplexer_11 (
    .in0(multiplexer_10_out), .in1(adder_5_out), .out(multiplexer_11_out), .sel(or_6_out));
  Comparator #(.width(32), .mode("twosComplement")) comparator_2 (
    .a(32'h22), .b(r1), .eq(comparator_2_eq));  // open: gt, lt
  assign CLK = nand_1_out ? clock_1_out : 1'bz;  // Controlled_Buffer controlled_buffer_1
  Pull_Resistor #(.pull(1)) pull_resistor_1 (.node(CLK));
  Multiplexer #(.select(1), .width(32), .disabled("Z"), .enable("false")) multiplexer_12 (
    .in0(multiplexer_11_out), .in1(U_adress), .out(RDin), .sel(auipc));
  not not_3 (not_3_out, comparator_2_eq);
  and and_5 (and_5_out, ecall, comparator_2_eq);
  and and_6 (and_6_out, ecall, not_3_out);
  Register #(.width(32), .trigger("rising"), .Select("low")) register_1 (
    .D(MDin), .en(and_5_out), .Q(LedData), .clk(CLK), .clr(RST));
  Multiplexer #(.select(1), .width(1), .disabled("Z"), .enable("false")) multiplexer_13 (
    .in0(and_6_out), .in1(1'b0), .out(halt), .sel(Go));
  not not_4 (not_4_out, halt);
  Counter #(.width(16), .max('hffff), .ongoal("wrap"), .trigger("rising"), .behavior("new")) counter_2 (
    .count(not_4_out), .Q(\总周期数 ), .clk(CLK), .clr(RST));  // open: load, D, carry, preset, down

  // Other names for the same wires on the sheet: I_imm[11:0] = IR[31:20]

  // Notes on the sheet:
  //   中断源
  //   中断等待指示
  //   数码管输出应该用寄存器锁存，否则显示数据只能一闪而过
  //   数码管输出
  //   指令探针
  //   指令存储器
  //   contents of rom_1 (hex, n*v repeats v):
  //   13 430497 900533 2200893 73 430497 900533 2200893 73 430497 900533 2200893 73 430497 900533 2200893
  //   73 430497 900533 2200893 73 430497 900533 2200893 73 430497 900533 2200893 73 430497 900533 2200893
  //   73 a00893 73
  //   指令字
  //   JAL
  //   JALR
  //   URET
  //   Beq
  //   Bne
  //   MemToReg
  //   MemWrite
  //   AluOP
  //   AluSrcB
  //   RegWrite
  //   为方便自动评测，需要输出PC，IR，寄存器堆写如数据RDin
  //   RAM写使能MemWrite、RAM写入数据MDin等信号
  //   数据存储器
  //   控制位
  //   暂停节拍，不能为0
  //   戳工具置1进入计数暂停模式，ctrl+k时钟自动运行到对应节拍暂停
  //   用这个时钟源需要去掉电路中的其他时钟源
  //   可计数暂停的时钟源
endmodule

module Regifile (
  input  [31:0] Din,
  input  Clk,
  input  WE,
  input  [4:0] R1_num,
  input  [4:0] W_num,
  input  [4:0] R2_num,
  output [31:0] R1,
  output [31:0] R2
);

  // RegisterFile registerfile_1: pin names not known; wires that end beside it: Din, Clk, WE, W_num, R1_num, R2_num, R1, R2
endmodule

// ALU
module ALU (
  input  [31:0] X,
  input  [31:0] Y,
  input  [3:0] AluOP,
  output out_4,
  output Equal,
  output out_6,
  output [31:0] Result,
  output [31:0] Result_2
);

  wire [0:0] comparator_1_lt, comparator_2_lt;
  wire [31:0] adder_1_out, AND_out, divider_1_out, divider_1_rem, multiplier_1_cout, multiplier_1_out,
       NOR_out, OR_out, shifter_1_out, shifter_2_out, shifter_3_out, subtractor_1_out, XOR_out;

  assign AND_out = X & Y;  // AND_Gate AND, 32 bits wide
  assign OR_out = X | Y;  // OR_Gate OR, 32 bits wide
  Shifter #(.width(32), .shift("ll")) shifter_1 (.in(X), .\dist (Y[4:0]), .out(shifter_1_out));
  Shifter #(.width(32), .shift("ar")) shifter_2 (.in(X), .\dist (Y[4:0]), .out(shifter_2_out));
  Shifter #(.width(32), .shift("lr")) shifter_3 (.in(X), .\dist (Y[4:0]), .out(shifter_3_out));
  Multiplier #(.width(32)) multiplier_1 (.a(X), .b(Y), .out(multiplier_1_out), .cout(multiplier_1_cout));  // open: cin
  Divider #(.width(32)) divider_1 (.a(X), .b(Y), .out(divider_1_out), .rem(divider_1_rem));  // open: upper
  Adder #(.width(32)) adder_1 (.a(X), .b(Y), .out(adder_1_out));  // open: cin, cout
  Subtractor #(.width(32)) subtractor_1 (.a(X), .b(Y), .out(subtractor_1_out));  // open: bin, bout
  assign XOR_out = X ^ Y;  // XOR_Gate XOR, 32 bits wide
  assign NOR_out = ~(X | Y);  // NOR_Gate NOR, 32 bits wide
  Comparator #(.width(32), .mode("twosComplement")) comparator_1 (
    .a(X), .b(Y), .eq(Equal), .lt(comparator_1_lt[0]));  // open: gt
  Comparator #(.width(32), .mode("unsigned")) comparator_2 (.a(X), .b(Y), .lt(comparator_2_lt[0]));  // open: gt, eq
  Multiplexer #(.select(4), .width(32), .disabled("Z"), .enable("false")) multiplexer_1 (
    .in0(shifter_1_out), .in1(shifter_2_out), .in2(shifter_3_out), .in3(multiplier_1_out),
    .in4(divider_1_out), .in5(adder_1_out), .in6(subtractor_1_out), .in7(AND_out), .in8(OR_out),
    .in9(XOR_out), .in10(NOR_out), .in11({{31{1'b0}}, comparator_1_lt[0]}),
    .in12({{31{1'b0}}, comparator_2_lt[0]}), .in13({32{1'b0}}), .in14({32{1'b0}}), .in15({32{1'b0}}),
    .out(Result), .sel(AluOP));
  Multiplexer #(.select(4), .width(32), .disabled("Z"), .enable("false")) multiplexer_2 (
    .in0({32{1'b0}}), .in1({32{1'b0}}), .in2({32{1'b0}}), .in3(multiplier_1_cout), .in4(divider_1_rem),
    .in5({32{1'b0}}), .in6({32{1'b0}}), .in7({32{1'b0}}), .in8({32{1'b0}}), .in9({32{1'b0}}),
    .in10({32{1'b0}}), .in11({32{1'b0}}), .in12({32{1'b0}}), .in13({32{1'b0}}), .in14({32{1'b0}}),
    .in15({32{1'b0}}), .out(Result_2), .sel(AluOP));
  Multiplexer #(.select(4), .width(1), .disabled("Z"), .enable("false")) multiplexer_3 (
    .in0(1'b0), .in1(1'b0), .in2(1'b0), .in3(1'b0), .in4(1'b0), .in5(1'b0), .in6(1'b0), .in7(1'b0),
    .in8(1'b0), .in9(1'b0), .in10(1'b0), .in11(comparator_1_lt[0]), .in12(comparator_2_lt[0]), .in13(1'b0),
    .in14(1'b0), .in15(1'b0), .out(out_6), .sel(AluOP));
  not not_1 (out_4, out_6);

  // Other names for the same wires on the sheet: Result2[31:0] = Result_2; S[3:0] = AluOP; tunnel = out_6;
  //   tunnel_t = out_4

  // Notes on the sheet:
  //   不要改变此引脚区域内容，也不要改变ALU封装形式
  //   输入引脚
  //   输出引脚
endmodule

module \气泡流水线  (
  output RegWrite,
  output MemWrite,
  output [31:0] IF_PC,
  output [31:0] ID_PC,
  output [31:0] EX_PC,
  output [31:0] M_PC,
  output [31:0] WB_PC,
  output [31:0] RDin,
  output [31:0] MDin,
  output [31:0] LedData
);

  wire alu_1_equal, alu_1_out_6, and_1_out, and_3_out, and_4_out, and_5_out, and_6_out, auipc, branchtaken,
       CLK, clock_1_out, comparator_1_eq, comparator_1_lt, comparator_2_eq, comparator_3_eq, d_ff_2_q,
       datahazzrd, ecall, ecallEq, ecallFB, ex_1_auipc_2, ex_1_ecall_2, ex_1_jal_2, ex_1_jalr_2,
       ex_1_memtoreg_2, ex_1_sb_2, ex_1_uret_2, EX_RegWrite, flush, Go, halt, id_1_alu_srcb_2, id_1_auipc_2,
       id_1_beq_2, id_1_bltu_2, id_1_bne_2, id_1_ecall_2, id_1_jal_2, id_1_jalr_2, id_1_memtoreg_2,
       id_1_memwrite_2, id_1_sb_2, id_1_uret_2, IR1, IR2, IR3, mem_1_jal_2, mem_1_jalr_2, MEN_MemtoReg,
       MEN_RegWrite, nand_1_out, not_1_out, not_2_out, not_3_out, not_4_out, not_5_out, not_6_out, not_7_out,
       not_8_out, or_1_out, or_2_out, or_3_out, or_5_out, or_6_out, rs1, rs2, RST, sltiu, stall, Stop, W1,
       W2, W3, WB_ecall, \单周期硬布线控制器_1_alu_src , \单周期硬布线控制器_1_auipc , \单周期硬布线控制器_1_beq , \单周期硬布线控制器_1_bltu ,
       \单周期硬布线控制器_1_bne , \单周期硬布线控制器_1_jal , \单周期硬布线控制器_1_jalr , \单周期硬布线控制器_1_memtoreg ,
       \单周期硬布线控制器_1_memwrite , \单周期硬布线控制器_1_regwrite , \单周期硬布线控制器_1_s_type , \单周期硬布线控制器_1_sb ,
       \单周期硬布线控制器_1_uret ;
  wire [3:0] id_1_alu_op_2, sb_1_out_3, \单周期硬布线控制器_1_alu_op ;
  wire [4:0] EX_RD, MEM_RD, R1_num, R2_num, WB_RD;
  wire [11:0] I_imm, multiplexer_6_out;
  wire [12:0] CNT_num;
  wire [15:0] \LoadUse次数 , \总周期数 , \插入气泡数 , \无条件分支数 , \条件分支成功数 ;
  wire [19:0] ID_IR;
  wire [31:0] adder_1_out, adder_4_out, alu_1_result, ALU_result, bit_extender_1_out, bit_extender_2_out,
       bit_extender_3_out, bit_extender_4_out, Branch_Adress, ex_1_pc_4_2, ex_1_r1_2, ex_1_r2_2, ex_1_u_2,
       EX_IR, EX_R1, EX_R2, id_1_bm_2, id_1_im_2, id_1_jm_2, id_1_pc_4_2, id_1_u_2, ID_PC_4, IF_IR,
       JAL_Adress, JALR_Adress, mem_1_alu_result_2, mem_1_mdata_2, mem_1_u_2, MEM_IR, mips_ram_1_p7,
       multiplexer_1_out, multiplexer_2_out, multiplexer_3_out, multiplexer_7_out, multiplexer_9_out,
       multiplexer_10_out, multiplexer_11_out, regifile_1_r1, regifile_1_r2, sb_1_darta, shifter_1_out,
       shifter_2_out, shifter_3_out, U_adress, WB_IR, WB_PC_4, WB_R1, WB_R2;

  Button \u_总复位  (.out(RST));
  Button _1 (.out(IR1));
  Button _2 (.out(IR2));
  Button _3 (.out(IR3));
  // Probe on \总周期数 
  // Probe on \总周期数 
  Button \u_继续运行  (.out(Go));
  LED #(.active("true")) led_1 (.in(W1));
  LED #(.active("true")) led_2 (.in(W2));
  LED #(.active("true")) led_3 (.in(W3));
  Hex_Digit_Display hex_digit_display_1 (.value(LedData[31:28]));  // open: dp
  // Probe on IF_PC[19:0]
  // RiscV_Probe riscv_probe_1: pin names not known; wires that end beside it: IF_IR
  Hex_Digit_Display hex_digit_display_2 (.value(LedData[27:24]));  // open: dp
  Hex_Digit_Display hex_digit_display_3 (.value(LedData[23:20]));  // open: dp
  // Probe on ID_PC[19:0]
  // RiscV_Probe riscv_probe_2: pin names not known; wires that end beside it: {I_imm, ID_IR}
  Hex_Digit_Display hex_digit_display_4 (.value(LedData[15:12]));  // open: dp
  Hex_Digit_Display hex_digit_display_5 (.value(LedData[19:16]));  // open: dp
  Multiplexer #(.select(1), .width(32), .disabled("Z"), .enable("false")) multiplexer_1 (
    .in0(adder_1_out), .in1(Branch_Adress), .out(multiplexer_1_out), .sel(or_5_out));
  Multiplexer #(.select(1), .width(32), .disabled("Z"), .enable("false")) multiplexer_2 (
    .in0(multiplexer_1_out), .in1(JAL_Adress), .out(multiplexer_2_out), .sel(id_1_jal_2));
  Adder #(.width(32)) adder_1 (.a(IF_PC), .b(32'h4), .out(adder_1_out));  // open: cin, cout
  datahazzard datahazzard_1 (
    .RtUsed(rs1), .Rt(R1_num), .Rt_2(R1_num), .MEN_WriteReg(MEM_RD), .MEN_Regwrite(MEN_RegWrite),
    .RtUsed_2(rs1), .Rt_3(R1_num), .Rt_4(R1_num), .EX_WriteReg(EX_RD), .EX_Regwrite(EX_RegWrite),
    .RsUsed(rs2), .Rs(R2_num), .Rs_2(R2_num), .EX_WriteReg_2(EX_RD), .EX_Regwrite_2(EX_RegWrite),
    .RsUsed_2(rs2), .Rs_3(R2_num), .Rs_4(R2_num), .MEN_WriteReg_2(MEM_RD), .MEN_Regwrite_2(MEN_RegWrite),
    .datahazzed(datahazzrd));
  Hex_Digit_Display hex_digit_display_6 (.value(LedData[11:8]));  // open: dp
  Hex_Digit_Display hex_digit_display_7 (.value(LedData[7:4]));  // open: dp
  // Probe on EX_PC[19:0]
  // RiscV_Probe riscv_probe_3: pin names not known; wires that end beside it: EX_IR
  Multiplexer #(.select(1), .width(32), .disabled("Z"), .enable("false")) multiplexer_3 (
    .in0(multiplexer_2_out), .in1(JALR_Adress), .out(multiplexer_3_out), .sel(id_1_jalr_2));
  not not_1 (not_1_out, datahazzrd);
  Hex_Digit_Display hex_digit_display_8 (.value(LedData[3:0]));  // open: dp
  Register #(.width(32), .trigger("rising"), .Select("low")) PC (
    .D(multiplexer_3_out), .en(and_1_out), .Q(IF_PC), .clk(CLK), .clr(RST));
  and and_1 (and_1_out, not_1_out, Stop);
  \气泡处理  \u_气泡处理_1  (
    .datahazzd(datahazzrd), .branch(branchtaken), .datahazzd_2(datahazzrd), .stall(stall), .flush(flush));
  // Probe on \总周期数 
  // Probe on M_PC[19:0]
  // RiscV_Probe riscv_probe_4: pin names not known; wires that end beside it: MEM_IR
  D_Flip_Flop #(.trigger("rising"), .Pre_Clr_Positions("LEGACY"), .NegatePresetClear("false"), .enable("true"), .NewFFLayout("false")) d_ff_1 (
    .Qn(Stop), .preset(halt), .reset(Go));  // open: clk, D, Q, en
  // Probe on \总周期数 
  // Probe on \无条件分支数 
  // Probe on \条件分支成功数 
  // Probe on \插入气泡数 
  // Probe on \LoadUse次数 
  // Probe on IF_PC[11:0]
  // Probe on WB_PC[19:0]
  // RiscV_Probe riscv_probe_5: pin names not known; wires that end beside it: WB_IR
  // Probe on EX_PC[11:0]
  // Probe on ID_PC[11:0]
  or or_1 (or_1_out, RST, branchtaken);
  // RiscV_Probe riscv_probe_6: pin names not known; wires that end beside it: IF_IR
  ROM #(.addrWidth(10), .dataWidth(32), .Select("high")) rom_1 (.addr(IF_PC[11:2]), .data(IF_IR));
  or or_2 (or_2_out, not_2_out, datahazzrd);
  not not_2 (not_2_out, Stop);
  // Probe on M_PC[11:0]
  D_Flip_Flop #(.trigger("high"), .Pre_Clr_Positions("LEGACY"), .NegatePresetClear("false"), .enable("true"), .NewFFLayout("false")) d_ff_2 (.Q(d_ff_2_q));  // open: clk, D, Qn, preset, en, reset
  // Probe on 13'hc
  IF if_1 (
    .CLK(CLK), .RST(or_1_out), .IR(IF_IR), .PC(IF_PC), .PC_4(adder_1_out), .IR_2({I_imm, ID_IR}),
    .PC_2(ID_PC), .PC_4_2(ID_PC_4), .flush(1'b0), .en(or_2_out));
  // Probe on WB_PC[11:0]
  Comparator #(.width(13), .mode("twosComplement")) comparator_1 (
    .a(CNT_num), .b(13'hc), .eq(comparator_1_eq), .lt(comparator_1_lt));  // open: gt
  Clock #(.highDuration(1), .lowDuration(1)) clock_1 (.out(clock_1_out));
  nand nand_1 (nand_1_out, d_ff_2_q, comparator_1_eq);
  Counter #(.width(13), .max('h1fff), .ongoal("stay"), .trigger("rising"), .behavior("old")) counter_1 (
    .count(comparator_1_lt), .Q(CNT_num), .clk(clock_1_out));  // open: load, D, carry, clr, preset
  assign CLK = nand_1_out ? clock_1_out : 1'bz;  // Controlled_Buffer controlled_buffer_1
  \单周期硬布线控制器  \u_单周期硬布线控制器_1  (
    .Funct({I_imm[10], I_imm[5], ID_IR[14:12]}), .OP(ID_IR[6:2]), .ALU_OP(\单周期硬布线控制器_1_alu_op ),
    .MemToReg(\单周期硬布线控制器_1_memtoreg ), .MemWrite(\单周期硬布线控制器_1_memwrite ), .ALU_SRC(\单周期硬布线控制器_1_alu_src ),
    .RegWrite(\单周期硬布线控制器_1_regwrite ), .ecall(ecall), .S_type(\单周期硬布线控制器_1_s_type ),
    .Jalr(\单周期硬布线控制器_1_jalr ), .Beq(\单周期硬布线控制器_1_beq ), .JAL(\单周期硬布线控制器_1_jal ), .Bne(\单周期硬布线控制器_1_bne ),
    .in_3(I_imm[1]), .uret(\单周期硬布线控制器_1_uret ), .sb(\单周期硬布线控制器_1_sb ), .auipc(\单周期硬布线控制器_1_auipc ),
    .bltu(\单周期硬布线控制器_1_bltu ), .sltiu(sltiu), .rs1(rs1), .rs2(rs2));  // open: CSRRSI, CSRRCI
  Multiplexer #(.select(1), .width(5), .disabled("Z"), .enable("false")) multiplexer_4 (
    .in0(ID_IR[19:15]), .in1(5'b10001), .out(R1_num), .sel(ecall));
  Multiplexer #(.select(1), .width(5), .disabled("Z"), .enable("false")) multiplexer_5 (
    .in0(I_imm[4:0]), .in1(5'b01010), .out(R2_num), .sel(ecall));
  Pull_Resistor #(.pull(1)) pull_resistor_1 (.node(CLK));
  Multiplexer #(.select(1), .width(12), .disabled("Z"), .enable("false")) multiplexer_6 (
    .in0(I_imm), .in1({I_imm[11:5], ID_IR[11:7]}), .out(multiplexer_6_out), .sel(\单周期硬布线控制器_1_s_type ));
  assign bit_extender_1_out = {{20{I_imm[11]}}, {I_imm[11], ID_IR[7], I_imm[10:5], ID_IR[11:8]}};  // Bit_Extender bit_extender_1
  assign bit_extender_2_out = {{12{I_imm[11]}}, {I_imm[11], ID_IR[19:12], I_imm[0], I_imm[10:1]}};  // Bit_Extender bit_extender_2
  assign bit_extender_3_out = {{12{1'b0}}, {I_imm, ID_IR[19:12]}};  // Bit_Extender bit_extender_3
  assign bit_extender_4_out = {{20{multiplexer_6_out[11]}}, multiplexer_6_out};  // Bit_Extender bit_extender_4
  Regifile regifile_1 (
    .Din(RDin), .Clk(CLK), .R1(regifile_1_r1), .R2(regifile_1_r2), .WE(RegWrite), .W_num(WB_RD),
    .R1_num(R1_num), .R2_num(R2_num));
  not not_3 (not_3_out, Stop);
  or or_3 (or_3_out, RST, branchtaken, datahazzrd);
  ID id_1 (
    .RST(or_3_out), .beq(\单周期硬布线控制器_1_beq ), .bne(\单周期硬布线控制器_1_bne ), .MemToReg(\单周期硬布线控制器_1_memtoreg ),
    .MemWrite(\单周期硬布线控制器_1_memwrite ), .ALU_OP(\单周期硬布线控制器_1_alu_op ), .ALU_SRCB(\单周期硬布线控制器_1_alu_src ),
    .RegWrite(\单周期硬布线控制器_1_regwrite ), .JAL(\单周期硬布线控制器_1_jal ), .JALR(\单周期硬布线控制器_1_jalr ),
    .URET(\单周期硬布线控制器_1_uret ), .ID_PC(ID_PC), .r1(regifile_1_r1), .r2(regifile_1_r2),
    .Bm(bit_extender_1_out), .Jm(bit_extender_2_out), .PC_4(ID_PC_4), .CLK(CLK), .beq_2(id_1_beq_2),
    .bne_2(id_1_bne_2), .MemToReg_2(id_1_memtoreg_2), .MemWrite_2(id_1_memwrite_2), .ALU_OP_2(id_1_alu_op_2),
    .ALU_SRCB_2(id_1_alu_srcb_2), .RegWrite_2(EX_RegWrite), .JAL_2(id_1_jal_2), .JALR_2(id_1_jalr_2),
    .URET_2(id_1_uret_2), .ID_PC_2(EX_PC), .r1_2(EX_R1), .r2_2(EX_R2), .Bm_2(id_1_bm_2), .Jm_2(id_1_jm_2),
    .PC_4_2(id_1_pc_4_2), .ID_IR({I_imm, ID_IR}), .ID_IR_2(EX_IR), .ecall(ecall), .ecall_2(id_1_ecall_2),
    .WRD(ID_IR[11:7]), .WRD_2(EX_RD), .Im(bit_extender_4_out), .Im_2(id_1_im_2), .halt(not_3_out),
    .auipc(\单周期硬布线控制器_1_auipc ), .bltu(\单周期硬布线控制器_1_bltu ), .sb(\单周期硬布线控制器_1_sb ), .bltu_2(id_1_bltu_2),
    .auipc_2(id_1_auipc_2), .sb_2(id_1_sb_2), .u(bit_extender_3_out), .u_2(id_1_u_2), .flush(1'b0));  // open: S_type, S_type_2, RsFoward, RtFoward, RsFoward_2, Rtfoward_2
  Shifter #(.width(32), .shift("ll")) shifter_1 (.in(id_1_bm_2), .\dist (5'b00001), .out(shifter_1_out));
  Shifter #(.width(32), .shift("ll")) shifter_2 (.in(id_1_jm_2), .\dist (5'b00001), .out(shifter_2_out));
  Multiplexer #(.select(1), .width(32), .disabled("Z"), .enable("false")) multiplexer_7 (
    .in0(EX_R2), .in1(id_1_im_2), .out(multiplexer_7_out), .sel(id_1_alu_srcb_2));
  Adder #(.width(32)) adder_2 (.a(shifter_1_out), .b(EX_PC), .out(Branch_Adress));  // open: cin, cout
  Adder #(.width(32)) adder_3 (.a(shifter_2_out), .b(EX_PC), .out(JAL_Adress));  // open: cin, cout
  ALU alu_1 (
    .X(EX_R1), .Y(multiplexer_7_out), .AluOP(id_1_alu_op_2), .Equal(alu_1_equal), .Result(alu_1_result),
    .out_6(alu_1_out_6));  // open: Result_2, out_4
  assign JALR_Adress = alu_1_result & 32'hfffffffe;  // AND_Gate and_2, 32 bits wide
  or or_4 (branchtaken, id_1_jalr_2, id_1_jal_2, or_5_out);
  or or_5 (or_5_out, and_5_out, and_4_out, and_3_out);
  and and_3 (and_3_out, id_1_beq_2, alu_1_equal);
  and and_4 (and_4_out, not_4_out, id_1_bne_2);
  and and_5 (and_5_out, id_1_bltu_2, alu_1_out_6);
  not not_4 (not_4_out, alu_1_equal);
  not not_5 (not_5_out, Stop);
  EX ex_1 (
    .RST(RST), .JAL(id_1_jal_2), .JALR(id_1_jalr_2), .URET(id_1_uret_2), .MemToReg(id_1_memtoreg_2),
    .MenWrite(id_1_memwrite_2), .ecall(id_1_ecall_2), .RegWirte(EX_RegWrite), .Write(EX_RD),
    .ALU_Result(alu_1_result), .EX_PC(EX_PC), .EX_IR(EX_IR), .PC_4(id_1_pc_4_2), .R1(EX_R1), .R2(EX_R2),
    .halt(not_5_out), .CLK(CLK), .JAL_2(ex_1_jal_2), .JALR_2(ex_1_jalr_2), .URET_2(ex_1_uret_2),
    .MemToReg_2(ex_1_memtoreg_2), .MemWrite(MemWrite), .ecall_2(ex_1_ecall_2), .RegWirte_2(MEN_RegWrite),
    .Write_2(MEM_RD), .ALU_Result_2(ALU_result), .MEN_PC(M_PC), .MEN_IR(MEM_IR), .PC_4_2(ex_1_pc_4_2),
    .R1_2(ex_1_r1_2), .R2_2(ex_1_r2_2), .sb(id_1_sb_2), .auipc(id_1_auipc_2), .sb_2(ex_1_sb_2),
    .auipc_2(ex_1_auipc_2), .U(id_1_u_2), .U_2(ex_1_u_2), .flush(1'b0));
  sb sb_1 (.in_1(ex_1_sb_2), .R2(ex_1_r2_2), .out_3(sb_1_out_3), .darta(sb_1_darta));
  not not_6 (not_6_out, ex_1_sb_2);
  Multiplexer #(.select(1), .width(32), .disabled("Z"), .enable("false")) multiplexer_8 (
    .in0(sb_1_darta), .in1(ex_1_r2_2), .out(MDin), .sel(not_6_out));
  // MIPS_RAM mips_ram_1: pin names not known; wires that end beside it: MDin, ALU_result[11:2], MemWrite, sb_1_out_3, CLK, RST, mips_ram_1_p7
  not not_7 (not_7_out, Stop);
  Mem mem_1 (
    .RST(RST), .JAL(ex_1_jal_2), .JALR(ex_1_jalr_2), .URET(ex_1_uret_2), .MemToReg(ex_1_memtoreg_2),
    .MenWrite(MemWrite), .ecall(ex_1_ecall_2), .RegWirte(MEN_RegWrite), .Write(MEM_RD),
    .ALU_Result(ALU_result), .Mem_PC(M_PC), .Mem_IR(MEM_IR), .PC_4(ex_1_pc_4_2), .R1(ex_1_r1_2),
    .R2(ex_1_r2_2), .CLK(CLK), .JAL_2(mem_1_jal_2), .JALR_2(mem_1_jalr_2), .MemToReg_2(MEN_MemtoReg),
    .ecall_2(WB_ecall), .RegWirte_2(RegWrite), .Write_2(WB_RD), .ALU_Result_2(mem_1_alu_result_2),
    .Mem_PC_2(WB_PC), .Mem_IR_2(WB_IR), .PC_4_2(WB_PC_4), .R1_2(WB_R1), .R2_2(WB_R2), .MData(mips_ram_1_p7),
    .halt(not_7_out), .Mdata_2(mem_1_mdata_2), .sb(ex_1_sb_2), .auipc(ex_1_auipc_2), .auipc_2(auipc),
    .u(ex_1_u_2), .u_2(mem_1_u_2), .flush(1'b0));  // open: URET_2, MemWrite, sb_2
  Multiplexer #(.select(1), .width(32), .disabled("Z"), .enable("false")) multiplexer_9 (
    .in0({32{1'b0}}), .in1(mem_1_u_2), .out(multiplexer_9_out), .sel(auipc));
  Multiplexer #(.select(1), .width(32), .disabled("Z"), .enable("false")) multiplexer_10 (
    .in0(mem_1_alu_result_2), .in1(mem_1_mdata_2), .out(multiplexer_10_out), .sel(MEN_MemtoReg));
  Adder #(.width(32)) adder_4 (.a(WB_PC), .b(32'h4), .out(adder_4_out));  // open: cin, cout
  or or_6 (or_6_out, mem_1_jalr_2, mem_1_jal_2);
  Multiplexer #(.select(1), .width(32), .disabled("Z"), .enable("false")) multiplexer_11 (
    .in0(multiplexer_10_out), .in1(adder_4_out), .out(multiplexer_11_out), .sel(or_6_out));
  Shifter #(.width(32), .shift("ll")) shifter_3 (.in(multiplexer_9_out), .\dist (5'b01100), .out(shifter_3_out));
  Multiplexer #(.select(1), .width(32), .disabled("Z"), .enable("false")) multiplexer_12 (
    .in0(multiplexer_11_out), .in1(U_adress), .out(RDin), .sel(auipc));
  Adder #(.width(32)) adder_5 (.a(shifter_3_out), .b(WB_PC), .out(U_adress));  // open: cin, cout
  Comparator #(.width(32), .mode("twosComplement")) comparator_2 (
    .a(WB_R1), .b(32'ha), .eq(comparator_2_eq));  // open: gt, lt
  not not_8 (not_8_out, halt);
  and and_6 (and_6_out, Go, halt);
  Comparator #(.width(32), .mode("twosComplement")) comparator_3 (
    .a(WB_R1), .b(32'h22), .eq(comparator_3_eq));  // open: gt, lt
  Register #(.width(32), .trigger("rising"), .Select("low")) register_1 (
    .D(WB_R2), .en(ecallEq), .Q(LedData), .clk(CLK), .clr(RST));
  Counter #(.width(16), .max('hffff), .ongoal("wrap"), .trigger("rising"), .behavior("new")) counter_2 (
    .count(not_8_out), .Q(\总周期数 ), .clk(CLK), .clr(RST));  // open: load, D, carry, preset, down
  Counter #(.width(1), .max('h1), .ongoal("stay"), .trigger("rising"), .behavior("new")) counter_3 (
    .D(and_6_out), .count(Stop), .Q(ecallFB), .clk(and_6_out), .clr(RST));  // open: load, carry, preset, down
  and and_7 (ecallEq, WB_ecall, comparator_3_eq);
  and and_8 (halt, WB_ecall, comparator_2_eq);

  // Other names for the same wires on the sheet: WDin[4:0] = ID_IR[11:7]; ID_IR[31:20] = I_imm; MEM_PC[31:0] = M_PC

  // Notes on the sheet:
  //   中断源
  //   中断等待指示
  //   数码管输出
  //   指令存储器
  //   控制位
  //   contents of rom_1 (hex, n*v repeats v):
  //   100493 100006f 100493 200913 300993 100006f 100493 200913 300993 100006f 100493 200913 300993
  //   100006f 100493 200913 300993 3e4000ef 100413 100493 1f49493 900533 2200893 73 24d493 48463 fedff06f
  //   900533 2200893 73 100493 249493 900533 2200893 73 48463 fedff06f 100493 1f49493 900533 2200893 73
  //   4034d493 900533 2200893 73 4044d493 900533 2200893 73 4044d493 900533 2200893 73 4044d493 900533
  //   2200893 73 4044d493 900533 2200893 73 4044d493 900533 2200893 73 4044d493 900533 2200893 73 4044d493
  //   900533 2200893 73 100413 1f41993 41f9d993 433 c00913 300b13 140413 f47413 800293 100313 499993
  //   89e9b3 1300533 2200893 73 406282b3 fe0294e3 140413 f00f93 1f47433 1c41413 800293 100313 49d993
  //   89e9b3 1300533 2200893 73 406282b3 fe0294e3 1c45413 406b0b33 b0463 f95ff06f 2b3 fff2c293 829293
  //   ff2e293 500533 2200893 73 fff00413 493 84a023 140413 448493 84a023 140413 448493 84a023 140413
  //   448493 84a023 140413 448493 84a023 140413 448493 84a023 140413 448493 84a023 140413 448493 84a023
  //   140413 448493 84a023 140413 448493 84a023 140413 448493 84a023 140413 448493 84a023 140413 448493
  //   84a023 140413 448493 84a023 140413 448493 84a023 140413 448493 84a023 140413 448493 140413 433
  //   3c00493 42983 4aa03 149a2b3 28663 134a023 1442023 ffc48493 fe9412e3 800533 2200893 73 440413 3c00493
  //   fc9416e3 a00893 73 313 2000e13 493 100913 930023 900533 2200893 73 12484b3 130313 fffe0e13 fe0e12e3
  //   800e13 313 32483 900533 2200893 73 430313 fffe0e13 fe0e14e3 a00893 73 13 430497 900533 2200893 73
  //   430497 900533 2200893 73 430497 900533 2200893 73 430497 900533 2200893 73 430497 900533 2200893 73
  //   430497 900533 2200893 73 430497 900533 2200893 73 430497 900533 2200893 73 a00893 73 fff00293 313
  //   1900413 841413 9700493 940533 2200893 73 5484b3 494b313 fe0306e3 a00893 73 ff100493 900533 2200893
  //   73 148493 fe9068e3 900533 2200893 73 a00893 73 413 140413 800533 2200893 73 240413 800533 2200893 73
  //   340413 800533 2200893 73 440413 800533 2200893 73 540413 800533 2200893 73 640413 800533 2200893 73
  //   740413 800533 2200893 73 840413 800533 2200893 2200893 73 8067
  //   流水调试日志用
  //   暂停节拍，不能为0
  //   可计数暂停的时钟源
  //   Beq
  //   Bne
  //   AluOP
  //   AluSrcB
  //   RegWrite
  //   MemToReg
  //   MemWrite
  //   为方便自动评测，需要输出流水线各段保存的PC值，注意是PC不是PC+4，另外ID段寄存器写入信息，Mem段内存写入信息也要输出
  //   数据存储器
  //   ecall比较$a7=?34
  //   ecallLED显示$a0
  //   ecall暂停
  //   ecall等待go按键
endmodule

module \重定向流水线  (
  output RegWrite,
  output MemWrite,
  output [31:0] IF_PC,
  output [31:0] ID_PC,
  output [31:0] EX_PC,
  output [31:0] M_PC,
  output [31:0] WB_PC,
  output [31:0] RDin,
  output [31:0] MDin,
  output [31:0] LedData
);

  wire alu_1_equal, alu_1_out_6, and_1_out, and_2_out, and_3_out, and_5_out, and_6_out, and_7_out, and_8_out,
       and_9_out, auipc, branchtaken, CLK, clock_1_out, comparator_1_eq, comparator_1_lt, comparator_2_eq,
       comparator_3_eq, d_ff_1_q, datahazzrd, ecall, ecallEq, ex_1_auipc_2, ex_1_ecall_2, ex_1_jal_2,
       ex_1_jalr_2, ex_1_sb_2, ex_1_uret_2, EX_ecall, EX_MemToReg, EX_RegWrite, flush, Go, halt,
       id_1_alu_srcb_2, id_1_auipc_2, id_1_beq_2, id_1_bltu_2, id_1_bne_2, id_1_jal_2, id_1_jalr_2,
       id_1_memwrite_2, id_1_sb_2, id_1_uret_2, IR1, IR2, IR3, LoadUse, mem_1_jal_2, mem_1_jalr_2,
       MEN_MemToReg, MEN_MemtoReg_t, MEN_RegWrite, nand_1_out, not_1_out, not_2_out, not_3_out, not_4_out,
       not_5_out, or_1_out, or_2_out, or_3_out, or_4_out, or_6_out, or_7_out, rs1, rs2, RST, sltiu, stall,
       W1, W2, W3, WB_ecall, \单周期硬布线控制器_1_alu_src , \单周期硬布线控制器_1_auipc , \单周期硬布线控制器_1_beq ,
       \单周期硬布线控制器_1_bltu , \单周期硬布线控制器_1_bne , \单周期硬布线控制器_1_jal , \单周期硬布线控制器_1_jalr , \单周期硬布线控制器_1_memtoreg ,
       \单周期硬布线控制器_1_memwrite , \单周期硬布线控制器_1_regwrite , \单周期硬布线控制器_1_s_type , \单周期硬布线控制器_1_sb ,
       \单周期硬布线控制器_1_uret ;
  wire [1:0] id_1_rsfoward_2, id_1_rtfoward_2, RSfoward, RTfoward;
  wire [3:0] id_1_alu_op_2, \单周期硬布线控制器_1_alu_op ;
  wire [4:0] EX_RD, MEM_RD, R1_num, R2_num, WB_RD;
  wire [11:0] I_imm, multiplexer_6_out;
  wire [12:0] CNT_num;
  wire [15:0] \LoadUse次数 , \总周期数 , \插入气泡数 , \无条件分支数 , \条件分支成功数 ;
  wire [19:0] ID_IR;
  wire [31:0] adder_1_out, adder_4_out, alu_1_result, ALU_result, bit_extender_1_out, bit_extender_2_out,
       bit_extender_3_out, bit_extender_4_out, Branch_Adress, ex_1_pc_4_2, ex_1_r1_2, ex_1_u_2, EX_IR, EX_R1,
       EX_R2, id_1_bm_2, id_1_im_2, id_1_jm_2, id_1_pc_4_2, id_1_u_2, ID_PC_4, IF_IR, JAL_Adress,
       JALR_Adress, mem_1_alu_result_2, mem_1_mdata_2, mem_1_u_2, MEM_IR, MEN_PC, mips_ram_1_p6,
       multiplexer_1_out, multiplexer_2_out, multiplexer_3_out, multiplexer_9_out, multiplexer_10_out,
       multiplexer_11_out, multiplexer_12_out, re_R1, re_R2, regifile_1_r1, regifile_1_r2, shifter_1_out,
       shifter_2_out, shifter_3_out, U_adress, WB_IR, WB_PC_4, WB_R1, WB_R2;

  Button \u_总复位  (.out(RST));
  Button _1 (.out(IR1));
  Button _2 (.out(IR2));
  Button _3 (.out(IR3));
  // Probe on \总周期数 
  // Probe on \总周期数 
  Button \u_继续运行  (.out(Go));
  LED #(.active("true")) led_1 (.in(W1));
  LED #(.active("true")) led_2 (.in(W2));
  LED #(.active("true")) led_3 (.in(W3));
  Hex_Digit_Display hex_digit_display_1 (.value(LedData[31:28]));  // open: dp
  // Probe on IF_PC[19:0]
  // RiscV_Probe riscv_probe_1: pin names not known; wires that end beside it: IF_IR
  foward foward_1 (
    .EX_WriteReg(EX_RD), .rs(R1_num), .EX_RegWrite(EX_RegWrite), .rsused(rs1), .EX_WriteReg_2(EX_RD),
    .MEM_WriteReg(MEM_RD), .rt(R2_num), .rs_2(R1_num), .EX_RegWrite_2(EX_RegWrite),
    .MEM_RegWrite(MEN_RegWrite), .rtused(rs2), .rsused_2(EX_RegWrite), .MEM_WriteReg_2(MEM_RD),
    .rt_2(R2_num), .MEM_RegWrite_2(MEN_RegWrite), .rtused_2(rs2), .RSFoward(RSfoward), .RTFoward(RTfoward));
  Hex_Digit_Display hex_digit_display_2 (.value(LedData[23:20]));  // open: dp
  Hex_Digit_Display hex_digit_display_3 (.value(LedData[27:24]));  // open: dp
  // Probe on ID_PC[19:0]
  // RiscV_Probe riscv_probe_2: pin names not known; wires that end beside it: {I_imm, ID_IR}
  Hex_Digit_Display hex_digit_display_4 (.value(LedData[19:16]));  // open: dp
  Hex_Digit_Display hex_digit_display_5 (.value(LedData[15:12]));  // open: dp
  loaduse loaduse_1 (
    .rsused(rs1), .rs(R1_num), .EX_WriteReg(EX_RD), .EX_MemRead(EX_MemToReg), .rtused(rs2), .rt(R2_num),
    .EX_WriteReg_2(EX_RD), .EX_MemRead_2(EX_MemToReg), .LoadUse(LoadUse));
  Hex_Digit_Display hex_digit_display_6 (.value(LedData[7:4]));  // open: dp
  Hex_Digit_Display hex_digit_display_7 (.value(LedData[11:8]));  // open: dp
  // Probe on EX_PC[19:0]
  // RiscV_Probe riscv_probe_3: pin names not known; wires that end beside it: EX_IR
  Hex_Digit_Display hex_digit_display_8 (.value(LedData[3:0]));  // open: dp
  // Probe on \总周期数 
  // Probe on M_PC[19:0]
  // RiscV_Probe riscv_probe_4: pin names not known; wires that end beside it: MEM_IR
  // Probe on \总周期数 
  // Probe on \无条件分支数 
  // Probe on \条件分支成功数 
  // Probe on \插入气泡数 
  // Probe on \LoadUse次数 
  // Probe on IF_PC[11:0]
  // Probe on WB_PC[19:0]
  // RiscV_Probe riscv_probe_5: pin names not known; wires that end beside it: WB_IR
  Multiplexer #(.select(1), .width(32), .disabled("Z"), .enable("false")) multiplexer_1 (
    .in0(adder_1_out), .in1(Branch_Adress), .out(multiplexer_1_out), .sel(or_6_out));
  // Probe on ID_PC[11:0]
  // Probe on EX_PC[11:0]
  Multiplexer #(.select(1), .width(32), .disabled("Z"), .enable("false")) multiplexer_2 (
    .in0(multiplexer_1_out), .in1(JAL_Adress), .out(multiplexer_2_out), .sel(id_1_jal_2));
  Adder #(.width(32)) adder_1 (.a(IF_PC), .b(32'h4), .out(adder_1_out));  // open: cin, cout
  datahazzard datahazzard_1 (
    .RtUsed(rs1), .Rt(R1_num), .Rt_2(R1_num), .MEN_WriteReg(MEM_RD), .MEN_Regwrite(MEN_RegWrite),
    .RtUsed_2(rs1), .Rt_3(R1_num), .Rt_4(R1_num), .EX_WriteReg(EX_RD), .EX_Regwrite(EX_RegWrite),
    .RsUsed(rs2), .Rs(R2_num), .Rs_2(R2_num), .EX_WriteReg_2(EX_RD), .EX_Regwrite_2(EX_RegWrite),
    .RsUsed_2(rs2), .Rs_3(R2_num), .Rs_4(R2_num), .MEN_WriteReg_2(MEM_RD), .MEN_Regwrite_2(MEN_RegWrite),
    .datahazzed(datahazzrd));
  // Probe on M_PC[11:0]
  D_Flip_Flop #(.trigger("high"), .Pre_Clr_Positions("LEGACY"), .NegatePresetClear("false"), .enable("true"), .NewFFLayout("false")) d_ff_1 (.Q(d_ff_1_q));  // open: clk, D, Qn, preset, en, reset
  // Probe on 13'h30
  Multiplexer #(.select(1), .width(32), .disabled("Z"), .enable("false")) multiplexer_3 (
    .in0(multiplexer_2_out), .in1(JALR_Adress), .out(multiplexer_3_out), .sel(id_1_jalr_2));
  or or_1 (or_1_out, and_1_out, Go);
  and and_1 (and_1_out, not_2_out, not_1_out);
  not not_1 (not_1_out, LoadUse);
  not not_2 (not_2_out, halt);
  // Probe on WB_PC[11:0]
  Comparator #(.width(13), .mode("twosComplement")) comparator_1 (
    .a(CNT_num), .b(13'h30), .eq(comparator_1_eq), .lt(comparator_1_lt));  // open: gt
  Clock #(.highDuration(1), .lowDuration(1)) clock_1 (.out(clock_1_out));
  Register #(.width(32), .trigger("rising"), .Select("low")) PC (
    .D(multiplexer_3_out), .en(or_1_out), .Q(IF_PC), .clk(CLK), .clr(RST));
  \气泡处理  \u_气泡处理_1  (
    .datahazzd(datahazzrd), .branch(branchtaken), .datahazzd_2(datahazzrd), .stall(stall), .flush(flush));
  nand nand_1 (nand_1_out, d_ff_1_q, comparator_1_eq);
  Counter #(.width(13), .max('h1fff), .ongoal("stay"), .trigger("rising"), .behavior("old")) counter_1 (
    .count(comparator_1_lt), .Q(CNT_num), .clk(clock_1_out));  // open: load, D, carry, clr, preset
  assign CLK = nand_1_out ? clock_1_out : 1'bz;  // Controlled_Buffer controlled_buffer_1
  Pull_Resistor #(.pull(1)) pull_resistor_1 (.node(CLK));
  ROM #(.addrWidth(10), .dataWidth(32), .Select("high")) rom_1 (.addr(IF_PC[11:2]), .data(IF_IR));
  and and_2 (and_2_out, not_3_out, Go);
  not not_3 (not_3_out, halt);
  or or_2 (or_2_out, RST, branchtaken);
  // RiscV_Probe riscv_probe_6: pin names not known; wires that end beside it: IF_IR
  IF if_1 (
    .CLK(CLK), .RST(or_2_out), .IR(IF_IR), .PC(IF_PC), .PC_4(adder_1_out), .IR_2({I_imm, ID_IR}),
    .PC_2(ID_PC), .PC_4_2(ID_PC_4), .flush(1'b0), .en(or_3_out));
  or or_3 (or_3_out, and_2_out, LoadUse);
  \单周期硬布线控制器  \u_单周期硬布线控制器_1  (
    .Funct({I_imm[10], I_imm[5], ID_IR[14:12]}), .OP(ID_IR[6:2]), .ALU_OP(\单周期硬布线控制器_1_alu_op ),
    .MemToReg(\单周期硬布线控制器_1_memtoreg ), .MemWrite(\单周期硬布线控制器_1_memwrite ), .ALU_SRC(\单周期硬布线控制器_1_alu_src ),
    .RegWrite(\单周期硬布线控制器_1_regwrite ), .ecall(ecall), .S_type(\单周期硬布线控制器_1_s_type ),
    .Jalr(\单周期硬布线控制器_1_jalr ), .Beq(\单周期硬布线控制器_1_beq ), .JAL(\单周期硬布线控制器_1_jal ), .Bne(\单周期硬布线控制器_1_bne ),
    .in_3(I_imm[1]), .uret(\单周期硬布线控制器_1_uret ), .sb(\单周期硬布线控制器_1_sb ), .auipc(\单周期硬布线控制器_1_auipc ),
    .bltu(\单周期硬布线控制器_1_bltu ), .sltiu(sltiu), .rs1(rs1), .rs2(rs2));  // open: CSRRSI, CSRRCI
  Multiplexer #(.select(1), .width(5), .disabled("Z"), .enable("false")) multiplexer_4 (
    .in0(ID_IR[19:15]), .in1(5'b10001), .out(R1_num), .sel(ecall));
  Multiplexer #(.select(1), .width(5), .disabled("Z"), .enable("false")) multiplexer_5 (
    .in0(I_imm[4:0]), .in1(5'b01010), .out(R2_num), .sel(ecall));
  Multiplexer #(.select(1), .width(12), .disabled("Z"), .enable("false")) multiplexer_6 (
    .in0(I_imm), .in1({I_imm[11:5], ID_IR[11:7]}), .out(multiplexer_6_out), .sel(\单周期硬布线控制器_1_s_type ));
  assign bit_extender_1_out = {{20{I_imm[11]}}, {I_imm[11], ID_IR[7], I_imm[10:5], ID_IR[11:8]}};  // Bit_Extender bit_extender_1
  assign bit_extender_2_out = {{12{I_imm[11]}}, {I_imm[11], ID_IR[19:12], I_imm[0], I_imm[10:1]}};  // Bit_Extender bit_extender_2
  assign bit_extender_3_out = {{12{1'b0}}, {I_imm, ID_IR[19:12]}};  // Bit_Extender bit_extender_3
  Regifile regifile_1 (
    .Din(RDin), .Clk(CLK), .R1(regifile_1_r1), .R2(regifile_1_r2), .WE(RegWrite), .W_num(WB_RD),
    .R1_num(R1_num), .R2_num(R2_num));
  assign bit_extender_4_out = {{20{multiplexer_6_out[11]}}, multiplexer_6_out};  // Bit_Extender bit_extender_4
  and and_3 (and_3_out, ~Go, halt);  // AND_Gate
  or or_4 (or_4_out, RST, branchtaken, LoadUse);
  ID id_1 (
    .RST(or_4_out), .beq(\单周期硬布线控制器_1_beq ), .bne(\单周期硬布线控制器_1_bne ), .MemToReg(\单周期硬布线控制器_1_memtoreg ),
    .MemWrite(\单周期硬布线控制器_1_memwrite ), .ALU_OP(\单周期硬布线控制器_1_alu_op ), .ALU_SRCB(\单周期硬布线控制器_1_alu_src ),
    .RegWrite(\单周期硬布线控制器_1_regwrite ), .JAL(\单周期硬布线控制器_1_jal ), .JALR(\单周期硬布线控制器_1_jalr ),
    .URET(\单周期硬布线控制器_1_uret ), .ID_PC(ID_PC), .r1(regifile_1_r1), .r2(regifile_1_r2),
    .Bm(bit_extender_1_out), .Jm(bit_extender_2_out), .PC_4(ID_PC_4), .CLK(CLK), .beq_2(id_1_beq_2),
    .bne_2(id_1_bne_2), .MemToReg_2(EX_MemToReg), .MemWrite_2(id_1_memwrite_2), .ALU_OP_2(id_1_alu_op_2),
    .ALU_SRCB_2(id_1_alu_srcb_2), .RegWrite_2(EX_RegWrite), .JAL_2(id_1_jal_2), .JALR_2(id_1_jalr_2),
    .URET_2(id_1_uret_2), .ID_PC_2(EX_PC), .r1_2(EX_R1), .r2_2(EX_R2), .Bm_2(id_1_bm_2), .Jm_2(id_1_jm_2),
    .PC_4_2(id_1_pc_4_2), .ID_IR({I_imm, ID_IR}), .ID_IR_2(EX_IR), .ecall(ecall), .ecall_2(EX_ecall),
    .WRD(ID_IR[11:7]), .WRD_2(EX_RD), .Im(bit_extender_4_out), .Im_2(id_1_im_2), .halt(and_3_out),
    .auipc(\单周期硬布线控制器_1_auipc ), .bltu(\单周期硬布线控制器_1_bltu ), .sb(\单周期硬布线控制器_1_sb ), .bltu_2(id_1_bltu_2),
    .auipc_2(id_1_auipc_2), .sb_2(id_1_sb_2), .u(bit_extender_3_out), .u_2(id_1_u_2), .flush(1'b0),
    .RsFoward(RSfoward), .RtFoward(RTfoward), .RsFoward_2(id_1_rsfoward_2), .Rtfoward_2(id_1_rtfoward_2));  // open: S_type, S_type_2
  Multiplexer #(.select(2), .width(32), .disabled("Z"), .enable("false")) multiplexer_7 (
    .in0(EX_R1), .in1(RDin), .in2(ALU_result), .out(re_R1), .sel(id_1_rsfoward_2));  // open: in3
  Multiplexer #(.select(2), .width(32), .disabled("Z"), .enable("false")) multiplexer_8 (
    .in0(EX_R2), .in1(RDin), .in2(ALU_result), .out(re_R2), .sel(id_1_rtfoward_2));  // open: in3
  Shifter #(.width(32), .shift("ll")) shifter_1 (.in(id_1_bm_2), .\dist (5'b00001), .out(shifter_1_out));
  Shifter #(.width(32), .shift("ll")) shifter_2 (.in(id_1_jm_2), .\dist (5'b00001), .out(shifter_2_out));
  Adder #(.width(32)) adder_2 (.a(shifter_1_out), .b(EX_PC), .out(Branch_Adress));  // open: cin, cout
  Adder #(.width(32)) adder_3 (.a(shifter_2_out), .b(EX_PC), .out(JAL_Adress));  // open: cin, cout
  Multiplexer #(.select(1), .width(32), .disabled("Z"), .enable("false")) multiplexer_9 (
    .in0(re_R2), .in1(id_1_im_2), .out(multiplexer_9_out), .sel(id_1_alu_srcb_2));
  ALU alu_1 (
    .X(re_R1), .Y(multiplexer_9_out), .AluOP(id_1_alu_op_2), .Equal(alu_1_equal), .Result(alu_1_result),
    .out_6(alu_1_out_6));  // open: Result_2, out_4
  assign JALR_Adress = alu_1_result & 32'hfffffffe;  // AND_Gate and_4, 32 bits wide
  or or_5 (branchtaken, id_1_jalr_2, id_1_jal_2, or_6_out);
  and and_5 (and_5_out, id_1_bltu_2, alu_1_out_6);
  not not_4 (not_4_out, alu_1_equal);
  or or_6 (or_6_out, and_5_out, and_6_out, and_7_out);
  and and_6 (and_6_out, not_4_out, id_1_bne_2);
  and and_7 (and_7_out, id_1_beq_2, alu_1_equal);
  and and_8 (and_8_out, ~Go, halt);  // AND_Gate
  EX ex_1 (
    .RST(RST), .JAL(id_1_jal_2), .JALR(id_1_jalr_2), .URET(id_1_uret_2), .MemToReg(EX_MemToReg),
    .MenWrite(id_1_memwrite_2), .ecall(EX_ecall), .RegWirte(EX_RegWrite), .Write(EX_RD),
    .ALU_Result(alu_1_result), .EX_PC(EX_PC), .EX_IR(EX_IR), .PC_4(id_1_pc_4_2), .R1(re_R1), .R2(re_R2),
    .halt(and_8_out), .CLK(CLK), .JAL_2(ex_1_jal_2), .JALR_2(ex_1_jalr_2), .URET_2(ex_1_uret_2),
    .MemToReg_2(MEN_MemToReg), .MemWrite(MemWrite), .ecall_2(ex_1_ecall_2), .RegWirte_2(MEN_RegWrite),
    .Write_2(MEM_RD), .ALU_Result_2(ALU_result), .MEN_PC(M_PC), .MEN_IR(MEM_IR), .PC_4_2(ex_1_pc_4_2),
    .R1_2(ex_1_r1_2), .R2_2(MDin), .sb(id_1_sb_2), .auipc(id_1_auipc_2), .sb_2(ex_1_sb_2),
    .auipc_2(ex_1_auipc_2), .U(id_1_u_2), .U_2(ex_1_u_2), .flush(1'b0));
  // MIPS_RAM mips_ram_1: pin names not known; wires that end beside it: ALU_result[11:2], MDin, MemWrite, CLK, RST, mips_ram_1_p6
  and and_9 (and_9_out, ~Go, halt);  // AND_Gate
  Mem mem_1 (
    .RST(RST), .JAL(ex_1_jal_2), .JALR(ex_1_jalr_2), .URET(ex_1_uret_2), .MemToReg(MEN_MemToReg),
    .MenWrite(MemWrite), .ecall(ex_1_ecall_2), .RegWirte(MEN_RegWrite), .Write(MEM_RD),
    .ALU_Result(ALU_result), .Mem_PC(M_PC), .Mem_IR(MEM_IR), .PC_4(ex_1_pc_4_2), .R1(ex_1_r1_2), .R2(MDin),
    .CLK(CLK), .JAL_2(mem_1_jal_2), .JALR_2(mem_1_jalr_2), .MemToReg_2(MEN_MemtoReg_t), .ecall_2(WB_ecall),
    .RegWirte_2(RegWrite), .Write_2(WB_RD), .ALU_Result_2(mem_1_alu_result_2), .Mem_PC_2(WB_PC),
    .Mem_IR_2(WB_IR), .PC_4_2(WB_PC_4), .R1_2(WB_R1), .R2_2(WB_R2), .MData(mips_ram_1_p6), .halt(and_9_out),
    .Mdata_2(mem_1_mdata_2), .sb(ex_1_sb_2), .auipc(ex_1_auipc_2), .auipc_2(auipc), .u(ex_1_u_2),
    .u_2(mem_1_u_2), .flush(1'b0));  // open: URET_2, MemWrite, sb_2
  Adder #(.width(32)) adder_4 (.a(WB_PC), .b(32'h4), .out(adder_4_out));  // open: cin, cout
  Multiplexer #(.select(1), .width(32), .disabled("Z"), .enable("false")) multiplexer_10 (
    .in0({32{1'b0}}), .in1(mem_1_u_2), .out(multiplexer_10_out), .sel(auipc));
  Multiplexer #(.select(1), .width(32), .disabled("Z"), .enable("false")) multiplexer_11 (
    .in0(mem_1_alu_result_2), .in1(mem_1_mdata_2), .out(multiplexer_11_out), .sel(MEN_MemtoReg_t));
  Shifter #(.width(32), .shift("ll")) shifter_3 (.in(multiplexer_10_out), .\dist (5'b01100), .out(shifter_3_out));
  or or_7 (or_7_out, mem_1_jalr_2, mem_1_jal_2);
  Multiplexer #(.select(1), .width(32), .disabled("Z"), .enable("false")) multiplexer_12 (
    .in0(multiplexer_11_out), .in1(adder_4_out), .out(multiplexer_12_out), .sel(or_7_out));
  Multiplexer #(.select(1), .width(32), .disabled("Z"), .enable("false")) multiplexer_13 (
    .in0(multiplexer_12_out), .in1(U_adress), .out(RDin), .sel(auipc));
  Adder #(.width(32)) adder_5 (.a(shifter_3_out), .b(MEN_PC), .out(U_adress));  // open: cin, cout
  Comparator #(.width(32), .mode("twosComplement")) comparator_2 (
    .a(EX_R1), .b(32'h22), .eq(comparator_2_eq));  // open: gt, lt
  Comparator #(.width(32), .mode("twosComplement")) comparator_3 (
    .a(EX_R1), .b(32'ha), .eq(comparator_3_eq));  // open: gt, lt
  Register #(.width(32), .trigger("rising"), .Select("low")) register_1 (
    .D(EX_R2), .en(ecallEq), .Q(LedData), .clk(CLK), .clr(RST));
  not not_5 (not_5_out, halt);
  Counter #(.width(16), .max('hffff), .ongoal("wrap"), .trigger("rising"), .behavior("new")) counter_2 (
    .count(not_5_out), .Q(\总周期数 ), .clk(CLK), .clr(RST));  // open: load, D, carry, preset, down
  and and_10 (ecallEq, EX_ecall, comparator_2_eq);
  and and_11 (halt, EX_ecall, comparator_3_eq);

  // Other names for the same wires on the sheet: WDin[4:0] = ID_IR[11:7]; ID_IR[31:20] = I_imm; MEM_PC[31:0] = M_PC

  // Notes on the sheet:
  //   中断源
  //   时空图监测，可删除
  //   中断等待指示
  //   数码管输出
  //   控制位
  //   流水调试日志用
  //   暂停节拍，不能为0
  //   戳工具置1进入计数暂停模式，ctrl+k时钟自动运行到对应节拍暂停
  //   ctrl+k关闭时钟连续运行，将控制位置零，进入单步调试模式调试
  //   可计数暂停的时钟源
  //   指令存储器
  //   contents of rom_1 (hex, n*v repeats v):
  //   100493 100006f 100493 200913 300993 100006f 100493 200913 300993 100006f 100493 200913 300993
  //   100006f 100493 200913 300993 29c000ef 100413 100493 1f49493 900533 2200893 73 24d493 48463 fedff06f
  //   900533 2200893 73 100493 249493 900533 2200893 73 48463 fedff06f 100493 1f49493 900533 2200893 73
  //   4034d493 900533 2200893 73 4044d493 900533 2200893 73 4044d493 900533 2200893 73 4044d493 900533
  //   2200893 73 4044d493 900533 2200893 73 4044d493 900533 2200893 73 4044d493 900533 2200893 73 4044d493
  //   900533 2200893 73 100413 1f41993 41f9d993 433 c00913 300b13 140413 f47413 800293 100313 499993
  //   89e9b3 1300533 2200893 73 406282b3 fe0294e3 140413 f00f93 1f47433 1c41413 800293 100313 49d993
  //   89e9b3 1300533 2200893 73 406282b3 fe0294e3 1c45413 406b0b33 b0463 f95ff06f 2b3 fff2c293 829293
  //   ff2e293 500533 2200893 73 fff00413 493 84a023 140413 448493 84a023 140413 448493 84a023 140413
  //   448493 84a023 140413 448493 84a023 140413 448493 84a023 140413 448493 84a023 140413 448493 84a023
  //   140413 448493 84a023 140413 448493 84a023 140413 448493 84a023 140413 448493 84a023 140413 448493
  //   84a023 140413 448493 84a023 140413 448493 84a023 140413 448493 84a023 140413 448493 140413 433
  //   3c00493 42983 4aa03 149a2b3 28663 134a023 1442023 ffc48493 fe9412e3 800533 2200893 73 440413 3c00493
  //   fc9416e3 a00893 73 413 140413 800533 2200893 73 240413 800533 2200893 73 340413 800533 2200893 73
  //   440413 800533 2200893 73 540413 800533 2200893 73 640413 800533 2200893 73 740413 800533 2200893 73
  //   840413 800533 2200893 2200893 73 8067
  //   为方便自动评测，需要输出流水线各段保存的PC值，注意是PC不是PC+4，另外ID段寄存器写入信息，Mem段内存写入信息也要输出
  //   Beq
  //   Bne
  //   MemToReg
  //   MemWrite
  //   AluOP
  //   AluSrcB
  //   RegWrite
  //   数据存储器
  //   ecall暂停
  //   ecall比较$a7=?34
  //   ecallLED显示$a0
endmodule
module \理想流水线  (
  output RegWrite,
  output MemWrite,
  output [31:0] IF_PC,
  output [31:0] ID_PC,
  output [31:0] EX_PC,
  output [31:0] M_PC,
  output [31:0] WB_PC,
  output [31:0] RDin,
  output [31:0] MDin,
  output [31:0] LedData
);

  wire alu_1_equal, alu_1_out_6, and_3_out, and_4_out, and_5_out, and_6_out, CLK, clock_1_out,
       comparator_1_eq, comparator_1_lt, comparator_2_eq, d_ff_1_q, ecall, ecallEq, ecallFB, ex_1_auipc_2,
       ex_1_ecall_2, ex_1_jal_2, ex_1_jalr_2, ex_1_memtoreg_2, ex_1_memwrite, ex_1_regwirte_2, ex_1_sb_2,
       ex_1_uret_2, Go, halt, id_1_alu_srcb_2, id_1_auipc_2, id_1_beq_2, id_1_bltu_2, id_1_bne_2,
       id_1_ecall_2, id_1_jal_2, id_1_jalr_2, id_1_memtoreg_2, id_1_memwrite_2, id_1_regwrite_2, id_1_sb_2,
       id_1_uret_2, IR1, IR2, IR3, mem_1_jal_2, mem_1_jalr_2, mem_1_sb_2, MEN_MemtoReg, MEN_RegWrite,
       nand_1_out, not_1_out, not_2_out, not_3_out, not_4_out, or_1_out, or_2_out, RST, sltiu, W1, W2, W3,
       WB_ecall, \单周期硬布线控制器_1_alu_src , \单周期硬布线控制器_1_auipc , \单周期硬布线控制器_1_beq , \单周期硬布线控制器_1_bltu ,
       \单周期硬布线控制器_1_bne , \单周期硬布线控制器_1_ecall , \单周期硬布线控制器_1_jal , \单周期硬布线控制器_1_jalr , \单周期硬布线控制器_1_memtoreg ,
       \单周期硬布线控制器_1_memwrite , \单周期硬布线控制器_1_regwrite , \单周期硬布线控制器_1_s_type , \单周期硬布线控制器_1_sb ,
       \单周期硬布线控制器_1_uret ;
  wire [3:0] id_1_alu_op_2, \单周期硬布线控制器_1_alu_op ;
  wire [4:0] ex_1_write_2, id_1_wrd_2, multiplexer_4_out, multiplexer_5_out, WB_RD;
  wire [11:0] I_imm, multiplexer_6_out;
  wire [12:0] CNT_num;
  wire [15:0] \LoadUse次数 , \总周期数 , \插入气泡数 , \无条件分支数 , \条件分支成功数 ;
  wire [19:0] ID_IR;
  wire [31:0] adder_1_out, adder_4_out, alu_1_result, ALU_result, bit_extender_1_out, bit_extender_2_out,
       bit_extender_3_out, bit_extender_4_out, Branch_Adress, ex_1_pc_4_2, ex_1_r1_2, ex_1_u_2, EX_IR, EX_R1,
       EX_R2, id_1_bm_2, id_1_im_2, id_1_jm_2, id_1_pc_4_2, id_1_u_2, ID_PC_4, IF_IR, JAL_Adress,
       JALR_Adress, mem_1_alu_result_2, mem_1_mdata_2, mem_1_u_2, MEM_IR, MEN_PC, mips_ram_1_p6,
       multiplexer_1_out, multiplexer_2_out, multiplexer_3_out, multiplexer_7_out, multiplexer_8_out,
       multiplexer_9_out, multiplexer_10_out, regifile_1_r1, regifile_1_r2, shifter_1_out, shifter_2_out,
       shifter_3_out, U_adress, WB_IR, WB_PC_4, WB_R1, WB_R2;

  Button \u_总复位  (.out(RST));
  Button _1 (.out(IR1));
  Button _2 (.out(IR2));
  Button _3 (.out(IR3));
  // Probe on \总周期数 
  // Probe on \总周期数 
  Button \u_继续运行  (.out(Go));
  LED #(.active("true")) led_1 (.in(W1));
  LED #(.active("true")) led_2 (.in(W2));
  LED #(.active("true")) led_3 (.in(W3));
  Hex_Digit_Display hex_digit_display_1 (.value(LedData[31:28]));  // open: dp
  // Probe on IF_PC[19:0]
  // RiscV_Probe riscv_probe_1: pin names not known; wires that end beside it: IF_IR
  Multiplexer #(.select(1), .width(32), .disabled("Z"), .enable("false")) multiplexer_1 (
    .in0(adder_1_out), .in1(Branch_Adress), .out(multiplexer_1_out), .sel(or_1_out));
  Adder #(.width(32)) adder_1 (.a(IF_PC), .b(32'h4), .out(adder_1_out));  // open: cin, cout
  Hex_Digit_Display hex_digit_display_2 (.value(LedData[23:20]));  // open: dp
  Hex_Digit_Display hex_digit_display_3 (.value(LedData[27:24]));  // open: dp
  // Probe on ID_PC[19:0]
  // RiscV_Probe riscv_probe_2: pin names not known; wires that end beside it: {I_imm, ID_IR}
  Multiplexer #(.select(1), .width(32), .disabled("Z"), .enable("false")) multiplexer_2 (
    .in0(multiplexer_1_out), .in1(JAL_Adress), .out(multiplexer_2_out), .sel(id_1_jal_2));
  Hex_Digit_Display hex_digit_display_4 (.value(LedData[15:12]));  // open: dp
  Hex_Digit_Display hex_digit_display_5 (.value(LedData[19:16]));  // open: dp
  Register #(.width(32), .trigger("rising"), .Select("low")) PC (
    .D(multiplexer_3_out), .en(not_1_out), .Q(IF_PC), .clk(CLK), .clr(RST));
  Multiplexer #(.select(1), .width(32), .disabled("Z"), .enable("false")) multiplexer_3 (
    .in0(multiplexer_2_out), .in1(JALR_Adress), .out(multiplexer_3_out), .sel(id_1_jalr_2));
  not not_1 (not_1_out, halt);
  Hex_Digit_Display hex_digit_display_6 (.value(LedData[7:4]));  // open: dp
  Hex_Digit_Display hex_digit_display_7 (.value(LedData[11:8]));  // open: dp
  // Probe on EX_PC[19:0]
  // RiscV_Probe riscv_probe_3: pin names not known; wires that end beside it: EX_IR
  Hex_Digit_Display hex_digit_display_8 (.value(LedData[3:0]));  // open: dp
  // Probe on \总周期数 
  // Probe on M_PC[19:0]
  // RiscV_Probe riscv_probe_4: pin names not known; wires that end beside it: MEM_IR
  // Probe on \总周期数 
  // Probe on \无条件分支数 
  // Probe on \条件分支成功数 
  // Probe on \插入气泡数 
  // Probe on \LoadUse次数 
  // RiscV_Probe riscv_probe_5: pin names not known; wires that end beside it: IF_IR
  ROM #(.addrWidth(10), .dataWidth(32), .Select("high")) rom_1 (.addr(IF_PC[11:2]), .data(IF_IR));
  // Probe on IF_PC[11:0]
  // Probe on WB_PC[19:0]
  // RiscV_Probe riscv_probe_6: pin names not known; wires that end beside it: WB_IR
  IF if_1 (
    .CLK(CLK), .RST(RST), .IR(IF_IR), .PC(IF_PC), .PC_4(adder_1_out), .IR_2({I_imm, ID_IR}), .PC_2(ID_PC),
    .PC_4_2(ID_PC_4), .flush(halt));  // open: en
  // Probe on ID_PC[11:0]
  // Probe on EX_PC[11:0]
  and and_1 (ecall, ~ecallFB, \单周期硬布线控制器_1_ecall );  // AND_Gate
  // Probe on M_PC[11:0]
  D_Flip_Flop #(.trigger("high"), .Pre_Clr_Positions("LEGACY"), .NegatePresetClear("false"), .enable("true"), .NewFFLayout("false")) d_ff_1 (.Q(d_ff_1_q));  // open: clk, D, Qn, preset, en, reset
  // Probe on 13'hc
  // Probe on WB_PC[11:0]
  Comparator #(.width(13), .mode("twosComplement")) comparator_1 (
    .a(CNT_num), .b(13'hc), .eq(comparator_1_eq), .lt(comparator_1_lt));  // open: gt
  Clock #(.highDuration(1), .lowDuration(1)) clock_1 (.out(clock_1_out));
  \单周期硬布线控制器  \u_单周期硬布线控制器_1  (
    .Funct({I_imm[10], I_imm[5], ID_IR[14:12]}), .OP(ID_IR[6:2]), .ALU_OP(\单周期硬布线控制器_1_alu_op ),
    .MemToReg(\单周期硬布线控制器_1_memtoreg ), .MemWrite(\单周期硬布线控制器_1_memwrite ), .ALU_SRC(\单周期硬布线控制器_1_alu_src ),
    .RegWrite(\单周期硬布线控制器_1_regwrite ), .ecall(\单周期硬布线控制器_1_ecall ), .S_type(\单周期硬布线控制器_1_s_type ),
    .Jalr(\单周期硬布线控制器_1_jalr ), .Beq(\单周期硬布线控制器_1_beq ), .JAL(\单周期硬布线控制器_1_jal ), .Bne(\单周期硬布线控制器_1_bne ),
    .in_3(I_imm[1]), .uret(\单周期硬布线控制器_1_uret ), .sb(\单周期硬布线控制器_1_sb ), .auipc(\单周期硬布线控制器_1_auipc ),
    .bltu(\单周期硬布线控制器_1_bltu ), .sltiu(sltiu));  // open: rs1, rs2, CSRRSI, CSRRCI
  Multiplexer #(.select(1), .width(5), .disabled("Z"), .enable("false")) multiplexer_4 (
    .in0(ID_IR[19:15]), .in1(5'b10001), .out(multiplexer_4_out), .sel(ecall));
  Multiplexer #(.select(1), .width(5), .disabled("Z"), .enable("false")) multiplexer_5 (
    .in0(I_imm[4:0]), .in1(5'b01010), .out(multiplexer_5_out), .sel(ecall));
  nand nand_1 (nand_1_out, d_ff_1_q, comparator_1_eq);
  Counter #(.width(13), .max('h1fff), .ongoal("stay"), .trigger("rising"), .behavior("old")) counter_1 (
    .count(comparator_1_lt), .Q(CNT_num), .clk(clock_1_out));  // open: load, D, carry, clr, preset
  Multiplexer #(.select(1), .width(12), .disabled("Z"), .enable("false")) multiplexer_6 (
    .in0(I_imm), .in1({I_imm[11:5], ID_IR[11:7]}), .out(multiplexer_6_out), .sel(\单周期硬布线控制器_1_s_type ));
  assign bit_extender_1_out = {{12{1'b0}}, {I_imm, ID_IR[19:12]}};  // Bit_Extender bit_extender_1
  assign CLK = nand_1_out ? clock_1_out : 1'bz;  // Controlled_Buffer controlled_buffer_1
  assign bit_extender_2_out = {{20{I_imm[11]}}, {I_imm[11], ID_IR[7], I_imm[10:5], ID_IR[11:8]}};  // Bit_Extender bit_extender_2
  assign bit_extender_3_out = {{12{I_imm[11]}}, {I_imm[11], ID_IR[19:12], I_imm[0], I_imm[10:1]}};  // Bit_Extender bit_extender_3
  Pull_Resistor #(.pull(1)) pull_resistor_1 (.node(CLK));
  Regifile regifile_1 (
    .Din(RDin), .Clk(CLK), .R1(regifile_1_r1), .R2(regifile_1_r2), .WE(MEN_RegWrite), .W_num(WB_RD),
    .R1_num(multiplexer_4_out), .R2_num(multiplexer_5_out));
  assign bit_extender_4_out = {{20{multiplexer_6_out[11]}}, multiplexer_6_out};  // Bit_Extender bit_extender_4
  ID id_1 (
    .RST(RST), .beq(\单周期硬布线控制器_1_beq ), .bne(\单周期硬布线控制器_1_bne ), .MemToReg(\单周期硬布线控制器_1_memtoreg ),
    .MemWrite(\单周期硬布线控制器_1_memwrite ), .ALU_OP(\单周期硬布线控制器_1_alu_op ), .ALU_SRCB(\单周期硬布线控制器_1_alu_src ),
    .RegWrite(\单周期硬布线控制器_1_regwrite ), .JAL(\单周期硬布线控制器_1_jal ), .JALR(\单周期硬布线控制器_1_jalr ),
    .URET(\单周期硬布线控制器_1_uret ), .ID_PC(ID_PC), .r1(regifile_1_r1), .r2(regifile_1_r2),
    .Bm(bit_extender_2_out), .Jm(bit_extender_3_out), .PC_4(ID_PC_4), .CLK(CLK), .beq_2(id_1_beq_2),
    .bne_2(id_1_bne_2), .MemToReg_2(id_1_memtoreg_2), .MemWrite_2(id_1_memwrite_2), .ALU_OP_2(id_1_alu_op_2),
    .ALU_SRCB_2(id_1_alu_srcb_2), .RegWrite_2(id_1_regwrite_2), .JAL_2(id_1_jal_2), .JALR_2(id_1_jalr_2),
    .URET_2(id_1_uret_2), .ID_PC_2(EX_PC), .r1_2(EX_R1), .r2_2(EX_R2), .Bm_2(id_1_bm_2), .Jm_2(id_1_jm_2),
    .PC_4_2(id_1_pc_4_2), .ID_IR({I_imm, ID_IR}), .ID_IR_2(EX_IR), .ecall(ecall), .ecall_2(id_1_ecall_2),
    .WRD(ID_IR[11:7]), .WRD_2(id_1_wrd_2), .Im(bit_extender_4_out), .Im_2(id_1_im_2), .halt(halt),
    .auipc(\单周期硬布线控制器_1_auipc ), .bltu(\单周期硬布线控制器_1_bltu ), .sb(\单周期硬布线控制器_1_sb ), .bltu_2(id_1_bltu_2),
    .auipc_2(id_1_auipc_2), .sb_2(id_1_sb_2), .u(bit_extender_1_out), .u_2(id_1_u_2), .flush(1'b0));  // open: S_type, S_type_2, RsFoward, RtFoward, RsFoward_2, Rtfoward_2
  Shifter #(.width(32), .shift("ll")) shifter_1 (.in(id_1_bm_2), .\dist (5'b00001), .out(shifter_1_out));
  Shifter #(.width(32), .shift("ll")) shifter_2 (.in(id_1_jm_2), .\dist (5'b00001), .out(shifter_2_out));
  Adder #(.width(32)) adder_2 (.a(shifter_1_out), .b(EX_PC), .out(Branch_Adress));  // open: cin, cout
  Adder #(.width(32)) adder_3 (.a(shifter_2_out), .b(EX_PC), .out(JAL_Adress));  // open: cin, cout
  Multiplexer #(.select(1), .width(32), .disabled("Z"), .enable("false")) multiplexer_7 (
    .in0(EX_R2), .in1(id_1_im_2), .out(multiplexer_7_out), .sel(id_1_alu_srcb_2));
  ALU alu_1 (
    .X(EX_R1), .Y(multiplexer_7_out), .AluOP(id_1_alu_op_2), .Equal(alu_1_equal), .Result(alu_1_result),
    .out_6(alu_1_out_6));  // open: Result_2, out_4
  assign JALR_Adress = alu_1_result & 32'hfffffffe;  // AND_Gate and_2, 32 bits wide
  or or_1 (or_1_out, and_4_out, and_3_out, and_5_out);
  and and_3 (and_3_out, not_2_out, id_1_bne_2);
  and and_4 (and_4_out, id_1_bltu_2, alu_1_out_6);
  and and_5 (and_5_out, id_1_beq_2, alu_1_equal);
  not not_2 (not_2_out, alu_1_equal);
  EX ex_1 (
    .RST(RST), .JAL(id_1_jal_2), .JALR(id_1_jalr_2), .URET(id_1_uret_2), .MemToReg(id_1_memtoreg_2),
    .MenWrite(id_1_memwrite_2), .ecall(id_1_ecall_2), .RegWirte(id_1_regwrite_2), .Write(id_1_wrd_2),
    .ALU_Result(alu_1_result), .EX_PC(EX_PC), .EX_IR(EX_IR), .PC_4(id_1_pc_4_2), .R1(EX_R1), .R2(EX_R2),
    .halt(halt), .CLK(CLK), .JAL_2(ex_1_jal_2), .JALR_2(ex_1_jalr_2), .URET_2(ex_1_uret_2),
    .MemToReg_2(ex_1_memtoreg_2), .MemWrite(ex_1_memwrite), .ecall_2(ex_1_ecall_2),
    .RegWirte_2(ex_1_regwirte_2), .Write_2(ex_1_write_2), .ALU_Result_2(ALU_result), .MEN_PC(M_PC),
    .MEN_IR(MEM_IR), .PC_4_2(ex_1_pc_4_2), .R1_2(ex_1_r1_2), .R2_2(MDin), .sb(id_1_sb_2),
    .auipc(id_1_auipc_2), .sb_2(ex_1_sb_2), .auipc_2(ex_1_auipc_2), .U(id_1_u_2), .U_2(ex_1_u_2), .flush(1'b0));
  // MIPS_RAM mips_ram_1: pin names not known; wires that end beside it: ALU_result[11:2], MDin, ex_1_memwrite, CLK, RST, mips_ram_1_p6
  Mem mem_1 (
    .RST(RST), .JAL(ex_1_jal_2), .JALR(ex_1_jalr_2), .URET(ex_1_uret_2), .MemToReg(ex_1_memtoreg_2),
    .MenWrite(ex_1_memwrite), .ecall(ex_1_ecall_2), .RegWirte(ex_1_regwirte_2), .Write(ex_1_write_2),
    .ALU_Result(ALU_result), .Mem_PC(M_PC), .Mem_IR(MEM_IR), .PC_4(ex_1_pc_4_2), .R1(ex_1_r1_2), .R2(MDin),
    .CLK(CLK), .JAL_2(mem_1_jal_2), .JALR_2(mem_1_jalr_2), .MemToReg_2(MEN_MemtoReg), .ecall_2(WB_ecall),
    .RegWirte_2(MEN_RegWrite), .Write_2(WB_RD), .ALU_Result_2(mem_1_alu_result_2), .Mem_PC_2(WB_PC),
    .Mem_IR_2(WB_IR), .PC_4_2(WB_PC_4), .R1_2(WB_R1), .R2_2(WB_R2), .MData(mips_ram_1_p6),
    .Mdata_2(mem_1_mdata_2), .sb(ex_1_sb_2), .auipc(ex_1_auipc_2), .sb_2(mem_1_sb_2), .u(ex_1_u_2),
    .u_2(mem_1_u_2), .flush(1'b0));  // open: URET_2, MemWrite, halt, auipc_2
  Multiplexer #(.select(1), .width(32), .disabled("Z"), .enable("false")) multiplexer_8 (
    .in0({32{1'b0}}), .in1(mem_1_u_2), .out(multiplexer_8_out));  // open: sel
  Multiplexer #(.select(1), .width(32), .disabled("Z"), .enable("false")) multiplexer_9 (
    .in0(mem_1_alu_result_2), .in1(mem_1_mdata_2), .out(multiplexer_9_out), .sel(MEN_MemtoReg));
  Adder #(.width(32)) adder_4 (.a(WB_PC), .b(32'h4), .out(adder_4_out));  // open: cin, cout
  or or_2 (or_2_out, mem_1_jalr_2, mem_1_jal_2);
  Multiplexer #(.select(1), .width(32), .disabled("Z"), .enable("false")) multiplexer_10 (
    .in0(multiplexer_9_out), .in1(adder_4_out), .out(multiplexer_10_out), .sel(or_2_out));
  Shifter #(.width(32), .shift("ll")) shifter_3 (.in(multiplexer_8_out), .\dist (5'b01100), .out(shifter_3_out));
  Multiplexer #(.select(1), .width(32), .disabled("Z"), .enable("false")) multiplexer_11 (
    .in0(multiplexer_10_out), .in1(U_adress), .out(RDin), .sel(mem_1_sb_2));
  Adder #(.width(32)) adder_5 (.a(shifter_3_out), .b(MEN_PC), .out(U_adress));  // open: cin, cout
  not not_3 (not_3_out, halt);
  and and_6 (and_6_out, Go, halt);
  Comparator #(.width(32), .mode("twosComplement")) comparator_2 (
    .a(WB_R1), .b(32'h22), .eq(comparator_2_eq));  // open: gt, lt
  Register #(.width(32), .trigger("rising"), .Select("low")) register_1 (
    .D(WB_R2), .en(ecallEq), .Q(LedData), .clk(CLK), .clr(RST));
  Counter #(.width(16), .max('hffff), .ongoal("wrap"), .trigger("rising"), .behavior("new")) counter_2 (
    .count(not_3_out), .Q(\总周期数 ), .clk(CLK), .clr(RST));  // open: load, D, carry, preset, down
  Counter #(.width(1), .max('h1), .ongoal("stay"), .trigger("rising"), .behavior("new")) counter_3 (
    .D(and_6_out), .Q(ecallFB), .clk(and_6_out), .clr(RST));  // open: load, count, carry, preset, down
  and and_7 (ecallEq, WB_ecall, comparator_2_eq);
  and and_8 (halt, WB_ecall, not_4_out);
  not not_4 (not_4_out, comparator_2_eq);

  // Other names for the same wires on the sheet: WDin[4:0] = ID_IR[11:7]; ID_IR[31:20] = I_imm; MEM_PC[31:0] = M_PC

  // Notes on the sheet:
  //   中断源
  //   时空图监测，可删除
  //   中断等待指示
  //   数码管输出
  //   指令存储器
  //   contents of rom_1 (hex, n*v repeats v):
  //   100493 100006f 100493 200913 300993 100006f 100493 200913 300993 100006f 100493 200913 300993
  //   100006f 100493 200913 300993 29c000ef 100413 100493 1f49493 900533 2200893 73 24d493 48463 fedff06f
  //   900533 2200893 73 100493 249493 900533 2200893 73 48463 fedff06f 100493 1f49493 900533 2200893 73
  //   4034d493 900533 2200893 73 4044d493 900533 2200893 73 4044d493 900533 2200893 73 4044d493 900533
  //   2200893 73 4044d493 900533 2200893 73 4044d493 900533 2200893 73 4044d493 900533 2200893 73 4044d493
  //   900533 2200893 73 100413 1f41993 41f9d993 433 c00913 300b13 140413 f47413 800293 100313 499993
  //   89e9b3 1300533 2200893 73 406282b3 fe0294e3 140413 f00f93 1f47433 1c41413 800293 100313 49d993
  //   89e9b3 1300533 2200893 73 406282b3 fe0294e3 1c45413 406b0b33 b0463 f95ff06f 2b3 fff2c293 829293
  //   ff2e293 500533 2200893 73 fff00413 493 84a023 140413 448493 84a023 140413 448493 84a023 140413
  //   448493 84a023 140413 448493 84a023 140413 448493 84a023 140413 448493 84a023 140413 448493 84a023
  //   140413 448493 84a023 140413 448493 84a023 140413 448493 84a023 140413 448493 84a023 140413 448493
  //   84a023 140413 448493 84a023 140413 448493 84a023 140413 448493 84a023 140413 448493 140413 433
  //   3c00493 42983 4aa03 149a2b3 28663 134a023 1442023 ffc48493 fe9412e3 800533 2200893 73 440413 3c00493
  //   fc9416e3 a00893 73 413 140413 800533 2200893 73 240413 800533 2200893 73 340413 800533 2200893 73
  //   440413 800533 2200893 73 540413 800533 2200893 73 640413 800533 2200893 73 740413 800533 2200893 73
  //   840413 800533 2200893 2200893 73 8067
  //   控制位
  //   流水调试日志用
  //   暂停节拍，不能为0
  //   Beq
  //   Bne
  //   MemToReg
  //   MemWrite
  //   AluOP
  //   AluSrcB
  //   RegWrite
  //   可计数暂停的时钟源
  //   为方便自动评测，需要输出流水线各段保存的PC值，注意是PC不是PC+4，另外ID段寄存器写入信息，Mem段内存写入信息也要输出
  //   数据存储器
  //   ecall比较$a7=?34
  //   ecallLED显示$a0
  //   ecall暂停
  //   ecall等待go按键
endmodule

module \中断按键参考电路  (
  input  \同步清零信号 ,
  output \与中断屏蔽位与 
);

  wire \_1号中断_out , and_1_out, clock_1_out, d_ff_1_q, or_1_out, or_2_out;

  Clock #(.highDuration(1), .lowDuration(1)) clock_1 (.out(clock_1_out));
  Button \_1号中断  (.out(\_1号中断_out ));
  or or_1 (or_1_out, \与中断屏蔽位与 , d_ff_1_q);
  LED #(.active("true")) \_1号中断等待指示灯  (.in(or_1_out));
  D_Flip_Flop #(.trigger("rising"), .Pre_Clr_Positions("LEGACY"), .NegatePresetClear("false"), .enable("true"), .NewFFLayout("false")) d_ff_1 (
    .clk(\_1号中断_out ), .D(1'b1), .Q(d_ff_1_q), .reset(\与中断屏蔽位与 ));  // open: Qn, preset, en
  or or_2 (or_2_out, d_ff_1_q, \与中断屏蔽位与 );
  and and_1 (and_1_out, or_2_out, ~\同步清零信号 );  // AND_Gate
  D_Flip_Flop #(.trigger("rising"), .Pre_Clr_Positions("LEGACY"), .NegatePresetClear("false"), .enable("true"), .NewFFLayout("false")) IR1 (
    .clk(clock_1_out), .D(and_1_out), .Q(\与中断屏蔽位与 ));  // open: Qn, preset, en, reset

  // Notes on the sheet:
  //   中断信号采样参考电路
  //   Reset 
endmodule

module \单周期_单级中断  (
  input  IR1,
  input  IR2,
  input  IR3,
  output RegWrite,
  output MemWrite,
  output [31:0] PC,
  output [31:0] IR,
  output [31:0] RDin,
  output [31:0] MDin,
  output [31:0] LedData
);

  wire alu_1_equal, alu_1_out_6, and_1_out, and_2_out, and_3_out, and_4_out, and_6_out, and_7_out, and_8_out,
       and_13_out, and_14_out, auipc, bltu, Branch, ClearA, ClearB, ClearC, CLK, clock_1_out,
       comparator_1_eq, comparator_2_eq, comparator_3_eq, comparator_4_eq, comparator_5_eq, comparator_5_lt,
       comparator_6_eq, d_ff_1_q, decoder_1_out1, decoder_1_out2, decoder_1_out3, ecall, Go, halt, IE, INT,
       IR1_t, IR2_t, IR3_t, IRA, IRB, IRC, JAL, JALR, MemToReg, nand_1_out, not_1_out, not_2_out, not_3_out,
       not_4_out, or_2_out, or_8_out, or_9_out, or_10_out, or_11_out, or_12_out, or_13_out, or_14_out,
       or_16_out, register_1_q, register_2_q, register_3_q, register_4_q, register_5_q, register_6_q, RST,
       sb, sltiu, URET, W1, W2, W3, \中断信号 , \单周期硬布线控制器_1_alu_src , \单周期硬布线控制器_1_beq , \单周期硬布线控制器_1_bne ,
       \单周期硬布线控制器_1_s_type ;
  wire [1:0] register_7_q, \中断号 ;
  wire [3:0] sb_1_out_3, \单周期硬布线控制器_1_alu_op ;
  wire [4:0] multiplexer_6_out, multiplexer_7_out;
  wire [11:0] multiplexer_8_out;
  wire [12:0] CNT_num;
  wire [15:0] \总周期数 ;
  wire [31:0] adder_1_out, adder_5_out, ALU_result, bit_extender_1_out, bit_extender_2_out,
       bit_extender_3_out, bit_extender_4_out, Branch_Adress, INTPC, JAL_Adress, JALR_Adress, LocalPC,
       mips_ram_1_p7, multiplexer_1_out, multiplexer_3_out, multiplexer_4_out, multiplexer_5_out,
       multiplexer_9_out, multiplexer_10_out, multiplexer_13_out, multiplexer_14_out, r1, r2, RETPC,
       sb_1_darta, shifter_1_out, shifter_2_out, shifter_3_out, U_adress;

  Button \u_继续运行  (.out(Go));
  Button _1 ();  // open: out
  Button _2 ();  // open: out
  Button _3 ();  // open: out
  LED #(.active("true")) led_1 (.in(W1));
  LED #(.active("true")) led_2 (.in(W2));
  LED #(.active("true")) led_3 (.in(W3));
  Multiplexer #(.select(1), .width(32), .disabled("Z"), .enable("false")) multiplexer_1 (
    .in0(adder_1_out), .in1(Branch_Adress), .out(multiplexer_1_out), .sel(Branch));
  Hex_Digit_Display hex_digit_display_1 (.value(LedData[31:28]));  // open: dp
  Multiplexer #(.select(1), .width(32), .disabled("Z"), .enable("false")) multiplexer_2 (
    .in0(multiplexer_3_out), .in1(JAL_Adress), .out(LocalPC), .sel(JAL));
  Multiplexer #(.select(1), .width(32), .disabled("Z"), .enable("false")) multiplexer_3 (
    .in0(multiplexer_1_out), .in1(JALR_Adress), .out(multiplexer_3_out), .sel(JALR));
  Hex_Digit_Display hex_digit_display_2 (.value(LedData[23:20]));  // open: dp
  Hex_Digit_Display hex_digit_display_3 (.value(LedData[27:24]));  // open: dp
  Hex_Digit_Display hex_digit_display_4 (.value(LedData[19:16]));  // open: dp
  Hex_Digit_Display hex_digit_display_5 (.value(LedData[15:12]));  // open: dp
  Multiplexer #(.select(1), .width(32), .disabled("Z"), .enable("false")) multiplexer_4 (
    .in0(LocalPC), .in1(RETPC), .out(multiplexer_4_out), .sel(URET));
  Hex_Digit_Display hex_digit_display_6 (.value(LedData[11:8]));  // open: dp
  Hex_Digit_Display hex_digit_display_7 (.value(LedData[7:4]));  // open: dp
  // Probe on \总周期数 
  Multiplexer #(.select(1), .width(32), .disabled("Z"), .enable("false")) multiplexer_5 (
    .in0(multiplexer_4_out), .in1(INTPC), .out(multiplexer_5_out), .sel(INT));
  Hex_Digit_Display hex_digit_display_8 (.value(LedData[3:0]));  // open: dp
  Button button_1 (.out(RST));
  not not_1 (not_1_out, halt);
  Register #(.width(32), .trigger("rising"), .Select("low")) u_PC (
    .D(multiplexer_5_out), .en(not_1_out), .Q(PC), .clk(CLK), .clr(RST));
  Adder #(.width(32)) adder_1 (.a(PC), .b(32'h4), .out(adder_1_out));  // open: cin, cout
  Comparator #(.width(16), .mode("twosComplement")) comparator_1 (
    .a(16'h23b), .b(\总周期数 ), .eq(comparator_1_eq));  // open: gt, lt
  Comparator #(.width(16), .mode("twosComplement")) comparator_2 (
    .a(\总周期数 ), .b(16'h1), .eq(comparator_2_eq));  // open: gt, lt
  Comparator #(.width(16), .mode("twosComplement")) comparator_3 (
    .a(\总周期数 ), .b(16'h4), .eq(comparator_3_eq));  // open: gt, lt
  Comparator #(.width(16), .mode("twosComplement")) comparator_4 (
    .a(\总周期数 ), .b(16'h7), .eq(comparator_4_eq));  // open: gt, lt
  or or_1 (IR1_t, IR1, IRA);
  or or_2 (or_2_out, comparator_1_eq, comparator_2_eq);
  Pull_Resistor #(.pull(0)) pull_resistor_1 (.node(IRA));
  assign IRA = or_2_out ? ~CLK : 1'bz;  // Controlled_Inverter controlled_inverter_1
  Pull_Resistor #(.pull(0)) pull_resistor_2 (.node(IRB));
  assign IRB = comparator_3_eq ? ~CLK : 1'bz;  // Controlled_Inverter controlled_inverter_2
  Pull_Resistor #(.pull(0)) pull_resistor_3 (.node(IRC));
  assign IRC = comparator_4_eq ? ~CLK : 1'bz;  // Controlled_Inverter controlled_inverter_3
  or or_3 (IR2_t, IR2, IRB);
  // RiscV_Probe riscv_probe_1: pin names not known; wires that end beside it: Branch, IR, ecall
  ROM #(.addrWidth(10), .dataWidth(32), .Select("high")) rom_1 (.addr(PC[11:2]), .data(IR));
  or or_4 (IR3_t, IR3, IRC);
  Multiplexer #(.select(1), .width(5), .disabled("Z"), .enable("false")) multiplexer_6 (
    .in0(IR[19:15]), .in1(5'b10001), .out(multiplexer_6_out), .sel(ecall));
  Multiplexer #(.select(1), .width(5), .disabled("Z"), .enable("false")) multiplexer_7 (
    .in0(IR[24:20]), .in1(5'b01010), .out(multiplexer_7_out), .sel(ecall));
  or or_5 (W1, register_4_q, register_1_q);
  or or_6 (W2, register_5_q, register_2_q);
  or or_7 (W3, register_6_q, register_3_q);
  \单周期硬布线控制器  \u_单周期硬布线控制器_1  (
    .Funct({IR[30], IR[25], IR[14:12]}), .OP(IR[6:2]), .ALU_OP(\单周期硬布线控制器_1_alu_op ), .MemToReg(MemToReg),
    .MemWrite(MemWrite), .ALU_SRC(\单周期硬布线控制器_1_alu_src ), .RegWrite(RegWrite), .ecall(ecall),
    .S_type(\单周期硬布线控制器_1_s_type ), .Jalr(JALR), .Beq(\单周期硬布线控制器_1_beq ), .JAL(JAL), .Bne(\单周期硬布线控制器_1_bne ),
    .in_3(IR[21]), .uret(URET), .sb(sb), .auipc(auipc), .bltu(bltu), .sltiu(sltiu));  // open: rs1, rs2, CSRRSI, CSRRCI
  Multiplexer #(.select(1), .width(12), .disabled("Z"), .enable("false")) multiplexer_8 (
    .in0(IR[31:20]), .in1({IR[31:25], IR[11:7]}), .out(multiplexer_8_out), .sel(\单周期硬布线控制器_1_s_type ));
  Register #(.width(1), .trigger("rising"), .Select("low")) register_1 (
    .D(1'b1), .Q(register_1_q), .clk(IRA), .clr(or_8_out));  // open: en
  or or_8 (or_8_out, register_4_q, RST);
  Register #(.width(1), .trigger("rising"), .Select("low")) register_2 (
    .D(1'b1), .Q(register_2_q), .clk(IRB), .clr(or_9_out));  // open: en
  or or_9 (or_9_out, register_5_q, RST);
  Register #(.width(1), .trigger("rising"), .Select("low")) register_3 (
    .D(1'b1), .Q(register_3_q), .clk(IRC), .clr(or_10_out));  // open: en
  or or_10 (or_10_out, register_6_q, RST);
  assign bit_extender_1_out = {{20{IR[31]}}, {IR[31], IR[7], IR[30:25], IR[11:8]}};  // Bit_Extender bit_extender_1
  assign bit_extender_2_out = {{12{IR[31]}}, {IR[31], IR[19:12], IR[20], IR[30:21]}};  // Bit_Extender bit_extender_2
  assign bit_extender_3_out = {{12{1'b0}}, IR[31:12]};  // Bit_Extender bit_extender_3
  or or_11 (or_11_out, register_1_q, register_4_q);
  or or_12 (or_12_out, register_2_q, register_5_q);
  or or_13 (or_13_out, register_3_q, register_6_q);
  Regifile regifile_1 (
    .Din(RDin), .Clk(CLK), .R1(r1), .R2(r2), .WE(RegWrite), .W_num(IR[11:7]), .R1_num(multiplexer_6_out),
    .R2_num(multiplexer_7_out));
  assign bit_extender_4_out = {{20{multiplexer_8_out[11]}}, multiplexer_8_out};  // Bit_Extender bit_extender_4
  Shifter #(.width(32), .shift("ll")) shifter_1 (.in(bit_extender_1_out), .\dist (5'b00001), .out(shifter_1_out));
  Shifter #(.width(32), .shift("ll")) shifter_2 (.in(bit_extender_2_out), .\dist (5'b00001), .out(shifter_2_out));
  Multiplexer #(.select(1), .width(32), .disabled("Z"), .enable("false")) multiplexer_9 (
    .in0({32{1'b0}}), .in1(bit_extender_3_out), .out(multiplexer_9_out), .sel(auipc));
  and and_1 (and_1_out, or_11_out, ~ClearA);  // AND_Gate
  and and_2 (and_2_out, or_12_out, ~ClearB);  // AND_Gate
  and and_3 (and_3_out, or_13_out, ~ClearC);  // AND_Gate
  Adder #(.width(32)) adder_2 (.a(shifter_1_out), .b(PC), .out(Branch_Adress));  // open: cin, cout
  Adder #(.width(32)) adder_3 (.a(shifter_2_out), .b(PC), .out(JAL_Adress));  // open: cin, cout
  Shifter #(.width(32), .shift("ll")) shifter_3 (.in(multiplexer_9_out), .\dist (5'b01100), .out(shifter_3_out));
  Register #(.width(1), .trigger("rising"), .Select("low")) register_4 (
    .D(and_1_out), .Q(register_4_q), .clk(CLK), .clr(RST));  // open: en
  Register #(.width(1), .trigger("rising"), .Select("low")) register_5 (
    .D(and_2_out), .Q(register_5_q), .clk(CLK), .clr(RST));  // open: en
  Register #(.width(1), .trigger("rising"), .Select("low")) register_6 (
    .D(and_3_out), .Q(register_6_q), .clk(CLK), .clr(RST));  // open: en
  Multiplexer #(.select(1), .width(32), .disabled("Z"), .enable("false")) multiplexer_10 (
    .in0(r2), .in1(bit_extender_4_out), .out(multiplexer_10_out), .sel(\单周期硬布线控制器_1_alu_src ));
  Adder #(.width(32)) adder_4 (.a(shifter_3_out), .b(PC), .out(U_adress));  // open: cin, cout
  Priority_Encoder #(.select(2), .disabled("Z")) priority_encoder_1 (
    .in1(register_4_q), .in2(register_5_q), .in3(register_6_q), .out(\中断号 ), .gs(\中断信号 ));  // open: in0, en_out, en_in
  D_Flip_Flop #(.trigger("high"), .Pre_Clr_Positions("LEGACY"), .NegatePresetClear("false"), .enable("true"), .NewFFLayout("false")) d_ff_1 (.Q(d_ff_1_q));  // open: clk, D, Qn, preset, en, reset
  // Probe on 13'hc
  Comparator #(.width(13), .mode("twosComplement")) comparator_5 (
    .a(CNT_num), .b(13'hc), .eq(comparator_5_eq), .lt(comparator_5_lt));  // open: gt
  Clock #(.highDuration(1), .lowDuration(1)) clock_1 (.out(clock_1_out));
  Register #(.width(2), .trigger("rising"), .Select("low")) register_7 (
    .D(\中断号 ), .en(INT), .Q(register_7_q), .clk(CLK), .clr(RST));
  Counter #(.width(13), .max('h1fff), .ongoal("stay"), .trigger("rising"), .behavior("old")) counter_1 (
    .count(comparator_5_lt), .Q(CNT_num), .clk(clock_1_out));  // open: load, D, carry, clr, preset
  not not_2 (not_2_out, alu_1_equal);
  ALU alu_1 (
    .X(r1), .Y(multiplexer_10_out), .AluOP(\单周期硬布线控制器_1_alu_op ), .Equal(alu_1_equal), .Result(ALU_result),
    .out_6(alu_1_out_6));  // open: Result_2, out_4
  sb sb_1 (.in_1(sb), .R2(r2), .out_3(sb_1_out_3), .darta(sb_1_darta));
  Multiplexer #(.select(1), .width(32), .disabled("Z"), .enable("false")) multiplexer_11 (
    .in0(r2), .in1(sb_1_darta), .out(MDin), .sel(sb));
  and and_4 (and_4_out, \中断信号 , ~URET);  // AND_Gate
  and and_5 (INT, \中断信号 , IE);
  Register #(.width(32), .trigger("falling"), .Select("low")) mEPC (
    .D(LocalPC), .en(INT), .Q(RETPC), .clk(CLK), .clr(RST));
  Decoder #(.select(2), .tristate("false"), .disabled("Z"), .enable("false")) decoder_1 (
    .out1(decoder_1_out1), .out2(decoder_1_out2), .out3(decoder_1_out3), .sel(register_7_q));  // open: out0
  nand nand_1 (nand_1_out, d_ff_1_q, comparator_5_eq);
  and and_6 (and_6_out, \单周期硬布线控制器_1_beq , alu_1_equal);
  and and_7 (and_7_out, \单周期硬布线控制器_1_bne , not_2_out);
  and and_8 (and_8_out, bltu, alu_1_out_6);
  D_Flip_Flop #(.trigger("rising"), .Pre_Clr_Positions("ABOVE_BELOW"), .NegatePresetClear("false"), .enable("false"), .NewFFLayout("true")) u_IE (
    .clk(CLK), .D(and_4_out), .Qn(IE), .reset(RST));  // open: Q, preset
  Multiplexer #(.select(2), .width(32), .disabled("Z"), .enable("false")) multiplexer_12 (
    .in1(32'h30ac), .in2(32'h3150), .in3(32'h31f4), .out(INTPC), .sel(\中断号 ));  // open: in0
  and and_9 (ClearA, URET, decoder_1_out1);
  and and_10 (ClearB, URET, decoder_1_out2);
  and and_11 (ClearC, decoder_1_out3, URET);
  assign CLK = nand_1_out ? clock_1_out : 1'bz;  // Controlled_Buffer controlled_buffer_1
  Pull_Resistor #(.pull(1)) pull_resistor_4 (.node(CLK));
  or or_14 (or_14_out, and_6_out, and_7_out);
  // MIPS_RAM mips_ram_1: pin names not known; wires that end beside it: ALU_result[11:2], MDin, MemWrite, sb_1_out_3, CLK, RST, mips_ram_1_p7
  or or_15 (Branch, or_14_out, and_8_out);
  Adder #(.width(32)) adder_5 (.a(PC), .b(32'h4), .out(adder_5_out));  // open: cin, cout
  Multiplexer #(.select(1), .width(32), .disabled("Z"), .enable("false")) multiplexer_13 (
    .in0(ALU_result), .in1(mips_ram_1_p7), .out(multiplexer_13_out), .sel(MemToReg));
  assign JALR_Adress = ALU_result & 32'hfffffffe;  // AND_Gate and_12, 32 bits wide
  or or_16 (or_16_out, JAL, JALR);
  Multiplexer #(.select(1), .width(32), .disabled("Z"), .enable("false")) multiplexer_14 (
    .in0(multiplexer_13_out), .in1(adder_5_out), .out(multiplexer_14_out), .sel(or_16_out));
  Comparator #(.width(32), .mode("twosComplement")) comparator_6 (
    .a(32'h22), .b(r1), .eq(comparator_6_eq));  // open: gt, lt
  Multiplexer #(.select(1), .width(32), .disabled("Z"), .enable("false")) multiplexer_15 (
    .in0(multiplexer_14_out), .in1(U_adress), .out(RDin), .sel(auipc));
  and and_13 (and_13_out, ecall, comparator_6_eq);
  and and_14 (and_14_out, ecall, not_3_out);
  not not_3 (not_3_out, comparator_6_eq);
  Multiplexer #(.select(1), .width(1), .disabled("Z"), .enable("false")) multiplexer_16 (
    .in0(and_14_out), .in1(1'b0), .out(halt), .sel(Go));
  Register #(.width(32), .trigger("rising"), .Select("low")) register_8 (
    .D(MDin), .en(and_13_out), .Q(LedData), .clk(CLK), .clr(RST));
  not not_4 (not_4_out, halt);
  Counter #(.width(16), .max('hffff), .ongoal("wrap"), .trigger("rising"), .behavior("new")) counter_2 (
    .count(not_4_out), .Q(\总周期数 ), .clk(CLK), .clr(RST));  // open: load, D, carry, preset, down

  // Other names for the same wires on the sheet: I_imm[11:0] = IR[31:20]

  // Notes on the sheet:
  //   中断源
  //   中断等待指示
  //   总复位信号应将除ROM以外所有存储组件全部清零
  //   数码管输出
  //   数码管输出应该用寄存器锁存，否则显示数据只能一闪而过
  //   数码管输出应该用寄存器锁存，否则显示数据只能一闪而过
  //   单级中断测试信号模拟器
  //   中断信号采样参考电路
  //   指令探针
  //   指令存储器
  //   contents of rom_1 (hex, n*v repeats v):
  //   7d000113 100413 1f41993 41f9d993 433 c00913 800b13 140413 f47413 800293 100313 499993 89e9b3 1300533
  //   2200893 73 406282b3 fe0294e3 140413 f00f93 1f47433 1c41413 800293 100313 49d993 89e9b3 1300533
  //   2200893 73 406282b3 fe0294e3 1c45413 406b0b33 b0463 f95ff06f 2b3 fff2c293 1029293 fff2e293 500533
  //   2200893 73 f5dff06f 1112023 410113 a12023 410113 812023 410113 1312023 410113 1412023 410113 1512023
  //   410113 1612023 410113 100b13 300a13 100a93 1600433 441413 14469b3 1300533 2200893 73 fe0416e3
  //   415a0a33 fe0a10e3 ffc10113 12b03 ffc10113 12a83 ffc10113 12a03 ffc10113 12983 ffc10113 12403
  //   ffc10113 12503 ffc10113 12883 200073 1112023 410113 a12023 410113 812023 410113 1312023 410113
  //   1412023 410113 1512023 410113 1612023 410113 200b13 300a13 100a93 1600433 441413 14469b3 1300533
  //   2200893 73 fe0416e3 415a0a33 fe0a10e3 ffc10113 12b03 ffc10113 12a83 ffc10113 12a03 ffc10113 12983
  //   ffc10113 12403 ffc10113 12503 ffc10113 12883 200073 1112023 410113 a12023 410113 812023 410113
  //   1312023 410113 1412023 410113 1512023 410113 1612023 410113 300b13 300a13 100a93 1600433 441413
  //   14469b3 1300533 2200893 73 fe0416e3 415a0a33 fe0a10e3 ffc10113 12b03 ffc10113 12a83 ffc10113 12a03
  //   ffc10113 12983 ffc10113 12403 ffc10113 12503 ffc10113 12883 200073
  //   指令字
  //   JAL
  //   JALR
  //   URET
  //   Beq
  //   Bne
  //   MemToReg
  //   MemWrite
  //   AluOP
  //   AluSrcB
  //   RegWrite
  //   为方便自动评测，需要输出PC，IR，寄存器堆写如数据RDin
  //   RAM写使能MemWrite、RAM写入数据MDin等信号
  //   控制位
  //   暂停节拍，不能为0
  //   戳工具置1进入计数暂停模式，ctrl+k时钟自动运行到对应节拍暂停
  //   ctrl+k关闭时钟连续运行，将控制位置零，进入单步调试模式调试
  //   数据存储器
  //   可计数暂停的时钟源
  //   用这个时钟源需要去掉电路中的其他时钟源
endmodule

module \单周期_多级中断  (
  input  IR1,
  input  IR2,
  input  IR3,
  output RegWrite,
  output MemWrite,
  output [31:0] PC,
  output [31:0] IR,
  output [31:0] RDin,
  output [31:0] MDin,
  output [31:0] LedData
);

  wire alu_1_equal, alu_1_out_6, and_1_out, and_2_out, and_3_out, and_8_out, and_9_out, and_10_out,
       and_11_out, and_12_out, and_13_out, and_14_out, and_15_out, and_16_out, and_17_out, and_18_out,
       and_19_out, and_20_out, and_21_out, auipc, bltu, Branch, ClearA, ClearB, ClearC, CLK, clock_1_out,
       comparator_1_eq, comparator_2_eq, comparator_3_eq, comparator_4_eq, comparator_5_eq, comparator_6_eq,
       comparator_6_lt, comparator_7_eq, comparator_8_gt, counter_3_q, CSRRCI, CSRRSI, d_ff_1_q,
       decoder_1_out1, decoder_1_out2, decoder_1_out3, decoder_2_out1, decoder_2_out2, decoder_2_out3,
       decoder_3_out1, decoder_3_out2, decoder_3_out3, ecall, EPC1_q, EPC2_q, EPC3_q, Go, halt, IE, INT,
       IR1_t, IR2_t, IR3_t, IRA, IRB, IRC, JAL, JALR, MemToReg, nand_1_out, not_1_out, not_2_out, not_3_out,
       not_4_out, not_5_out, or_1_out, or_2_out, or_6_out, or_8_out, or_9_out, or_13_out, or_14_out,
       or_15_out, or_16_out, or_17_out, or_18_out, or_20_out, or_21_out, register_2_q, register_3_q,
       register_4_q, register_5_q, register_6_q, register_7_q, RST, sb, sltiu, URET, W1, W2, W3, \中断信号 ,
       \优先中断 , \单周期硬布线控制器_1_alu_src , \单周期硬布线控制器_1_beq , \单周期硬布线控制器_1_bne , \单周期硬布线控制器_1_s_type ;
  wire [1:0] \中断号 , \当前中断号 ;
  wire [3:0] sb_1_out_3, \单周期硬布线控制器_1_alu_op ;
  wire [4:0] multiplexer_6_out, multiplexer_7_out;
  wire [11:0] multiplexer_8_out;
  wire [12:0] CNT_num;
  wire [15:0] \总周期数 ;
  wire [31:0] adder_1_out, adder_5_out, ALU_result, bit_extender_1_out, bit_extender_2_out,
       bit_extender_3_out, bit_extender_4_out, Branch_Adress, INTPC, JAL_Adress, JALR_Adress, LocalPC,
       mEPC1_q, mEPC2_q, mEPC3_q, mips_ram_1_p7, multiplexer_1_out, multiplexer_3_out, multiplexer_4_out,
       multiplexer_5_out, multiplexer_9_out, multiplexer_10_out, multiplexer_12_out, multiplexer_13_out, r1,
       r2, RETPC, sb_1_darta, shifter_1_out, shifter_2_out, shifter_3_out, U_adress;

  Button \u_继续运行  (.out(Go));
  Button _1 ();  // open: out
  Button _2 ();  // open: out
  Button _3 ();  // open: out
  LED #(.active("true")) led_1 (.in(W1));
  LED #(.active("true")) led_2 (.in(W2));
  LED #(.active("true")) led_3 (.in(W3));
  Multiplexer #(.select(1), .width(32), .disabled("Z"), .enable("false")) multiplexer_1 (
    .in0(adder_1_out), .in1(Branch_Adress), .out(multiplexer_1_out), .sel(Branch));
  Hex_Digit_Display hex_digit_display_1 (.value(LedData[31:28]));  // open: dp
  Comparator #(.width(16), .mode("twosComplement")) comparator_1 (
    .a(\总周期数 ), .b(16'h7), .eq(comparator_1_eq));  // open: gt, lt
  Comparator #(.width(16), .mode("twosComplement")) comparator_2 (
    .a(\总周期数 ), .b(16'h241), .eq(comparator_2_eq));  // open: gt, lt
  Multiplexer #(.select(1), .width(32), .disabled("Z"), .enable("false")) multiplexer_2 (
    .in0(multiplexer_3_out), .in1(JAL_Adress), .out(LocalPC), .sel(JAL));
  Multiplexer #(.select(1), .width(32), .disabled("Z"), .enable("false")) multiplexer_3 (
    .in0(multiplexer_1_out), .in1(JALR_Adress), .out(multiplexer_3_out), .sel(JALR));
  Hex_Digit_Display hex_digit_display_2 (.value(LedData[27:24]));  // open: dp
  Hex_Digit_Display hex_digit_display_3 (.value(LedData[23:20]));  // open: dp
  Comparator #(.width(16), .mode("twosComplement")) comparator_3 (
    .a(16'h258), .b(\总周期数 ), .eq(comparator_3_eq));  // open: gt, lt
  or or_1 (or_1_out, comparator_3_eq, comparator_4_eq);
  Comparator #(.width(16), .mode("twosComplement")) comparator_4 (
    .a(\总周期数 ), .b(16'h1), .eq(comparator_4_eq));  // open: gt, lt
  Comparator #(.width(16), .mode("twosComplement")) comparator_5 (
    .a(\总周期数 ), .b(16'h4), .eq(comparator_5_eq));  // open: gt, lt
  or or_2 (or_2_out, comparator_1_eq, comparator_2_eq);
  Hex_Digit_Display hex_digit_display_4 (.value(LedData[19:16]));  // open: dp
  Hex_Digit_Display hex_digit_display_5 (.value(LedData[15:12]));  // open: dp
  Pull_Resistor #(.pull(0)) pull_resistor_1 (.node(IRA));
  assign IRA = or_1_out ? ~CLK : 1'bz;  // Controlled_Inverter controlled_inverter_1
  Pull_Resistor #(.pull(0)) pull_resistor_2 (.node(IRB));
  assign IRB = comparator_5_eq ? ~CLK : 1'bz;  // Controlled_Inverter controlled_inverter_2
  Pull_Resistor #(.pull(0)) pull_resistor_3 (.node(IRC));
  assign IRC = or_2_out ? ~CLK : 1'bz;  // Controlled_Inverter controlled_inverter_3
  Multiplexer #(.select(1), .width(32), .disabled("Z"), .enable("false")) multiplexer_4 (
    .in0(LocalPC), .in1(RETPC), .out(multiplexer_4_out), .sel(URET));
  Hex_Digit_Display hex_digit_display_6 (.value(LedData[11:8]));  // open: dp
  Hex_Digit_Display hex_digit_display_7 (.value(LedData[7:4]));  // open: dp
  // Probe on \总周期数 
  Multiplexer #(.select(1), .width(32), .disabled("Z"), .enable("false")) multiplexer_5 (
    .in0(multiplexer_4_out), .in1(INTPC), .out(multiplexer_5_out), .sel(INT));
  Hex_Digit_Display hex_digit_display_8 (.value(LedData[3:0]));  // open: dp
  Button button_1 (.out(RST));
  not not_1 (not_1_out, halt);
  Register #(.width(32), .trigger("rising"), .Select("low")) u_PC (
    .D(multiplexer_5_out), .en(not_1_out), .Q(PC), .clk(CLK), .clr(RST));
  Adder #(.width(32)) adder_1 (.a(PC), .b(32'h4), .out(adder_1_out));  // open: cin, cout
  or or_3 (IR1_t, IR1, IRA);
  or or_4 (IR2_t, IR2, IRB);
  // RiscV_Probe riscv_probe_1: pin names not known; wires that end beside it: Branch, IR, ecall
  ROM #(.addrWidth(10), .dataWidth(32), .Select("high")) rom_1 (.addr(PC[11:2]), .data(IR));
  or or_5 (IR3_t, IR3, IRC);
  Multiplexer #(.select(1), .width(5), .disabled("Z"), .enable("false")) multiplexer_6 (
    .in0(IR[19:15]), .in1(5'b10001), .out(multiplexer_6_out), .sel(ecall));
  Multiplexer #(.select(1), .width(5), .disabled("Z"), .enable("false")) multiplexer_7 (
    .in0(IR[24:20]), .in1(5'b01010), .out(multiplexer_7_out), .sel(ecall));
  \单周期硬布线控制器  \u_单周期硬布线控制器_1  (
    .Funct({IR[30], IR[25], IR[14:12]}), .OP(IR[6:2]), .ALU_OP(\单周期硬布线控制器_1_alu_op ), .MemToReg(MemToReg),
    .MemWrite(MemWrite), .ALU_SRC(\单周期硬布线控制器_1_alu_src ), .RegWrite(RegWrite), .ecall(ecall),
    .S_type(\单周期硬布线控制器_1_s_type ), .Jalr(JALR), .Beq(\单周期硬布线控制器_1_beq ), .JAL(JAL), .Bne(\单周期硬布线控制器_1_bne ),
    .in_3(IR[21]), .uret(URET), .sb(sb), .auipc(auipc), .bltu(bltu), .sltiu(sltiu), .CSRRSI(CSRRSI),
    .CSRRCI(CSRRCI));  // open: rs1, rs2
  Multiplexer #(.select(1), .width(12), .disabled("Z"), .enable("false")) multiplexer_8 (
    .in0(IR[31:20]), .in1({IR[31:25], IR[11:7]}), .out(multiplexer_8_out), .sel(\单周期硬布线控制器_1_s_type ));
  assign bit_extender_1_out = {{20{IR[31]}}, {IR[31], IR[7], IR[30:25], IR[11:8]}};  // Bit_Extender bit_extender_1
  assign bit_extender_2_out = {{12{IR[31]}}, {IR[31], IR[19:12], IR[20], IR[30:21]}};  // Bit_Extender bit_extender_2
  assign bit_extender_3_out = {{12{1'b0}}, IR[31:12]};  // Bit_Extender bit_extender_3
  Regifile regifile_1 (
    .Din(RDin), .Clk(CLK), .R1(r1), .R2(r2), .WE(RegWrite), .W_num(IR[11:7]), .R1_num(multiplexer_6_out),
    .R2_num(multiplexer_7_out));
  assign bit_extender_4_out = {{20{multiplexer_8_out[11]}}, multiplexer_8_out};  // Bit_Extender bit_extender_4
  Shifter #(.width(32), .shift("ll")) shifter_1 (.in(bit_extender_1_out), .\dist (5'b00001), .out(shifter_1_out));
  Shifter #(.width(32), .shift("ll")) shifter_2 (.in(bit_extender_2_out), .\dist (5'b00001), .out(shifter_2_out));
  Multiplexer #(.select(1), .width(32), .disabled("Z"), .enable("false")) multiplexer_9 (
    .in0({32{1'b0}}), .in1(bit_extender_3_out), .out(multiplexer_9_out), .sel(auipc));
  Adder #(.width(32)) adder_2 (.a(shifter_1_out), .b(PC), .out(Branch_Adress));  // open: cin, cout
  Adder #(.width(32)) adder_3 (.a(shifter_2_out), .b(PC), .out(JAL_Adress));  // open: cin, cout
  Shifter #(.width(32), .shift("ll")) shifter_3 (.in(multiplexer_9_out), .\dist (5'b01100), .out(shifter_3_out));
  Multiplexer #(.select(1), .width(32), .disabled("Z"), .enable("false")) multiplexer_10 (
    .in0(r2), .in1(bit_extender_4_out), .out(multiplexer_10_out), .sel(\单周期硬布线控制器_1_alu_src ));
  Adder #(.width(32)) adder_4 (.a(shifter_3_out), .b(PC), .out(U_adress));  // open: cin, cout
  D_Flip_Flop #(.trigger("high"), .Pre_Clr_Positions("LEGACY"), .NegatePresetClear("false"), .enable("true"), .NewFFLayout("false")) d_ff_1 (.Q(d_ff_1_q));  // open: clk, D, Qn, preset, en, reset
  // Probe on 13'hc
  Comparator #(.width(13), .mode("twosComplement")) comparator_6 (
    .a(CNT_num), .b(13'hc), .eq(comparator_6_eq), .lt(comparator_6_lt));  // open: gt
  Clock #(.highDuration(1), .lowDuration(1)) clock_1 (.out(clock_1_out));
  Counter #(.width(13), .max('h1fff), .ongoal("stay"), .trigger("rising"), .behavior("old")) counter_1 (
    .count(comparator_6_lt), .Q(CNT_num), .clk(clock_1_out));  // open: load, D, carry, clr, preset
  not not_2 (not_2_out, alu_1_equal);
  ALU alu_1 (
    .X(r1), .Y(multiplexer_10_out), .AluOP(\单周期硬布线控制器_1_alu_op ), .Equal(alu_1_equal), .Result(ALU_result),
    .out_6(alu_1_out_6));  // open: Result_2, out_4
  sb sb_1 (.in_1(sb), .R2(r2), .out_3(sb_1_out_3), .darta(sb_1_darta));
  Multiplexer #(.select(1), .width(32), .disabled("Z"), .enable("false")) multiplexer_11 (
    .in0(r2), .in1(sb_1_darta), .out(MDin), .sel(sb));
  nand nand_1 (nand_1_out, d_ff_1_q, comparator_6_eq);
  and and_1 (and_1_out, \单周期硬布线控制器_1_beq , alu_1_equal);
  and and_2 (and_2_out, \单周期硬布线控制器_1_bne , not_2_out);
  and and_3 (and_3_out, bltu, alu_1_out_6);
  assign CLK = nand_1_out ? clock_1_out : 1'bz;  // Controlled_Buffer controlled_buffer_1
  Pull_Resistor #(.pull(1)) pull_resistor_4 (.node(CLK));
  or or_6 (or_6_out, and_1_out, and_2_out);
  // MIPS_RAM mips_ram_1: pin names not known; wires that end beside it: ALU_result[11:2], MDin, MemWrite, sb_1_out_3, CLK, RST, mips_ram_1_p7
  or or_7 (Branch, or_6_out, and_3_out);
  Adder #(.width(32)) adder_5 (.a(PC), .b(32'h4), .out(adder_5_out));  // open: cin, cout
  Decoder #(.select(2), .tristate("false"), .disabled("Z"), .enable("false")) decoder_1 (
    .out1(decoder_1_out1), .out2(decoder_1_out2), .out3(decoder_1_out3), .sel(\当前中断号 ));  // open: out0
  Multiplexer #(.select(1), .width(32), .disabled("Z"), .enable("false")) multiplexer_12 (
    .in0(ALU_result), .in1(mips_ram_1_p7), .out(multiplexer_12_out), .sel(MemToReg));
  assign JALR_Adress = ALU_result & 32'hfffffffe;  // AND_Gate and_4, 32 bits wide
  and and_5 (ClearA, URET, decoder_1_out1);
  and and_6 (ClearB, URET, decoder_1_out2);
  and and_7 (ClearC, decoder_1_out3, URET);
  or or_8 (or_8_out, JAL, JALR);
  Multiplexer #(.select(1), .width(32), .disabled("Z"), .enable("false")) multiplexer_13 (
    .in0(multiplexer_12_out), .in1(adder_5_out), .out(multiplexer_13_out), .sel(or_8_out));
  Comparator #(.width(32), .mode("twosComplement")) comparator_7 (
    .a(32'h22), .b(r1), .eq(comparator_7_eq));  // open: gt, lt
  Multiplexer #(.select(1), .width(32), .disabled("Z"), .enable("false")) multiplexer_14 (
    .in0(multiplexer_13_out), .in1(U_adress), .out(RDin), .sel(auipc));
  and and_8 (and_8_out, ecall, comparator_7_eq);
  and and_9 (and_9_out, ecall, not_3_out);
  not not_3 (not_3_out, comparator_7_eq);
  or or_9 (or_9_out, URET, IE);
  Decoder #(.select(2), .tristate("false"), .disabled("Z"), .enable("false")) decoder_2 (
    .out1(decoder_2_out1), .out2(decoder_2_out2), .out3(decoder_2_out3), .sel(\中断号 ));  // open: out0
  Multiplexer #(.select(1), .width(1), .disabled("Z"), .enable("false")) multiplexer_15 (
    .in0(and_9_out), .in1(1'b0), .out(halt), .sel(Go));
  Decoder #(.select(2), .tristate("false"), .disabled("Z"), .enable("false")) decoder_3 (
    .out1(decoder_3_out1), .out2(decoder_3_out2), .out3(decoder_3_out3), .sel(\中断号 ));  // open: out0
  Register #(.width(32), .trigger("rising"), .Select("low")) register_1 (
    .D(MDin), .en(and_8_out), .Q(LedData), .clk(CLK), .clr(RST));
  not not_4 (not_4_out, halt);
  Counter #(.width(16), .max('hffff), .ongoal("wrap"), .trigger("rising"), .behavior("new")) counter_2 (
    .count(not_4_out), .Q(\总周期数 ), .clk(CLK), .clr(RST));  // open: load, D, carry, preset, down
  and and_10 (and_10_out, \优先中断 , decoder_3_out1);
  and and_11 (and_11_out, decoder_3_out2, \优先中断 );
  and and_12 (and_12_out, decoder_3_out3, \优先中断 );
  and and_13 (and_13_out, or_9_out, decoder_2_out1);
  and and_14 (and_14_out, decoder_2_out2, or_9_out);
  and and_15 (and_15_out, decoder_2_out3, or_9_out);
  Register #(.width(32), .trigger("rising"), .Select("low")) mEPC1 (
    .D(LocalPC), .en(and_10_out), .Q(mEPC1_q), .clk(CLK), .clr(RST));
  Register #(.width(1), .trigger("rising"), .Select("low")) EPC1 (
    .D(and_16_out), .en(and_13_out), .Q(EPC1_q), .clk(CLK), .clr(RST));
  and and_16 (and_16_out, ~ClearA, 1'b1);  // AND_Gate
  Register #(.width(32), .trigger("rising"), .Select("low")) mEPC2 (
    .D(LocalPC), .en(and_11_out), .Q(mEPC2_q), .clk(CLK), .clr(RST));
  Register #(.width(32), .trigger("rising"), .Select("low")) mEPC3 (
    .D(LocalPC), .en(and_12_out), .Q(mEPC3_q), .clk(CLK), .clr(RST));
  and and_17 (and_17_out, ~ClearB, 1'b1);  // AND_Gate
  Register #(.width(1), .trigger("rising"), .Select("low")) EPC2 (
    .D(and_17_out), .en(and_14_out), .Q(EPC2_q), .clk(CLK), .clr(RST));
  and and_18 (and_18_out, ~ClearC, 1'b1);  // AND_Gate
  Multiplexer #(.select(2), .width(32), .disabled("Z"), .enable("false")) multiplexer_16 (
    .in1(mEPC1_q), .in2(mEPC2_q), .in3(mEPC3_q), .out(RETPC), .sel(\当前中断号 ));  // open: in0
  Register #(.width(1), .trigger("rising"), .Select("low")) EPC3 (
    .D(and_18_out), .en(and_15_out), .Q(EPC3_q), .clk(CLK), .clr(RST));
  Priority_Encoder #(.select(2), .disabled("Z")) priority_encoder_1 (
    .in0(1'b1), .in1(EPC1_q), .in2(EPC2_q), .in3(EPC3_q), .out(\当前中断号 ));  // open: gs, en_out, en_in
  or or_10 (W1, register_5_q, register_2_q);
  or or_11 (W2, register_6_q, register_3_q);
  or or_12 (W3, register_7_q, register_4_q);
  or or_13 (or_13_out, register_5_q, RST);
  or or_14 (or_14_out, register_6_q, RST);
  or or_15 (or_15_out, register_7_q, RST);
  Register #(.width(1), .trigger("rising"), .Select("low")) register_2 (
    .D(1'b1), .Q(register_2_q), .clk(IR1_t), .clr(or_13_out));  // open: en
  Register #(.width(1), .trigger("rising"), .Select("low")) register_3 (
    .D(1'b1), .Q(register_3_q), .clk(IR2_t), .clr(or_14_out));  // open: en
  Register #(.width(1), .trigger("rising"), .Select("low")) register_4 (
    .D(1'b1), .Q(register_4_q), .clk(IR3_t), .clr(or_15_out));  // open: en
  or or_16 (or_16_out, register_2_q, register_5_q);
  or or_17 (or_17_out, register_3_q, register_6_q);
  or or_18 (or_18_out, register_4_q, register_7_q);
  and and_19 (and_19_out, or_16_out, ~ClearA);  // AND_Gate
  and and_20 (and_20_out, or_17_out, ~ClearB);  // AND_Gate
  and and_21 (and_21_out, or_18_out, ~ClearC);  // AND_Gate
  Register #(.width(1), .trigger("rising"), .Select("low")) register_5 (
    .D(and_19_out), .Q(register_5_q), .clk(CLK), .clr(RST));  // open: en
  Register #(.width(1), .trigger("rising"), .Select("low")) register_6 (
    .D(and_20_out), .Q(register_6_q), .clk(CLK), .clr(RST));  // open: en
  Register #(.width(1), .trigger("rising"), .Select("low")) register_7 (
    .D(and_21_out), .Q(register_7_q), .clk(CLK), .clr(RST));  // open: en
  Priority_Encoder #(.select(2), .disabled("Z")) priority_encoder_2 (
    .in0(1'b1), .in1(register_5_q), .in2(register_6_q), .in3(register_7_q), .out(\中断号 ));  // open: gs, en_out, en_in
  or or_19 (\中断信号 , register_5_q, register_6_q, register_7_q);
  Comparator #(.width(2), .mode("unsigned")) comparator_8 (
    .a(\中断号 ), .b(\当前中断号 ), .gt(comparator_8_gt));  // open: eq, lt
  Counter #(.width(1), .max('h1), .ongoal("stay"), .trigger("rising"), .behavior("new")) counter_3 (
    .Q(counter_3_q), .clk(or_20_out), .clr(or_21_out));  // open: load, D, count, carry, preset, down
  or or_20 (or_20_out, CSRRCI, \优先中断 );
  or or_21 (or_21_out, CSRRSI, URET);
  and and_22 (INT, IE, \优先中断 );
  Multiplexer #(.select(2), .width(32), .disabled("Z"), .enable("false")) multiplexer_17 (
    .in1(32'h30ac), .in2(32'h3158), .in3(32'h3204), .out(INTPC), .sel(\中断号 ));  // open: in0
  and and_23 (\优先中断 , \中断信号 , comparator_8_gt);
  Register #(.width(1), .trigger("rising"), .Select("low")) register_8 (
    .D(not_5_out), .Q(IE), .clk(CLK));  // open: en, clr
  not not_5 (not_5_out, counter_3_q);

  // Other names for the same wires on the sheet: I_imm[11:0] = IR[31:20]

  // Notes on the sheet:
  //   中断源
  //   中断等待指示
  //   总复位信号应将除ROM以外所有存储组件全部清零
  //   多级中断测试信号模拟器
  //   数码管输出
  //   数码管输出应该用寄存器锁存，否则显示数据只能一闪而过
  //   数码管输出应该用寄存器锁存，否则显示数据只能一闪而过
  //   中断信号采样参考电路
  //   指令探针
  //   指令存储器
  //   contents of rom_1 (hex, n*v repeats v):
  //   7d000113 100413 1f41993 41f9d993 433 c00913 800b13 140413 f47413 800293 100313 499993 89e9b3 1300533
  //   2200893 73 406282b3 fe0294e3 140413 f00f93 1f47433 1c41413 800293 100313 49d993 89e9b3 1300533
  //   2200893 73 406282b3 fe0294e3 1c45413 406b0b33 b0463 f95ff06f 2b3 fff2c293 1029293 fff2e293 500533
  //   2200893 73 f5dff06f 1112023 410113 a12023 410113 812023 410113 1312023 410113 1412023 410113 1512023
  //   410113 1612023 410113 40e073 100b13 300a13 100a93 1600433 441413 14469b3 1300533 2200893 73 fe0416e3
  //   415a0a33 fe0a10e3 40f073 ffc10113 12b03 ffc10113 12a83 ffc10113 12a03 ffc10113 12983 ffc10113 12403
  //   ffc10113 12503 ffc10113 12883 200073 1112023 410113 a12023 410113 812023 410113 1312023 410113
  //   1412023 410113 1512023 410113 1612023 410113 40e073 200b13 300a13 100a93 1600433 441413 14469b3
  //   1300533 2200893 73 fe0416e3 415a0a33 fe0a10e3 40f073 ffc10113 12b03 ffc10113 12a83 ffc10113 12a03
  //   ffc10113 12983 ffc10113 12403 ffc10113 12503 ffc10113 12883 200073 1112023 410113 a12023 410113
  //   812023 410113 1312023 410113 1412023 410113 1512023 410113 1612023 410113 40e073 300b13 300a13
  //   100a93 1600433 441413 14469b3 1300533 2200893 73 fe0416e3 415a0a33 fe0a10e3 40f073 ffc10113 12b03
  //   ffc10113 12a83 ffc10113 12a03 ffc10113 12983 ffc10113 12403 ffc10113 12503 ffc10113 12883 200073
  //   指令字
  //   JAL
  //   JALR
  //   URET
  //   Beq
  //   Bne
  //   MemToReg
  //   MemWrite
  //   AluOP
  //   AluSrcB
  //   RegWrite
  //   为方便自动评测，需要输出PC，IR，寄存器堆写如数据RDin
  //   RAM写使能MemWrite、RAM写入数据MDin等信号
  //   控制位
  //   暂停节拍，不能为0
  //   戳工具置1进入计数暂停模式，ctrl+k时钟自动运行到对应节拍暂停
  //   ctrl+k关闭时钟连续运行，将控制位置零，进入单步调试模式调试
  //   数据存储器
  //   可计数暂停的时钟源
  //   用这个时钟源需要去掉电路中的其他时钟源
  //   保护现场，保存返回地址
  //   当前中断号
  //   高优先级中断判断
  //   中断使能寄存器IE
endmodule

module \封装正确性测试  (
);

  wire IR1, IR2, IR3, MemW, RegW;
  wire [31:0] EX_PC, ID_PC, IF_PC, IR, LED, MDin, MDinr, MEM_PC, PC, RDin, RDinr, WB_PC;

  \单周期RISC_V  \u_单周期risc_v_1  (
    .IR1(IR1), .IR2(IR2), .IR3(IR3), .RegWrite(RegW), .MemWrite(MemW), .PC(PC), .IR(IR), .RDin(RDin),
    .MDin(MDin), .LedData(LED));
  \气泡流水线  \u_气泡流水线_1  (
    .RegWrite(RegW), .MemWrite(MemW), .IF_PC(IF_PC), .ID_PC(ID_PC), .EX_PC(EX_PC), .M_PC(MEM_PC),
    .WB_PC(WB_PC), .RDin(RDinr), .MDin(MDinr), .LedData(LED));
  \单周期_单级中断  \u_单周期_单级中断_1  (
    .IR1(IR1), .IR2(IR2), .IR3(IR3), .RegWrite(RegW), .MemWrite(MemW), .PC(PC), .IR(IR), .RDin(RDin),
    .MDin(MDin), .LedData(LED));
  \理想流水线  \u_理想流水线_1  (
    .RegWrite(RegW), .MemWrite(MemW), .IF_PC(IF_PC), .ID_PC(ID_PC), .EX_PC(EX_PC), .M_PC(MEM_PC),
    .WB_PC(WB_PC), .RDin(RDinr), .MDin(MDinr), .LedData(LED));
  \重定向流水线  \u_重定向流水线_1  (
    .RegWrite(RegW), .MemWrite(MemW), .IF_PC(IF_PC), .ID_PC(ID_PC), .EX_PC(EX_PC), .M_PC(MEM_PC),
    .WB_PC(WB_PC), .RDin(RDinr), .MDin(MDinr), .LedData(LED));
  \单周期_多级中断  \u_单周期_多级中断_1  (
    .IR1(IR1), .IR2(IR2), .IR3(IR3), .RegWrite(RegW), .MemWrite(MemW), .PC(PC), .IR(IR), .RDin(RDin),
    .MDin(MDin), .LedData(LED));

  // Notes on the sheet:
  //   单周期封装测试
  //   气泡流水封装测试
  //   单周期+单级中断封装测试
  //   请检查上面封装有无位宽不匹配，引脚标签是否和连接的标签相对应，否则无法在educoder平台上正确测试
  //   理想流水封装测试
  //   重定向流水封装测试
  //   单周期+多级中断封装测试
endmodule

module ID (
  input  RST,
  input  halt,
  input  flush,
  input  beq,
  input  bne,
  input  MemToReg,
  input  MemWrite,
  input  [3:0] ALU_OP,
  input  ALU_SRCB,
  input  RegWrite,
  input  S_type,
  input  JAL,
  input  JALR,
  input  URET,
  input  ecall,
  input  [31:0] ID_PC,
  input  [31:0] r1,
  input  [31:0] r2,
  input  [31:0] Im,
  input  [31:0] Bm,
  input  [31:0] Jm,
  input  [31:0] PC_4,
  input  [31:0] ID_IR,
  input  [4:0] WRD,
  input  bltu,
  input  auipc,
  input  sb,
  input  [31:0] u,
  input  [1:0] RsFoward,
  input  [1:0] RtFoward,
  input  CLK,
  output beq_2,
  output bne_2,
  output MemToReg_2,
  output MemWrite_2,
  output [3:0] ALU_OP_2,
  output ALU_SRCB_2,
  output RegWrite_2,
  output S_type_2,
  output JAL_2,
  output JALR_2,
  output URET_2,
  output ecall_2,
  output [31:0] ID_PC_2,
  output [31:0] r1_2,
  output [31:0] r2_2,
  output [31:0] Im_2,
  output [31:0] Bm_2,
  output [31:0] Jm_2,
  output [31:0] PC_4_2,
  output [31:0] ID_IR_2,
  output [4:0] WRD_2,
  output bltu_2,
  output auipc_2,
  output sb_2,
  output [31:0] u_2,
  output [1:0] RsFoward_2,
  output [1:0] Rtfoward_2
);

  wire multiplexer_1_out, multiplexer_2_out, multiplexer_3_out, multiplexer_4_out, multiplexer_6_out,
       multiplexer_7_out, multiplexer_8_out, multiplexer_9_out, multiplexer_10_out, multiplexer_11_out,
       multiplexer_12_out, multiplexer_16_out, multiplexer_17_out, multiplexer_18_out, not_1_out, or_1_out,
       undriven;
  wire [1:0] multiplexer_20_out, multiplexer_21_out;
  wire [3:0] multiplexer_5_out;
  wire [4:0] multiplexer_27_out;
  wire [31:0] multiplexer_13_out, multiplexer_14_out, multiplexer_15_out, multiplexer_19_out,
       multiplexer_22_out, multiplexer_23_out, multiplexer_24_out, multiplexer_25_out, multiplexer_26_out;

  or or_1 (or_1_out, RST, flush);
  Multiplexer #(.select(1), .width(1), .disabled("Z"), .enable("false")) multiplexer_1 (
    .in0(beq), .in1(1'b0), .out(multiplexer_1_out), .sel(or_1_out));
  Multiplexer #(.select(1), .width(1), .disabled("Z"), .enable("false")) multiplexer_2 (
    .in0(bne), .in1(1'b0), .out(multiplexer_2_out), .sel(or_1_out));
  Multiplexer #(.select(1), .width(1), .disabled("Z"), .enable("false")) multiplexer_3 (
    .in0(MemToReg), .in1(1'b0), .out(multiplexer_3_out), .sel(or_1_out));
  Multiplexer #(.select(1), .width(1), .disabled("Z"), .enable("false")) multiplexer_4 (
    .in0(MemWrite), .in1(1'b0), .out(multiplexer_4_out), .sel(or_1_out));
  Multiplexer #(.select(1), .width(4), .disabled("Z"), .enable("false")) multiplexer_5 (
    .in0(ALU_OP), .in1(4'b0000), .out(multiplexer_5_out), .sel(or_1_out));
  Multiplexer #(.select(1), .width(1), .disabled("Z"), .enable("false")) multiplexer_6 (
    .in0(ALU_SRCB), .in1(1'b0), .out(multiplexer_6_out), .sel(or_1_out));
  Multiplexer #(.select(1), .width(1), .disabled("Z"), .enable("false")) multiplexer_7 (
    .in0(RegWrite), .in1(1'b0), .out(multiplexer_7_out), .sel(or_1_out));
  Multiplexer #(.select(1), .width(1), .disabled("Z"), .enable("false")) multiplexer_8 (
    .in0(S_type), .in1(1'b0), .out(multiplexer_8_out), .sel(or_1_out));
  Multiplexer #(.select(1), .width(1), .disabled("Z"), .enable("false")) multiplexer_9 (
    .in0(JAL), .in1(1'b0), .out(multiplexer_9_out), .sel(or_1_out));
  Multiplexer #(.select(1), .width(1), .disabled("Z"), .enable("false")) multiplexer_10 (
    .in0(JALR), .in1(1'b0), .out(multiplexer_10_out), .sel(or_1_out));
  Multiplexer #(.select(1), .width(1), .disabled("Z"), .enable("false")) multiplexer_11 (
    .in0(URET), .in1(1'b0), .out(multiplexer_11_out), .sel(or_1_out));
  Multiplexer #(.select(1), .width(1), .disabled("Z"), .enable("false")) multiplexer_12 (
    .in0(ecall), .in1(1'b0), .out(multiplexer_12_out), .sel(or_1_out));
  Multiplexer #(.select(1), .width(32), .disabled("Z"), .enable("false")) multiplexer_13 (
    .in0(ID_PC), .in1({32{1'b0}}), .out(multiplexer_13_out), .sel(or_1_out));
  Multiplexer #(.select(1), .width(32), .disabled("Z"), .enable("false")) multiplexer_14 (
    .in0(r1), .in1({32{1'b0}}), .out(multiplexer_14_out), .sel(or_1_out));
  Multiplexer #(.select(1), .width(32), .disabled("Z"), .enable("false")) multiplexer_15 (
    .in0(r2), .in1({32{1'b0}}), .out(multiplexer_15_out), .sel(or_1_out));
  Multiplexer #(.select(1), .width(1), .disabled("Z"), .enable("false")) multiplexer_16 (
    .in0(bltu), .in1(1'b0), .out(multiplexer_16_out), .sel(or_1_out));
  Multiplexer #(.select(1), .width(1), .disabled("Z"), .enable("false")) multiplexer_17 (
    .in0(auipc), .in1(1'b0), .out(multiplexer_17_out), .sel(or_1_out));
  Multiplexer #(.select(1), .width(1), .disabled("Z"), .enable("false")) multiplexer_18 (
    .in0(sb), .in1(1'b0), .out(multiplexer_18_out), .sel(or_1_out));
  Multiplexer #(.select(1), .width(32), .disabled("Z"), .enable("false")) multiplexer_19 (
    .in0(u), .in1({32{1'b0}}), .out(multiplexer_19_out), .sel(or_1_out));
  Multiplexer #(.select(1), .width(2), .disabled("Z"), .enable("false")) multiplexer_20 (
    .in0(RsFoward), .in1(2'b00), .out(multiplexer_20_out), .sel(or_1_out));
  Multiplexer #(.select(1), .width(2), .disabled("Z"), .enable("false")) multiplexer_21 (
    .in0(RtFoward), .in1(2'b00), .out(multiplexer_21_out), .sel(or_1_out));
  Multiplexer #(.select(1), .width(32), .disabled("Z"), .enable("false")) multiplexer_22 (
    .in0(Im), .in1({32{1'b0}}), .out(multiplexer_22_out), .sel(or_1_out));
  Multiplexer #(.select(1), .width(32), .disabled("Z"), .enable("false")) multiplexer_23 (
    .in0(Bm), .in1({32{1'b0}}), .out(multiplexer_23_out), .sel(or_1_out));
  Multiplexer #(.select(1), .width(32), .disabled("Z"), .enable("false")) multiplexer_24 (
    .in0(Jm), .in1({32{1'b0}}), .out(multiplexer_24_out), .sel(or_1_out));
  Multiplexer #(.select(1), .width(32), .disabled("Z"), .enable("false")) multiplexer_25 (
    .in0(PC_4), .in1({32{1'b0}}), .out(multiplexer_25_out), .sel(or_1_out));
  Multiplexer #(.select(1), .width(32), .disabled("Z"), .enable("false")) multiplexer_26 (
    .in0(ID_IR), .in1({32{1'b0}}), .out(multiplexer_26_out), .sel(or_1_out));
  Multiplexer #(.select(1), .width(5), .disabled("Z"), .enable("false")) multiplexer_27 (
    .in0(WRD), .in1({5{1'b0}}), .out(multiplexer_27_out), .sel(or_1_out));
  not not_1 (not_1_out, halt);
  Register #(.width(1), .trigger("rising"), .Select("low")) register_1 (
    .D(multiplexer_1_out), .en(not_1_out), .Q(beq_2), .clk(CLK));  // open: clr
  Register #(.width(1), .trigger("rising"), .Select("low")) register_2 (
    .D(multiplexer_2_out), .en(not_1_out), .Q(bne_2), .clk(CLK));  // open: clr
  Register #(.width(1), .trigger("rising"), .Select("low")) register_3 (
    .D(multiplexer_3_out), .en(not_1_out), .Q(MemToReg_2), .clk(CLK));  // open: clr
  Register #(.width(1), .trigger("rising"), .Select("low")) register_4 (
    .D(multiplexer_4_out), .en(not_1_out), .Q(MemWrite_2), .clk(CLK), .clr(undriven));
  Register #(.width(4), .trigger("rising"), .Select("low")) register_5 (
    .D(multiplexer_5_out), .en(not_1_out), .Q(ALU_OP_2), .clk(CLK));  // open: clr
  Register #(.width(1), .trigger("rising"), .Select("low")) register_6 (
    .D(multiplexer_6_out), .en(not_1_out), .Q(ALU_SRCB_2), .clk(CLK));  // open: clr
  Register #(.width(1), .trigger("rising"), .Select("low")) register_7 (
    .D(multiplexer_7_out), .en(not_1_out), .Q(RegWrite_2), .clk(CLK));  // open: clr
  Register #(.width(1), .trigger("rising"), .Select("low")) register_8 (
    .D(multiplexer_8_out), .en(not_1_out), .Q(S_type_2), .clk(CLK));  // open: clr
  Register #(.width(1), .trigger("rising"), .Select("low")) register_9 (
    .D(multiplexer_9_out), .en(not_1_out), .Q(JAL_2), .clk(CLK));  // open: clr
  Register #(.width(1), .trigger("rising"), .Select("low")) register_10 (
    .D(multiplexer_10_out), .en(not_1_out), .Q(JALR_2), .clk(CLK));  // open: clr
  Register #(.width(1), .trigger("rising"), .Select("low")) register_11 (
    .D(multiplexer_11_out), .en(not_1_out), .Q(URET_2), .clk(CLK));  // open: clr
  Register #(.width(1), .trigger("rising"), .Select("low")) register_12 (
    .D(multiplexer_12_out), .en(not_1_out), .Q(ecall_2), .clk(CLK));  // open: clr
  Register #(.width(32), .trigger("rising"), .Select("low")) register_13 (
    .D(multiplexer_13_out), .en(not_1_out), .Q(ID_PC_2), .clk(CLK));  // open: clr
  Register #(.width(32), .trigger("rising"), .Select("low")) register_14 (
    .D(multiplexer_14_out), .en(not_1_out), .Q(r1_2), .clk(CLK));  // open: clr
  Register #(.width(32), .trigger("rising"), .Select("low")) register_15 (
    .D(multiplexer_15_out), .en(not_1_out), .Q(r2_2), .clk(CLK));  // open: clr
  Register #(.width(32), .trigger("rising"), .Select("low")) register_16 (
    .D(multiplexer_22_out), .en(not_1_out), .Q(Im_2), .clk(CLK));  // open: clr
  Register #(.width(32), .trigger("rising"), .Select("low")) register_17 (
    .D(multiplexer_23_out), .en(not_1_out), .Q(Bm_2), .clk(CLK));  // open: clr
  Register #(.width(32), .trigger("rising"), .Select("low")) register_18 (
    .D(multiplexer_24_out), .en(not_1_out), .Q(Jm_2), .clk(CLK));  // open: clr
  Register #(.width(32), .trigger("rising"), .Select("low")) register_19 (
    .D(multiplexer_25_out), .en(not_1_out), .Q(PC_4_2), .clk(CLK));  // open: clr
  Register #(.width(32), .trigger("rising"), .Select("low")) register_20 (
    .D(multiplexer_26_out), .en(not_1_out), .Q(ID_IR_2), .clk(CLK));  // open: clr
  Register #(.width(5), .trigger("rising"), .Select("low")) register_21 (
    .D(multiplexer_27_out), .en(not_1_out), .Q(WRD_2), .clk(CLK));  // open: clr
  Register #(.width(1), .trigger("rising"), .Select("low")) register_22 (
    .D(multiplexer_16_out), .en(not_1_out), .Q(bltu_2), .clk(CLK));  // open: clr
  Register #(.width(1), .trigger("rising"), .Select("low")) register_23 (
    .D(multiplexer_17_out), .en(not_1_out), .Q(auipc_2), .clk(CLK));  // open: clr
  Register #(.width(1), .trigger("rising"), .Select("low")) register_24 (
    .D(multiplexer_18_out), .en(not_1_out), .Q(sb_2), .clk(CLK));  // open: clr
  Register #(.width(32), .trigger("rising"), .Select("low")) register_25 (
    .D(multiplexer_19_out), .en(not_1_out), .Q(u_2), .clk(CLK));  // open: clr
  Register #(.width(2), .trigger("rising"), .Select("low")) register_26 (
    .D(multiplexer_20_out), .en(not_1_out), .Q(RsFoward_2), .clk(CLK));  // open: clr
  Register #(.width(2), .trigger("rising"), .Select("low")) register_27 (
    .D(multiplexer_21_out), .en(not_1_out), .Q(Rtfoward_2), .clk(CLK));  // open: clr
  Pull_Resistor #(.pull(0)) pull_resistor_1 (.node(not_1_out));
endmodule

module IF (
  input  RST,
  input  CLK,
  input  flush,
  input  [31:0] IR,
  input  [31:0] PC,
  input  [31:0] PC_4,
  input  en,
  output [31:0] IR_2,
  output [31:0] PC_2,
  output [31:0] PC_4_2
);

  wire not_1_out, or_1_out;
  wire [31:0] multiplexer_1_out, multiplexer_2_out, multiplexer_3_out;

  or or_1 (or_1_out, RST, flush);
  Multiplexer #(.select(1), .width(32), .disabled("Z"), .enable("false")) multiplexer_1 (
    .in0(IR), .in1({32{1'b0}}), .out(multiplexer_1_out), .sel(or_1_out));
  Multiplexer #(.select(1), .width(32), .disabled("Z"), .enable("false")) multiplexer_2 (
    .in0(PC), .in1({32{1'b0}}), .out(multiplexer_2_out), .sel(or_1_out));
  Multiplexer #(.select(1), .width(32), .disabled("Z"), .enable("false")) multiplexer_3 (
    .in0(PC_4), .in1({32{1'b0}}), .out(multiplexer_3_out), .sel(or_1_out));
  Register #(.width(32), .trigger("rising"), .Select("low")) register_1 (
    .D(multiplexer_1_out), .en(not_1_out), .Q(IR_2), .clk(CLK));  // open: clr
  Register #(.width(32), .trigger("rising"), .Select("low")) register_2 (
    .D(multiplexer_2_out), .en(not_1_out), .Q(PC_2), .clk(CLK));  // open: clr
  Register #(.width(32), .trigger("rising"), .Select("low")) register_3 (
    .D(multiplexer_3_out), .en(not_1_out), .Q(PC_4_2), .clk(CLK));  // open: clr
  not not_1 (not_1_out, en);
endmodule

module EX (
  input  sb,
  input  auipc,
  input  RST,
  input  flush,
  input  JAL,
  input  JALR,
  input  URET,
  input  MemToReg,
  input  MenWrite,
  input  ecall,
  input  RegWirte,
  input  [4:0] Write,
  input  [31:0] ALU_Result,
  input  [31:0] EX_PC,
  input  [31:0] EX_IR,
  input  [31:0] PC_4,
  input  [31:0] R1,
  input  [31:0] R2,
  input  halt,
  input  CLK,
  input  [31:0] U,
  output sb_2,
  output auipc_2,
  output JAL_2,
  output JALR_2,
  output URET_2,
  output MemToReg_2,
  output MemWrite,
  output ecall_2,
  output RegWirte_2,
  output [4:0] Write_2,
  output [31:0] ALU_Result_2,
  output [31:0] MEN_PC,
  output [31:0] MEN_IR,
  output [31:0] PC_4_2,
  output [31:0] R1_2,
  output [31:0] R2_2,
  output [31:0] U_2
);

  wire multiplexer_1_out, multiplexer_2_out, multiplexer_3_out, multiplexer_4_out, multiplexer_5_out,
       multiplexer_6_out, multiplexer_7_out, multiplexer_8_out, multiplexer_9_out, not_1_out, or_1_out;
  wire [4:0] multiplexer_10_out;
  wire [31:0] multiplexer_11_out, multiplexer_12_out, multiplexer_13_out, multiplexer_14_out,
       multiplexer_15_out, multiplexer_16_out, multiplexer_17_out;

  or or_1 (or_1_out, RST, flush);
  not not_1 (not_1_out, halt);
  Multiplexer #(.select(1), .width(1), .disabled("Z"), .enable("false")) multiplexer_1 (
    .in0(sb), .in1(1'b0), .out(multiplexer_1_out), .sel(or_1_out));
  Multiplexer #(.select(1), .width(1), .disabled("Z"), .enable("false")) multiplexer_2 (
    .in0(auipc), .in1(1'b0), .out(multiplexer_2_out), .sel(or_1_out));
  Multiplexer #(.select(1), .width(1), .disabled("Z"), .enable("false")) multiplexer_3 (
    .in0(JAL), .in1(1'b0), .out(multiplexer_3_out), .sel(or_1_out));
  Multiplexer #(.select(1), .width(1), .disabled("Z"), .enable("false")) multiplexer_4 (
    .in0(JALR), .in1(1'b0), .out(multiplexer_4_out), .sel(or_1_out));
  Multiplexer #(.select(1), .width(1), .disabled("Z"), .enable("false")) multiplexer_5 (
    .in0(URET), .in1(1'b0), .out(multiplexer_5_out), .sel(or_1_out));
  Multiplexer #(.select(1), .width(1), .disabled("Z"), .enable("false")) multiplexer_6 (
    .in0(MemToReg), .in1(1'b0), .out(multiplexer_6_out), .sel(or_1_out));
  Multiplexer #(.select(1), .width(1), .disabled("Z"), .enable("false")) multiplexer_7 (
    .in0(MenWrite), .in1(1'b0), .out(multiplexer_7_out), .sel(or_1_out));
  Multiplexer #(.select(1), .width(1), .disabled("Z"), .enable("false")) multiplexer_8 (
    .in0(ecall), .in1(1'b0), .out(multiplexer_8_out), .sel(or_1_out));
  Multiplexer #(.select(1), .width(1), .disabled("Z"), .enable("false")) multiplexer_9 (
    .in0(RegWirte), .in1(1'b0), .out(multiplexer_9_out), .sel(or_1_out));
  Multiplexer #(.select(1), .width(5), .disabled("Z"), .enable("false")) multiplexer_10 (
    .in0(Write), .in1({5{1'b0}}), .out(multiplexer_10_out), .sel(or_1_out));
  Multiplexer #(.select(1), .width(32), .disabled("Z"), .enable("false")) multiplexer_11 (
    .in0(ALU_Result), .in1({32{1'b0}}), .out(multiplexer_11_out), .sel(or_1_out));
  Multiplexer #(.select(1), .width(32), .disabled("Z"), .enable("false")) multiplexer_12 (
    .in0(EX_PC), .in1({32{1'b0}}), .out(multiplexer_12_out), .sel(or_1_out));
  Multiplexer #(.select(1), .width(32), .disabled("Z"), .enable("false")) multiplexer_13 (
    .in0(EX_IR), .in1({32{1'b0}}), .out(multiplexer_13_out), .sel(or_1_out));
  Multiplexer #(.select(1), .width(32), .disabled("Z"), .enable("false")) multiplexer_14 (
    .in0(PC_4), .in1({32{1'b0}}), .out(multiplexer_14_out), .sel(or_1_out));
  Multiplexer #(.select(1), .width(32), .disabled("Z"), .enable("false")) multiplexer_15 (
    .in0(R1), .in1({32{1'b0}}), .out(multiplexer_15_out), .sel(or_1_out));
  Multiplexer #(.select(1), .width(32), .disabled("Z"), .enable("false")) multiplexer_16 (
    .in0(R2), .in1({32{1'b0}}), .out(multiplexer_16_out), .sel(or_1_out));
  Multiplexer #(.select(1), .width(32), .disabled("Z"), .enable("false")) multiplexer_17 (
    .in0(U), .in1({32{1'b0}}), .out(multiplexer_17_out), .sel(or_1_out));
  Register #(.width(1), .trigger("rising"), .Select("low")) register_1 (
    .D(multiplexer_1_out), .en(not_1_out), .Q(sb_2), .clk(CLK));  // open: clr
  Register #(.width(1), .trigger("rising"), .Select("low")) register_2 (
    .D(multiplexer_2_out), .en(not_1_out), .Q(auipc_2), .clk(CLK));  // open: clr
  Register #(.width(1), .trigger("rising"), .Select("low")) register_3 (
    .D(multiplexer_3_out), .en(not_1_out), .Q(JAL_2), .clk(CLK));  // open: clr
  Register #(.width(1), .trigger("rising"), .Select("low")) register_4 (
    .D(multiplexer_4_out), .en(not_1_out), .Q(JALR_2), .clk(CLK));  // open: clr
  Register #(.width(1), .trigger("rising"), .Select("low")) register_5 (
    .D(multiplexer_5_out), .en(not_1_out), .Q(URET_2), .clk(CLK));  // open: clr
  Register #(.width(1), .trigger("rising"), .Select("low")) register_6 (
    .D(multiplexer_6_out), .en(not_1_out), .Q(MemToReg_2), .clk(CLK));  // open: clr
  Register #(.width(1), .trigger("rising"), .Select("low")) register_7 (
    .D(multiplexer_7_out), .en(not_1_out), .Q(MemWrite), .clk(CLK));  // open: clr
  Register #(.width(1), .trigger("rising"), .Select("low")) register_8 (
    .D(multiplexer_8_out), .en(not_1_out), .Q(ecall_2), .clk(CLK));  // open: clr
  Register #(.width(1), .trigger("rising"), .Select("low")) register_9 (
    .D(multiplexer_9_out), .en(not_1_out), .Q(RegWirte_2), .clk(CLK));  // open: clr
  Register #(.width(5), .trigger("rising"), .Select("low")) register_10 (
    .D(multiplexer_10_out), .en(not_1_out), .Q(Write_2), .clk(CLK));  // open: clr
  Register #(.width(32), .trigger("rising"), .Select("low")) register_11 (
    .D(multiplexer_11_out), .en(not_1_out), .Q(ALU_Result_2), .clk(CLK));  // open: clr
  Register #(.width(32), .trigger("rising"), .Select("low")) register_12 (
    .D(multiplexer_12_out), .en(not_1_out), .Q(MEN_PC), .clk(CLK));  // open: clr
  Register #(.width(32), .trigger("rising"), .Select("low")) register_13 (
    .D(multiplexer_13_out), .en(not_1_out), .Q(MEN_IR), .clk(CLK));  // open: clr
  Register #(.width(32), .trigger("rising"), .Select("low")) register_14 (
    .D(multiplexer_14_out), .en(not_1_out), .Q(PC_4_2), .clk(CLK));  // open: clr
  Register #(.width(32), .trigger("rising"), .Select("low")) register_15 (
    .D(multiplexer_15_out), .en(not_1_out), .Q(R1_2), .clk(CLK));  // open: clr
  Register #(.width(32), .trigger("rising"), .Select("low")) register_16 (
    .D(multiplexer_16_out), .en(not_1_out), .Q(R2_2), .clk(CLK));  // open: clr
  Register #(.width(32), .trigger("rising"), .Select("low")) register_17 (
    .D(multiplexer_17_out), .en(not_1_out), .Q(U_2), .clk(CLK));  // open: clr
  Pull_Resistor #(.pull(0)) pull_resistor_1 (.node(not_1_out));
endmodule

module Mem (
  input  auipc,
  input  sb,
  input  RST,
  input  flush,
  input  JAL,
  input  JALR,
  input  URET,
  input  MemToReg,
  input  MenWrite,
  input  ecall,
  input  RegWirte,
  input  [4:0] Write,
  input  [31:0] ALU_Result,
  input  [31:0] Mem_PC,
  input  [31:0] Mem_IR,
  input  [31:0] PC_4,
  input  [31:0] R1,
  input  [31:0] R2,
  input  [31:0] MData,
  input  CLK,
  input  halt,
  input  [31:0] u,
  output auipc_2,
  output sb_2,
  output JAL_2,
  output JALR_2,
  output URET_2,
  output MemToReg_2,
  output MemWrite,
  output ecall_2,
  output RegWirte_2,
  output [4:0] Write_2,
  output [31:0] ALU_Result_2,
  output [31:0] Mem_PC_2,
  output [31:0] Mem_IR_2,
  output [31:0] PC_4_2,
  output [31:0] R1_2,
  output [31:0] R2_2,
  output [31:0] Mdata_2,
  output [31:0] u_2
);

  wire multiplexer_1_out, multiplexer_2_out, multiplexer_3_out, multiplexer_4_out, multiplexer_5_out,
       multiplexer_6_out, multiplexer_7_out, multiplexer_17_out, multiplexer_18_out, not_1_out, or_1_out;
  wire [4:0] multiplexer_8_out;
  wire [31:0] multiplexer_9_out, multiplexer_10_out, multiplexer_11_out, multiplexer_12_out,
       multiplexer_13_out, multiplexer_14_out, multiplexer_15_out, multiplexer_16_out;

  or or_1 (or_1_out, RST, flush);
  not not_1 (not_1_out, halt);
  Multiplexer #(.select(1), .width(1), .disabled("Z"), .enable("false")) multiplexer_1 (
    .in0(JAL), .in1(1'b0), .out(multiplexer_1_out), .sel(or_1_out));
  Multiplexer #(.select(1), .width(1), .disabled("Z"), .enable("false")) multiplexer_2 (
    .in0(JALR), .in1(1'b0), .out(multiplexer_2_out), .sel(or_1_out));
  Multiplexer #(.select(1), .width(1), .disabled("Z"), .enable("false")) multiplexer_3 (
    .in0(URET), .in1(1'b0), .out(multiplexer_3_out), .sel(or_1_out));
  Multiplexer #(.select(1), .width(1), .disabled("Z"), .enable("false")) multiplexer_4 (
    .in0(MemToReg), .in1(1'b0), .out(multiplexer_4_out), .sel(or_1_out));
  Multiplexer #(.select(1), .width(1), .disabled("Z"), .enable("false")) multiplexer_5 (
    .in0(MenWrite), .in1(1'b0), .out(multiplexer_5_out), .sel(or_1_out));
  Multiplexer #(.select(1), .width(1), .disabled("Z"), .enable("false")) multiplexer_6 (
    .in0(ecall), .in1(1'b0), .out(multiplexer_6_out), .sel(or_1_out));
  Multiplexer #(.select(1), .width(1), .disabled("Z"), .enable("false")) multiplexer_7 (
    .in0(RegWirte), .in1(1'b0), .out(multiplexer_7_out), .sel(or_1_out));
  Multiplexer #(.select(1), .width(5), .disabled("Z"), .enable("false")) multiplexer_8 (
    .in0(Write), .in1({5{1'b0}}), .out(multiplexer_8_out), .sel(or_1_out));
  Multiplexer #(.select(1), .width(32), .disabled("Z"), .enable("false")) multiplexer_9 (
    .in0(ALU_Result), .in1({32{1'b0}}), .out(multiplexer_9_out), .sel(or_1_out));
  Multiplexer #(.select(1), .width(32), .disabled("Z"), .enable("false")) multiplexer_10 (
    .in0(Mem_PC), .in1({32{1'b0}}), .out(multiplexer_10_out), .sel(or_1_out));
  Multiplexer #(.select(1), .width(32), .disabled("Z"), .enable("false")) multiplexer_11 (
    .in0(Mem_IR), .in1({32{1'b0}}), .out(multiplexer_11_out), .sel(or_1_out));
  Multiplexer #(.select(1), .width(32), .disabled("Z"), .enable("false")) multiplexer_12 (
    .in0(PC_4), .in1({32{1'b0}}), .out(multiplexer_12_out), .sel(or_1_out));
  Multiplexer #(.select(1), .width(32), .disabled("Z"), .enable("false")) multiplexer_13 (
    .in0(R1), .in1({32{1'b0}}), .out(multiplexer_13_out), .sel(or_1_out));
  Multiplexer #(.select(1), .width(32), .disabled("Z"), .enable("false")) multiplexer_14 (
    .in0(R2), .in1({32{1'b0}}), .out(multiplexer_14_out), .sel(or_1_out));
  Multiplexer #(.select(1), .width(32), .disabled("Z"), .enable("false")) multiplexer_15 (
    .in0(MData), .in1({32{1'b0}}), .out(multiplexer_15_out), .sel(or_1_out));
  Multiplexer #(.select(1), .width(32), .disabled("Z"), .enable("false")) multiplexer_16 (
    .in0(u), .in1({32{1'b0}}), .out(multiplexer_16_out), .sel(or_1_out));
  Multiplexer #(.select(1), .width(1), .disabled("Z"), .enable("false")) multiplexer_17 (
    .in0(auipc), .in1(1'b0), .out(multiplexer_17_out), .sel(or_1_out));
  Multiplexer #(.select(1), .width(1), .disabled("Z"), .enable("false")) multiplexer_18 (
    .in0(sb), .in1(1'b0), .out(multiplexer_18_out), .sel(or_1_out));
  Register #(.width(1), .trigger("rising"), .Select("low")) register_1 (
    .D(multiplexer_17_out), .en(not_1_out), .Q(auipc_2), .clk(CLK));  // open: clr
  Register #(.width(1), .trigger("rising"), .Select("low")) register_2 (
    .D(multiplexer_18_out), .en(not_1_out), .Q(sb_2), .clk(CLK));  // open: clr
  Register #(.width(1), .trigger("rising"), .Select("low")) register_3 (
    .D(multiplexer_1_out), .en(not_1_out), .Q(JAL_2), .clk(CLK));  // open: clr
  Register #(.width(1), .trigger("rising"), .Select("low")) register_4 (
    .D(multiplexer_2_out), .en(not_1_out), .Q(JALR_2), .clk(CLK));  // open: clr
  Register #(.width(1), .trigger("rising"), .Select("low")) register_5 (
    .D(multiplexer_3_out), .en(not_1_out), .Q(URET_2), .clk(CLK));  // open: clr
  Register #(.width(1), .trigger("rising"), .Select("low")) register_6 (
    .D(multiplexer_4_out), .en(not_1_out), .Q(MemToReg_2), .clk(CLK));  // open: clr
  Register #(.width(1), .trigger("rising"), .Select("low")) register_7 (
    .D(multiplexer_5_out), .en(not_1_out), .Q(MemWrite), .clk(CLK));  // open: clr
  Register #(.width(1), .trigger("rising"), .Select("low")) register_8 (
    .D(multiplexer_6_out), .en(not_1_out), .Q(ecall_2), .clk(CLK));  // open: clr
  Register #(.width(1), .trigger("rising"), .Select("low")) register_9 (
    .D(multiplexer_7_out), .en(not_1_out), .Q(RegWirte_2), .clk(CLK));  // open: clr
  Register #(.width(5), .trigger("rising"), .Select("low")) register_10 (
    .D(multiplexer_8_out), .en(not_1_out), .Q(Write_2), .clk(CLK));  // open: clr
  Register #(.width(32), .trigger("rising"), .Select("low")) register_11 (
    .D(multiplexer_9_out), .en(not_1_out), .Q(ALU_Result_2), .clk(CLK));  // open: clr
  Register #(.width(32), .trigger("rising"), .Select("low")) register_12 (
    .D(multiplexer_10_out), .en(not_1_out), .Q(Mem_PC_2), .clk(CLK));  // open: clr
  Register #(.width(32), .trigger("rising"), .Select("low")) register_13 (
    .D(multiplexer_11_out), .en(not_1_out), .Q(Mem_IR_2), .clk(CLK));  // open: clr
  Register #(.width(32), .trigger("rising"), .Select("low")) register_14 (
    .D(multiplexer_12_out), .en(not_1_out), .Q(PC_4_2), .clk(CLK));  // open: clr
  Register #(.width(32), .trigger("rising"), .Select("low")) register_15 (
    .D(multiplexer_13_out), .en(not_1_out), .Q(R1_2), .clk(CLK));  // open: clr
  Register #(.width(32), .trigger("rising"), .Select("low")) register_16 (
    .D(multiplexer_14_out), .en(not_1_out), .Q(R2_2), .clk(CLK));  // open: clr
  Register #(.width(32), .trigger("rising"), .Select("low")) register_17 (
    .D(multiplexer_15_out), .en(not_1_out), .Q(Mdata_2), .clk(CLK));  // open: clr
  Register #(.width(32), .trigger("rising"), .Select("low")) register_18 (
    .D(multiplexer_16_out), .en(not_1_out), .Q(u_2), .clk(CLK));  // open: clr
  Pull_Resistor #(.pull(0)) pull_resistor_1 (.node(not_1_out));
endmodule

module sb (
  input  in_1,
  input  [31:0] R2,
  output [3:0] out_3,
  output [31:0] darta
);

  wire [3:0] multiplexer_1_out;

  Multiplexer #(.select(2), .width(4), .disabled("Z"), .enable("false")) multiplexer_1 (
    .in0(4'b0001), .in1(4'b0010), .in2(4'b0100), .in3(4'b1000), .out(multiplexer_1_out), .sel(R2[1:0]));
  Demultiplexer #(.select(2), .width(8), .tristate("false"), .disabled("Z"), .enable("false")) demultiplexer_1 (
    .out0(darta[7:0]), .out1(darta[15:8]), .out2(darta[23:16]), .out3(darta[31:24]), .in(R2[7:0]),
    .sel(R2[1:0]));
  Multiplexer #(.select(1), .width(4), .disabled("Z"), .enable("false")) multiplexer_2 (
    .in0(4'b1111), .in1(multiplexer_1_out), .out(out_3), .sel(in_1));
endmodule

module datahazzard (
  input  RtUsed,
  input  [4:0] Rt,
  input  [4:0] Rt_2,
  input  [4:0] MEN_WriteReg,
  input  MEN_Regwrite,
  input  RtUsed_2,
  input  [4:0] Rt_3,
  input  [4:0] Rt_4,
  input  [4:0] EX_WriteReg,
  input  EX_Regwrite,
  input  RsUsed,
  input  [4:0] Rs,
  input  [4:0] Rs_2,
  input  [4:0] EX_WriteReg_2,
  input  EX_Regwrite_2,
  input  RsUsed_2,
  input  [4:0] Rs_3,
  input  [4:0] Rs_4,
  input  [4:0] MEN_WriteReg_2,
  input  MEN_Regwrite_2,
  output datahazzed
);

  wire and_1_out, and_2_out, and_3_out, and_4_out, and_5_out, and_6_out, and_7_out, and_8_out, and_9_out,
       and_10_out, and_11_out, and_12_out, comparator_1_eq, comparator_2_eq, comparator_3_eq,
       comparator_4_eq, comparator_5_eq, comparator_6_eq, comparator_7_eq, comparator_8_eq, not_1_out,
       not_2_out, not_3_out, not_4_out, or_1_out, or_2_out;

  not not_1 (not_1_out, comparator_1_eq);
  Comparator #(.width(5), .mode("unsigned")) comparator_1 (
    .a(Rt), .b({5{1'b0}}), .eq(comparator_1_eq));  // open: gt, lt
  Comparator #(.width(5), .mode("unsigned")) comparator_2 (
    .a(Rt_2), .b(MEN_WriteReg), .eq(comparator_2_eq));  // open: gt, lt
  not not_2 (not_2_out, comparator_3_eq);
  Comparator #(.width(5), .mode("unsigned")) comparator_3 (
    .a(Rt_3), .b({5{1'b0}}), .eq(comparator_3_eq));  // open: gt, lt
  Comparator #(.width(5), .mode("unsigned")) comparator_4 (
    .a(Rt_4), .b(EX_WriteReg), .eq(comparator_4_eq));  // open: gt, lt
  Comparator #(.width(5), .mode("unsigned")) comparator_5 (
    .a(Rs), .b({5{1'b0}}), .eq(comparator_5_eq));  // open: gt, lt
  not not_3 (not_3_out, comparator_5_eq);
  Comparator #(.width(5), .mode("unsigned")) comparator_6 (
    .a(Rs_2), .b(EX_WriteReg_2), .eq(comparator_6_eq));  // open: gt, lt
  Comparator #(.width(5), .mode("unsigned")) comparator_7 (
    .a(Rs_3), .b({5{1'b0}}), .eq(comparator_7_eq));  // open: gt, lt
  not not_4 (not_4_out, comparator_7_eq);
  Comparator #(.width(5), .mode("unsigned")) comparator_8 (
    .a(Rs_4), .b(MEN_WriteReg_2), .eq(comparator_8_eq));  // open: gt, lt
  and and_1 (and_1_out, RtUsed, not_1_out);
  and and_2 (and_2_out, comparator_2_eq, MEN_Regwrite);
  and and_3 (and_3_out, RtUsed_2, not_2_out);
  and and_4 (and_4_out, comparator_4_eq, EX_Regwrite);
  and and_5 (and_5_out, RsUsed, not_3_out);
  and and_6 (and_6_out, comparator_6_eq, EX_Regwrite_2);
  and and_7 (and_7_out, RsUsed_2, not_4_out);
  and and_8 (and_8_out, comparator_8_eq, MEN_Regwrite_2);
  and and_9 (and_9_out, and_1_out, and_2_out);
  and and_10 (and_10_out, and_3_out, and_4_out);
  and and_11 (and_11_out, and_5_out, and_6_out);
  and and_12 (and_12_out, and_7_out, and_8_out);
  or or_1 (or_1_out, and_9_out, and_10_out);
  or or_2 (or_2_out, and_11_out, and_12_out);
  or or_3 (datahazzed, or_1_out, or_2_out);
endmodule

module \气泡处理  (
  input  datahazzd,
  input  branch,
  input  datahazzd_2,
  output stall,
  output flush
);

  or or_1 (flush, branch, datahazzd_2);

  assign stall = datahazzd;
endmodule

module loaduse (
  input  rsused,
  input  [4:0] rs,
  input  [4:0] EX_WriteReg,
  input  EX_MemRead,
  input  rtused,
  input  [4:0] rt,
  input  [4:0] EX_WriteReg_2,
  input  EX_MemRead_2,
  output LoadUse
);

  wire and_1_out, and_2_out, comparator_1_eq, comparator_2_eq, comparator_3_eq, comparator_4_eq, not_1_out,
       not_2_out;

  Comparator #(.width(5), .mode("twosComplement")) comparator_1 (
    .a(rs), .b({5{1'b0}}), .eq(comparator_1_eq));  // open: gt, lt
  not not_1 (not_1_out, comparator_1_eq);
  Comparator #(.width(5), .mode("twosComplement")) comparator_2 (
    .a(rs), .b(EX_WriteReg), .eq(comparator_2_eq));  // open: gt, lt
  Comparator #(.width(5), .mode("twosComplement")) comparator_3 (
    .a(rt), .b({5{1'b0}}), .eq(comparator_3_eq));  // open: gt, lt
  not not_2 (not_2_out, comparator_3_eq);
  Comparator #(.width(5), .mode("twosComplement")) comparator_4 (
    .a(rt), .b(EX_WriteReg_2), .eq(comparator_4_eq));  // open: gt, lt
  and and_1 (and_1_out, rsused, not_1_out, comparator_2_eq, EX_MemRead);
  and and_2 (and_2_out, rtused, not_2_out, comparator_4_eq, EX_MemRead_2);
  or or_1 (LoadUse, and_1_out, and_2_out);
endmodule

module foward (
  input  [4:0] EX_WriteReg,
  input  [4:0] rs,
  input  EX_RegWrite,
  input  rsused,
  input  [4:0] EX_WriteReg_2,
  input  [4:0] MEM_WriteReg,
  input  [4:0] rt,
  input  [4:0] rs_2,
  input  EX_RegWrite_2,
  input  MEM_RegWrite,
  input  rtused,
  input  rsused_2,
  input  [4:0] MEM_WriteReg_2,
  input  [4:0] rt_2,
  input  MEM_RegWrite_2,
  input  rtused_2,
  output [1:0] RSFoward,
  output [1:0] RTFoward
);

  wire comparator_1_eq, comparator_2_eq, comparator_3_eq, comparator_4_eq, comparator_5_eq, comparator_6_eq,
       comparator_7_eq, comparator_8_eq, not_1_out, not_2_out, not_3_out, not_4_out;
  wire [1:0] and_1_out, and_3_out;

  Comparator #(.width(5), .mode("twosComplement")) comparator_1 (
    .a(rs), .b({5{1'b0}}), .eq(comparator_1_eq));  // open: gt, lt
  Comparator #(.width(5), .mode("twosComplement")) comparator_2 (
    .a(rs_2), .b({5{1'b0}}), .eq(comparator_2_eq));  // open: gt, lt
  Comparator #(.width(5), .mode("twosComplement")) comparator_3 (
    .a(EX_WriteReg), .b(rs), .eq(comparator_3_eq));  // open: gt, lt
  not not_1 (not_1_out, comparator_1_eq);
  Comparator #(.width(5), .mode("twosComplement")) comparator_4 (
    .a(MEM_WriteReg), .b(rs_2), .eq(comparator_4_eq));  // open: gt, lt
  not not_2 (not_2_out, comparator_2_eq);
  and and_1 (and_1_out[0], comparator_3_eq, not_1_out, EX_RegWrite, rsused);
  and and_2 (and_1_out[1], comparator_4_eq, not_2_out, MEM_RegWrite, rsused_2);
  Multiplexer #(.select(2), .width(2), .disabled("Z"), .enable("false")) multiplexer_1 (
    .in0(2'b00), .in1(2'b10), .in2(2'b01), .in3(2'b10), .out(RSFoward), .sel(and_1_out));
  Comparator #(.width(5), .mode("twosComplement")) comparator_5 (
    .a(EX_WriteReg_2), .b(rt), .eq(comparator_5_eq));  // open: gt, lt
  not not_3 (not_3_out, comparator_6_eq);
  Comparator #(.width(5), .mode("twosComplement")) comparator_6 (
    .a(rt), .b({5{1'b0}}), .eq(comparator_6_eq));  // open: gt, lt
  Comparator #(.width(5), .mode("twosComplement")) comparator_7 (
    .a(MEM_WriteReg_2), .b(rt_2), .eq(comparator_7_eq));  // open: gt, lt
  Comparator #(.width(5), .mode("twosComplement")) comparator_8 (
    .a(rt_2), .b({5{1'b0}}), .eq(comparator_8_eq));  // open: gt, lt
  not not_4 (not_4_out, comparator_8_eq);
  and and_3 (and_3_out[0], comparator_5_eq, not_3_out, EX_RegWrite_2, rtused);
  and and_4 (and_3_out[1], comparator_7_eq, not_4_out, MEM_RegWrite_2, rtused_2);
  Multiplexer #(.select(2), .width(2), .disabled("Z"), .enable("false")) multiplexer_2 (
    .in0(2'b00), .in1(2'b10), .in2(2'b01), .in3(2'b10), .out(RTFoward), .sel(and_3_out));
endmodule
