// Logisim project teamwork.circ as structural Verilog: 34 circuits, main circuit ◇单周期RISC-V
// 单周期硬布线控制器
module \单周期硬布线控制器  (
  input  [4:0] OP,
  input  [4:0] Funct,
  input  in_3,
  output [3:0] ALU_OP,
  output uret,
  output MemToReg,
  output ecall,
  output MemWrite,
  output ALU_SRC,
  output BGEU,
  output RegWrite,
  output S_type,
  output Beq,
  output Bne,
  output Jalr,
  output JAL
);

  wire \控制信号自动生成_1_ecall ;

  \运算控制器自动生成  \u_运算控制器自动生成_1  (
    .OP2(OP[0]), .OP3(OP[1]), .OP4(OP[2]), .OP5(OP[3]), .OP6(OP[4]), .F12(Funct[0]), .F13(Funct[1]),
    .F14(Funct[2]), .F25(Funct[3]), .F30(Funct[4]), .S0(ALU_OP[0]), .S1(ALU_OP[1]), .S2(ALU_OP[2]),
    .S3(ALU_OP[3]));
  \控制信号自动生成  \u_控制信号自动生成_1  (
    .OP2(OP[0]), .OP3(OP[1]), .OP4(OP[2]), .OP5(OP[3]), .MemToReg(MemToReg), .OP6(OP[4]), .F12(Funct[0]),
    .F13(Funct[1]), .F14(Funct[2]), .F25(Funct[3]), .F30(Funct[4]), .MemWrite(MemWrite), .ALU_SRC(ALU_SRC),
    .bgeu(BGEU), .RegWrite(RegWrite), .ecall(\控制信号自动生成_1_ecall ), .S_Type(S_type), .BEQ(Beq), .BNE(Bne),
    .JALR(Jalr), .JAL(JAL));
  and and_1 (uret, in_3, \控制信号自动生成_1_ecall );
  and and_2 (ecall, ~in_3, \控制信号自动生成_1_ecall );  // AND_Gate

  // Other names for the same wires on the sheet: IR21 = in_3; OP_CODE[4:0] = OP

  // Notes on the sheet:
  //   运算器控制器，根据指令生成运算器功能选择信号
  //   控制信号生成，产生数据通路需要的其他控制信号
endmodule

module \单周期RISC_V  (
  input  IR1,
  input  IR2,
  input  IR3,
  output RegWrite,
  output MemWrite,
  output [31:0] PC,
  output [31:0] IR,
  output [31:0] RDin,
  output [31:0] MDin,
  output [31:0] LedData
);

  wire AluSrcB, and_1_out, and_2_out, and_4_out, and_5_out, BGEU, CLK, clock_1_out, comparator_2_eq,
       comparator_3_eq, comparator_4_eq, comparator_4_lt, d_ff_1_q, ecall, equal, flag, GE, Go, halt, IR1_t,
       IR2_t, IR3_t, IRA, IRB, IRC, JAL, JALR, MemToReg, nand_1_out, not_1_out, not_2_out, not_3_out,
       not_4_out, not_5_out, not_6_out, not_7_out, or_1_out, or_2_out, or_7_out, riscv_probe_1_p3, RST,
       S_type, tunnel1, W1, W2, W3, \单周期硬布线控制器_1_beq , \单周期硬布线控制器_1_bne ;
  wire [3:0] \单周期硬布线控制器_1_alu_op ;
  wire [4:0] multiplexer_1_out, multiplexer_3_out;
  wire [11:0] multiplexer_2_out;
  wire [12:0] CNT_num;
  wire [15:0] \总周期数 ;
  wire [31:0] adder_1_out, adder_2_out, adder_3_out, adder_4_out, alu_1_result, alu_1_result_2, aluresult,
       and_3_out, bit_extender_1_out, bit_extender_2_out, bit_extender_3_out, bit_extender_4_out,
       bit_extender_5_out, multiplexer_4_out, multiplexer_6_out, multiplexer_7_out, multiplexer_8_out,
       multiplexer_9_out, multiplexer_10_out, multiplexer_11_out, multiplexer_12_out, ram_1_data,
       regifile_1_r1, shifter_1_out, shifter_2_out;

  Button \u_继续运行  (.out(Go));
  Button _1 (.out(IRA));
  Button _2 (.out(IRB));
  Button _3 (.out(IRC));
  Button u_RST (.out(RST));
  LED #(.active("true")) led_1 (.in(W1));
  LED #(.active("true")) led_2 (.in(W2));
  LED #(.active("true")) led_3 (.in(W3));
  Hex_Digit_Display hex_digit_display_1 (.value(LedData[31:28]));  // open: dp
  not not_1 (not_1_out, halt);
  or or_1 (or_1_out, not_1_out, Go);
  Counter #(.width(16), .max('hffff), .ongoal("wrap"), .trigger("rising"), .behavior("new")) counter_1 (
    .count(or_1_out), .Q(\总周期数 ), .clk(CLK), .clr(RST));  // open: load, D, carry, preset, down
  Register #(.width(32), .trigger("rising"), .Select("low")) u_PC (
    .D(multiplexer_8_out), .en(or_2_out), .Q(PC), .clk(CLK), .clr(RST));
  or or_2 (or_2_out, not_2_out, Go);
  not not_2 (not_2_out, halt);
  Hex_Digit_Display hex_digit_display_2 (.value(LedData[23:20]));  // open: dp
  Hex_Digit_Display hex_digit_display_3 (.value(LedData[27:24]));  // open: dp
  Hex_Digit_Display hex_digit_display_4 (.value(LedData[15:12]));  // open: dp
  Hex_Digit_Display hex_digit_display_5 (.value(LedData[19:16]));  // open: dp
  // RiscV_Probe riscv_probe_1: pin names not known; wires that end beside it: PC[11:2], IR, riscv_probe_1_p3
  Hex_Digit_Display hex_digit_display_6 (.value(LedData[7:4]));  // open: dp
  Hex_Digit_Display hex_digit_display_7 (.value(LedData[11:8]));  // open: dp
  // Probe on \总周期数 
  ROM #(.addrWidth(10), .dataWidth(32), .Select("high")) rom_1 (.addr(PC[11:2]), .data(IR));
  Hex_Digit_Display hex_digit_display_8 (.value(LedData[3:0]));  // open: dp
  \单周期硬布线控制器  \u_单周期硬布线控制器_1  (
    .Funct({IR[30], IR[25], IR[14:12]}), .OP(IR[6:2]), .ALU_OP(\单周期硬布线控制器_1_alu_op ), .MemToReg(MemToReg),
    .MemWrite(MemWrite), .ALU_SRC(AluSrcB), .RegWrite(RegWrite), .ecall(ecall), .S_type(S_type), .Jalr(JALR),
    .Beq(\单周期硬布线控制器_1_beq ), .JAL(JAL), .Bne(\单周期硬布线控制器_1_bne ), .in_3(IR[21]), .uret(riscv_probe_1_p3),
    .BGEU(BGEU));
  Multiplexer #(.select(1), .width(5), .disabled("Z"), .enable("false")) multiplexer_1 (
    .in0(IR[24:20]), .in1(5'b01010), .out(multiplexer_1_out), .sel(ecall));
  Multiplexer #(.select(1), .width(12), .disabled("Z"), .enable("false")) multiplexer_2 (
    .in0(IR[31:20]), .in1({IR[31:25], IR[11:7]}), .out(multiplexer_2_out), .sel(S_type));
  or or_3 (IR1_t, IR1, IRA);
  Multiplexer #(.select(1), .width(5), .disabled("Z"), .enable("false")) multiplexer_3 (
    .in0(IR[19:15]), .in1(5'b10001), .out(multiplexer_3_out), .sel(ecall));
  assign bit_extender_1_out = {{20{IR[31]}}, {IR[31], IR[7], IR[30:25], IR[11:8]}};  // Bit_Extender bit_extender_1
  assign bit_extender_2_out = {{12{IR[31]}}, {IR[31], IR[19:12], IR[20], IR[30:21]}};  // Bit_Extender bit_extender_2
  or or_4 (IR2_t, IR2, IRB);
  not not_3 (not_3_out, CLK);
  Regifile regifile_1 (
    .Din(RDin), .Clk(not_3_out), .R1(regifile_1_r1), .R2(MDin), .WE(RegWrite), .W_num(IR[11:7]),
    .R1_num(multiplexer_3_out), .R2_num(multiplexer_1_out));
  assign bit_extender_3_out = {{20{multiplexer_2_out[11]}}, multiplexer_2_out};  // Bit_Extender bit_extender_3
  Shifter #(.width(32), .shift("ll")) shifter_1 (.in(bit_extender_1_out), .\dist (5'b00001), .out(shifter_1_out));
  Shifter #(.width(32), .shift("ll")) shifter_2 (.in(bit_extender_2_out), .\dist (5'b00001), .out(shifter_2_out));
  Adder #(.width(32)) adder_1 (.a(shifter_1_out), .b(PC), .out(adder_1_out));  // open: cin, cout
  Adder #(.width(32)) adder_2 (.a(shifter_2_out), .b(PC), .out(adder_2_out));  // open: cin, cout
  or or_5 (IR3_t, IR3, IRC);
  Multiplexer #(.select(1), .width(32), .disabled("Z"), .enable("false")) multiplexer_4 (
    .in0(MDin), .in1(bit_extender_3_out), .out(multiplexer_4_out), .sel(AluSrcB));
  and and_1 (and_1_out, equal, \单周期硬布线控制器_1_beq );
  not not_4 (not_4_out, equal);
  and and_2 (and_2_out, not_4_out, \单周期硬布线控制器_1_bne );
  ALU alu_1 (
    .X(regifile_1_r1), .Y(multiplexer_4_out), .AluOP(\单周期硬布线控制器_1_alu_op ), .Equal(equal),
    .Result(alu_1_result), .Result_2(alu_1_result_2), .out_4(GE));  // open: out_6
  Multiplexer #(.select(1), .width(32), .disabled("Z"), .enable("false")) multiplexer_5 (
    .in0(alu_1_result), .in1(alu_1_result_2), .out(aluresult), .sel(comparator_2_eq));
  Adder #(.width(32)) adder_3 (.a(PC), .b(32'h4), .out(adder_3_out));  // open: cin, cout
  Comparator #(.width(32), .mode("twosComplement")) comparator_1 (
    .a(32'h22), .b(regifile_1_r1), .eq(flag));  // open: gt, lt
  Multiplexer #(.select(1), .width(32), .disabled("Z"), .enable("false")) multiplexer_6 (
    .in0(adder_3_out), .in1(adder_1_out), .out(multiplexer_6_out), .sel(tunnel1));
  Comparator #(.width(4), .mode("twosComplement")) comparator_2 (
    .a(\单周期硬布线控制器_1_alu_op ), .b(4'b0100), .eq(comparator_2_eq));  // open: gt, lt
  Multiplexer #(.select(1), .width(32), .disabled("Z"), .enable("false")) multiplexer_7 (
    .in0(multiplexer_6_out), .in1(adder_2_out), .out(multiplexer_7_out), .sel(JAL));
  assign and_3_out = aluresult & 32'hfffffffe;  // AND_Gate and_3, 32 bits wide
  and and_4 (and_4_out, GE, BGEU);
  not not_5 (not_5_out, MemWrite);
  Multiplexer #(.select(1), .width(32), .disabled("Z"), .enable("false")) multiplexer_8 (
    .in0(multiplexer_7_out), .in1(and_3_out), .out(multiplexer_8_out), .sel(JALR));
  or or_6 (tunnel1, and_1_out, and_2_out, and_4_out);
  RAM #(.addrWidth(10), .dataWidth(32), .bus("separate"), .Select("high")) ram_1 (
    .addr(aluresult[11:2]), .din(MDin), .data(ram_1_data), .str(MemWrite), .clk(CLK), .ld(not_5_out));  // open: sel, clr
  Multiplexer #(.select(1), .width(32), .disabled("Z"), .enable("false")) multiplexer_9 (
    .in0({32{1'b0}}), .in1(MDin), .out(multiplexer_9_out), .sel(and_5_out));
  and and_5 (and_5_out, ecall, flag);
  not not_6 (not_6_out, flag);
  assign bit_extender_4_out = {{16{1'b0}}, ram_1_data[15:0]};  // Bit_Extender bit_extender_4
  assign bit_extender_5_out = {{16{1'b0}}, ram_1_data[31:16]};  // Bit_Extender bit_extender_5
  Register #(.width(32), .trigger("rising"), .Select("low")) register_1 (
    .D(multiplexer_9_out), .en(and_5_out), .Q(LedData), .clk(CLK), .clr(RST));
  and and_6 (halt, ecall, not_6_out);
  D_Flip_Flop #(.trigger("high"), .Pre_Clr_Positions("LEGACY"), .NegatePresetClear("false"), .enable("true"), .NewFFLayout("false")) d_ff_1 (.Q(d_ff_1_q));  // open: clk, D, Qn, preset, en, reset
  // Probe on 13'hc
  Comparator #(.width(3), .mode("twosComplement")) comparator_3 (
    .a(IR[14:12]), .b(3'b101), .eq(comparator_3_eq));  // open: gt, lt
  not not_7 (not_7_out, comparator_3_eq);
  Multiplexer #(.select(1), .width(32), .disabled("Z"), .enable("false")) multiplexer_10 (
    .in0(bit_extender_4_out), .in1(bit_extender_5_out), .out(multiplexer_10_out), .sel(aluresult[1]));
  Comparator #(.width(13), .mode("twosComplement")) comparator_4 (
    .a(CNT_num), .b(13'hc), .eq(comparator_4_eq), .lt(comparator_4_lt));  // open: gt
  Clock #(.highDuration(1), .lowDuration(1)) clock_1 (.out(clock_1_out));
  Multiplexer #(.select(1), .width(32), .disabled("Z"), .enable("false")) multiplexer_11 (
    .in0(multiplexer_10_out), .in1(ram_1_data), .out(multiplexer_11_out), .sel(not_7_out));
  Adder #(.width(32)) adder_4 (.a(PC), .b(32'h4), .out(adder_4_out));  // open: cin, cout
  Counter #(.width(13), .max('h1fff), .ongoal("stay"), .trigger("rising"), .behavior("old")) counter_2 (
    .count(comparator_4_lt), .Q(CNT_num), .clk(clock_1_out));  // open: load, D, carry, clr, preset
  Multiplexer #(.select(1), .width(32), .disabled("Z"), .enable("false")) multiplexer_12 (
    .in0(aluresult), .in1(multiplexer_11_out), .out(multiplexer_12_out), .sel(MemToReg));
  or or_7 (or_7_out, JALR, JAL);
  nand nand_1 (nand_1_out, d_ff_1_q, comparator_4_eq);
  Multiplexer #(.select(1), .width(32), .disabled("Z"), .enable("false")) multiplexer_13 (
    .in0(multiplexer_12_out), .in1(adder_4_out), .out(RDin), .sel(or_7_out));
  assign CLK = nand_1_out ? clock_1_out : 1'bz;  // Controlled_Buffer controlled_buffer_1
  Pull_Resistor #(.pull(1)) pull_resistor_1 (.node(CLK));

  // Notes on the sheet:
  //   中断源
  //   中断等待指示
  //   数码管输出应该用寄存器锁存，否则显示数据只能一闪而过
  //   数码管输出
  //   指令探针
  //   指令存储器
  //   指令字
  //   contents of rom_1 (hex, n*v repeats v):
  //   100493 100006f 100493 200913 300993 100006f 100493 200913 300993 100006f 100493 200913 300993
  //   100006f 100493 200913 300993 3bc000ef 100413 100493 1f49493 900533 2200893 73 24d493 48463 fedff06f
  //   900533 2200893 73 100493 249493 900533 2200893 73 48463 fedff06f 100493 1f49493 900533 2200893 73
  //   4034d493 900533 2200893 73 4044d493 900533 2200893 73 4044d493 900533 2200893 73 4044d493 900533
  //   2200893 73 4044d493 900533 2200893 73 4044d493 900533 2200893 73 4044d493 900533 2200893 73 4044d493
  //   900533 2200893 73 100413 1f41993 41f9d993 433 c00913 300b13 140413 f47413 800293 100313 499993
  //   89e9b3 1300533 2200893 73 406282b3 fe0294e3 140413 f00f93 1f47433 1c41413 800293 100313 49d993
  //   89e9b3 1300533 2200893 73 406282b3 fe0294e3 1c45413 406b0b33 b0463 f95ff06f 2b3 fff2c293 829293
  //   ff2e293 500533 2200893 73 fff00413 493 84a023 140413 448493 84a023 140413 448493 84a023 140413
  //   448493 84a023 140413 448493 84a023 140413 448493 84a023 140413 448493 84a023 140413 448493 84a023
  //   140413 448493 84a023 140413 448493 84a023 140413 448493 84a023 140413 448493 84a023 140413 448493
  //   84a023 140413 448493 84a023 140413 448493 84a023 140413 448493 84a023 140413 448493 140413 433
  //   3c00493 42983 4aa03 149a2b3 28663 134a023 1442023 ffc48493 fe9412e3 800533 2200893 73 440413 3c00493
  //   fc9416e3 a00893 73 200293 1100493 849493 1148493 900533 2200893 73 2000e13 25484b3 900533 2200893 73
  //   fffe0e13 fe0e16e3 a00893 73 8800493 849493 4848493 8700913 891913 5490913 2997933 1091913 11096913
  //   1200533 2200893 73 a00893 73 313 1000e13 8400493 849493 8348493 400913 891913 490913 849493 8248493
  //   849493 8148493 891913 490913 891913 490913 932023 12484b3 430313 fffe0e13 fe0e18e3 2000e13 313 35483
  //   900533 2200893 73 230313 fffe0e13 fe0e14e3 a00893 73 f00493 100913 409909b3 900533 2200893 73
  //   fff48493 ff29f6e3 a00893 73 413 140413 800533 2200893 73 240413 800533 2200893 73 340413 800533
  //   2200893 73 440413 800533 2200893 73 540413 800533 2200893 73 640413 800533 2200893 73 740413 800533
  //   2200893 73 840413 800533 2200893 2200893 73 8067
  //   JAL
  //   JALR
  //   URET
  //   Beq
  //   Bne
  //   MemToReg
  //   MemWrite
  //   AluOP
  //   AluSrcB
  //   RegWrite
  //   为方便自动评测，需要输出PC，IR，寄存器堆写如数据RDin
  //   RAM写使能MemWrite、RAM写入数据MDin等信号
  //   数据存储器
  //   控制位
  //   暂停节拍，不能为0
  //   戳工具置1进入计数暂停模式，ctrl+k时钟自动运行到对应节拍暂停
  //   ctrl+k关闭时钟连续运行，将控制位置零，进入单步调试模式调试
  //   用这个时钟源需要去掉电路中的其他时钟源
  //   可计数暂停的时钟源
endmodule

// 运算器控制器
module \运算控制器自动生成  (
  input  OP2,
  input  OP3,
  input  OP4,
  input  OP5,
  input  OP6,
  input  F12,
  input  F13,
  input  F14,
  input  F25,
  input  F30,
  output S0,
  output S1,
  output S2,
  output S3
);

  wire and_1_out, and_2_out, and_3_out, and_4_out, and_5_out, and_6_out, and_7_out, and_8_out, and_9_out,
       and_10_out, and_11_out, and_12_out, and_13_out, and_14_out, and_15_out, and_16_out, and_17_out,
       and_18_out, and_19_out, and_20_out, and_21_out, and_22_out, and_23_out, and_24_out, and_25_out,
       and_26_out, and_27_out, and_28_out, and_29_out, and_30_out, and_31_out, and_32_out, and_33_out,
       and_34_out, and_35_out, and_36_out, and_37_out, not_1_out, not_2_out, not_3_out, not_4_out, not_5_out,
       not_6_out, not_7_out, not_8_out, not_9_out, not_10_out, not_11_out, not_12_out, not_13_out,
       not_14_out, not_15_out, not_16_out, not_17_out, not_18_out, not_19_out, not_20_out, not_21_out,
       not_22_out, not_23_out, not_24_out, not_25_out, not_26_out, not_27_out, not_28_out, not_29_out,
       not_30_out, not_31_out, not_32_out, not_33_out, not_34_out, not_35_out, not_36_out, not_37_out,
       not_38_out, not_39_out, not_40_out, not_41_out, not_42_out, not_43_out, not_44_out, not_45_out,
       not_46_out, not_47_out, not_48_out, not_49_out, not_50_out, not_51_out, not_52_out, not_53_out,
       not_54_out, not_55_out, not_56_out, not_57_out, not_58_out, not_59_out, not_60_out, not_61_out,
       not_62_out, not_63_out, not_64_out, not_65_out, not_66_out, not_67_out, not_68_out, not_69_out,
       not_70_out, not_71_out, not_72_out, not_73_out, not_74_out, not_75_out, not_76_out, not_77_out,
       not_78_out, not_79_out, not_80_out, not_81_out, not_82_out, not_83_out, not_84_out, not_85_out,
       not_86_out, not_87_out, not_88_out, not_89_out, not_90_out, not_91_out, not_92_out, not_93_out,
       not_94_out, not_95_out, not_96_out, not_97_out, not_98_out, not_99_out, not_100_out, not_101_out,
       not_102_out, not_103_out, not_104_out, not_105_out, not_106_out, not_107_out, not_108_out,
       not_109_out, not_110_out, not_111_out, not_112_out, not_113_out, not_114_out, not_115_out,
       not_116_out, not_117_out, not_118_out, not_119_out, not_120_out, not_121_out, not_122_out,
       not_123_out, not_124_out, not_125_out, not_126_out, not_127_out, not_128_out, not_129_out,
       not_130_out, not_131_out, not_132_out, not_133_out, not_134_out, not_135_out, not_136_out,
       not_137_out, not_138_out, not_139_out, not_140_out, not_141_out, not_142_out, not_143_out,
       not_144_out, not_145_out, not_146_out, not_147_out, not_148_out, not_149_out, not_150_out,
       not_151_out, not_152_out, not_153_out, not_154_out, not_155_out, not_156_out, not_157_out,
       not_158_out, not_159_out, not_160_out, not_161_out, not_162_out, not_163_out, not_164_out,
       not_165_out, not_166_out, not_167_out, not_168_out, not_169_out, not_170_out, not_171_out,
       not_172_out, not_173_out, not_174_out, not_175_out, not_176_out, not_177_out, not_178_out,
       not_179_out, not_180_out, not_181_out, not_182_out, not_183_out, not_184_out, not_185_out,
       not_186_out, not_187_out, not_188_out, not_189_out, not_190_out, not_191_out, not_192_out,
       not_193_out, not_194_out, not_195_out, not_196_out, not_197_out, not_198_out, not_199_out,
       not_200_out, not_201_out, not_202_out, not_203_out, not_204_out;

  not not_1 (not_1_out, F30);
  not not_2 (not_2_out, F25);
  not not_3 (not_3_out, F14);
  not not_4 (not_4_out, F13);
  not not_5 (not_5_out, F12);
  not not_6 (not_6_out, OP6);
  not not_7 (not_7_out, OP3);
  not not_8 (not_8_out, OP2);
  not not_9 (not_9_out, F30);
  not not_10 (not_10_out, F25);
  not not_11 (not_11_out, OP6);
  not not_12 (not_12_out, OP3);
  not not_13 (not_13_out, OP2);
  not not_14 (not_14_out, F30);
  not not_15 (not_15_out, F25);
  not not_16 (not_16_out, F14);
  not not_17 (not_17_out, F12);
  not not_18 (not_18_out, OP6);
  not not_19 (not_19_out, OP3);
  not not_20 (not_20_out, OP2);
  not not_21 (not_21_out, F14);
  not not_22 (not_22_out, F13);
  not not_23 (not_23_out, F12);
  not not_24 (not_24_out, OP6);
  not not_25 (not_25_out, OP5);
  not not_26 (not_26_out, OP3);
  not not_27 (not_27_out, OP2);
  not not_28 (not_28_out, OP6);
  not not_29 (not_29_out, OP5);
  not not_30 (not_30_out, OP3);
  not not_31 (not_31_out, OP2);
  not not_32 (not_32_out, F25);
  not not_33 (not_33_out, F13);
  not not_34 (not_34_out, OP6);
  not not_35 (not_35_out, OP5);
  not not_36 (not_36_out, OP3);
  not not_37 (not_37_out, OP2);
  not not_38 (not_38_out, F14);
  not not_39 (not_39_out, F12);
  not not_40 (not_40_out, OP6);
  not not_41 (not_41_out, OP5);
  not not_42 (not_42_out, OP3);
  not not_43 (not_43_out, OP2);
  not not_44 (not_44_out, F14);
  not not_45 (not_45_out, F12);
  not not_46 (not_46_out, OP6);
  not not_47 (not_47_out, OP5);
  not not_48 (not_48_out, OP4);
  not not_49 (not_49_out, OP3);
  not not_50 (not_50_out, OP2);
  not not_51 (not_51_out, F14);
  not not_52 (not_52_out, F12);
  not not_53 (not_53_out, OP6);
  not not_54 (not_54_out, OP4);
  not not_55 (not_55_out, OP3);
  not not_56 (not_56_out, OP2);
  not not_57 (not_57_out, F13);
  not not_58 (not_58_out, F12);
  not not_59 (not_59_out, OP6);
  not not_60 (not_60_out, OP5);
  not not_61 (not_61_out, OP3);
  not not_62 (not_62_out, OP2);
  not not_63 (not_63_out, OP3);
  not not_64 (not_64_out, OP2);
  not not_65 (not_65_out, F30);
  not not_66 (not_66_out, F14);
  not not_67 (not_67_out, F13);
  not not_68 (not_68_out, F12);
  not not_69 (not_69_out, OP6);
  not not_70 (not_70_out, OP3);
  not not_71 (not_71_out, OP2);
  not not_72 (not_72_out, F13);
  not not_73 (not_73_out, OP6);
  not not_74 (not_74_out, OP5);
  not not_75 (not_75_out, OP4);
  not not_76 (not_76_out, OP3);
  not not_77 (not_77_out, OP2);
  not not_78 (not_78_out, OP2);
  not not_79 (not_79_out, OP3);
  not not_80 (not_80_out, OP5);
  not not_81 (not_81_out, OP6);
  not not_82 (not_82_out, F12);
  not not_83 (not_83_out, F14);
  not not_84 (not_84_out, OP2);
  not not_85 (not_85_out, OP3);
  not not_86 (not_86_out, OP6);
  not not_87 (not_87_out, F12);
  not not_88 (not_88_out, F14);
  not not_89 (not_89_out, F25);
  not not_90 (not_90_out, F30);
  not not_91 (not_91_out, OP2);
  not not_92 (not_92_out, OP3);
  not not_93 (not_93_out, OP5);
  not not_94 (not_94_out, OP6);
  not not_95 (not_95_out, F25);
  not not_96 (not_96_out, F30);
  not not_97 (not_97_out, OP2);
  not not_98 (not_98_out, OP3);
  not not_99 (not_99_out, OP5);
  not not_100 (not_100_out, OP6);
  not not_101 (not_101_out, OP2);
  not not_102 (not_102_out, OP3);
  not not_103 (not_103_out, OP6);
  not not_104 (not_104_out, F25);
  not not_105 (not_105_out, F30);
  not not_106 (not_106_out, OP2);
  not not_107 (not_107_out, OP3);
  not not_108 (not_108_out, OP6);
  not not_109 (not_109_out, F12);
  not not_110 (not_110_out, F13);
  not not_111 (not_111_out, F14);
  not not_112 (not_112_out, F25);
  not not_113 (not_113_out, OP2);
  not not_114 (not_114_out, OP3);
  not not_115 (not_115_out, OP6);
  not not_116 (not_116_out, F12);
  not not_117 (not_117_out, F13);
  not not_118 (not_118_out, F14);
  not not_119 (not_119_out, F30);
  not not_120 (not_120_out, OP2);
  not not_121 (not_121_out, OP3);
  not not_122 (not_122_out, OP2);
  not not_123 (not_123_out, OP3);
  not not_124 (not_124_out, OP4);
  not not_125 (not_125_out, OP6);
  not not_126 (not_126_out, F12);
  not not_127 (not_127_out, F14);
  not not_128 (not_128_out, OP2);
  not not_129 (not_129_out, OP3);
  not not_130 (not_130_out, OP4);
  not not_131 (not_131_out, OP5);
  not not_132 (not_132_out, OP6);
  not not_133 (not_133_out, F13);
  not not_134 (not_134_out, OP2);
  not not_135 (not_135_out, OP3);
  not not_136 (not_136_out, OP2);
  not not_137 (not_137_out, OP3);
  not not_138 (not_138_out, OP5);
  not not_139 (not_139_out, OP6);
  not not_140 (not_140_out, F12);
  not not_141 (not_141_out, F13);
  not not_142 (not_142_out, F14);
  not not_143 (not_143_out, OP2);
  not not_144 (not_144_out, OP3);
  not not_145 (not_145_out, OP6);
  not not_146 (not_146_out, F12);
  not not_147 (not_147_out, F13);
  not not_148 (not_148_out, F14);
  not not_149 (not_149_out, F25);
  not not_150 (not_150_out, OP2);
  not not_151 (not_151_out, OP3);
  not not_152 (not_152_out, OP5);
  not not_153 (not_153_out, OP6);
  not not_154 (not_154_out, OP2);
  not not_155 (not_155_out, OP3);
  not not_156 (not_156_out, OP6);
  not not_157 (not_157_out, F30);
  not not_158 (not_158_out, OP2);
  not not_159 (not_159_out, OP3);
  not not_160 (not_160_out, OP6);
  not not_161 (not_161_out, F25);
  not not_162 (not_162_out, F30);
  not not_163 (not_163_out, F30);
  not not_164 (not_164_out, F25);
  not not_165 (not_165_out, F12);
  not not_166 (not_166_out, OP6);
  not not_167 (not_167_out, OP3);
  not not_168 (not_168_out, OP2);
  not not_169 (not_169_out, F30);
  not not_170 (not_170_out, F25);
  not not_171 (not_171_out, F14);
  not not_172 (not_172_out, F12);
  not not_173 (not_173_out, OP6);
  not not_174 (not_174_out, OP3);
  not not_175 (not_175_out, OP2);
  not not_176 (not_176_out, F30);
  not not_177 (not_177_out, F25);
  not not_178 (not_178_out, F14);
  not not_179 (not_179_out, OP6);
  not not_180 (not_180_out, OP3);
  not not_181 (not_181_out, OP2);
  not not_182 (not_182_out, F12);
  not not_183 (not_183_out, OP6);
  not not_184 (not_184_out, OP5);
  not not_185 (not_185_out, OP3);
  not not_186 (not_186_out, OP2);
  not not_187 (not_187_out, F14);
  not not_188 (not_188_out, F12);
  not not_189 (not_189_out, OP6);
  not not_190 (not_190_out, OP5);
  not not_191 (not_191_out, OP3);
  not not_192 (not_192_out, OP2);
  not not_193 (not_193_out, F13);
  not not_194 (not_194_out, F12);
  not not_195 (not_195_out, OP6);
  not not_196 (not_196_out, OP5);
  not not_197 (not_197_out, OP3);
  not not_198 (not_198_out, OP2);
  not not_199 (not_199_out, F12);
  not not_200 (not_200_out, OP3);
  not not_201 (not_201_out, OP2);
  not not_202 (not_202_out, OP4);
  not not_203 (not_203_out, OP3);
  not not_204 (not_204_out, OP2);
  and and_1 (and_1_out, not_1_out, not_2_out, not_3_out, not_4_out, not_5_out, not_6_out, OP5, OP4, not_7_out, not_8_out);
  and and_2 (and_2_out, not_9_out, not_10_out, F14, F13, F12, not_11_out, OP5, OP4, not_12_out, not_13_out);
  and and_3 (and_3_out, not_14_out, not_15_out, not_16_out, F13, not_17_out, not_18_out, OP5, OP4, not_19_out, not_20_out);
  and and_4 (and_4_out, not_21_out, not_22_out, not_23_out, not_24_out, not_25_out, OP4, not_26_out, not_27_out);
  and and_5 (and_5_out, F14, F13, F12, not_28_out, not_29_out, OP4, not_30_out, not_31_out);
  and and_6 (and_6_out, F30, not_32_out, F14, not_33_out, F12, not_34_out, not_35_out, OP4, not_36_out, not_37_out);
  and and_7 (and_7_out, not_38_out, F13, not_39_out, not_40_out, not_41_out, OP4, not_42_out, not_43_out);
  and and_8 (and_8_out, not_44_out, F13, not_45_out, not_46_out, not_47_out, not_48_out, not_49_out, not_50_out);
  and and_9 (and_9_out, not_51_out, F13, not_52_out, not_53_out, OP5, not_54_out, not_55_out, not_56_out);
  and and_10 (and_10_out, F14, not_57_out, not_58_out, not_59_out, not_60_out, OP4, not_61_out, not_62_out);
  and and_11 (and_11_out, F14, F13, F12, OP6, OP5, OP4, not_63_out, not_64_out);
  and and_12 (and_12_out, not_65_out, F25, not_66_out, not_67_out, not_68_out, not_69_out, OP5, OP4, not_70_out, not_71_out);
  and and_13 (and_13_out, F14, not_72_out, F12, not_73_out, not_74_out, not_75_out, not_76_out, not_77_out);
  and and_14 (and_14_out, not_78_out, not_79_out, OP4, not_80_out, not_81_out, not_82_out, F13, not_83_out);
  and and_15 (and_15_out, not_84_out, not_85_out, OP4, not_86_out, not_87_out, F13, not_88_out, not_89_out, not_90_out);
  and and_16 (and_16_out, not_91_out, not_92_out, OP4, not_93_out, not_94_out, F12, F14, not_95_out, not_96_out);
  and and_17 (and_17_out, not_97_out, not_98_out, OP4, not_99_out, not_100_out, F12, F13, F14);
  and and_18 (and_18_out, not_101_out, not_102_out, OP4, not_103_out, F12, F13, F14, not_104_out, not_105_out);
  and and_19 (and_19_out, not_106_out, not_107_out, OP4, OP5, not_108_out, not_109_out, not_110_out, not_111_out, not_112_out, F30);
  and and_20 (and_20_out, not_113_out, not_114_out, OP4, OP5, not_115_out, not_116_out, not_117_out, not_118_out, F25, not_119_out);
  and and_21 (and_21_out, not_120_out, not_121_out, OP4, OP5, OP6, F12, F13, F14);
  and and_22 (and_22_out, not_122_out, not_123_out, not_124_out, not_125_out, not_126_out, F13, not_127_out);
  and and_23 (and_23_out, not_128_out, not_129_out, not_130_out, not_131_out, not_132_out, F12, not_133_out, F14);
  and and_24 (and_24_out, not_134_out, not_135_out, OP5, OP6, F12, F13, F14);
  and and_25 (and_25_out, not_136_out, not_137_out, OP4, not_138_out, not_139_out, not_140_out, not_141_out, not_142_out);
  and and_26 (and_26_out, not_143_out, not_144_out, OP4, not_145_out, not_146_out, not_147_out, not_148_out, not_149_out);
  and and_27 (and_27_out, not_150_out, not_151_out, OP4, not_152_out, not_153_out, F12, F13, F14);
  and and_28 (and_28_out, not_154_out, not_155_out, OP4, not_156_out, F12, F13, F14, not_157_out);
  and and_29 (and_29_out, not_158_out, not_159_out, OP4, OP5, not_160_out, F12, F13, not_161_out, not_162_out);
  and and_30 (and_30_out, not_163_out, not_164_out, F14, F13, not_165_out, not_166_out, OP5, OP4, not_167_out, not_168_out);
  and and_31 (and_31_out, not_169_out, not_170_out, not_171_out, F13, not_172_out, not_173_out, OP5, OP4, not_174_out, not_175_out);
  and and_32 (and_32_out, not_176_out, not_177_out, not_178_out, F13, F12, not_179_out, OP5, OP4, not_180_out, not_181_out);
  and and_33 (and_33_out, F14, F13, not_182_out, not_183_out, not_184_out, OP4, not_185_out, not_186_out);
  and and_34 (and_34_out, not_187_out, F13, not_188_out, not_189_out, not_190_out, OP4, not_191_out, not_192_out);
  and and_35 (and_35_out, F14, not_193_out, not_194_out, not_195_out, not_196_out, OP4, not_197_out, not_198_out);
  and and_36 (and_36_out, F14, F13, not_199_out, OP6, OP5, OP4, not_200_out, not_201_out);
  and and_37 (and_37_out, F14, F13, F12, OP6, OP5, not_202_out, not_203_out, not_204_out);
  or or_1 (S0, and_1_out, and_2_out, and_3_out, and_4_out, and_5_out, and_6_out, and_7_out, and_8_out, and_9_out, and_10_out, and_11_out, and_12_out, and_13_out);
  or or_2 (S1, and_14_out, and_15_out, and_16_out, and_17_out, and_18_out, and_19_out, and_20_out, and_21_out);
  or or_3 (S2, and_22_out, and_23_out, and_24_out, and_25_out, and_26_out, and_27_out, and_28_out, and_29_out);
  or or_4 (S3, and_30_out, and_31_out, and_32_out, and_33_out, and_34_out, and_35_out, and_36_out, and_37_out);
endmodule

// 控制信号生成
module \控制信号自动生成  (
  input  OP2,
  input  OP3,
  input  OP4,
  input  OP5,
  input  OP6,
  input  F12,
  input  F13,
  input  F14,
  input  F25,
  input  F30,
  output MemToReg,
  output MemWrite,
  output ALU_SRC,
  output bgeu,
  output RegWrite,
  output ecall,
  output S_Type,
  output BEQ,
  output BNE,
  output JALR,
  output JAL
);

  wire and_1_out, and_2_out, and_4_out, and_5_out, and_6_out, and_7_out, and_8_out, and_9_out, and_10_out,
       and_11_out, and_12_out, and_13_out, and_14_out, and_15_out, and_16_out, and_17_out, and_19_out,
       and_20_out, and_21_out, and_22_out, and_23_out, and_24_out, and_25_out, and_26_out, and_27_out,
       and_28_out, and_29_out, and_30_out, and_31_out, and_32_out, and_33_out, and_34_out, and_35_out,
       and_36_out, and_37_out, and_38_out, and_39_out, and_40_out, not_1_out, not_2_out, not_3_out,
       not_4_out, not_5_out, not_6_out, not_7_out, not_8_out, not_9_out, not_10_out, not_11_out, not_12_out,
       not_13_out, not_14_out, not_15_out, not_16_out, not_17_out, not_18_out, not_19_out, not_20_out,
       not_21_out, not_22_out, not_23_out, not_24_out, not_25_out, not_26_out, not_27_out, not_28_out,
       not_29_out, not_30_out, not_31_out, not_32_out, not_33_out, not_34_out, not_35_out, not_36_out,
       not_37_out, not_38_out, not_39_out, not_40_out, not_41_out, not_42_out, not_43_out, not_44_out,
       not_45_out, not_46_out, not_47_out, not_48_out, not_49_out, not_50_out, not_51_out, not_52_out,
       not_53_out, not_54_out, not_55_out, not_56_out, not_57_out, not_58_out, not_59_out, not_60_out,
       not_61_out, not_62_out, not_63_out, not_64_out, not_65_out, not_66_out, not_67_out, not_68_out,
       not_69_out, not_70_out, not_71_out, not_72_out, not_73_out, not_74_out, not_75_out, not_76_out,
       not_77_out, not_78_out, not_79_out, not_80_out, not_81_out, not_82_out, not_83_out, not_84_out,
       not_85_out, not_86_out, not_87_out, not_88_out, not_89_out, not_90_out, not_91_out, not_92_out,
       not_93_out, not_94_out, not_95_out, not_96_out, not_97_out, not_98_out, not_99_out, not_100_out,
       not_101_out, not_102_out, not_103_out, not_104_out, not_105_out, not_106_out, not_107_out,
       not_108_out, not_109_out, not_110_out, not_111_out, not_112_out, not_113_out, not_114_out,
       not_115_out, not_116_out, not_117_out, not_118_out, not_119_out, not_120_out, not_121_out,
       not_122_out, not_123_out, not_124_out, not_125_out, not_126_out, not_127_out, not_128_out,
       not_129_out, not_130_out, not_131_out, not_132_out, not_133_out, not_134_out, not_135_out,
       not_136_out, not_137_out, not_138_out, not_139_out, not_140_out, not_141_out, not_142_out,
       not_143_out, not_144_out, not_145_out, not_146_out, not_147_out, not_148_out, not_149_out,
       not_150_out, not_151_out, not_152_out, not_153_out, not_154_out, not_155_out, not_156_out,
       not_157_out, not_158_out, not_159_out, not_160_out, not_161_out, not_162_out, not_163_out,
       not_164_out, not_165_out, not_166_out, not_167_out, not_168_out, not_169_out, not_170_out,
       not_171_out, not_172_out, not_173_out, not_174_out, not_175_out, not_176_out, not_177_out,
       not_178_out, not_179_out, not_180_out, not_181_out, not_182_out, not_183_out, not_184_out,
       not_185_out, not_186_out, not_187_out, not_188_out, not_189_out, not_190_out, not_191_out,
       not_192_out, not_193_out, not_194_out, not_195_out, not_196_out, not_197_out, not_198_out,
       not_199_out, not_200_out, not_201_out, not_202_out, not_203_out, not_204_out, not_205_out,
       not_206_out, not_207_out, not_208_out, not_209_out, not_210_out, not_211_out, not_212_out,
       not_213_out, not_214_out, not_215_out, not_216_out, not_217_out, not_218_out, not_219_out,
       not_220_out, not_221_out, not_222_out, not_223_out, not_224_out, not_225_out, not_226_out,
       not_227_out, not_228_out, not_229_out, not_230_out, not_231_out, not_232_out, not_233_out,
       not_234_out, not_235_out, not_236_out, not_237_out, not_238_out, not_239_out, not_240_out,
       not_241_out, not_242_out, not_243_out, not_244_out, not_245_out, not_246_out, not_247_out,
       not_248_out, not_249_out, not_250_out, not_251_out, not_252_out, not_253_out, not_254_out, not_255_out;

  not not_1 (not_1_out, F14);
  not not_2 (not_2_out, F12);
  not not_3 (not_3_out, OP6);
  not not_4 (not_4_out, OP5);
  not not_5 (not_5_out, OP4);
  not not_6 (not_6_out, OP3);
  not not_7 (not_7_out, OP2);
  not not_8 (not_8_out, F13);
  not not_9 (not_9_out, OP6);
  not not_10 (not_10_out, OP5);
  not not_11 (not_11_out, OP4);
  not not_12 (not_12_out, OP3);
  not not_13 (not_13_out, OP2);
  not not_14 (not_14_out, F14);
  not not_15 (not_15_out, F12);
  not not_16 (not_16_out, OP6);
  not not_17 (not_17_out, OP4);
  not not_18 (not_18_out, OP3);
  not not_19 (not_19_out, OP2);
  not not_20 (not_20_out, F14);
  not not_21 (not_21_out, F13);
  not not_22 (not_22_out, F12);
  not not_23 (not_23_out, OP6);
  not not_24 (not_24_out, OP5);
  not not_25 (not_25_out, OP3);
  not not_26 (not_26_out, OP2);
  not not_27 (not_27_out, OP6);
  not not_28 (not_28_out, OP5);
  not not_29 (not_29_out, OP3);
  not not_30 (not_30_out, OP2);
  not not_31 (not_31_out, F12);
  not not_32 (not_32_out, OP6);
  not not_33 (not_33_out, OP5);
  not not_34 (not_34_out, OP3);
  not not_35 (not_35_out, OP2);
  not not_36 (not_36_out, F30);
  not not_37 (not_37_out, F25);
  not not_38 (not_38_out, F14);
  not not_39 (not_39_out, F13);
  not not_40 (not_40_out, OP6);
  not not_41 (not_41_out, OP5);
  not not_42 (not_42_out, OP3);
  not not_43 (not_43_out, OP2);
  not not_44 (not_44_out, F25);
  not not_45 (not_45_out, F13);
  not not_46 (not_46_out, OP6);
  not not_47 (not_47_out, OP5);
  not not_48 (not_48_out, OP3);
  not not_49 (not_49_out, OP2);
  not not_50 (not_50_out, F30);
  not not_51 (not_51_out, F25);
  not not_52 (not_52_out, F13);
  not not_53 (not_53_out, OP6);
  not not_54 (not_54_out, OP5);
  not not_55 (not_55_out, OP3);
  not not_56 (not_56_out, OP2);
  not not_57 (not_57_out, F14);
  not not_58 (not_58_out, F12);
  not not_59 (not_59_out, OP6);
  not not_60 (not_60_out, OP5);
  not not_61 (not_61_out, OP3);
  not not_62 (not_62_out, OP2);
  not not_63 (not_63_out, F14);
  not not_64 (not_64_out, F12);
  not not_65 (not_65_out, OP6);
  not not_66 (not_66_out, OP5);
  not not_67 (not_67_out, OP4);
  not not_68 (not_68_out, OP3);
  not not_69 (not_69_out, OP2);
  not not_70 (not_70_out, F14);
  not not_71 (not_71_out, F12);
  not not_72 (not_72_out, OP6);
  not not_73 (not_73_out, OP4);
  not not_74 (not_74_out, OP3);
  not not_75 (not_75_out, OP2);
  not not_76 (not_76_out, F13);
  not not_77 (not_77_out, F12);
  not not_78 (not_78_out, OP6);
  not not_79 (not_79_out, OP5);
  not not_80 (not_80_out, OP3);
  not not_81 (not_81_out, OP2);
  not not_82 (not_82_out, F14);
  not not_83 (not_83_out, F13);
  not not_84 (not_84_out, F12);
  not not_85 (not_85_out, OP4);
  not not_86 (not_86_out, OP3);
  not not_87 (not_87_out, F12);
  not not_88 (not_88_out, OP3);
  not not_89 (not_89_out, OP2);
  not not_90 (not_90_out, OP3);
  not not_91 (not_91_out, OP2);
  not not_92 (not_92_out, F13);
  not not_93 (not_93_out, OP6);
  not not_94 (not_94_out, OP5);
  not not_95 (not_95_out, OP4);
  not not_96 (not_96_out, OP3);
  not not_97 (not_97_out, OP2);
  not not_98 (not_98_out, OP4);
  not not_99 (not_99_out, OP3);
  not not_100 (not_100_out, OP2);
  not not_101 (not_101_out, F30);
  not not_102 (not_102_out, F25);
  not not_103 (not_103_out, F14);
  not not_104 (not_104_out, F13);
  not not_105 (not_105_out, F12);
  not not_106 (not_106_out, OP6);
  not not_107 (not_107_out, OP3);
  not not_108 (not_108_out, OP2);
  not not_109 (not_109_out, F25);
  not not_110 (not_110_out, F14);
  not not_111 (not_111_out, F13);
  not not_112 (not_112_out, F12);
  not not_113 (not_113_out, OP6);
  not not_114 (not_114_out, OP3);
  not not_115 (not_115_out, OP2);
  not not_116 (not_116_out, F30);
  not not_117 (not_117_out, F25);
  not not_118 (not_118_out, OP6);
  not not_119 (not_119_out, OP3);
  not not_120 (not_120_out, OP2);
  not not_121 (not_121_out, F30);
  not not_122 (not_122_out, F25);
  not not_123 (not_123_out, F12);
  not not_124 (not_124_out, OP6);
  not not_125 (not_125_out, OP3);
  not not_126 (not_126_out, OP2);
  not not_127 (not_127_out, F30);
  not not_128 (not_128_out, F25);
  not not_129 (not_129_out, F14);
  not not_130 (not_130_out, F12);
  not not_131 (not_131_out, OP6);
  not not_132 (not_132_out, OP3);
  not not_133 (not_133_out, OP2);
  not not_134 (not_134_out, F30);
  not not_135 (not_135_out, F25);
  not not_136 (not_136_out, F14);
  not not_137 (not_137_out, OP6);
  not not_138 (not_138_out, OP3);
  not not_139 (not_139_out, OP2);
  not not_140 (not_140_out, F14);
  not not_141 (not_141_out, F13);
  not not_142 (not_142_out, F12);
  not not_143 (not_143_out, OP6);
  not not_144 (not_144_out, OP5);
  not not_145 (not_145_out, OP3);
  not not_146 (not_146_out, OP2);
  not not_147 (not_147_out, OP6);
  not not_148 (not_148_out, OP5);
  not not_149 (not_149_out, OP3);
  not not_150 (not_150_out, OP2);
  not not_151 (not_151_out, F12);
  not not_152 (not_152_out, OP6);
  not not_153 (not_153_out, OP5);
  not not_154 (not_154_out, OP3);
  not not_155 (not_155_out, OP2);
  not not_156 (not_156_out, F30);
  not not_157 (not_157_out, F25);
  not not_158 (not_158_out, F14);
  not not_159 (not_159_out, F13);
  not not_160 (not_160_out, OP6);
  not not_161 (not_161_out, OP5);
  not not_162 (not_162_out, OP3);
  not not_163 (not_163_out, OP2);
  not not_164 (not_164_out, F25);
  not not_165 (not_165_out, F13);
  not not_166 (not_166_out, OP6);
  not not_167 (not_167_out, OP5);
  not not_168 (not_168_out, OP3);
  not not_169 (not_169_out, OP2);
  not not_170 (not_170_out, F30);
  not not_171 (not_171_out, F25);
  not not_172 (not_172_out, F13);
  not not_173 (not_173_out, OP6);
  not not_174 (not_174_out, OP5);
  not not_175 (not_175_out, OP3);
  not not_176 (not_176_out, OP2);
  not not_177 (not_177_out, F14);
  not not_178 (not_178_out, F12);
  not not_179 (not_179_out, OP6);
  not not_180 (not_180_out, OP5);
  not not_181 (not_181_out, OP3);
  not not_182 (not_182_out, OP2);
  not not_183 (not_183_out, F14);
  not not_184 (not_184_out, F12);
  not not_185 (not_185_out, OP6);
  not not_186 (not_186_out, OP5);
  not not_187 (not_187_out, OP4);
  not not_188 (not_188_out, OP3);
  not not_189 (not_189_out, OP2);
  not not_190 (not_190_out, OP4);
  not not_191 (not_191_out, F13);
  not not_192 (not_192_out, F12);
  not not_193 (not_193_out, OP6);
  not not_194 (not_194_out, OP5);
  not not_195 (not_195_out, OP3);
  not not_196 (not_196_out, OP2);
  not not_197 (not_197_out, F14);
  not not_198 (not_198_out, F13);
  not not_199 (not_199_out, F12);
  not not_200 (not_200_out, OP4);
  not not_201 (not_201_out, OP3);
  not not_202 (not_202_out, F30);
  not not_203 (not_203_out, F14);
  not not_204 (not_204_out, F13);
  not not_205 (not_205_out, F12);
  not not_206 (not_206_out, OP6);
  not not_207 (not_207_out, OP3);
  not not_208 (not_208_out, OP2);
  not not_209 (not_209_out, F30);
  not not_210 (not_210_out, OP6);
  not not_211 (not_211_out, OP3);
  not not_212 (not_212_out, OP2);
  not not_213 (not_213_out, F13);
  not not_214 (not_214_out, OP6);
  not not_215 (not_215_out, OP5);
  not not_216 (not_216_out, OP4);
  not not_217 (not_217_out, OP3);
  not not_218 (not_218_out, OP2);
  not not_219 (not_219_out, F30);
  not not_220 (not_220_out, F25);
  not not_221 (not_221_out, F14);
  not not_222 (not_222_out, F13);
  not not_223 (not_223_out, F12);
  not not_224 (not_224_out, OP3);
  not not_225 (not_225_out, OP2);
  not not_226 (not_226_out, F30);
  not not_227 (not_227_out, F25);
  not not_228 (not_228_out, F14);
  not not_229 (not_229_out, F13);
  not not_230 (not_230_out, F12);
  not not_231 (not_231_out, OP3);
  not not_232 (not_232_out, OP2);
  not not_233 (not_233_out, F14);
  not not_234 (not_234_out, F12);
  not not_235 (not_235_out, OP6);
  not not_236 (not_236_out, OP4);
  not not_237 (not_237_out, OP3);
  not not_238 (not_238_out, OP2);
  not not_239 (not_239_out, F14);
  not not_240 (not_240_out, F13);
  not not_241 (not_241_out, F12);
  not not_242 (not_242_out, OP4);
  not not_243 (not_243_out, OP3);
  not not_244 (not_244_out, OP2);
  not not_245 (not_245_out, F14);
  not not_246 (not_246_out, F13);
  not not_247 (not_247_out, OP4);
  not not_248 (not_248_out, OP3);
  not not_249 (not_249_out, OP2);
  not not_250 (not_250_out, F14);
  not not_251 (not_251_out, F13);
  not not_252 (not_252_out, F12);
  not not_253 (not_253_out, OP4);
  not not_254 (not_254_out, OP3);
  not not_255 (not_255_out, OP4);
  and and_1 (and_1_out, not_1_out, F13, not_2_out, not_3_out, not_4_out, not_5_out, not_6_out, not_7_out);
  and and_2 (and_2_out, F14, not_8_out, F12, not_9_out, not_10_out, not_11_out, not_12_out, not_13_out);
  and and_3 (MemWrite, not_14_out, F13, not_15_out, not_16_out, OP5, not_17_out, not_18_out, not_19_out);
  and and_4 (and_4_out, not_20_out, not_21_out, not_22_out, not_23_out, not_24_out, OP4, not_25_out, not_26_out);
  and and_5 (and_5_out, F14, F13, F12, not_27_out, not_28_out, OP4, not_29_out, not_30_out);
  and and_6 (and_6_out, F14, F13, not_31_out, not_32_out, not_33_out, OP4, not_34_out, not_35_out);
  and and_7 (and_7_out, not_36_out, not_37_out, not_38_out, not_39_out, F12, not_40_out, not_41_out, OP4, not_42_out, not_43_out);
  and and_8 (and_8_out, F30, not_44_out, F14, not_45_out, F12, not_46_out, not_47_out, OP4, not_48_out, not_49_out);
  and and_9 (and_9_out, not_50_out, not_51_out, F14, not_52_out, F12, not_53_out, not_54_out, OP4, not_55_out, not_56_out);
  and and_10 (and_10_out, not_57_out, F13, not_58_out, not_59_out, not_60_out, OP4, not_61_out, not_62_out);
  and and_11 (and_11_out, not_63_out, F13, not_64_out, not_65_out, not_66_out, not_67_out, not_68_out, not_69_out);
  and and_12 (and_12_out, not_70_out, F13, not_71_out, not_72_out, OP5, not_73_out, not_74_out, not_75_out);
  and and_13 (and_13_out, F14, not_76_out, not_77_out, not_78_out, not_79_out, OP4, not_80_out, not_81_out);
  and and_14 (and_14_out, not_82_out, not_83_out, not_84_out, OP6, OP5, not_85_out, not_86_out, OP2);
  and and_15 (and_15_out, F14, F13, not_87_out, OP6, OP5, OP4, not_88_out, not_89_out);
  and and_16 (and_16_out, F14, F13, F12, OP6, OP5, OP4, not_90_out, not_91_out);
  and and_17 (and_17_out, F14, not_92_out, F12, not_93_out, not_94_out, not_95_out, not_96_out, not_97_out);
  and and_18 (bgeu, F14, F13, F12, OP6, OP5, not_98_out, not_99_out, not_100_out);
  and and_19 (and_19_out, not_101_out, not_102_out, not_103_out, not_104_out, not_105_out, not_106_out, OP5, OP4, not_107_out, not_108_out);
  and and_20 (and_20_out, F30, not_109_out, not_110_out, not_111_out, not_112_out, not_113_out, OP5, OP4, not_114_out, not_115_out);
  and and_21 (and_21_out, not_116_out, not_117_out, F14, F13, F12, not_118_out, OP5, OP4, not_119_out, not_120_out);
  and and_22 (and_22_out, not_121_out, not_122_out, F14, F13, not_123_out, not_124_out, OP5, OP4, not_125_out, not_126_out);
  and and_23 (and_23_out, not_127_out, not_128_out, not_129_out, F13, not_130_out, not_131_out, OP5, OP4, not_132_out, not_133_out);
  and and_24 (and_24_out, not_134_out, not_135_out, not_136_out, F13, F12, not_137_out, OP5, OP4, not_138_out, not_139_out);
  and and_25 (and_25_out, not_140_out, not_141_out, not_142_out, not_143_out, not_144_out, OP4, not_145_out, not_146_out);
  and and_26 (and_26_out, F14, F13, F12, not_147_out, not_148_out, OP4, not_149_out, not_150_out);
  and and_27 (and_27_out, F14, F13, not_151_out, not_152_out, not_153_out, OP4, not_154_out, not_155_out);
  and and_28 (and_28_out, not_156_out, not_157_out, not_158_out, not_159_out, F12, not_160_out, not_161_out, OP4, not_162_out, not_163_out);
  and and_29 (and_29_out, F30, not_164_out, F14, not_165_out, F12, not_166_out, not_167_out, OP4, not_168_out, not_169_out);
  and and_30 (and_30_out, not_170_out, not_171_out, F14, not_172_out, F12, not_173_out, not_174_out, OP4, not_175_out, not_176_out);
  and and_31 (and_31_out, not_177_out, F13, not_178_out, not_179_out, not_180_out, OP4, not_181_out, not_182_out);
  and and_32 (and_32_out, not_183_out, F13, not_184_out, not_185_out, not_186_out, not_187_out, not_188_out, not_189_out);
  and and_33 (and_33_out, OP6, OP5, not_190_out, OP3, OP2);
  and and_34 (and_34_out, F14, not_191_out, not_192_out, not_193_out, not_194_out, OP4, not_195_out, not_196_out);
  and and_35 (and_35_out, not_197_out, not_198_out, not_199_out, OP6, OP5, not_200_out, not_201_out, OP2);
  and and_36 (and_36_out, not_202_out, F25, not_203_out, not_204_out, not_205_out, not_206_out, OP5, OP4, not_207_out, not_208_out);
  and and_37 (and_37_out, not_209_out, F25, F14, F13, F12, not_210_out, OP5, OP4, not_211_out, not_212_out);
  and and_38 (and_38_out, F14, not_213_out, F12, not_214_out, not_215_out, not_216_out, not_217_out, not_218_out);
  and and_39 (and_39_out, not_219_out, not_220_out, not_221_out, not_222_out, not_223_out, OP6, OP5, OP4, not_224_out, not_225_out);
  and and_40 (and_40_out, not_226_out, not_227_out, not_228_out, not_229_out, not_230_out, OP6, OP5, OP4, not_231_out, not_232_out);
  and and_41 (S_Type, not_233_out, F13, not_234_out, not_235_out, OP5, not_236_out, not_237_out, not_238_out);
  and and_42 (BEQ, not_239_out, not_240_out, not_241_out, OP6, OP5, not_242_out, not_243_out, not_244_out);
  and and_43 (BNE, not_245_out, not_246_out, F12, OP6, OP5, not_247_out, not_248_out, not_249_out);
  and and_44 (JALR, not_250_out, not_251_out, not_252_out, OP6, OP5, not_253_out, not_254_out, OP2);
  and and_45 (JAL, OP6, OP5, not_255_out, OP3, OP2);
  or or_1 (MemToReg, and_1_out, and_2_out);
  or or_2 (ecall, and_39_out, and_40_out);
  or or_3 (ALU_SRC, and_4_out, and_5_out, and_6_out, and_7_out, and_8_out, and_9_out, and_10_out, and_11_out, and_12_out, and_13_out, and_14_out, and_15_out, and_16_out, and_17_out);
  or or_4 (RegWrite, and_19_out, and_20_out, and_21_out, and_22_out, and_23_out, and_24_out, and_25_out, and_26_out, and_27_out, and_28_out, and_29_out, and_30_out, and_31_out, and_32_out, and_33_out, and_34_out, and_35_out, and_36_out, and_37_out, and_38_out);
endmodule

// ALU
module ALU (
  input  [31:0] X,
  input  [31:0] Y,
  input  [3:0] AluOP,
  output out_4,
  output Equal,
  output out_6,
  output [31:0] Result,
  output [31:0] Result_2
);

  wire [0:0] comparator_1_lt, comparator_2_lt;
  wire [31:0] adder_1_out, AND_out, divider_1_out, divider_1_rem, multiplier_1_cout, multiplier_1_out,
       NOR_out, OR_out, shifter_1_out, shifter_2_out, shifter_3_out, subtractor_1_out, XOR_out;

  assign AND_out = X & Y;  // AND_Gate AND, 32 bits wide
  assign OR_out = X | Y;  // OR_Gate OR, 32 bits wide
  Shifter #(.width(32), .shift("ll")) shifter_1 (.in(X), .\dist (Y[4:0]), .out(shifter_1_out));
  Shifter #(.width(32), .shift("ar")) shifter_2 (.in(X), .\dist (Y[4:0]), .out(shifter_2_out));
  Shifter #(.width(32), .shift("lr")) shifter_3 (.in(X), .\dist (Y[4:0]), .out(shifter_3_out));
  Multiplier #(.width(32)) multiplier_1 (.a(X), .b(Y), .out(multiplier_1_out), .cout(multiplier_1_cout));  // open: cin
  Divider #(.width(32)) divider_1 (.a(X), .b(Y), .out(divider_1_out), .rem(divider_1_rem));  // open: upper
  Adder #(.width(32)) adder_1 (.a(X), .b(Y), .out(adder_1_out));  // open: cin, cout
  Subtractor #(.width(32)) subtractor_1 (.a(X), .b(Y), .out(subtractor_1_out));  // open: bin, bout
  assign XOR_out = X ^ Y;  // XOR_Gate XOR, 32 bits wide
  assign NOR_out = ~(X | Y);  // NOR_Gate NOR, 32 bits wide
  Comparator #(.width(32), .mode("twosComplement")) comparator_1 (
    .a(X), .b(Y), .eq(Equal), .lt(comparator_1_lt[0]));  // open: gt
  Comparator #(.width(32), .mode("unsigned")) comparator_2 (.a(X), .b(Y), .lt(comparator_2_lt[0]));  // open: gt, eq
  Multiplexer #(.select(4), .width(32), .disabled("Z"), .enable("false")) multiplexer_1 (
    .in0(shifter_1_out), .in1(shifter_2_out), .in2(shifter_3_out), .in3(multiplier_1_out),
    .in4(divider_1_out), .in5(adder_1_out), .in6(subtractor_1_out), .in7(AND_out), .in8(OR_out),
    .in9(XOR_out), .in10(NOR_out), .in11({{31{1'b0}}, comparator_1_lt[0]}),
    .in12({{31{1'b0}}, comparator_2_lt[0]}), .in13({32{1'b0}}), .in14({32{1'b0}}), .in15({32{1'b0}}),
    .out(Result), .sel(AluOP));
  Multiplexer #(.select(4), .width(32), .disabled("Z"), .enable("false")) multiplexer_2 (
    .in0({32{1'b0}}), .in1({32{1'b0}}), .in2({32{1'b0}}), .in3(multiplier_1_cout), .in4(divider_1_rem),
    .in5({32{1'b0}}), .in6({32{1'b0}}), .in7({32{1'b0}}), .in8({32{1'b0}}), .in9({32{1'b0}}),
    .in10({32{1'b0}}), .in11({32{1'b0}}), .in12({32{1'b0}}), .in13({32{1'b0}}), .in14({32{1'b0}}),
    .in15({32{1'b0}}), .out(Result_2), .sel(AluOP));
  Multiplexer #(.select(4), .width(1), .disabled("Z"), .enable("false")) multiplexer_3 (
    .in0(1'b0), .in1(1'b0), .in2(1'b0), .in3(1'b0), .in4(1'b0), .in5(1'b0), .in6(1'b0), .in7(1'b0),
    .in8(1'b0), .in9(1'b0), .in10(1'b0), .in11(comparator_1_lt[0]), .in12(comparator_2_lt[0]), .in13(1'b0),
    .in14(1'b0), .in15(1'b0), .out(out_6), .sel(AluOP));
  not not_1 (out_4, out_6);

  // Other names for the same wires on the sheet: Result2[31:0] = Result_2; S[3:0] = AluOP; tunnel = out_6;
  //   tunnel_t = out_4

  // Notes on the sheet:
  //   不要改变此引脚区域内容，也不要改变ALU封装形式
  //   输入引脚
  //   输出引脚
endmodule

module Regifile (
  input  [31:0] Din,
  input  Clk,
  input  WE,
  input  [4:0] R1_num,
  input  [4:0] W_num,
  input  [4:0] R2_num,
  output [31:0] R1,
  output [31:0] R2
);

  // RegisterFile registerfile_1: pin names not known; wires that end beside it: Din, Clk, WE, W_num, R1_num, R2_num, R1, R2
endmodule

module \气泡流水线  (
  output RegWrite,
  output MemWrite,
  output [31:0] IF_PC,
  output [31:0] ID_PC,
  output [31:0] EX_PC,
  output [31:0] M_PC,
  output [31:0] WB_PC,
  output [31:0] RDin,
  output [31:0] MDin,
  output [31:0] LedData
);

  wire AluSrcB, and_1_out, and_2_out, and_3_out, and_4_out, and_5_out, and_6_out, and_8_out, BGEU, branch,
       clash, CLK, clock_1_out, comparator_1_eq, comparator_1_lt, comparator_3_eq, comparator_4_eq, d_ff_1_q,
       ecall, equal, ex_mem2_1_halt_out, ex_mem2_1_high_out, ex_mem2_1_jal_out, ex_mem2_1_jalr_out,
       ex_mem2_1_memtoreg_out, EX_rw, flag, GE, Go, halt, id_ex2_1_beq_out, id_ex2_1_bne_out,
       id_ex2_1_ecall_out, id_ex2_1_memtoreg_out, id_ex2_1_memwrite_out, IR1, IR2, IR3, JAL, JALR, MEM_rw,
       mem_wb2_1_jal_out, mem_wb2_1_jalr_out, mem_wb2_1_memtoreg_out, nand_1_out, not_1_out, not_2_out,
       not_3_out, not_4_out, not_5_out, not_6_out, not_7_out, not_8_out, not_9_out, not_10_out, or_1_out,
       or_2_out, or_3_out, or_4_out, or_5_out, or_8_out, or_9_out, riscv_probe_6_p2, RST, S_type, tunnel1,
       W1, W2, W3, \单周期硬布线控制器_1_alu_src , \单周期硬布线控制器_1_beq , \单周期硬布线控制器_1_bgeu , \单周期硬布线控制器_1_bne ,
       \单周期硬布线控制器_1_jal , \单周期硬布线控制器_1_jalr , \单周期硬布线控制器_1_memtoreg , \单周期硬布线控制器_1_memwrite ,
       \单周期硬布线控制器_1_regwrite ;
  wire [3:0] id_ex2_1_aluop_out, \单周期硬布线控制器_1_alu_op ;
  wire [4:0] EX_W, MEM_W, mem_wb2_1_w_out, R1_num, R2_num;
  wire [9:0] ex_mem2_1_ma_out;
  wire [11:0] multiplexer_3_out;
  wire [12:0] CNT_num;
  wire [15:0] \总周期数 , \插入气泡数 , \无条件分支数 , \条件分支成功数 ;
  wire [31:0] adder_1_out, adder_2_out, adder_3_out, adder_4_out, alu_1_result, alu_1_result_2, aluresult,
       and_7_out, bit_extender_1_out, bit_extender_2_out, bit_extender_3_out, bit_extender_4_out,
       bit_extender_5_out, EX_IR, ex_mem2_1_aluresult_out, ex_mem2_1_imm_out, id_ex2_1_b_out,
       id_ex2_1_imm_out, id_ex2_1_j_out, id_ex2_1_r1_out, id_ex2_1_r2_out, ID_IR, IF_IR, MEM_IR,
       mem_wb2_1_aluresult_out, mem_wb2_1_dout_out, mem_wb2_1_imm_out, multiplexer_4_out, multiplexer_5_out,
       multiplexer_6_out, multiplexer_7_out, multiplexer_8_out, multiplexer_10_out, multiplexer_11_out,
       multiplexer_12_out, ram_1_data, regifile_1_r1, regifile_1_r2, shifter_1_out, shifter_2_out, WB_IR;

  Button \u_总复位  (.out(RST));
  Button _1 (.out(IR1));
  Button _2 (.out(IR2));
  Button _3 (.out(IR3));
  // Probe on \总周期数 
  // Probe on \总周期数 
  Button \u_继续运行  (.out(Go));
  LED #(.active("true")) led_1 (.in(W1));
  LED #(.active("true")) led_2 (.in(W2));
  LED #(.active("true")) led_3 (.in(W3));
  Hex_Digit_Display hex_digit_display_1 (.value(LedData[31:28]));  // open: dp
  // Probe on IF_PC[19:0]
  // RiscV_Probe riscv_probe_1: pin names not known; wires that end beside it: IF_IR
  Hex_Digit_Display hex_digit_display_2 (.value(LedData[27:24]));  // open: dp
  Hex_Digit_Display hex_digit_display_3 (.value(LedData[23:20]));  // open: dp
  // Probe on ID_PC[19:0]
  // RiscV_Probe riscv_probe_2: pin names not known; wires that end beside it: ID_IR
  Counter #(.width(16), .max('hffff), .ongoal("wrap"), .trigger("rising"), .behavior("new")) counter_1 (
    .Q(\插入气泡数 ), .clk(clash), .clr(RST));  // open: load, D, count, carry, preset, down
  Counter #(.width(16), .max('hffff), .ongoal("wrap"), .trigger("rising"), .behavior("new")) counter_2 (
    .Q(\条件分支成功数 ), .clk(tunnel1), .clr(RST));  // open: load, D, count, carry, preset, down
  Hex_Digit_Display hex_digit_display_4 (.value(LedData[15:12]));  // open: dp
  Hex_Digit_Display hex_digit_display_5 (.value(LedData[19:16]));  // open: dp
  Register #(.width(32), .trigger("rising"), .Select("low")) PC (
    .D(multiplexer_8_out), .en(and_1_out), .Q(IF_PC), .clk(CLK), .clr(RST));
  and and_1 (and_1_out, or_1_out, not_1_out);
  or or_1 (or_1_out, not_2_out, Go);
  not not_1 (not_1_out, clash);
  not not_2 (not_2_out, halt);
  Hex_Digit_Display hex_digit_display_6 (.value(LedData[7:4]));  // open: dp
  Hex_Digit_Display hex_digit_display_7 (.value(LedData[11:8]));  // open: dp
  // Probe on EX_PC[19:0]
  // RiscV_Probe riscv_probe_3: pin names not known; wires that end beside it: EX_IR
  not not_3 (not_3_out, halt);
  or or_2 (or_2_out, not_3_out, Go);
  Counter #(.width(16), .max('hffff), .ongoal("wrap"), .trigger("rising"), .behavior("new")) counter_3 (
    .count(or_2_out), .Q(\总周期数 ), .clk(CLK), .clr(RST));  // open: load, D, carry, preset, down
  Hex_Digit_Display hex_digit_display_8 (.value(LedData[3:0]));  // open: dp
  Counter #(.width(16), .max('hffff), .ongoal("wrap"), .trigger("rising"), .behavior("new")) counter_4 (
    .Q(\无条件分支数 ), .clk(or_3_out), .clr(RST));  // open: load, D, count, carry, preset, down
  or or_3 (or_3_out, JAL, JALR);
  // Probe on \总周期数 
  // Probe on M_PC[19:0]
  // RiscV_Probe riscv_probe_4: pin names not known; wires that end beside it: MEM_IR
  ROM #(.addrWidth(10), .dataWidth(32), .Select("high")) rom_1 (.addr(IF_PC[11:2]), .data(IF_IR));
  Adder #(.width(32)) adder_1 (.a(IF_PC), .b(32'h4), .out(adder_1_out));  // open: cin, cout
  not not_4 (not_4_out, clash);
  or or_4 (or_4_out, not_5_out, Go);
  not not_5 (not_5_out, halt);
  // Probe on \总周期数 
  // Probe on \无条件分支数 
  // Probe on \条件分支成功数 
  // Probe on \插入气泡数 
  // Probe on {16{1'b0}}
  IF_ID2 if_id2_1 (
    .IR_IN(IF_IR), .PC_IN(IF_PC), .IR_OUT(ID_IR), .PC_OUT(ID_PC), .CLR(branch), .RST(RST), .en(and_2_out),
    .CLK(CLK));  // open: PREDICTJUMP_IN, PREDICTJUMP_OUT
  and and_2 (and_2_out, not_4_out, or_4_out);
  // Probe on IF_PC[11:0]
  // Probe on WB_PC[19:0]
  // RiscV_Probe riscv_probe_5: pin names not known; wires that end beside it: WB_IR
  // RiscV_Probe riscv_probe_6: pin names not known; wires that end beside it: ID_IR, riscv_probe_6_p2
  // Probe on ID_PC[11:0]
  // Probe on EX_PC[11:0]
  // Probe on M_PC[11:0]
  D_Flip_Flop #(.trigger("high"), .Pre_Clr_Positions("LEGACY"), .NegatePresetClear("false"), .enable("true"), .NewFFLayout("false")) d_ff_1 (.Q(d_ff_1_q));  // open: clk, D, Qn, preset, en, reset
  // Probe on 13'hc
  // Probe on WB_PC[11:0]
  Comparator #(.width(13), .mode("twosComplement")) comparator_1 (
    .a(CNT_num), .b(13'hc), .eq(comparator_1_eq), .lt(comparator_1_lt));  // open: gt
  Clock #(.highDuration(1), .lowDuration(1)) clock_1 (.out(clock_1_out));
  \单周期硬布线控制器  \u_单周期硬布线控制器_1  (
    .Funct({ID_IR[30], ID_IR[25], ID_IR[14:12]}), .OP(ID_IR[6:2]), .ALU_OP(\单周期硬布线控制器_1_alu_op ),
    .MemToReg(\单周期硬布线控制器_1_memtoreg ), .MemWrite(\单周期硬布线控制器_1_memwrite ), .ALU_SRC(\单周期硬布线控制器_1_alu_src ),
    .RegWrite(\单周期硬布线控制器_1_regwrite ), .ecall(ecall), .S_type(S_type), .Jalr(\单周期硬布线控制器_1_jalr ),
    .Beq(\单周期硬布线控制器_1_beq ), .JAL(\单周期硬布线控制器_1_jal ), .Bne(\单周期硬布线控制器_1_bne ), .in_3(ID_IR[21]),
    .uret(riscv_probe_6_p2), .BGEU(\单周期硬布线控制器_1_bgeu ));
  Multiplexer #(.select(1), .width(5), .disabled("Z"), .enable("false")) multiplexer_1 (
    .in0(ID_IR[19:15]), .in1(5'b10001), .out(R1_num), .sel(ecall));
  Multiplexer #(.select(1), .width(5), .disabled("Z"), .enable("false")) multiplexer_2 (
    .in0(ID_IR[24:20]), .in1(5'b01010), .out(R2_num), .sel(ecall));
  Multiplexer #(.select(1), .width(12), .disabled("Z"), .enable("false")) multiplexer_3 (
    .in0(ID_IR[31:20]), .in1({ID_IR[31:25], ID_IR[11:7]}), .out(multiplexer_3_out), .sel(S_type));
  assign bit_extender_1_out = {{20{ID_IR[31]}}, {ID_IR[31], ID_IR[7], ID_IR[30:25], ID_IR[11:8]}};  // Bit_Extender bit_extender_1
  nand nand_1 (nand_1_out, d_ff_1_q, comparator_1_eq);
  Counter #(.width(13), .max('h1fff), .ongoal("stay"), .trigger("rising"), .behavior("old")) counter_5 (
    .count(comparator_1_lt), .Q(CNT_num), .clk(clock_1_out));  // open: load, D, carry, clr, preset
  Shifter #(.width(32), .shift("ll")) shifter_1 (.in(bit_extender_1_out), .\dist (5'b00001), .out(shifter_1_out));
  assign bit_extender_2_out = {{12{ID_IR[31]}}, {ID_IR[31], ID_IR[19:12], ID_IR[20], ID_IR[30:21]}};  // Bit_Extender bit_extender_2
  assign CLK = nand_1_out ? clock_1_out : 1'bz;  // Controlled_Buffer controlled_buffer_1
  CLASH clash_1 (
    .R1_num(R1_num), .EX_W_num(EX_W), .EX_RegWrite(EX_rw), .R2_num(R2_num), .OP(ID_IR[6:2]),
    .MEM_W_num(MEM_W), .MEM_RegWrite(MEM_rw), .clash(clash));
  Regifile regifile_1 (
    .Din(RDin), .Clk(CLK), .R1(regifile_1_r1), .R2(regifile_1_r2), .WE(RegWrite), .W_num(mem_wb2_1_w_out),
    .R1_num(R1_num), .R2_num(R2_num));
  assign bit_extender_3_out = {{20{multiplexer_3_out[11]}}, multiplexer_3_out};  // Bit_Extender bit_extender_3
  Shifter #(.width(32), .shift("ll")) shifter_2 (.in(bit_extender_2_out), .\dist (5'b00001), .out(shifter_2_out));
  Pull_Resistor #(.pull(1)) pull_resistor_1 (.node(CLK));
  or or_5 (or_5_out, branch, clash);
  ID_EX2 id_ex2_1 (
    .JAL(\单周期硬布线控制器_1_jal ), .JALR(\单周期硬布线控制器_1_jalr ), .BEQ(\单周期硬布线控制器_1_beq ), .BNE(\单周期硬布线控制器_1_bne ),
    .MEMTOREG(\单周期硬布线控制器_1_memtoreg ), .MEMWRITE(\单周期硬布线控制器_1_memwrite ), .ALUOP(\单周期硬布线控制器_1_alu_op ),
    .ALUSRC(\单周期硬布线控制器_1_alu_src ), .REGWRITE(\单周期硬布线控制器_1_regwrite ), .ECALL(ecall), .R1(regifile_1_r1),
    .R2(regifile_1_r2), .W_num(ID_IR[11:7]), .IMM(bit_extender_3_out), .B(shifter_1_out), .IR(ID_IR),
    .J(shifter_2_out), .PC(ID_PC), .JAL_OUT(JAL), .JALR_OUT(JALR), .BEQ_OUT(id_ex2_1_beq_out),
    .BNE_OUT(id_ex2_1_bne_out), .MEMTOREG_OUT(id_ex2_1_memtoreg_out), .MEMWRITE_OUT(id_ex2_1_memwrite_out),
    .ALUOP_OUT(id_ex2_1_aluop_out), .ALUSRC_OUT(AluSrcB), .REGWRITE_OUT(EX_rw),
    .ECALL_OUT(id_ex2_1_ecall_out), .R1_OUT(id_ex2_1_r1_out), .R2_OUT(id_ex2_1_r2_out), .W__OUT(EX_W),
    .IMM_OUT(id_ex2_1_imm_out), .B_OUT(id_ex2_1_b_out), .IR_OUT(EX_IR), .J_OUT(id_ex2_1_j_out),
    .PC_OUT(EX_PC), .CLK(CLK), .RST(RST), .CLR(or_5_out), .EN(or_8_out), .BGEU_IN(\单周期硬布线控制器_1_bgeu ),
    .BGEU_OUT(BGEU));
  and and_3 (and_3_out, equal, id_ex2_1_beq_out);
  not not_6 (not_6_out, equal);
  Comparator #(.width(32), .mode("twosComplement")) comparator_2 (
    .a(32'h22), .b(id_ex2_1_r1_out), .eq(flag));  // open: gt, lt
  Multiplexer #(.select(1), .width(32), .disabled("Z"), .enable("false")) multiplexer_4 (
    .in0(id_ex2_1_r2_out), .in1(id_ex2_1_imm_out), .out(multiplexer_4_out), .sel(AluSrcB));
  Adder #(.width(32)) adder_2 (.a(id_ex2_1_b_out), .b(EX_PC), .out(adder_2_out));  // open: cin, cout
  Multiplexer #(.select(1), .width(32), .disabled("Z"), .enable("false")) multiplexer_5 (
    .in0({32{1'b0}}), .in1(id_ex2_1_r2_out), .out(multiplexer_5_out), .sel(and_4_out));
  and and_4 (and_4_out, id_ex2_1_ecall_out, flag);
  and and_5 (and_5_out, not_6_out, id_ex2_1_bne_out);
  ALU alu_1 (
    .X(id_ex2_1_r1_out), .Y(multiplexer_4_out), .AluOP(id_ex2_1_aluop_out), .Equal(equal),
    .Result(alu_1_result), .Result_2(alu_1_result_2), .out_4(GE));  // open: out_6
  Multiplexer #(.select(1), .width(32), .disabled("Z"), .enable("false")) multiplexer_6 (
    .in0(adder_1_out), .in1(adder_2_out), .out(multiplexer_6_out), .sel(tunnel1));
  Adder #(.width(32)) adder_3 (.a(id_ex2_1_j_out), .b(EX_PC), .out(adder_3_out));  // open: cin, cout
  or or_6 (branch, JALR, JAL, tunnel1);
  not not_7 (not_7_out, flag);
  or or_7 (tunnel1, and_3_out, and_5_out, and_6_out);
  and and_6 (and_6_out, BGEU, GE);
  Comparator #(.width(4), .mode("twosComplement")) comparator_3 (
    .a(id_ex2_1_aluop_out), .b(4'b0100), .eq(comparator_3_eq));  // open: gt, lt
  Multiplexer #(.select(1), .width(32), .disabled("Z"), .enable("false")) multiplexer_7 (
    .in0(multiplexer_6_out), .in1(adder_3_out), .out(multiplexer_7_out), .sel(JAL));
  Multiplexer #(.select(1), .width(32), .disabled("Z"), .enable("false")) multiplexer_8 (
    .in0(multiplexer_7_out), .in1(and_7_out), .out(multiplexer_8_out), .sel(JALR));
  assign and_7_out = aluresult & 32'hfffffffe;  // AND_Gate and_7, 32 bits wide
  Register #(.width(32), .trigger("rising"), .Select("low")) register_1 (
    .D(multiplexer_5_out), .en(and_4_out), .Q(LedData), .clk(CLK));  // open: clr
  and and_8 (and_8_out, id_ex2_1_ecall_out, not_7_out);
  Multiplexer #(.select(1), .width(32), .disabled("Z"), .enable("false")) multiplexer_9 (
    .in0(alu_1_result), .in1(alu_1_result_2), .out(aluresult), .sel(comparator_3_eq));
  Adder #(.width(32)) adder_4 (.a(EX_PC), .b(32'h4), .out(adder_4_out));  // open: cin, cout
  EX_MEM2 ex_mem2_1 (
    .JAL_IN(JAL), .JALR_IN(JALR), .halt_IN(and_8_out), .MemToReg_IN(id_ex2_1_memtoreg_out),
    .MemWrite_IN(id_ex2_1_memwrite_out), .RegWrite_IN(EX_rw), .aluresult_IN(aluresult),
    .MA_IN(aluresult[11:2]), .MDin_IN(id_ex2_1_r2_out), .W_IN(EX_W), .PC_IN(EX_PC), .IR_IN(EX_IR),
    .IMM_IN(adder_4_out), .JAL_OUT(ex_mem2_1_jal_out), .JALR_OUT(ex_mem2_1_jalr_out),
    .halt_OUT(ex_mem2_1_halt_out), .MemToReg_OUT(ex_mem2_1_memtoreg_out), .MemWrite_OUT(MemWrite),
    .RegWrite_OUT(MEM_rw), .aluresult_OUT(ex_mem2_1_aluresult_out), .MA_OUT(ex_mem2_1_ma_out),
    .MDin_OUT(MDin), .W_OUT(MEM_W), .PC_OUT(M_PC), .IR_OUT(MEM_IR), .IMM_OUT(ex_mem2_1_imm_out), .CLR(1'b0),
    .RST(RST), .en(or_8_out), .CLK(CLK), .HIGH_IN(aluresult[1]), .HIGH_OUT(ex_mem2_1_high_out));
  not not_8 (not_8_out, MemWrite);
  not not_9 (not_9_out, halt);
  RAM #(.addrWidth(10), .dataWidth(32), .bus("separate"), .Select("high")) ram_1 (
    .addr(ex_mem2_1_ma_out), .din(MDin), .data(ram_1_data), .str(MemWrite), .clk(CLK), .ld(not_8_out));  // open: sel, clr
  or or_8 (or_8_out, not_9_out, Go);
  assign bit_extender_4_out = {{16{1'b0}}, ram_1_data[15:0]};  // Bit_Extender bit_extender_4
  assign bit_extender_5_out = {{16{1'b0}}, ram_1_data[31:16]};  // Bit_Extender bit_extender_5
  Multiplexer #(.select(1), .width(32), .disabled("Z"), .enable("false")) multiplexer_10 (
    .in0(bit_extender_4_out), .in1(bit_extender_5_out), .out(multiplexer_10_out), .sel(ex_mem2_1_high_out));
  Comparator #(.width(3), .mode("twosComplement")) comparator_4 (
    .a(MEM_IR[14:12]), .b(3'b101), .eq(comparator_4_eq));  // open: gt, lt
  not not_10 (not_10_out, comparator_4_eq);
  MEM_WB2 mem_wb2_1 (
    .JAL_IN(ex_mem2_1_jal_out), .JALR_IN(ex_mem2_1_jalr_out), .halt_IN(ex_mem2_1_halt_out),
    .MemToReg_IN(ex_mem2_1_memtoreg_out), .RegWrite_IN(MEM_rw), .aluresult_IN(ex_mem2_1_aluresult_out),
    .Dout_IN(multiplexer_11_out), .W_IN(MEM_W), .IR_IN(MEM_IR), .PC_IN(M_PC), .IMM_IN(ex_mem2_1_imm_out),
    .JAL_OUT(mem_wb2_1_jal_out), .JALR_OUT(mem_wb2_1_jalr_out), .halt_OUT(halt),
    .MemToReg_OUT(mem_wb2_1_memtoreg_out), .RegWrite_OUT(RegWrite), .aluresult_OUT(mem_wb2_1_aluresult_out),
    .Dout_OUT(mem_wb2_1_dout_out), .W_OUT(mem_wb2_1_w_out), .IR_OUT(WB_IR), .PC_OUT(WB_PC),
    .IMM_OUT(mem_wb2_1_imm_out), .CLR(1'b0), .RST(RST), .en(or_8_out), .CLK(CLK));
  Multiplexer #(.select(1), .width(32), .disabled("Z"), .enable("false")) multiplexer_11 (
    .in0(multiplexer_10_out), .in1(ram_1_data), .out(multiplexer_11_out), .sel(not_10_out));
  Multiplexer #(.select(1), .width(32), .disabled("Z"), .enable("false")) multiplexer_12 (
    .in0(mem_wb2_1_aluresult_out), .in1(mem_wb2_1_dout_out), .out(multiplexer_12_out),
    .sel(mem_wb2_1_memtoreg_out));
  or or_9 (or_9_out, mem_wb2_1_jalr_out, mem_wb2_1_jal_out);
  Multiplexer #(.select(1), .width(32), .disabled("Z"), .enable("false")) multiplexer_13 (
    .in0(multiplexer_12_out), .in1(mem_wb2_1_imm_out), .out(RDin), .sel(or_9_out));
  // Probe on nothing

  // Other names for the same wires on the sheet: op[4:0] = ID_IR[6:2]; MEM_PC[31:0] = M_PC

  // Notes on the sheet:
  //   中断源
  //   时空图监测，可删除
  //   中断等待指示
  //   数码管输出
  //   指令存储器
  //   contents of rom_1 (hex, n*v repeats v):
  //   100493 100006f 100493 200913 300993 100006f 100493 200913 300993 100006f 100493 200913 300993
  //   100006f 100493 200913 300993 3bc000ef 100413 100493 1f49493 900533 2200893 73 24d493 48463 fedff06f
  //   900533 2200893 73 100493 249493 900533 2200893 73 48463 fedff06f 100493 1f49493 900533 2200893 73
  //   4034d493 900533 2200893 73 4044d493 900533 2200893 73 4044d493 900533 2200893 73 4044d493 900533
  //   2200893 73 4044d493 900533 2200893 73 4044d493 900533 2200893 73 4044d493 900533 2200893 73 4044d493
  //   900533 2200893 73 100413 1f41993 41f9d993 433 c00913 300b13 140413 f47413 800293 100313 499993
  //   89e9b3 1300533 2200893 73 406282b3 fe0294e3 140413 f00f93 1f47433 1c41413 800293 100313 49d993
  //   89e9b3 1300533 2200893 73 406282b3 fe0294e3 1c45413 406b0b33 b0463 f95ff06f 2b3 fff2c293 829293
  //   ff2e293 500533 2200893 73 fff00413 493 84a023 140413 448493 84a023 140413 448493 84a023 140413
  //   448493 84a023 140413 448493 84a023 140413 448493 84a023 140413 448493 84a023 140413 448493 84a023
  //   140413 448493 84a023 140413 448493 84a023 140413 448493 84a023 140413 448493 84a023 140413 448493
  //   84a023 140413 448493 84a023 140413 448493 84a023 140413 448493 84a023 140413 448493 140413 433
  //   3c00493 42983 4aa03 149a2b3 28663 134a023 1442023 ffc48493 fe9412e3 800533 2200893 73 440413 3c00493
  //   fc9416e3 a00893 73 200293 1100493 849493 1148493 900533 2200893 73 2000e13 25484b3 900533 2200893 73
  //   fffe0e13 fe0e16e3 a00893 73 8800493 849493 4848493 8700913 891913 5490913 2997933 1091913 11096913
  //   1200533 2200893 73 a00893 73 313 1000e13 8400493 849493 8348493 400913 891913 490913 849493 8248493
  //   849493 8148493 891913 490913 891913 490913 932023 12484b3 430313 fffe0e13 fe0e18e3 2000e13 313 35483
  //   900533 2200893 73 230313 fffe0e13 fe0e14e3 a00893 73 f00493 100913 409909b3 900533 2200893 73
  //   fff48493 ff29f6e3 a00893 73 413 140413 800533 2200893 73 240413 800533 2200893 73 340413 800533
  //   2200893 73 440413 800533 2200893 73 540413 800533 2200893 73 640413 800533 2200893 73 740413 800533
  //   2200893 73 840413 800533 2200893 2200893 73 8067
  //   指令探针
  //   控制位
  //   指令字
  //   流水调试日志用
  //   暂停节拍，不能为0
  //   JAL
  //   JALR
  //   URET
  //   戳工具置1进入计数暂停模式，ctrl+k时钟自动运行到对应节拍暂停
  //   ctrl+k关闭时钟连续运行，将控制位置零，进入单步调试模式调试
  //   Beq
  //   Bne
  //   MemToReg
  //   MemWrite
  //   AluOP
  //   AluSrcB
  //   RegWrite
  //   冲突检测
  //   可计数暂停的时钟源
  //   为方便自动评测，需要输出流水线各段保存的PC值，注意是PC不是PC+4，另外ID段寄存器写入信息，Mem段内存写入信息也要输出
  //   数据存储器
endmodule

// IF.IR
module \理想流水线  (
  output RegWrite,
  output MemWrite,
  output [31:0] IF_PC,
  output [31:0] ID_PC,
  output [31:0] EX_PC,
  output [31:0] M_PC,
  output [31:0] WB_PC,
  output [31:0] RDin,
  output [31:0] MDin,
  output [31:0] LedData
);

  wire AluSrcB, and_1_out, and_2_out, and_3_out, and_4_out, and_6_out, BGEU, CLK, clock_1_out,
       comparator_1_eq, comparator_1_lt, comparator_3_eq, comparator_4_eq, d_ff_1_q, ecall, equal,
       ex_mem1_1_halt_out, ex_mem1_1_high_out, ex_mem1_1_jal_out, ex_mem1_1_jalr_out, ex_mem1_1_memtoreg_out,
       ex_mem1_1_regwrite_out, flag, GE, Go, halt, id_ex1_1_beq_out, id_ex1_1_bne_out, id_ex1_1_ecall_out,
       id_ex1_1_memtoreg_out, id_ex1_1_memwrite_out, id_ex1_1_regwrite_out, IR1, IR2, IR3, JAL, JALR,
       mem_wb1_1_jal_out, mem_wb1_1_jalr_out, MemToReg, nand_1_out, not_1_out, not_2_out, not_3_out,
       not_4_out, not_5_out, not_6_out, not_7_out, or_1_out, or_2_out, or_3_out, or_5_out, riscv_probe_5_p2,
       RST, S_type, tunnel1, W1, W2, W3, \单周期硬布线控制器_1_alu_src , \单周期硬布线控制器_1_beq , \单周期硬布线控制器_1_bgeu ,
       \单周期硬布线控制器_1_bne , \单周期硬布线控制器_1_jal , \单周期硬布线控制器_1_jalr , \单周期硬布线控制器_1_memtoreg ,
       \单周期硬布线控制器_1_memwrite , \单周期硬布线控制器_1_regwrite ;
  wire [3:0] id_ex1_1_aluop_out, \单周期硬布线控制器_1_alu_op ;
  wire [4:0] ex_mem1_1_w_out, id_ex1_1_w_out, mem_wb1_1_w_out, multiplexer_1_out, multiplexer_2_out;
  wire [9:0] ex_mem1_1_ma_out;
  wire [11:0] multiplexer_3_out;
  wire [12:0] CNT_num;
  wire [15:0] \总周期数 ;
  wire [31:0] adder_1_out, adder_2_out, adder_3_out, adder_4_out, alu_1_result, alu_1_result_2, aluresult,
       and_5_out, bit_extender_1_out, bit_extender_2_out, bit_extender_3_out, bit_extender_4_out,
       bit_extender_5_out, EX_IR, ex_mem1_1_aluresult_out, ex_mem1_1_imm_out, id_ex1_1_b_out,
       id_ex1_1_imm_out, id_ex1_1_j_out, id_ex1_1_r1_out, id_ex1_1_r2_out, ID_IR, IF_IR, MEM_IR,
       mem_wb1_1_aluresult_out, mem_wb1_1_dout_out, mem_wb1_1_imm_out, multiplexer_4_out, multiplexer_5_out,
       multiplexer_6_out, multiplexer_8_out, multiplexer_9_out, multiplexer_10_out, multiplexer_11_out,
       multiplexer_12_out, ram_1_data, regifile_1_r1, regifile_1_r2, shifter_1_out, shifter_2_out, WB_IR;

  Button \u_总复位  (.out(RST));
  Button _1 (.out(IR1));
  Button _2 (.out(IR2));
  Button _3 (.out(IR3));
  // Probe on \总周期数 
  // Probe on \总周期数 
  Button \u_继续运行  (.out(Go));
  LED #(.active("true")) led_1 (.in(W1));
  LED #(.active("true")) led_2 (.in(W2));
  LED #(.active("true")) led_3 (.in(W3));
  Hex_Digit_Display hex_digit_display_1 (.value(LedData[31:28]));  // open: dp
  // Probe on IF_PC[19:0]
  // RiscV_Probe riscv_probe_1: pin names not known; wires that end beside it: IF_IR
  or or_1 (or_1_out, not_1_out, Go);
  not not_1 (not_1_out, halt);
  Hex_Digit_Display hex_digit_display_2 (.value(LedData[23:20]));  // open: dp
  Hex_Digit_Display hex_digit_display_3 (.value(LedData[27:24]));  // open: dp
  // Probe on ID_PC[19:0]
  // RiscV_Probe riscv_probe_2: pin names not known; wires that end beside it: ID_IR
  not not_2 (not_2_out, halt);
  or or_2 (or_2_out, not_2_out, Go);
  Register #(.width(32), .trigger("rising"), .Select("low")) PC (
    .D(multiplexer_9_out), .en(or_1_out), .Q(IF_PC), .clk(CLK), .clr(RST));
  Hex_Digit_Display hex_digit_display_4 (.value(LedData[15:12]));  // open: dp
  Hex_Digit_Display hex_digit_display_5 (.value(LedData[19:16]));  // open: dp
  Counter #(.width(16), .max('hffff), .ongoal("wrap"), .trigger("rising"), .behavior("new")) counter_1 (
    .count(or_2_out), .Q(\总周期数 ), .clk(CLK), .clr(RST));  // open: load, D, carry, preset, down
  Hex_Digit_Display hex_digit_display_6 (.value(LedData[11:8]));  // open: dp
  Hex_Digit_Display hex_digit_display_7 (.value(LedData[7:4]));  // open: dp
  // Probe on EX_PC[19:0]
  // RiscV_Probe riscv_probe_3: pin names not known; wires that end beside it: EX_IR
  Hex_Digit_Display hex_digit_display_8 (.value(LedData[3:0]));  // open: dp
  ROM #(.addrWidth(10), .dataWidth(32), .Select("high")) rom_1 (.addr(IF_PC[11:2]), .data(IF_IR));
  Adder #(.width(32)) adder_1 (.a(IF_PC), .b(32'h4), .out(adder_1_out));  // open: cin, cout
  or or_3 (or_3_out, not_3_out, Go);
  not not_3 (not_3_out, halt);
  // Probe on \总周期数 
  // Probe on M_PC[19:0]
  // RiscV_Probe riscv_probe_4: pin names not known; wires that end beside it: MEM_IR
  IF_ID1 if_id1_1 (.IR_IN(IF_IR), .IR_OUT(ID_IR), .RST(RST), .en(or_3_out), .CLK(CLK), .PC_IN(IF_PC), .PC_OUT(ID_PC));
  // Probe on \总周期数 
  // Probe on {16{1'b0}}
  // Probe on {16{1'b0}}
  // Probe on {16{1'b0}}
  // Probe on {16{1'b0}}
  // RiscV_Probe riscv_probe_5: pin names not known; wires that end beside it: ID_IR, riscv_probe_5_p2
  // Probe on IF_PC[11:0]
  // Probe on WB_PC[19:0]
  // RiscV_Probe riscv_probe_6: pin names not known; wires that end beside it: WB_IR
  // Probe on ID_PC[11:0]
  // Probe on EX_PC[11:0]
  // Probe on M_PC[11:0]
  D_Flip_Flop #(.trigger("high"), .Pre_Clr_Positions("LEGACY"), .NegatePresetClear("false"), .enable("true"), .NewFFLayout("false")) d_ff_1 (.Q(d_ff_1_q));  // open: clk, D, Qn, preset, en, reset
  // Probe on 13'hc
  \单周期硬布线控制器  \u_单周期硬布线控制器_1  (
    .Funct({ID_IR[30], ID_IR[25], ID_IR[14:12]}), .OP(ID_IR[6:2]), .ALU_OP(\单周期硬布线控制器_1_alu_op ),
    .MemToReg(\单周期硬布线控制器_1_memtoreg ), .MemWrite(\单周期硬布线控制器_1_memwrite ), .ALU_SRC(\单周期硬布线控制器_1_alu_src ),
    .RegWrite(\单周期硬布线控制器_1_regwrite ), .ecall(ecall), .S_type(S_type), .Jalr(\单周期硬布线控制器_1_jalr ),
    .Beq(\单周期硬布线控制器_1_beq ), .JAL(\单周期硬布线控制器_1_jal ), .Bne(\单周期硬布线控制器_1_bne ), .in_3(ID_IR[21]),
    .uret(riscv_probe_5_p2), .BGEU(\单周期硬布线控制器_1_bgeu ));
  Multiplexer #(.select(1), .width(5), .disabled("Z"), .enable("false")) multiplexer_1 (
    .in0(ID_IR[19:15]), .in1(5'b10001), .out(multiplexer_1_out), .sel(ecall));
  Multiplexer #(.select(1), .width(5), .disabled("Z"), .enable("false")) multiplexer_2 (
    .in0(ID_IR[24:20]), .in1(5'b01010), .out(multiplexer_2_out), .sel(ecall));
  Multiplexer #(.select(1), .width(12), .disabled("Z"), .enable("false")) multiplexer_3 (
    .in0(ID_IR[31:20]), .in1({ID_IR[31:25], ID_IR[11:7]}), .out(multiplexer_3_out), .sel(S_type));
  assign bit_extender_1_out = {{20{ID_IR[31]}}, {ID_IR[31], ID_IR[7], ID_IR[30:25], ID_IR[11:8]}};  // Bit_Extender bit_extender_1
  assign bit_extender_2_out = {{12{ID_IR[31]}}, {ID_IR[31], ID_IR[19:12], ID_IR[20], ID_IR[30:21]}};  // Bit_Extender bit_extender_2
  // Probe on WB_PC[11:0]
  Comparator #(.width(13), .mode("twosComplement")) comparator_1 (
    .a(CNT_num), .b(13'hc), .eq(comparator_1_eq), .lt(comparator_1_lt));  // open: gt
  Clock #(.highDuration(1), .lowDuration(1)) clock_1 (.out(clock_1_out));
  assign bit_extender_3_out = {{20{multiplexer_3_out[11]}}, multiplexer_3_out};  // Bit_Extender bit_extender_3
  Shifter #(.width(32), .shift("ll")) shifter_1 (.in(bit_extender_1_out), .\dist (5'b00001), .out(shifter_1_out));
  Shifter #(.width(32), .shift("ll")) shifter_2 (.in(bit_extender_2_out), .\dist (5'b00001), .out(shifter_2_out));
  nand nand_1 (nand_1_out, d_ff_1_q, comparator_1_eq);
  Counter #(.width(13), .max('h1fff), .ongoal("stay"), .trigger("rising"), .behavior("old")) counter_2 (
    .count(comparator_1_lt), .Q(CNT_num), .clk(clock_1_out));  // open: load, D, carry, clr, preset
  Regifile regifile_1 (
    .Din(RDin), .Clk(CLK), .R1(regifile_1_r1), .R2(regifile_1_r2), .WE(RegWrite), .W_num(mem_wb1_1_w_out),
    .R1_num(multiplexer_1_out), .R2_num(multiplexer_2_out));
  assign CLK = nand_1_out ? clock_1_out : 1'bz;  // Controlled_Buffer controlled_buffer_1
  ID_EX1 id_ex1_1 (
    .JAL_IN(\单周期硬布线控制器_1_jal ), .JALR_IN(\单周期硬布线控制器_1_jalr ), .Beq_IN(\单周期硬布线控制器_1_beq ),
    .Bne_IN(\单周期硬布线控制器_1_bne ), .MemToReg_IN(\单周期硬布线控制器_1_memtoreg ), .MemWrite_IN(\单周期硬布线控制器_1_memwrite ),
    .AluOP_IN(\单周期硬布线控制器_1_alu_op ), .AluSrcB_IN(\单周期硬布线控制器_1_alu_src ), .R1_IN(regifile_1_r1),
    .R2_IN(regifile_1_r2), .IMM_IN(bit_extender_3_out), .JAL_OUT(JAL), .JALR_OUT(JALR),
    .Beq_OUT(id_ex1_1_beq_out), .Bne_OUT(id_ex1_1_bne_out), .MemToReg_OUT(id_ex1_1_memtoreg_out),
    .MemWrite_OUT(id_ex1_1_memwrite_out), .AluOP_OUT(id_ex1_1_aluop_out), .AluSrcB_OUT(AluSrcB),
    .R1_OUT(id_ex1_1_r1_out), .R2_OUT(id_ex1_1_r2_out), .IMM_OUT(id_ex1_1_imm_out), .RST(RST), .en(or_3_out),
    .CLK(CLK), .B_IN(shifter_1_out), .B_OUT(id_ex1_1_b_out), .J_IN(shifter_2_out), .J_OUT(id_ex1_1_j_out),
    .PC_IN(ID_PC), .PC_OUT(EX_PC), .W_IN(ID_IR[11:7]), .W_OUT(id_ex1_1_w_out), .IR_IN(ID_IR), .IR_OUT(EX_IR),
    .ECALL_IN(ecall), .ECALL_OUT(id_ex1_1_ecall_out), .RegWrite_IN(\单周期硬布线控制器_1_regwrite ),
    .RegWrite_OUT(id_ex1_1_regwrite_out), .BGEU_IN(\单周期硬布线控制器_1_bgeu ), .BGEU_OUT(BGEU));
  Pull_Resistor #(.pull(1)) pull_resistor_1 (.node(CLK));
  Multiplexer #(.select(1), .width(32), .disabled("Z"), .enable("false")) multiplexer_4 (
    .in0(id_ex1_1_r2_out), .in1(id_ex1_1_imm_out), .out(multiplexer_4_out), .sel(AluSrcB));
  and and_1 (and_1_out, equal, id_ex1_1_beq_out);
  not not_4 (not_4_out, equal);
  and and_2 (and_2_out, not_4_out, id_ex1_1_bne_out);
  Comparator #(.width(32), .mode("twosComplement")) comparator_2 (
    .a(32'h22), .b(id_ex1_1_r1_out), .eq(flag));  // open: gt, lt
  ALU alu_1 (
    .X(id_ex1_1_r1_out), .Y(multiplexer_4_out), .AluOP(id_ex1_1_aluop_out), .Equal(equal),
    .Result(alu_1_result), .Result_2(alu_1_result_2), .out_4(GE));  // open: out_6
  Adder #(.width(32)) adder_2 (.a(id_ex1_1_b_out), .b(EX_PC), .out(adder_2_out));  // open: cin, cout
  Multiplexer #(.select(1), .width(32), .disabled("Z"), .enable("false")) multiplexer_5 (
    .in0({32{1'b0}}), .in1(id_ex1_1_r2_out), .out(multiplexer_5_out), .sel(and_3_out));
  and and_3 (and_3_out, id_ex1_1_ecall_out, flag);
  and and_4 (and_4_out, GE, BGEU);
  Comparator #(.width(4), .mode("twosComplement")) comparator_3 (
    .a(id_ex1_1_aluop_out), .b(4'b0100), .eq(comparator_3_eq));  // open: gt, lt
  Multiplexer #(.select(1), .width(32), .disabled("Z"), .enable("false")) multiplexer_6 (
    .in0(adder_1_out), .in1(adder_2_out), .out(multiplexer_6_out), .sel(tunnel1));
  Adder #(.width(32)) adder_3 (.a(id_ex1_1_j_out), .b(EX_PC), .out(adder_3_out));  // open: cin, cout
  assign and_5_out = aluresult & 32'hfffffffe;  // AND_Gate and_5, 32 bits wide
  Register #(.width(32), .trigger("rising"), .Select("low")) register_1 (
    .D(multiplexer_5_out), .en(and_3_out), .Q(LedData), .clk(CLK), .clr(RST));
  and and_6 (and_6_out, id_ex1_1_ecall_out, not_5_out);
  not not_5 (not_5_out, flag);
  or or_4 (tunnel1, and_1_out, and_2_out, and_4_out);
  Multiplexer #(.select(1), .width(32), .disabled("Z"), .enable("false")) multiplexer_7 (
    .in0(alu_1_result), .in1(alu_1_result_2), .out(aluresult), .sel(comparator_3_eq));
  Multiplexer #(.select(1), .width(32), .disabled("Z"), .enable("false")) multiplexer_8 (
    .in0(multiplexer_6_out), .in1(adder_3_out), .out(multiplexer_8_out), .sel(JAL));
  Multiplexer #(.select(1), .width(32), .disabled("Z"), .enable("false")) multiplexer_9 (
    .in0(multiplexer_8_out), .in1(and_5_out), .out(multiplexer_9_out), .sel(JALR));
  Adder #(.width(32)) adder_4 (.a(EX_PC), .b(32'h4), .out(adder_4_out));  // open: cin, cout
  EX_MEM1 ex_mem1_1 (
    .JAL_IN(JAL), .JALR_IN(JALR), .MemToReg_IN(id_ex1_1_memtoreg_out), .MemWrite_IN(id_ex1_1_memwrite_out),
    .aluresult_IN(aluresult), .MA_IN(aluresult[11:2]), .MDin_IN(id_ex1_1_r2_out), .PC_IN(EX_PC),
    .JAL_OUT(ex_mem1_1_jal_out), .JALR_OUT(ex_mem1_1_jalr_out), .MemToReg_OUT(ex_mem1_1_memtoreg_out),
    .MemWrite_OUT(MemWrite), .aluresult_OUT(ex_mem1_1_aluresult_out), .MA_OUT(ex_mem1_1_ma_out),
    .MDin_OUT(MDin), .PC_OUT(M_PC), .RST(RST), .en(or_3_out), .CLK(CLK), .W_IN(id_ex1_1_w_out),
    .W_OUT(ex_mem1_1_w_out), .IR_IN(EX_IR), .IR_OUT(MEM_IR), .RegWrite_IN(id_ex1_1_regwrite_out),
    .RegWrite_OUT(ex_mem1_1_regwrite_out), .halt_IN(and_6_out), .halt_OUT(ex_mem1_1_halt_out),
    .IMM_IN(adder_4_out), .IMM_OUT(ex_mem1_1_imm_out), .HIGH_IN(aluresult[1]), .HIGH_OUT(ex_mem1_1_high_out));
  not not_6 (not_6_out, MemWrite);
  RAM #(.addrWidth(10), .dataWidth(32), .bus("separate"), .Select("high")) ram_1 (
    .addr(ex_mem1_1_ma_out), .din(MDin), .data(ram_1_data), .str(MemWrite), .clk(CLK), .ld(not_6_out));  // open: sel, clr
  assign bit_extender_4_out = {{16{1'b0}}, ram_1_data[15:0]};  // Bit_Extender bit_extender_4
  assign bit_extender_5_out = {{16{1'b0}}, ram_1_data[31:16]};  // Bit_Extender bit_extender_5
  Multiplexer #(.select(1), .width(32), .disabled("Z"), .enable("false")) multiplexer_10 (
    .in0(bit_extender_4_out), .in1(bit_extender_5_out), .out(multiplexer_10_out), .sel(ex_mem1_1_high_out));
  Comparator #(.width(3), .mode("twosComplement")) comparator_4 (
    .a(MEM_IR[14:12]), .b(3'b101), .eq(comparator_4_eq));  // open: gt, lt
  not not_7 (not_7_out, comparator_4_eq);
  MEM_WB1 mem_wb1_1 (
    .JAL_IN(ex_mem1_1_jal_out), .JALR_IN(ex_mem1_1_jalr_out), .MemToReg_IN(ex_mem1_1_memtoreg_out),
    .aluresult_IN(ex_mem1_1_aluresult_out), .Dout_IN(multiplexer_11_out), .PC_IN(M_PC),
    .JAL_OUT(mem_wb1_1_jal_out), .JALR_OUT(mem_wb1_1_jalr_out), .MemToReg_OUT(MemToReg),
    .aluresult_OUT(mem_wb1_1_aluresult_out), .Dout_OUT(mem_wb1_1_dout_out), .PC_OUT(WB_PC), .RST(RST),
    .en(or_3_out), .CLK(CLK), .W_IN(ex_mem1_1_w_out), .W_OUT(mem_wb1_1_w_out), .IR_IN(MEM_IR),
    .IR_OUT(WB_IR), .RegWrite_IN(ex_mem1_1_regwrite_out), .RegWrite_OUT(RegWrite),
    .halt_IN(ex_mem1_1_halt_out), .halt_OUT(halt), .IMM_IN(ex_mem1_1_imm_out), .IMM_OUT(mem_wb1_1_imm_out));
  Multiplexer #(.select(1), .width(32), .disabled("Z"), .enable("false")) multiplexer_11 (
    .in0(multiplexer_10_out), .in1(ram_1_data), .out(multiplexer_11_out), .sel(not_7_out));
  Multiplexer #(.select(1), .width(32), .disabled("Z"), .enable("false")) multiplexer_12 (
    .in0(mem_wb1_1_aluresult_out), .in1(mem_wb1_1_dout_out), .out(multiplexer_12_out), .sel(MemToReg));
  or or_5 (or_5_out, mem_wb1_1_jalr_out, mem_wb1_1_jal_out);
  Multiplexer #(.select(1), .width(32), .disabled("Z"), .enable("false")) multiplexer_13 (
    .in0(multiplexer_12_out), .in1(mem_wb1_1_imm_out), .out(RDin), .sel(or_5_out));

  // Other names for the same wires on the sheet: MEM_PC[31:0] = M_PC

  // Notes on the sheet:
  //   中断源
  //   时空图监测，可删除
  //   中断等待指示
  //   数码管输出
  //   指令存储器
  //   contents of rom_1 (hex, n*v repeats v):
  //   413 493 913 993 46413 14e493 296913 39e993 842023 942223 1242423 1342623 a00893 493 913 993 73
  //   指令探针
  //   指令字
  //   控制位
  //   JAL
  //   JALR
  //   URET
  //   流水调试日志用
  //   暂停节拍，不能为0
  //   Beq
  //   Bne
  //   MemToReg
  //   MemWrite
  //   AluOP
  //   AluSrcB
  //   RegWrite
  //   戳工具置1进入计数暂停模式，ctrl+k时钟自动运行到对应节拍暂停
  //   ctrl+k关闭时钟连续运行，将控制位置零，进入单步调试模式调试
  //   用这个时钟源需要去掉电路中的其他时钟源
  //   可计数暂停的时钟源
  //   为方便自动评测，需要输出流水线各段保存的PC值，注意是PC不是PC+4，另外ID段寄存器写入信息，Mem段内存写入信息也要输出
  //   数据存储器
endmodule
module \重定向流水线  (
  output RegWrite,
  output MemWrite,
  output [31:0] IF_PC,
  output [31:0] ID_PC,
  output [31:0] EX_PC,
  output [31:0] M_PC,
  output [31:0] WB_PC,
  output [31:0] RDin,
  output [31:0] MDin,
  output [31:0] LedData
);

  wire AluSrcB, and_1_out, and_2_out, and_3_out, and_4_out, and_5_out, and_6_out, and_8_out, BGEU, branch,
       clash, CLK, clock_1_out, comparator_1_eq, comparator_1_lt, comparator_3_eq, comparator_5_eq, d_ff_1_q,
       ecall, equal, ex_mem2_1_halt_out, ex_mem2_1_high_out, ex_mem2_1_jal_out, ex_mem2_1_jalr_out,
       ex_memtoreg, EX_rw, flag, GE, Go, halt, id_ex3_1_beq_out, id_ex3_1_bne_out, id_ex3_1_ecall_out,
       id_ex3_1_memwrite_out, IR1, IR2, IR3, JAL, JALR, mem_memtoreg, MEM_rw, mem_wb2_1_jal_out,
       mem_wb2_1_jalr_out, MemToReg, nand_1_out, not_1_out, not_2_out, not_3_out, not_4_out, not_5_out,
       not_6_out, not_7_out, not_8_out, not_9_out, not_10_out, or_1_out, or_2_out, or_3_out, or_4_out,
       or_5_out, or_8_out, or_9_out, or_10_out, or_11_out, riscv_probe_6_p2, RST, S_type, tunnel1, W1, W2,
       W3, \单周期硬布线控制器_1_alu_src , \单周期硬布线控制器_1_beq , \单周期硬布线控制器_1_bgeu , \单周期硬布线控制器_1_bne ,
       \单周期硬布线控制器_1_jal , \单周期硬布线控制器_1_jalr , \单周期硬布线控制器_1_memtoreg , \单周期硬布线控制器_1_memwrite ,
       \单周期硬布线控制器_1_regwrite ;
  wire [1:0] id_ex3_1_r1forward_out, id_ex3_1_r2forward_out, r1_forward, r2_forward;
  wire [3:0] id_ex3_1_aluop_out, \单周期硬布线控制器_1_alu_op ;
  wire [4:0] EX_W, funct, MEM_W, mem_wb2_1_w_out, R1_num, R2_num;
  wire [9:0] ex_mem2_1_ma_out;
  wire [11:0] multiplexer_2_out;
  wire [12:0] CNT_num;
  wire [15:0] \LoadUse次数 , \总周期数 , \插入气泡数 , \无条件分支数 , \条件分支成功数 ;
  wire [31:0] adder_1_out, adder_2_out, adder_3_out, adder_4_out, alu_1_result, alu_1_result_2, aluresult,
       and_7_out, bit_extender_1_out, bit_extender_2_out, bit_extender_3_out, bit_extender_4_out,
       bit_extender_5_out, EX_IR, ex_mem2_1_aluresult_out, ex_mem2_1_imm_out, id_ex3_1_b_out,
       id_ex3_1_imm_out, id_ex3_1_j_out, id_ex3_1_r1_out, id_ex3_1_r2_out, ID_IR, IF_IR, MEM_IR,
       mem_wb2_1_aluresult_out, mem_wb2_1_dout_out, mem_wb2_1_imm_out, multiplexer_4_out, multiplexer_5_out,
       multiplexer_6_out, multiplexer_7_out, multiplexer_8_out, multiplexer_9_out, multiplexer_10_out,
       multiplexer_13_out, multiplexer_14_out, multiplexer_15_out, new_1, ram_1_data, regifile_1_r1,
       regifile_1_r2, shifter_1_out, shifter_2_out, WB_IR;

  Button \u_总复位  (.out(RST));
  Button _1 (.out(IR1));
  Button _2 (.out(IR2));
  Button _3 (.out(IR3));
  // Probe on \总周期数 
  // Probe on \总周期数 
  Button \u_继续运行  (.out(Go));
  LED #(.active("true")) led_1 (.in(W1));
  LED #(.active("true")) led_2 (.in(W2));
  LED #(.active("true")) led_3 (.in(W3));
  Hex_Digit_Display hex_digit_display_1 (.value(LedData[31:28]));  // open: dp
  // Probe on IF_PC[19:0]
  // RiscV_Probe riscv_probe_1: pin names not known; wires that end beside it: IF_IR
  Counter #(.width(16), .max('hffff), .ongoal("wrap"), .trigger("rising"), .behavior("new")) counter_1 (
    .count(tunnel1), .Q(\条件分支成功数 ), .clk(CLK), .clr(RST));  // open: load, D, carry, preset, down
  Hex_Digit_Display hex_digit_display_2 (.value(LedData[23:20]));  // open: dp
  Hex_Digit_Display hex_digit_display_3 (.value(LedData[27:24]));  // open: dp
  // Probe on ID_PC[19:0]
  // RiscV_Probe riscv_probe_2: pin names not known; wires that end beside it: {ID_IR[31], funct[4], ID_IR[29:26], funct[3], ID_IR[24:15], funct[2:0], ID_IR[11:0]}
  Counter #(.width(16), .max('hffff), .ongoal("wrap"), .trigger("rising"), .behavior("new")) counter_2 (
    .Q(\插入气泡数 ), .clk(clash), .clr(RST));  // open: load, D, count, carry, preset, down
  Hex_Digit_Display hex_digit_display_4 (.value(LedData[15:12]));  // open: dp
  Hex_Digit_Display hex_digit_display_5 (.value(LedData[19:16]));  // open: dp
  and and_1 (and_1_out, or_1_out, not_1_out);
  not not_1 (not_1_out, clash);
  or or_1 (or_1_out, not_2_out, Go);
  not not_2 (not_2_out, halt);
  Hex_Digit_Display hex_digit_display_6 (.value(LedData[7:4]));  // open: dp
  Hex_Digit_Display hex_digit_display_7 (.value(LedData[11:8]));  // open: dp
  // Probe on EX_PC[19:0]
  // RiscV_Probe riscv_probe_3: pin names not known; wires that end beside it: EX_IR
  not not_3 (not_3_out, halt);
  or or_2 (or_2_out, not_3_out, Go);
  Counter #(.width(16), .max('hffff), .ongoal("wrap"), .trigger("rising"), .behavior("new")) counter_3 (
    .count(or_2_out), .Q(\总周期数 ), .clk(CLK), .clr(RST));  // open: load, D, carry, preset, down
  Register #(.width(32), .trigger("rising"), .Select("low")) PC (
    .D(multiplexer_10_out), .en(and_1_out), .Q(IF_PC), .clk(CLK), .clr(RST));
  Hex_Digit_Display hex_digit_display_8 (.value(LedData[3:0]));  // open: dp
  Counter #(.width(16), .max('hffff), .ongoal("wrap"), .trigger("rising"), .behavior("new")) counter_4 (
    .Q(\无条件分支数 ), .clk(or_3_out), .clr(RST));  // open: load, D, count, carry, preset, down
  or or_3 (or_3_out, JAL, JALR);
  // Probe on \总周期数 
  // Probe on M_PC[19:0]
  // RiscV_Probe riscv_probe_4: pin names not known; wires that end beside it: MEM_IR
  ROM #(.addrWidth(10), .dataWidth(32), .Select("high")) rom_1 (.addr(IF_PC[11:2]), .data(IF_IR));
  Adder #(.width(32)) adder_1 (.a(IF_PC), .b(32'h4), .out(adder_1_out));  // open: cin, cout
  not not_4 (not_4_out, clash);
  or or_4 (or_4_out, not_5_out, Go);
  not not_5 (not_5_out, halt);
  // Probe on \总周期数 
  // Probe on \无条件分支数 
  // Probe on \条件分支成功数 
  // Probe on \插入气泡数 
  // Probe on \LoadUse次数 
  IF_ID2 if_id2_1 (
    .IR_IN(IF_IR), .PC_IN(IF_PC),
    .IR_OUT({ID_IR[31], funct[4], ID_IR[29:26], funct[3], ID_IR[24:15], funct[2:0], ID_IR[11:0]}),
    .PC_OUT(ID_PC), .CLR(branch), .RST(RST), .en(and_2_out), .CLK(CLK));  // open: PREDICTJUMP_IN, PREDICTJUMP_OUT
  and and_2 (and_2_out, not_4_out, or_4_out);
  // Probe on IF_PC[11:0]
  // Probe on WB_PC[19:0]
  // RiscV_Probe riscv_probe_5: pin names not known; wires that end beside it: WB_IR
  // Probe on ID_PC[11:0]
  // Probe on EX_PC[11:0]
  // RiscV_Probe riscv_probe_6: pin names not known; wires that end beside it: {ID_IR[31], funct[4], ID_IR[29:26], funct[3], ID_IR[24:15], funct[2:0], ID_IR[11:0]}, riscv_probe_6_p2
  // Probe on M_PC[11:0]
  D_Flip_Flop #(.trigger("high"), .Pre_Clr_Positions("LEGACY"), .NegatePresetClear("false"), .enable("true"), .NewFFLayout("false")) d_ff_1 (.Q(d_ff_1_q));  // open: clk, D, Qn, preset, en, reset
  // Probe on 13'hc
  Counter #(.width(16), .max('hffff), .ongoal("wrap"), .trigger("rising"), .behavior("new")) counter_5 (
    .Q(\LoadUse次数 ), .clk(clash), .clr(RST));  // open: load, D, count, carry, preset, down
  // Probe on WB_PC[11:0]
  Comparator #(.width(13), .mode("twosComplement")) comparator_1 (
    .a(CNT_num), .b(13'hc), .eq(comparator_1_eq), .lt(comparator_1_lt));  // open: gt
  Clock #(.highDuration(1), .lowDuration(1)) clock_1 (.out(clock_1_out));
  \单周期硬布线控制器  \u_单周期硬布线控制器_1  (
    .Funct(funct), .OP(ID_IR[6:2]), .ALU_OP(\单周期硬布线控制器_1_alu_op ), .MemToReg(\单周期硬布线控制器_1_memtoreg ),
    .MemWrite(\单周期硬布线控制器_1_memwrite ), .ALU_SRC(\单周期硬布线控制器_1_alu_src ), .RegWrite(\单周期硬布线控制器_1_regwrite ),
    .ecall(ecall), .S_type(S_type), .Jalr(\单周期硬布线控制器_1_jalr ), .Beq(\单周期硬布线控制器_1_beq ),
    .JAL(\单周期硬布线控制器_1_jal ), .Bne(\单周期硬布线控制器_1_bne ), .in_3(ID_IR[21]), .uret(riscv_probe_6_p2),
    .BGEU(\单周期硬布线控制器_1_bgeu ));
  Multiplexer #(.select(1), .width(5), .disabled("Z"), .enable("false")) multiplexer_1 (
    .in0(ID_IR[24:20]), .in1(5'b01010), .out(R2_num), .sel(ecall));
  Multiplexer #(.select(1), .width(12), .disabled("Z"), .enable("false")) multiplexer_2 (
    .in0({ID_IR[31], funct[4], ID_IR[29:26], funct[3], ID_IR[24:20]}),
    .in1({ID_IR[31], funct[4], ID_IR[29:26], funct[3], ID_IR[11:7]}), .out(multiplexer_2_out), .sel(S_type));
  nand nand_1 (nand_1_out, d_ff_1_q, comparator_1_eq);
  Counter #(.width(13), .max('h1fff), .ongoal("stay"), .trigger("rising"), .behavior("old")) counter_6 (
    .count(comparator_1_lt), .Q(CNT_num), .clk(clock_1_out));  // open: load, D, carry, clr, preset
  Multiplexer #(.select(1), .width(5), .disabled("Z"), .enable("false")) multiplexer_3 (
    .in0(ID_IR[19:15]), .in1(5'b10001), .out(R1_num), .sel(ecall));
  assign bit_extender_1_out = {{20{ID_IR[31]}}, {ID_IR[31], ID_IR[7], funct[4], ID_IR[29:26], funct[3], ID_IR[11:8]}};  // Bit_Extender bit_extender_1
  Shifter #(.width(32), .shift("ll")) shifter_1 (.in(bit_extender_1_out), .\dist (5'b00001), .out(shifter_1_out));
  assign bit_extender_2_out = {{12{ID_IR[31]}}, {ID_IR[31], ID_IR[19:15], funct[2:0], ID_IR[20], funct[4], ID_IR[29:26], funct[3], ID_IR[24:21]}};  // Bit_Extender bit_extender_2
  assign CLK = nand_1_out ? clock_1_out : 1'bz;  // Controlled_Buffer controlled_buffer_1
  Regifile regifile_1 (
    .Din(RDin), .Clk(CLK), .R1(regifile_1_r1), .R2(regifile_1_r2), .WE(RegWrite), .W_num(mem_wb2_1_w_out),
    .R1_num(R1_num), .R2_num(R2_num));
  assign bit_extender_3_out = {{20{multiplexer_2_out[11]}}, multiplexer_2_out};  // Bit_Extender bit_extender_3
  Shifter #(.width(32), .shift("ll")) shifter_2 (.in(bit_extender_2_out), .\dist (5'b00001), .out(shifter_2_out));
  REDIRECT redirect_1 (
    .R1_num(R1_num), .EX_W_num(EX_W), .EX_RegWrite(EX_rw), .R2_num(R2_num), .EX_MEMTOREG(ex_memtoreg),
    .OP(ID_IR[6:2]), .MEM_W_num(MEM_W), .MEM_RegWrite(MEM_rw), .R1_FORWARD(r1_forward), .clash(clash),
    .R2_FORWARD(r2_forward), .funct3(funct[2:0]));
  Pull_Resistor #(.pull(1)) pull_resistor_1 (.node(CLK));
  or or_5 (or_5_out, branch, clash);
  ID_EX3 id_ex3_1 (
    .JAL(\单周期硬布线控制器_1_jal ), .JALR(\单周期硬布线控制器_1_jalr ), .BEQ(\单周期硬布线控制器_1_beq ), .BNE(\单周期硬布线控制器_1_bne ),
    .MEMTOREG(\单周期硬布线控制器_1_memtoreg ), .MEMWRITE(\单周期硬布线控制器_1_memwrite ), .ALUOP(\单周期硬布线控制器_1_alu_op ),
    .ALUSRC(\单周期硬布线控制器_1_alu_src ), .REGWRITE(\单周期硬布线控制器_1_regwrite ), .ECALL(ecall), .R1(regifile_1_r1),
    .R1FORWARD(r1_forward), .R2(regifile_1_r2), .R2FORWARD(r2_forward), .W_num(ID_IR[11:7]),
    .IMM(bit_extender_3_out), .B(shifter_1_out),
    .IR({ID_IR[31], funct[4], ID_IR[29:26], funct[3], ID_IR[24:15], funct[2:0], ID_IR[11:0]}),
    .J(shifter_2_out), .PC(ID_PC), .JAL_OUT(JAL), .JALR_OUT(JALR), .BEQ_OUT(id_ex3_1_beq_out),
    .BNE_OUT(id_ex3_1_bne_out), .MEMTOREG_OUT(ex_memtoreg), .MEMWRITE_OUT(id_ex3_1_memwrite_out),
    .ALUOP_OUT(id_ex3_1_aluop_out), .ALUSRC_OUT(AluSrcB), .REGWRITE_OUT(EX_rw),
    .ECALL_OUT(id_ex3_1_ecall_out), .R1_OUT(id_ex3_1_r1_out), .R1FORWARD_OUT(id_ex3_1_r1forward_out),
    .R2_OUT(id_ex3_1_r2_out), .R2FORWARD_OUT(id_ex3_1_r2forward_out), .W__OUT(EX_W),
    .IMM_OUT(id_ex3_1_imm_out), .B_OUT(id_ex3_1_b_out), .IR_OUT(EX_IR), .J_OUT(id_ex3_1_j_out),
    .PC_OUT(EX_PC), .CLK(CLK), .RST(RST), .CLR(or_5_out), .EN(or_9_out), .BGEU_IN(\单周期硬布线控制器_1_bgeu ),
    .BGEU_OUT(BGEU));  // open: PREDICTJUMP_IN, PREDICTJUMP_OUT, URET_IN, URET_OUT
  and and_3 (and_3_out, equal, id_ex3_1_beq_out);
  not not_6 (not_6_out, equal);
  Multiplexer #(.select(1), .width(32), .disabled("Z"), .enable("false")) multiplexer_4 (
    .in0({32{1'b0}}), .in1(multiplexer_6_out), .out(multiplexer_4_out), .sel(and_4_out));
  and and_4 (and_4_out, id_ex3_1_ecall_out, flag);
  and and_5 (and_5_out, not_6_out, id_ex3_1_bne_out);
  Multiplexer #(.select(2), .width(32), .disabled("Z"), .enable("false")) multiplexer_5 (
    .in0(id_ex3_1_r1_out), .in1(new_1), .in2(RDin), .in3(RDin), .out(multiplexer_5_out),
    .sel(id_ex3_1_r1forward_out));
  Multiplexer #(.select(2), .width(32), .disabled("Z"), .enable("false")) multiplexer_6 (
    .in0(id_ex3_1_r2_out), .in1(new_1), .in2(RDin), .in3(RDin), .out(multiplexer_6_out),
    .sel(id_ex3_1_r2forward_out));
  Multiplexer #(.select(1), .width(32), .disabled("Z"), .enable("false")) multiplexer_7 (
    .in0(adder_1_out), .in1(adder_2_out), .out(multiplexer_7_out), .sel(tunnel1));
  Adder #(.width(32)) adder_2 (.a(id_ex3_1_b_out), .b(EX_PC), .out(adder_2_out));  // open: cin, cout
  Adder #(.width(32)) adder_3 (.a(id_ex3_1_j_out), .b(EX_PC), .out(adder_3_out));  // open: cin, cout
  or or_6 (branch, JALR, JAL, tunnel1);
  not not_7 (not_7_out, flag);
  or or_7 (tunnel1, and_3_out, and_5_out, and_6_out);
  and and_6 (and_6_out, BGEU, GE);
  Comparator #(.width(32), .mode("twosComplement")) comparator_2 (
    .a(32'h22), .b(multiplexer_5_out), .eq(flag));  // open: gt, lt
  Multiplexer #(.select(1), .width(32), .disabled("Z"), .enable("false")) multiplexer_8 (
    .in0(multiplexer_6_out), .in1(id_ex3_1_imm_out), .out(multiplexer_8_out), .sel(AluSrcB));
  Multiplexer #(.select(1), .width(32), .disabled("Z"), .enable("false")) multiplexer_9 (
    .in0(multiplexer_7_out), .in1(adder_3_out), .out(multiplexer_9_out), .sel(JAL));
  assign and_7_out = aluresult & 32'hfffffffe;  // AND_Gate and_7, 32 bits wide
  Register #(.width(32), .trigger("rising"), .Select("low")) register_1 (
    .D(multiplexer_4_out), .en(and_4_out), .Q(LedData), .clk(CLK), .clr(RST));
  and and_8 (and_8_out, id_ex3_1_ecall_out, not_7_out);
  ALU alu_1 (
    .X(multiplexer_5_out), .Y(multiplexer_8_out), .AluOP(id_ex3_1_aluop_out), .Equal(equal),
    .Result(alu_1_result), .Result_2(alu_1_result_2), .out_4(GE));  // open: out_6
  Multiplexer #(.select(1), .width(32), .disabled("Z"), .enable("false")) multiplexer_10 (
    .in0(multiplexer_9_out), .in1(and_7_out), .out(multiplexer_10_out), .sel(JALR));
  Comparator #(.width(4), .mode("twosComplement")) comparator_3 (
    .a(id_ex3_1_aluop_out), .b(4'b0100), .eq(comparator_3_eq));  // open: gt, lt
  Adder #(.width(32)) adder_4 (.a(EX_PC), .b(32'h4), .out(adder_4_out));  // open: cin, cout
  Comparator #(.width(20), .mode("twosComplement")) comparator_4 (.a(IF_PC[19:0]), .b(20'h2f0));  // open: gt, eq, lt
  or or_8 (or_8_out, 1'b0, and_8_out);
  Multiplexer #(.select(1), .width(32), .disabled("Z"), .enable("false")) multiplexer_11 (
    .in0(alu_1_result), .in1(alu_1_result_2), .out(aluresult), .sel(comparator_3_eq));
  EX_MEM2 ex_mem2_1 (
    .JAL_IN(JAL), .JALR_IN(JALR), .halt_IN(or_8_out), .MemToReg_IN(ex_memtoreg),
    .MemWrite_IN(id_ex3_1_memwrite_out), .RegWrite_IN(EX_rw), .aluresult_IN(aluresult),
    .MA_IN(aluresult[11:2]), .MDin_IN(multiplexer_6_out), .W_IN(EX_W), .PC_IN(EX_PC), .IR_IN(EX_IR),
    .IMM_IN(adder_4_out), .JAL_OUT(ex_mem2_1_jal_out), .JALR_OUT(ex_mem2_1_jalr_out),
    .halt_OUT(ex_mem2_1_halt_out), .MemToReg_OUT(mem_memtoreg), .MemWrite_OUT(MemWrite),
    .RegWrite_OUT(MEM_rw), .aluresult_OUT(ex_mem2_1_aluresult_out), .MA_OUT(ex_mem2_1_ma_out),
    .MDin_OUT(MDin), .W_OUT(MEM_W), .PC_OUT(M_PC), .IR_OUT(MEM_IR), .IMM_OUT(ex_mem2_1_imm_out), .CLR(1'b0),
    .RST(RST), .en(or_9_out), .CLK(CLK), .HIGH_IN(aluresult[1]), .HIGH_OUT(ex_mem2_1_high_out));
  or or_9 (or_9_out, not_8_out, Go);
  not not_8 (not_8_out, halt);
  or or_10 (or_10_out, ex_mem2_1_jal_out, ex_mem2_1_jalr_out);
  Multiplexer #(.select(1), .width(32), .disabled("Z"), .enable("false")) multiplexer_12 (
    .in0(ex_mem2_1_aluresult_out), .in1(ex_mem2_1_imm_out), .out(new_1), .sel(or_10_out));
  RAM #(.addrWidth(10), .dataWidth(32), .bus("separate"), .Select("high")) ram_1 (
    .addr(ex_mem2_1_ma_out), .din(MDin), .data(ram_1_data), .str(MemWrite), .clk(CLK), .ld(not_9_out));  // open: sel, clr
  not not_9 (not_9_out, MemWrite);
  assign bit_extender_4_out = {{16{1'b0}}, ram_1_data[15:0]};  // Bit_Extender bit_extender_4
  Multiplexer #(.select(1), .width(32), .disabled("Z"), .enable("false")) multiplexer_13 (
    .in0(bit_extender_4_out), .in1(bit_extender_5_out), .out(multiplexer_13_out), .sel(ex_mem2_1_high_out));
  assign bit_extender_5_out = {{16{1'b0}}, ram_1_data[31:16]};  // Bit_Extender bit_extender_5
  Comparator #(.width(3), .mode("twosComplement")) comparator_5 (
    .a(MEM_IR[14:12]), .b(3'b101), .eq(comparator_5_eq));  // open: gt, lt
  not not_10 (not_10_out, comparator_5_eq);
  Multiplexer #(.select(1), .width(32), .disabled("Z"), .enable("false")) multiplexer_14 (
    .in0(multiplexer_13_out), .in1(ram_1_data), .out(multiplexer_14_out), .sel(not_10_out));
  MEM_WB2 mem_wb2_1 (
    .JAL_IN(ex_mem2_1_jal_out), .JALR_IN(ex_mem2_1_jalr_out), .halt_IN(ex_mem2_1_halt_out),
    .MemToReg_IN(mem_memtoreg), .RegWrite_IN(MEM_rw), .aluresult_IN(ex_mem2_1_aluresult_out),
    .Dout_IN(multiplexer_14_out), .W_IN(MEM_W), .IR_IN(MEM_IR), .PC_IN(M_PC), .IMM_IN(ex_mem2_1_imm_out),
    .JAL_OUT(mem_wb2_1_jal_out), .JALR_OUT(mem_wb2_1_jalr_out), .halt_OUT(halt), .MemToReg_OUT(MemToReg),
    .RegWrite_OUT(RegWrite), .aluresult_OUT(mem_wb2_1_aluresult_out), .Dout_OUT(mem_wb2_1_dout_out),
    .W_OUT(mem_wb2_1_w_out), .IR_OUT(WB_IR), .PC_OUT(WB_PC), .IMM_OUT(mem_wb2_1_imm_out), .CLR(1'b0),
    .RST(RST), .en(or_9_out), .CLK(CLK));
  or or_11 (or_11_out, mem_wb2_1_jalr_out, mem_wb2_1_jal_out);
  Multiplexer #(.select(1), .width(32), .disabled("Z"), .enable("false")) multiplexer_15 (
    .in0(mem_wb2_1_aluresult_out), .in1(mem_wb2_1_dout_out), .out(multiplexer_15_out), .sel(MemToReg));
  Multiplexer #(.select(1), .width(32), .disabled("Z"), .enable("false")) multiplexer_16 (
    .in0(multiplexer_15_out), .in1(mem_wb2_1_imm_out), .out(RDin), .sel(or_11_out));

  // Other names for the same wires on the sheet: ID_IR (some bits) = funct; op[4:0] = ID_IR[6:2]; MEM_PC[31:0] = M_PC

  // Notes on the sheet:
  //   中断源
  //   时空图监测，可删除
  //   中断等待指示
  //   数码管输出
  //   指令存储器
  //   contents of rom_1 (hex, n*v repeats v):
  //   100493 100006f 100493 200913 300993 100006f 100493 200913 300993 100006f 100493 200913 300993
  //   100006f 100493 200913 300993 3bc000ef 100413 100493 1f49493 900533 2200893 73 24d493 48463 fedff06f
  //   900533 2200893 73 100493 249493 900533 2200893 73 48463 fedff06f 100493 1f49493 900533 2200893 73
  //   4034d493 900533 2200893 73 4044d493 900533 2200893 73 4044d493 900533 2200893 73 4044d493 900533
  //   2200893 73 4044d493 900533 2200893 73 4044d493 900533 2200893 73 4044d493 900533 2200893 73 4044d493
  //   900533 2200893 73 100413 1f41993 41f9d993 433 c00913 300b13 140413 f47413 800293 100313 499993
  //   89e9b3 1300533 2200893 73 406282b3 fe0294e3 140413 f00f93 1f47433 1c41413 800293 100313 49d993
  //   89e9b3 1300533 2200893 73 406282b3 fe0294e3 1c45413 406b0b33 b0463 f95ff06f 2b3 fff2c293 829293
  //   ff2e293 500533 2200893 73 fff00413 493 84a023 140413 448493 84a023 140413 448493 84a023 140413
  //   448493 84a023 140413 448493 84a023 140413 448493 84a023 140413 448493 84a023 140413 448493 84a023
  //   140413 448493 84a023 140413 448493 84a023 140413 448493 84a023 140413 448493 84a023 140413 448493
  //   84a023 140413 448493 84a023 140413 448493 84a023 140413 448493 84a023 140413 448493 140413 433
  //   3c00493 42983 4aa03 149a2b3 28663 134a023 1442023 ffc48493 fe9412e3 800533 2200893 73 440413 3c00493
  //   fc9416e3 a00893 73 200293 1100493 849493 1148493 900533 2200893 73 2000e13 25484b3 900533 2200893 73
  //   fffe0e13 fe0e16e3 a00893 73 8800493 849493 4848493 8700913 891913 5490913 2997933 1091913 11096913
  //   1200533 2200893 73 a00893 73 313 1000e13 8400493 849493 8348493 400913 891913 490913 849493 8248493
  //   849493 8148493 891913 490913 891913 490913 932023 12484b3 430313 fffe0e13 fe0e18e3 2000e13 313 35483
  //   900533 2200893 73 230313 fffe0e13 fe0e14e3 a00893 73 f00493 100913 409909b3 900533 2200893 73
  //   fff48493 ff29f6e3 a00893 73 413 140413 800533 2200893 73 240413 800533 2200893 73 340413 800533
  //   2200893 73 440413 800533 2200893 73 540413 800533 2200893 73 640413 800533 2200893 73 740413 800533
  //   2200893 73 840413 800533 2200893 2200893 73 8067
  //   控制位
  //   指令探针
  //   指令字
  //   流水调试日志用
  //   暂停节拍，不能为0
  //   JAL
  //   JALR
  //   URET
  //   戳工具置1进入计数暂停模式，ctrl+k时钟自动运行到对应节拍暂停
  //   ctrl+k关闭时钟连续运行，将控制位置零，进入单步调试模式调试
  //   Beq
  //   Bne
  //   MemToReg
  //   MemWrite
  //   AluOP
  //   AluSrcB
  //   RegWrite
  //   重定向检测和进行
  //   可计数暂停的时钟源
  //   为方便自动评测，需要输出流水线各段保存的PC值，注意是PC不是PC+4，另外ID段寄存器写入信息，Mem段内存写入信息也要输出
  //   数据存储器
endmodule

module \中断按键参考电路  (
  input  \同步清零信号 ,
  output \与中断屏蔽位与 
);

  wire \_1号中断_out , and_1_out, clock_1_out, d_ff_1_q, or_1_out, or_2_out;

  Clock #(.highDuration(1), .lowDuration(1)) clock_1 (.out(clock_1_out));
  Button \_1号中断  (.out(\_1号中断_out ));
  LED #(.active("true")) \_1号中断等待指示灯  (.in(or_1_out));
  or or_1 (or_1_out, \与中断屏蔽位与 , d_ff_1_q);
  D_Flip_Flop #(.trigger("rising"), .Pre_Clr_Positions("LEGACY"), .NegatePresetClear("false"), .enable("true"), .NewFFLayout("false")) d_ff_1 (
    .clk(\_1号中断_out ), .D(1'b1), .Q(d_ff_1_q), .reset(\与中断屏蔽位与 ));  // open: Qn, preset, en
  or or_2 (or_2_out, d_ff_1_q, \与中断屏蔽位与 );
  and and_1 (and_1_out, or_2_out, ~\同步清零信号 );  // AND_Gate
  D_Flip_Flop #(.trigger("rising"), .Pre_Clr_Positions("LEGACY"), .NegatePresetClear("false"), .enable("true"), .NewFFLayout("false")) IR1 (
    .clk(clock_1_out), .D(and_1_out), .Q(\与中断屏蔽位与 ));  // open: Qn, preset, en, reset

  // Notes on the sheet:
  //   中断信号采样参考电路
  //   Reset 
endmodule

module \单周期_单级中断  (
  input  IR1,
  input  IR2,
  input  IR3,
  output RegWrite,
  output MemWrite,
  output [31:0] PC,
  output [31:0] IR,
  output [31:0] RDin,
  output [31:0] MDin,
  output [31:0] LedData
);

  wire AluSrcB, and_1_out, and_2_out, and_3_out, and_4_out, and_5_out, and_9_out, and_10_out, and_11_out,
       and_12_out, and_13_out, and_14_out, and_16_out, BGEU, CLK, clock_1_out, comparator_1_eq,
       comparator_2_eq, comparator_3_eq, comparator_4_eq, comparator_5_gt, comparator_5_lt, comparator_6_gt,
       comparator_6_lt, comparator_7_gt, comparator_8_eq, comparator_8_lt, comparator_10_eq,
       comparator_11_eq, d_ff_1_q, d_ff_2_q, d_ff_3_q, d_ff_4_q, ecall, equal, flag, GE, Go, halt, IE, IR1_q,
       IR1_t, IR2_q, IR2_t, IR3_q, IR3_t, IRA, IRB, IRC, JAL, JALR, MemToReg, nand_1_out, not_1_out,
       not_2_out, not_3_out, not_4_out, not_5_out, not_6_out, not_7_out, not_8_out, not_9_out, not_10_out,
       not_11_out, or_4_out, or_5_out, or_6_out, or_7_out, or_8_out, or_11_out, or_13_out, or_15_out, RST,
       S_type, tunnel1, URET, URETA, URETB, URETC, W1, W2, W3, \单周期硬布线控制器_1_beq , \单周期硬布线控制器_1_bne ;
  wire [1:0] priority_encoder_1_out;
  wire [3:0] \单周期硬布线控制器_1_alu_op ;
  wire [4:0] multiplexer_3_out, multiplexer_4_out;
  wire [11:0] multiplexer_5_out;
  wire [12:0] CNT_num;
  wire [15:0] \总周期数 ;
  wire [31:0] adder_1_out, adder_2_out, adder_3_out, adder_4_out, alu_1_result, alu_1_result_2, aluresult,
       and_15_out, bit_extender_1_out, bit_extender_2_out, bit_extender_3_out, bit_extender_4_out,
       bit_extender_5_out, EPC, EPC_IN, multiplexer_1_out, multiplexer_2_out, multiplexer_6_out,
       multiplexer_8_out, multiplexer_9_out, multiplexer_11_out, multiplexer_12_out, multiplexer_13_out,
       multiplexer_14_out, ram_1_data, regifile_1_r1, shifter_1_out, shifter_2_out;

  Button \u_继续运行  (.out(Go));
  Button _1 ();  // open: out
  Button _2 ();  // open: out
  Button _3 ();  // open: out
  LED #(.active("true")) led_1 (.in(W1));
  LED #(.active("true")) led_2 (.in(W2));
  LED #(.active("true")) led_3 (.in(W3));
  Hex_Digit_Display hex_digit_display_1 (.value(LedData[31:28]));  // open: dp
  Comparator #(.width(16), .mode("twosComplement")) comparator_1 (
    .a(16'h23c), .b(\总周期数 ), .eq(comparator_1_eq));  // open: gt, lt
  Comparator #(.width(16), .mode("twosComplement")) comparator_2 (
    .a(\总周期数 ), .b(16'h2), .eq(comparator_2_eq));  // open: gt, lt
  Comparator #(.width(16), .mode("twosComplement")) comparator_3 (
    .a(\总周期数 ), .b(16'h3), .eq(comparator_3_eq));  // open: gt, lt
  Comparator #(.width(16), .mode("twosComplement")) comparator_4 (
    .a(\总周期数 ), .b(16'h4), .eq(comparator_4_eq));  // open: gt, lt
  or or_1 (W1, IR1_q, d_ff_1_q);
  or or_2 (W2, IR2_q, d_ff_2_q);
  or or_3 (W3, IR3_q, d_ff_3_q);
  Hex_Digit_Display hex_digit_display_2 (.value(LedData[23:20]));  // open: dp
  Hex_Digit_Display hex_digit_display_3 (.value(LedData[27:24]));  // open: dp
  or or_4 (or_4_out, comparator_1_eq, comparator_2_eq);
  D_Flip_Flop #(.trigger("rising"), .Pre_Clr_Positions("LEGACY"), .NegatePresetClear("false"), .enable("true"), .NewFFLayout("false")) d_ff_1 (
    .clk(IRA), .D(1'b1), .Q(d_ff_1_q), .reset(IR1_q));  // open: Qn, preset, en
  D_Flip_Flop #(.trigger("rising"), .Pre_Clr_Positions("LEGACY"), .NegatePresetClear("false"), .enable("true"), .NewFFLayout("false")) d_ff_2 (
    .clk(IRB), .D(1'b1), .Q(d_ff_2_q), .reset(IR2_q));  // open: Qn, preset, en
  D_Flip_Flop #(.trigger("rising"), .Pre_Clr_Positions("LEGACY"), .NegatePresetClear("false"), .enable("true"), .NewFFLayout("false")) d_ff_3 (
    .clk(IRC), .D(1'b1), .Q(d_ff_3_q), .reset(IR3_q));  // open: Qn, preset, en
  or or_5 (or_5_out, W1, W2, W3);
  Hex_Digit_Display hex_digit_display_4 (.value(LedData[15:12]));  // open: dp
  Hex_Digit_Display hex_digit_display_5 (.value(LedData[19:16]));  // open: dp
  Pull_Resistor #(.pull(0)) pull_resistor_1 (.node(IRA));
  assign IRA = or_4_out ? ~CLK : 1'bz;  // Controlled_Inverter controlled_inverter_1
  Pull_Resistor #(.pull(0)) pull_resistor_2 (.node(IRB));
  assign IRB = comparator_3_eq ? ~CLK : 1'bz;  // Controlled_Inverter controlled_inverter_2
  Pull_Resistor #(.pull(0)) pull_resistor_3 (.node(IRC));
  assign IRC = comparator_4_eq ? ~CLK : 1'bz;  // Controlled_Inverter controlled_inverter_3
  or or_6 (or_6_out, d_ff_1_q, IR1_q);
  and and_1 (and_1_out, or_6_out, ~URETA);  // AND_Gate
  or or_7 (or_7_out, d_ff_2_q, IR2_q);
  or or_8 (or_8_out, d_ff_3_q, IR3_q);
  Comparator #(.width(32), .mode("twosComplement")) comparator_5 (
    .a(PC), .b(32'h31f4), .gt(comparator_5_gt), .lt(comparator_5_lt));  // open: eq
  Comparator #(.width(32), .mode("twosComplement")) comparator_6 (
    .a(PC), .b(32'h3150), .gt(comparator_6_gt), .lt(comparator_6_lt));  // open: eq
  Comparator #(.width(32), .mode("twosComplement")) comparator_7 (
    .a(PC), .b(32'h30ac), .gt(comparator_7_gt));  // open: eq, lt
  Hex_Digit_Display hex_digit_display_6 (.value(LedData[11:8]));  // open: dp
  Hex_Digit_Display hex_digit_display_7 (.value(LedData[7:4]));  // open: dp
  // Probe on \总周期数 
  D_Flip_Flop #(.trigger("rising"), .Pre_Clr_Positions("LEGACY"), .NegatePresetClear("false"), .enable("true"), .NewFFLayout("false")) u_IR1 (
    .clk(CLK), .D(and_1_out), .Q(IR1_q));  // open: Qn, preset, en, reset
  and and_2 (and_2_out, or_7_out, ~URETB);  // AND_Gate
  and and_3 (and_3_out, or_8_out, ~URETC);  // AND_Gate
  Register #(.width(1), .trigger("rising"), .Select("low")) register_1 (
    .D(or_5_out), .Q(IE), .clk(CLK), .clr(URET));  // open: en
  Hex_Digit_Display hex_digit_display_8 (.value(LedData[3:0]));  // open: dp
  D_Flip_Flop #(.trigger("rising"), .Pre_Clr_Positions("LEGACY"), .NegatePresetClear("false"), .enable("true"), .NewFFLayout("false")) u_IR2 (
    .clk(CLK), .D(and_2_out), .Q(IR2_q));  // open: Qn, preset, en, reset
  D_Flip_Flop #(.trigger("rising"), .Pre_Clr_Positions("LEGACY"), .NegatePresetClear("false"), .enable("true"), .NewFFLayout("false")) u_IR3 (
    .clk(CLK), .D(and_3_out), .Q(IR3_q));  // open: Qn, preset, en, reset
  and and_4 (and_4_out, comparator_5_lt, comparator_6_gt);
  and and_5 (and_5_out, comparator_6_lt, comparator_7_gt);
  Register #(.width(32), .trigger("rising"), .Select("low")) register_2 (
    .D(EPC_IN), .en(not_1_out), .Q(EPC), .clk(CLK));  // open: clr
  not not_1 (not_1_out, IE);
  and and_6 (URETC, URET, comparator_5_gt);
  and and_7 (URETB, URET, and_4_out);
  and and_8 (URETA, URET, and_5_out);
  or or_9 (IR1_t, IR1, IRA);
  and and_9 (and_9_out, W1, not_3_out);
  and and_10 (and_10_out, W2, not_2_out);
  not not_2 (not_2_out, IE);
  or or_10 (IR2_t, IR2, IRB);
  Multiplexer #(.select(2), .width(32), .disabled("Z"), .enable("false")) multiplexer_1 (
    .in0(EPC_IN), .in1(32'h30ac), .in2(32'h3150), .in3(32'h31f4), .out(multiplexer_1_out),
    .sel(priority_encoder_1_out));
  not not_3 (not_3_out, IE);
  Priority_Encoder #(.select(2), .disabled("Z")) priority_encoder_1 (
    .in0(1'b1), .in1(and_9_out), .in2(and_10_out), .in3(and_11_out), .out(priority_encoder_1_out));  // open: gs, en_out, en_in
  and and_11 (and_11_out, W3, not_4_out);
  not not_4 (not_4_out, IE);
  Button u_RST (.out(RST));
  not not_5 (not_5_out, halt);
  or or_11 (or_11_out, not_6_out, Go);
  not not_6 (not_6_out, halt);
  Multiplexer #(.select(1), .width(32), .disabled("Z"), .enable("false")) multiplexer_2 (
    .in0(multiplexer_1_out), .in1(EPC), .out(multiplexer_2_out), .sel(URET));
  or or_12 (IR3_t, IR3, IRC);
  or or_13 (or_13_out, not_5_out, Go);
  Counter #(.width(16), .max('hffff), .ongoal("wrap"), .trigger("rising"), .behavior("new")) counter_1 (
    .count(or_13_out), .Q(\总周期数 ), .clk(CLK), .clr(RST));  // open: load, D, carry, preset, down
  Register #(.width(32), .trigger("rising"), .Select("low")) u_PC (
    .D(multiplexer_2_out), .en(or_11_out), .Q(PC), .clk(CLK), .clr(RST));
  // RiscV_Probe riscv_probe_1: pin names not known; wires that end beside it: PC[11:2], IR
  ROM #(.addrWidth(10), .dataWidth(32), .Select("high")) rom_1 (.addr(PC[11:2]), .data(IR));
  \单周期硬布线控制器  \u_单周期硬布线控制器_1  (
    .Funct({IR[30], IR[25], IR[14:12]}), .OP(IR[6:2]), .ALU_OP(\单周期硬布线控制器_1_alu_op ), .MemToReg(MemToReg),
    .MemWrite(MemWrite), .ALU_SRC(AluSrcB), .RegWrite(RegWrite), .ecall(ecall), .S_type(S_type), .Jalr(JALR),
    .Beq(\单周期硬布线控制器_1_beq ), .JAL(JAL), .Bne(\单周期硬布线控制器_1_bne ), .in_3(IR[21]), .uret(URET), .BGEU(BGEU));
  Multiplexer #(.select(1), .width(5), .disabled("Z"), .enable("false")) multiplexer_3 (
    .in0(IR[19:15]), .in1(5'b10001), .out(multiplexer_3_out), .sel(ecall));
  Multiplexer #(.select(1), .width(5), .disabled("Z"), .enable("false")) multiplexer_4 (
    .in0(IR[24:20]), .in1(5'b01010), .out(multiplexer_4_out), .sel(ecall));
  Multiplexer #(.select(1), .width(12), .disabled("Z"), .enable("false")) multiplexer_5 (
    .in0(IR[31:20]), .in1({IR[31:25], IR[11:7]}), .out(multiplexer_5_out), .sel(S_type));
  assign bit_extender_1_out = {{20{IR[31]}}, {IR[31], IR[7], IR[30:25], IR[11:8]}};  // Bit_Extender bit_extender_1
  assign bit_extender_2_out = {{12{IR[31]}}, {IR[31], IR[19:12], IR[20], IR[30:21]}};  // Bit_Extender bit_extender_2
  assign bit_extender_3_out = {{20{multiplexer_5_out[11]}}, multiplexer_5_out};  // Bit_Extender bit_extender_3
  D_Flip_Flop #(.trigger("high"), .Pre_Clr_Positions("LEGACY"), .NegatePresetClear("false"), .enable("true"), .NewFFLayout("false")) d_ff_4 (.Q(d_ff_4_q));  // open: clk, D, Qn, preset, en, reset
  // Probe on 13'hc
  and and_12 (and_12_out, equal, \单周期硬布线控制器_1_beq );
  not not_7 (not_7_out, equal);
  and and_13 (and_13_out, not_7_out, \单周期硬布线控制器_1_bne );
  not not_8 (not_8_out, CLK);
  Regifile regifile_1 (
    .Din(RDin), .Clk(not_8_out), .R1(regifile_1_r1), .R2(MDin), .WE(RegWrite), .W_num(IR[11:7]),
    .R1_num(multiplexer_3_out), .R2_num(multiplexer_4_out));
  Shifter #(.width(32), .shift("ll")) shifter_1 (.in(bit_extender_1_out), .\dist (5'b00001), .out(shifter_1_out));
  Shifter #(.width(32), .shift("ll")) shifter_2 (.in(bit_extender_2_out), .\dist (5'b00001), .out(shifter_2_out));
  Comparator #(.width(13), .mode("twosComplement")) comparator_8 (
    .a(CNT_num), .b(13'hc), .eq(comparator_8_eq), .lt(comparator_8_lt));  // open: gt
  Clock #(.highDuration(1), .lowDuration(1)) clock_1 (.out(clock_1_out));
  and and_14 (and_14_out, BGEU, GE);
  Multiplexer #(.select(1), .width(32), .disabled("Z"), .enable("false")) multiplexer_6 (
    .in0(MDin), .in1(bit_extender_3_out), .out(multiplexer_6_out), .sel(AluSrcB));
  Adder #(.width(32)) adder_1 (.a(shifter_1_out), .b(PC), .out(adder_1_out));  // open: cin, cout
  Adder #(.width(32)) adder_2 (.a(shifter_2_out), .b(PC), .out(adder_2_out));  // open: cin, cout
  Counter #(.width(13), .max('h1fff), .ongoal("stay"), .trigger("rising"), .behavior("old")) counter_2 (
    .count(comparator_8_lt), .Q(CNT_num), .clk(clock_1_out));  // open: load, D, carry, clr, preset
  or or_14 (tunnel1, and_12_out, and_13_out, and_14_out);
  ALU alu_1 (
    .X(regifile_1_r1), .Y(multiplexer_6_out), .AluOP(\单周期硬布线控制器_1_alu_op ), .Equal(equal),
    .Result(alu_1_result), .Result_2(alu_1_result_2), .out_4(GE));  // open: out_6
  Adder #(.width(32)) adder_3 (.a(PC), .b(32'h4), .out(adder_3_out));  // open: cin, cout
  nand nand_1 (nand_1_out, d_ff_4_q, comparator_8_eq);
  Comparator #(.width(32), .mode("twosComplement")) comparator_9 (
    .a(32'h22), .b(regifile_1_r1), .eq(flag));  // open: gt, lt
  Multiplexer #(.select(1), .width(32), .disabled("Z"), .enable("false")) multiplexer_7 (
    .in0(alu_1_result), .in1(alu_1_result_2), .out(aluresult), .sel(comparator_10_eq));
  Multiplexer #(.select(1), .width(32), .disabled("Z"), .enable("false")) multiplexer_8 (
    .in0(adder_3_out), .in1(adder_1_out), .out(multiplexer_8_out), .sel(tunnel1));
  assign CLK = nand_1_out ? clock_1_out : 1'bz;  // Controlled_Buffer controlled_buffer_1
  Pull_Resistor #(.pull(1)) pull_resistor_4 (.node(CLK));
  Comparator #(.width(4), .mode("twosComplement")) comparator_10 (
    .a(\单周期硬布线控制器_1_alu_op ), .b(4'b0100), .eq(comparator_10_eq));  // open: gt, lt
  Multiplexer #(.select(1), .width(32), .disabled("Z"), .enable("false")) multiplexer_9 (
    .in0(multiplexer_8_out), .in1(adder_2_out), .out(multiplexer_9_out), .sel(JAL));
  assign and_15_out = aluresult & 32'hfffffffe;  // AND_Gate and_15, 32 bits wide
  Multiplexer #(.select(1), .width(32), .disabled("Z"), .enable("false")) multiplexer_10 (
    .in0(multiplexer_9_out), .in1(and_15_out), .out(EPC_IN), .sel(JALR));
  not not_9 (not_9_out, MemWrite);
  Multiplexer #(.select(1), .width(32), .disabled("Z"), .enable("false")) multiplexer_11 (
    .in0({32{1'b0}}), .in1(MDin), .out(multiplexer_11_out), .sel(and_16_out));
  and and_16 (and_16_out, ecall, flag);
  RAM #(.addrWidth(10), .dataWidth(32), .bus("separate"), .Select("high")) ram_1 (
    .addr(aluresult[11:2]), .din(MDin), .data(ram_1_data), .str(MemWrite), .clk(CLK), .ld(not_9_out));  // open: sel, clr
  Register #(.width(32), .trigger("rising"), .Select("low")) register_3 (
    .D(multiplexer_11_out), .en(and_16_out), .Q(LedData), .clk(CLK), .clr(RST));
  not not_10 (not_10_out, flag);
  assign bit_extender_4_out = {{16{1'b0}}, ram_1_data[15:0]};  // Bit_Extender bit_extender_4
  assign bit_extender_5_out = {{16{1'b0}}, ram_1_data[31:16]};  // Bit_Extender bit_extender_5
  and and_17 (halt, ecall, not_10_out);
  Comparator #(.width(3), .mode("twosComplement")) comparator_11 (
    .a(IR[14:12]), .b(3'b101), .eq(comparator_11_eq));  // open: gt, lt
  not not_11 (not_11_out, comparator_11_eq);
  Multiplexer #(.select(1), .width(32), .disabled("Z"), .enable("false")) multiplexer_12 (
    .in0(bit_extender_4_out), .in1(bit_extender_5_out), .out(multiplexer_12_out), .sel(aluresult[1]));
  Multiplexer #(.select(1), .width(32), .disabled("Z"), .enable("false")) multiplexer_13 (
    .in0(aluresult), .in1(multiplexer_14_out), .out(multiplexer_13_out), .sel(MemToReg));
  Multiplexer #(.select(1), .width(32), .disabled("Z"), .enable("false")) multiplexer_14 (
    .in0(multiplexer_12_out), .in1(ram_1_data), .out(multiplexer_14_out), .sel(not_11_out));
  Adder #(.width(32)) adder_4 (.a(PC), .b(32'h4), .out(adder_4_out));  // open: cin, cout
  Multiplexer #(.select(1), .width(32), .disabled("Z"), .enable("false")) multiplexer_15 (
    .in0(multiplexer_13_out), .in1(adder_4_out), .out(RDin), .sel(or_15_out));
  or or_15 (or_15_out, JALR, JAL);

  // Notes on the sheet:
  //   中断源
  //   中断等待指示
  //   总复位信号应将除ROM以外所有存储组件全部清零
  //   单级中断测试信号模拟器
  //   生成关中断指令
  //   数码管输出
  //   数码管输出应该用寄存器锁存，否则显示数据只能一闪而过
  //   Reset 
  //   生成中断等待指示
  //   Reset 
  //   Reset 
  //   判断是哪个中断的结束
  //   存储中断返回地址
  //   用于开关中断
  //   存储中断入口地址
  //   指令探针
  //   指令存储器
  //   为方便自动评测，需要输出PC，IR，寄存器堆写如数据RDin
  //   指令字
  //   contents of rom_1 (hex, n*v repeats v):
  //   7d000113 100413 1f41993 41f9d993 433 c00913 800b13 140413 f47413 800293 100313 499993 89e9b3 1300533
  //   2200893 73 406282b3 fe0294e3 140413 f00f93 1f47433 1c41413 800293 100313 49d993 89e9b3 1300533
  //   2200893 73 406282b3 fe0294e3 1c45413 406b0b33 b0463 f95ff06f 2b3 fff2c293 1029293 fff2e293 500533
  //   2200893 73 f5dff06f 1112023 410113 a12023 410113 812023 410113 1312023 410113 1412023 410113 1512023
  //   410113 1612023 410113 100b13 300a13 100a93 1600433 441413 14469b3 1300533 2200893 73 fe0416e3
  //   415a0a33 fe0a10e3 ffc10113 12b03 ffc10113 12a83 ffc10113 12a03 ffc10113 12983 ffc10113 12403
  //   ffc10113 12503 ffc10113 12883 200073 1112023 410113 a12023 410113 812023 410113 1312023 410113
  //   1412023 410113 1512023 410113 1612023 410113 200b13 300a13 100a93 1600433 441413 14469b3 1300533
  //   2200893 73 fe0416e3 415a0a33 fe0a10e3 ffc10113 12b03 ffc10113 12a83 ffc10113 12a03 ffc10113 12983
  //   ffc10113 12403 ffc10113 12503 ffc10113 12883 200073 1112023 410113 a12023 410113 812023 410113
  //   1312023 410113 1412023 410113 1512023 410113 1612023 410113 300b13 300a13 100a93 1600433 441413
  //   14469b3 1300533 2200893 73 fe0416e3 415a0a33 fe0a10e3 ffc10113 12b03 ffc10113 12a83 ffc10113 12a03
  //   ffc10113 12983 ffc10113 12403 ffc10113 12503 ffc10113 12883 200073
  //   RAM写使能MemWrite、RAM写入数据MDin等信号
  //   JAL
  //   JALR
  //   URET
  //   Beq
  //   Bne
  //   MemToReg
  //   MemWrite
  //   AluOP
  //   AluSrcB
  //   RegWrite
  //   控制位
  //   暂停节拍，不能为0
  //   戳工具置1进入计数暂停模式，ctrl+k时钟自动运行到对应节拍暂停
  //   ctrl+k关闭时钟连续运行，将控制位置零，进入单步调试模式调试
  //   可计数暂停的时钟源
  //   数据存储器
endmodule

module \单周期_多级中断  (
  input  IR1,
  input  IR2,
  input  IR3,
  output RegWrite,
  output MemWrite,
  output [31:0] PC,
  output [31:0] IR,
  output [31:0] RDin,
  output [31:0] MDin,
  output [31:0] LedData
);

  wire AluSrcB, and_1_out, and_2_out, and_3_out, and_4_out, and_5_out, and_9_out, and_10_out, and_11_out,
       and_12_out, and_13_out, and_15_out, and_16_out, BGEU, CLK, clock_1_out, comparator_1_eq,
       comparator_2_eq, comparator_3_eq, comparator_4_eq, comparator_5_eq, comparator_6_gt, comparator_6_lt,
       comparator_7_gt, comparator_7_lt, comparator_8_gt, comparator_9_eq, comparator_9_lt, comparator_11_eq,
       comparator_12_eq, d_ff_1_q, d_ff_2_q, d_ff_3_q, d_ff_4_q, ecall, equal, flag, GE, Go, halt, IE, IR1_q,
       IR1_t, IR2_q, IR2_t, IR3_q, IR3_t, IRA, IRB, IRC, JAL, JALR, MemToReg, nand_1_out, not_1_out,
       not_2_out, not_3_out, not_4_out, not_5_out, not_6_out, not_7_out, not_8_out, not_9_out, not_10_out,
       or_4_out, or_5_out, or_6_out, or_7_out, or_8_out, or_9_out, or_12_out, or_14_out, or_15_out,
       or_17_out, register_2_q, register_3_q, register_4_q, RST, S_type, tunnel1, URET, URETA, URETB, URETC,
       W1, W2, W3, \单周期硬布线控制器_1_beq , \单周期硬布线控制器_1_bne ;
  wire [1:0] priority_encoder_1_out;
  wire [2:0] adder_1_out, counter_2_q, multiplexer_3_out;
  wire [3:0] \单周期硬布线控制器_1_alu_op ;
  wire [4:0] multiplexer_4_out, multiplexer_5_out;
  wire [11:0] multiplexer_6_out;
  wire [12:0] CNT_num;
  wire [15:0] \总周期数 ;
  wire [31:0] adder_2_out, adder_3_out, adder_4_out, adder_5_out, alu_1_result, alu_1_result_2, aluresult,
       and_14_out, bit_extender_1_out, bit_extender_2_out, bit_extender_3_out, bit_extender_4_out,
       bit_extender_5_out, EPC, EPC_IN, multiplexer_1_out, multiplexer_2_out, multiplexer_7_out,
       multiplexer_9_out, multiplexer_10_out, multiplexer_12_out, multiplexer_13_out, multiplexer_14_out,
       multiplexer_15_out, ram_1_data, regifile_1_r1, shifter_1_out, shifter_2_out;

  Button \u_继续运行  (.out(Go));
  Button _1 ();  // open: out
  Button _2 ();  // open: out
  Button _3 ();  // open: out
  LED #(.active("true")) led_1 (.in(W1));
  LED #(.active("true")) led_2 (.in(W2));
  LED #(.active("true")) led_3 (.in(W3));
  or or_1 (W1, IR1_q, d_ff_1_q);
  or or_2 (W2, IR2_q, d_ff_2_q);
  or or_3 (W3, IR3_q, d_ff_3_q);
  Hex_Digit_Display hex_digit_display_1 (.value(LedData[31:28]));  // open: dp
  Comparator #(.width(16), .mode("twosComplement")) comparator_1 (
    .a(\总周期数 ), .b(16'h2fe), .eq(comparator_1_eq));  // open: gt, lt
  Comparator #(.width(16), .mode("twosComplement")) comparator_2 (
    .a(\总周期数 ), .b(16'h2), .eq(comparator_2_eq));  // open: gt, lt
  Comparator #(.width(16), .mode("twosComplement")) comparator_3 (
    .a(\总周期数 ), .b(16'hce), .eq(comparator_3_eq));  // open: gt, lt
  Comparator #(.width(16), .mode("twosComplement")) comparator_4 (
    .a(\总周期数 ), .b(16'h12), .eq(comparator_4_eq));  // open: gt, lt
  Comparator #(.width(16), .mode("twosComplement")) comparator_5 (
    .a(\总周期数 ), .b(16'h242), .eq(comparator_5_eq));  // open: gt, lt
  D_Flip_Flop #(.trigger("rising"), .Pre_Clr_Positions("LEGACY"), .NegatePresetClear("false"), .enable("true"), .NewFFLayout("false")) d_ff_1 (
    .clk(IRA), .D(1'b1), .Q(d_ff_1_q), .reset(IR1_q));  // open: Qn, preset, en
  D_Flip_Flop #(.trigger("rising"), .Pre_Clr_Positions("LEGACY"), .NegatePresetClear("false"), .enable("true"), .NewFFLayout("false")) d_ff_2 (
    .clk(IRB), .D(1'b1), .Q(d_ff_2_q), .reset(IR2_q));  // open: Qn, preset, en
  D_Flip_Flop #(.trigger("rising"), .Pre_Clr_Positions("LEGACY"), .NegatePresetClear("false"), .enable("true"), .NewFFLayout("false")) d_ff_3 (
    .clk(IRC), .D(1'b1), .Q(d_ff_3_q), .reset(IR3_q));  // open: Qn, preset, en
  Hex_Digit_Display hex_digit_display_2 (.value(LedData[23:20]));  // open: dp
  Hex_Digit_Display hex_digit_display_3 (.value(LedData[27:24]));  // open: dp
  or or_4 (or_4_out, comparator_1_eq, comparator_2_eq);
  or or_5 (or_5_out, comparator_4_eq, comparator_5_eq);
  or or_6 (or_6_out, d_ff_1_q, IR1_q);
  or or_7 (or_7_out, d_ff_2_q, IR2_q);
  or or_8 (or_8_out, d_ff_3_q, IR3_q);
  or or_9 (or_9_out, W1, W2, W3);
  Hex_Digit_Display hex_digit_display_4 (.value(LedData[15:12]));  // open: dp
  Hex_Digit_Display hex_digit_display_5 (.value(LedData[19:16]));  // open: dp
  Pull_Resistor #(.pull(0)) pull_resistor_1 (.node(IRA));
  assign IRA = or_4_out ? ~CLK : 1'bz;  // Controlled_Inverter controlled_inverter_1
  Pull_Resistor #(.pull(0)) pull_resistor_2 (.node(IRB));
  assign IRB = comparator_3_eq ? ~CLK : 1'bz;  // Controlled_Inverter controlled_inverter_2
  Pull_Resistor #(.pull(0)) pull_resistor_3 (.node(IRC));
  assign IRC = or_5_out ? ~CLK : 1'bz;  // Controlled_Inverter controlled_inverter_3
  and and_1 (and_1_out, or_6_out, ~URETA);  // AND_Gate
  and and_2 (and_2_out, or_7_out, ~URETB);  // AND_Gate
  and and_3 (and_3_out, or_8_out, ~URETC);  // AND_Gate
  Register #(.width(1), .trigger("rising"), .Select("low")) register_1 (
    .D(or_9_out), .Q(IE), .clk(CLK), .clr(URET));  // open: en
  Comparator #(.width(32), .mode("twosComplement")) comparator_6 (
    .a(PC), .b(32'h3204), .gt(comparator_6_gt), .lt(comparator_6_lt));  // open: eq
  Comparator #(.width(32), .mode("twosComplement")) comparator_7 (
    .a(PC), .b(32'h3158), .gt(comparator_7_gt), .lt(comparator_7_lt));  // open: eq
  Comparator #(.width(32), .mode("twosComplement")) comparator_8 (
    .a(PC), .b(32'h30ac), .gt(comparator_8_gt));  // open: eq, lt
  Hex_Digit_Display hex_digit_display_6 (.value(LedData[11:8]));  // open: dp
  Hex_Digit_Display hex_digit_display_7 (.value(LedData[7:4]));  // open: dp
  // Probe on \总周期数 
  D_Flip_Flop #(.trigger("rising"), .Pre_Clr_Positions("LEGACY"), .NegatePresetClear("false"), .enable("true"), .NewFFLayout("false")) u_IR1 (
    .clk(CLK), .D(and_1_out), .Q(IR1_q));  // open: Qn, preset, en, reset
  D_Flip_Flop #(.trigger("rising"), .Pre_Clr_Positions("LEGACY"), .NegatePresetClear("false"), .enable("true"), .NewFFLayout("false")) u_IR2 (
    .clk(CLK), .D(and_2_out), .Q(IR2_q));  // open: Qn, preset, en, reset
  D_Flip_Flop #(.trigger("rising"), .Pre_Clr_Positions("LEGACY"), .NegatePresetClear("false"), .enable("true"), .NewFFLayout("false")) u_IR3 (
    .clk(CLK), .D(and_3_out), .Q(IR3_q));  // open: Qn, preset, en, reset
  and and_4 (and_4_out, comparator_6_lt, comparator_7_gt);
  and and_5 (and_5_out, comparator_7_lt, comparator_8_gt);
  Hex_Digit_Display hex_digit_display_8 (.value(LedData[3:0]));  // open: dp
  not not_1 (not_1_out, W1);
  not not_2 (not_2_out, W2);
  not not_3 (not_3_out, W3);
  and and_6 (URETC, URET, comparator_6_gt);
  and and_7 (URETB, URET, and_4_out);
  and and_8 (URETA, URET, and_5_out);
  or or_10 (IR1_t, IR1, IRA);
  Button u_RST (.out(RST));
  Register #(.width(1), .trigger("falling"), .Select("low")) register_2 (
    .D(not_1_out), .Q(register_2_q), .clk(CLK));  // open: en, clr
  Register #(.width(1), .trigger("falling"), .Select("low")) register_3 (
    .D(not_2_out), .Q(register_3_q), .clk(CLK));  // open: en, clr
  Register #(.width(1), .trigger("falling"), .Select("low")) register_4 (
    .D(not_3_out), .Q(register_4_q), .clk(CLK));  // open: en, clr
  or or_11 (IR2_t, IR2, IRB);
  not not_4 (not_4_out, halt);
  or or_12 (or_12_out, not_4_out, Go);
  Counter #(.width(16), .max('hffff), .ongoal("wrap"), .trigger("rising"), .behavior("new")) counter_1 (
    .count(or_12_out), .Q(\总周期数 ), .clk(CLK), .clr(RST));  // open: load, D, carry, preset, down
  and and_9 (and_9_out, IRA, register_2_q, register_3_q, register_4_q);
  and and_10 (and_10_out, IRB, register_3_q, register_4_q);
  // Probe on multiplexer_2_out
  Multiplexer #(.select(2), .width(32), .disabled("Z"), .enable("false")) multiplexer_1 (
    .in0(EPC_IN), .in1(32'h30ac), .in2(32'h3158), .in3(32'h3204), .out(multiplexer_1_out),
    .sel(priority_encoder_1_out));
  Priority_Encoder #(.select(2), .disabled("Z")) priority_encoder_1 (
    .in0(1'b1), .in1(and_9_out), .in2(and_10_out), .in3(and_11_out), .out(priority_encoder_1_out));  // open: gs, en_out, en_in
  and and_11 (and_11_out, IRC, register_4_q);
  or or_13 (IR3_t, IR3, IRC);
  or or_14 (or_14_out, not_5_out, Go);
  not not_5 (not_5_out, halt);
  Multiplexer #(.select(1), .width(32), .disabled("Z"), .enable("false")) multiplexer_2 (
    .in0(multiplexer_1_out), .in1(EPC), .out(multiplexer_2_out), .sel(URET));
  or or_15 (or_15_out, IRA, IRB, IRC, URET);
  // Probe on PC
  Register #(.width(32), .trigger("rising"), .Select("low")) u_PC (
    .D(multiplexer_2_out), .en(or_14_out), .Q(PC), .clk(CLK), .clr(RST));
  Counter #(.width(3), .max('h7), .ongoal("wrap"), .trigger("rising"), .behavior("new")) counter_2 (
    .count(or_15_out), .Q(counter_2_q), .clk(CLK), .down(URET));  // open: load, D, carry, clr, preset
  Adder #(.width(3)) adder_1 (.a(counter_2_q), .b(3'b001), .out(adder_1_out));  // open: cin, cout
  // RiscV_Probe riscv_probe_1: pin names not known; wires that end beside it: PC[11:2], IR
  EPC_regfile epc_regfile_1 (.EPC_IN(EPC_IN), .EPC_OUT(EPC), .CLK(CLK), .R(multiplexer_3_out));
  Multiplexer #(.select(1), .width(3), .disabled("Z"), .enable("false")) multiplexer_3 (
    .in0(adder_1_out), .in1(counter_2_q), .out(multiplexer_3_out), .sel(URET));
  ROM #(.addrWidth(10), .dataWidth(32), .Select("high")) rom_1 (.addr(PC[11:2]), .data(IR));
  // Probe on multiplexer_3_out
  \单周期硬布线控制器  \u_单周期硬布线控制器_1  (
    .Funct({IR[30], IR[25], IR[14:12]}), .OP(IR[6:2]), .ALU_OP(\单周期硬布线控制器_1_alu_op ), .MemToReg(MemToReg),
    .MemWrite(MemWrite), .ALU_SRC(AluSrcB), .RegWrite(RegWrite), .ecall(ecall), .S_type(S_type), .Jalr(JALR),
    .Beq(\单周期硬布线控制器_1_beq ), .JAL(JAL), .Bne(\单周期硬布线控制器_1_bne ), .in_3(IR[21]), .uret(URET), .BGEU(BGEU));
  Multiplexer #(.select(1), .width(5), .disabled("Z"), .enable("false")) multiplexer_4 (
    .in0(IR[19:15]), .in1(5'b10001), .out(multiplexer_4_out), .sel(ecall));
  Multiplexer #(.select(1), .width(5), .disabled("Z"), .enable("false")) multiplexer_5 (
    .in0(IR[24:20]), .in1(5'b01010), .out(multiplexer_5_out), .sel(ecall));
  Multiplexer #(.select(1), .width(12), .disabled("Z"), .enable("false")) multiplexer_6 (
    .in0(IR[31:20]), .in1({IR[31:25], IR[11:7]}), .out(multiplexer_6_out), .sel(S_type));
  assign bit_extender_1_out = {{20{IR[31]}}, {IR[31], IR[7], IR[30:25], IR[11:8]}};  // Bit_Extender bit_extender_1
  assign bit_extender_2_out = {{12{IR[31]}}, {IR[31], IR[19:12], IR[20], IR[30:21]}};  // Bit_Extender bit_extender_2
  D_Flip_Flop #(.trigger("high"), .Pre_Clr_Positions("LEGACY"), .NegatePresetClear("false"), .enable("true"), .NewFFLayout("false")) d_ff_4 (.Q(d_ff_4_q));  // open: clk, D, Qn, preset, en, reset
  // Probe on 13'hc
  assign bit_extender_3_out = {{20{multiplexer_6_out[11]}}, multiplexer_6_out};  // Bit_Extender bit_extender_3
  Comparator #(.width(13), .mode("twosComplement")) comparator_9 (
    .a(CNT_num), .b(13'hc), .eq(comparator_9_eq), .lt(comparator_9_lt));  // open: gt
  Clock #(.highDuration(1), .lowDuration(1)) clock_1 (.out(clock_1_out));
  not not_6 (not_6_out, CLK);
  Regifile regifile_1 (
    .Din(RDin), .Clk(not_6_out), .R1(regifile_1_r1), .R2(MDin), .WE(RegWrite), .W_num(IR[11:7]),
    .R1_num(multiplexer_4_out), .R2_num(multiplexer_5_out));
  Shifter #(.width(32), .shift("ll")) shifter_1 (.in(bit_extender_1_out), .\dist (5'b00001), .out(shifter_1_out));
  Shifter #(.width(32), .shift("ll")) shifter_2 (.in(bit_extender_2_out), .\dist (5'b00001), .out(shifter_2_out));
  Counter #(.width(13), .max('h1fff), .ongoal("stay"), .trigger("rising"), .behavior("old")) counter_3 (
    .count(comparator_9_lt), .Q(CNT_num), .clk(clock_1_out));  // open: load, D, carry, clr, preset
  Multiplexer #(.select(1), .width(32), .disabled("Z"), .enable("false")) multiplexer_7 (
    .in0(MDin), .in1(bit_extender_3_out), .out(multiplexer_7_out), .sel(AluSrcB));
  Adder #(.width(32)) adder_2 (.a(shifter_1_out), .b(PC), .out(adder_2_out));  // open: cin, cout
  Adder #(.width(32)) adder_3 (.a(shifter_2_out), .b(PC), .out(adder_3_out));  // open: cin, cout
  nand nand_1 (nand_1_out, d_ff_4_q, comparator_9_eq);
  and and_12 (and_12_out, equal, \单周期硬布线控制器_1_beq );
  not not_7 (not_7_out, equal);
  and and_13 (and_13_out, not_7_out, \单周期硬布线控制器_1_bne );
  ALU alu_1 (
    .X(regifile_1_r1), .Y(multiplexer_7_out), .AluOP(\单周期硬布线控制器_1_alu_op ), .Equal(equal),
    .Result(alu_1_result), .Result_2(alu_1_result_2), .out_4(GE));  // open: out_6
  Adder #(.width(32)) adder_4 (.a(PC), .b(32'h4), .out(adder_4_out));  // open: cin, cout
  assign CLK = nand_1_out ? clock_1_out : 1'bz;  // Controlled_Buffer controlled_buffer_1
  Pull_Resistor #(.pull(1)) pull_resistor_4 (.node(CLK));
  Comparator #(.width(32), .mode("twosComplement")) comparator_10 (
    .a(32'h22), .b(regifile_1_r1), .eq(flag));  // open: gt, lt
  Comparator #(.width(4), .mode("twosComplement")) comparator_11 (
    .a(\单周期硬布线控制器_1_alu_op ), .b(4'b0100), .eq(comparator_11_eq));  // open: gt, lt
  Multiplexer #(.select(1), .width(32), .disabled("Z"), .enable("false")) multiplexer_8 (
    .in0(alu_1_result), .in1(alu_1_result_2), .out(aluresult), .sel(comparator_11_eq));
  Multiplexer #(.select(1), .width(32), .disabled("Z"), .enable("false")) multiplexer_9 (
    .in0(adder_4_out), .in1(adder_2_out), .out(multiplexer_9_out), .sel(tunnel1));
  Multiplexer #(.select(1), .width(32), .disabled("Z"), .enable("false")) multiplexer_10 (
    .in0(multiplexer_9_out), .in1(adder_3_out), .out(multiplexer_10_out), .sel(JAL));
  assign and_14_out = aluresult & 32'hfffffffe;  // AND_Gate and_14, 32 bits wide
  and and_15 (and_15_out, BGEU, GE);
  Multiplexer #(.select(1), .width(32), .disabled("Z"), .enable("false")) multiplexer_11 (
    .in0(multiplexer_10_out), .in1(and_14_out), .out(EPC_IN), .sel(JALR));
  or or_16 (tunnel1, and_12_out, and_13_out, and_15_out);
  not not_8 (not_8_out, MemWrite);
  Multiplexer #(.select(1), .width(32), .disabled("Z"), .enable("false")) multiplexer_12 (
    .in0({32{1'b0}}), .in1(MDin), .out(multiplexer_12_out), .sel(and_16_out));
  and and_16 (and_16_out, ecall, flag);
  RAM #(.addrWidth(10), .dataWidth(32), .bus("separate"), .Select("high")) ram_1 (
    .addr(aluresult[11:2]), .din(MDin), .data(ram_1_data), .str(MemWrite), .clk(CLK), .ld(not_8_out));  // open: sel, clr
  Register #(.width(32), .trigger("rising"), .Select("low")) register_5 (
    .D(multiplexer_12_out), .en(and_16_out), .Q(LedData), .clk(CLK), .clr(RST));
  not not_9 (not_9_out, flag);
  assign bit_extender_4_out = {{16{1'b0}}, ram_1_data[15:0]};  // Bit_Extender bit_extender_4
  assign bit_extender_5_out = {{16{1'b0}}, ram_1_data[31:16]};  // Bit_Extender bit_extender_5
  and and_17 (halt, ecall, not_9_out);
  Comparator #(.width(3), .mode("twosComplement")) comparator_12 (
    .a(IR[14:12]), .b(3'b101), .eq(comparator_12_eq));  // open: gt, lt
  Multiplexer #(.select(1), .width(32), .disabled("Z"), .enable("false")) multiplexer_13 (
    .in0(bit_extender_4_out), .in1(bit_extender_5_out), .out(multiplexer_13_out), .sel(aluresult[1]));
  not not_10 (not_10_out, comparator_12_eq);
  Multiplexer #(.select(1), .width(32), .disabled("Z"), .enable("false")) multiplexer_14 (
    .in0(multiplexer_13_out), .in1(ram_1_data), .out(multiplexer_14_out), .sel(not_10_out));
  Multiplexer #(.select(1), .width(32), .disabled("Z"), .enable("false")) multiplexer_15 (
    .in0(aluresult), .in1(multiplexer_14_out), .out(multiplexer_15_out), .sel(MemToReg));
  Adder #(.width(32)) adder_5 (.a(PC), .b(32'h4), .out(adder_5_out));  // open: cin, cout
  Multiplexer #(.select(1), .width(32), .disabled("Z"), .enable("false")) multiplexer_16 (
    .in0(multiplexer_15_out), .in1(adder_5_out), .out(RDin), .sel(or_17_out));
  or or_17 (or_17_out, JALR, JAL);

  // Notes on the sheet:
  //   中断源
  //   中断等待指示
  //   总复位信号应将除ROM以外所有存储组件全部清零
  //   多级中断测试信号模拟器
  //   生成关中断指令
  //   数码管输出
  //   Reset 
  //   生成中断等待指示
  //   Reset 
  //   Reset 
  //   数码管输出应该用寄存器锁存，否则显示数据只能一闪而过
  //   判断是哪个中断的结束
  //   用于开关中断
  //   存储中断入口地址
  //   存储多级的中断返回地址
  //   为方便自动评测，需要输出PC，IR，寄存器堆写如数据RDin
  //   指令探针
  //   指令存储器
  //   RAM写使能MemWrite、RAM写入数据MDin等信号
  //   指令字
  //   contents of rom_1 (hex, n*v repeats v):
  //   7d000113 100413 1f41993 41f9d993 433 c00913 800b13 140413 f47413 800293 100313 499993 89e9b3 1300533
  //   2200893 73 406282b3 fe0294e3 140413 f00f93 1f47433 1c41413 800293 100313 49d993 89e9b3 1300533
  //   2200893 73 406282b3 fe0294e3 1c45413 406b0b33 b0463 f95ff06f 2b3 fff2c293 1029293 fff2e293 500533
  //   2200893 73 f5dff06f 1112023 410113 a12023 410113 812023 410113 1312023 410113 1412023 410113 1512023
  //   410113 1612023 410113 40e073 100b13 300a13 100a93 1600433 441413 14469b3 1300533 2200893 73 fe0416e3
  //   415a0a33 fe0a10e3 40f073 ffc10113 12b03 ffc10113 12a83 ffc10113 12a03 ffc10113 12983 ffc10113 12403
  //   ffc10113 12503 ffc10113 12883 200073 1112023 410113 a12023 410113 812023 410113 1312023 410113
  //   1412023 410113 1512023 410113 1612023 410113 40e073 200b13 300a13 100a93 1600433 441413 14469b3
  //   1300533 2200893 73 fe0416e3 415a0a33 fe0a10e3 40f073 ffc10113 12b03 ffc10113 12a83 ffc10113 12a03
  //   ffc10113 12983 ffc10113 12403 ffc10113 12503 ffc10113 12883 200073 1112023 410113 a12023 410113
  //   812023 410113 1312023 410113 1412023 410113 1512023 410113 1612023 410113 40e073 300b13 300a13
  //   100a93 1600433 441413 14469b3 1300533 2200893 73 fe0416e3 415a0a33 fe0a10e3 40f073 ffc10113 12b03
  //   ffc10113 12a83 ffc10113 12a03 ffc10113 12983 ffc10113 12403 ffc10113 12503 ffc10113 12883 200073
  //   JAL
  //   JALR
  //   URET
  //   Beq
  //   Bne
  //   MemToReg
  //   MemWrite
  //   AluOP
  //   AluSrcB
  //   RegWrite
  //   控制位
  //   暂停节拍，不能为0
  //   戳工具置1进入计数暂停模式，ctrl+k时钟自动运行到对应节拍暂停
  //   ctrl+k关闭时钟连续运行，将控制位置零，进入单步调试模式调试
  //   可计数暂停的时钟源
  //   数据存储器
endmodule

module \封装正确性测试  (
);

  wire IR1, IR2, IR3, MemW, RegW;
  wire [31:0] EX_PC, ID_PC, IF_PC, IR, LED, MDin, MDinr, MEM_PC, PC, RDin, RDinr, WB_PC;

  \单周期RISC_V  \u_单周期risc_v_1  (
    .IR1(IR1), .IR2(IR2), .IR3(IR3), .RegWrite(RegW), .MemWrite(MemW), .PC(PC), .IR(IR), .RDin(RDin),
    .MDin(MDin), .LedData(LED));
  \气泡流水线  \u_气泡流水线_1  (
    .RegWrite(RegW), .MemWrite(MemW), .IF_PC(IF_PC), .ID_PC(ID_PC), .EX_PC(EX_PC), .M_PC(MEM_PC),
    .WB_PC(WB_PC), .RDin(RDinr), .MDin(MDinr), .LedData(LED));
  \单周期_单级中断  \u_单周期_单级中断_1  (
    .IR1(IR1), .IR2(IR2), .IR3(IR3), .RegWrite(RegW), .MemWrite(MemW), .PC(PC), .IR(IR), .RDin(RDin),
    .MDin(MDin), .LedData(LED));
  \理想流水线  \u_理想流水线_1  (
    .RegWrite(RegW), .MemWrite(MemW), .IF_PC(IF_PC), .ID_PC(ID_PC), .EX_PC(EX_PC), .M_PC(MEM_PC),
    .WB_PC(WB_PC), .RDin(RDinr), .MDin(MDinr), .LedData(LED));
  \重定向流水线  \u_重定向流水线_1  (
    .RegWrite(RegW), .MemWrite(MemW), .IF_PC(IF_PC), .ID_PC(ID_PC), .EX_PC(EX_PC), .M_PC(MEM_PC),
    .WB_PC(WB_PC), .RDin(RDinr), .MDin(MDinr), .LedData(LED));
  \单周期_多级中断  \u_单周期_多级中断_1  (
    .IR1(IR1), .IR2(IR2), .IR3(IR3), .RegWrite(RegW), .MemWrite(MemW), .PC(PC), .IR(IR), .RDin(RDin),
    .MDin(MDin), .LedData(LED));

  // Notes on the sheet:
  //   单周期封装测试
  //   气泡流水封装测试
  //   单周期+单级中断封装测试
  //   请检查上面封装有无位宽不匹配，引脚标签是否和连接的标签相对应，否则无法在educoder平台上正确测试
  //   理想流水封装测试
  //   重定向流水封装测试
  //   单周期+多级中断封装测试
endmodule

// IF/ID
module IF_ID1 (
  input  RST,
  input  [31:0] IR_IN,
  input  [31:0] PC_IN,
  input  en,
  input  CLK,
  output [31:0] IR_OUT,
  output [31:0] PC_OUT
);

  Register #(.width(32), .trigger("rising"), .Select("low")) register_1 (
    .D(IR_IN), .en(en), .Q(IR_OUT), .clk(CLK), .clr(RST));
  Register #(.width(32), .trigger("rising"), .Select("low")) register_2 (
    .D(PC_IN), .en(en), .Q(PC_OUT), .clk(CLK), .clr(RST));
endmodule

// ID/EX
module ID_EX1 (
  input  RST,
  input  JAL_IN,
  input  JALR_IN,
  input  Beq_IN,
  input  Bne_IN,
  input  MemToReg_IN,
  input  MemWrite_IN,
  input  [3:0] AluOP_IN,
  input  AluSrcB_IN,
  input  RegWrite_IN,
  input  ECALL_IN,
  input  BGEU_IN,
  input  [31:0] R1_IN,
  input  [31:0] R2_IN,
  input  [4:0] W_IN,
  input  [31:0] IMM_IN,
  input  [31:0] B_IN,
  input  [31:0] IR_IN,
  input  [31:0] J_IN,
  input  [31:0] PC_IN,
  input  en,
  input  CLK,
  output JAL_OUT,
  output JALR_OUT,
  output Beq_OUT,
  output Bne_OUT,
  output MemToReg_OUT,
  output MemWrite_OUT,
  output [3:0] AluOP_OUT,
  output AluSrcB_OUT,
  output RegWrite_OUT,
  output ECALL_OUT,
  output BGEU_OUT,
  output [31:0] R1_OUT,
  output [31:0] R2_OUT,
  output [4:0] W_OUT,
  output [31:0] IMM_OUT,
  output [31:0] B_OUT,
  output [31:0] IR_OUT,
  output [31:0] J_OUT,
  output [31:0] PC_OUT
);

  Register #(.width(1), .trigger("rising"), .Select("low")) register_1 (
    .D(JAL_IN), .en(en), .Q(JAL_OUT), .clk(CLK), .clr(RST));
  Register #(.width(1), .trigger("rising"), .Select("low")) register_2 (
    .D(JALR_IN), .en(en), .Q(JALR_OUT), .clk(CLK), .clr(RST));
  Register #(.width(1), .trigger("rising"), .Select("low")) register_3 (
    .D(Beq_IN), .en(en), .Q(Beq_OUT), .clk(CLK), .clr(RST), .cs(Beq_IN));  // open: preset
  Register #(.width(1), .trigger("rising"), .Select("low")) register_4 (
    .D(Bne_IN), .en(en), .Q(Bne_OUT), .clk(CLK), .clr(RST));
  Register #(.width(1), .trigger("rising"), .Select("low")) register_5 (
    .D(MemToReg_IN), .en(en), .Q(MemToReg_OUT), .clk(CLK), .clr(RST));
  Register #(.width(1), .trigger("rising"), .Select("low")) register_6 (
    .D(MemWrite_IN), .en(en), .Q(MemWrite_OUT), .clk(CLK), .clr(RST));
  Register #(.width(4), .trigger("rising"), .Select("low")) register_7 (
    .D(AluOP_IN), .en(en), .Q(AluOP_OUT), .clk(CLK), .clr(RST));
  Register #(.width(1), .trigger("rising"), .Select("low")) register_8 (
    .D(AluSrcB_IN), .en(en), .Q(AluSrcB_OUT), .clk(CLK), .clr(RST));
  Register #(.width(1), .trigger("rising"), .Select("low")) register_9 (
    .D(RegWrite_IN), .en(en), .Q(RegWrite_OUT), .clk(CLK), .clr(RST));
  Register #(.width(1), .trigger("rising"), .Select("low")) register_10 (
    .D(ECALL_IN), .en(en), .Q(ECALL_OUT), .clk(CLK), .clr(RST));
  Register #(.width(1), .trigger("rising"), .Select("low")) register_11 (
    .D(BGEU_IN), .en(en), .Q(BGEU_OUT), .clk(CLK), .clr(RST));
  Register #(.width(32), .trigger("rising"), .Select("low")) register_12 (
    .D(R1_IN), .en(en), .Q(R1_OUT), .clk(CLK), .clr(RST));
  Register #(.width(32), .trigger("rising"), .Select("low")) register_13 (
    .D(R2_IN), .en(en), .Q(R2_OUT), .clk(CLK), .clr(RST));
  Register #(.width(5), .trigger("rising"), .Select("low")) register_14 (
    .D(W_IN), .en(en), .Q(W_OUT), .clk(CLK), .clr(RST));
  Register #(.width(32), .trigger("rising"), .Select("low")) register_15 (
    .D(IMM_IN), .en(en), .Q(IMM_OUT), .clk(CLK), .clr(RST));
  Register #(.width(32), .trigger("rising"), .Select("low")) register_16 (
    .D(B_IN), .en(en), .Q(B_OUT), .clk(CLK), .clr(RST));
  Register #(.width(32), .trigger("rising"), .Select("low")) register_17 (
    .D(IR_IN), .en(en), .Q(IR_OUT), .clk(CLK), .clr(RST));
  Register #(.width(32), .trigger("rising"), .Select("low")) register_18 (
    .D(J_IN), .en(en), .Q(J_OUT), .clk(CLK), .clr(RST));
  Register #(.width(32), .trigger("rising"), .Select("low")) register_19 (
    .D(PC_IN), .en(en), .Q(PC_OUT), .clk(CLK), .clr(RST));
endmodule

// EX/MEM
module EX_MEM1 (
  input  RST,
  input  JAL_IN,
  input  JALR_IN,
  input  halt_IN,
  input  MemToReg_IN,
  input  MemWrite_IN,
  input  RegWrite_IN,
  input  [31:0] aluresult_IN,
  input  HIGH_IN,
  input  [9:0] MA_IN,
  input  [31:0] MDin_IN,
  input  [4:0] W_IN,
  input  [31:0] PC_IN,
  input  [31:0] IR_IN,
  input  [31:0] IMM_IN,
  input  en,
  input  CLK,
  output JAL_OUT,
  output JALR_OUT,
  output halt_OUT,
  output MemToReg_OUT,
  output MemWrite_OUT,
  output RegWrite_OUT,
  output [31:0] aluresult_OUT,
  output HIGH_OUT,
  output [9:0] MA_OUT,
  output [31:0] MDin_OUT,
  output [4:0] W_OUT,
  output [31:0] PC_OUT,
  output [31:0] IR_OUT,
  output [31:0] IMM_OUT
);

  Register #(.width(1), .trigger("rising"), .Select("low")) register_1 (
    .D(JAL_IN), .en(en), .Q(JAL_OUT), .clk(CLK), .clr(RST));
  Register #(.width(1), .trigger("rising"), .Select("low")) register_2 (
    .D(JALR_IN), .en(en), .Q(JALR_OUT), .clk(CLK), .clr(RST));
  Register #(.width(1), .trigger("rising"), .Select("low")) register_3 (
    .D(halt_IN), .en(en), .Q(halt_OUT), .clk(CLK), .clr(RST));
  Register #(.width(1), .trigger("rising"), .Select("low")) register_4 (
    .D(MemToReg_IN), .en(en), .Q(MemToReg_OUT), .clk(CLK), .clr(RST));
  Register #(.width(1), .trigger("rising"), .Select("low")) register_5 (
    .D(MemWrite_IN), .en(en), .Q(MemWrite_OUT), .clk(CLK), .clr(RST));
  Register #(.width(1), .trigger("rising"), .Select("low")) register_6 (
    .D(RegWrite_IN), .en(en), .Q(RegWrite_OUT), .clk(CLK), .clr(RST));
  Register #(.width(32), .trigger("rising"), .Select("low")) register_7 (
    .D(aluresult_IN), .en(en), .Q(aluresult_OUT), .clk(CLK), .clr(RST));
  Register #(.width(1), .trigger("rising"), .Select("low")) register_8 (
    .D(HIGH_IN), .en(en), .Q(HIGH_OUT), .clk(CLK), .clr(RST));
  Register #(.width(10), .trigger("rising"), .Select("low")) register_9 (
    .D(MA_IN), .en(en), .Q(MA_OUT), .clk(CLK), .clr(RST));
  Register #(.width(32), .trigger("rising"), .Select("low")) register_10 (
    .D(MDin_IN), .en(en), .Q(MDin_OUT), .clk(CLK), .clr(RST));
  Register #(.width(5), .trigger("rising"), .Select("low")) register_11 (
    .D(W_IN), .en(en), .Q(W_OUT), .clk(CLK), .clr(RST));
  Register #(.width(32), .trigger("rising"), .Select("low")) register_12 (
    .D(PC_IN), .en(en), .Q(PC_OUT), .clk(CLK), .clr(RST));
  Register #(.width(32), .trigger("rising"), .Select("low")) register_13 (
    .D(IR_IN), .en(en), .Q(IR_OUT), .clk(CLK), .clr(RST));
  Register #(.width(32), .trigger("rising"), .Select("low")) register_14 (
    .D(IMM_IN), .en(en), .Q(IMM_OUT), .clk(CLK), .clr(RST));
endmodule

// MEM/WB
module MEM_WB1 (
  input  RST,
  input  JAL_IN,
  input  JALR_IN,
  input  halt_IN,
  input  MemToReg_IN,
  input  RegWrite_IN,
  input  [31:0] aluresult_IN,
  input  [31:0] Dout_IN,
  input  [4:0] W_IN,
  input  [31:0] IR_IN,
  input  [31:0] PC_IN,
  input  [31:0] IMM_IN,
  input  en,
  input  CLK,
  output JAL_OUT,
  output JALR_OUT,
  output halt_OUT,
  output MemToReg_OUT,
  output RegWrite_OUT,
  output [31:0] aluresult_OUT,
  output [31:0] Dout_OUT,
  output [4:0] W_OUT,
  output [31:0] IR_OUT,
  output [31:0] PC_OUT,
  output [31:0] IMM_OUT
);

  Register #(.width(1), .trigger("rising"), .Select("low")) register_1 (
    .D(JAL_IN), .en(en), .Q(JAL_OUT), .clk(CLK), .clr(RST));
  Register #(.width(1), .trigger("rising"), .Select("low")) register_2 (
    .D(JALR_IN), .en(en), .Q(JALR_OUT), .clk(CLK), .clr(RST));
  Register #(.width(1), .trigger("rising"), .Select("low")) register_3 (
    .D(halt_IN), .en(en), .Q(halt_OUT), .clk(CLK), .clr(RST));
  Register #(.width(1), .trigger("rising"), .Select("low")) register_4 (
    .D(MemToReg_IN), .en(en), .Q(MemToReg_OUT), .clk(CLK), .clr(RST));
  Register #(.width(1), .trigger("rising"), .Select("low")) register_5 (
    .D(RegWrite_IN), .en(en), .Q(RegWrite_OUT), .clk(CLK), .clr(RST));
  Register #(.width(32), .trigger("rising"), .Select("low")) register_6 (
    .D(aluresult_IN), .en(en), .Q(aluresult_OUT), .clk(CLK), .clr(RST));
  Register #(.width(32), .trigger("rising"), .Select("low")) register_7 (
    .D(Dout_IN), .en(en), .Q(Dout_OUT), .clk(CLK), .clr(RST));
  Register #(.width(5), .trigger("rising"), .Select("low")) register_8 (
    .D(W_IN), .en(en), .Q(W_OUT), .clk(CLK), .clr(RST));
  Register #(.width(32), .trigger("rising"), .Select("low")) register_9 (
    .D(IR_IN), .en(en), .Q(IR_OUT), .clk(CLK), .clr(RST));
  Register #(.width(32), .trigger("rising"), .Select("low")) register_10 (
    .D(PC_IN), .en(en), .Q(PC_OUT), .clk(CLK), .clr(RST));
  Register #(.width(32), .trigger("rising"), .Select("low")) register_11 (
    .D(IMM_IN), .en(en), .Q(IMM_OUT), .clk(CLK), .clr(RST));
endmodule

// IF/ID
module IF_ID2 (
  input  CLR,
  input  RST,
  input  [31:0] IR_IN,
  input  PREDICTJUMP_IN,
  input  [31:0] PC_IN,
  input  en,
  input  CLK,
  output [31:0] IR_OUT,
  output PREDICTJUMP_OUT,
  output [31:0] PC_OUT
);

  wire multiplexer_2_out;
  wire [31:0] multiplexer_1_out, multiplexer_3_out;

  Multiplexer #(.select(1), .width(32), .disabled("Z"), .enable("false")) multiplexer_1 (
    .in0(IR_IN), .in1({32{1'b0}}), .out(multiplexer_1_out), .sel(CLR));
  Multiplexer #(.select(1), .width(1), .disabled("Z"), .enable("false")) multiplexer_2 (
    .in0(PREDICTJUMP_IN), .in1(1'b0), .out(multiplexer_2_out), .sel(CLR));
  Multiplexer #(.select(1), .width(32), .disabled("Z"), .enable("false")) multiplexer_3 (
    .in0(PC_IN), .in1({32{1'b0}}), .out(multiplexer_3_out), .sel(CLR));
  Register #(.width(32), .trigger("rising"), .Select("low")) register_1 (
    .D(multiplexer_1_out), .en(en), .Q(IR_OUT), .clk(CLK), .clr(RST));
  Register #(.width(1), .trigger("rising"), .Select("low")) register_2 (
    .D(multiplexer_2_out), .en(en), .Q(PREDICTJUMP_OUT), .clk(CLK), .clr(RST));
  Register #(.width(32), .trigger("rising"), .Select("low")) register_3 (
    .D(multiplexer_3_out), .en(en), .Q(PC_OUT), .clk(CLK), .clr(RST));
endmodule

// EX/MEM
module EX_MEM2 (
  input  CLR,
  input  RST,
  input  JAL_IN,
  input  JALR_IN,
  input  halt_IN,
  input  MemToReg_IN,
  input  MemWrite_IN,
  input  RegWrite_IN,
  input  [31:0] aluresult_IN,
  input  HIGH_IN,
  input  [9:0] MA_IN,
  input  [31:0] MDin_IN,
  input  [4:0] W_IN,
  input  [31:0] PC_IN,
  input  [31:0] IR_IN,
  input  [31:0] IMM_IN,
  input  en,
  input  CLK,
  output JAL_OUT,
  output JALR_OUT,
  output halt_OUT,
  output MemToReg_OUT,
  output MemWrite_OUT,
  output RegWrite_OUT,
  output [31:0] aluresult_OUT,
  output HIGH_OUT,
  output [9:0] MA_OUT,
  output [31:0] MDin_OUT,
  output [4:0] W_OUT,
  output [31:0] PC_OUT,
  output [31:0] IR_OUT,
  output [31:0] IMM_OUT
);

  wire multiplexer_1_out, multiplexer_2_out, multiplexer_3_out, multiplexer_4_out, multiplexer_5_out,
       multiplexer_6_out, multiplexer_8_out;
  wire [4:0] multiplexer_11_out;
  wire [9:0] multiplexer_9_out;
  wire [31:0] multiplexer_7_out, multiplexer_10_out, multiplexer_12_out, multiplexer_13_out,
       multiplexer_14_out;

  Multiplexer #(.select(1), .width(1), .disabled("Z"), .enable("false")) multiplexer_1 (
    .in0(JAL_IN), .in1(1'b0), .out(multiplexer_1_out), .sel(CLR));
  Multiplexer #(.select(1), .width(1), .disabled("Z"), .enable("false")) multiplexer_2 (
    .in0(JALR_IN), .in1(1'b0), .out(multiplexer_2_out), .sel(CLR));
  Multiplexer #(.select(1), .width(1), .disabled("Z"), .enable("false")) multiplexer_3 (
    .in0(halt_IN), .in1(1'b0), .out(multiplexer_3_out), .sel(CLR));
  Multiplexer #(.select(1), .width(1), .disabled("Z"), .enable("false")) multiplexer_4 (
    .in0(MemToReg_IN), .in1(1'b0), .out(multiplexer_4_out), .sel(CLR));
  Multiplexer #(.select(1), .width(1), .disabled("Z"), .enable("false")) multiplexer_5 (
    .in0(MemWrite_IN), .in1(1'b0), .out(multiplexer_5_out), .sel(CLR));
  Multiplexer #(.select(1), .width(1), .disabled("Z"), .enable("false")) multiplexer_6 (
    .in0(RegWrite_IN), .in1(1'b0), .out(multiplexer_6_out), .sel(CLR));
  Multiplexer #(.select(1), .width(32), .disabled("Z"), .enable("false")) multiplexer_7 (
    .in0(aluresult_IN), .in1({32{1'b0}}), .out(multiplexer_7_out), .sel(CLR));
  Multiplexer #(.select(1), .width(1), .disabled("Z"), .enable("false")) multiplexer_8 (
    .in0(HIGH_IN), .in1(1'b0), .out(multiplexer_8_out), .sel(CLR));
  Multiplexer #(.select(1), .width(10), .disabled("Z"), .enable("false")) multiplexer_9 (
    .in0(MA_IN), .in1({10{1'b0}}), .out(multiplexer_9_out), .sel(CLR));
  Multiplexer #(.select(1), .width(32), .disabled("Z"), .enable("false")) multiplexer_10 (
    .in0(MDin_IN), .in1({32{1'b0}}), .out(multiplexer_10_out), .sel(CLR));
  Multiplexer #(.select(1), .width(5), .disabled("Z"), .enable("false")) multiplexer_11 (
    .in0(W_IN), .in1({5{1'b0}}), .out(multiplexer_11_out), .sel(CLR));
  Multiplexer #(.select(1), .width(32), .disabled("Z"), .enable("false")) multiplexer_12 (
    .in0(PC_IN), .in1({32{1'b0}}), .out(multiplexer_12_out), .sel(CLR));
  Multiplexer #(.select(1), .width(32), .disabled("Z"), .enable("false")) multiplexer_13 (
    .in0(IR_IN), .in1({32{1'b0}}), .out(multiplexer_13_out), .sel(CLR));
  Multiplexer #(.select(1), .width(32), .disabled("Z"), .enable("false")) multiplexer_14 (
    .in0(IMM_IN), .in1({32{1'b0}}), .out(multiplexer_14_out), .sel(CLR));
  Register #(.width(1), .trigger("rising"), .Select("low")) register_1 (
    .D(multiplexer_1_out), .en(en), .Q(JAL_OUT), .clk(CLK), .clr(RST));
  Register #(.width(1), .trigger("rising"), .Select("low")) register_2 (
    .D(multiplexer_2_out), .en(en), .Q(JALR_OUT), .clk(CLK), .clr(RST));
  Register #(.width(1), .trigger("rising"), .Select("low")) register_3 (
    .D(multiplexer_3_out), .en(en), .Q(halt_OUT), .clk(CLK), .clr(RST));
  Register #(.width(1), .trigger("rising"), .Select("low")) register_4 (
    .D(multiplexer_4_out), .en(en), .Q(MemToReg_OUT), .clk(CLK), .clr(RST));
  Register #(.width(1), .trigger("rising"), .Select("low")) register_5 (
    .D(multiplexer_5_out), .en(en), .Q(MemWrite_OUT), .clk(CLK), .clr(RST));
  Register #(.width(1), .trigger("rising"), .Select("low")) register_6 (
    .D(multiplexer_6_out), .en(en), .Q(RegWrite_OUT), .clk(CLK), .clr(RST));
  Register #(.width(32), .trigger("rising"), .Select("low")) register_7 (
    .D(multiplexer_7_out), .en(en), .Q(aluresult_OUT), .clk(CLK), .clr(RST));
  Register #(.width(1), .trigger("rising"), .Select("low")) register_8 (
    .D(multiplexer_8_out), .en(en), .Q(HIGH_OUT), .clk(CLK), .clr(RST));
  Register #(.width(10), .trigger("rising"), .Select("low")) register_9 (
    .D(multiplexer_9_out), .en(en), .Q(MA_OUT), .clk(CLK), .clr(RST));
  Register #(.width(32), .trigger("rising"), .Select("low")) register_10 (
    .D(multiplexer_10_out), .en(en), .Q(MDin_OUT), .clk(CLK), .clr(RST));
  Register #(.width(5), .trigger("rising"), .Select("low")) register_11 (
    .D(multiplexer_11_out), .en(en), .Q(W_OUT), .clk(CLK), .clr(RST));
  Register #(.width(32), .trigger("rising"), .Select("low")) register_12 (
    .D(multiplexer_12_out), .en(en), .Q(PC_OUT), .clk(CLK), .clr(RST));
  Register #(.width(32), .trigger("rising"), .Select("low")) register_13 (
    .D(multiplexer_13_out), .en(en), .Q(IR_OUT), .clk(CLK), .clr(RST));
  Register #(.width(32), .trigger("rising"), .Select("low")) register_14 (
    .D(multiplexer_14_out), .en(en), .Q(IMM_OUT), .clk(CLK), .clr(RST));
endmodule

// MEM/WB
module MEM_WB2 (
  input  CLR,
  input  RST,
  input  JAL_IN,
  input  JALR_IN,
  input  halt_IN,
  input  MemToReg_IN,
  input  RegWrite_IN,
  input  [31:0] aluresult_IN,
  input  [31:0] Dout_IN,
  input  [4:0] W_IN,
  input  [31:0] IR_IN,
  input  [31:0] PC_IN,
  input  [31:0] IMM_IN,
  input  en,
  input  CLK,
  output JAL_OUT,
  output JALR_OUT,
  output halt_OUT,
  output MemToReg_OUT,
  output RegWrite_OUT,
  output [31:0] aluresult_OUT,
  output [31:0] Dout_OUT,
  output [4:0] W_OUT,
  output [31:0] IR_OUT,
  output [31:0] PC_OUT,
  output [31:0] IMM_OUT
);

  wire multiplexer_1_out, multiplexer_2_out, multiplexer_3_out, multiplexer_4_out, multiplexer_5_out;
  wire [4:0] multiplexer_8_out;
  wire [31:0] multiplexer_6_out, multiplexer_7_out, multiplexer_9_out, multiplexer_10_out, multiplexer_11_out;

  Multiplexer #(.select(1), .width(1), .disabled("Z"), .enable("false")) multiplexer_1 (
    .in0(JAL_IN), .in1(1'b0), .out(multiplexer_1_out), .sel(CLR));
  Multiplexer #(.select(1), .width(1), .disabled("Z"), .enable("false")) multiplexer_2 (
    .in0(JALR_IN), .in1(1'b0), .out(multiplexer_2_out), .sel(CLR));
  Multiplexer #(.select(1), .width(1), .disabled("Z"), .enable("false")) multiplexer_3 (
    .in0(halt_IN), .in1(1'b0), .out(multiplexer_3_out), .sel(CLR));
  Multiplexer #(.select(1), .width(1), .disabled("Z"), .enable("false")) multiplexer_4 (
    .in0(MemToReg_IN), .in1(1'b0), .out(multiplexer_4_out), .sel(CLR));
  Multiplexer #(.select(1), .width(1), .disabled("Z"), .enable("false")) multiplexer_5 (
    .in0(RegWrite_IN), .in1(1'b0), .out(multiplexer_5_out), .sel(CLR));
  Multiplexer #(.select(1), .width(32), .disabled("Z"), .enable("false")) multiplexer_6 (
    .in0(aluresult_IN), .in1({32{1'b0}}), .out(multiplexer_6_out), .sel(CLR));
  Multiplexer #(.select(1), .width(32), .disabled("Z"), .enable("false")) multiplexer_7 (
    .in0(Dout_IN), .in1({32{1'b0}}), .out(multiplexer_7_out), .sel(CLR));
  Multiplexer #(.select(1), .width(5), .disabled("Z"), .enable("false")) multiplexer_8 (
    .in0(W_IN), .in1({5{1'b0}}), .out(multiplexer_8_out), .sel(CLR));
  Multiplexer #(.select(1), .width(32), .disabled("Z"), .enable("false")) multiplexer_9 (
    .in0(IR_IN), .in1({32{1'b0}}), .out(multiplexer_9_out), .sel(CLR));
  Multiplexer #(.select(1), .width(32), .disabled("Z"), .enable("false")) multiplexer_10 (
    .in0(PC_IN), .in1({32{1'b0}}), .out(multiplexer_10_out), .sel(CLR));
  Multiplexer #(.select(1), .width(32), .disabled("Z"), .enable("false")) multiplexer_11 (
    .in0(IMM_IN), .in1({32{1'b0}}), .out(multiplexer_11_out), .sel(CLR));
  Register #(.width(1), .trigger("rising"), .Select("low")) register_1 (
    .D(multiplexer_1_out), .en(en), .Q(JAL_OUT), .clk(CLK), .clr(RST));
  Register #(.width(1), .trigger("rising"), .Select("low")) register_2 (
    .D(multiplexer_2_out), .en(en), .Q(JALR_OUT), .clk(CLK), .clr(RST));
  Register #(.width(1), .trigger("rising"), .Select("low")) register_3 (
    .D(multiplexer_3_out), .en(en), .Q(halt_OUT), .clk(CLK), .clr(RST));
  Register #(.width(1), .trigger("rising"), .Select("low")) register_4 (
    .D(multiplexer_4_out), .en(en), .Q(MemToReg_OUT), .clk(CLK), .clr(RST));
  Register #(.width(1), .trigger("rising"), .Select("low")) register_5 (
    .D(multiplexer_5_out), .en(en), .Q(RegWrite_OUT), .clk(CLK), .clr(RST));
  Register #(.width(32), .trigger("rising"), .Select("low")) register_6 (
    .D(multiplexer_6_out), .en(en), .Q(aluresult_OUT), .clk(CLK), .clr(RST));
  Register #(.width(32), .trigger("rising"), .Select("low")) register_7 (
    .D(multiplexer_7_out), .en(en), .Q(Dout_OUT), .clk(CLK), .clr(RST));
  Register #(.width(5), .trigger("rising"), .Select("low")) register_8 (
    .D(multiplexer_8_out), .en(en), .Q(W_OUT), .clk(CLK), .clr(RST));
  Register #(.width(32), .trigger("rising"), .Select("low")) register_9 (
    .D(multiplexer_9_out), .en(en), .Q(IR_OUT), .clk(CLK), .clr(RST));
  Register #(.width(32), .trigger("rising"), .Select("low")) register_10 (
    .D(multiplexer_10_out), .en(en), .Q(PC_OUT), .clk(CLK), .clr(RST));
  Register #(.width(32), .trigger("rising"), .Select("low")) register_11 (
    .D(multiplexer_11_out), .en(en), .Q(IMM_OUT), .clk(CLK), .clr(RST));
endmodule

module CLASH (
  input  [4:0] R1_num,
  input  [4:0] EX_W_num,
  input  EX_RegWrite,
  input  [4:0] R2_num,
  input  [4:0] OP,
  input  [4:0] MEM_W_num,
  input  MEM_RegWrite,
  output clash
);

  wire and_1_out, and_2_out, and_3_out, and_4_out, and_5_out, and_6_out, and_7_out, and_8_out,
       comparator_1_eq, comparator_2_eq, comparator_3_eq, comparator_4_eq, comparator_5_eq, comparator_6_eq,
       comparator_7_eq, comparator_8_eq, comparator_9_eq, comparator_10_eq, comparator_11_eq,
       comparator_12_eq, comparator_13_eq, comparator_14_eq, comparator_15_eq, not_1_out, not_2_out,
       not_3_out, not_4_out, or_1_out, or_2_out;

  Comparator #(.width(5), .mode("twosComplement")) comparator_1 (
    .a({5{1'b0}}), .b(R1_num), .eq(comparator_1_eq));  // open: gt, lt
  Comparator #(.width(5), .mode("twosComplement")) comparator_2 (
    .a(R1_num), .b(EX_W_num), .eq(comparator_2_eq));  // open: gt, lt
  Comparator #(.width(5), .mode("twosComplement")) comparator_3 (
    .a(EX_W_num), .b(R2_num), .eq(comparator_3_eq));  // open: gt, lt
  Comparator #(.width(5), .mode("twosComplement")) comparator_4 (
    .a(R2_num), .b({5{1'b0}}), .eq(comparator_4_eq));  // open: gt, lt
  Comparator #(.width(5), .mode("twosComplement")) comparator_5 (
    .a(5'b00100), .b(OP), .eq(comparator_5_eq));  // open: gt, lt
  Comparator #(.width(5), .mode("twosComplement")) comparator_6 (
    .a(5'b01000), .b(OP), .eq(comparator_6_eq));  // open: gt, lt
  Comparator #(.width(5), .mode("twosComplement")) comparator_7 (
    .a(OP), .b(5'b01100), .eq(comparator_7_eq));  // open: gt, lt
  Comparator #(.width(5), .mode("twosComplement")) comparator_8 (
    .a(OP), .b(5'b11000), .eq(comparator_8_eq));  // open: gt, lt
  Comparator #(.width(5), .mode("twosComplement")) comparator_9 (
    .a(OP), .b(5'b11100), .eq(comparator_9_eq));  // open: gt, lt
  Comparator #(.width(5), .mode("twosComplement")) comparator_10 (
    .a(OP), .b({5{1'b0}}), .eq(comparator_10_eq));  // open: gt, lt
  Comparator #(.width(5), .mode("twosComplement")) comparator_11 (
    .a(OP), .b(5'b11001), .eq(comparator_11_eq));  // open: gt, lt
  Comparator #(.width(5), .mode("twosComplement")) comparator_12 (
    .a({5{1'b0}}), .b(R1_num), .eq(comparator_12_eq));  // open: gt, lt
  Comparator #(.width(5), .mode("twosComplement")) comparator_13 (
    .a(R1_num), .b(MEM_W_num), .eq(comparator_13_eq));  // open: gt, lt
  Comparator #(.width(5), .mode("twosComplement")) comparator_14 (
    .a(MEM_W_num), .b(R2_num), .eq(comparator_14_eq));  // open: gt, lt
  Comparator #(.width(5), .mode("twosComplement")) comparator_15 (
    .a(R2_num), .b({5{1'b0}}), .eq(comparator_15_eq));  // open: gt, lt
  not not_1 (not_1_out, comparator_1_eq);
  not not_2 (not_2_out, comparator_4_eq);
  not not_3 (not_3_out, comparator_12_eq);
  not not_4 (not_4_out, comparator_15_eq);
  and and_1 (and_1_out, not_1_out, comparator_2_eq, EX_RegWrite);
  and and_2 (and_2_out, EX_RegWrite, comparator_3_eq, not_2_out);
  and and_3 (and_3_out, not_3_out, comparator_13_eq, MEM_RegWrite);
  and and_4 (and_4_out, MEM_RegWrite, comparator_14_eq, not_4_out);
  or or_1 (or_1_out, comparator_5_eq, comparator_6_eq, comparator_7_eq, comparator_8_eq, comparator_9_eq, comparator_10_eq, comparator_11_eq);
  or or_2 (or_2_out, comparator_6_eq, comparator_7_eq, comparator_8_eq);
  and and_5 (and_5_out, and_1_out, or_1_out);
  and and_6 (and_6_out, or_1_out, and_3_out);
  and and_7 (and_7_out, or_2_out, and_4_out);
  and and_8 (and_8_out, and_2_out, or_2_out);
  or or_3 (clash, and_5_out, and_8_out, and_6_out, and_7_out);
endmodule

module REDIRECT (
  input  [4:0] R1_num,
  input  [4:0] EX_W_num,
  input  EX_RegWrite,
  input  [4:0] R2_num,
  input  EX_MEMTOREG,
  input  [4:0] OP,
  input  [2:0] funct3,
  input  [4:0] MEM_W_num,
  input  MEM_RegWrite,
  output clash,
  output [1:0] R1_FORWARD,
  output [1:0] R2_FORWARD
);

  wire and_1_out, and_2_out, and_3_out, and_4_out, and_5_out, and_6_out, and_7_out, and_8_out, and_9_out,
       comparator_1_eq, comparator_2_eq, comparator_3_eq, comparator_4_eq, comparator_5_eq, comparator_6_eq,
       comparator_7_eq, comparator_8_eq, comparator_9_eq, comparator_10_eq, comparator_11_eq,
       comparator_12_eq, comparator_13_eq, comparator_14_eq, comparator_15_eq, comparator_16_eq, not_1_out,
       not_2_out, not_3_out, not_4_out, or_1_out, or_2_out, or_3_out;
  wire [1:0] multiplexer_1_out, multiplexer_2_out, multiplexer_3_out, multiplexer_4_out;

  Comparator #(.width(3), .mode("twosComplement")) comparator_1 (
    .a(funct3), .b(3'b000), .eq(comparator_1_eq));  // open: gt, lt
  Comparator #(.width(5), .mode("twosComplement")) comparator_2 (
    .a({5{1'b0}}), .b(R1_num), .eq(comparator_2_eq));  // open: gt, lt
  Comparator #(.width(5), .mode("twosComplement")) comparator_3 (
    .a(R1_num), .b(EX_W_num), .eq(comparator_3_eq));  // open: gt, lt
  Comparator #(.width(5), .mode("twosComplement")) comparator_4 (
    .a(EX_W_num), .b(R2_num), .eq(comparator_4_eq));  // open: gt, lt
  Comparator #(.width(5), .mode("twosComplement")) comparator_5 (
    .a(R2_num), .b({5{1'b0}}), .eq(comparator_5_eq));  // open: gt, lt
  Comparator #(.width(5), .mode("twosComplement")) comparator_6 (
    .a(5'b00100), .b(OP), .eq(comparator_6_eq));  // open: gt, lt
  Comparator #(.width(5), .mode("twosComplement")) comparator_7 (
    .a(5'b01000), .b(OP), .eq(comparator_7_eq));  // open: gt, lt
  Comparator #(.width(5), .mode("twosComplement")) comparator_8 (
    .a(OP), .b(5'b01100), .eq(comparator_8_eq));  // open: gt, lt
  Comparator #(.width(5), .mode("twosComplement")) comparator_9 (
    .a(OP), .b(5'b11000), .eq(comparator_9_eq));  // open: gt, lt
  Comparator #(.width(5), .mode("twosComplement")) comparator_10 (
    .a(OP), .b(5'b11100), .eq(comparator_10_eq));  // open: gt, lt
  Comparator #(.width(5), .mode("twosComplement")) comparator_11 (
    .a(OP), .b({5{1'b0}}), .eq(comparator_11_eq));  // open: gt, lt
  Comparator #(.width(5), .mode("twosComplement")) comparator_12 (
    .a(OP), .b(5'b11001), .eq(comparator_12_eq));  // open: gt, lt
  Comparator #(.width(5), .mode("twosComplement")) comparator_13 (
    .a({5{1'b0}}), .b(R1_num), .eq(comparator_13_eq));  // open: gt, lt
  Comparator #(.width(5), .mode("twosComplement")) comparator_14 (
    .a(R1_num), .b(MEM_W_num), .eq(comparator_14_eq));  // open: gt, lt
  Comparator #(.width(5), .mode("twosComplement")) comparator_15 (
    .a(MEM_W_num), .b(R2_num), .eq(comparator_15_eq));  // open: gt, lt
  Comparator #(.width(5), .mode("twosComplement")) comparator_16 (
    .a(R2_num), .b({5{1'b0}}), .eq(comparator_16_eq));  // open: gt, lt
  not not_1 (not_1_out, comparator_2_eq);
  not not_2 (not_2_out, comparator_5_eq);
  not not_3 (not_3_out, comparator_13_eq);
  not not_4 (not_4_out, comparator_16_eq);
  and and_1 (and_1_out, not_1_out, comparator_3_eq, EX_RegWrite);
  and and_2 (and_2_out, EX_RegWrite, comparator_4_eq, not_2_out);
  and and_3 (and_3_out, not_3_out, comparator_14_eq, MEM_RegWrite);
  and and_4 (and_4_out, MEM_RegWrite, comparator_15_eq, not_4_out);
  or or_1 (or_1_out, comparator_6_eq, comparator_7_eq, comparator_8_eq, comparator_9_eq, comparator_10_eq, comparator_11_eq, comparator_12_eq);
  or or_2 (or_2_out, comparator_7_eq, comparator_8_eq, comparator_9_eq, and_5_out);
  and and_5 (and_5_out, comparator_1_eq, comparator_10_eq);
  and and_6 (and_6_out, and_1_out, or_1_out);
  and and_7 (and_7_out, or_1_out, and_3_out);
  and and_8 (and_8_out, or_2_out, and_4_out);
  and and_9 (and_9_out, and_2_out, or_2_out);
  Multiplexer #(.select(1), .width(2), .disabled("Z"), .enable("false")) multiplexer_1 (
    .in0(2'b00), .in1(2'b01), .out(multiplexer_1_out), .sel(and_6_out));
  or or_3 (or_3_out, and_6_out, and_9_out);
  Multiplexer #(.select(1), .width(2), .disabled("Z"), .enable("false")) multiplexer_2 (
    .in0(2'b00), .in1(2'b01), .out(multiplexer_2_out), .sel(and_9_out));
  and and_10 (clash, or_3_out, EX_MEMTOREG);
  Multiplexer #(.select(1), .width(2), .disabled("Z"), .enable("false")) multiplexer_3 (
    .in0(2'b00), .in1(2'b10), .out(multiplexer_3_out), .sel(and_7_out));
  Multiplexer #(.select(1), .width(2), .disabled("Z"), .enable("false")) multiplexer_4 (
    .in0(2'b00), .in1(2'b10), .out(multiplexer_4_out), .sel(and_8_out));
  Multiplexer #(.select(1), .width(2), .disabled("Z"), .enable("false")) multiplexer_5 (
    .in0(multiplexer_3_out), .in1(multiplexer_1_out), .out(R1_FORWARD), .sel(and_6_out));
  Multiplexer #(.select(1), .width(2), .disabled("Z"), .enable("false")) multiplexer_6 (
    .in0(multiplexer_4_out), .in1(multiplexer_2_out), .out(R2_FORWARD), .sel(and_9_out));
endmodule

// ID/EX
module ID_EX2 (
  input  CLK,
  input  RST,
  input  JAL,
  input  JALR,
  input  BEQ,
  input  BNE,
  input  MEMTOREG,
  input  MEMWRITE,
  input  [3:0] ALUOP,
  input  ALUSRC,
  input  REGWRITE,
  input  ECALL,
  input  BGEU_IN,
  input  [31:0] R1,
  input  [31:0] R2,
  input  [4:0] W_num,
  input  [31:0] IMM,
  input  [31:0] B,
  input  [31:0] IR,
  input  [31:0] J,
  input  [31:0] PC,
  input  CLR,
  input  EN,
  output JAL_OUT,
  output JALR_OUT,
  output BEQ_OUT,
  output BNE_OUT,
  output MEMTOREG_OUT,
  output MEMWRITE_OUT,
  output [3:0] ALUOP_OUT,
  output ALUSRC_OUT,
  output REGWRITE_OUT,
  output ECALL_OUT,
  output BGEU_OUT,
  output [31:0] R1_OUT,
  output [31:0] R2_OUT,
  output [4:0] W__OUT,
  output [31:0] IMM_OUT,
  output [31:0] B_OUT,
  output [31:0] IR_OUT,
  output [31:0] J_OUT,
  output [31:0] PC_OUT
);

  wire multiplexer_1_out, multiplexer_2_out, multiplexer_3_out, multiplexer_4_out, multiplexer_5_out,
       multiplexer_6_out, multiplexer_8_out, multiplexer_9_out, multiplexer_10_out, multiplexer_11_out;
  wire [3:0] multiplexer_7_out;
  wire [4:0] multiplexer_14_out;
  wire [31:0] multiplexer_12_out, multiplexer_13_out, multiplexer_15_out, multiplexer_16_out,
       multiplexer_17_out, multiplexer_18_out, multiplexer_19_out;

  Multiplexer #(.select(1), .width(1), .disabled("Z"), .enable("false")) multiplexer_1 (
    .in0(JAL), .in1(1'b0), .out(multiplexer_1_out), .sel(CLR));
  Multiplexer #(.select(1), .width(1), .disabled("Z"), .enable("false")) multiplexer_2 (
    .in0(JALR), .in1(1'b0), .out(multiplexer_2_out), .sel(CLR));
  Multiplexer #(.select(1), .width(1), .disabled("Z"), .enable("false")) multiplexer_3 (
    .in0(BEQ), .in1(1'b0), .out(multiplexer_3_out), .sel(CLR));
  Multiplexer #(.select(1), .width(1), .disabled("Z"), .enable("false")) multiplexer_4 (
    .in0(BNE), .in1(1'b0), .out(multiplexer_4_out), .sel(CLR));
  Multiplexer #(.select(1), .width(1), .disabled("Z"), .enable("false")) multiplexer_5 (
    .in0(MEMTOREG), .in1(1'b0), .out(multiplexer_5_out), .sel(CLR));
  Multiplexer #(.select(1), .width(1), .disabled("Z"), .enable("false")) multiplexer_6 (
    .in0(MEMWRITE), .in1(1'b0), .out(multiplexer_6_out), .sel(CLR));
  Multiplexer #(.select(1), .width(4), .disabled("Z"), .enable("false")) multiplexer_7 (
    .in0(ALUOP), .in1(4'b0000), .out(multiplexer_7_out), .sel(CLR));
  Multiplexer #(.select(1), .width(1), .disabled("Z"), .enable("false")) multiplexer_8 (
    .in0(ALUSRC), .in1(1'b0), .out(multiplexer_8_out), .sel(CLR));
  Multiplexer #(.select(1), .width(1), .disabled("Z"), .enable("false")) multiplexer_9 (
    .in0(REGWRITE), .in1(1'b0), .out(multiplexer_9_out), .sel(CLR));
  Multiplexer #(.select(1), .width(1), .disabled("Z"), .enable("false")) multiplexer_10 (
    .in0(ECALL), .in1(1'b0), .out(multiplexer_10_out), .sel(CLR));
  Multiplexer #(.select(1), .width(1), .disabled("Z"), .enable("false")) multiplexer_11 (
    .in0(BGEU_IN), .in1(1'b0), .out(multiplexer_11_out), .sel(CLR));
  Multiplexer #(.select(1), .width(32), .disabled("Z"), .enable("false")) multiplexer_12 (
    .in0(R1), .in1({32{1'b0}}), .out(multiplexer_12_out), .sel(CLR));
  Multiplexer #(.select(1), .width(32), .disabled("Z"), .enable("false")) multiplexer_13 (
    .in0(R2), .in1({32{1'b0}}), .out(multiplexer_13_out), .sel(CLR));
  Multiplexer #(.select(1), .width(5), .disabled("Z"), .enable("false")) multiplexer_14 (
    .in0(W_num), .in1({5{1'b0}}), .out(multiplexer_14_out), .sel(CLR));
  Multiplexer #(.select(1), .width(32), .disabled("Z"), .enable("false")) multiplexer_15 (
    .in0(IMM), .in1({32{1'b0}}), .out(multiplexer_15_out), .sel(CLR));
  Multiplexer #(.select(1), .width(32), .disabled("Z"), .enable("false")) multiplexer_16 (
    .in0(B), .in1({32{1'b0}}), .out(multiplexer_16_out), .sel(CLR));
  Multiplexer #(.select(1), .width(32), .disabled("Z"), .enable("false")) multiplexer_17 (
    .in0(IR), .in1({32{1'b0}}), .out(multiplexer_17_out), .sel(CLR));
  Multiplexer #(.select(1), .width(32), .disabled("Z"), .enable("false")) multiplexer_18 (
    .in0(J), .in1({32{1'b0}}), .out(multiplexer_18_out), .sel(CLR));
  Multiplexer #(.select(1), .width(32), .disabled("Z"), .enable("false")) multiplexer_19 (
    .in0(PC), .in1({32{1'b0}}), .out(multiplexer_19_out), .sel(CLR));
  Register #(.width(1), .trigger("rising"), .Select("low")) register_1 (
    .D(multiplexer_1_out), .en(EN), .Q(JAL_OUT), .clk(CLK), .clr(RST));
  Register #(.width(1), .trigger("rising"), .Select("low")) register_2 (
    .D(multiplexer_2_out), .en(EN), .Q(JALR_OUT), .clk(CLK), .clr(RST));
  Register #(.width(1), .trigger("rising"), .Select("low")) register_3 (
    .D(multiplexer_3_out), .en(EN), .Q(BEQ_OUT), .clk(CLK), .clr(RST));
  Register #(.width(1), .trigger("rising"), .Select("low")) register_4 (
    .D(multiplexer_4_out), .en(EN), .Q(BNE_OUT), .clk(CLK), .clr(RST));
  Register #(.width(1), .trigger("rising"), .Select("low")) register_5 (
    .D(multiplexer_5_out), .en(EN), .Q(MEMTOREG_OUT), .clk(CLK), .clr(RST));
  Register #(.width(1), .trigger("rising"), .Select("low")) register_6 (
    .D(multiplexer_6_out), .en(EN), .Q(MEMWRITE_OUT), .clk(CLK), .clr(RST));
  Register #(.width(4), .trigger("rising"), .Select("low")) register_7 (
    .D(multiplexer_7_out), .en(EN), .Q(ALUOP_OUT), .clk(CLK), .clr(RST));
  Register #(.width(1), .trigger("rising"), .Select("low")) register_8 (
    .D(multiplexer_8_out), .en(EN), .Q(ALUSRC_OUT), .clk(CLK), .clr(RST));
  Register #(.width(1), .trigger("rising"), .Select("low")) register_9 (
    .D(multiplexer_9_out), .en(EN), .Q(REGWRITE_OUT), .clk(CLK), .clr(RST));
  Register #(.width(1), .trigger("rising"), .Select("low")) register_10 (
    .D(multiplexer_10_out), .en(EN), .Q(ECALL_OUT), .clk(CLK), .clr(RST));
  Register #(.width(1), .trigger("rising"), .Select("low")) register_11 (
    .D(multiplexer_11_out), .en(EN), .Q(BGEU_OUT), .clk(CLK), .clr(RST));
  Register #(.width(32), .trigger("rising"), .Select("low")) register_12 (
    .D(multiplexer_12_out), .en(EN), .Q(R1_OUT), .clk(CLK), .clr(RST));
  Register #(.width(32), .trigger("rising"), .Select("low")) register_13 (
    .D(multiplexer_13_out), .en(EN), .Q(R2_OUT), .clk(CLK), .clr(RST));
  Register #(.width(5), .trigger("rising"), .Select("low")) register_14 (
    .D(multiplexer_14_out), .en(EN), .Q(W__OUT), .clk(CLK), .clr(RST));
  Register #(.width(32), .trigger("rising"), .Select("low")) register_15 (
    .D(multiplexer_15_out), .en(EN), .Q(IMM_OUT), .clk(CLK), .clr(RST));
  Register #(.width(32), .trigger("rising"), .Select("low")) register_16 (
    .D(multiplexer_16_out), .en(EN), .Q(B_OUT), .clk(CLK), .clr(RST));
  Register #(.width(32), .trigger("rising"), .Select("low")) register_17 (
    .D(multiplexer_17_out), .en(EN), .Q(IR_OUT), .clk(CLK), .clr(RST));
  Register #(.width(32), .trigger("rising"), .Select("low")) register_18 (
    .D(multiplexer_18_out), .en(EN), .Q(J_OUT), .clk(CLK), .clr(RST));
  Register #(.width(32), .trigger("rising"), .Select("low")) register_19 (
    .D(multiplexer_19_out), .en(EN), .Q(PC_OUT), .clk(CLK), .clr(RST));
endmodule
// ID/EX
module ID_EX3 (
  input  CLK,
  input  RST,
  input  JAL,
  input  JALR,
  input  URET_IN,
  input  BEQ,
  input  BNE,
  input  MEMTOREG,
  input  MEMWRITE,
  input  [3:0] ALUOP,
  input  ALUSRC,
  input  REGWRITE,
  input  ECALL,
  input  [31:0] R1,
  input  [1:0] R1FORWARD,
  input  [31:0] R2,
  input  [1:0] R2FORWARD,
  input  [4:0] W_num,
  input  [31:0] IMM,
  input  [31:0] B,
  input  PREDICTJUMP_IN,
  input  [31:0] IR,
  input  [31:0] J,
  input  [31:0] PC,
  input  BGEU_IN,
  input  CLR,
  input  EN,
  output JAL_OUT,
  output JALR_OUT,
  output URET_OUT,
  output BEQ_OUT,
  output BNE_OUT,
  output MEMTOREG_OUT,
  output MEMWRITE_OUT,
  output [3:0] ALUOP_OUT,
  output ALUSRC_OUT,
  output REGWRITE_OUT,
  output ECALL_OUT,
  output [31:0] R1_OUT,
  output [1:0] R1FORWARD_OUT,
  output [31:0] R2_OUT,
  output [1:0] R2FORWARD_OUT,
  output [4:0] W__OUT,
  output [31:0] IMM_OUT,
  output [31:0] B_OUT,
  output PREDICTJUMP_OUT,
  output [31:0] IR_OUT,
  output [31:0] J_OUT,
  output [31:0] PC_OUT,
  output BGEU_OUT
);

  wire multiplexer_1_out, multiplexer_2_out, multiplexer_3_out, multiplexer_4_out, multiplexer_5_out,
       multiplexer_6_out, multiplexer_7_out, multiplexer_9_out, multiplexer_10_out, multiplexer_11_out,
       multiplexer_19_out, multiplexer_23_out;
  wire [1:0] multiplexer_13_out, multiplexer_15_out;
  wire [3:0] multiplexer_8_out;
  wire [4:0] multiplexer_16_out;
  wire [31:0] multiplexer_12_out, multiplexer_14_out, multiplexer_17_out, multiplexer_18_out,
       multiplexer_20_out, multiplexer_21_out, multiplexer_22_out;

  Multiplexer #(.select(1), .width(1), .disabled("Z"), .enable("false")) multiplexer_1 (
    .in0(JAL), .in1(1'b0), .out(multiplexer_1_out), .sel(CLR));
  Multiplexer #(.select(1), .width(1), .disabled("Z"), .enable("false")) multiplexer_2 (
    .in0(JALR), .in1(1'b0), .out(multiplexer_2_out), .sel(CLR));
  Multiplexer #(.select(1), .width(1), .disabled("Z"), .enable("false")) multiplexer_3 (
    .in0(URET_IN), .in1(1'b0), .out(multiplexer_3_out), .sel(CLR));
  Multiplexer #(.select(1), .width(1), .disabled("Z"), .enable("false")) multiplexer_4 (
    .in0(BEQ), .in1(1'b0), .out(multiplexer_4_out), .sel(CLR));
  Multiplexer #(.select(1), .width(1), .disabled("Z"), .enable("false")) multiplexer_5 (
    .in0(BNE), .in1(1'b0), .out(multiplexer_5_out), .sel(CLR));
  Multiplexer #(.select(1), .width(1), .disabled("Z"), .enable("false")) multiplexer_6 (
    .in0(MEMTOREG), .in1(1'b0), .out(multiplexer_6_out), .sel(CLR));
  Multiplexer #(.select(1), .width(1), .disabled("Z"), .enable("false")) multiplexer_7 (
    .in0(MEMWRITE), .in1(1'b0), .out(multiplexer_7_out), .sel(CLR));
  Multiplexer #(.select(1), .width(4), .disabled("Z"), .enable("false")) multiplexer_8 (
    .in0(ALUOP), .in1(4'b0000), .out(multiplexer_8_out), .sel(CLR));
  Multiplexer #(.select(1), .width(1), .disabled("Z"), .enable("false")) multiplexer_9 (
    .in0(ALUSRC), .in1(1'b0), .out(multiplexer_9_out), .sel(CLR));
  Multiplexer #(.select(1), .width(1), .disabled("Z"), .enable("false")) multiplexer_10 (
    .in0(REGWRITE), .in1(1'b0), .out(multiplexer_10_out), .sel(CLR));
  Multiplexer #(.select(1), .width(1), .disabled("Z"), .enable("false")) multiplexer_11 (
    .in0(ECALL), .in1(1'b0), .out(multiplexer_11_out), .sel(CLR));
  Multiplexer #(.select(1), .width(32), .disabled("Z"), .enable("false")) multiplexer_12 (
    .in0(R1), .in1({32{1'b0}}), .out(multiplexer_12_out), .sel(CLR));
  Multiplexer #(.select(1), .width(2), .disabled("Z"), .enable("false")) multiplexer_13 (
    .in0(R1FORWARD), .in1(2'b00), .out(multiplexer_13_out), .sel(CLR));
  Multiplexer #(.select(1), .width(32), .disabled("Z"), .enable("false")) multiplexer_14 (
    .in0(R2), .in1({32{1'b0}}), .out(multiplexer_14_out), .sel(CLR));
  Multiplexer #(.select(1), .width(2), .disabled("Z"), .enable("false")) multiplexer_15 (
    .in0(R2FORWARD), .in1(2'b00), .out(multiplexer_15_out), .sel(CLR));
  Multiplexer #(.select(1), .width(5), .disabled("Z"), .enable("false")) multiplexer_16 (
    .in0(W_num), .in1({5{1'b0}}), .out(multiplexer_16_out), .sel(CLR));
  Multiplexer #(.select(1), .width(32), .disabled("Z"), .enable("false")) multiplexer_17 (
    .in0(IMM), .in1({32{1'b0}}), .out(multiplexer_17_out), .sel(CLR));
  Multiplexer #(.select(1), .width(32), .disabled("Z"), .enable("false")) multiplexer_18 (
    .in0(B), .in1({32{1'b0}}), .out(multiplexer_18_out), .sel(CLR));
  Multiplexer #(.select(1), .width(1), .disabled("Z"), .enable("false")) multiplexer_19 (
    .in0(PREDICTJUMP_IN), .in1(1'b0), .out(multiplexer_19_out), .sel(CLR));
  Multiplexer #(.select(1), .width(32), .disabled("Z"), .enable("false")) multiplexer_20 (
    .in0(IR), .in1({32{1'b0}}), .out(multiplexer_20_out), .sel(CLR));
  Multiplexer #(.select(1), .width(32), .disabled("Z"), .enable("false")) multiplexer_21 (
    .in0(J), .in1({32{1'b0}}), .out(multiplexer_21_out), .sel(CLR));
  Multiplexer #(.select(1), .width(32), .disabled("Z"), .enable("false")) multiplexer_22 (
    .in0(PC), .in1({32{1'b0}}), .out(multiplexer_22_out), .sel(CLR));
  Multiplexer #(.select(1), .width(1), .disabled("Z"), .enable("false")) multiplexer_23 (
    .in0(BGEU_IN), .in1(1'b0), .out(multiplexer_23_out), .sel(CLR));
  Register #(.width(1), .trigger("rising"), .Select("low")) register_1 (
    .D(multiplexer_1_out), .en(EN), .Q(JAL_OUT), .clk(CLK), .clr(RST));
  Register #(.width(1), .trigger("rising"), .Select("low")) register_2 (
    .D(multiplexer_2_out), .en(EN), .Q(JALR_OUT), .clk(CLK), .clr(RST));
  Register #(.width(1), .trigger("rising"), .Select("low")) register_3 (
    .D(multiplexer_3_out), .en(EN), .Q(URET_OUT), .clk(CLK), .clr(RST));
  Register #(.width(1), .trigger("rising"), .Select("low")) register_4 (
    .D(multiplexer_4_out), .en(EN), .Q(BEQ_OUT), .clk(CLK), .clr(RST));
  Register #(.width(1), .trigger("rising"), .Select("low")) register_5 (
    .D(multiplexer_5_out), .en(EN), .Q(BNE_OUT), .clk(CLK), .clr(RST));
  Register #(.width(1), .trigger("rising"), .Select("low")) register_6 (
    .D(multiplexer_6_out), .en(EN), .Q(MEMTOREG_OUT), .clk(CLK), .clr(RST));
  Register #(.width(1), .trigger("rising"), .Select("low")) register_7 (
    .D(multiplexer_7_out), .en(EN), .Q(MEMWRITE_OUT), .clk(CLK), .clr(RST));
  Register #(.width(4), .trigger("rising"), .Select("low")) register_8 (
    .D(multiplexer_8_out), .en(EN), .Q(ALUOP_OUT), .clk(CLK), .clr(RST));
  Register #(.width(1), .trigger("rising"), .Select("low")) register_9 (
    .D(multiplexer_9_out), .en(EN), .Q(ALUSRC_OUT), .clk(CLK), .clr(RST));
  Register #(.width(1), .trigger("rising"), .Select("low")) register_10 (
    .D(multiplexer_10_out), .en(EN), .Q(REGWRITE_OUT), .clk(CLK), .clr(RST));
  Register #(.width(1), .trigger("rising"), .Select("low")) register_11 (
    .D(multiplexer_11_out), .en(EN), .Q(ECALL_OUT), .clk(CLK), .clr(RST));
  Register #(.width(32), .trigger("rising"), .Select("low")) register_12 (
    .D(multiplexer_12_out), .en(EN), .Q(R1_OUT), .clk(CLK), .clr(RST));
  Register #(.width(2), .trigger("rising"), .Select("low")) register_13 (
    .D(multiplexer_13_out), .en(EN), .Q(R1FORWARD_OUT), .clk(CLK), .clr(RST));
  Register #(.width(32), .trigger("rising"), .Select("low")) register_14 (
    .D(multiplexer_14_out), .en(EN), .Q(R2_OUT), .clk(CLK), .clr(RST));
  Register #(.width(2), .trigger("rising"), .Select("low")) register_15 (
    .D(multiplexer_15_out), .en(EN), .Q(R2FORWARD_OUT), .clk(CLK), .clr(RST));
  Register #(.width(5), .trigger("rising"), .Select("low")) register_16 (
    .D(multiplexer_16_out), .en(EN), .Q(W__OUT), .clk(CLK), .clr(RST));
  Register #(.width(32), .trigger("rising"), .Select("low")) register_17 (
    .D(multiplexer_17_out), .en(EN), .Q(IMM_OUT), .clk(CLK), .clr(RST));
  Register #(.width(32), .trigger("rising"), .Select("low")) register_18 (
    .D(multiplexer_18_out), .en(EN), .Q(B_OUT), .clk(CLK), .clr(RST));
  Register #(.width(1), .trigger("rising"), .Select("low")) register_19 (
    .D(multiplexer_19_out), .en(EN), .Q(PREDICTJUMP_OUT), .clk(CLK), .clr(RST));
  Register #(.width(32), .trigger("rising"), .Select("low")) register_20 (
    .D(multiplexer_20_out), .en(EN), .Q(IR_OUT), .clk(CLK), .clr(RST));
  Register #(.width(32), .trigger("rising"), .Select("low")) register_21 (
    .D(multiplexer_21_out), .en(EN), .Q(J_OUT), .clk(CLK), .clr(RST));
  Register #(.width(32), .trigger("rising"), .Select("low")) register_22 (
    .D(multiplexer_22_out), .en(EN), .Q(PC_OUT), .clk(CLK), .clr(RST));
  Register #(.width(1), .trigger("rising"), .Select("low")) register_23 (
    .D(multiplexer_23_out), .en(EN), .Q(BGEU_OUT), .clk(CLK), .clr(RST));
endmodule

module \动态分支预测  (
  output RegWrite,
  output MemWrite,
  output [31:0] IF_PC,
  output [31:0] ID_PC,
  output [31:0] EX_PC,
  output [31:0] M_PC,
  output [31:0] WB_PC,
  output [31:0] RDin,
  output [31:0] MDin,
  output [31:0] LedData
);

  wire AluSrcB, and_1_out, and_2_out, and_3_out, and_5_out, and_6_out, and_7_out, and_8_out, BEQ, BGEU, BNE,
       branch, clash, CLK, clock_1_out, comparator_1_eq, comparator_1_lt, comparator_3_eq, comparator_5_eq,
       CORRECT, d_ff_1_q, ecall, equal, EX_BRANCH, ex_mem2_1_halt_out, ex_mem2_1_high_out, ex_mem2_1_jal_out,
       ex_mem2_1_jalr_out, ex_memtoreg, EX_rw, flag, GE, Go, halt, id_ex3_1_ecall_out, id_ex3_1_memwrite_out,
       if_id2_1_predictjump_out, IR1, IR2, IR3, JAL, JALR, mem_memtoreg, MEM_rw, mem_wb2_1_jal_out,
       mem_wb2_1_jalr_out, MemToReg, nand_1_out, not_1_out, not_2_out, not_3_out, not_4_out, not_5_out,
       not_6_out, not_7_out, not_8_out, not_9_out, not_10_out, or_1_out, or_3_out, or_4_out, or_5_out,
       or_6_out, or_9_out, or_10_out, or_11_out, or_12_out, or_13_out, PREDICT_JUMP, PREDICTJUMP,
       riscv_probe_6_p2, RST, S_type, tunnel1, W1, W2, W3, \单周期硬布线控制器_1_alu_src , \单周期硬布线控制器_1_beq ,
       \单周期硬布线控制器_1_bgeu , \单周期硬布线控制器_1_bne , \单周期硬布线控制器_1_jal , \单周期硬布线控制器_1_jalr , \单周期硬布线控制器_1_memtoreg ,
       \单周期硬布线控制器_1_memwrite , \单周期硬布线控制器_1_regwrite ;
  wire [1:0] id_ex3_1_r1forward_out, id_ex3_1_r2forward_out, priority_encoder_1_out, r1_forward, r2_forward;
  wire [3:0] id_ex3_1_aluop_out, \单周期硬布线控制器_1_alu_op ;
  wire [4:0] EX_W, funct, MEM_W, mem_wb2_1_w_out, R1_num, R2_num;
  wire [9:0] ex_mem2_1_ma_out;
  wire [11:0] multiplexer_4_out;
  wire [12:0] CNT_num;
  wire [15:0] \LoadUse次数 , \总周期数 , \插入气泡数 , \无条件分支数 , \条件分支成功数 ;
  wire [31:0] adder_1_out, adder_2_out, adder_3_out, alu_1_result, alu_1_result_2, aluresult, and_4_out,
       bit_extender_1_out, bit_extender_2_out, bit_extender_3_out, bit_extender_4_out, bit_extender_5_out,
       btb_1_jumpaddr, EX_BRANCHADDR, EX_IR, ex_mem2_1_aluresult_out, ex_mem2_1_imm_out, id_ex3_1_b_out,
       id_ex3_1_imm_out, id_ex3_1_j_out, id_ex3_1_r1_out, id_ex3_1_r2_out, ID_IR, IF_IR, MEM_IR,
       mem_wb2_1_aluresult_out, mem_wb2_1_dout_out, mem_wb2_1_imm_out, multiplexer_1_out, multiplexer_2_out,
       multiplexer_7_out, multiplexer_8_out, multiplexer_9_out, multiplexer_10_out, multiplexer_11_out,
       multiplexer_12_out, multiplexer_16_out, multiplexer_17_out, multiplexer_18_out, new_1, PC_4,
       ram_1_data, regifile_1_r1, regifile_1_r2, shifter_1_out, shifter_2_out, TRUE_PC, WB_IR;

  Button \u_总复位  (.out(RST));
  Button _1 (.out(IR1));
  Button _2 (.out(IR2));
  Button _3 (.out(IR3));
  // Probe on \总周期数 
  // Probe on \总周期数 
  Button \u_继续运行  (.out(Go));
  LED #(.active("true")) led_1 (.in(W1));
  LED #(.active("true")) led_2 (.in(W2));
  LED #(.active("true")) led_3 (.in(W3));
  Counter #(.width(16), .max('hffff), .ongoal("wrap"), .trigger("rising"), .behavior("new")) counter_1 (
    .count(tunnel1), .Q(\条件分支成功数 ), .clk(CLK), .clr(RST));  // open: load, D, carry, preset, down
  Multiplexer #(.select(1), .width(32), .disabled("Z"), .enable("false")) multiplexer_1 (
    .in0(adder_1_out), .in1(btb_1_jumpaddr), .out(multiplexer_1_out), .sel(PREDICTJUMP));
  Hex_Digit_Display hex_digit_display_1 (.value(LedData[31:28]));  // open: dp
  // Probe on IF_PC[19:0]
  // RiscV_Probe riscv_probe_1: pin names not known; wires that end beside it: IF_IR
  BTB btb_1 (
    .EX_PC(EX_PC), .EX_BRANCH(EX_BRANCH), .CLK(CLK), .PC(IF_PC), .EX_BRANCHADDR(EX_BRANCHADDR), .RST(RST),
    .EX_BRANCHTAKEN(branch), .predictjump(PREDICTJUMP), .jumpaddr(btb_1_jumpaddr));
  Hex_Digit_Display hex_digit_display_2 (.value(LedData[27:24]));  // open: dp
  Hex_Digit_Display hex_digit_display_3 (.value(LedData[23:20]));  // open: dp
  // Probe on ID_PC[19:0]
  // RiscV_Probe riscv_probe_2: pin names not known; wires that end beside it: {ID_IR[31], funct[4], ID_IR[29:26], funct[3], ID_IR[24:15], funct[2:0], ID_IR[11:0]}
  Counter #(.width(16), .max('hffff), .ongoal("wrap"), .trigger("rising"), .behavior("new")) counter_2 (
    .Q(\插入气泡数 ), .clk(clash), .clr(RST));  // open: load, D, count, carry, preset, down
  Counter #(.width(16), .max('hffff), .ongoal("wrap"), .trigger("rising"), .behavior("new")) counter_3 (
    .Q(\LoadUse次数 ), .clk(clash), .clr(RST));  // open: load, D, count, carry, preset, down
  Multiplexer #(.select(1), .width(32), .disabled("Z"), .enable("false")) multiplexer_2 (
    .in0(multiplexer_1_out), .in1(TRUE_PC), .out(multiplexer_2_out), .sel(CORRECT));
  Hex_Digit_Display hex_digit_display_4 (.value(LedData[19:16]));  // open: dp
  Hex_Digit_Display hex_digit_display_5 (.value(LedData[15:12]));  // open: dp
  and and_1 (and_1_out, or_1_out, not_1_out);
  or or_1 (or_1_out, not_2_out, Go);
  not not_1 (not_1_out, clash);
  not not_2 (not_2_out, halt);
  or or_2 (EX_BRANCH, JALR, JAL, BEQ, BGEU, BNE);
  Hex_Digit_Display hex_digit_display_6 (.value(LedData[7:4]));  // open: dp
  Hex_Digit_Display hex_digit_display_7 (.value(LedData[11:8]));  // open: dp
  // Probe on EX_PC[19:0]
  // RiscV_Probe riscv_probe_3: pin names not known; wires that end beside it: EX_IR
  Register #(.width(32), .trigger("rising"), .Select("low")) PC (
    .D(multiplexer_2_out), .en(and_1_out), .Q(IF_PC), .clk(CLK), .clr(RST));
  Hex_Digit_Display hex_digit_display_8 (.value(LedData[3:0]));  // open: dp
  Counter #(.width(16), .max('hffff), .ongoal("wrap"), .trigger("rising"), .behavior("new")) counter_4 (
    .Q(\无条件分支数 ), .clk(or_3_out), .clr(RST));  // open: load, D, count, carry, preset, down
  or or_3 (or_3_out, JAL, JALR);
  // Probe on \总周期数 
  // Probe on M_PC[19:0]
  // RiscV_Probe riscv_probe_4: pin names not known; wires that end beside it: MEM_IR
  ROM #(.addrWidth(10), .dataWidth(32), .Select("high")) rom_1 (.addr(IF_PC[11:2]), .data(IF_IR));
  Adder #(.width(32)) adder_1 (.a(IF_PC), .b(32'h4), .out(adder_1_out));  // open: cin, cout
  not not_3 (not_3_out, clash);
  or or_4 (or_4_out, not_4_out, Go);
  not not_4 (not_4_out, halt);
  // Probe on \总周期数 
  // Probe on \无条件分支数 
  // Probe on \条件分支成功数 
  // Probe on \插入气泡数 
  // Probe on \LoadUse次数 
  IF_ID2 if_id2_1 (
    .IR_IN(IF_IR), .PC_IN(IF_PC),
    .IR_OUT({ID_IR[31], funct[4], ID_IR[29:26], funct[3], ID_IR[24:15], funct[2:0], ID_IR[11:0]}),
    .PC_OUT(ID_PC), .CLR(CORRECT), .RST(RST), .en(and_2_out), .CLK(CLK), .PREDICTJUMP_IN(PREDICTJUMP),
    .PREDICTJUMP_OUT(if_id2_1_predictjump_out));
  and and_2 (and_2_out, not_3_out, or_4_out);
  // Probe on IF_PC[11:0]
  // Probe on WB_PC[19:0]
  // RiscV_Probe riscv_probe_5: pin names not known; wires that end beside it: WB_IR
  not not_5 (not_5_out, halt);
  or or_5 (or_5_out, not_5_out, Go);
  Counter #(.width(16), .max('hffff), .ongoal("wrap"), .trigger("rising"), .behavior("new")) counter_5 (
    .count(or_5_out), .Q(\总周期数 ), .clk(CLK), .clr(RST));  // open: load, D, carry, preset, down
  // Probe on ID_PC[11:0]
  // Probe on EX_PC[11:0]
  // RiscV_Probe riscv_probe_6: pin names not known; wires that end beside it: {ID_IR[31], funct[4], ID_IR[29:26], funct[3], ID_IR[24:15], funct[2:0], ID_IR[11:0]}, riscv_probe_6_p2
  // Probe on M_PC[11:0]
  D_Flip_Flop #(.trigger("high"), .Pre_Clr_Positions("LEGACY"), .NegatePresetClear("false"), .enable("true"), .NewFFLayout("false")) d_ff_1 (.Q(d_ff_1_q));  // open: clk, D, Qn, preset, en, reset
  // Probe on 13'hc
  // Probe on WB_PC[11:0]
  Comparator #(.width(13), .mode("twosComplement")) comparator_1 (
    .a(CNT_num), .b(13'hc), .eq(comparator_1_eq), .lt(comparator_1_lt));  // open: gt
  Clock #(.highDuration(1), .lowDuration(1)) clock_1 (.out(clock_1_out));
  \单周期硬布线控制器  \u_单周期硬布线控制器_1  (
    .Funct(funct), .OP(ID_IR[6:2]), .ALU_OP(\单周期硬布线控制器_1_alu_op ), .MemToReg(\单周期硬布线控制器_1_memtoreg ),
    .MemWrite(\单周期硬布线控制器_1_memwrite ), .ALU_SRC(\单周期硬布线控制器_1_alu_src ), .RegWrite(\单周期硬布线控制器_1_regwrite ),
    .ecall(ecall), .S_type(S_type), .Jalr(\单周期硬布线控制器_1_jalr ), .Beq(\单周期硬布线控制器_1_beq ),
    .JAL(\单周期硬布线控制器_1_jal ), .Bne(\单周期硬布线控制器_1_bne ), .in_3(ID_IR[21]), .uret(riscv_probe_6_p2),
    .BGEU(\单周期硬布线控制器_1_bgeu ));
  Multiplexer #(.select(1), .width(5), .disabled("Z"), .enable("false")) multiplexer_3 (
    .in0(ID_IR[24:20]), .in1(5'b01010), .out(R2_num), .sel(ecall));
  Multiplexer #(.select(1), .width(12), .disabled("Z"), .enable("false")) multiplexer_4 (
    .in0({ID_IR[31], funct[4], ID_IR[29:26], funct[3], ID_IR[24:20]}),
    .in1({ID_IR[31], funct[4], ID_IR[29:26], funct[3], ID_IR[11:7]}), .out(multiplexer_4_out), .sel(S_type));
  nand nand_1 (nand_1_out, d_ff_1_q, comparator_1_eq);
  Counter #(.width(13), .max('h1fff), .ongoal("stay"), .trigger("rising"), .behavior("old")) counter_6 (
    .count(comparator_1_lt), .Q(CNT_num), .clk(clock_1_out));  // open: load, D, carry, clr, preset
  Multiplexer #(.select(1), .width(5), .disabled("Z"), .enable("false")) multiplexer_5 (
    .in0(ID_IR[19:15]), .in1(5'b10001), .out(R1_num), .sel(ecall));
  assign bit_extender_1_out = {{20{ID_IR[31]}}, {ID_IR[31], ID_IR[7], funct[4], ID_IR[29:26], funct[3], ID_IR[11:8]}};  // Bit_Extender bit_extender_1
  Shifter #(.width(32), .shift("ll")) shifter_1 (.in(bit_extender_1_out), .\dist (5'b00001), .out(shifter_1_out));
  assign bit_extender_2_out = {{12{ID_IR[31]}}, {ID_IR[31], ID_IR[19:15], funct[2:0], ID_IR[20], funct[4], ID_IR[29:26], funct[3], ID_IR[24:21]}};  // Bit_Extender bit_extender_2
  assign CLK = nand_1_out ? clock_1_out : 1'bz;  // Controlled_Buffer controlled_buffer_1
  Regifile regifile_1 (
    .Din(RDin), .Clk(CLK), .R1(regifile_1_r1), .R2(regifile_1_r2), .WE(RegWrite), .W_num(mem_wb2_1_w_out),
    .R1_num(R1_num), .R2_num(R2_num));
  assign bit_extender_3_out = {{20{multiplexer_4_out[11]}}, multiplexer_4_out};  // Bit_Extender bit_extender_3
  Shifter #(.width(32), .shift("ll")) shifter_2 (.in(bit_extender_2_out), .\dist (5'b00001), .out(shifter_2_out));
  REDIRECT redirect_1 (
    .R1_num(R1_num), .EX_W_num(EX_W), .EX_RegWrite(EX_rw), .R2_num(R2_num), .EX_MEMTOREG(ex_memtoreg),
    .OP(ID_IR[6:2]), .MEM_W_num(MEM_W), .MEM_RegWrite(MEM_rw), .R1_FORWARD(r1_forward), .clash(clash),
    .R2_FORWARD(r2_forward), .funct3(funct[2:0]));
  Pull_Resistor #(.pull(1)) pull_resistor_1 (.node(CLK));
  or or_6 (or_6_out, CORRECT, clash);
  ID_EX3 id_ex3_1 (
    .JAL(\单周期硬布线控制器_1_jal ), .JALR(\单周期硬布线控制器_1_jalr ), .BEQ(\单周期硬布线控制器_1_beq ), .BNE(\单周期硬布线控制器_1_bne ),
    .MEMTOREG(\单周期硬布线控制器_1_memtoreg ), .MEMWRITE(\单周期硬布线控制器_1_memwrite ), .ALUOP(\单周期硬布线控制器_1_alu_op ),
    .ALUSRC(\单周期硬布线控制器_1_alu_src ), .REGWRITE(\单周期硬布线控制器_1_regwrite ), .ECALL(ecall), .R1(regifile_1_r1),
    .R1FORWARD(r1_forward), .R2(regifile_1_r2), .R2FORWARD(r2_forward), .W_num(ID_IR[11:7]),
    .IMM(bit_extender_3_out), .B(shifter_1_out),
    .IR({ID_IR[31], funct[4], ID_IR[29:26], funct[3], ID_IR[24:15], funct[2:0], ID_IR[11:0]}),
    .J(shifter_2_out), .PC(ID_PC), .JAL_OUT(JAL), .JALR_OUT(JALR), .BEQ_OUT(BEQ), .BNE_OUT(BNE),
    .MEMTOREG_OUT(ex_memtoreg), .MEMWRITE_OUT(id_ex3_1_memwrite_out), .ALUOP_OUT(id_ex3_1_aluop_out),
    .ALUSRC_OUT(AluSrcB), .REGWRITE_OUT(EX_rw), .ECALL_OUT(id_ex3_1_ecall_out), .R1_OUT(id_ex3_1_r1_out),
    .R1FORWARD_OUT(id_ex3_1_r1forward_out), .R2_OUT(id_ex3_1_r2_out), .R2FORWARD_OUT(id_ex3_1_r2forward_out),
    .W__OUT(EX_W), .IMM_OUT(id_ex3_1_imm_out), .B_OUT(id_ex3_1_b_out), .IR_OUT(EX_IR),
    .J_OUT(id_ex3_1_j_out), .PC_OUT(EX_PC), .CLK(CLK), .RST(RST), .CLR(or_6_out), .EN(or_11_out),
    .BGEU_IN(\单周期硬布线控制器_1_bgeu ), .BGEU_OUT(BGEU), .PREDICTJUMP_IN(if_id2_1_predictjump_out),
    .PREDICTJUMP_OUT(PREDICT_JUMP));  // open: URET_IN, URET_OUT
  and and_3 (and_3_out, equal, BEQ);
  not not_6 (not_6_out, equal);
  assign and_4_out = aluresult & 32'hfffffffe;  // AND_Gate and_4, 32 bits wide
  Multiplexer #(.select(2), .width(32), .disabled("Z"), .enable("false")) multiplexer_6 (
    .in0({32{1'b0}}), .in1(adder_3_out), .in2(adder_2_out), .in3(and_4_out), .out(EX_BRANCHADDR),
    .sel(priority_encoder_1_out));
  Multiplexer #(.select(1), .width(32), .disabled("Z"), .enable("false")) multiplexer_7 (
    .in0({32{1'b0}}), .in1(multiplexer_9_out), .out(multiplexer_7_out), .sel(and_5_out));
  and and_5 (and_5_out, id_ex3_1_ecall_out, flag);
  and and_6 (and_6_out, not_6_out, BNE);
  Multiplexer #(.select(2), .width(32), .disabled("Z"), .enable("false")) multiplexer_8 (
    .in0(id_ex3_1_r1_out), .in1(new_1), .in2(RDin), .in3(RDin), .out(multiplexer_8_out),
    .sel(id_ex3_1_r1forward_out));
  Multiplexer #(.select(2), .width(32), .disabled("Z"), .enable("false")) multiplexer_9 (
    .in0(id_ex3_1_r2_out), .in1(new_1), .in2(RDin), .in3(RDin), .out(multiplexer_9_out),
    .sel(id_ex3_1_r2forward_out));
  Adder #(.width(32)) adder_2 (.a(id_ex3_1_b_out), .b(EX_PC), .out(adder_2_out));  // open: cin, cout
  Adder #(.width(32)) adder_3 (.a(id_ex3_1_j_out), .b(EX_PC), .out(adder_3_out));  // open: cin, cout
  Multiplexer #(.select(1), .width(32), .disabled("Z"), .enable("false")) multiplexer_10 (
    .in0(PC_4), .in1(and_4_out), .out(multiplexer_10_out), .sel(JALR));
  or or_7 (branch, JALR, JAL, tunnel1);
  not not_7 (not_7_out, flag);
  or or_8 (tunnel1, and_3_out, and_6_out, and_7_out);
  and and_7 (and_7_out, BGEU, GE);
  Comparator #(.width(32), .mode("twosComplement")) comparator_2 (
    .a(32'h22), .b(multiplexer_8_out), .eq(flag));  // open: gt, lt
  Multiplexer #(.select(1), .width(32), .disabled("Z"), .enable("false")) multiplexer_11 (
    .in0(multiplexer_9_out), .in1(id_ex3_1_imm_out), .out(multiplexer_11_out), .sel(AluSrcB));
  Priority_Encoder #(.select(2), .disabled("Z")) priority_encoder_1 (
    .in0(1'b1), .in1(JAL), .in2(or_9_out), .in3(JALR), .out(priority_encoder_1_out));  // open: gs, en_out, en_in
  xor xor_1 (CORRECT, branch, PREDICT_JUMP);
  Register #(.width(32), .trigger("rising"), .Select("low")) register_1 (
    .D(multiplexer_7_out), .en(and_5_out), .Q(LedData), .clk(CLK), .clr(RST));
  and and_8 (and_8_out, id_ex3_1_ecall_out, not_7_out);
  ALU alu_1 (
    .X(multiplexer_8_out), .Y(multiplexer_11_out), .AluOP(id_ex3_1_aluop_out), .Equal(equal),
    .Result(alu_1_result), .Result_2(alu_1_result_2), .out_4(GE));  // open: out_6
  Multiplexer #(.select(1), .width(32), .disabled("Z"), .enable("false")) multiplexer_12 (
    .in0(multiplexer_10_out), .in1(adder_3_out), .out(multiplexer_12_out), .sel(JAL));
  or or_9 (or_9_out, BEQ, BGEU, BNE);
  Comparator #(.width(4), .mode("twosComplement")) comparator_3 (
    .a(id_ex3_1_aluop_out), .b(4'b0100), .eq(comparator_3_eq));  // open: gt, lt
  Adder #(.width(32)) adder_4 (.a(EX_PC), .b(32'h4), .out(PC_4));  // open: cin, cout
  Multiplexer #(.select(1), .width(32), .disabled("Z"), .enable("false")) multiplexer_13 (
    .in0(multiplexer_12_out), .in1(adder_2_out), .out(TRUE_PC), .sel(tunnel1));
  Comparator #(.width(20), .mode("twosComplement")) comparator_4 (.a(IF_PC[19:0]), .b(20'h2f0));  // open: gt, eq, lt
  or or_10 (or_10_out, 1'b0, and_8_out);
  Multiplexer #(.select(1), .width(32), .disabled("Z"), .enable("false")) multiplexer_14 (
    .in0(alu_1_result), .in1(alu_1_result_2), .out(aluresult), .sel(comparator_3_eq));
  EX_MEM2 ex_mem2_1 (
    .JAL_IN(JAL), .JALR_IN(JALR), .halt_IN(or_10_out), .MemToReg_IN(ex_memtoreg),
    .MemWrite_IN(id_ex3_1_memwrite_out), .RegWrite_IN(EX_rw), .aluresult_IN(aluresult),
    .MA_IN(aluresult[11:2]), .MDin_IN(multiplexer_9_out), .W_IN(EX_W), .PC_IN(EX_PC), .IR_IN(EX_IR),
    .IMM_IN(PC_4), .JAL_OUT(ex_mem2_1_jal_out), .JALR_OUT(ex_mem2_1_jalr_out), .halt_OUT(ex_mem2_1_halt_out),
    .MemToReg_OUT(mem_memtoreg), .MemWrite_OUT(MemWrite), .RegWrite_OUT(MEM_rw),
    .aluresult_OUT(ex_mem2_1_aluresult_out), .MA_OUT(ex_mem2_1_ma_out), .MDin_OUT(MDin), .W_OUT(MEM_W),
    .PC_OUT(M_PC), .IR_OUT(MEM_IR), .IMM_OUT(ex_mem2_1_imm_out), .CLR(1'b0), .RST(RST), .en(or_11_out),
    .CLK(CLK), .HIGH_IN(aluresult[1]), .HIGH_OUT(ex_mem2_1_high_out));
  or or_11 (or_11_out, not_8_out, Go);
  not not_8 (not_8_out, halt);
  or or_12 (or_12_out, ex_mem2_1_jal_out, ex_mem2_1_jalr_out);
  Multiplexer #(.select(1), .width(32), .disabled("Z"), .enable("false")) multiplexer_15 (
    .in0(ex_mem2_1_aluresult_out), .in1(ex_mem2_1_imm_out), .out(new_1), .sel(or_12_out));
  RAM #(.addrWidth(10), .dataWidth(32), .bus("separate"), .Select("high")) ram_1 (
    .addr(ex_mem2_1_ma_out), .din(MDin), .data(ram_1_data), .str(MemWrite), .clk(CLK), .ld(not_9_out));  // open: sel, clr
  not not_9 (not_9_out, MemWrite);
  assign bit_extender_4_out = {{16{1'b0}}, ram_1_data[15:0]};  // Bit_Extender bit_extender_4
  Multiplexer #(.select(1), .width(32), .disabled("Z"), .enable("false")) multiplexer_16 (
    .in0(bit_extender_4_out), .in1(bit_extender_5_out), .out(multiplexer_16_out), .sel(ex_mem2_1_high_out));
  assign bit_extender_5_out = {{16{1'b0}}, ram_1_data[31:16]};  // Bit_Extender bit_extender_5
  Comparator #(.width(3), .mode("twosComplement")) comparator_5 (
    .a(MEM_IR[14:12]), .b(3'b101), .eq(comparator_5_eq));  // open: gt, lt
  not not_10 (not_10_out, comparator_5_eq);
  Multiplexer #(.select(1), .width(32), .disabled("Z"), .enable("false")) multiplexer_17 (
    .in0(multiplexer_16_out), .in1(ram_1_data), .out(multiplexer_17_out), .sel(not_10_out));
  MEM_WB2 mem_wb2_1 (
    .JAL_IN(ex_mem2_1_jal_out), .JALR_IN(ex_mem2_1_jalr_out), .halt_IN(ex_mem2_1_halt_out),
    .MemToReg_IN(mem_memtoreg), .RegWrite_IN(MEM_rw), .aluresult_IN(ex_mem2_1_aluresult_out),
    .Dout_IN(multiplexer_17_out), .W_IN(MEM_W), .IR_IN(MEM_IR), .PC_IN(M_PC), .IMM_IN(ex_mem2_1_imm_out),
    .JAL_OUT(mem_wb2_1_jal_out), .JALR_OUT(mem_wb2_1_jalr_out), .halt_OUT(halt), .MemToReg_OUT(MemToReg),
    .RegWrite_OUT(RegWrite), .aluresult_OUT(mem_wb2_1_aluresult_out), .Dout_OUT(mem_wb2_1_dout_out),
    .W_OUT(mem_wb2_1_w_out), .IR_OUT(WB_IR), .PC_OUT(WB_PC), .IMM_OUT(mem_wb2_1_imm_out), .CLR(1'b0),
    .RST(RST), .en(or_11_out), .CLK(CLK));
  or or_13 (or_13_out, mem_wb2_1_jalr_out, mem_wb2_1_jal_out);
  Multiplexer #(.select(1), .width(32), .disabled("Z"), .enable("false")) multiplexer_18 (
    .in0(mem_wb2_1_aluresult_out), .in1(mem_wb2_1_dout_out), .out(multiplexer_18_out), .sel(MemToReg));
  Multiplexer #(.select(1), .width(32), .disabled("Z"), .enable("false")) multiplexer_19 (
    .in0(multiplexer_18_out), .in1(mem_wb2_1_imm_out), .out(RDin), .sel(or_13_out));

  // Other names for the same wires on the sheet: ID_IR (some bits) = funct; op[4:0] = ID_IR[6:2]; MEM_PC[31:0] = M_PC

  // Notes on the sheet:
  //   中断源
  //   时空图监测，可删除
  //   中断等待指示
  //   数码管输出
  //   分支预测缓冲器
  //   判断是否是分支信号
  //   指令存储器
  //   contents of rom_1 (hex, n*v repeats v):
  //   100493 100006f 100493 200913 300993 100006f 100493 200913 300993 100006f 100493 200913 300993
  //   100006f 100493 200913 300993 3bc000ef 100413 100493 1f49493 900533 2200893 73 24d493 48463 fedff06f
  //   900533 2200893 73 100493 249493 900533 2200893 73 48463 fedff06f 100493 1f49493 900533 2200893 73
  //   4034d493 900533 2200893 73 4044d493 900533 2200893 73 4044d493 900533 2200893 73 4044d493 900533
  //   2200893 73 4044d493 900533 2200893 73 4044d493 900533 2200893 73 4044d493 900533 2200893 73 4044d493
  //   900533 2200893 73 100413 1f41993 41f9d993 433 c00913 300b13 140413 f47413 800293 100313 499993
  //   89e9b3 1300533 2200893 73 406282b3 fe0294e3 140413 f00f93 1f47433 1c41413 800293 100313 49d993
  //   89e9b3 1300533 2200893 73 406282b3 fe0294e3 1c45413 406b0b33 b0463 f95ff06f 2b3 fff2c293 829293
  //   ff2e293 500533 2200893 73 fff00413 493 84a023 140413 448493 84a023 140413 448493 84a023 140413
  //   448493 84a023 140413 448493 84a023 140413 448493 84a023 140413 448493 84a023 140413 448493 84a023
  //   140413 448493 84a023 140413 448493 84a023 140413 448493 84a023 140413 448493 84a023 140413 448493
  //   84a023 140413 448493 84a023 140413 448493 84a023 140413 448493 84a023 140413 448493 140413 433
  //   3c00493 42983 4aa03 149a2b3 28663 134a023 1442023 ffc48493 fe9412e3 800533 2200893 73 440413 3c00493
  //   fc9416e3 a00893 73 200293 1100493 849493 1148493 900533 2200893 73 2000e13 25484b3 900533 2200893 73
  //   fffe0e13 fe0e16e3 a00893 73 8800493 849493 4848493 8700913 891913 5490913 2997933 1091913 11096913
  //   1200533 2200893 73 a00893 73 313 1000e13 8400493 849493 8348493 400913 891913 490913 849493 8248493
  //   849493 8148493 891913 490913 891913 490913 932023 12484b3 430313 fffe0e13 fe0e18e3 2000e13 313 35483
  //   900533 2200893 73 230313 fffe0e13 fe0e14e3 a00893 73 f00493 100913 409909b3 900533 2200893 73
  //   fff48493 ff29f6e3 a00893 73 413 140413 800533 2200893 73 240413 800533 2200893 73 340413 800533
  //   2200893 73 440413 800533 2200893 73 540413 800533 2200893 73 640413 800533 2200893 73 740413 800533
  //   2200893 73 840413 800533 2200893 2200893 73 8067
  //   控制位
  //   指令探针
  //   指令字
  //   流水调试日志用
  //   暂停节拍，不能为0
  //   JAL
  //   JALR
  //   URET
  //   戳工具置1进入计数暂停模式，ctrl+k时钟自动运行到对应节拍暂停
  //   ctrl+k关闭时钟连续运行，将控制位置零，进入单步调试模式调试
  //   Beq
  //   Bne
  //   MemToReg
  //   MemWrite
  //   AluOP
  //   AluSrcB
  //   RegWrite
  //   重定向检测和进行
  //   可计数暂停的时钟源
  //   为方便自动评测，需要输出流水线各段保存的PC值，注意是PC不是PC+4，另外ID段寄存器写入信息，Mem段内存写入信息也要输出
  //   生成预测是否成功的信号
  //   数据存储器
endmodule

module BTB (
  input  [31:0] EX_PC,
  input  EX_BRANCH,
  input  CLK,
  input  [31:0] PC,
  input  [31:0] EX_BRANCHADDR,
  input  RST,
  input  EX_BRANCHTAKEN,
  output predictjump,
  output [31:0] jumpaddr
);

  wire and_1_out, and_2_out, and_3_out, and_4_out, and_5_out, and_6_out, and_7_out, and_8_out, and_9_out,
       and_10_out, and_11_out, and_12_out, and_13_out, and_14_out, and_15_out, and_16_out, and_18_out,
       and_19_out, and_20_out, and_21_out, and_22_out, and_23_out, and_24_out, and_25_out, and_26_out,
       and_27_out, and_28_out, and_29_out, and_30_out, and_31_out, and_32_out, and_33_out, and_34_out,
       compara1, compara2, compara3, compara4, compara5, compara6, compara7, comparator_1_eq,
       comparator_2_eq, comparator_3_eq, comparator_4_eq, comparator_5_eq, comparator_6_eq, comparator_7_eq,
       comparator_8_eq, comparator_9_eq, comparator_10_eq, comparator_11_eq, comparator_12_eq,
       comparator_13_eq, comparator_14_eq, comparator_15_eq, comparator_16_eq, comparator_24_eq,
       comparator_25_eq, comparator_26_eq, comparator_27_eq, comparator_28_eq, comparator_29_eq,
       decoder_1_out0, decoder_1_out1, decoder_1_out2, decoder_1_out3, decoder_1_out4, decoder_1_out5,
       decoder_1_out6, decoder_1_out7, nohit, not_1_out, not_2_out, not_3_out, not_4_out, not_5_out,
       not_6_out, not_7_out, not_8_out, not_9_out, not_10_out, not_11_out, not_12_out, not_13_out,
       not_14_out, not_15_out, not_16_out, not_17_out, not_18_out, not_19_out, not_20_out, not_21_out,
       not_22_out, not_23_out, not_24_out, not_25_out, not_26_out, not_27_out, not_28_out, not_29_out,
       not_30_out, not_31_out, not_32_out, not_33_out, not_34_out, or_1_out, or_2_out, or_3_out, or_4_out,
       or_5_out, or_6_out, or_7_out, or_8_out, or_9_out, or_10_out, or_11_out, or_12_out, or_13_out,
       or_14_out, or_15_out, or_16_out, or_17_out, or_18_out, or_19_out, or_20_out, or_21_out, or_22_out,
       or_23_out, or_24_out, or_25_out, pre_nohit, priority_encoder_3_gs, undriven, undriven_2, undriven_3,
       undriven_4, va1, va2, va3, va4, va5, va6, va7, va8, w1, w2, w3, w4, w5, w6, w7, w8, w_1, w_2, w_3,
       w_4, w_5, w_6, w_7, w_8;
  wire [1:0] multiplexer_10_out, multiplexer_11_out, multiplexer_12_out, multiplexer_13_out,
       multiplexer_14_out, multiplexer_15_out, multiplexer_16_out, pre, pre1, pre2, pre3, pre4, pre5, pre6,
       pre7, pre8, predict, priority_encoder_4_out;
  wire [2:0] hit, pre_hit, priority_encoder_3_out;
  wire [31:0] add1, add2, add3, add4, add5, add6, add7, add8, count1, count2, count3, count4, count5, count6,
       count7, count8, des1, des2, des3, des4, des5, des6, des7, des8, multiplexer_1_out, multiplexer_2_out,
       multiplexer_3_out, multiplexer_4_out, multiplexer_5_out, multiplexer_6_out, multiplexer_7_out;

  Register #(.width(1), .trigger("rising"), .Select("low")) register_1 (
    .D(1'b1), .en(w1), .Q(va1), .clk(CLK), .clr(RST));
  Register #(.width(1), .trigger("rising"), .Select("low")) register_2 (
    .D(1'b1), .en(w2), .Q(va2), .clk(CLK), .clr(RST));
  Register #(.width(1), .trigger("rising"), .Select("low")) register_3 (
    .D(1'b1), .en(w3), .Q(va3), .clk(CLK), .clr(RST));
  Register #(.width(1), .trigger("rising"), .Select("low")) register_4 (
    .D(1'b1), .en(w4), .Q(va4), .clk(CLK), .clr(RST));
  Register #(.width(1), .trigger("rising"), .Select("low")) register_5 (
    .D(1'b1), .en(w5), .Q(va5), .clk(CLK), .clr(RST));
  Register #(.width(1), .trigger("rising"), .Select("low")) register_6 (
    .D(1'b1), .en(w6), .Q(va6), .clk(CLK), .clr(RST));
  Register #(.width(1), .trigger("rising"), .Select("low")) register_7 (
    .D(1'b1), .en(w7), .Q(va7), .clk(CLK), .clr(RST));
  Register #(.width(1), .trigger("rising"), .Select("low")) register_8 (
    .D(1'b1), .en(w8), .Q(va8), .clk(CLK), .clr(RST), .preset(undriven));  // open: cs
  Register #(.width(32), .trigger("rising"), .Select("low")) register_9 (
    .D(EX_PC), .en(w1), .Q(add1), .clk(CLK), .clr(RST));
  Register #(.width(32), .trigger("rising"), .Select("low")) register_10 (
    .D(EX_PC), .en(w2), .Q(add2), .clk(CLK), .clr(RST));
  Register #(.width(32), .trigger("rising"), .Select("low")) register_11 (
    .D(EX_PC), .en(w3), .Q(add3), .clk(CLK), .clr(RST));
  Register #(.width(32), .trigger("rising"), .Select("low")) register_12 (
    .D(EX_PC), .en(w4), .Q(add4), .clk(CLK), .clr(RST));
  Register #(.width(32), .trigger("rising"), .Select("low")) register_13 (
    .D(EX_PC), .en(w5), .Q(add5), .clk(CLK), .clr(RST));
  Register #(.width(32), .trigger("rising"), .Select("low")) register_14 (
    .D(EX_PC), .en(w6), .Q(add6), .clk(CLK), .clr(RST));
  Register #(.width(32), .trigger("rising"), .Select("low")) register_15 (
    .D(EX_PC), .en(w7), .Q(add7), .clk(CLK), .clr(RST));
  Register #(.width(32), .trigger("rising"), .Select("low")) register_16 (
    .D(EX_PC), .en(w8), .Q(add8), .clk(CLK), .clr(RST), .preset(undriven_2));  // open: cs
  Register #(.width(32), .trigger("rising"), .Select("low")) register_17 (
    .D(EX_BRANCHADDR), .en(w1), .Q(des1), .clk(CLK), .clr(RST));
  Register #(.width(32), .trigger("rising"), .Select("low")) register_18 (
    .D(EX_BRANCHADDR), .en(w2), .Q(des2), .clk(CLK), .clr(RST));
  Register #(.width(32), .trigger("rising"), .Select("low")) register_19 (
    .D(EX_BRANCHADDR), .en(w3), .Q(des3), .clk(CLK), .clr(RST));
  Register #(.width(32), .trigger("rising"), .Select("low")) register_20 (
    .D(EX_BRANCHADDR), .en(w4), .Q(des4), .clk(CLK), .clr(RST));
  Register #(.width(32), .trigger("rising"), .Select("low")) register_21 (
    .D(EX_BRANCHADDR), .en(w5), .Q(des5), .clk(CLK), .clr(RST));
  Register #(.width(32), .trigger("rising"), .Select("low")) register_22 (
    .D(EX_BRANCHADDR), .en(w6), .Q(des6), .clk(CLK), .clr(RST));
  Register #(.width(32), .trigger("rising"), .Select("low")) register_23 (
    .D(EX_BRANCHADDR), .en(w7), .Q(des7), .clk(CLK), .clr(RST));
  Register #(.width(32), .trigger("rising"), .Select("low")) register_24 (
    .D(EX_BRANCHADDR), .en(w8), .Q(des8), .clk(CLK), .clr(RST), .preset(undriven_3));  // open: cs
  not not_1 (not_1_out, nohit);
  Decoder #(.select(3), .tristate("false"), .disabled(0), .enable("true")) decoder_1 (
    .out0(decoder_1_out0), .out1(decoder_1_out1), .out2(decoder_1_out2), .out3(decoder_1_out3),
    .out4(decoder_1_out4), .out5(decoder_1_out5), .out6(decoder_1_out6), .out7(decoder_1_out7), .sel(hit),
    .en(not_1_out));
  or or_1 (or_1_out, decoder_1_out0, w1);
  or or_2 (or_2_out, decoder_1_out1, w2);
  or or_3 (or_3_out, decoder_1_out2, w3);
  or or_4 (or_4_out, decoder_1_out3, w4);
  or or_5 (or_5_out, decoder_1_out4, w5);
  or or_6 (or_6_out, decoder_1_out5, w6);
  or or_7 (or_7_out, decoder_1_out6, w7);
  or or_8 (or_8_out, decoder_1_out7, w8);
  Register #(.width(2), .trigger("rising"), .Select("low")) register_25 (
    .D(predict), .en(or_1_out), .Q(pre1), .clk(CLK), .clr(RST));
  Register #(.width(2), .trigger("rising"), .Select("low")) register_26 (
    .D(predict), .en(or_2_out), .Q(pre2), .clk(CLK), .clr(RST));
  Register #(.width(2), .trigger("rising"), .Select("low")) register_27 (
    .D(predict), .en(or_3_out), .Q(pre3), .clk(CLK), .clr(RST));
  Register #(.width(2), .trigger("rising"), .Select("low")) register_28 (
    .D(predict), .en(or_4_out), .Q(pre4), .clk(CLK), .clr(RST));
  Register #(.width(2), .trigger("rising"), .Select("low")) register_29 (
    .D(predict), .en(or_5_out), .Q(pre5), .clk(CLK), .clr(RST));
  Register #(.width(2), .trigger("rising"), .Select("low")) register_30 (
    .D(predict), .en(or_6_out), .Q(pre6), .clk(CLK), .clr(RST));
  Register #(.width(2), .trigger("rising"), .Select("low")) register_31 (
    .D(predict), .en(or_7_out), .Q(pre7), .clk(CLK), .clr(RST));
  Register #(.width(2), .trigger("rising"), .Select("low")) register_32 (
    .D(predict), .en(or_8_out), .Q(pre8), .clk(CLK), .clr(RST), .preset(undriven_4));  // open: cs
  Comparator #(.width(32), .mode("twosComplement")) comparator_1 (
    .a(EX_PC), .b(add1), .eq(comparator_1_eq));  // open: gt, lt
  Comparator #(.width(32), .mode("twosComplement")) comparator_2 (
    .a(EX_PC), .b(add2), .eq(comparator_2_eq));  // open: gt, lt
  Comparator #(.width(32), .mode("twosComplement")) comparator_3 (
    .a(EX_PC), .b(add3), .eq(comparator_3_eq));  // open: gt, lt
  Comparator #(.width(32), .mode("twosComplement")) comparator_4 (
    .a(EX_PC), .b(add4), .eq(comparator_4_eq));  // open: gt, lt
  Comparator #(.width(32), .mode("twosComplement")) comparator_5 (
    .a(EX_PC), .b(add5), .eq(comparator_5_eq));  // open: gt, lt
  Comparator #(.width(32), .mode("twosComplement")) comparator_6 (
    .a(EX_PC), .b(add6), .eq(comparator_6_eq));  // open: gt, lt
  Comparator #(.width(32), .mode("twosComplement")) comparator_7 (
    .a(EX_PC), .b(add7), .eq(comparator_7_eq));  // open: gt, lt
  Comparator #(.width(32), .mode("twosComplement")) comparator_8 (
    .a(EX_PC), .b(add8), .eq(comparator_8_eq));  // open: gt, lt
  Counter #(.width(32), .max('hffffffff), .ongoal("wrap"), .trigger("rising"), .behavior("new")) counter_1 (
    .Q(count1), .clk(CLK), .clr(or_1_out));  // open: load, D, count, carry, preset, down
  Counter #(.width(32), .max('hffffffff), .ongoal("wrap"), .trigger("rising"), .behavior("new")) counter_2 (
    .Q(count2), .clk(CLK), .clr(or_2_out));  // open: load, D, count, carry, preset, down
  Counter #(.width(32), .max('hffffffff), .ongoal("wrap"), .trigger("rising"), .behavior("new")) counter_3 (
    .Q(count3), .clk(CLK), .clr(or_3_out));  // open: load, D, count, carry, preset, down
  Counter #(.width(32), .max('hffffffff), .ongoal("continue"), .trigger("rising"), .behavior("new")) counter_4 (
    .Q(count4), .clk(CLK), .clr(or_4_out));  // open: load, D, count, carry, preset, down
  Counter #(.width(32), .max('hffffffff), .ongoal("wrap"), .trigger("rising"), .behavior("new")) counter_5 (
    .Q(count5), .clk(CLK), .clr(or_5_out));  // open: load, D, count, carry, preset, down
  Counter #(.width(32), .max('hffffffff), .ongoal("wrap"), .trigger("rising"), .behavior("new")) counter_6 (
    .Q(count6), .clk(CLK), .clr(or_6_out));  // open: load, D, count, carry, preset, down
  Counter #(.width(32), .max('hffffffff), .ongoal("wrap"), .trigger("rising"), .behavior("new")) counter_7 (
    .Q(count7), .clk(CLK), .clr(or_7_out));  // open: load, D, count, carry, preset, down
  Counter #(.width(32), .max('hffffffff), .ongoal("wrap"), .trigger("rising"), .behavior("new")) counter_8 (
    .Q(count8), .clk(CLK), .clr(or_8_out));  // open: load, D, count, carry, preset, down
  and and_1 (and_1_out, comparator_1_eq, va1);
  and and_2 (and_2_out, comparator_2_eq, va2);
  and and_3 (and_3_out, comparator_3_eq, va3);
  and and_4 (and_4_out, comparator_4_eq, va4);
  and and_5 (and_5_out, comparator_5_eq, va5);
  and and_6 (and_6_out, comparator_6_eq, va6);
  and and_7 (and_7_out, comparator_7_eq, va7);
  and and_8 (and_8_out, comparator_8_eq, va8);
  Priority_Encoder #(.select(3), .disabled("Z")) priority_encoder_1 (
    .in0(and_1_out), .in1(and_2_out), .in2(and_3_out), .in3(and_4_out), .in4(and_5_out), .in5(and_6_out),
    .in6(and_7_out), .in7(and_8_out), .out(hit), .en_out(nohit));  // open: gs, en_in
  Comparator #(.width(32), .mode("twosComplement")) comparator_9 (
    .a(PC), .b(add1), .eq(comparator_9_eq));  // open: gt, lt
  Comparator #(.width(32), .mode("twosComplement")) comparator_10 (
    .a(PC), .b(add2), .eq(comparator_10_eq));  // open: gt, lt
  Comparator #(.width(32), .mode("twosComplement")) comparator_11 (
    .a(PC), .b(add3), .eq(comparator_11_eq));  // open: gt, lt
  Comparator #(.width(32), .mode("twosComplement")) comparator_12 (
    .a(PC), .b(add4), .eq(comparator_12_eq));  // open: gt, lt
  Comparator #(.width(32), .mode("twosComplement")) comparator_13 (
    .a(PC), .b(add5), .eq(comparator_13_eq));  // open: gt, lt
  Comparator #(.width(32), .mode("twosComplement")) comparator_14 (
    .a(PC), .b(add6), .eq(comparator_14_eq));  // open: gt, lt
  Comparator #(.width(32), .mode("twosComplement")) comparator_15 (
    .a(PC), .b(add7), .eq(comparator_15_eq));  // open: gt, lt
  Comparator #(.width(32), .mode("twosComplement")) comparator_16 (
    .a(PC), .b(add8), .eq(comparator_16_eq));  // open: gt, lt
  and and_9 (and_9_out, comparator_9_eq, va1);
  and and_10 (and_10_out, comparator_10_eq, va2);
  and and_11 (and_11_out, comparator_11_eq, va3);
  and and_12 (and_12_out, comparator_12_eq, va4);
  and and_13 (and_13_out, comparator_13_eq, va5);
  and and_14 (and_14_out, comparator_14_eq, va6);
  and and_15 (and_15_out, comparator_15_eq, va7);
  and and_16 (and_16_out, comparator_16_eq, va8);
  Comparator #(.width(32), .mode("twosComplement")) comparator_17 (
    .a(count1), .b(count2), .lt(compara1));  // open: gt, eq
  Comparator #(.width(32), .mode("twosComplement")) comparator_18 (
    .a(count3), .b(count4), .lt(compara2));  // open: gt, eq
  Multiplexer #(.select(1), .width(32), .disabled("Z"), .enable("false")) multiplexer_1 (
    .in0(count5), .in1(count6), .out(multiplexer_1_out), .sel(compara3));
  Comparator #(.width(32), .mode("twosComplement")) comparator_19 (
    .a(count5), .b(count6), .lt(compara3));  // open: gt, eq
  Multiplexer #(.select(1), .width(32), .disabled("Z"), .enable("false")) multiplexer_2 (
    .in0(count7), .in1(count8), .out(multiplexer_2_out), .sel(compara4));
  Comparator #(.width(32), .mode("twosComplement")) comparator_20 (
    .a(count7), .b(count8), .lt(compara4));  // open: gt, eq
  Multiplexer #(.select(1), .width(32), .disabled("Z"), .enable("false")) multiplexer_3 (
    .in0(count1), .in1(count2), .out(multiplexer_3_out), .sel(compara1));
  Multiplexer #(.select(1), .width(32), .disabled("Z"), .enable("false")) multiplexer_4 (
    .in0(count3), .in1(count4), .out(multiplexer_4_out), .sel(compara2));
  Priority_Encoder #(.select(3), .disabled("Z")) priority_encoder_2 (
    .in0(and_9_out), .in1(and_10_out), .in2(and_11_out), .in3(and_12_out), .in4(and_13_out),
    .in5(and_14_out), .in6(and_15_out), .in7(and_16_out), .out(pre_hit), .en_out(pre_nohit));  // open: gs, en_in
  Multiplexer #(.select(1), .width(32), .disabled("Z"), .enable("false")) multiplexer_5 (
    .in0(multiplexer_3_out), .in1(multiplexer_4_out), .out(multiplexer_5_out), .sel(compara5));
  Comparator #(.width(32), .mode("twosComplement")) comparator_21 (
    .a(multiplexer_3_out), .b(multiplexer_4_out), .lt(compara5));  // open: gt, eq
  Multiplexer #(.select(1), .width(32), .disabled("Z"), .enable("false")) multiplexer_6 (
    .in0(multiplexer_1_out), .in1(multiplexer_2_out), .out(multiplexer_6_out), .sel(compara6));
  Comparator #(.width(32), .mode("twosComplement")) comparator_22 (
    .a(multiplexer_1_out), .b(multiplexer_2_out), .lt(compara6));  // open: gt, eq
  Comparator #(.width(32), .mode("twosComplement")) comparator_23 (
    .a(multiplexer_5_out), .b(multiplexer_6_out), .lt(compara7));  // open: gt, eq
  Comparator #(.width(2), .mode("unsigned")) comparator_24 (.a(pre), .b(2'b10), .eq(comparator_24_eq));  // open: gt, lt
  Comparator #(.width(2), .mode("unsigned")) comparator_25 (.a(pre), .b(2'b11), .eq(comparator_25_eq));  // open: gt, lt
  not not_2 (not_2_out, pre_nohit);
  or or_9 (or_9_out, comparator_24_eq, comparator_25_eq);
  and and_17 (predictjump, not_2_out, or_9_out);
  Multiplexer #(.select(3), .width(32), .disabled(0), .enable("true")) multiplexer_7 (
    .in0(des1), .in1(des2), .in2(des3), .in3(des4), .in4(des5), .in5(des6), .in6(des7), .in7(des8),
    .out(multiplexer_7_out), .sel(pre_hit), .en(not_3_out));
  not not_3 (not_3_out, pre_nohit);
  Multiplexer #(.select(3), .width(2), .disabled(0), .enable("true")) multiplexer_8 (
    .in0(pre1), .in1(pre2), .in2(pre3), .in3(pre4), .in4(pre5), .in5(pre6), .in6(pre7), .in7(pre8),
    .out(pre), .sel(pre_hit), .en(not_4_out));
  not not_4 (not_4_out, pre_nohit);
  not not_5 (not_5_out, va1);
  not not_6 (not_6_out, va2);
  not not_7 (not_7_out, va3);
  not not_8 (not_8_out, va4);
  not not_9 (not_9_out, va5);
  not not_10 (not_10_out, va6);
  not not_11 (not_11_out, va7);
  not not_12 (not_12_out, va8);
  Multiplexer #(.select(1), .width(32), .disabled("Z"), .enable("false")) multiplexer_9 (
    .in0(multiplexer_7_out), .in1({32{1'b0}}), .out(jumpaddr), .sel(pre_nohit));
  or or_10 (or_10_out, compara1, compara5, compara7);
  not not_13 (not_13_out, compara1);
  or or_11 (or_11_out, not_13_out, compara5, compara7);
  or or_12 (or_12_out, compara2, not_14_out, compara7);
  not not_14 (not_14_out, compara5);
  not not_15 (not_15_out, compara2);
  or or_13 (or_13_out, not_15_out, not_16_out, compara7);
  not not_16 (not_16_out, compara5);
  Priority_Encoder #(.select(3), .disabled("Z")) priority_encoder_3 (
    .in0(not_5_out), .in1(not_6_out), .in2(not_7_out), .in3(not_8_out), .in4(not_9_out), .in5(not_10_out),
    .in6(not_11_out), .in7(not_12_out), .out(priority_encoder_3_out), .gs(priority_encoder_3_gs), .en_in(1'b1));  // open: en_out
  not not_17 (not_17_out, or_10_out);
  not not_18 (not_18_out, or_11_out);
  not not_19 (not_19_out, or_12_out);
  not not_20 (not_20_out, or_13_out);
  Decoder #(.select(3), .tristate("false"), .disabled(0), .enable("true")) decoder_2 (
    .out0(w_1), .out1(w_2), .out2(w_3), .out3(w_4), .out4(w_5), .out5(w_6), .out6(w_7), .out7(w_8),
    .sel(priority_encoder_3_out), .en(priority_encoder_3_gs));
  not not_21 (not_21_out, priority_encoder_3_gs);
  and and_18 (and_18_out, nohit, EX_BRANCH);
  and and_19 (and_19_out, not_21_out, not_17_out);
  and and_20 (and_20_out, not_21_out, not_18_out);
  and and_21 (and_21_out, not_21_out, not_19_out);
  and and_22 (and_22_out, not_21_out, not_20_out);
  or or_14 (or_14_out, w_1, and_19_out);
  or or_15 (or_15_out, w_2, and_20_out);
  or or_16 (or_16_out, w_3, and_21_out);
  or or_17 (or_17_out, w_4, and_22_out);
  and and_23 (and_23_out, and_18_out, or_14_out);
  Register #(.width(1), .trigger("falling"), .Select("low")) register_33 (
    .D(and_23_out), .Q(w1), .clk(CLK));  // open: en, clr
  Register #(.width(1), .trigger("falling"), .Select("low")) register_34 (
    .D(and_24_out), .Q(w2), .clk(CLK));  // open: en, clr
  and and_24 (and_24_out, and_18_out, or_15_out);
  and and_25 (and_25_out, and_18_out, or_16_out);
  Register #(.width(1), .trigger("falling"), .Select("low")) register_35 (
    .D(and_25_out), .Q(w3), .clk(CLK));  // open: en, clr
  Register #(.width(1), .trigger("falling"), .Select("low")) register_36 (
    .D(and_26_out), .Q(w4), .clk(CLK));  // open: en, clr
  and and_26 (and_26_out, and_18_out, or_17_out);
  Multiplexer #(.select(3), .width(2), .disabled(0), .enable("true")) multiplexer_10 (
    .in0(pre1), .in1(pre2), .in2(pre3), .in3(pre4), .in4(pre5), .in5(pre6), .in6(pre7), .in7(pre8),
    .out(multiplexer_10_out), .sel(hit), .en(not_22_out));
  not not_22 (not_22_out, nohit);
  not not_23 (not_23_out, compara7);
  not not_24 (not_24_out, compara3);
  not not_25 (not_25_out, compara7);
  not not_26 (not_26_out, compara6);
  not not_27 (not_27_out, compara7);
  not not_28 (not_28_out, compara4);
  not not_29 (not_29_out, compara6);
  not not_30 (not_30_out, compara7);
  Comparator #(.width(2), .mode("unsigned")) comparator_26 (
    .a(multiplexer_10_out), .b(2'b00), .eq(comparator_26_eq));  // open: gt, lt
  Comparator #(.width(2), .mode("unsigned")) comparator_27 (
    .a(multiplexer_10_out), .b(2'b01), .eq(comparator_27_eq));  // open: gt, lt
  Comparator #(.width(2), .mode("unsigned")) comparator_28 (
    .a(multiplexer_10_out), .b(2'b10), .eq(comparator_28_eq));  // open: gt, lt
  Comparator #(.width(2), .mode("unsigned")) comparator_29 (
    .a(multiplexer_10_out), .b(2'b11), .eq(comparator_29_eq));  // open: gt, lt
  or or_18 (or_18_out, compara3, compara6, not_23_out);
  not not_31 (not_31_out, or_18_out);
  or or_19 (or_19_out, not_24_out, compara6, not_25_out);
  not not_32 (not_32_out, or_19_out);
  or or_20 (or_20_out, compara4, not_26_out, not_27_out);
  not not_33 (not_33_out, or_20_out);
  not not_34 (not_34_out, or_21_out);
  or or_21 (or_21_out, not_28_out, not_29_out, not_30_out);
  Priority_Encoder #(.select(2), .disabled("Z")) priority_encoder_4 (
    .in0(comparator_26_eq), .in1(comparator_27_eq), .in2(comparator_28_eq), .in3(comparator_29_eq),
    .out(priority_encoder_4_out));  // open: gs, en_out, en_in
  or or_22 (or_22_out, w_5, and_27_out);
  and and_27 (and_27_out, not_21_out, not_31_out);
  or or_23 (or_23_out, w_6, and_28_out);
  and and_28 (and_28_out, not_21_out, not_32_out);
  or or_24 (or_24_out, w_7, and_29_out);
  and and_29 (and_29_out, not_21_out, not_33_out);
  or or_25 (or_25_out, w_8, and_30_out);
  and and_30 (and_30_out, not_21_out, not_34_out);
  Multiplexer #(.select(1), .width(2), .disabled("Z"), .enable("false")) multiplexer_11 (
    .in0(2'b00), .in1(2'b01), .out(multiplexer_11_out), .sel(EX_BRANCHTAKEN));
  Multiplexer #(.select(1), .width(2), .disabled("Z"), .enable("false")) multiplexer_12 (
    .in0(2'b00), .in1(2'b10), .out(multiplexer_12_out), .sel(EX_BRANCHTAKEN));
  Multiplexer #(.select(1), .width(2), .disabled("Z"), .enable("false")) multiplexer_13 (
    .in0(2'b11), .in1(2'b10), .out(multiplexer_13_out), .sel(EX_BRANCHTAKEN));
  Multiplexer #(.select(1), .width(2), .disabled("Z"), .enable("false")) multiplexer_14 (
    .in0(2'b00), .in1(2'b10), .out(multiplexer_14_out), .sel(EX_BRANCHTAKEN));
  Register #(.width(1), .trigger("falling"), .Select("low")) register_37 (
    .D(and_31_out), .Q(w5), .clk(CLK));  // open: en, clr
  and and_31 (and_31_out, and_18_out, or_22_out);
  Register #(.width(1), .trigger("falling"), .Select("low")) register_38 (
    .D(and_32_out), .Q(w6), .clk(CLK));  // open: en, clr
  and and_32 (and_32_out, and_18_out, or_23_out);
  and and_33 (and_33_out, and_18_out, or_24_out);
  Register #(.width(1), .trigger("falling"), .Select("low")) register_39 (
    .D(and_33_out), .Q(w7), .clk(CLK));  // open: en, clr
  Register #(.width(1), .trigger("falling"), .Select("low")) register_40 (
    .D(and_34_out), .Q(w8), .clk(CLK));  // open: en, clr
  and and_34 (and_34_out, and_18_out, or_25_out);
  Multiplexer #(.select(2), .width(2), .disabled("Z"), .enable("false")) multiplexer_15 (
    .in0(multiplexer_11_out), .in1(multiplexer_12_out), .in2(multiplexer_13_out), .in3(multiplexer_14_out),
    .out(multiplexer_15_out), .sel(priority_encoder_4_out));
  Multiplexer #(.select(1), .width(2), .disabled("Z"), .enable("false")) multiplexer_16 (
    .in0(2'b00), .in1(2'b10), .out(multiplexer_16_out), .sel(EX_BRANCHTAKEN));
  Multiplexer #(.select(1), .width(2), .disabled("Z"), .enable("false")) multiplexer_17 (
    .in0(multiplexer_15_out), .in1(multiplexer_16_out), .out(predict), .sel(nohit));
endmodule

module \流水线单级中断  (
  input  IR1,
  input  IR2,
  input  IR3,
  output RegWrite,
  output MemWrite,
  output [31:0] PC,
  output [31:0] IR,
  output [31:0] RDin,
  output [31:0] MDin,
  output [31:0] LedData
);

  wire AluSrcB, and_1_out, and_2_out, and_3_out, and_4_out, and_5_out, and_9_out, and_10_out, and_11_out,
       and_12_out, and_13_out, and_14_out, and_15_out, and_16_out, and_17_out, and_19_out, BGEU, branch,
       clash, CLK, clock_1_out, comparator_1_gt, comparator_1_lt, comparator_2_gt, comparator_2_lt,
       comparator_3_gt, comparator_5_eq, comparator_5_lt, comparator_7_eq, comparator_9_eq, d_ff_1_q,
       d_ff_2_q, d_ff_3_q, d_ff_4_q, ecall, equal, ex_mem2_1_halt_out, ex_mem2_1_high_out, ex_mem2_1_jal_out,
       ex_mem2_1_jalr_out, ex_memtoreg, EX_rw, flag, GE, Go, halt, id_ex3_1_beq_out, id_ex3_1_bne_out,
       id_ex3_1_ecall_out, id_ex3_1_memwrite_out, IE, IR1_q, IR1_t, IR2_q, IR2_t, IR3_q, IR3_t, IRA, IRB,
       IRC, JAL, JALR, jump1, mem_memtoreg, MEM_rw, mem_wb2_1_jal_out, mem_wb2_1_jalr_out, MemToReg,
       nand_1_out, not_1_out, not_2_out, not_3_out, not_4_out, not_5_out, not_6_out, not_7_out, not_8_out,
       not_9_out, not_10_out, not_11_out, not_12_out, not_13_out, not_14_out, or_4_out, or_5_out, or_6_out,
       or_7_out, or_11_out, or_12_out, or_13_out, or_14_out, or_15_out, or_18_out, or_19_out, or_20_out,
       or_21_out, RST, S_type, tunnel1, URET, URETA, URETB, URETC, W1, W2, W3, \单周期硬布线控制器_1_alu_src ,
       \单周期硬布线控制器_1_beq , \单周期硬布线控制器_1_bgeu , \单周期硬布线控制器_1_bne , \单周期硬布线控制器_1_jal , \单周期硬布线控制器_1_jalr ,
       \单周期硬布线控制器_1_memtoreg , \单周期硬布线控制器_1_memwrite , \单周期硬布线控制器_1_regwrite , \单周期硬布线控制器_1_uret ;
  wire [1:0] id_ex3_1_r1forward_out, id_ex3_1_r2forward_out, priority_encoder_1_out, r1_forward, r2_forward;
  wire [3:0] id_ex3_1_aluop_out, \单周期硬布线控制器_1_alu_op ;
  wire [4:0] EX_W, funct, MEM_W, mem_wb2_1_w_out, R1_num, R2_num;
  wire [9:0] ex_mem2_1_ma_out;
  wire [11:0] multiplexer_5_out;
  wire [12:0] CNT_num;
  wire [15:0] \LoadUse次数 , \总周期数 , \插入气泡数 , \无条件分支数 , \条件分支成功数 ;
  wire [31:0] adder_1_out, adder_2_out, adder_3_out, adder_4_out, alu_1_result, alu_1_result_2, aluresult,
       and_18_out, bit_extender_1_out, bit_extender_2_out, bit_extender_3_out, bit_extender_4_out,
       bit_extender_5_out, EPC, EPC_IN, EX_IR, ex_mem2_1_aluresult_out, ex_mem2_1_imm_out, EX_PC,
       id_ex3_1_b_out, id_ex3_1_imm_out, id_ex3_1_j_out, id_ex3_1_r1_out, id_ex3_1_r2_out, ID_IR, ID_PC,
       IF_IR, IF_PC, MEM_IR, MEM_PC, mem_wb2_1_aluresult_out, mem_wb2_1_dout_out, mem_wb2_1_imm_out,
       multiplexer_1_out, multiplexer_2_out, multiplexer_6_out, multiplexer_7_out, multiplexer_8_out,
       multiplexer_9_out, multiplexer_10_out, multiplexer_11_out, multiplexer_15_out, multiplexer_16_out,
       multiplexer_17_out, new_1, ram_1_data, regifile_1_r1, regifile_1_r2, shifter_1_out, shifter_2_out,
       WB_IR, WB_PC;

  Button \u_继续运行  (.out(Go));
  Button _1 (.out(IRA));
  Button _2 (.out(IRB));
  Button _3 (.out(IRC));
  LED #(.active("true")) led_1 (.in(W1));
  LED #(.active("true")) led_2 (.in(W2));
  LED #(.active("true")) led_3 (.in(W3));
  Hex_Digit_Display hex_digit_display_1 (.value(LedData[31:28]));  // open: dp
  Button u_RST (.out(RST));
  not not_1 (not_1_out, IE);
  or or_1 (W1, IR1_q, d_ff_1_q);
  or or_2 (W2, IR2_q, d_ff_2_q);
  or or_3 (W3, IR3_q, d_ff_3_q);
  Hex_Digit_Display hex_digit_display_2 (.value(LedData[27:24]));  // open: dp
  Hex_Digit_Display hex_digit_display_3 (.value(LedData[23:20]));  // open: dp
  Register #(.width(32), .trigger("rising"), .Select("low")) register_1 (
    .D(EPC_IN), .en(not_1_out), .Q(EPC), .clk(CLK));  // open: clr
  D_Flip_Flop #(.trigger("rising"), .Pre_Clr_Positions("LEGACY"), .NegatePresetClear("false"), .enable("true"), .NewFFLayout("false")) d_ff_1 (
    .clk(IRA), .D(1'b1), .Q(d_ff_1_q), .reset(IR1_q));  // open: Qn, preset, en
  D_Flip_Flop #(.trigger("rising"), .Pre_Clr_Positions("LEGACY"), .NegatePresetClear("false"), .enable("true"), .NewFFLayout("false")) d_ff_2 (
    .clk(IRB), .D(1'b1), .Q(d_ff_2_q), .reset(IR2_q));  // open: Qn, preset, en
  D_Flip_Flop #(.trigger("rising"), .Pre_Clr_Positions("LEGACY"), .NegatePresetClear("false"), .enable("true"), .NewFFLayout("false")) d_ff_3 (
    .clk(IRC), .D(1'b1), .Q(d_ff_3_q), .reset(IR3_q));  // open: Qn, preset, en
  or or_4 (or_4_out, W1, W2, W3);
  Hex_Digit_Display hex_digit_display_4 (.value(LedData[15:12]));  // open: dp
  Hex_Digit_Display hex_digit_display_5 (.value(LedData[19:16]));  // open: dp
  or or_5 (or_5_out, d_ff_1_q, IR1_q);
  and and_1 (and_1_out, or_5_out, ~URETA);  // AND_Gate
  or or_6 (or_6_out, d_ff_2_q, IR2_q);
  or or_7 (or_7_out, d_ff_3_q, IR3_q);
  Comparator #(.width(32), .mode("twosComplement")) comparator_1 (
    .a(EX_PC), .b(32'h31f4), .gt(comparator_1_gt), .lt(comparator_1_lt));  // open: eq
  Comparator #(.width(32), .mode("twosComplement")) comparator_2 (
    .a(EX_PC), .b(32'h3150), .gt(comparator_2_gt), .lt(comparator_2_lt));  // open: eq
  Comparator #(.width(32), .mode("twosComplement")) comparator_3 (
    .a(EX_PC), .b(32'h30ac), .gt(comparator_3_gt));  // open: eq, lt
  Hex_Digit_Display hex_digit_display_6 (.value(LedData[11:8]));  // open: dp
  Hex_Digit_Display hex_digit_display_7 (.value(LedData[7:4]));  // open: dp
  // Probe on \总周期数 
  D_Flip_Flop #(.trigger("rising"), .Pre_Clr_Positions("LEGACY"), .NegatePresetClear("false"), .enable("true"), .NewFFLayout("false")) u_IR1 (
    .clk(CLK), .D(and_1_out), .Q(IR1_q));  // open: Qn, preset, en, reset
  and and_2 (and_2_out, or_6_out, ~URETB);  // AND_Gate
  and and_3 (and_3_out, or_7_out, ~URETC);  // AND_Gate
  Register #(.width(1), .trigger("rising"), .Select("low")) register_2 (
    .D(or_4_out), .Q(IE), .clk(CLK), .clr(URET));  // open: en
  Hex_Digit_Display hex_digit_display_8 (.value(LedData[3:0]));  // open: dp
  D_Flip_Flop #(.trigger("rising"), .Pre_Clr_Positions("LEGACY"), .NegatePresetClear("false"), .enable("true"), .NewFFLayout("false")) u_IR2 (
    .clk(CLK), .D(and_2_out), .Q(IR2_q));  // open: Qn, preset, en, reset
  D_Flip_Flop #(.trigger("rising"), .Pre_Clr_Positions("LEGACY"), .NegatePresetClear("false"), .enable("true"), .NewFFLayout("false")) u_IR3 (
    .clk(CLK), .D(and_3_out), .Q(IR3_q));  // open: Qn, preset, en, reset
  and and_4 (and_4_out, comparator_1_lt, comparator_2_gt);
  and and_5 (and_5_out, comparator_2_lt, comparator_3_gt);
  and and_6 (URETC, URET, comparator_1_gt);
  and and_7 (URETB, URET, and_4_out);
  and and_8 (URETA, URET, and_5_out);
  or or_8 (IR1_t, IR1, IRA);
  or or_9 (IR2_t, IR2, IRB);
  not not_2 (not_2_out, IE);
  // Probe on multiplexer_1_out
  not not_3 (not_3_out, IE);
  and and_9 (and_9_out, W1, not_3_out);
  and and_10 (and_10_out, W2, not_2_out);
  and and_11 (and_11_out, W3, not_4_out);
  or or_10 (IR3_t, IR3, IRC);
  Counter #(.width(16), .max('hffff), .ongoal("wrap"), .trigger("rising"), .behavior("new")) counter_1 (
    .count(tunnel1), .Q(\条件分支成功数 ), .clk(CLK), .clr(RST));  // open: load, D, carry, preset, down
  Counter #(.width(16), .max('hffff), .ongoal("wrap"), .trigger("rising"), .behavior("new")) counter_2 (
    .Q(\LoadUse次数 ), .clk(clash), .clr(RST));  // open: load, D, count, carry, preset, down
  Multiplexer #(.select(1), .width(32), .disabled("Z"), .enable("false")) multiplexer_1 (
    .in0(multiplexer_2_out), .in1(EPC), .out(multiplexer_1_out), .sel(URET));
  Multiplexer #(.select(2), .width(32), .disabled("Z"), .enable("false")) multiplexer_2 (
    .in0(EPC_IN), .in1(32'h30ac), .in2(32'h3150), .in3(32'h31f4), .out(multiplexer_2_out),
    .sel(priority_encoder_1_out));
  Priority_Encoder #(.select(2), .disabled("Z")) priority_encoder_1 (
    .in0(1'b1), .in1(and_9_out), .in2(and_10_out), .in3(and_11_out), .out(priority_encoder_1_out));  // open: gs, en_out, en_in
  not not_4 (not_4_out, IE);
  Counter #(.width(16), .max('hffff), .ongoal("wrap"), .trigger("rising"), .behavior("new")) counter_3 (
    .Q(\插入气泡数 ), .clk(clash), .clr(RST));  // open: load, D, count, carry, preset, down
  Register #(.width(32), .trigger("rising"), .Select("low")) u_PC (
    .D(multiplexer_1_out), .en(and_12_out), .Q(IF_PC), .clk(CLK), .clr(RST));
  and and_12 (and_12_out, or_11_out, not_5_out);
  not not_5 (not_5_out, clash);
  or or_11 (or_11_out, not_6_out, Go);
  not not_6 (not_6_out, halt);
  Comparator #(.width(2), .mode("unsigned")) comparator_4 (
    .a(priority_encoder_1_out), .b(2'b00), .gt(jump1));  // open: eq, lt
  or or_12 (or_12_out, JAL, JALR);
  not not_7 (not_7_out, halt);
  or or_13 (or_13_out, not_7_out, Go);
  Counter #(.width(16), .max('hffff), .ongoal("wrap"), .trigger("rising"), .behavior("new")) counter_4 (
    .count(or_13_out), .Q(\总周期数 ), .clk(CLK), .clr(RST));  // open: load, D, carry, preset, down
  Counter #(.width(16), .max('hffff), .ongoal("wrap"), .trigger("rising"), .behavior("new")) counter_5 (
    .Q(\无条件分支数 ), .clk(or_12_out), .clr(RST));  // open: load, D, count, carry, preset, down
  ROM #(.addrWidth(10), .dataWidth(32), .Select("high")) rom_1 (.addr(IF_PC[11:2]), .data(IF_IR));
  Adder #(.width(32)) adder_1 (.a(IF_PC), .b(32'h4), .out(adder_1_out));  // open: cin, cout
  not not_8 (not_8_out, clash);
  or or_14 (or_14_out, not_9_out, Go);
  not not_9 (not_9_out, halt);
  IF_ID2 if_id2_1 (
    .IR_IN(IF_IR), .PC_IN(IF_PC),
    .IR_OUT({ID_IR[31], funct[4], ID_IR[29:26], funct[3], ID_IR[24:15], funct[2:0], ID_IR[11:0]}),
    .PC_OUT(ID_PC), .CLR(branch), .RST(RST), .en(and_13_out), .CLK(CLK));  // open: PREDICTJUMP_IN, PREDICTJUMP_OUT
  and and_13 (and_13_out, not_8_out, or_14_out);
  D_Flip_Flop #(.trigger("high"), .Pre_Clr_Positions("LEGACY"), .NegatePresetClear("false"), .enable("true"), .NewFFLayout("false")) d_ff_4 (.Q(d_ff_4_q));  // open: clk, D, Qn, preset, en, reset
  // Probe on 13'hc
  // RiscV_Probe riscv_probe_1: pin names not known; wires that end beside it: {ID_IR[31], funct[4], ID_IR[29:26], funct[3], ID_IR[24:15], funct[2:0], ID_IR[11:0]}
  Comparator #(.width(13), .mode("twosComplement")) comparator_5 (
    .a(CNT_num), .b(13'hc), .eq(comparator_5_eq), .lt(comparator_5_lt));  // open: gt
  Clock #(.highDuration(1), .lowDuration(1)) clock_1 (.out(clock_1_out));
  Counter #(.width(13), .max('h1fff), .ongoal("stay"), .trigger("rising"), .behavior("old")) counter_6 (
    .count(comparator_5_lt), .Q(CNT_num), .clk(clock_1_out));  // open: load, D, carry, clr, preset
  nand nand_1 (nand_1_out, d_ff_4_q, comparator_5_eq);
  \单周期硬布线控制器  \u_单周期硬布线控制器_1  (
    .Funct(funct), .OP(ID_IR[6:2]), .ALU_OP(\单周期硬布线控制器_1_alu_op ), .MemToReg(\单周期硬布线控制器_1_memtoreg ),
    .MemWrite(\单周期硬布线控制器_1_memwrite ), .ALU_SRC(\单周期硬布线控制器_1_alu_src ), .RegWrite(\单周期硬布线控制器_1_regwrite ),
    .ecall(ecall), .S_type(S_type), .Jalr(\单周期硬布线控制器_1_jalr ), .Beq(\单周期硬布线控制器_1_beq ),
    .JAL(\单周期硬布线控制器_1_jal ), .Bne(\单周期硬布线控制器_1_bne ), .in_3(ID_IR[21]), .uret(\单周期硬布线控制器_1_uret ),
    .BGEU(\单周期硬布线控制器_1_bgeu ));
  Multiplexer #(.select(1), .width(5), .disabled("Z"), .enable("false")) multiplexer_3 (
    .in0(ID_IR[19:15]), .in1(5'b10001), .out(R1_num), .sel(ecall));
  Multiplexer #(.select(1), .width(5), .disabled("Z"), .enable("false")) multiplexer_4 (
    .in0(ID_IR[24:20]), .in1(5'b01010), .out(R2_num), .sel(ecall));
  Multiplexer #(.select(1), .width(12), .disabled("Z"), .enable("false")) multiplexer_5 (
    .in0({ID_IR[31], funct[4], ID_IR[29:26], funct[3], ID_IR[24:20]}),
    .in1({ID_IR[31], funct[4], ID_IR[29:26], funct[3], ID_IR[11:7]}), .out(multiplexer_5_out), .sel(S_type));
  assign bit_extender_1_out = {{20{ID_IR[31]}}, {ID_IR[31], ID_IR[7], funct[4], ID_IR[29:26], funct[3], ID_IR[11:8]}};  // Bit_Extender bit_extender_1
  assign CLK = nand_1_out ? clock_1_out : 1'bz;  // Controlled_Buffer controlled_buffer_1
  Pull_Resistor #(.pull(1)) pull_resistor_1 (.node(CLK));
  assign bit_extender_2_out = {{20{multiplexer_5_out[11]}}, multiplexer_5_out};  // Bit_Extender bit_extender_2
  Shifter #(.width(32), .shift("ll")) shifter_1 (.in(bit_extender_1_out), .\dist (5'b00001), .out(shifter_1_out));
  assign bit_extender_3_out = {{12{ID_IR[31]}}, {ID_IR[31], ID_IR[19:15], funct[2:0], ID_IR[20], funct[4], ID_IR[29:26], funct[3], ID_IR[24:21]}};  // Bit_Extender bit_extender_3
  Shifter #(.width(32), .shift("ll")) shifter_2 (.in(bit_extender_3_out), .\dist (5'b00001), .out(shifter_2_out));
  Regifile regifile_1 (
    .Din(RDin), .Clk(CLK), .R1(regifile_1_r1), .R2(regifile_1_r2), .WE(RegWrite), .W_num(mem_wb2_1_w_out),
    .R1_num(R1_num), .R2_num(R2_num));
  REDIRECT redirect_1 (
    .R1_num(R1_num), .EX_W_num(EX_W), .EX_RegWrite(EX_rw), .R2_num(R2_num), .EX_MEMTOREG(ex_memtoreg),
    .OP(ID_IR[6:2]), .MEM_W_num(MEM_W), .MEM_RegWrite(MEM_rw), .R1_FORWARD(r1_forward), .clash(clash),
    .R2_FORWARD(r2_forward), .funct3(funct[2:0]));
  // Probe on \总周期数 
  // Probe on \总周期数 
  or or_15 (or_15_out, branch, clash);
  ID_EX3 id_ex3_1 (
    .JAL(\单周期硬布线控制器_1_jal ), .JALR(\单周期硬布线控制器_1_jalr ), .BEQ(\单周期硬布线控制器_1_beq ), .BNE(\单周期硬布线控制器_1_bne ),
    .MEMTOREG(\单周期硬布线控制器_1_memtoreg ), .MEMWRITE(\单周期硬布线控制器_1_memwrite ), .ALUOP(\单周期硬布线控制器_1_alu_op ),
    .ALUSRC(\单周期硬布线控制器_1_alu_src ), .REGWRITE(\单周期硬布线控制器_1_regwrite ), .ECALL(ecall), .R1(regifile_1_r1),
    .R1FORWARD(r1_forward), .R2(regifile_1_r2), .R2FORWARD(r2_forward), .W_num(ID_IR[11:7]),
    .IMM(bit_extender_2_out), .B(shifter_1_out),
    .IR({ID_IR[31], funct[4], ID_IR[29:26], funct[3], ID_IR[24:15], funct[2:0], ID_IR[11:0]}),
    .J(shifter_2_out), .PC(ID_PC), .JAL_OUT(JAL), .JALR_OUT(JALR), .BEQ_OUT(id_ex3_1_beq_out),
    .BNE_OUT(id_ex3_1_bne_out), .MEMTOREG_OUT(ex_memtoreg), .MEMWRITE_OUT(id_ex3_1_memwrite_out),
    .ALUOP_OUT(id_ex3_1_aluop_out), .ALUSRC_OUT(AluSrcB), .REGWRITE_OUT(EX_rw),
    .ECALL_OUT(id_ex3_1_ecall_out), .R1_OUT(id_ex3_1_r1_out), .R1FORWARD_OUT(id_ex3_1_r1forward_out),
    .R2_OUT(id_ex3_1_r2_out), .R2FORWARD_OUT(id_ex3_1_r2forward_out), .W__OUT(EX_W),
    .IMM_OUT(id_ex3_1_imm_out), .B_OUT(id_ex3_1_b_out), .IR_OUT(EX_IR), .J_OUT(id_ex3_1_j_out),
    .PC_OUT(EX_PC), .CLK(CLK), .RST(RST), .CLR(or_15_out), .EN(or_19_out), .BGEU_IN(\单周期硬布线控制器_1_bgeu ),
    .BGEU_OUT(BGEU), .URET_IN(\单周期硬布线控制器_1_uret ), .URET_OUT(URET));  // open: PREDICTJUMP_IN, PREDICTJUMP_OUT
  // Probe on IF_PC[19:0]
  // RiscV_Probe riscv_probe_2: pin names not known; wires that end beside it: IF_IR
  and and_14 (and_14_out, equal, id_ex3_1_beq_out);
  not not_10 (not_10_out, equal);
  and and_15 (and_15_out, not_10_out, id_ex3_1_bne_out);
  Multiplexer #(.select(2), .width(32), .disabled("Z"), .enable("false")) multiplexer_6 (
    .in0(id_ex3_1_r1_out), .in1(new_1), .in2(RDin), .in3(RDin), .out(multiplexer_6_out),
    .sel(id_ex3_1_r1forward_out));
  Multiplexer #(.select(2), .width(32), .disabled("Z"), .enable("false")) multiplexer_7 (
    .in0(id_ex3_1_r2_out), .in1(new_1), .in2(RDin), .in3(RDin), .out(multiplexer_7_out),
    .sel(id_ex3_1_r2forward_out));
  Adder #(.width(32)) adder_2 (.a(id_ex3_1_b_out), .b(EX_PC), .out(adder_2_out));  // open: cin, cout
  // Probe on ID_PC[19:0]
  // RiscV_Probe riscv_probe_3: pin names not known; wires that end beside it: {32{1'b0}}, {ID_IR[31], funct[4], ID_IR[29:26], funct[3], ID_IR[24:15], funct[2:0], ID_IR[11:0]}
  Multiplexer #(.select(1), .width(32), .disabled("Z"), .enable("false")) multiplexer_8 (
    .in0({32{1'b0}}), .in1(multiplexer_7_out), .out(multiplexer_8_out), .sel(and_16_out));
  and and_16 (and_16_out, id_ex3_1_ecall_out, flag);
  Comparator #(.width(32), .mode("twosComplement")) comparator_6 (
    .a(32'h22), .b(multiplexer_6_out), .eq(flag));  // open: gt, lt
  Multiplexer #(.select(1), .width(32), .disabled("Z"), .enable("false")) multiplexer_9 (
    .in0(multiplexer_7_out), .in1(id_ex3_1_imm_out), .out(multiplexer_9_out), .sel(AluSrcB));
  Multiplexer #(.select(1), .width(32), .disabled("Z"), .enable("false")) multiplexer_10 (
    .in0(adder_1_out), .in1(adder_2_out), .out(multiplexer_10_out), .sel(tunnel1));
  Adder #(.width(32)) adder_3 (.a(id_ex3_1_j_out), .b(EX_PC), .out(adder_3_out));  // open: cin, cout
  or or_16 (branch, URET, JALR, JAL, jump1, tunnel1);
  Register #(.width(32), .trigger("rising"), .Select("low")) register_3 (
    .D(multiplexer_8_out), .en(and_16_out), .Q(LedData), .clk(CLK), .clr(RST));
  not not_11 (not_11_out, flag);
  or or_17 (tunnel1, and_14_out, and_15_out, and_17_out);
  and and_17 (and_17_out, BGEU, GE);
  ALU alu_1 (
    .X(multiplexer_6_out), .Y(multiplexer_9_out), .AluOP(id_ex3_1_aluop_out), .Equal(equal),
    .Result(alu_1_result), .Result_2(alu_1_result_2), .out_4(GE));  // open: out_6
  Multiplexer #(.select(1), .width(32), .disabled("Z"), .enable("false")) multiplexer_11 (
    .in0(multiplexer_10_out), .in1(adder_3_out), .out(multiplexer_11_out), .sel(JAL));
  assign and_18_out = aluresult & 32'hfffffffe;  // AND_Gate and_18, 32 bits wide
  // Probe on EX_PC[19:0]
  // RiscV_Probe riscv_probe_4: pin names not known; wires that end beside it: EX_IR
  and and_19 (and_19_out, id_ex3_1_ecall_out, not_11_out);
  Adder #(.width(32)) adder_4 (.a(EX_PC), .b(32'h4), .out(adder_4_out));  // open: cin, cout
  Multiplexer #(.select(1), .width(32), .disabled("Z"), .enable("false")) multiplexer_12 (
    .in0(multiplexer_11_out), .in1(and_18_out), .out(EPC_IN), .sel(JALR));
  // RiscV_Probe riscv_probe_5: pin names not known; wires that end beside it: MEM_IR
  Comparator #(.width(4), .mode("twosComplement")) comparator_7 (
    .a(id_ex3_1_aluop_out), .b(4'b0100), .eq(comparator_7_eq));  // open: gt, lt
  Multiplexer #(.select(1), .width(32), .disabled("Z"), .enable("false")) multiplexer_13 (
    .in0(alu_1_result), .in1(alu_1_result_2), .out(aluresult), .sel(comparator_7_eq));
  // Probe on MEM_PC[19:0]
  Comparator #(.width(20), .mode("twosComplement")) comparator_8 (.a(IF_PC[19:0]), .b(20'h2f0));  // open: gt, eq, lt
  or or_18 (or_18_out, 1'b0, and_19_out);
  // Probe on WB_PC[19:0]
  // RiscV_Probe riscv_probe_6: pin names not known; wires that end beside it: WB_IR
  EX_MEM2 ex_mem2_1 (
    .JAL_IN(JAL), .JALR_IN(JALR), .halt_IN(or_18_out), .MemToReg_IN(ex_memtoreg),
    .MemWrite_IN(id_ex3_1_memwrite_out), .RegWrite_IN(EX_rw), .aluresult_IN(aluresult),
    .MA_IN(aluresult[11:2]), .MDin_IN(multiplexer_7_out), .W_IN(EX_W), .PC_IN(EX_PC), .IR_IN(EX_IR),
    .IMM_IN(adder_4_out), .JAL_OUT(ex_mem2_1_jal_out), .JALR_OUT(ex_mem2_1_jalr_out),
    .halt_OUT(ex_mem2_1_halt_out), .MemToReg_OUT(mem_memtoreg), .MemWrite_OUT(MemWrite),
    .RegWrite_OUT(MEM_rw), .aluresult_OUT(ex_mem2_1_aluresult_out), .MA_OUT(ex_mem2_1_ma_out),
    .MDin_OUT(MDin), .W_OUT(MEM_W), .PC_OUT(MEM_PC), .IR_OUT(MEM_IR), .IMM_OUT(ex_mem2_1_imm_out),
    .CLR(1'b0), .RST(RST), .en(or_19_out), .CLK(CLK), .HIGH_IN(aluresult[1]), .HIGH_OUT(ex_mem2_1_high_out));
  or or_19 (or_19_out, not_12_out, Go);
  not not_12 (not_12_out, halt);
  not not_13 (not_13_out, MemWrite);
  or or_20 (or_20_out, ex_mem2_1_jal_out, ex_mem2_1_jalr_out);
  Multiplexer #(.select(1), .width(32), .disabled("Z"), .enable("false")) multiplexer_14 (
    .in0(ex_mem2_1_aluresult_out), .in1(ex_mem2_1_imm_out), .out(new_1), .sel(or_20_out));
  RAM #(.addrWidth(10), .dataWidth(32), .bus("separate"), .Select("high")) ram_1 (
    .addr(ex_mem2_1_ma_out), .din(MDin), .data(ram_1_data), .str(MemWrite), .clk(CLK), .ld(not_13_out));  // open: sel, clr
  assign bit_extender_4_out = {{16{1'b0}}, ram_1_data[15:0]};  // Bit_Extender bit_extender_4
  assign bit_extender_5_out = {{16{1'b0}}, ram_1_data[31:16]};  // Bit_Extender bit_extender_5
  Comparator #(.width(3), .mode("twosComplement")) comparator_9 (
    .a(MEM_IR[14:12]), .b(3'b101), .eq(comparator_9_eq));  // open: gt, lt
  Multiplexer #(.select(1), .width(32), .disabled("Z"), .enable("false")) multiplexer_15 (
    .in0(bit_extender_4_out), .in1(bit_extender_5_out), .out(multiplexer_15_out), .sel(ex_mem2_1_high_out));
  MEM_WB2 mem_wb2_1 (
    .JAL_IN(ex_mem2_1_jal_out), .JALR_IN(ex_mem2_1_jalr_out), .halt_IN(ex_mem2_1_halt_out),
    .MemToReg_IN(mem_memtoreg), .RegWrite_IN(MEM_rw), .aluresult_IN(ex_mem2_1_aluresult_out),
    .Dout_IN(multiplexer_16_out), .W_IN(MEM_W), .IR_IN(MEM_IR), .PC_IN(MEM_PC), .IMM_IN(ex_mem2_1_imm_out),
    .JAL_OUT(mem_wb2_1_jal_out), .JALR_OUT(mem_wb2_1_jalr_out), .halt_OUT(halt), .MemToReg_OUT(MemToReg),
    .RegWrite_OUT(RegWrite), .aluresult_OUT(mem_wb2_1_aluresult_out), .Dout_OUT(mem_wb2_1_dout_out),
    .W_OUT(mem_wb2_1_w_out), .IR_OUT(WB_IR), .PC_OUT(WB_PC), .IMM_OUT(mem_wb2_1_imm_out), .CLR(1'b0),
    .RST(RST), .en(or_19_out), .CLK(CLK));
  not not_14 (not_14_out, comparator_9_eq);
  Multiplexer #(.select(1), .width(32), .disabled("Z"), .enable("false")) multiplexer_16 (
    .in0(multiplexer_15_out), .in1(ram_1_data), .out(multiplexer_16_out), .sel(not_14_out));
  Multiplexer #(.select(1), .width(32), .disabled("Z"), .enable("false")) multiplexer_17 (
    .in0(mem_wb2_1_aluresult_out), .in1(mem_wb2_1_dout_out), .out(multiplexer_17_out), .sel(MemToReg));
  or or_21 (or_21_out, mem_wb2_1_jalr_out, mem_wb2_1_jal_out);
  Multiplexer #(.select(1), .width(32), .disabled("Z"), .enable("false")) multiplexer_18 (
    .in0(multiplexer_17_out), .in1(mem_wb2_1_imm_out), .out(RDin), .sel(or_21_out));
  // Probe on nothing

  // Other names for the same wires on the sheet: ID_IR (some bits) = funct; op[4:0] = ID_IR[6:2]

  // Notes on the sheet:
  //   中断源
  //   中断等待指示
  //   总复位信号应将除ROM以外所有存储组件全部清零
  //   数码管输出
  //   数码管输出应该用寄存器锁存，否则显示数据只能一闪而过
  //   Reset 
  //   Reset 
  //   Reset 
  //   为方便自动评测，需要输出PC，IR，寄存器堆写如数据RDin
  //   RAM写使能MemWrite、RAM写入数据MDin等信号
  //   指令存储器
  //   contents of rom_1 (hex, n*v repeats v):
  //   7d000113 100413 1f41993 41f9d993 433 c00913 800b13 140413 f47413 800293 100313 499993 89e9b3 1300533
  //   2200893 73 406282b3 fe0294e3 140413 f00f93 1f47433 1c41413 800293 100313 49d993 89e9b3 1300533
  //   2200893 73 406282b3 fe0294e3 1c45413 406b0b33 b0463 f95ff06f 2b3 fff2c293 1029293 fff2e293 500533
  //   2200893 73 f5dff06f 1112023 410113 a12023 410113 812023 410113 1312023 410113 1412023 410113 1512023
  //   410113 1612023 410113 100b13 300a13 100a93 1600433 441413 14469b3 1300533 2200893 73 fe0416e3
  //   415a0a33 fe0a10e3 ffc10113 12b03 ffc10113 12a83 ffc10113 12a03 ffc10113 12983 ffc10113 12403
  //   ffc10113 12503 ffc10113 12883 200073 1112023 410113 a12023 410113 812023 410113 1312023 410113
  //   1412023 410113 1512023 410113 1612023 410113 200b13 300a13 100a93 1600433 441413 14469b3 1300533
  //   2200893 73 fe0416e3 415a0a33 fe0a10e3 ffc10113 12b03 ffc10113 12a83 ffc10113 12a03 ffc10113 12983
  //   ffc10113 12403 ffc10113 12503 ffc10113 12883 200073 1112023 410113 a12023 410113 812023 410113
  //   1312023 410113 1412023 410113 1512023 410113 1612023 410113 300b13 300a13 100a93 1600433 441413
  //   14469b3 1300533 2200893 73 fe0416e3 415a0a33 fe0a10e3 ffc10113 12b03 ffc10113 12a83 ffc10113 12a03
  //   ffc10113 12983 ffc10113 12403 ffc10113 12503 ffc10113 12883 200073
  //   控制位
  //   暂停节拍，不能为0
  //   指令探针
  //   戳工具置1进入计数暂停模式，ctrl+k时钟自动运行到对应节拍暂停
  //   ctrl+k关闭时钟连续运行，将控制位置零，进入单步调试模式调试
  //   指令字
  //   JAL
  //   JALR
  //   URET
  //   Beq
  //   Bne
  //   MemToReg
  //   MemWrite
  //   AluOP
  //   AluSrcB
  //   RegWrite
  //   可计数暂停的时钟源
  //   时空图监测，可删除
  //   数据存储器
endmodule

// EPC
module EPC_regfile (
  input  [2:0] R,
  input  [31:0] EPC_IN,
  input  CLK,
  output [31:0] EPC_OUT
);

  wire demultiplexer_2_out0, demultiplexer_2_out1, demultiplexer_2_out2, demultiplexer_2_out3,
       demultiplexer_2_out4, demultiplexer_2_out5, demultiplexer_2_out6, demultiplexer_2_out7;
  wire [31:0] demultiplexer_1_out0, demultiplexer_1_out1, demultiplexer_1_out2, demultiplexer_1_out3,
       demultiplexer_1_out4, demultiplexer_1_out5, demultiplexer_1_out6, demultiplexer_1_out7, register_1_q,
       register_2_q, register_3_q, register_4_q, register_5_q, register_6_q, register_7_q, register_8_q;

  Demultiplexer #(.select(3), .width(32), .tristate("false"), .disabled("Z"), .enable("false")) demultiplexer_1 (
    .out0(demultiplexer_1_out0), .out1(demultiplexer_1_out1), .out2(demultiplexer_1_out2),
    .out3(demultiplexer_1_out3), .out4(demultiplexer_1_out4), .out5(demultiplexer_1_out5),
    .out6(demultiplexer_1_out6), .out7(demultiplexer_1_out7), .in(EPC_IN), .sel(R));
  Demultiplexer #(.select(3), .width(1), .tristate("false"), .disabled("Z"), .enable("false")) demultiplexer_2 (
    .out0(demultiplexer_2_out0), .out1(demultiplexer_2_out1), .out2(demultiplexer_2_out2),
    .out3(demultiplexer_2_out3), .out4(demultiplexer_2_out4), .out5(demultiplexer_2_out5),
    .out6(demultiplexer_2_out6), .out7(demultiplexer_2_out7), .in(1'b1), .sel(R));
  Register #(.width(32), .trigger("rising"), .Select("low")) register_1 (
    .D(demultiplexer_1_out0), .en(demultiplexer_2_out0), .Q(register_1_q), .clk(CLK));  // open: clr
  Register #(.width(32), .trigger("rising"), .Select("low")) register_2 (
    .D(demultiplexer_1_out1), .en(demultiplexer_2_out1), .Q(register_2_q), .clk(CLK));  // open: clr
  Register #(.width(32), .trigger("rising"), .Select("low")) register_3 (
    .D(demultiplexer_1_out2), .en(demultiplexer_2_out2), .Q(register_3_q), .clk(CLK));  // open: clr
  Register #(.width(32), .trigger("rising"), .Select("low")) register_4 (
    .D(demultiplexer_1_out3), .en(demultiplexer_2_out3), .Q(register_4_q), .clk(CLK));  // open: clr
  Register #(.width(32), .trigger("rising"), .Select("low")) register_5 (
    .D(demultiplexer_1_out4), .en(demultiplexer_2_out4), .Q(register_5_q), .clk(CLK));  // open: clr
  Register #(.width(32), .trigger("rising"), .Select("low")) register_6 (
    .D(demultiplexer_1_out5), .en(demultiplexer_2_out5), .Q(register_6_q), .clk(CLK));  // open: clr
  Register #(.width(32), .trigger("rising"), .Select("low")) register_7 (
    .D(demultiplexer_1_out6), .en(demultiplexer_2_out6), .Q(register_7_q), .clk(CLK));  // open: clr
  Register #(.width(32), .trigger("rising"), .Select("low")) register_8 (
    .D(demultiplexer_1_out7), .en(demultiplexer_2_out7), .Q(register_8_q), .clk(CLK));  // open: clr
  Multiplexer #(.select(3), .width(32), .disabled("Z"), .enable("false")) multiplexer_1 (
    .in0(register_1_q), .in1(register_2_q), .in2(register_3_q), .in3(register_4_q), .in4(register_5_q),
    .in5(register_6_q), .in6(register_7_q), .in7(register_8_q), .out(EPC_OUT), .sel(R));
endmodule
module \流水线多级中断  (
  input  IR1,
  input  IR2,
  input  IR3,
  output RegWrite,
  output MemWrite,
  output [31:0] PC,
  output [31:0] IR,
  output [31:0] RDin,
  output [31:0] MDin,
  output [31:0] LedData
);

  wire a, AluSrcB, and_1_out, and_2_out, and_3_out, and_4_out, and_5_out, and_9_out, and_10_out, and_11_out,
       and_12_out, and_13_out, and_14_out, and_15_out, and_16_out, and_17_out, and_20_out, and_21_out,
       and_22_out, and_23_out, and_24_out, and_26_out, b, BGEU, branch, clash, CLK, clock_1_out,
       comparator_1_gt, comparator_1_lt, comparator_2_gt, comparator_2_lt, comparator_3_gt, comparator_4_eq,
       comparator_5_eq, comparator_7_eq, comparator_7_lt, comparator_9_eq, comparator_11_eq, d_ff_1_q,
       d_ff_2_q, d_ff_4_q, d_ff_5_q, d_ff_6_q, ecall, equal, ex_mem2_1_halt_out, ex_mem2_1_high_out,
       ex_mem2_1_jal_out, ex_mem2_1_jalr_out, ex_memtoreg, EX_rw, flag, GE, Go, halt, id_ex3_1_beq_out,
       id_ex3_1_bne_out, id_ex3_1_ecall_out, id_ex3_1_memwrite_out, IE, IR1_q, IR1_t, IR2_q, IR2_t, IR3_q,
       IR3_t, IR_A, IR_B, IR_C, IRA, IRB, IRC, JAL, JALR, jump1, mem_memtoreg, MEM_rw, mem_wb2_1_jal_out,
       mem_wb2_1_jalr_out, MemToReg, nand_1_out, not_1_out, not_2_out, not_3_out, not_4_out, not_5_out,
       not_6_out, not_7_out, not_8_out, not_9_out, not_10_out, not_11_out, not_12_out, not_13_out,
       not_14_out, not_15_out, or_4_out, or_6_out, or_8_out, or_9_out, or_12_out, or_14_out, or_15_out,
       or_16_out, or_17_out, or_18_out, or_19_out, or_22_out, or_23_out, or_24_out, or_25_out, register_2_q,
       register_3_q, register_4_q, register_5_q, register_6_q, RST, S_type, tunnel1, URET, URETA, URETB,
       URETC, W1, W2, W3, \单周期硬布线控制器_1_alu_src , \单周期硬布线控制器_1_beq , \单周期硬布线控制器_1_bgeu , \单周期硬布线控制器_1_bne ,
       \单周期硬布线控制器_1_jal , \单周期硬布线控制器_1_jalr , \单周期硬布线控制器_1_memtoreg , \单周期硬布线控制器_1_memwrite ,
       \单周期硬布线控制器_1_regwrite , \单周期硬布线控制器_1_uret ;
  wire [1:0] id_ex3_1_r1forward_out, id_ex3_1_r2forward_out, priority_encoder_1_out, r1_forward, r2_forward;
  wire [2:0] adder_2_out, counter_6_q, epc_sign;
  wire [3:0] id_ex3_1_aluop_out, \单周期硬布线控制器_1_alu_op ;
  wire [4:0] EX_W, funct, MEM_W, mem_wb2_1_w_out, R1_num, R2_num;
  wire [9:0] ex_mem2_1_ma_out;
  wire [11:0] multiplexer_6_out;
  wire [12:0] CNT_num;
  wire [15:0] \LoadUse次数 , \总周期数 , \插入气泡数 , \无条件分支数 , \条件分支成功数 ;
  wire [31:0] adder_1_out, adder_3_out, adder_4_out, adder_5_out, alu_1_result, alu_1_result_2, aluresult,
       and_25_out, bit_extender_1_out, bit_extender_2_out, bit_extender_3_out, bit_extender_4_out,
       bit_extender_5_out, EPC, EPC_IN, EX_IR, ex_mem2_1_aluresult_out, ex_mem2_1_imm_out, EX_PC,
       id_ex3_1_b_out, id_ex3_1_imm_out, id_ex3_1_j_out, id_ex3_1_r1_out, id_ex3_1_r2_out, ID_IR, ID_PC,
       IF_IR, IF_PC, MEM_IR, MEM_PC, mem_wb2_1_aluresult_out, mem_wb2_1_dout_out, mem_wb2_1_imm_out,
       multiplexer_1_out, multiplexer_2_out, multiplexer_7_out, multiplexer_8_out, multiplexer_9_out,
       multiplexer_10_out, multiplexer_11_out, multiplexer_12_out, multiplexer_16_out, multiplexer_17_out,
       multiplexer_18_out, new_1, ram_1_data, regifile_1_r1, regifile_1_r2, shifter_1_out, shifter_2_out,
       WB_IR, WB_PC;

  Button \u_继续运行  (.out(Go));
  Button _1 (.out(IRA));
  Button _2 (.out(IRB));
  Button _3 (.out(IRC));
  LED #(.active("true")) led_1 (.in(W1));
  LED #(.active("true")) led_2 (.in(W2));
  LED #(.active("true")) led_3 (.in(W3));
  Button u_RST (.out(RST));
  Hex_Digit_Display hex_digit_display_1 (.value(LedData[31:28]));  // open: dp
  Counter #(.width(16), .max('hffff), .ongoal("wrap"), .trigger("rising"), .behavior("new")) counter_1 (
    .Q(\插入气泡数 ), .clk(clash), .clr(RST));  // open: load, D, count, carry, preset, down
  or or_1 (W1, IR1_q, d_ff_1_q);
  or or_2 (W2, IR2_q, d_ff_2_q);
  or or_3 (W3, IR3_q, IR_C);
  Hex_Digit_Display hex_digit_display_2 (.value(LedData[27:24]));  // open: dp
  Hex_Digit_Display hex_digit_display_3 (.value(LedData[23:20]));  // open: dp
  D_Flip_Flop #(.trigger("rising"), .Pre_Clr_Positions("LEGACY"), .NegatePresetClear("false"), .enable("true"), .NewFFLayout("false")) d_ff_1 (
    .clk(IRA), .D(1'b1), .Q(d_ff_1_q), .reset(IR1_q));  // open: Qn, preset, en
  D_Flip_Flop #(.trigger("rising"), .Pre_Clr_Positions("LEGACY"), .NegatePresetClear("false"), .enable("true"), .NewFFLayout("false")) d_ff_2 (
    .clk(IRB), .D(1'b1), .Q(d_ff_2_q), .reset(IR2_q));  // open: Qn, preset, en
  D_Flip_Flop #(.trigger("rising"), .Pre_Clr_Positions("LEGACY"), .NegatePresetClear("false"), .enable("true"), .NewFFLayout("false")) d_ff_3 (
    .clk(IRC), .D(1'b1), .Q(IR_C), .reset(IR3_q));  // open: Qn, preset, en
  or or_4 (or_4_out, W1, W2, W3);
  Hex_Digit_Display hex_digit_display_4 (.value(LedData[19:16]));  // open: dp
  Hex_Digit_Display hex_digit_display_5 (.value(LedData[15:12]));  // open: dp
  or or_5 (IR_A, a, d_ff_1_q);
  or or_6 (or_6_out, d_ff_1_q, IR1_q);
  or or_7 (IR_B, b, d_ff_2_q);
  or or_8 (or_8_out, d_ff_2_q, IR2_q);
  or or_9 (or_9_out, IR_C, IR3_q);
  Register #(.width(1), .trigger("rising"), .Select("low")) register_1 (
    .D(or_4_out), .Q(IE), .clk(CLK), .clr(URET));  // open: en
  Hex_Digit_Display hex_digit_display_6 (.value(LedData[7:4]));  // open: dp
  Hex_Digit_Display hex_digit_display_7 (.value(LedData[11:8]));  // open: dp
  and and_1 (and_1_out, or_6_out, ~URETA);  // AND_Gate
  and and_2 (and_2_out, or_8_out, ~URETB);  // AND_Gate
  and and_3 (and_3_out, or_9_out, ~URETC);  // AND_Gate
  Hex_Digit_Display hex_digit_display_8 (.value(LedData[3:0]));  // open: dp
  // Probe on \总周期数 
  D_Flip_Flop #(.trigger("rising"), .Pre_Clr_Positions("LEGACY"), .NegatePresetClear("false"), .enable("true"), .NewFFLayout("false")) u_IR1 (
    .clk(CLK), .D(and_1_out), .Q(IR1_q));  // open: Qn, preset, en, reset
  D_Flip_Flop #(.trigger("rising"), .Pre_Clr_Positions("LEGACY"), .NegatePresetClear("false"), .enable("true"), .NewFFLayout("false")) u_IR2 (
    .clk(CLK), .D(and_2_out), .Q(IR2_q));  // open: Qn, preset, en, reset
  D_Flip_Flop #(.trigger("rising"), .Pre_Clr_Positions("LEGACY"), .NegatePresetClear("false"), .enable("true"), .NewFFLayout("false")) u_IR3 (
    .clk(CLK), .D(and_3_out), .Q(IR3_q));  // open: Qn, preset, en, reset
  Comparator #(.width(32), .mode("twosComplement")) comparator_1 (
    .a(EX_PC), .b(32'h3204), .gt(comparator_1_gt), .lt(comparator_1_lt));  // open: eq
  Comparator #(.width(32), .mode("twosComplement")) comparator_2 (
    .a(EX_PC), .b(32'h3158), .gt(comparator_2_gt), .lt(comparator_2_lt));  // open: eq
  Comparator #(.width(32), .mode("twosComplement")) comparator_3 (
    .a(EX_PC), .b(32'h30ac), .gt(comparator_3_gt));  // open: eq, lt
  and and_4 (and_4_out, comparator_1_lt, comparator_2_gt);
  and and_5 (and_5_out, comparator_2_lt, comparator_3_gt);
  or or_10 (IR1_t, IR1, IRA);
  Register #(.width(1), .trigger("falling"), .Select("low")) register_2 (
    .D(URET), .en(1'b1), .Q(register_2_q), .clk(CLK));  // open: clr
  not not_1 (not_1_out, W1);
  not not_2 (not_2_out, W2);
  not not_3 (not_3_out, W3);
  or or_11 (IR2_t, IR2, IRB);
  Comparator #(.width(3), .mode("twosComplement")) comparator_4 (
    .a(epc_sign), .b(3'b001), .eq(comparator_4_eq));  // open: gt, lt
  Register #(.width(1), .trigger("rising"), .Select("low")) register_3 (
    .D(register_2_q), .en(1'b1), .Q(register_3_q), .clk(CLK));  // open: clr
  Register #(.width(1), .trigger("rising"), .Select("low")) register_4 (
    .D(not_1_out), .Q(register_4_q), .clk(CLK), .preset(and_11_out));  // open: en, clr, cs
  Register #(.width(1), .trigger("rising"), .Select("low")) register_5 (
    .D(not_2_out), .Q(register_5_q), .clk(CLK), .preset(and_11_out));  // open: en, clr, cs
  Register #(.width(1), .trigger("rising"), .Select("low")) register_6 (
    .D(not_3_out), .Q(register_6_q), .clk(CLK), .preset(and_11_out));  // open: en, clr, cs
  and and_6 (URETC, URET, comparator_1_gt);
  and and_7 (URETB, URET, and_4_out);
  and and_8 (URETA, URET, and_5_out);
  or or_12 (or_12_out, comparator_1_gt, and_4_out);
  and and_9 (and_9_out, or_12_out, W1);
  and and_10 (and_10_out, comparator_1_gt, W2);
  Counter #(.width(16), .max('hffff), .ongoal("wrap"), .trigger("rising"), .behavior("new")) counter_2 (
    .count(tunnel1), .Q(\条件分支成功数 ), .clk(CLK), .clr(RST));  // open: load, D, carry, preset, down
  Counter #(.width(16), .max('hffff), .ongoal("wrap"), .trigger("rising"), .behavior("new")) counter_3 (
    .Q(\LoadUse次数 ), .clk(clash), .clr(RST));  // open: load, D, count, carry, preset, down
  // Probe on multiplexer_1_out
  and and_11 (and_11_out, comparator_4_eq, register_3_q);
  and and_12 (and_12_out, IR_A, register_4_q, register_5_q, register_6_q);
  and and_13 (and_13_out, IR_B, register_5_q, register_6_q);
  and and_14 (and_14_out, IR_C, register_6_q);
  not not_4 (not_4_out, and_9_out);
  or or_13 (IR3_t, IR3, IRC);
  Multiplexer #(.select(1), .width(32), .disabled("Z"), .enable("false")) multiplexer_1 (
    .in0(multiplexer_2_out), .in1(EPC), .out(multiplexer_1_out), .sel(URET));
  Multiplexer #(.select(2), .width(32), .disabled("Z"), .enable("false")) multiplexer_2 (
    .in0(EPC_IN), .in1(32'h30ac), .in2(32'h3158), .in3(32'h3204), .out(multiplexer_2_out),
    .sel(priority_encoder_1_out));
  Priority_Encoder #(.select(2), .disabled("Z")) priority_encoder_1 (
    .in0(1'b1), .in1(and_12_out), .in2(and_13_out), .in3(and_14_out), .out(priority_encoder_1_out));  // open: gs, en_out, en_in
  D_Flip_Flop #(.trigger("rising"), .Pre_Clr_Positions("ABOVE_BELOW"), .NegatePresetClear("false"), .enable("false"), .NewFFLayout("true")) d_ff_4 (
    .clk(CLK), .D(and_9_out), .Q(d_ff_4_q));  // open: Qn, preset, reset
  D_Flip_Flop #(.trigger("rising"), .Pre_Clr_Positions("ABOVE_BELOW"), .NegatePresetClear("false"), .enable("false"), .NewFFLayout("true")) d_ff_5 (
    .clk(CLK), .D(and_10_out), .Q(d_ff_5_q));  // open: Qn, preset, reset
  not not_5 (not_5_out, and_10_out);
  Comparator #(.width(3), .mode("twosComplement")) comparator_5 (
    .a(epc_sign), .b(3'b001), .eq(comparator_5_eq));  // open: gt, lt
  and and_15 (and_15_out, d_ff_4_q, not_4_out);
  and and_16 (and_16_out, d_ff_5_q, not_5_out);
  not not_6 (not_6_out, halt);
  Register #(.width(32), .trigger("rising"), .Select("low")) u_PC (
    .D(multiplexer_1_out), .en(and_17_out), .Q(IF_PC), .clk(CLK), .clr(RST));
  and and_17 (and_17_out, or_14_out, not_7_out);
  not not_7 (not_7_out, clash);
  or or_14 (or_14_out, not_8_out, Go);
  not not_8 (not_8_out, halt);
  Comparator #(.width(2), .mode("unsigned")) comparator_6 (
    .a(priority_encoder_1_out), .b(2'b00), .gt(jump1));  // open: eq, lt
  and and_18 (a, comparator_5_eq, and_15_out);
  and and_19 (b, comparator_5_eq, and_16_out);
  or or_15 (or_15_out, not_6_out, Go);
  Counter #(.width(16), .max('hffff), .ongoal("wrap"), .trigger("rising"), .behavior("new")) counter_4 (
    .count(or_15_out), .Q(\总周期数 ), .clk(CLK), .clr(RST));  // open: load, D, carry, preset, down
  Counter #(.width(16), .max('hffff), .ongoal("wrap"), .trigger("rising"), .behavior("new")) counter_5 (
    .Q(\无条件分支数 ), .clk(or_16_out), .clr(RST));  // open: load, D, count, carry, preset, down
  or or_16 (or_16_out, JAL, JALR);
  ROM #(.addrWidth(10), .dataWidth(32), .Select("high")) rom_1 (.addr(IF_PC[11:2]), .data(IF_IR));
  Adder #(.width(32)) adder_1 (.a(IF_PC), .b(32'h4), .out(adder_1_out));  // open: cin, cout
  not not_9 (not_9_out, clash);
  or or_17 (or_17_out, not_10_out, Go);
  not not_10 (not_10_out, halt);
  IF_ID2 if_id2_1 (
    .IR_IN(IF_IR), .PC_IN(IF_PC),
    .IR_OUT({ID_IR[31], funct[4], ID_IR[29:26], funct[3], ID_IR[24:15], funct[2:0], ID_IR[11:0]}),
    .PC_OUT(ID_PC), .CLR(branch), .RST(RST), .en(and_20_out), .CLK(CLK));  // open: PREDICTJUMP_IN, PREDICTJUMP_OUT
  and and_20 (and_20_out, not_9_out, or_17_out);
  or or_18 (or_18_out, jump1, URET);
  D_Flip_Flop #(.trigger("high"), .Pre_Clr_Positions("LEGACY"), .NegatePresetClear("false"), .enable("true"), .NewFFLayout("false")) d_ff_6 (.Q(d_ff_6_q));  // open: clk, D, Qn, preset, en, reset
  // Probe on 13'hc
  // RiscV_Probe riscv_probe_1: pin names not known; wires that end beside it: {ID_IR[31], funct[4], ID_IR[29:26], funct[3], ID_IR[24:15], funct[2:0], ID_IR[11:0]}
  Counter #(.width(3), .max('h7), .ongoal("wrap"), .trigger("rising"), .behavior("new")) counter_6 (
    .count(or_18_out), .Q(counter_6_q), .clk(CLK), .down(URET));  // open: load, D, carry, clr, preset
  Clock #(.highDuration(1), .lowDuration(1)) clock_1 (.out(clock_1_out));
  Adder #(.width(3)) adder_2 (.a(counter_6_q), .b(3'b001), .out(adder_2_out));  // open: cin, cout
  Comparator #(.width(13), .mode("twosComplement")) comparator_7 (
    .a(CNT_num), .b(13'hc), .eq(comparator_7_eq), .lt(comparator_7_lt));  // open: gt
  Multiplexer #(.select(1), .width(3), .disabled("Z"), .enable("false")) multiplexer_3 (
    .in0(adder_2_out), .in1(counter_6_q), .out(epc_sign), .sel(URET));
  nand nand_1 (nand_1_out, d_ff_6_q, comparator_7_eq);
  Counter #(.width(13), .max('h1fff), .ongoal("stay"), .trigger("rising"), .behavior("old")) counter_7 (
    .count(comparator_7_lt), .Q(CNT_num), .clk(clock_1_out));  // open: load, D, carry, clr, preset
  \单周期硬布线控制器  \u_单周期硬布线控制器_1  (
    .Funct(funct), .OP(ID_IR[6:2]), .ALU_OP(\单周期硬布线控制器_1_alu_op ), .MemToReg(\单周期硬布线控制器_1_memtoreg ),
    .MemWrite(\单周期硬布线控制器_1_memwrite ), .ALU_SRC(\单周期硬布线控制器_1_alu_src ), .RegWrite(\单周期硬布线控制器_1_regwrite ),
    .ecall(ecall), .S_type(S_type), .Jalr(\单周期硬布线控制器_1_jalr ), .Beq(\单周期硬布线控制器_1_beq ),
    .JAL(\单周期硬布线控制器_1_jal ), .Bne(\单周期硬布线控制器_1_bne ), .in_3(ID_IR[21]), .uret(\单周期硬布线控制器_1_uret ),
    .BGEU(\单周期硬布线控制器_1_bgeu ));
  Multiplexer #(.select(1), .width(5), .disabled("Z"), .enable("false")) multiplexer_4 (
    .in0(ID_IR[19:15]), .in1(5'b10001), .out(R1_num), .sel(ecall));
  Multiplexer #(.select(1), .width(5), .disabled("Z"), .enable("false")) multiplexer_5 (
    .in0(ID_IR[24:20]), .in1(5'b01010), .out(R2_num), .sel(ecall));
  Multiplexer #(.select(1), .width(12), .disabled("Z"), .enable("false")) multiplexer_6 (
    .in0({ID_IR[31], funct[4], ID_IR[29:26], funct[3], ID_IR[24:20]}),
    .in1({ID_IR[31], funct[4], ID_IR[29:26], funct[3], ID_IR[11:7]}), .out(multiplexer_6_out), .sel(S_type));
  assign bit_extender_1_out = {{20{ID_IR[31]}}, {ID_IR[31], ID_IR[7], funct[4], ID_IR[29:26], funct[3], ID_IR[11:8]}};  // Bit_Extender bit_extender_1
  EPC_regfile epc_regfile_1 (.EPC_IN(EPC_IN), .EPC_OUT(EPC), .CLK(CLK), .R(epc_sign));
  assign CLK = nand_1_out ? clock_1_out : 1'bz;  // Controlled_Buffer controlled_buffer_1
  Pull_Resistor #(.pull(1)) pull_resistor_1 (.node(CLK));
  Shifter #(.width(32), .shift("ll")) shifter_1 (.in(bit_extender_1_out), .\dist (5'b00001), .out(shifter_1_out));
  assign bit_extender_2_out = {{12{ID_IR[31]}}, {ID_IR[31], ID_IR[19:15], funct[2:0], ID_IR[20], funct[4], ID_IR[29:26], funct[3], ID_IR[24:21]}};  // Bit_Extender bit_extender_2
  // Probe on epc_sign
  Regifile regifile_1 (
    .Din(RDin), .Clk(CLK), .R1(regifile_1_r1), .R2(regifile_1_r2), .WE(RegWrite), .W_num(mem_wb2_1_w_out),
    .R1_num(R1_num), .R2_num(R2_num));
  assign bit_extender_3_out = {{20{multiplexer_6_out[11]}}, multiplexer_6_out};  // Bit_Extender bit_extender_3
  Shifter #(.width(32), .shift("ll")) shifter_2 (.in(bit_extender_2_out), .\dist (5'b00001), .out(shifter_2_out));
  REDIRECT redirect_1 (
    .R1_num(R1_num), .EX_W_num(EX_W), .EX_RegWrite(EX_rw), .R2_num(R2_num), .EX_MEMTOREG(ex_memtoreg),
    .OP(ID_IR[6:2]), .MEM_W_num(MEM_W), .MEM_RegWrite(MEM_rw), .R1_FORWARD(r1_forward), .clash(clash),
    .R2_FORWARD(r2_forward), .funct3(funct[2:0]));
  // Probe on \总周期数 
  // Probe on \总周期数 
  or or_19 (or_19_out, branch, clash);
  // Probe on IF_PC[19:0]
  // RiscV_Probe riscv_probe_2: pin names not known; wires that end beside it: IF_IR
  ID_EX3 id_ex3_1 (
    .JAL(\单周期硬布线控制器_1_jal ), .JALR(\单周期硬布线控制器_1_jalr ), .BEQ(\单周期硬布线控制器_1_beq ), .BNE(\单周期硬布线控制器_1_bne ),
    .MEMTOREG(\单周期硬布线控制器_1_memtoreg ), .MEMWRITE(\单周期硬布线控制器_1_memwrite ), .ALUOP(\单周期硬布线控制器_1_alu_op ),
    .ALUSRC(\单周期硬布线控制器_1_alu_src ), .REGWRITE(\单周期硬布线控制器_1_regwrite ), .ECALL(ecall), .R1(regifile_1_r1),
    .R1FORWARD(r1_forward), .R2(regifile_1_r2), .R2FORWARD(r2_forward), .W_num(ID_IR[11:7]),
    .IMM(bit_extender_3_out), .B(shifter_1_out),
    .IR({ID_IR[31], funct[4], ID_IR[29:26], funct[3], ID_IR[24:15], funct[2:0], ID_IR[11:0]}),
    .J(shifter_2_out), .PC(ID_PC), .JAL_OUT(JAL), .JALR_OUT(JALR), .BEQ_OUT(id_ex3_1_beq_out),
    .BNE_OUT(id_ex3_1_bne_out), .MEMTOREG_OUT(ex_memtoreg), .MEMWRITE_OUT(id_ex3_1_memwrite_out),
    .ALUOP_OUT(id_ex3_1_aluop_out), .ALUSRC_OUT(AluSrcB), .REGWRITE_OUT(EX_rw),
    .ECALL_OUT(id_ex3_1_ecall_out), .R1_OUT(id_ex3_1_r1_out), .R1FORWARD_OUT(id_ex3_1_r1forward_out),
    .R2_OUT(id_ex3_1_r2_out), .R2FORWARD_OUT(id_ex3_1_r2forward_out), .W__OUT(EX_W),
    .IMM_OUT(id_ex3_1_imm_out), .B_OUT(id_ex3_1_b_out), .IR_OUT(EX_IR), .J_OUT(id_ex3_1_j_out),
    .PC_OUT(EX_PC), .CLK(CLK), .RST(RST), .CLR(or_19_out), .EN(or_23_out), .BGEU_IN(\单周期硬布线控制器_1_bgeu ),
    .BGEU_OUT(BGEU), .URET_IN(\单周期硬布线控制器_1_uret ), .URET_OUT(URET));  // open: PREDICTJUMP_IN, PREDICTJUMP_OUT
  and and_21 (and_21_out, equal, id_ex3_1_beq_out);
  not not_11 (not_11_out, equal);
  and and_22 (and_22_out, not_11_out, id_ex3_1_bne_out);
  Multiplexer #(.select(2), .width(32), .disabled("Z"), .enable("false")) multiplexer_7 (
    .in0(id_ex3_1_r2_out), .in1(new_1), .in2(RDin), .in3(RDin), .out(multiplexer_7_out),
    .sel(id_ex3_1_r2forward_out));
  Adder #(.width(32)) adder_3 (.a(id_ex3_1_b_out), .b(EX_PC), .out(adder_3_out));  // open: cin, cout
  // Probe on ID_PC[19:0]
  // RiscV_Probe riscv_probe_3: pin names not known; wires that end beside it: {32{1'b0}}, {ID_IR[31], funct[4], ID_IR[29:26], funct[3], ID_IR[24:15], funct[2:0], ID_IR[11:0]}
  Multiplexer #(.select(1), .width(32), .disabled("Z"), .enable("false")) multiplexer_8 (
    .in0({32{1'b0}}), .in1(multiplexer_7_out), .out(multiplexer_8_out), .sel(and_23_out));
  and and_23 (and_23_out, id_ex3_1_ecall_out, flag);
  Comparator #(.width(32), .mode("twosComplement")) comparator_8 (
    .a(32'h22), .b(multiplexer_9_out), .eq(flag));  // open: gt, lt
  Multiplexer #(.select(2), .width(32), .disabled("Z"), .enable("false")) multiplexer_9 (
    .in0(id_ex3_1_r1_out), .in1(new_1), .in2(RDin), .in3(RDin), .out(multiplexer_9_out),
    .sel(id_ex3_1_r1forward_out));
  Multiplexer #(.select(1), .width(32), .disabled("Z"), .enable("false")) multiplexer_10 (
    .in0(multiplexer_7_out), .in1(id_ex3_1_imm_out), .out(multiplexer_10_out), .sel(AluSrcB));
  Multiplexer #(.select(1), .width(32), .disabled("Z"), .enable("false")) multiplexer_11 (
    .in0(adder_1_out), .in1(adder_3_out), .out(multiplexer_11_out), .sel(tunnel1));
  Adder #(.width(32)) adder_4 (.a(id_ex3_1_j_out), .b(EX_PC), .out(adder_4_out));  // open: cin, cout
  or or_20 (branch, URET, JALR, JAL, jump1, tunnel1);
  not not_12 (not_12_out, flag);
  or or_21 (tunnel1, and_21_out, and_22_out, and_24_out);
  and and_24 (and_24_out, BGEU, GE);
  ALU alu_1 (
    .X(multiplexer_9_out), .Y(multiplexer_10_out), .AluOP(id_ex3_1_aluop_out), .Equal(equal),
    .Result(alu_1_result), .Result_2(alu_1_result_2), .out_4(GE));  // open: out_6
  Multiplexer #(.select(1), .width(32), .disabled("Z"), .enable("false")) multiplexer_12 (
    .in0(multiplexer_11_out), .in1(adder_4_out), .out(multiplexer_12_out), .sel(JAL));
  assign and_25_out = aluresult & 32'hfffffffe;  // AND_Gate and_25, 32 bits wide
  // Probe on EX_PC[19:0]
  // RiscV_Probe riscv_probe_4: pin names not known; wires that end beside it: EX_IR
  Register #(.width(32), .trigger("rising"), .Select("low")) register_7 (
    .D(multiplexer_8_out), .en(and_23_out), .Q(LedData), .clk(CLK), .clr(RST));
  and and_26 (and_26_out, id_ex3_1_ecall_out, not_12_out);
  Multiplexer #(.select(1), .width(32), .disabled("Z"), .enable("false")) multiplexer_13 (
    .in0(multiplexer_12_out), .in1(and_25_out), .out(EPC_IN), .sel(JALR));
  Comparator #(.width(4), .mode("twosComplement")) comparator_9 (
    .a(id_ex3_1_aluop_out), .b(4'b0100), .eq(comparator_9_eq));  // open: gt, lt
  Multiplexer #(.select(1), .width(32), .disabled("Z"), .enable("false")) multiplexer_14 (
    .in0(alu_1_result), .in1(alu_1_result_2), .out(aluresult), .sel(comparator_9_eq));
  Adder #(.width(32)) adder_5 (.a(EX_PC), .b(32'h4), .out(adder_5_out));  // open: cin, cout
  // Probe on MEM_PC[19:0]
  // RiscV_Probe riscv_probe_5: pin names not known; wires that end beside it: MEM_IR
  Comparator #(.width(20), .mode("twosComplement")) comparator_10 (.a(IF_PC[19:0]), .b(20'h2f0));  // open: gt, eq, lt
  or or_22 (or_22_out, 1'b0, and_26_out);
  // Probe on WB_PC[19:0]
  // RiscV_Probe riscv_probe_6: pin names not known; wires that end beside it: WB_IR
  EX_MEM2 ex_mem2_1 (
    .JAL_IN(JAL), .JALR_IN(JALR), .halt_IN(or_22_out), .MemToReg_IN(ex_memtoreg),
    .MemWrite_IN(id_ex3_1_memwrite_out), .RegWrite_IN(EX_rw), .aluresult_IN(aluresult),
    .MA_IN(aluresult[11:2]), .MDin_IN(multiplexer_7_out), .W_IN(EX_W), .PC_IN(EX_PC), .IR_IN(EX_IR),
    .IMM_IN(adder_5_out), .JAL_OUT(ex_mem2_1_jal_out), .JALR_OUT(ex_mem2_1_jalr_out),
    .halt_OUT(ex_mem2_1_halt_out), .MemToReg_OUT(mem_memtoreg), .MemWrite_OUT(MemWrite),
    .RegWrite_OUT(MEM_rw), .aluresult_OUT(ex_mem2_1_aluresult_out), .MA_OUT(ex_mem2_1_ma_out),
    .MDin_OUT(MDin), .W_OUT(MEM_W), .PC_OUT(MEM_PC), .IR_OUT(MEM_IR), .IMM_OUT(ex_mem2_1_imm_out),
    .CLR(1'b0), .RST(RST), .en(or_23_out), .CLK(CLK), .HIGH_IN(aluresult[1]), .HIGH_OUT(ex_mem2_1_high_out));
  not not_13 (not_13_out, halt);
  or or_23 (or_23_out, not_13_out, Go);
  not not_14 (not_14_out, MemWrite);
  or or_24 (or_24_out, ex_mem2_1_jal_out, ex_mem2_1_jalr_out);
  Multiplexer #(.select(1), .width(32), .disabled("Z"), .enable("false")) multiplexer_15 (
    .in0(ex_mem2_1_aluresult_out), .in1(ex_mem2_1_imm_out), .out(new_1), .sel(or_24_out));
  RAM #(.addrWidth(10), .dataWidth(32), .bus("separate"), .Select("high")) ram_1 (
    .addr(ex_mem2_1_ma_out), .din(MDin), .data(ram_1_data), .str(MemWrite), .clk(CLK), .ld(not_14_out));  // open: sel, clr
  assign bit_extender_4_out = {{16{1'b0}}, ram_1_data[15:0]};  // Bit_Extender bit_extender_4
  assign bit_extender_5_out = {{16{1'b0}}, ram_1_data[31:16]};  // Bit_Extender bit_extender_5
  Multiplexer #(.select(1), .width(32), .disabled("Z"), .enable("false")) multiplexer_16 (
    .in0(bit_extender_4_out), .in1(bit_extender_5_out), .out(multiplexer_16_out), .sel(ex_mem2_1_high_out));
  Comparator #(.width(3), .mode("twosComplement")) comparator_11 (
    .a(MEM_IR[14:12]), .b(3'b101), .eq(comparator_11_eq));  // open: gt, lt
  not not_15 (not_15_out, comparator_11_eq);
  Multiplexer #(.select(1), .width(32), .disabled("Z"), .enable("false")) multiplexer_17 (
    .in0(multiplexer_16_out), .in1(ram_1_data), .out(multiplexer_17_out), .sel(not_15_out));
  MEM_WB2 mem_wb2_1 (
    .JAL_IN(ex_mem2_1_jal_out), .JALR_IN(ex_mem2_1_jalr_out), .halt_IN(ex_mem2_1_halt_out),
    .MemToReg_IN(mem_memtoreg), .RegWrite_IN(MEM_rw), .aluresult_IN(ex_mem2_1_aluresult_out),
    .Dout_IN(multiplexer_17_out), .W_IN(MEM_W), .IR_IN(MEM_IR), .PC_IN(MEM_PC), .IMM_IN(ex_mem2_1_imm_out),
    .JAL_OUT(mem_wb2_1_jal_out), .JALR_OUT(mem_wb2_1_jalr_out), .halt_OUT(halt), .MemToReg_OUT(MemToReg),
    .RegWrite_OUT(RegWrite), .aluresult_OUT(mem_wb2_1_aluresult_out), .Dout_OUT(mem_wb2_1_dout_out),
    .W_OUT(mem_wb2_1_w_out), .IR_OUT(WB_IR), .PC_OUT(WB_PC), .IMM_OUT(mem_wb2_1_imm_out), .CLR(1'b0),
    .RST(RST), .en(or_23_out), .CLK(CLK));
  Multiplexer #(.select(1), .width(32), .disabled("Z"), .enable("false")) multiplexer_18 (
    .in0(mem_wb2_1_aluresult_out), .in1(mem_wb2_1_dout_out), .out(multiplexer_18_out), .sel(MemToReg));
  or or_25 (or_25_out, mem_wb2_1_jalr_out, mem_wb2_1_jal_out);
  Multiplexer #(.select(1), .width(32), .disabled("Z"), .enable("false")) multiplexer_19 (
    .in0(multiplexer_18_out), .in1(mem_wb2_1_imm_out), .out(RDin), .sel(or_25_out));

  // Other names for the same wires on the sheet: ID_IR (some bits) = funct; op[4:0] = ID_IR[6:2]

  // Notes on the sheet:
  //   中断源
  //   中断等待指示
  //   总复位信号应将除ROM以外所有存储组件全部清零
  //   生成关中断指令
  //   数码管输出
  //   数码管输出应该用寄存器锁存，否则显示数据只能一闪而过
  //   Reset 
  //   生成中断等待指示
  //   Reset 
  //   Reset 
  //   判断是哪个中断的结束
  //   用于开关中断
  //   存储中断入口地址
  //   为方便自动评测，需要输出PC，IR，寄存器堆写如数据RDin
  //   RAM写使能MemWrite、RAM写入数据MDin等信号
  //   指令存储器
  //   contents of rom_1 (hex, n*v repeats v):
  //   7d000113 100413 1f41993 41f9d993 433 c00913 800b13 140413 f47413 800293 100313 499993 89e9b3 1300533
  //   2200893 73 406282b3 fe0294e3 140413 f00f93 1f47433 1c41413 800293 100313 49d993 89e9b3 1300533
  //   2200893 73 406282b3 fe0294e3 1c45413 406b0b33 b0463 f95ff06f 2b3 fff2c293 1029293 fff2e293 500533
  //   2200893 73 f5dff06f 1112023 410113 a12023 410113 812023 410113 1312023 410113 1412023 410113 1512023
  //   410113 1612023 410113 40e073 100b13 300a13 100a93 1600433 441413 14469b3 1300533 2200893 73 fe0416e3
  //   415a0a33 fe0a10e3 40f073 ffc10113 12b03 ffc10113 12a83 ffc10113 12a03 ffc10113 12983 ffc10113 12403
  //   ffc10113 12503 ffc10113 12883 200073 1112023 410113 a12023 410113 812023 410113 1312023 410113
  //   1412023 410113 1512023 410113 1612023 410113 40e073 200b13 300a13 100a93 1600433 441413 14469b3
  //   1300533 2200893 73 fe0416e3 415a0a33 fe0a10e3 40f073 ffc10113 12b03 ffc10113 12a83 ffc10113 12a03
  //   ffc10113 12983 ffc10113 12403 ffc10113 12503 ffc10113 12883 200073 1112023 410113 a12023 410113
  //   812023 410113 1312023 410113 1412023 410113 1512023 410113 1612023 410113 40e073 300b13 300a13
  //   100a93 1600433 441413 14469b3 1300533 2200893 73 fe0416e3 415a0a33 fe0a10e3 40f073 ffc10113 12b03
  //   ffc10113 12a83 ffc10113 12a03 ffc10113 12983 ffc10113 12403 ffc10113 12503 ffc10113 12883 200073
  //   控制位
  //   暂停节拍，不能为0
  //   指令探针
  //   戳工具置1进入计数暂停模式，ctrl+k时钟自动运行到对应节拍暂停
  //   ctrl+k关闭时钟连续运行，将控制位置零，进入单步调试模式调试
  //   指令字
  //   存储多级的中断返回地址
  //   JAL
  //   JALR
  //   URET
  //   Beq
  //   Bne
  //   MemToReg
  //   MemWrite
  //   AluOP
  //   AluSrcB
  //   RegWrite
  //   重定向检测和进行
  //   可计数暂停的时钟源
  //   时空图监测，可删除
  //   数据存储器
endmodule

module \单周期_单级中断_测试  (
  input  IR1,
  input  IR2,
  input  IR3,
  output RegWrite,
  output MemWrite,
  output [31:0] PC,
  output [31:0] IR,
  output [31:0] RDin,
  output [31:0] MDin,
  output [31:0] LedData
);

  wire AluSrcB, and_1_out, and_2_out, and_3_out, and_4_out, and_5_out, and_9_out, and_10_out, and_11_out,
       and_12_out, and_13_out, and_14_out, and_16_out, BGEU, CLK, clock_1_out, comparator_1_gt,
       comparator_1_lt, comparator_2_gt, comparator_2_lt, comparator_3_gt, comparator_4_eq, comparator_4_lt,
       comparator_6_eq, comparator_7_eq, d_ff_1_q, d_ff_2_q, d_ff_3_q, d_ff_4_q, ecall, equal, flag, GE, Go,
       halt, IE, IR1_q, IR1_t, IR2_q, IR2_t, IR3_q, IR3_t, IRA, IRB, IRC, JAL, JALR, MemToReg, nand_1_out,
       not_1_out, not_2_out, not_3_out, not_4_out, not_5_out, not_6_out, not_7_out, not_8_out, not_9_out,
       not_10_out, not_11_out, or_4_out, or_5_out, or_6_out, or_7_out, or_9_out, or_11_out, or_14_out, RST,
       S_type, tunnel1, URET, URETA, URETB, URETC, W1, W2, W3, \单周期硬布线控制器_1_beq , \单周期硬布线控制器_1_bne ;
  wire [1:0] priority_encoder_1_out;
  wire [3:0] \单周期硬布线控制器_1_alu_op ;
  wire [4:0] multiplexer_3_out, multiplexer_4_out;
  wire [11:0] multiplexer_5_out;
  wire [12:0] CNT_num;
  wire [15:0] \总周期数 ;
  wire [31:0] adder_1_out, adder_2_out, adder_3_out, adder_4_out, alu_1_result, alu_1_result_2, aluresult,
       and_15_out, bit_extender_1_out, bit_extender_2_out, bit_extender_3_out, bit_extender_4_out,
       bit_extender_5_out, EPC, EPC_IN, multiplexer_1_out, multiplexer_2_out, multiplexer_6_out,
       multiplexer_8_out, multiplexer_9_out, multiplexer_11_out, multiplexer_12_out, multiplexer_13_out,
       multiplexer_14_out, ram_1_data, regifile_1_r1, shifter_1_out, shifter_2_out;

  Button \u_继续运行  (.out(Go));
  Button _1 (.out(IRA));
  Button _2 (.out(IRB));
  Button _3 (.out(IRC));
  LED #(.active("true")) led_1 (.in(W1));
  LED #(.active("true")) led_2 (.in(W2));
  LED #(.active("true")) led_3 (.in(W3));
  Hex_Digit_Display hex_digit_display_1 (.value(LedData[31:28]));  // open: dp
  or or_1 (W1, IR1_q, d_ff_1_q);
  or or_2 (W2, IR2_q, d_ff_2_q);
  or or_3 (W3, IR3_q, d_ff_3_q);
  Hex_Digit_Display hex_digit_display_2 (.value(LedData[27:24]));  // open: dp
  Hex_Digit_Display hex_digit_display_3 (.value(LedData[23:20]));  // open: dp
  Button u_RST (.out(RST));
  not not_1 (not_1_out, IE);
  D_Flip_Flop #(.trigger("rising"), .Pre_Clr_Positions("LEGACY"), .NegatePresetClear("false"), .enable("true"), .NewFFLayout("false")) d_ff_1 (
    .clk(IRA), .D(1'b1), .Q(d_ff_1_q), .reset(IR1_q));  // open: Qn, preset, en
  D_Flip_Flop #(.trigger("rising"), .Pre_Clr_Positions("LEGACY"), .NegatePresetClear("false"), .enable("true"), .NewFFLayout("false")) d_ff_2 (
    .clk(IRB), .D(1'b1), .Q(d_ff_2_q), .reset(IR2_q));  // open: Qn, preset, en
  D_Flip_Flop #(.trigger("rising"), .Pre_Clr_Positions("LEGACY"), .NegatePresetClear("false"), .enable("true"), .NewFFLayout("false")) d_ff_3 (
    .clk(IRC), .D(1'b1), .Q(d_ff_3_q), .reset(IR3_q));  // open: Qn, preset, en
  or or_4 (or_4_out, W1, W2, W3);
  Hex_Digit_Display hex_digit_display_4 (.value(LedData[19:16]));  // open: dp
  Hex_Digit_Display hex_digit_display_5 (.value(LedData[15:12]));  // open: dp
  Register #(.width(32), .trigger("rising"), .Select("low")) register_1 (
    .D(EPC_IN), .en(not_1_out), .Q(EPC), .clk(CLK));  // open: clr
  or or_5 (or_5_out, d_ff_1_q, IR1_q);
  and and_1 (and_1_out, or_5_out, ~URETA);  // AND_Gate
  or or_6 (or_6_out, d_ff_2_q, IR2_q);
  or or_7 (or_7_out, d_ff_3_q, IR3_q);
  Comparator #(.width(32), .mode("twosComplement")) comparator_1 (
    .a(PC), .b(32'h31f4), .gt(comparator_1_gt), .lt(comparator_1_lt));  // open: eq
  Comparator #(.width(32), .mode("twosComplement")) comparator_2 (
    .a(PC), .b(32'h3150), .gt(comparator_2_gt), .lt(comparator_2_lt));  // open: eq
  Comparator #(.width(32), .mode("twosComplement")) comparator_3 (
    .a(PC), .b(32'h30ac), .gt(comparator_3_gt));  // open: eq, lt
  Hex_Digit_Display hex_digit_display_6 (.value(LedData[11:8]));  // open: dp
  Hex_Digit_Display hex_digit_display_7 (.value(LedData[7:4]));  // open: dp
  // Probe on \总周期数 
  D_Flip_Flop #(.trigger("rising"), .Pre_Clr_Positions("LEGACY"), .NegatePresetClear("false"), .enable("true"), .NewFFLayout("false")) u_IR1 (
    .clk(CLK), .D(and_1_out), .Q(IR1_q));  // open: Qn, preset, en, reset
  and and_2 (and_2_out, or_6_out, ~URETB);  // AND_Gate
  and and_3 (and_3_out, or_7_out, ~URETC);  // AND_Gate
  Register #(.width(1), .trigger("rising"), .Select("low")) register_2 (
    .D(or_4_out), .Q(IE), .clk(CLK), .clr(URET));  // open: en
  Hex_Digit_Display hex_digit_display_8 (.value(LedData[3:0]));  // open: dp
  D_Flip_Flop #(.trigger("rising"), .Pre_Clr_Positions("LEGACY"), .NegatePresetClear("false"), .enable("true"), .NewFFLayout("false")) u_IR2 (
    .clk(CLK), .D(and_2_out), .Q(IR2_q));  // open: Qn, preset, en, reset
  D_Flip_Flop #(.trigger("rising"), .Pre_Clr_Positions("LEGACY"), .NegatePresetClear("false"), .enable("true"), .NewFFLayout("false")) u_IR3 (
    .clk(CLK), .D(and_3_out), .Q(IR3_q));  // open: Qn, preset, en, reset
  and and_4 (and_4_out, comparator_1_lt, comparator_2_gt);
  and and_5 (and_5_out, comparator_2_lt, comparator_3_gt);
  and and_6 (URETC, URET, comparator_1_gt);
  and and_7 (URETB, URET, and_4_out);
  and and_8 (URETA, URET, and_5_out);
  or or_8 (IR1_t, IR1, IRA);
  not not_2 (not_2_out, halt);
  or or_9 (or_9_out, not_2_out, Go);
  Counter #(.width(16), .max('hffff), .ongoal("wrap"), .trigger("rising"), .behavior("new")) counter_1 (
    .count(or_9_out), .Q(\总周期数 ), .clk(CLK), .clr(RST));  // open: load, D, carry, preset, down
  and and_9 (and_9_out, W1, not_4_out);
  and and_10 (and_10_out, W2, not_3_out);
  not not_3 (not_3_out, IE);
  or or_10 (IR2_t, IR2, IRB);
  Multiplexer #(.select(2), .width(32), .disabled("Z"), .enable("false")) multiplexer_1 (
    .in0(EPC_IN), .in1(32'h30ac), .in2(32'h3150), .in3(32'h31f4), .out(multiplexer_1_out),
    .sel(priority_encoder_1_out));
  not not_4 (not_4_out, IE);
  Priority_Encoder #(.select(2), .disabled("Z")) priority_encoder_1 (
    .in0(1'b1), .in1(and_9_out), .in2(and_10_out), .in3(and_11_out), .out(priority_encoder_1_out));  // open: gs, en_out, en_in
  and and_11 (and_11_out, W3, not_5_out);
  not not_5 (not_5_out, IE);
  or or_11 (or_11_out, not_6_out, Go);
  not not_6 (not_6_out, halt);
  Multiplexer #(.select(1), .width(32), .disabled("Z"), .enable("false")) multiplexer_2 (
    .in0(multiplexer_1_out), .in1(EPC), .out(multiplexer_2_out), .sel(URET));
  or or_12 (IR3_t, IR3, IRC);
  Register #(.width(32), .trigger("rising"), .Select("low")) u_PC (
    .D(multiplexer_2_out), .en(or_11_out), .Q(PC), .clk(CLK), .clr(RST));
  // RiscV_Probe riscv_probe_1: pin names not known; wires that end beside it: PC[11:2], IR
  ROM #(.addrWidth(10), .dataWidth(32), .Select("high")) rom_1 (.addr(PC[11:2]), .data(IR));
  \单周期硬布线控制器  \u_单周期硬布线控制器_1  (
    .Funct({IR[30], IR[25], IR[14:12]}), .OP(IR[6:2]), .ALU_OP(\单周期硬布线控制器_1_alu_op ), .MemToReg(MemToReg),
    .MemWrite(MemWrite), .ALU_SRC(AluSrcB), .RegWrite(RegWrite), .ecall(ecall), .S_type(S_type), .Jalr(JALR),
    .Beq(\单周期硬布线控制器_1_beq ), .JAL(JAL), .Bne(\单周期硬布线控制器_1_bne ), .in_3(IR[21]), .uret(URET), .BGEU(BGEU));
  Multiplexer #(.select(1), .width(5), .disabled("Z"), .enable("false")) multiplexer_3 (
    .in0(IR[19:15]), .in1(5'b10001), .out(multiplexer_3_out), .sel(ecall));
  Multiplexer #(.select(1), .width(5), .disabled("Z"), .enable("false")) multiplexer_4 (
    .in0(IR[24:20]), .in1(5'b01010), .out(multiplexer_4_out), .sel(ecall));
  Multiplexer #(.select(1), .width(12), .disabled("Z"), .enable("false")) multiplexer_5 (
    .in0(IR[31:20]), .in1({IR[31:25], IR[11:7]}), .out(multiplexer_5_out), .sel(S_type));
  assign bit_extender_1_out = {{20{IR[31]}}, {IR[31], IR[7], IR[30:25], IR[11:8]}};  // Bit_Extender bit_extender_1
  assign bit_extender_2_out = {{12{IR[31]}}, {IR[31], IR[19:12], IR[20], IR[30:21]}};  // Bit_Extender bit_extender_2
  assign bit_extender_3_out = {{20{multiplexer_5_out[11]}}, multiplexer_5_out};  // Bit_Extender bit_extender_3
  D_Flip_Flop #(.trigger("high"), .Pre_Clr_Positions("LEGACY"), .NegatePresetClear("false"), .enable("true"), .NewFFLayout("false")) d_ff_4 (.Q(d_ff_4_q));  // open: clk, D, Qn, preset, en, reset
  // Probe on 13'hc
  and and_12 (and_12_out, equal, \单周期硬布线控制器_1_beq );
  not not_7 (not_7_out, equal);
  and and_13 (and_13_out, not_7_out, \单周期硬布线控制器_1_bne );
  not not_8 (not_8_out, CLK);
  Regifile regifile_1 (
    .Din(RDin), .Clk(not_8_out), .R1(regifile_1_r1), .R2(MDin), .WE(RegWrite), .W_num(IR[11:7]),
    .R1_num(multiplexer_3_out), .R2_num(multiplexer_4_out));
  Shifter #(.width(32), .shift("ll")) shifter_1 (.in(bit_extender_1_out), .\dist (5'b00001), .out(shifter_1_out));
  Shifter #(.width(32), .shift("ll")) shifter_2 (.in(bit_extender_2_out), .\dist (5'b00001), .out(shifter_2_out));
  Comparator #(.width(13), .mode("twosComplement")) comparator_4 (
    .a(CNT_num), .b(13'hc), .eq(comparator_4_eq), .lt(comparator_4_lt));  // open: gt
  Clock #(.highDuration(1), .lowDuration(1)) clock_1 (.out(clock_1_out));
  and and_14 (and_14_out, BGEU, GE);
  Multiplexer #(.select(1), .width(32), .disabled("Z"), .enable("false")) multiplexer_6 (
    .in0(MDin), .in1(bit_extender_3_out), .out(multiplexer_6_out), .sel(AluSrcB));
  Adder #(.width(32)) adder_1 (.a(shifter_1_out), .b(PC), .out(adder_1_out));  // open: cin, cout
  Adder #(.width(32)) adder_2 (.a(shifter_2_out), .b(PC), .out(adder_2_out));  // open: cin, cout
  Counter #(.width(13), .max('h1fff), .ongoal("stay"), .trigger("rising"), .behavior("old")) counter_2 (
    .count(comparator_4_lt), .Q(CNT_num), .clk(clock_1_out));  // open: load, D, carry, clr, preset
  or or_13 (tunnel1, and_12_out, and_13_out, and_14_out);
  ALU alu_1 (
    .X(regifile_1_r1), .Y(multiplexer_6_out), .AluOP(\单周期硬布线控制器_1_alu_op ), .Equal(equal),
    .Result(alu_1_result), .Result_2(alu_1_result_2), .out_4(GE));  // open: out_6
  Adder #(.width(32)) adder_3 (.a(PC), .b(32'h4), .out(adder_3_out));  // open: cin, cout
  nand nand_1 (nand_1_out, d_ff_4_q, comparator_4_eq);
  Comparator #(.width(32), .mode("twosComplement")) comparator_5 (
    .a(32'h22), .b(regifile_1_r1), .eq(flag));  // open: gt, lt
  Multiplexer #(.select(1), .width(32), .disabled("Z"), .enable("false")) multiplexer_7 (
    .in0(alu_1_result), .in1(alu_1_result_2), .out(aluresult), .sel(comparator_6_eq));
  Multiplexer #(.select(1), .width(32), .disabled("Z"), .enable("false")) multiplexer_8 (
    .in0(adder_3_out), .in1(adder_1_out), .out(multiplexer_8_out), .sel(tunnel1));
  assign CLK = nand_1_out ? clock_1_out : 1'bz;  // Controlled_Buffer controlled_buffer_1
  Pull_Resistor #(.pull(1)) pull_resistor_1 (.node(CLK));
  Comparator #(.width(4), .mode("twosComplement")) comparator_6 (
    .a(\单周期硬布线控制器_1_alu_op ), .b(4'b0100), .eq(comparator_6_eq));  // open: gt, lt
  Multiplexer #(.select(1), .width(32), .disabled("Z"), .enable("false")) multiplexer_9 (
    .in0(multiplexer_8_out), .in1(adder_2_out), .out(multiplexer_9_out), .sel(JAL));
  assign and_15_out = aluresult & 32'hfffffffe;  // AND_Gate and_15, 32 bits wide
  Multiplexer #(.select(1), .width(32), .disabled("Z"), .enable("false")) multiplexer_10 (
    .in0(multiplexer_9_out), .in1(and_15_out), .out(EPC_IN), .sel(JALR));
  not not_9 (not_9_out, MemWrite);
  Multiplexer #(.select(1), .width(32), .disabled("Z"), .enable("false")) multiplexer_11 (
    .in0({32{1'b0}}), .in1(MDin), .out(multiplexer_11_out), .sel(and_16_out));
  and and_16 (and_16_out, ecall, flag);
  RAM #(.addrWidth(10), .dataWidth(32), .bus("separate"), .Select("high")) ram_1 (
    .addr(aluresult[11:2]), .din(MDin), .data(ram_1_data), .str(MemWrite), .clk(CLK), .ld(not_9_out));  // open: sel, clr
  Register #(.width(32), .trigger("rising"), .Select("low")) register_3 (
    .D(multiplexer_11_out), .en(and_16_out), .Q(LedData), .clk(CLK), .clr(RST));
  not not_10 (not_10_out, flag);
  assign bit_extender_4_out = {{16{1'b0}}, ram_1_data[15:0]};  // Bit_Extender bit_extender_4
  assign bit_extender_5_out = {{16{1'b0}}, ram_1_data[31:16]};  // Bit_Extender bit_extender_5
  and and_17 (halt, ecall, not_10_out);
  Comparator #(.width(3), .mode("twosComplement")) comparator_7 (
    .a(IR[14:12]), .b(3'b101), .eq(comparator_7_eq));  // open: gt, lt
  not not_11 (not_11_out, comparator_7_eq);
  Multiplexer #(.select(1), .width(32), .disabled("Z"), .enable("false")) multiplexer_12 (
    .in0(bit_extender_4_out), .in1(bit_extender_5_out), .out(multiplexer_12_out), .sel(aluresult[1]));
  Multiplexer #(.select(1), .width(32), .disabled("Z"), .enable("false")) multiplexer_13 (
    .in0(aluresult), .in1(multiplexer_14_out), .out(multiplexer_13_out), .sel(MemToReg));
  Multiplexer #(.select(1), .width(32), .disabled("Z"), .enable("false")) multiplexer_14 (
    .in0(multiplexer_12_out), .in1(ram_1_data), .out(multiplexer_14_out), .sel(not_11_out));
  Adder #(.width(32)) adder_4 (.a(PC), .b(32'h4), .out(adder_4_out));  // open: cin, cout
  Multiplexer #(.select(1), .width(32), .disabled("Z"), .enable("false")) multiplexer_15 (
    .in0(multiplexer_13_out), .in1(adder_4_out), .out(RDin), .sel(or_14_out));
  or or_14 (or_14_out, JALR, JAL);

  // Notes on the sheet:
  //   中断源
  //   中断等待指示
  //   总复位信号应将除ROM以外所有存储组件全部清零
  //   生成关中断指令
  //   数码管输出
  //   数码管输出应该用寄存器锁存，否则显示数据只能一闪而过
  //   Reset 
  //   生成中断等待指示
  //   Reset 
  //   Reset 
  //   判断是哪个中断的结束
  //   用于开关中断
  //   存储中断入口地址
  //   指令探针
  //   指令存储器
  //   为方便自动评测，需要输出PC，IR，寄存器堆写如数据RDin
  //   指令字
  //   contents of rom_1 (hex, n*v repeats v):
  //   7d000113 100413 1f41993 41f9d993 433 c00913 800b13 140413 f47413 800293 100313 499993 89e9b3 1300533
  //   2200893 73 406282b3 fe0294e3 140413 f00f93 1f47433 1c41413 800293 100313 49d993 89e9b3 1300533
  //   2200893 73 406282b3 fe0294e3 1c45413 406b0b33 b0463 f95ff06f 2b3 fff2c293 1029293 fff2e293 500533
  //   2200893 73 f5dff06f 1112023 410113 a12023 410113 812023 410113 1312023 410113 1412023 410113 1512023
  //   410113 1612023 410113 100b13 300a13 100a93 1600433 441413 14469b3 1300533 2200893 73 fe0416e3
  //   415a0a33 fe0a10e3 ffc10113 12b03 ffc10113 12a83 ffc10113 12a03 ffc10113 12983 ffc10113 12403
  //   ffc10113 12503 ffc10113 12883 200073 1112023 410113 a12023 410113 812023 410113 1312023 410113
  //   1412023 410113 1512023 410113 1612023 410113 200b13 300a13 100a93 1600433 441413 14469b3 1300533
  //   2200893 73 fe0416e3 415a0a33 fe0a10e3 ffc10113 12b03 ffc10113 12a83 ffc10113 12a03 ffc10113 12983
  //   ffc10113 12403 ffc10113 12503 ffc10113 12883 200073 1112023 410113 a12023 410113 812023 410113
  //   1312023 410113 1412023 410113 1512023 410113 1612023 410113 300b13 300a13 100a93 1600433 441413
  //   14469b3 1300533 2200893 73 fe0416e3 415a0a33 fe0a10e3 ffc10113 12b03 ffc10113 12a83 ffc10113 12a03
  //   ffc10113 12983 ffc10113 12403 ffc10113 12503 ffc10113 12883 200073
  //   RAM写使能MemWrite、RAM写入数据MDin等信号
  //   JAL
  //   JALR
  //   URET
  //   Beq
  //   Bne
  //   MemToReg
  //   MemWrite
  //   AluOP
  //   AluSrcB
  //   RegWrite
  //   控制位
  //   暂停节拍，不能为0
  //   戳工具置1进入计数暂停模式，ctrl+k时钟自动运行到对应节拍暂停
  //   ctrl+k关闭时钟连续运行，将控制位置零，进入单步调试模式调试
  //   可计数暂停的时钟源
  //   数据存储器
endmodule

module \单周期_多级中断_测试  (
  input  IR1,
  input  IR2,
  input  IR3,
  output RegWrite,
  output MemWrite,
  output [31:0] PC,
  output [31:0] IR,
  output [31:0] RDin,
  output [31:0] MDin,
  output [31:0] LedData
);

  wire a, AluSrcB, and_1_out, and_2_out, and_3_out, and_4_out, and_5_out, and_9_out, and_10_out, and_11_out,
       and_12_out, and_13_out, and_14_out, and_15_out, and_16_out, and_19_out, and_20_out, and_22_out,
       and_23_out, b, BGEU, CLK, clock_1_out, comparator_1_gt, comparator_1_lt, comparator_2_gt,
       comparator_2_lt, comparator_3_gt, comparator_4_eq, comparator_5_eq, comparator_6_gt, comparator_7_eq,
       comparator_7_lt, comparator_9_eq, comparator_10_eq, d_ff_1_q, d_ff_2_q, d_ff_4_q, d_ff_5_q, d_ff_6_q,
       ecall, equal, flag, GE, Go, halt, IE, IR1_q, IR1_t, IR2_q, IR2_t, IR3_q, IR3_t, IR_A, IR_B, IR_C, IRA,
       IRB, IRC, JAL, JALR, MemToReg, nand_1_out, not_1_out, not_2_out, not_3_out, not_4_out, not_5_out,
       not_6_out, not_7_out, not_8_out, not_9_out, not_10_out, not_11_out, not_12_out, or_5_out, or_7_out,
       or_8_out, or_9_out, or_10_out, or_11_out, or_15_out, or_16_out, or_18_out, register_2_q, register_3_q,
       register_4_q, register_5_q, register_6_q, RST, S_type, tunnel1, URET, URETA, URETB, URETC, W1, W2, W3,
       \单周期硬布线控制器_1_beq , \单周期硬布线控制器_1_bne ;
  wire [1:0] priority_encoder_1_out;
  wire [2:0] adder_1_out, counter_2_q, epc_sign;
  wire [3:0] \单周期硬布线控制器_1_alu_op ;
  wire [4:0] multiplexer_4_out, multiplexer_5_out;
  wire [11:0] multiplexer_6_out;
  wire [12:0] CNT_num;
  wire [15:0] \总周期数 ;
  wire [31:0] adder_2_out, adder_3_out, adder_4_out, adder_5_out, alu_1_result, alu_1_result_2, aluresult,
       and_21_out, bit_extender_1_out, bit_extender_2_out, bit_extender_3_out, bit_extender_4_out,
       bit_extender_5_out, EPC, EPC_IN, multiplexer_1_out, multiplexer_2_out, multiplexer_7_out,
       multiplexer_9_out, multiplexer_10_out, multiplexer_12_out, multiplexer_13_out, multiplexer_14_out,
       multiplexer_15_out, ram_1_data, regifile_1_r1, shifter_1_out, shifter_2_out;

  Button \u_继续运行  (.out(Go));
  Button _1 (.out(IRA));
  Button _2 (.out(IRB));
  Button _3 (.out(IRC));
  LED #(.active("true")) led_1 (.in(W1));
  LED #(.active("true")) led_2 (.in(W2));
  LED #(.active("true")) led_3 (.in(W3));
  Button u_RST (.out(RST));
  or or_1 (W1, IR1_q, d_ff_1_q);
  or or_2 (W2, IR2_q, d_ff_2_q);
  Hex_Digit_Display hex_digit_display_1 (.value(LedData[31:28]));  // open: dp
  D_Flip_Flop #(.trigger("rising"), .Pre_Clr_Positions("LEGACY"), .NegatePresetClear("false"), .enable("true"), .NewFFLayout("false")) d_ff_1 (
    .clk(IRA), .D(1'b1), .Q(d_ff_1_q), .reset(IR1_q));  // open: Qn, preset, en
  D_Flip_Flop #(.trigger("rising"), .Pre_Clr_Positions("LEGACY"), .NegatePresetClear("false"), .enable("true"), .NewFFLayout("false")) d_ff_2 (
    .clk(IRB), .D(1'b1), .Q(d_ff_2_q), .reset(IR2_q));  // open: Qn, preset, en
  D_Flip_Flop #(.trigger("rising"), .Pre_Clr_Positions("LEGACY"), .NegatePresetClear("false"), .enable("true"), .NewFFLayout("false")) d_ff_3 (
    .clk(IRC), .D(1'b1), .Q(IR_C), .reset(IR3_q));  // open: Qn, preset, en
  or or_3 (W3, IR3_q, IR_C);
  Hex_Digit_Display hex_digit_display_2 (.value(LedData[23:20]));  // open: dp
  Hex_Digit_Display hex_digit_display_3 (.value(LedData[27:24]));  // open: dp
  or or_4 (IR_A, a, d_ff_1_q);
  or or_5 (or_5_out, d_ff_1_q, IR1_q);
  or or_6 (IR_B, b, d_ff_2_q);
  or or_7 (or_7_out, d_ff_2_q, IR2_q);
  or or_8 (or_8_out, IR_C, IR3_q);
  or or_9 (or_9_out, W1, W2, W3);
  Hex_Digit_Display hex_digit_display_4 (.value(LedData[15:12]));  // open: dp
  Hex_Digit_Display hex_digit_display_5 (.value(LedData[19:16]));  // open: dp
  not not_1 (not_1_out, halt);
  or or_10 (or_10_out, not_1_out, Go);
  Counter #(.width(16), .max('hffff), .ongoal("wrap"), .trigger("rising"), .behavior("new")) counter_1 (
    .count(or_10_out), .Q(\总周期数 ), .clk(CLK), .clr(RST));  // open: load, D, carry, preset, down
  and and_1 (and_1_out, or_5_out, ~URETA);  // AND_Gate
  and and_2 (and_2_out, or_7_out, ~URETB);  // AND_Gate
  and and_3 (and_3_out, or_8_out, ~URETC);  // AND_Gate
  Register #(.width(1), .trigger("rising"), .Select("low")) register_1 (
    .D(or_9_out), .Q(IE), .clk(CLK), .clr(URET));  // open: en
  Comparator #(.width(32), .mode("twosComplement")) comparator_1 (
    .a(PC), .b(32'h3204), .gt(comparator_1_gt), .lt(comparator_1_lt));  // open: eq
  Comparator #(.width(32), .mode("twosComplement")) comparator_2 (
    .a(PC), .b(32'h3158), .gt(comparator_2_gt), .lt(comparator_2_lt));  // open: eq
  Comparator #(.width(32), .mode("twosComplement")) comparator_3 (
    .a(PC), .b(32'h30ac), .gt(comparator_3_gt));  // open: eq, lt
  Hex_Digit_Display hex_digit_display_6 (.value(LedData[11:8]));  // open: dp
  Hex_Digit_Display hex_digit_display_7 (.value(LedData[7:4]));  // open: dp
  D_Flip_Flop #(.trigger("rising"), .Pre_Clr_Positions("LEGACY"), .NegatePresetClear("false"), .enable("true"), .NewFFLayout("false")) u_IR1 (
    .clk(CLK), .D(and_1_out), .Q(IR1_q));  // open: Qn, preset, en, reset
  D_Flip_Flop #(.trigger("rising"), .Pre_Clr_Positions("LEGACY"), .NegatePresetClear("false"), .enable("true"), .NewFFLayout("false")) u_IR2 (
    .clk(CLK), .D(and_2_out), .Q(IR2_q));  // open: Qn, preset, en, reset
  D_Flip_Flop #(.trigger("rising"), .Pre_Clr_Positions("LEGACY"), .NegatePresetClear("false"), .enable("true"), .NewFFLayout("false")) u_IR3 (
    .clk(CLK), .D(and_3_out), .Q(IR3_q));  // open: Qn, preset, en, reset
  and and_4 (and_4_out, comparator_1_lt, comparator_2_gt);
  and and_5 (and_5_out, comparator_2_lt, comparator_3_gt);
  Hex_Digit_Display hex_digit_display_8 (.value(LedData[3:0]));  // open: dp
  // Probe on \总周期数 
  Register #(.width(1), .trigger("falling"), .Select("low")) register_2 (
    .D(URET), .en(1'b1), .Q(register_2_q), .clk(CLK));  // open: clr
  not not_2 (not_2_out, W1);
  not not_3 (not_3_out, W2);
  not not_4 (not_4_out, W3);
  and and_6 (URETC, URET, comparator_1_gt);
  and and_7 (URETB, URET, and_4_out);
  and and_8 (URETA, URET, and_5_out);
  or or_11 (or_11_out, comparator_1_gt, and_4_out);
  and and_9 (and_9_out, or_11_out, W1);
  and and_10 (and_10_out, comparator_1_gt, W2);
  or or_12 (IR1_t, IR1, IRA);
  Comparator #(.width(3), .mode("twosComplement")) comparator_4 (
    .a(epc_sign), .b(3'b001), .eq(comparator_4_eq));  // open: gt, lt
  Register #(.width(1), .trigger("rising"), .Select("low")) register_3 (
    .D(register_2_q), .en(1'b1), .Q(register_3_q), .clk(CLK));  // open: clr
  Register #(.width(1), .trigger("rising"), .Select("low")) register_4 (
    .D(not_2_out), .Q(register_4_q), .clk(CLK), .preset(and_11_out));  // open: en, clr, cs
  Register #(.width(1), .trigger("rising"), .Select("low")) register_5 (
    .D(not_3_out), .Q(register_5_q), .clk(CLK), .preset(and_11_out));  // open: en, clr, cs
  Register #(.width(1), .trigger("rising"), .Select("low")) register_6 (
    .D(not_4_out), .Q(register_6_q), .clk(CLK), .preset(and_11_out));  // open: en, clr, cs
  not not_5 (not_5_out, and_9_out);
  or or_13 (IR2_t, IR2, IRB);
  and and_11 (and_11_out, comparator_4_eq, register_3_q);
  and and_12 (and_12_out, IR_A, register_4_q, register_5_q, register_6_q);
  and and_13 (and_13_out, IR_B, register_5_q, register_6_q);
  D_Flip_Flop #(.trigger("rising"), .Pre_Clr_Positions("ABOVE_BELOW"), .NegatePresetClear("false"), .enable("false"), .NewFFLayout("true")) d_ff_4 (
    .clk(CLK), .D(and_9_out), .Q(d_ff_4_q));  // open: Qn, preset, reset
  D_Flip_Flop #(.trigger("rising"), .Pre_Clr_Positions("ABOVE_BELOW"), .NegatePresetClear("false"), .enable("false"), .NewFFLayout("true")) d_ff_5 (
    .clk(CLK), .D(and_10_out), .Q(d_ff_5_q));  // open: Qn, preset, reset
  not not_6 (not_6_out, and_10_out);
  // Probe on multiplexer_1_out
  and and_14 (and_14_out, IR_C, register_6_q);
  Comparator #(.width(3), .mode("twosComplement")) comparator_5 (
    .a(epc_sign), .b(3'b001), .eq(comparator_5_eq));  // open: gt, lt
  and and_15 (and_15_out, d_ff_4_q, not_5_out);
  and and_16 (and_16_out, d_ff_5_q, not_6_out);
  or or_14 (IR3_t, IR3, IRC);
  or or_15 (or_15_out, not_7_out, Go);
  not not_7 (not_7_out, halt);
  Multiplexer #(.select(1), .width(32), .disabled("Z"), .enable("false")) multiplexer_1 (
    .in0(multiplexer_2_out), .in1(EPC), .out(multiplexer_1_out), .sel(URET));
  Multiplexer #(.select(2), .width(32), .disabled("Z"), .enable("false")) multiplexer_2 (
    .in0(EPC_IN), .in1(32'h30ac), .in2(32'h3158), .in3(32'h3204), .out(multiplexer_2_out),
    .sel(priority_encoder_1_out));
  Priority_Encoder #(.select(2), .disabled("Z")) priority_encoder_1 (
    .in0(1'b1), .in1(and_12_out), .in2(and_13_out), .in3(and_14_out), .out(priority_encoder_1_out));  // open: gs, en_out, en_in
  and and_17 (a, comparator_5_eq, and_15_out);
  and and_18 (b, comparator_5_eq, and_16_out);
  // Probe on PC
  Register #(.width(32), .trigger("rising"), .Select("low")) u_PC (
    .D(multiplexer_1_out), .en(or_15_out), .Q(PC), .clk(CLK), .clr(RST));
  Comparator #(.width(2), .mode("unsigned")) comparator_6 (
    .a(priority_encoder_1_out), .b(2'b00), .gt(comparator_6_gt));  // open: eq, lt
  or or_16 (or_16_out, comparator_6_gt, URET);
  Counter #(.width(3), .max('h7), .ongoal("wrap"), .trigger("rising"), .behavior("new")) counter_2 (
    .count(or_16_out), .Q(counter_2_q), .clk(CLK), .down(URET));  // open: load, D, carry, clr, preset
  // RiscV_Probe riscv_probe_1: pin names not known; wires that end beside it: PC[11:2], IR
  Adder #(.width(3)) adder_1 (.a(counter_2_q), .b(3'b001), .out(adder_1_out));  // open: cin, cout
  ROM #(.addrWidth(10), .dataWidth(32), .Select("high")) rom_1 (.addr(PC[11:2]), .data(IR));
  EPC_regfile epc_regfile_1 (.EPC_IN(EPC_IN), .EPC_OUT(EPC), .CLK(CLK), .R(epc_sign));
  Multiplexer #(.select(1), .width(3), .disabled("Z"), .enable("false")) multiplexer_3 (
    .in0(adder_1_out), .in1(counter_2_q), .out(epc_sign), .sel(URET));
  \单周期硬布线控制器  \u_单周期硬布线控制器_1  (
    .Funct({IR[30], IR[25], IR[14:12]}), .OP(IR[6:2]), .ALU_OP(\单周期硬布线控制器_1_alu_op ), .MemToReg(MemToReg),
    .MemWrite(MemWrite), .ALU_SRC(AluSrcB), .RegWrite(RegWrite), .ecall(ecall), .S_type(S_type), .Jalr(JALR),
    .Beq(\单周期硬布线控制器_1_beq ), .JAL(JAL), .Bne(\单周期硬布线控制器_1_bne ), .in_3(IR[21]), .uret(URET), .BGEU(BGEU));
  Multiplexer #(.select(1), .width(5), .disabled("Z"), .enable("false")) multiplexer_4 (
    .in0(IR[19:15]), .in1(5'b10001), .out(multiplexer_4_out), .sel(ecall));
  Multiplexer #(.select(1), .width(5), .disabled("Z"), .enable("false")) multiplexer_5 (
    .in0(IR[24:20]), .in1(5'b01010), .out(multiplexer_5_out), .sel(ecall));
  Multiplexer #(.select(1), .width(12), .disabled("Z"), .enable("false")) multiplexer_6 (
    .in0(IR[31:20]), .in1({IR[31:25], IR[11:7]}), .out(multiplexer_6_out), .sel(S_type));
  assign bit_extender_1_out = {{20{IR[31]}}, {IR[31], IR[7], IR[30:25], IR[11:8]}};  // Bit_Extender bit_extender_1
  assign bit_extender_2_out = {{12{IR[31]}}, {IR[31], IR[19:12], IR[20], IR[30:21]}};  // Bit_Extender bit_extender_2
  // Probe on epc_sign
  D_Flip_Flop #(.trigger("high"), .Pre_Clr_Positions("LEGACY"), .NegatePresetClear("false"), .enable("true"), .NewFFLayout("false")) d_ff_6 (.Q(d_ff_6_q));  // open: clk, D, Qn, preset, en, reset
  // Probe on 13'hc
  assign bit_extender_3_out = {{20{multiplexer_6_out[11]}}, multiplexer_6_out};  // Bit_Extender bit_extender_3
  Clock #(.highDuration(1), .lowDuration(1)) clock_1 (.out(clock_1_out));
  not not_8 (not_8_out, CLK);
  Regifile regifile_1 (
    .Din(RDin), .Clk(not_8_out), .R1(regifile_1_r1), .R2(MDin), .WE(RegWrite), .W_num(IR[11:7]),
    .R1_num(multiplexer_4_out), .R2_num(multiplexer_5_out));
  Shifter #(.width(32), .shift("ll")) shifter_1 (.in(bit_extender_1_out), .\dist (5'b00001), .out(shifter_1_out));
  Shifter #(.width(32), .shift("ll")) shifter_2 (.in(bit_extender_2_out), .\dist (5'b00001), .out(shifter_2_out));
  Comparator #(.width(13), .mode("twosComplement")) comparator_7 (
    .a(CNT_num), .b(13'hc), .eq(comparator_7_eq), .lt(comparator_7_lt));  // open: gt
  Multiplexer #(.select(1), .width(32), .disabled("Z"), .enable("false")) multiplexer_7 (
    .in0(MDin), .in1(bit_extender_3_out), .out(multiplexer_7_out), .sel(AluSrcB));
  Adder #(.width(32)) adder_2 (.a(shifter_1_out), .b(PC), .out(adder_2_out));  // open: cin, cout
  Adder #(.width(32)) adder_3 (.a(shifter_2_out), .b(PC), .out(adder_3_out));  // open: cin, cout
  nand nand_1 (nand_1_out, d_ff_6_q, comparator_7_eq);
  Counter #(.width(13), .max('h1fff), .ongoal("stay"), .trigger("rising"), .behavior("old")) counter_3 (
    .count(comparator_7_lt), .Q(CNT_num), .clk(clock_1_out));  // open: load, D, carry, clr, preset
  and and_19 (and_19_out, equal, \单周期硬布线控制器_1_beq );
  not not_9 (not_9_out, equal);
  ALU alu_1 (
    .X(regifile_1_r1), .Y(multiplexer_7_out), .AluOP(\单周期硬布线控制器_1_alu_op ), .Equal(equal),
    .Result(alu_1_result), .Result_2(alu_1_result_2), .out_4(GE));  // open: out_6
  assign CLK = nand_1_out ? clock_1_out : 1'bz;  // Controlled_Buffer controlled_buffer_1
  Pull_Resistor #(.pull(1)) pull_resistor_1 (.node(CLK));
  and and_20 (and_20_out, not_9_out, \单周期硬布线控制器_1_bne );
  Comparator #(.width(32), .mode("twosComplement")) comparator_8 (
    .a(32'h22), .b(regifile_1_r1), .eq(flag));  // open: gt, lt
  Comparator #(.width(4), .mode("twosComplement")) comparator_9 (
    .a(\单周期硬布线控制器_1_alu_op ), .b(4'b0100), .eq(comparator_9_eq));  // open: gt, lt
  Multiplexer #(.select(1), .width(32), .disabled("Z"), .enable("false")) multiplexer_8 (
    .in0(alu_1_result), .in1(alu_1_result_2), .out(aluresult), .sel(comparator_9_eq));
  Adder #(.width(32)) adder_4 (.a(PC), .b(32'h4), .out(adder_4_out));  // open: cin, cout
  Multiplexer #(.select(1), .width(32), .disabled("Z"), .enable("false")) multiplexer_9 (
    .in0(adder_4_out), .in1(adder_2_out), .out(multiplexer_9_out), .sel(tunnel1));
  Multiplexer #(.select(1), .width(32), .disabled("Z"), .enable("false")) multiplexer_10 (
    .in0(multiplexer_9_out), .in1(adder_3_out), .out(multiplexer_10_out), .sel(JAL));
  assign and_21_out = aluresult & 32'hfffffffe;  // AND_Gate and_21, 32 bits wide
  and and_22 (and_22_out, BGEU, GE);
  Multiplexer #(.select(1), .width(32), .disabled("Z"), .enable("false")) multiplexer_11 (
    .in0(multiplexer_10_out), .in1(and_21_out), .out(EPC_IN), .sel(JALR));
  or or_17 (tunnel1, and_19_out, and_20_out, and_22_out);
  not not_10 (not_10_out, MemWrite);
  Multiplexer #(.select(1), .width(32), .disabled("Z"), .enable("false")) multiplexer_12 (
    .in0({32{1'b0}}), .in1(MDin), .out(multiplexer_12_out), .sel(and_23_out));
  and and_23 (and_23_out, ecall, flag);
  RAM #(.addrWidth(10), .dataWidth(32), .bus("separate"), .Select("high")) ram_1 (
    .addr(aluresult[11:2]), .din(MDin), .data(ram_1_data), .str(MemWrite), .clk(CLK), .ld(not_10_out));  // open: sel, clr
  not not_11 (not_11_out, flag);
  assign bit_extender_4_out = {{16{1'b0}}, ram_1_data[15:0]};  // Bit_Extender bit_extender_4
  assign bit_extender_5_out = {{16{1'b0}}, ram_1_data[31:16]};  // Bit_Extender bit_extender_5
  Register #(.width(32), .trigger("rising"), .Select("low")) register_7 (
    .D(multiplexer_12_out), .en(and_23_out), .Q(LedData), .clk(CLK), .clr(RST));
  and and_24 (halt, ecall, not_11_out);
  Multiplexer #(.select(1), .width(32), .disabled("Z"), .enable("false")) multiplexer_13 (
    .in0(bit_extender_4_out), .in1(bit_extender_5_out), .out(multiplexer_13_out), .sel(aluresult[1]));
  Comparator #(.width(3), .mode("twosComplement")) comparator_10 (
    .a(IR[14:12]), .b(3'b101), .eq(comparator_10_eq));  // open: gt, lt
  not not_12 (not_12_out, comparator_10_eq);
  Multiplexer #(.select(1), .width(32), .disabled("Z"), .enable("false")) multiplexer_14 (
    .in0(multiplexer_13_out), .in1(ram_1_data), .out(multiplexer_14_out), .sel(not_12_out));
  Multiplexer #(.select(1), .width(32), .disabled("Z"), .enable("false")) multiplexer_15 (
    .in0(aluresult), .in1(multiplexer_14_out), .out(multiplexer_15_out), .sel(MemToReg));
  or or_18 (or_18_out, JALR, JAL);
  Adder #(.width(32)) adder_5 (.a(PC), .b(32'h4), .out(adder_5_out));  // open: cin, cout
  Multiplexer #(.select(1), .width(32), .disabled("Z"), .enable("false")) multiplexer_16 (
    .in0(multiplexer_15_out), .in1(adder_5_out), .out(RDin), .sel(or_18_out));

  // Notes on the sheet:
  //   中断源
  //   中断等待指示
  //   总复位信号应将除ROM以外所有存储组件全部清零
  //   生成关中断指令
  //   判断是哪个中断的结束
  //   数码管输出
  //   Reset 
  //   生成中断等待指示
  //   Reset 
  //   数码管输出应该用寄存器锁存，否则显示数据只能一闪而过
  //   Reset 
  //   用于开关中断
  //   为方便自动评测，需要输出PC，IR，寄存器堆写如数据RDin
  //   指令探针
  //   指令存储器
  //   RAM写使能MemWrite、RAM写入数据MDin等信号
  //   指令字
  //   contents of rom_1 (hex, n*v repeats v):
  //   7d000113 100413 1f41993 41f9d993 433 c00913 800b13 140413 f47413 800293 100313 499993 89e9b3 1300533
  //   2200893 73 406282b3 fe0294e3 140413 f00f93 1f47433 1c41413 800293 100313 49d993 89e9b3 1300533
  //   2200893 73 406282b3 fe0294e3 1c45413 406b0b33 b0463 f95ff06f 2b3 fff2c293 1029293 fff2e293 500533
  //   2200893 73 f5dff06f 1112023 410113 a12023 410113 812023 410113 1312023 410113 1412023 410113 1512023
  //   410113 1612023 410113 40e073 100b13 300a13 100a93 1600433 441413 14469b3 1300533 2200893 73 fe0416e3
  //   415a0a33 fe0a10e3 40f073 ffc10113 12b03 ffc10113 12a83 ffc10113 12a03 ffc10113 12983 ffc10113 12403
  //   ffc10113 12503 ffc10113 12883 200073 1112023 410113 a12023 410113 812023 410113 1312023 410113
  //   1412023 410113 1512023 410113 1612023 410113 40e073 200b13 300a13 100a93 1600433 441413 14469b3
  //   1300533 2200893 73 fe0416e3 415a0a33 fe0a10e3 40f073 ffc10113 12b03 ffc10113 12a83 ffc10113 12a03
  //   ffc10113 12983 ffc10113 12403 ffc10113 12503 ffc10113 12883 200073 1112023 410113 a12023 410113
  //   812023 410113 1312023 410113 1412023 410113 1512023 410113 1612023 410113 40e073 300b13 300a13
  //   100a93 1600433 441413 14469b3 1300533 2200893 73 fe0416e3 415a0a33 fe0a10e3 40f073 ffc10113 12b03
  //   ffc10113 12a83 ffc10113 12a03 ffc10113 12983 ffc10113 12403 ffc10113 12503 ffc10113 12883 200073
  //   JAL
  //   JALR
  //   URET
  //   存储多级的中断返回地址
  //   Beq
  //   Bne
  //   MemToReg
  //   MemWrite
  //   AluOP
  //   AluSrcB
  //   RegWrite
  //   控制位
  //   暂停节拍，不能为0
  //   戳工具置1进入计数暂停模式，ctrl+k时钟自动运行到对应节拍暂停
  //   ctrl+k关闭时钟连续运行，将控制位置零，进入单步调试模式调试
  //   可计数暂停的时钟源
  //   数据存储器
endmodule

module \团队作业_扫雷游戏  (
  output RegWrite,
  output MemWrite,
  output [31:0] PC,
  output [31:0] IR,
  output [31:0] RDin,
  output [31:0] MDin,
  output [31:0] LedData
);

  wire AluSrcB, and_1_out, and_2_out, and_3_out, and_4_out, and_5_out, and_6_out, and_7_out, and_8_out,
       and_9_out, and_10_out, and_11_out, and_12_out, and_13_out, and_14_out, and_15_out, and_16_out,
       and_17_out, and_18_out, and_19_out, and_20_out, and_21_out, and_22_out, and_23_out, and_24_out,
       and_25_out, and_26_out, and_27_out, and_28_out, and_29_out, and_30_out, and_31_out, and_32_out,
       and_33_out, and_34_out, and_35_out, and_36_out, and_37_out, and_38_out, and_39_out, and_40_out,
       and_41_out, and_42_out, and_43_out, and_45_out, and_46_out, and_47_out, and_48_out, and_49_out,
       and_50_out, and_52_out, and_53_out, and_54_out, and_55_out, and_56_out, and_57_out, and_58_out,
       and_59_out, and_60_out, and_61_out, and_62_out, and_63_out, BGEU, CLK, clock_1_out, comparator_1_eq,
       comparator_1_lt, comparator_3_eq, comparator_4_eq, comparator_5_eq, comparator_6_eq, comparator_7_eq,
       comparator_8_gt, comparator_9_eq, comparator_10_eq, comparator_11_eq, d_ff_1_q, d_ff_2_q, d_ff_3_q,
       d_ff_4_q, d_ff_5_q, d_ff_6_q, d_ff_7_q, d_ff_8_q, d_ff_9_q, d_ff_10_q, d_ff_11_q, d_ff_12_q,
       d_ff_13_q, d_ff_14_q, d_ff_15_q, d_ff_16_q, d_ff_17_q, d_ff_18_q, d_ff_19_q, d_ff_20_q, d_ff_21_q,
       d_ff_22_q, d_ff_23_q, d_ff_24_q, d_ff_25_q, d_ff_26_q, d_ff_27_q, d_ff_28_q, d_ff_29_q, d_ff_30_q,
       d_ff_31_q, d_ff_32_q, d_ff_33_q, d_ff_34_q, d_ff_35_q, d_ff_36_q, d_ff_37_q, d_ff_38_q, d_ff_39_q,
       d_ff_40_q, d_ff_41_q, d_ff_42_q, d_ff_43_q, d_ff_44_q, d_ff_45_q, d_ff_46_q, d_ff_47_q, d_ff_48_q,
       d_ff_49_q, d_ff_50_q, d_ff_51_q, ecall, equal, flag, GE, Go, halt, IE, IR0, IR1, IR2, IR3, IR4, IR5,
       IR6, IR7, IR8, IR9, IR10, IR11, IR12, IR13, IR14, IR15, IR16, IR17, IR18, IR19, IR20, IR21, IR22,
       IR23, IR24, JAL, JALR, MemToReg, nand_1_out, not_1_out, not_2_out, not_3_out, not_4_out, not_5_out,
       not_6_out, not_7_out, not_8_out, not_9_out, not_10_out, not_11_out, not_12_out, not_13_out,
       not_14_out, not_15_out, not_16_out, not_17_out, not_18_out, not_19_out, not_20_out, not_21_out,
       not_22_out, not_23_out, not_24_out, not_25_out, not_26_out, not_27_out, not_28_out, not_29_out,
       not_30_out, not_31_out, not_32_out, not_33_out, or_6_out, or_7_out, or_8_out, or_9_out, or_10_out,
       or_11_out, or_17_out, or_18_out, or_19_out, or_20_out, or_21_out, or_22_out, or_28_out, or_29_out,
       or_30_out, or_31_out, or_32_out, or_39_out, or_40_out, or_41_out, or_42_out, or_43_out, or_44_out,
       or_50_out, or_51_out, or_52_out, or_53_out, or_54_out, or_55_out, or_56_out, register_8_q, RST,
       S_type, tunnel1, URET, URET0, URET1, URET2, URET3, URET4, URET5, URET6, URET7, URET8, URET9, URET10,
       URET11, URET12, URET13, URET14, URET15, URET16, URET17, URET18, URET19, URET20, URET21, URET22,
       URET23, URET24, W0, W1, W2, W3, W4, W5, W6, W7, W8, W9, W10, W11, W12, W13, W14, W15, W16, W17, W18,
       W19, W20, W21, W22, W23, W24, \单周期硬布线控制器_1_beq , \单周期硬布线控制器_1_bne , \继续运行_out ;
  wire [3:0] \单周期硬布线控制器_1_alu_op ;
  wire [4:0] multiplexer_3_out, multiplexer_4_out, priority_encoder_1_out, register_7_q;
  wire [6:0] register_3_q, register_4_q;
  wire [7:0] count_1_sum, register_5_q, register_6_q;
  wire [11:0] multiplexer_5_out;
  wire [12:0] CNT_num;
  wire [15:0] \总周期数 ;
  wire [31:0] adder_1_out, adder_2_out, adder_3_out, adder_4_out, alu_1_result, alu_1_result_2, aluresult,
       and_44_out, bit_extender_1_out, bit_extender_2_out, bit_extender_3_out, bit_extender_4_out,
       bit_extender_5_out, EPC, EPC_IN, multiplexer_1_out, multiplexer_2_out, multiplexer_6_out,
       multiplexer_8_out, multiplexer_9_out, multiplexer_11_out, multiplexer_12_out, multiplexer_13_out,
       multiplexer_14_out, ram_1_data, regifile_1_r1, shifter_1_out, shifter_2_out;

  Button \u_继续运行  (.out(\继续运行_out ));
  Button _1 ();  // open: out
  Button _2 ();  // open: out
  Button _3 ();  // open: out
  LED #(.active("true")) led_1 ();  // open: in
  LED #(.active("true")) led_2 ();  // open: in
  LED #(.active("true")) led_3 ();  // open: in
  Hex_Digit_Display hex_digit_display_1 (.value(LedData[31:28]));  // open: dp
  Button u_RST (.out(RST));
  not not_1 (not_1_out, IE);
  not not_2 (not_2_out, IE);
  and and_1 (and_1_out, not_2_out, W0);
  not not_3 (not_3_out, IE);
  and and_2 (and_2_out, not_3_out, W2);
  not not_4 (not_4_out, IE);
  and and_3 (and_3_out, not_4_out, W4);
  not not_5 (not_5_out, IE);
  and and_4 (and_4_out, not_5_out, W6);
  not not_6 (not_6_out, IE);
  and and_5 (and_5_out, not_6_out, W8);
  not not_7 (not_7_out, IE);
  and and_6 (and_6_out, not_7_out, W10);
  not not_8 (not_8_out, IE);
  and and_7 (and_7_out, not_8_out, W12);
  not not_9 (not_9_out, IE);
  and and_8 (and_8_out, not_9_out, W14);
  not not_10 (not_10_out, IE);
  and and_9 (and_9_out, not_10_out, W16);
  not not_11 (not_11_out, IE);
  and and_10 (and_10_out, not_11_out, W18);
  not not_12 (not_12_out, IE);
  and and_11 (and_11_out, not_12_out, W20);
  not not_13 (not_13_out, IE);
  and and_12 (and_12_out, not_13_out, W22);
  not not_14 (not_14_out, IE);
  and and_13 (and_13_out, not_14_out, W24);
  or or_1 (W0, d_ff_6_q, d_ff_1_q);
  or or_2 (W5, d_ff_7_q, d_ff_2_q);
  or or_3 (W10, d_ff_8_q, d_ff_3_q);
  or or_4 (W15, d_ff_9_q, d_ff_4_q);
  or or_5 (W20, d_ff_10_q, d_ff_5_q);
  Hex_Digit_Display hex_digit_display_2 (.value(LedData[27:24]));  // open: dp
  Hex_Digit_Display hex_digit_display_3 (.value(LedData[23:20]));  // open: dp
  Register #(.width(32), .trigger("rising"), .Select("low")) register_1 (
    .D(EPC_IN), .en(not_1_out), .Q(EPC), .clk(CLK));  // open: clr
  not not_15 (not_15_out, IE);
  not not_16 (not_16_out, IE);
  not not_17 (not_17_out, IE);
  not not_18 (not_18_out, IE);
  not not_19 (not_19_out, IE);
  not not_20 (not_20_out, IE);
  not not_21 (not_21_out, IE);
  not not_22 (not_22_out, IE);
  not not_23 (not_23_out, IE);
  not not_24 (not_24_out, IE);
  not not_25 (not_25_out, IE);
  not not_26 (not_26_out, IE);
  D_Flip_Flop #(.trigger("rising"), .Pre_Clr_Positions("LEGACY"), .NegatePresetClear("false"), .enable("true"), .NewFFLayout("false")) d_ff_1 (
    .clk(IR0), .D(1'b1), .Q(d_ff_1_q), .reset(d_ff_6_q));  // open: Qn, preset, en
  D_Flip_Flop #(.trigger("rising"), .Pre_Clr_Positions("LEGACY"), .NegatePresetClear("false"), .enable("true"), .NewFFLayout("false")) d_ff_2 (
    .clk(IR5), .D(1'b1), .Q(d_ff_2_q), .reset(d_ff_7_q));  // open: Qn, preset, en
  D_Flip_Flop #(.trigger("rising"), .Pre_Clr_Positions("LEGACY"), .NegatePresetClear("false"), .enable("true"), .NewFFLayout("false")) d_ff_3 (
    .clk(IR10), .D(1'b1), .Q(d_ff_3_q), .reset(d_ff_8_q));  // open: Qn, preset, en
  D_Flip_Flop #(.trigger("rising"), .Pre_Clr_Positions("LEGACY"), .NegatePresetClear("false"), .enable("true"), .NewFFLayout("false")) d_ff_4 (
    .clk(IR15), .D(1'b1), .Q(d_ff_4_q), .reset(d_ff_9_q));  // open: Qn, preset, en
  D_Flip_Flop #(.trigger("rising"), .Pre_Clr_Positions("LEGACY"), .NegatePresetClear("false"), .enable("true"), .NewFFLayout("false")) d_ff_5 (
    .clk(IR20), .D(1'b1), .Q(d_ff_5_q), .reset(d_ff_10_q));  // open: Qn, preset, en
  Hex_Digit_Display hex_digit_display_4 (.value(LedData[19:16]));  // open: dp
  Hex_Digit_Display hex_digit_display_5 (.value(LedData[15:12]));  // open: dp
  and and_14 (and_14_out, not_15_out, W1);
  and and_15 (and_15_out, not_16_out, W3);
  and and_16 (and_16_out, not_17_out, W5);
  and and_17 (and_17_out, not_18_out, W7);
  and and_18 (and_18_out, not_19_out, W9);
  and and_19 (and_19_out, not_20_out, W11);
  and and_20 (and_20_out, not_21_out, W13);
  and and_21 (and_21_out, not_22_out, W15);
  and and_22 (and_22_out, not_23_out, W17);
  and and_23 (and_23_out, not_24_out, W19);
  and and_24 (and_24_out, not_25_out, W21);
  and and_25 (and_25_out, not_26_out, W23);
  or or_6 (or_6_out, d_ff_1_q, d_ff_6_q);
  or or_7 (or_7_out, d_ff_2_q, d_ff_7_q);
  or or_8 (or_8_out, d_ff_3_q, d_ff_8_q);
  or or_9 (or_9_out, d_ff_4_q, d_ff_9_q);
  or or_10 (or_10_out, d_ff_5_q, d_ff_10_q);
  Hex_Digit_Display hex_digit_display_6 (.value(LedData[11:8]));  // open: dp
  Hex_Digit_Display hex_digit_display_7 (.value(LedData[7:4]));  // open: dp
  // Probe on \总周期数 
  and and_26 (and_26_out, or_6_out, ~URET0);  // AND_Gate
  and and_27 (and_27_out, or_7_out, ~URET5);  // AND_Gate
  and and_28 (and_28_out, or_8_out, ~URET10);  // AND_Gate
  and and_29 (and_29_out, or_9_out, ~URET15);  // AND_Gate
  and and_30 (and_30_out, or_10_out, ~URET20);  // AND_Gate
  Hex_Digit_Display hex_digit_display_8 (.value(LedData[3:0]));  // open: dp
  D_Flip_Flop #(.trigger("rising"), .Pre_Clr_Positions("LEGACY"), .NegatePresetClear("false"), .enable("true"), .NewFFLayout("false")) d_ff_6 (
    .clk(CLK), .D(and_26_out), .Q(d_ff_6_q));  // open: Qn, preset, en, reset
  D_Flip_Flop #(.trigger("rising"), .Pre_Clr_Positions("LEGACY"), .NegatePresetClear("false"), .enable("true"), .NewFFLayout("false")) d_ff_7 (
    .clk(CLK), .D(and_27_out), .Q(d_ff_7_q));  // open: Qn, preset, en, reset
  D_Flip_Flop #(.trigger("rising"), .Pre_Clr_Positions("LEGACY"), .NegatePresetClear("false"), .enable("true"), .NewFFLayout("false")) d_ff_8 (
    .clk(CLK), .D(and_28_out), .Q(d_ff_8_q));  // open: Qn, preset, en, reset
  D_Flip_Flop #(.trigger("rising"), .Pre_Clr_Positions("LEGACY"), .NegatePresetClear("false"), .enable("true"), .NewFFLayout("false")) d_ff_9 (
    .clk(CLK), .D(and_29_out), .Q(d_ff_9_q));  // open: Qn, preset, en, reset
  D_Flip_Flop #(.trigger("rising"), .Pre_Clr_Positions("LEGACY"), .NegatePresetClear("false"), .enable("true"), .NewFFLayout("false")) d_ff_10 (
    .clk(CLK), .D(and_30_out), .Q(d_ff_10_q));  // open: Qn, preset, en, reset
  not not_27 (not_27_out, halt);
  or or_11 (or_11_out, not_27_out, Go);
  Counter #(.width(16), .max('hffff), .ongoal("wrap"), .trigger("rising"), .behavior("new")) counter_1 (
    .count(or_11_out), .Q(\总周期数 ), .clk(CLK), .clr(RST));  // open: load, D, carry, preset, down
  Priority_Encoder #(.select(5), .disabled("Z")) priority_encoder_1 (
    .in0(1'b1), .in1(and_1_out), .in2(and_14_out), .in3(and_2_out), .in4(and_15_out), .in5(and_3_out),
    .in6(and_16_out), .in7(and_4_out), .in8(and_17_out), .in9(and_5_out), .in10(and_18_out),
    .in11(and_6_out), .in12(and_19_out), .in13(and_7_out), .in14(and_20_out), .in15(and_8_out),
    .in16(and_21_out), .in17(and_9_out), .in18(and_22_out), .in19(and_10_out), .in20(and_23_out),
    .in21(and_11_out), .in22(and_24_out), .in23(and_12_out), .in24(and_25_out), .in25(and_13_out),
    .out(priority_encoder_1_out));  // open: in26, in27, in28, in29, in30, in31, gs, en_out, en_in
  or or_12 (W1, d_ff_16_q, d_ff_11_q);
  Multiplexer #(.select(5), .width(32), .disabled("Z"), .enable("false")) multiplexer_1 (
    .in0(EPC_IN), .in1(32'h6a0), .in2(32'h6c4), .in3(32'h6e8), .in4(32'h70c), .in5(32'h730), .in6(32'h754),
    .in7(32'h778), .in8(32'h79c), .in9(32'h7c0), .in10(32'h7e4), .in11(32'h808), .in12(32'h82c),
    .in13(32'h858), .in14(32'h884), .in15(32'h8b0), .in16(32'h8dc), .in17(32'h908), .in18(32'h934),
    .in19(32'h960), .in20(32'h98c), .in21(32'h9b8), .in22(32'h9e4), .in23(32'ha10), .in24(32'ha3c),
    .in25(32'ha68), .out(multiplexer_1_out), .sel(priority_encoder_1_out));  // open: in26, in27, in28, in29, in30, in31
  D_Flip_Flop #(.trigger("rising"), .Pre_Clr_Positions("LEGACY"), .NegatePresetClear("false"), .enable("true"), .NewFFLayout("false")) d_ff_11 (
    .clk(IR1), .D(1'b1), .Q(d_ff_11_q), .reset(d_ff_16_q));  // open: Qn, preset, en
  D_Flip_Flop #(.trigger("rising"), .Pre_Clr_Positions("LEGACY"), .NegatePresetClear("false"), .enable("true"), .NewFFLayout("false")) d_ff_12 (
    .clk(IR6), .D(1'b1), .Q(d_ff_12_q), .reset(d_ff_17_q));  // open: Qn, preset, en
  or or_13 (W6, d_ff_17_q, d_ff_12_q);
  D_Flip_Flop #(.trigger("rising"), .Pre_Clr_Positions("LEGACY"), .NegatePresetClear("false"), .enable("true"), .NewFFLayout("false")) d_ff_13 (
    .clk(IR11), .D(1'b1), .Q(d_ff_13_q), .reset(d_ff_18_q));  // open: Qn, preset, en
  or or_14 (W11, d_ff_18_q, d_ff_13_q);
  D_Flip_Flop #(.trigger("rising"), .Pre_Clr_Positions("LEGACY"), .NegatePresetClear("false"), .enable("true"), .NewFFLayout("false")) d_ff_14 (
    .clk(IR16), .D(1'b1), .Q(d_ff_14_q), .reset(d_ff_19_q));  // open: Qn, preset, en
  or or_15 (W16, d_ff_19_q, d_ff_14_q);
  D_Flip_Flop #(.trigger("rising"), .Pre_Clr_Positions("LEGACY"), .NegatePresetClear("false"), .enable("true"), .NewFFLayout("false")) d_ff_15 (
    .clk(IR21), .D(1'b1), .Q(d_ff_15_q), .reset(d_ff_20_q));  // open: Qn, preset, en
  or or_16 (W21, d_ff_20_q, d_ff_15_q);
  or or_17 (or_17_out, not_28_out, Go);
  not not_28 (not_28_out, halt);
  Multiplexer #(.select(1), .width(32), .disabled("Z"), .enable("false")) multiplexer_2 (
    .in0(multiplexer_1_out), .in1(EPC), .out(multiplexer_2_out), .sel(URET));
  or or_18 (or_18_out, d_ff_11_q, d_ff_16_q);
  or or_19 (or_19_out, d_ff_12_q, d_ff_17_q);
  Register #(.width(32), .trigger("rising"), .Select("low")) u_PC (
    .D(multiplexer_2_out), .en(or_17_out), .Q(PC), .clk(CLK), .clr(RST));
  and and_31 (and_31_out, or_18_out, ~URET1);  // AND_Gate
  and and_32 (and_32_out, or_19_out, ~URET6);  // AND_Gate
  or or_20 (or_20_out, d_ff_13_q, d_ff_18_q);
  and and_33 (and_33_out, or_20_out, ~URET11);  // AND_Gate
  or or_21 (or_21_out, d_ff_14_q, d_ff_19_q);
  and and_34 (and_34_out, or_21_out, ~URET16);  // AND_Gate
  or or_22 (or_22_out, d_ff_15_q, d_ff_20_q);
  and and_35 (and_35_out, or_22_out, ~URET21);  // AND_Gate
  Button button_1 (.out(IR0));
  Button button_2 (.out(IR5));
  Button button_3 (.out(IR10));
  Button button_4 (.out(IR15));
  Button button_5 (.out(IR20));
  D_Flip_Flop #(.trigger("rising"), .Pre_Clr_Positions("LEGACY"), .NegatePresetClear("false"), .enable("true"), .NewFFLayout("false")) d_ff_16 (
    .clk(CLK), .D(and_31_out), .Q(d_ff_16_q));  // open: Qn, preset, en, reset
  D_Flip_Flop #(.trigger("rising"), .Pre_Clr_Positions("LEGACY"), .NegatePresetClear("false"), .enable("true"), .NewFFLayout("false")) d_ff_17 (
    .clk(CLK), .D(and_32_out), .Q(d_ff_17_q));  // open: Qn, preset, en, reset
  D_Flip_Flop #(.trigger("rising"), .Pre_Clr_Positions("LEGACY"), .NegatePresetClear("false"), .enable("true"), .NewFFLayout("false")) d_ff_18 (
    .clk(CLK), .D(and_33_out), .Q(d_ff_18_q));  // open: Qn, preset, en, reset
  D_Flip_Flop #(.trigger("rising"), .Pre_Clr_Positions("LEGACY"), .NegatePresetClear("false"), .enable("true"), .NewFFLayout("false")) d_ff_19 (
    .clk(CLK), .D(and_34_out), .Q(d_ff_19_q));  // open: Qn, preset, en, reset
  D_Flip_Flop #(.trigger("rising"), .Pre_Clr_Positions("LEGACY"), .NegatePresetClear("false"), .enable("true"), .NewFFLayout("false")) d_ff_20 (
    .clk(CLK), .D(and_35_out), .Q(d_ff_20_q));  // open: Qn, preset, en, reset
  // RiscV_Probe riscv_probe_1: pin names not known; wires that end beside it: PC[11:2], IR
  LED #(.active("true")) led_4 (.in(W0));
  LED #(.active("true")) led_5 (.in(W5));
  LED #(.active("true")) led_6 (.in(W10));
  LED #(.active("true")) led_7 (.in(W15));
  LED #(.active("true")) led_8 (.in(W20));
  ROM #(.addrWidth(10), .dataWidth(32), .Select("high")) rom_1 (.addr(PC[11:2]), .data(IR));
  Button button_6 (.out(IR1));
  Button button_7 (.out(IR6));
  Button button_8 (.out(IR11));
  Button button_9 (.out(IR16));
  Button button_10 (.out(IR21));
  Button \u_开始游戏  (.out(Go));
  LED #(.active("true")) led_9 (.in(W1));
  LED #(.active("true")) led_10 (.in(W6));
  LED #(.active("true")) led_11 (.in(W11));
  LED #(.active("true")) led_12 (.in(W16));
  LED #(.active("true")) led_13 (.in(W21));
  or or_23 (W2, d_ff_27_q, d_ff_21_q);
  or or_24 (W7, d_ff_28_q, d_ff_22_q);
  or or_25 (W12, d_ff_29_q, d_ff_23_q);
  or or_26 (W17, d_ff_30_q, d_ff_24_q);
  or or_27 (W22, d_ff_31_q, d_ff_25_q);
  \单周期硬布线控制器  \u_单周期硬布线控制器_1  (
    .Funct({IR[30], IR[25], IR[14:12]}), .OP(IR[6:2]), .ALU_OP(\单周期硬布线控制器_1_alu_op ), .MemToReg(MemToReg),
    .MemWrite(MemWrite), .ALU_SRC(AluSrcB), .RegWrite(RegWrite), .ecall(ecall), .S_type(S_type), .Jalr(JALR),
    .Beq(\单周期硬布线控制器_1_beq ), .JAL(JAL), .Bne(\单周期硬布线控制器_1_bne ), .in_3(IR[21]), .uret(URET), .BGEU(BGEU));
  Multiplexer #(.select(1), .width(5), .disabled("Z"), .enable("false")) multiplexer_3 (
    .in0(IR[19:15]), .in1(5'b10001), .out(multiplexer_3_out), .sel(ecall));
  Multiplexer #(.select(1), .width(5), .disabled("Z"), .enable("false")) multiplexer_4 (
    .in0(IR[24:20]), .in1(5'b01010), .out(multiplexer_4_out), .sel(ecall));
  Multiplexer #(.select(1), .width(12), .disabled("Z"), .enable("false")) multiplexer_5 (
    .in0(IR[31:20]), .in1({IR[31:25], IR[11:7]}), .out(multiplexer_5_out), .sel(S_type));
  assign bit_extender_1_out = {{20{IR[31]}}, {IR[31], IR[7], IR[30:25], IR[11:8]}};  // Bit_Extender bit_extender_1
  assign bit_extender_2_out = {{12{IR[31]}}, {IR[31], IR[19:12], IR[20], IR[30:21]}};  // Bit_Extender bit_extender_2
  Button button_11 (.out(IR2));
  Button button_12 (.out(IR7));
  Button button_13 (.out(IR12));
  Button button_14 (.out(IR17));
  Button button_15 (.out(IR22));
  D_Flip_Flop #(.trigger("rising"), .Pre_Clr_Positions("LEGACY"), .NegatePresetClear("false"), .enable("true"), .NewFFLayout("false")) d_ff_21 (
    .clk(IR2), .D(1'b1), .Q(d_ff_21_q), .reset(d_ff_27_q));  // open: Qn, preset, en
  D_Flip_Flop #(.trigger("rising"), .Pre_Clr_Positions("LEGACY"), .NegatePresetClear("false"), .enable("true"), .NewFFLayout("false")) d_ff_22 (
    .clk(IR7), .D(1'b1), .Q(d_ff_22_q), .reset(d_ff_28_q));  // open: Qn, preset, en
  D_Flip_Flop #(.trigger("rising"), .Pre_Clr_Positions("LEGACY"), .NegatePresetClear("false"), .enable("true"), .NewFFLayout("false")) d_ff_23 (
    .clk(IR12), .D(1'b1), .Q(d_ff_23_q), .reset(d_ff_29_q));  // open: Qn, preset, en
  D_Flip_Flop #(.trigger("rising"), .Pre_Clr_Positions("LEGACY"), .NegatePresetClear("false"), .enable("true"), .NewFFLayout("false")) d_ff_24 (
    .clk(IR17), .D(1'b1), .Q(d_ff_24_q), .reset(d_ff_30_q));  // open: Qn, preset, en
  D_Flip_Flop #(.trigger("rising"), .Pre_Clr_Positions("LEGACY"), .NegatePresetClear("false"), .enable("true"), .NewFFLayout("false")) d_ff_25 (
    .clk(IR22), .D(1'b1), .Q(d_ff_25_q), .reset(d_ff_31_q));  // open: Qn, preset, en
  assign bit_extender_3_out = {{20{multiplexer_5_out[11]}}, multiplexer_5_out};  // Bit_Extender bit_extender_3
  Button button_16 (.out(IR3));
  LED #(.active("true")) led_14 (.in(W2));
  Button button_17 (.out(IR8));
  LED #(.active("true")) led_15 (.in(W7));
  Button button_18 (.out(IR13));
  LED #(.active("true")) led_16 (.in(W12));
  Button button_19 (.out(IR18));
  LED #(.active("true")) led_17 (.in(W17));
  LED #(.active("true")) led_18 (.in(W22));
  Button button_20 (.out(IR23));
  or or_28 (or_28_out, d_ff_21_q, d_ff_27_q);
  and and_36 (and_36_out, or_28_out, ~URET2);  // AND_Gate
  or or_29 (or_29_out, d_ff_22_q, d_ff_28_q);
  and and_37 (and_37_out, or_29_out, ~URET7);  // AND_Gate
  or or_30 (or_30_out, d_ff_23_q, d_ff_29_q);
  or or_31 (or_31_out, d_ff_24_q, d_ff_30_q);
  or or_32 (or_32_out, d_ff_25_q, d_ff_31_q);
  D_Flip_Flop #(.trigger("high"), .Pre_Clr_Positions("LEGACY"), .NegatePresetClear("false"), .enable("true"), .NewFFLayout("false")) d_ff_26 (.Q(d_ff_26_q));  // open: clk, D, Qn, preset, en, reset
  // Probe on 13'hc
  and and_38 (and_38_out, equal, \单周期硬布线控制器_1_beq );
  not not_29 (not_29_out, equal);
  and and_39 (and_39_out, not_29_out, \单周期硬布线控制器_1_bne );
  not not_30 (not_30_out, CLK);
  Regifile regifile_1 (
    .Din(RDin), .Clk(not_30_out), .R1(regifile_1_r1), .R2(MDin), .WE(RegWrite), .W_num(IR[11:7]),
    .R1_num(multiplexer_3_out), .R2_num(multiplexer_4_out));
  Shifter #(.width(32), .shift("ll")) shifter_1 (.in(bit_extender_1_out), .\dist (5'b00001), .out(shifter_1_out));
  Shifter #(.width(32), .shift("ll")) shifter_2 (.in(bit_extender_2_out), .\dist (5'b00001), .out(shifter_2_out));
  D_Flip_Flop #(.trigger("rising"), .Pre_Clr_Positions("LEGACY"), .NegatePresetClear("false"), .enable("true"), .NewFFLayout("false")) d_ff_27 (
    .clk(CLK), .D(and_36_out), .Q(d_ff_27_q));  // open: Qn, preset, en, reset
  D_Flip_Flop #(.trigger("rising"), .Pre_Clr_Positions("LEGACY"), .NegatePresetClear("false"), .enable("true"), .NewFFLayout("false")) d_ff_28 (
    .clk(CLK), .D(and_37_out), .Q(d_ff_28_q));  // open: Qn, preset, en, reset
  and and_40 (and_40_out, or_30_out, ~URET12);  // AND_Gate
  and and_41 (and_41_out, or_31_out, ~URET17);  // AND_Gate
  and and_42 (and_42_out, or_32_out, ~URET22);  // AND_Gate
  Comparator #(.width(13), .mode("twosComplement")) comparator_1 (
    .a(CNT_num), .b(13'hc), .eq(comparator_1_eq), .lt(comparator_1_lt));  // open: gt
  Clock #(.highDuration(1), .lowDuration(1)) clock_1 (.out(clock_1_out));
  and and_43 (and_43_out, BGEU, GE);
  Multiplexer #(.select(1), .width(32), .disabled("Z"), .enable("false")) multiplexer_6 (
    .in0(MDin), .in1(bit_extender_3_out), .out(multiplexer_6_out), .sel(AluSrcB));
  Adder #(.width(32)) adder_1 (.a(shifter_1_out), .b(PC), .out(adder_1_out));  // open: cin, cout
  Adder #(.width(32)) adder_2 (.a(shifter_2_out), .b(PC), .out(adder_2_out));  // open: cin, cout
  LED #(.active("true")) led_19 (.in(W3));
  Button button_21 (.out(IR4));
  Button button_22 (.out(IR9));
  LED #(.active("true")) led_20 (.in(W8));
  LED #(.active("true")) led_21 (.in(W13));
  Button button_23 (.out(IR14));
  Button button_24 (.out(IR19));
  LED #(.active("true")) led_22 (.in(W18));
  Button button_25 (.out(IR24));
  LED #(.active("true")) led_23 (.in(W23));
  D_Flip_Flop #(.trigger("rising"), .Pre_Clr_Positions("LEGACY"), .NegatePresetClear("false"), .enable("true"), .NewFFLayout("false")) d_ff_29 (
    .clk(CLK), .D(and_40_out), .Q(d_ff_29_q));  // open: Qn, preset, en, reset
  D_Flip_Flop #(.trigger("rising"), .Pre_Clr_Positions("LEGACY"), .NegatePresetClear("false"), .enable("true"), .NewFFLayout("false")) d_ff_30 (
    .clk(CLK), .D(and_41_out), .Q(d_ff_30_q));  // open: Qn, preset, en, reset
  D_Flip_Flop #(.trigger("rising"), .Pre_Clr_Positions("LEGACY"), .NegatePresetClear("false"), .enable("true"), .NewFFLayout("false")) d_ff_31 (
    .clk(CLK), .D(and_42_out), .Q(d_ff_31_q));  // open: Qn, preset, en, reset
  Counter #(.width(13), .max('h1fff), .ongoal("stay"), .trigger("rising"), .behavior("old")) counter_2 (
    .count(comparator_1_lt), .Q(CNT_num), .clk(clock_1_out));  // open: load, D, carry, clr, preset
  or or_33 (tunnel1, and_38_out, and_39_out, and_43_out);
  ALU alu_1 (
    .X(regifile_1_r1), .Y(multiplexer_6_out), .AluOP(\单周期硬布线控制器_1_alu_op ), .Equal(equal),
    .Result(alu_1_result), .Result_2(alu_1_result_2), .out_4(GE));  // open: out_6
  Adder #(.width(32)) adder_3 (.a(PC), .b(32'h4), .out(adder_3_out));  // open: cin, cout
  LED #(.active("true")) led_24 (.in(W4));
  LED #(.active("true")) led_25 (.in(W9));
  LED #(.active("true")) led_26 (.in(W14));
  LED #(.active("true")) led_27 (.in(W19));
  LED #(.active("true")) led_28 (.in(W24));
  nand nand_1 (nand_1_out, d_ff_26_q, comparator_1_eq);
  Comparator #(.width(32), .mode("twosComplement")) comparator_2 (
    .a(32'h22), .b(regifile_1_r1), .eq(flag));  // open: gt, lt
  Multiplexer #(.select(1), .width(32), .disabled("Z"), .enable("false")) multiplexer_7 (
    .in0(alu_1_result), .in1(alu_1_result_2), .out(aluresult), .sel(comparator_3_eq));
  Multiplexer #(.select(1), .width(32), .disabled("Z"), .enable("false")) multiplexer_8 (
    .in0(adder_3_out), .in1(adder_1_out), .out(multiplexer_8_out), .sel(tunnel1));
  or or_34 (W3, d_ff_37_q, d_ff_32_q);
  or or_35 (W8, d_ff_38_q, d_ff_33_q);
  or or_36 (W13, d_ff_39_q, d_ff_34_q);
  or or_37 (W18, d_ff_40_q, d_ff_35_q);
  or or_38 (W23, d_ff_41_q, d_ff_36_q);
  assign CLK = nand_1_out ? clock_1_out : 1'bz;  // Controlled_Buffer controlled_buffer_1
  Pull_Resistor #(.pull(1)) pull_resistor_1 (.node(CLK));
  Comparator #(.width(4), .mode("twosComplement")) comparator_3 (
    .a(\单周期硬布线控制器_1_alu_op ), .b(4'b0100), .eq(comparator_3_eq));  // open: gt, lt
  Multiplexer #(.select(1), .width(32), .disabled("Z"), .enable("false")) multiplexer_9 (
    .in0(multiplexer_8_out), .in1(adder_2_out), .out(multiplexer_9_out), .sel(JAL));
  assign and_44_out = aluresult & 32'hfffffffe;  // AND_Gate and_44, 32 bits wide
  D_Flip_Flop #(.trigger("rising"), .Pre_Clr_Positions("LEGACY"), .NegatePresetClear("false"), .enable("true"), .NewFFLayout("false")) d_ff_32 (
    .clk(IR3), .D(1'b1), .Q(d_ff_32_q), .reset(d_ff_37_q));  // open: Qn, preset, en
  D_Flip_Flop #(.trigger("rising"), .Pre_Clr_Positions("LEGACY"), .NegatePresetClear("false"), .enable("true"), .NewFFLayout("false")) d_ff_33 (
    .clk(IR8), .D(1'b1), .Q(d_ff_33_q), .reset(d_ff_38_q));  // open: Qn, preset, en
  D_Flip_Flop #(.trigger("rising"), .Pre_Clr_Positions("LEGACY"), .NegatePresetClear("false"), .enable("true"), .NewFFLayout("false")) d_ff_34 (
    .clk(IR13), .D(1'b1), .Q(d_ff_34_q), .reset(d_ff_39_q));  // open: Qn, preset, en
  D_Flip_Flop #(.trigger("rising"), .Pre_Clr_Positions("LEGACY"), .NegatePresetClear("false"), .enable("true"), .NewFFLayout("false")) d_ff_35 (
    .clk(IR18), .D(1'b1), .Q(d_ff_35_q), .reset(d_ff_40_q));  // open: Qn, preset, en
  D_Flip_Flop #(.trigger("rising"), .Pre_Clr_Positions("LEGACY"), .NegatePresetClear("false"), .enable("true"), .NewFFLayout("false")) d_ff_36 (
    .clk(IR23), .D(1'b1), .Q(d_ff_36_q), .reset(d_ff_41_q));  // open: Qn, preset, en
  Multiplexer #(.select(1), .width(32), .disabled("Z"), .enable("false")) multiplexer_10 (
    .in0(multiplexer_9_out), .in1(and_44_out), .out(EPC_IN), .sel(JALR));
  or or_39 (or_39_out, d_ff_32_q, d_ff_37_q);
  and and_45 (and_45_out, or_39_out, ~URET3);  // AND_Gate
  or or_40 (or_40_out, d_ff_33_q, d_ff_38_q);
  or or_41 (or_41_out, d_ff_34_q, d_ff_39_q);
  or or_42 (or_42_out, d_ff_35_q, d_ff_40_q);
  or or_43 (or_43_out, d_ff_36_q, d_ff_41_q);
  not not_31 (not_31_out, MemWrite);
  Multiplexer #(.select(1), .width(32), .disabled("Z"), .enable("false")) multiplexer_11 (
    .in0({32{1'b0}}), .in1(MDin), .out(multiplexer_11_out), .sel(and_46_out));
  and and_46 (and_46_out, ecall, flag);
  Comparator #(.width(5), .mode("unsigned")) comparator_4 (
    .a(IR[11:7]), .b(5'b00101), .eq(comparator_4_eq));  // open: gt, lt
  Comparator #(.width(5), .mode("unsigned")) comparator_5 (
    .a(IR[11:7]), .b(5'b00110), .eq(comparator_5_eq));  // open: gt, lt
  D_Flip_Flop #(.trigger("rising"), .Pre_Clr_Positions("LEGACY"), .NegatePresetClear("false"), .enable("true"), .NewFFLayout("false")) d_ff_37 (
    .clk(CLK), .D(and_45_out), .Q(d_ff_37_q));  // open: Qn, preset, en, reset
  and and_47 (and_47_out, or_40_out, ~URET8);  // AND_Gate
  and and_48 (and_48_out, or_41_out, ~URET13);  // AND_Gate
  and and_49 (and_49_out, or_42_out, ~URET18);  // AND_Gate
  and and_50 (and_50_out, or_43_out, ~URET23);  // AND_Gate
  RAM #(.addrWidth(10), .dataWidth(32), .bus("separate"), .Select("high")) ram_1 (
    .addr(aluresult[11:2]), .din(MDin), .data(ram_1_data), .str(MemWrite), .clk(CLK), .ld(not_31_out));  // open: sel, clr
  Register #(.width(32), .trigger("rising"), .Select("low")) register_2 (
    .D(multiplexer_11_out), .en(and_46_out), .Q(LedData), .clk(CLK), .clr(RST));
  not not_32 (not_32_out, flag);
  or or_44 (or_44_out, comparator_4_eq, comparator_5_eq);
  D_Flip_Flop #(.trigger("rising"), .Pre_Clr_Positions("LEGACY"), .NegatePresetClear("false"), .enable("true"), .NewFFLayout("false")) d_ff_38 (
    .clk(CLK), .D(and_47_out), .Q(d_ff_38_q));  // open: Qn, preset, en, reset
  D_Flip_Flop #(.trigger("rising"), .Pre_Clr_Positions("LEGACY"), .NegatePresetClear("false"), .enable("true"), .NewFFLayout("false")) d_ff_39 (
    .clk(CLK), .D(and_48_out), .Q(d_ff_39_q));  // open: Qn, preset, en, reset
  D_Flip_Flop #(.trigger("rising"), .Pre_Clr_Positions("LEGACY"), .NegatePresetClear("false"), .enable("true"), .NewFFLayout("false")) d_ff_40 (
    .clk(CLK), .D(and_49_out), .Q(d_ff_40_q));  // open: Qn, preset, en, reset
  D_Flip_Flop #(.trigger("rising"), .Pre_Clr_Positions("LEGACY"), .NegatePresetClear("false"), .enable("true"), .NewFFLayout("false")) d_ff_41 (
    .clk(CLK), .D(and_50_out), .Q(d_ff_41_q));  // open: Qn, preset, en, reset
  assign bit_extender_4_out = {{16{1'b0}}, ram_1_data[15:0]};  // Bit_Extender bit_extender_4
  assign bit_extender_5_out = {{16{1'b0}}, ram_1_data[31:16]};  // Bit_Extender bit_extender_5
  and and_51 (halt, ecall, not_32_out);
  and and_52 (and_52_out, RegWrite, or_44_out);
  and and_53 (and_53_out, comparator_4_eq, RegWrite);
  and and_54 (and_54_out, comparator_5_eq, RegWrite);
  Comparator #(.width(3), .mode("twosComplement")) comparator_6 (
    .a(IR[14:12]), .b(3'b101), .eq(comparator_6_eq));  // open: gt, lt
  not not_33 (not_33_out, comparator_6_eq);
  Multiplexer #(.select(1), .width(32), .disabled("Z"), .enable("false")) multiplexer_12 (
    .in0(bit_extender_4_out), .in1(bit_extender_5_out), .out(multiplexer_12_out), .sel(aluresult[1]));
  Register #(.width(7), .trigger("rising"), .Select("low")) register_3 (
    .D(RDin[6:0]), .en(and_53_out), .Q(register_3_q), .clk(CLK));  // open: clr
  Register #(.width(7), .trigger("rising"), .Select("low")) register_4 (
    .D(RDin[6:0]), .en(and_54_out), .Q(register_4_q), .clk(CLK));  // open: clr
  or or_45 (W4, d_ff_47_q, d_ff_42_q);
  or or_46 (W9, d_ff_48_q, d_ff_43_q);
  or or_47 (W14, d_ff_49_q, d_ff_44_q);
  or or_48 (W19, d_ff_50_q, d_ff_45_q);
  or or_49 (W24, d_ff_51_q, d_ff_46_q);
  Multiplexer #(.select(1), .width(32), .disabled("Z"), .enable("false")) multiplexer_13 (
    .in0(aluresult), .in1(multiplexer_14_out), .out(multiplexer_13_out), .sel(MemToReg));
  Multiplexer #(.select(1), .width(32), .disabled("Z"), .enable("false")) multiplexer_14 (
    .in0(multiplexer_12_out), .in1(ram_1_data), .out(multiplexer_14_out), .sel(not_33_out));
  Adder #(.width(32)) adder_4 (.a(PC), .b(32'h4), .out(adder_4_out));  // open: cin, cout
  D_Flip_Flop #(.trigger("rising"), .Pre_Clr_Positions("LEGACY"), .NegatePresetClear("false"), .enable("true"), .NewFFLayout("false")) d_ff_42 (
    .clk(IR4), .D(1'b1), .Q(d_ff_42_q), .reset(d_ff_47_q));  // open: Qn, preset, en
  D_Flip_Flop #(.trigger("rising"), .Pre_Clr_Positions("LEGACY"), .NegatePresetClear("false"), .enable("true"), .NewFFLayout("false")) d_ff_43 (
    .clk(IR9), .D(1'b1), .Q(d_ff_43_q), .reset(d_ff_48_q));  // open: Qn, preset, en
  D_Flip_Flop #(.trigger("rising"), .Pre_Clr_Positions("LEGACY"), .NegatePresetClear("false"), .enable("true"), .NewFFLayout("false")) d_ff_44 (
    .clk(IR14), .D(1'b1), .Q(d_ff_44_q), .reset(d_ff_49_q));  // open: Qn, preset, en
  D_Flip_Flop #(.trigger("rising"), .Pre_Clr_Positions("LEGACY"), .NegatePresetClear("false"), .enable("true"), .NewFFLayout("false")) d_ff_45 (
    .clk(IR19), .D(1'b1), .Q(d_ff_45_q), .reset(d_ff_50_q));  // open: Qn, preset, en
  D_Flip_Flop #(.trigger("rising"), .Pre_Clr_Positions("LEGACY"), .NegatePresetClear("false"), .enable("true"), .NewFFLayout("false")) d_ff_46 (
    .clk(IR24), .D(1'b1), .Q(d_ff_46_q), .reset(d_ff_51_q));  // open: Qn, preset, en
  Multiplexer #(.select(1), .width(32), .disabled("Z"), .enable("false")) multiplexer_15 (
    .in0(multiplexer_13_out), .in1(adder_4_out), .out(RDin), .sel(or_55_out));
  // LCD_Video lcd_video_1: pin names not known; wires that end beside it: RST, CLK, and_52_out, register_3_q, register_4_q, 16'hff00
  or or_50 (or_50_out, d_ff_42_q, d_ff_47_q);
  or or_51 (or_51_out, d_ff_43_q, d_ff_48_q);
  or or_52 (or_52_out, d_ff_44_q, d_ff_49_q);
  or or_53 (or_53_out, d_ff_45_q, d_ff_50_q);
  or or_54 (or_54_out, d_ff_46_q, d_ff_51_q);
  or or_55 (or_55_out, JALR, JAL);
  and and_55 (and_55_out, or_50_out, ~URET4);  // AND_Gate
  and and_56 (and_56_out, or_51_out, ~URET9);  // AND_Gate
  and and_57 (and_57_out, or_52_out, ~URET14);  // AND_Gate
  and and_58 (and_58_out, or_53_out, ~URET19);  // AND_Gate
  and and_59 (and_59_out, or_54_out, ~URET24);  // AND_Gate
  D_Flip_Flop #(.trigger("rising"), .Pre_Clr_Positions("LEGACY"), .NegatePresetClear("false"), .enable("true"), .NewFFLayout("false")) d_ff_47 (
    .clk(CLK), .D(and_55_out), .Q(d_ff_47_q));  // open: Qn, preset, en, reset
  D_Flip_Flop #(.trigger("rising"), .Pre_Clr_Positions("LEGACY"), .NegatePresetClear("false"), .enable("true"), .NewFFLayout("false")) d_ff_48 (
    .clk(CLK), .D(and_56_out), .Q(d_ff_48_q));  // open: Qn, preset, en, reset
  D_Flip_Flop #(.trigger("rising"), .Pre_Clr_Positions("LEGACY"), .NegatePresetClear("false"), .enable("true"), .NewFFLayout("false")) d_ff_49 (
    .clk(CLK), .D(and_57_out), .Q(d_ff_49_q));  // open: Qn, preset, en, reset
  D_Flip_Flop #(.trigger("rising"), .Pre_Clr_Positions("LEGACY"), .NegatePresetClear("false"), .enable("true"), .NewFFLayout("false")) d_ff_50 (
    .clk(CLK), .D(and_58_out), .Q(d_ff_50_q));  // open: Qn, preset, en, reset
  D_Flip_Flop #(.trigger("rising"), .Pre_Clr_Positions("LEGACY"), .NegatePresetClear("false"), .enable("true"), .NewFFLayout("false")) d_ff_51 (
    .clk(CLK), .D(and_59_out), .Q(d_ff_51_q));  // open: Qn, preset, en, reset
  _7_Segment_Display #(.active("true")) u_7_segment_display_1 (
    .g(register_8_q), .f(register_8_q), .a(register_8_q), .b(register_8_q), .e(register_8_q), .c(register_8_q));  // open: d, dp
  _7_Segment_Display #(.active("true")) u_7_segment_display_2 (
    .g(register_8_q), .f(register_8_q), .a(register_8_q), .e(register_8_q));  // open: b, d, c, dp
  Hex_Digit_Display hex_digit_display_9 (.value(register_5_q[7:4]), .dp(RST));
  Register #(.width(8), .trigger("rising"), .Select("low")) register_5 (
    .D(RDin[7:0]), .en(and_61_out), .Q(register_5_q), .clk(CLK));  // open: clr
  _7_Segment_Display #(.active("true")) u_7_segment_display_3 (
    .f(register_8_q), .e(register_8_q));  // open: g, a, b, d, c, dp
  _7_Segment_Display #(.active("true")) u_7_segment_display_4 (
    .f(register_8_q), .e(register_8_q), .d(register_8_q));  // open: g, a, b, c, dp
  Hex_Digit_Display hex_digit_display_10 (.value(register_5_q[3:0]), .dp(RST));
  count count_1 (.NUM(RDin), .SUM(count_1_sum));
  Register #(.width(8), .trigger("rising"), .Select("low")) register_6 (
    .D(count_1_sum), .en(and_60_out), .Q(register_6_q), .clk(CLK));  // open: clr
  Hex_Digit_Display hex_digit_display_11 (.value(register_6_q[3:0]), .dp(RST));
  Hex_Digit_Display hex_digit_display_12 (.value(register_6_q[7:4]), .dp(RST));
  Comparator #(.width(5), .mode("unsigned")) comparator_7 (
    .a(IR[11:7]), .b({5{1'b1}}), .eq(comparator_7_eq));  // open: gt, lt
  and and_60 (and_60_out, comparator_11_eq, RegWrite);
  and and_61 (and_61_out, RegWrite, comparator_10_eq);
  and and_62 (and_62_out, comparator_7_eq, RegWrite);
  Register #(.width(5), .trigger("rising"), .Select("low")) register_7 (
    .D(RDin[4:0]), .en(and_62_out), .Q(register_7_q), .clk(CLK));  // open: clr
  Comparator #(.width(32), .mode("unsigned")) comparator_8 (
    .a(RDin), .b({32{1'b0}}), .gt(comparator_8_gt));  // open: eq, lt
  Demultiplexer #(.select(5), .width(1), .tristate("false"), .disabled("Z"), .enable("false")) demultiplexer_1 (
    .out0(URET0), .out1(URET1), .out2(URET2), .out3(URET3), .out4(URET4), .out5(URET5), .out6(URET6),
    .out7(URET7), .out8(URET8), .out9(URET9), .out10(URET10), .out11(URET11), .out12(URET12), .out13(URET13),
    .out14(URET14), .out15(URET15), .out16(URET16), .out17(URET17), .out18(URET18), .out19(URET19),
    .out20(URET20), .out21(URET21), .out22(URET22), .out23(URET23), .out24(URET24), .in(URET),
    .sel(register_7_q));  // open: out25, out26, out27, out28, out29, out30, out31
  Comparator #(.width(5), .mode("unsigned")) comparator_9 (
    .a(IR[11:7]), .b(5'b11101), .eq(comparator_9_eq));  // open: gt, lt
  Comparator #(.width(5), .mode("unsigned")) comparator_10 (
    .a(IR[11:7]), .b(5'b11011), .eq(comparator_10_eq));  // open: gt, lt
  Comparator #(.width(5), .mode("unsigned")) comparator_11 (
    .a(IR[11:7]), .b(5'b01010), .eq(comparator_11_eq));  // open: gt, lt
  Register #(.width(1), .trigger("rising"), .Select("low")) register_8 (
    .D(1'b1), .en(and_63_out), .Q(register_8_q), .clk(CLK), .clr(RST));
  and and_63 (and_63_out, comparator_8_gt, comparator_9_eq, RegWrite);
  or or_56 (or_56_out, W0, W1, W2, W3, W4, W5, W6, W7, W8, W9, W10, W11, W12, W13, W14, W15, W16, W17, W18, W19, W20, W21, W22, W23, W24);
  Register #(.width(1), .trigger("rising"), .Select("low")) register_9 (
    .D(or_56_out), .Q(IE), .clk(CLK), .clr(URET));  // open: en

  // Other names for the same wires on the sheet: W[4:0] = IR[11:7]

  // Notes on the sheet:
  //   中断源
  //   中断等待指示
  //   总复位信号应将除ROM以外所有存储组件全部清零
  //   数码管输出
  //   数码管输出应该用寄存器锁存，否则显示数据只能一闪而过
  //   Reset 
  //   Reset 
  //   Reset 
  //   Reset 
  //   Reset 
  //   存储中断入口地址
  //   Reset 
  //   Reset 
  //   Reset 
  //   Reset 
  //   Reset 
  //   指令探针
  //   指令存储器
  //   为方便自动评测，需要输出PC，IR，寄存器堆写如数据RDin
  //   指令字
  //   contents of rom_1 (hex, n*v repeats v):
  //   100293 100313 7e00393 130313 fe731ee3 1a00293 100313 130313 fe731ee3 3300293 100313 130313 fe731ee3
  //   4c00293 100313 130313 fe731ee3 6500293 100313 130313 fe731ee3 7e00293 100313 130313 fe731ee3 100293
  //   100313 128293 fe729ee3 100293 1a00313 128293 fe729ee3 100293 3300313 128293 fe729ee3 100293 4c00313
  //   128293 fe729ee3 100293 6500313 128293 fe729ee3 100293 7e00313 128293 fe729ee3 893 73 393 593 513
  //   138393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
  //   RAM写使能MemWrite、RAM写入数据MDin等信号
  //   JAL
  //   JALR
  //   URET
  //   Beq
  //   Bne
  //   MemToReg
  //   MemWrite
  //   AluOP
  //   AluSrcB
  //   RegWrite
  //   控制位
  //   暂停节拍，不能为0
  //   Reset 
  //   Reset 
  //   Reset 
  //   Reset 
  //   Reset 
  //   戳工具置1进入计数暂停模式，ctrl+k时钟自动运行到对应节拍暂停
  //   ctrl+k关闭时钟连续运行，将控制位置零，进入单步调试模式调试
  //   可计数暂停的时钟源
  //   数据存储器
  //   Reset 
  //   Reset 
  //   Reset 
  //   Reset 
  //   Reset 
  //   Reset 
  //   Reset 
  //   Reset 
  //   Reset 
  //   Reset 
  //   已排除个数
  //   总个数
endmodule
module count (
  input  [31:0] NUM,
  output [7:0] SUM
);

  wire [7:0] adder_1_out, adder_2_out, adder_3_out, adder_4_out, adder_5_out, adder_6_out, adder_7_out,
       adder_8_out, adder_9_out, adder_10_out, adder_11_out, adder_12_out, adder_13_out, adder_14_out,
       adder_15_out, adder_16_out, adder_17_out, adder_18_out, adder_19_out, adder_20_out, adder_21_out,
       adder_22_out, adder_23_out, adder_24_out, bit_extender_1_out, bit_extender_2_out, bit_extender_3_out,
       bit_extender_4_out, bit_extender_5_out, bit_extender_6_out, bit_extender_7_out, bit_extender_8_out,
       bit_extender_9_out, bit_extender_10_out, bit_extender_11_out, bit_extender_12_out,
       bit_extender_13_out, bit_extender_14_out, bit_extender_15_out, bit_extender_16_out,
       bit_extender_17_out, bit_extender_18_out, bit_extender_19_out, bit_extender_20_out,
       bit_extender_21_out, bit_extender_22_out, bit_extender_23_out, bit_extender_24_out,
       bit_extender_25_out, not_1_out;

  assign bit_extender_1_out = {{7{1'b0}}, NUM[0]};  // Bit_Extender bit_extender_1
  assign bit_extender_2_out = {{7{1'b0}}, NUM[1]};  // Bit_Extender bit_extender_2
  assign bit_extender_3_out = {{7{1'b0}}, NUM[2]};  // Bit_Extender bit_extender_3
  assign bit_extender_4_out = {{7{1'b0}}, NUM[3]};  // Bit_Extender bit_extender_4
  assign bit_extender_5_out = {{7{1'b0}}, NUM[4]};  // Bit_Extender bit_extender_5
  assign bit_extender_6_out = {{7{1'b0}}, NUM[5]};  // Bit_Extender bit_extender_6
  assign bit_extender_7_out = {{7{1'b0}}, NUM[6]};  // Bit_Extender bit_extender_7
  assign bit_extender_8_out = {{7{1'b0}}, NUM[7]};  // Bit_Extender bit_extender_8
  assign bit_extender_9_out = {{7{1'b0}}, NUM[8]};  // Bit_Extender bit_extender_9
  assign bit_extender_10_out = {{7{1'b0}}, NUM[9]};  // Bit_Extender bit_extender_10
  assign bit_extender_11_out = {{7{1'b0}}, NUM[10]};  // Bit_Extender bit_extender_11
  assign bit_extender_12_out = {{7{1'b0}}, NUM[11]};  // Bit_Extender bit_extender_12
  assign bit_extender_13_out = {{7{1'b0}}, NUM[12]};  // Bit_Extender bit_extender_13
  assign bit_extender_14_out = {{7{1'b0}}, NUM[13]};  // Bit_Extender bit_extender_14
  assign bit_extender_15_out = {{7{1'b0}}, NUM[14]};  // Bit_Extender bit_extender_15
  assign bit_extender_16_out = {{7{1'b0}}, NUM[15]};  // Bit_Extender bit_extender_16
  assign bit_extender_17_out = {{7{1'b0}}, NUM[16]};  // Bit_Extender bit_extender_17
  assign bit_extender_18_out = {{7{1'b0}}, NUM[17]};  // Bit_Extender bit_extender_18
  assign bit_extender_19_out = {{7{1'b0}}, NUM[18]};  // Bit_Extender bit_extender_19
  assign bit_extender_20_out = {{7{1'b0}}, NUM[19]};  // Bit_Extender bit_extender_20
  assign bit_extender_21_out = {{7{1'b0}}, NUM[20]};  // Bit_Extender bit_extender_21
  assign bit_extender_22_out = {{7{1'b0}}, NUM[21]};  // Bit_Extender bit_extender_22
  assign bit_extender_23_out = {{7{1'b0}}, NUM[22]};  // Bit_Extender bit_extender_23
  assign bit_extender_24_out = {{7{1'b0}}, NUM[23]};  // Bit_Extender bit_extender_24
  assign bit_extender_25_out = {{7{1'b0}}, NUM[24]};  // Bit_Extender bit_extender_25
  Adder #(.width(8)) adder_1 (.a(bit_extender_1_out), .b(bit_extender_2_out), .out(adder_1_out));  // open: cin, cout
  Adder #(.width(8)) adder_2 (.a(bit_extender_3_out), .b(bit_extender_4_out), .out(adder_2_out));  // open: cin, cout
  Adder #(.width(8)) adder_3 (.a(bit_extender_5_out), .b(bit_extender_6_out), .out(adder_3_out));  // open: cin, cout
  Adder #(.width(8)) adder_4 (.a(bit_extender_7_out), .b(bit_extender_8_out), .out(adder_4_out));  // open: cin, cout
  Adder #(.width(8)) adder_5 (.a(bit_extender_9_out), .b(bit_extender_10_out), .out(adder_5_out));  // open: cin, cout
  Adder #(.width(8)) adder_6 (.a(bit_extender_11_out), .b(bit_extender_12_out), .out(adder_6_out));  // open: cin, cout
  Adder #(.width(8)) adder_7 (.a(bit_extender_13_out), .b(bit_extender_14_out), .out(adder_7_out));  // open: cin, cout
  Adder #(.width(8)) adder_8 (.a(bit_extender_15_out), .b(bit_extender_16_out), .out(adder_8_out));  // open: cin, cout
  Adder #(.width(8)) adder_9 (.a(bit_extender_17_out), .b(bit_extender_18_out), .out(adder_9_out));  // open: cin, cout
  Adder #(.width(8)) adder_10 (
    .a(bit_extender_19_out), .b(bit_extender_20_out), .out(adder_10_out));  // open: cin, cout
  Adder #(.width(8)) adder_11 (
    .a(bit_extender_21_out), .b(bit_extender_22_out), .out(adder_11_out));  // open: cin, cout
  Adder #(.width(8)) adder_12 (
    .a(bit_extender_23_out), .b(bit_extender_24_out), .out(adder_12_out));  // open: cin, cout
  Adder #(.width(8)) adder_13 (.a(adder_1_out), .b(adder_2_out), .out(adder_13_out));  // open: cin, cout
  Adder #(.width(8)) adder_14 (.a(adder_3_out), .b(adder_4_out), .out(adder_14_out));  // open: cin, cout
  Adder #(.width(8)) adder_15 (.a(adder_5_out), .b(adder_6_out), .out(adder_15_out));  // open: cin, cout
  Adder #(.width(8)) adder_16 (.a(adder_7_out), .b(adder_8_out), .out(adder_16_out));  // open: cin, cout
  Adder #(.width(8)) adder_17 (.a(adder_9_out), .b(adder_10_out), .out(adder_17_out));  // open: cin, cout
  Adder #(.width(8)) adder_18 (.a(adder_11_out), .b(adder_12_out), .out(adder_18_out));  // open: cin, cout
  Adder #(.width(8)) adder_19 (.a(adder_13_out), .b(adder_14_out), .out(adder_19_out));  // open: cin, cout
  Adder #(.width(8)) adder_20 (.a(adder_15_out), .b(adder_16_out), .out(adder_20_out));  // open: cin, cout
  Adder #(.width(8)) adder_21 (.a(adder_17_out), .b(adder_18_out), .out(adder_21_out));  // open: cin, cout
  Adder #(.width(8)) adder_22 (.a(adder_19_out), .b(adder_20_out), .out(adder_22_out));  // open: cin, cout
  Adder #(.width(8)) adder_23 (.a(adder_21_out), .b(bit_extender_25_out), .out(adder_23_out));  // open: cin, cout
  Adder #(.width(8)) adder_24 (.a(adder_22_out), .b(adder_23_out), .out(adder_24_out));  // open: cin, cout
  assign not_1_out = ~adder_24_out;  // NOT_Gate not_1, 8 bits wide
  Adder #(.width(8)) adder_25 (.a(not_1_out), .b(8'h1a), .out(SUM));  // open: cin, cout
endmodule

// ID/EX
module ID_EX4 (
  input  CLK,
  input  RST,
  input  JAL,
  input  JALR,
  input  BEQ,
  input  BNE,
  input  MEMTOREG,
  input  MEMWRITE,
  input  [3:0] ALUOP,
  input  ALUSRC,
  input  REGWRITE,
  input  ECALL,
  input  BGEU_IN,
  input  [31:0] R1,
  input  [31:0] R2,
  input  [4:0] W_num,
  input  [31:0] IMM,
  input  [31:0] B,
  input  predict_jump,
  input  [31:0] IR,
  input  [31:0] J,
  input  [31:0] PC,
  input  CLR,
  input  EN,
  output JAL_OUT,
  output JALR_OUT,
  output BEQ_OUT,
  output BNE_OUT,
  output MEMTOREG_OUT,
  output MEMWRITE_OUT,
  output [3:0] ALUOP_OUT,
  output ALUSRC_OUT,
  output REGWRITE_OUT,
  output ECALL_OUT,
  output BGEU_OUT,
  output [31:0] R1_OUT,
  output [31:0] R2_OUT,
  output [4:0] W__OUT,
  output [31:0] IMM_OUT,
  output [31:0] B_OUT,
  output predict_jump_out,
  output [31:0] IR_OUT,
  output [31:0] J_OUT,
  output [31:0] PC_OUT
);

  wire multiplexer_1_out, multiplexer_2_out, multiplexer_3_out, multiplexer_4_out, multiplexer_5_out,
       multiplexer_6_out, multiplexer_8_out, multiplexer_9_out, multiplexer_10_out, multiplexer_11_out,
       multiplexer_17_out;
  wire [3:0] multiplexer_7_out;
  wire [4:0] multiplexer_14_out;
  wire [31:0] multiplexer_12_out, multiplexer_13_out, multiplexer_15_out, multiplexer_16_out,
       multiplexer_18_out, multiplexer_19_out, multiplexer_20_out;

  Multiplexer #(.select(1), .width(1), .disabled("Z"), .enable("false")) multiplexer_1 (
    .in0(JAL), .in1(1'b0), .out(multiplexer_1_out), .sel(CLR));
  Multiplexer #(.select(1), .width(1), .disabled("Z"), .enable("false")) multiplexer_2 (
    .in0(JALR), .in1(1'b0), .out(multiplexer_2_out), .sel(CLR));
  Multiplexer #(.select(1), .width(1), .disabled("Z"), .enable("false")) multiplexer_3 (
    .in0(BEQ), .in1(1'b0), .out(multiplexer_3_out), .sel(CLR));
  Multiplexer #(.select(1), .width(1), .disabled("Z"), .enable("false")) multiplexer_4 (
    .in0(BNE), .in1(1'b0), .out(multiplexer_4_out), .sel(CLR));
  Multiplexer #(.select(1), .width(1), .disabled("Z"), .enable("false")) multiplexer_5 (
    .in0(MEMTOREG), .in1(1'b0), .out(multiplexer_5_out), .sel(CLR));
  Multiplexer #(.select(1), .width(1), .disabled("Z"), .enable("false")) multiplexer_6 (
    .in0(MEMWRITE), .in1(1'b0), .out(multiplexer_6_out), .sel(CLR));
  Multiplexer #(.select(1), .width(4), .disabled("Z"), .enable("false")) multiplexer_7 (
    .in0(ALUOP), .in1(4'b0000), .out(multiplexer_7_out), .sel(CLR));
  Multiplexer #(.select(1), .width(1), .disabled("Z"), .enable("false")) multiplexer_8 (
    .in0(ALUSRC), .in1(1'b0), .out(multiplexer_8_out), .sel(CLR));
  Multiplexer #(.select(1), .width(1), .disabled("Z"), .enable("false")) multiplexer_9 (
    .in0(REGWRITE), .in1(1'b0), .out(multiplexer_9_out), .sel(CLR));
  Multiplexer #(.select(1), .width(1), .disabled("Z"), .enable("false")) multiplexer_10 (
    .in0(ECALL), .in1(1'b0), .out(multiplexer_10_out), .sel(CLR));
  Multiplexer #(.select(1), .width(1), .disabled("Z"), .enable("false")) multiplexer_11 (
    .in0(BGEU_IN), .in1(1'b0), .out(multiplexer_11_out), .sel(CLR));
  Multiplexer #(.select(1), .width(32), .disabled("Z"), .enable("false")) multiplexer_12 (
    .in0(R1), .in1({32{1'b0}}), .out(multiplexer_12_out), .sel(CLR));
  Multiplexer #(.select(1), .width(32), .disabled("Z"), .enable("false")) multiplexer_13 (
    .in0(R2), .in1({32{1'b0}}), .out(multiplexer_13_out), .sel(CLR));
  Multiplexer #(.select(1), .width(5), .disabled("Z"), .enable("false")) multiplexer_14 (
    .in0(W_num), .in1({5{1'b0}}), .out(multiplexer_14_out), .sel(CLR));
  Multiplexer #(.select(1), .width(32), .disabled("Z"), .enable("false")) multiplexer_15 (
    .in0(IMM), .in1({32{1'b0}}), .out(multiplexer_15_out), .sel(CLR));
  Multiplexer #(.select(1), .width(32), .disabled("Z"), .enable("false")) multiplexer_16 (
    .in0(B), .in1({32{1'b0}}), .out(multiplexer_16_out), .sel(CLR));
  Multiplexer #(.select(1), .width(1), .disabled("Z"), .enable("false")) multiplexer_17 (
    .in0(predict_jump), .in1(1'b0), .out(multiplexer_17_out), .sel(CLR));
  Multiplexer #(.select(1), .width(32), .disabled("Z"), .enable("false")) multiplexer_18 (
    .in0(IR), .in1({32{1'b0}}), .out(multiplexer_18_out), .sel(CLR));
  Multiplexer #(.select(1), .width(32), .disabled("Z"), .enable("false")) multiplexer_19 (
    .in0(J), .in1({32{1'b0}}), .out(multiplexer_19_out), .sel(CLR));
  Multiplexer #(.select(1), .width(32), .disabled("Z"), .enable("false")) multiplexer_20 (
    .in0(PC), .in1({32{1'b0}}), .out(multiplexer_20_out), .sel(CLR));
  Register #(.width(1), .trigger("rising"), .Select("low")) register_1 (
    .D(multiplexer_1_out), .en(EN), .Q(JAL_OUT), .clk(CLK), .clr(RST));
  Register #(.width(1), .trigger("rising"), .Select("low")) register_2 (
    .D(multiplexer_2_out), .en(EN), .Q(JALR_OUT), .clk(CLK), .clr(RST));
  Register #(.width(1), .trigger("rising"), .Select("low")) register_3 (
    .D(multiplexer_3_out), .en(EN), .Q(BEQ_OUT), .clk(CLK), .clr(RST));
  Register #(.width(1), .trigger("rising"), .Select("low")) register_4 (
    .D(multiplexer_4_out), .en(EN), .Q(BNE_OUT), .clk(CLK), .clr(RST));
  Register #(.width(1), .trigger("rising"), .Select("low")) register_5 (
    .D(multiplexer_5_out), .en(EN), .Q(MEMTOREG_OUT), .clk(CLK), .clr(RST));
  Register #(.width(1), .trigger("rising"), .Select("low")) register_6 (
    .D(multiplexer_6_out), .en(EN), .Q(MEMWRITE_OUT), .clk(CLK), .clr(RST));
  Register #(.width(4), .trigger("rising"), .Select("low")) register_7 (
    .D(multiplexer_7_out), .en(EN), .Q(ALUOP_OUT), .clk(CLK), .clr(RST));
  Register #(.width(1), .trigger("rising"), .Select("low")) register_8 (
    .D(multiplexer_8_out), .en(EN), .Q(ALUSRC_OUT), .clk(CLK), .clr(RST));
  Register #(.width(1), .trigger("rising"), .Select("low")) register_9 (
    .D(multiplexer_9_out), .en(EN), .Q(REGWRITE_OUT), .clk(CLK), .clr(RST));
  Register #(.width(1), .trigger("rising"), .Select("low")) register_10 (
    .D(multiplexer_10_out), .en(EN), .Q(ECALL_OUT), .clk(CLK), .clr(RST));
  Register #(.width(1), .trigger("rising"), .Select("low")) register_11 (
    .D(multiplexer_11_out), .en(EN), .Q(BGEU_OUT), .clk(CLK), .clr(RST));
  Register #(.width(32), .trigger("rising"), .Select("low")) register_12 (
    .D(multiplexer_12_out), .en(EN), .Q(R1_OUT), .clk(CLK), .clr(RST));
  Register #(.width(32), .trigger("rising"), .Select("low")) register_13 (
    .D(multiplexer_13_out), .en(EN), .Q(R2_OUT), .clk(CLK), .clr(RST));
  Register #(.width(5), .trigger("rising"), .Select("low")) register_14 (
    .D(multiplexer_14_out), .en(EN), .Q(W__OUT), .clk(CLK), .clr(RST));
  Register #(.width(32), .trigger("rising"), .Select("low")) register_15 (
    .D(multiplexer_15_out), .en(EN), .Q(IMM_OUT), .clk(CLK), .clr(RST));
  Register #(.width(32), .trigger("rising"), .Select("low")) register_16 (
    .D(multiplexer_16_out), .en(EN), .Q(B_OUT), .clk(CLK), .clr(RST));
  Register #(.width(1), .trigger("rising"), .Select("low")) register_17 (
    .D(multiplexer_17_out), .en(EN), .Q(predict_jump_out), .clk(CLK), .clr(RST));
  Register #(.width(32), .trigger("rising"), .Select("low")) register_18 (
    .D(multiplexer_18_out), .en(EN), .Q(IR_OUT), .clk(CLK), .clr(RST));
  Register #(.width(32), .trigger("rising"), .Select("low")) register_19 (
    .D(multiplexer_19_out), .en(EN), .Q(J_OUT), .clk(CLK), .clr(RST));
  Register #(.width(32), .trigger("rising"), .Select("low")) register_20 (
    .D(multiplexer_20_out), .en(EN), .Q(PC_OUT), .clk(CLK), .clr(RST));
endmodule
