// Logisim project 新建 文本文档.circ as structural Verilog: 35 circuits, main circuit ◇单周期RISC-V
// 单周期硬布线控制器
module \单周期硬布线控制器  (
  input  [4:0] OP,
  input  [4:0] Funct,
  input  in_3,
  output [3:0] ALU_OP,
  output uret,
  output MemToReg,
  output ecall,
  output MemWrite,
  output ALU_SRC,
  output RegWrite,
  output S_type,
  output Beq,
  output Bne,
  output Jalr,
  output JAL,
  output sb,
  output auipc,
  output bltu,
  output sltiu,
  output rs1,
  output rs2,
  output CSRRSI,
  output CSRRCI
);

  wire \控制信号自动生成_1_ecall ;

  \运算控制器自动生成  \u_运算控制器自动生成_1  (
    .OP2(OP[0]), .OP3(OP[1]), .OP4(OP[2]), .OP5(OP[3]), .OP6(OP[4]), .F12(Funct[0]), .F13(Funct[1]),
    .F14(Funct[2]), .F25(Funct[3]), .F30(Funct[4]), .S0(ALU_OP[0]), .S1(ALU_OP[1]), .S2(ALU_OP[2]),
    .S3(ALU_OP[3]));
  \控制信号自动生成  \u_控制信号自动生成_1  (
    .OP2(OP[0]), .OP3(OP[1]), .MemToReg(MemToReg), .OP4(OP[2]), .OP5(OP[3]), .OP6(OP[4]), .F12(Funct[0]),
    .F13(Funct[1]), .F14(Funct[2]), .MemWrite(MemWrite), .F25(Funct[3]), .F30(Funct[4]), .ALU_SRC(ALU_SRC),
    .RegWrite(RegWrite), .ecall(\控制信号自动生成_1_ecall ), .S_Type(S_type), .BEQ(Beq), .BNE(Bne), .JALR(Jalr),
    .JAL(JAL), .sb(sb), .auipc(auipc), .bltu(bltu), .sltiu(sltiu), .rs1(rs1), .rs2(rs2), .CSRRSI(CSRRSI),
    .CSRRCI(CSRRCI));
  and and_1 (uret, in_3, \控制信号自动生成_1_ecall );
  and and_2 (ecall, ~in_3, \控制信号自动生成_1_ecall );  // AND_Gate

  // Other names for the same wires on the sheet: IR21 = in_3; OP_CODE[4:0] = OP

  // Notes on the sheet:
  //   运算器控制器，根据指令生成运算器功能选择信号
  //   控制信号生成，产生数据通路需要的其他控制信号
endmodule

// 运算器控制器
module \运算控制器自动生成  (
  input  OP2,
  input  OP3,
  input  OP4,
  input  OP5,
  input  OP6,
  input  F12,
  input  F13,
  input  F14,
  input  F25,
  input  F30,
  output S0,
  output S1,
  output S2,
  output S3
);

  wire and_1_out, and_2_out, and_3_out, and_4_out, and_5_out, and_6_out, and_7_out, and_8_out, and_9_out,
       and_10_out, and_11_out, and_12_out, and_13_out, and_14_out, and_15_out, and_16_out, and_17_out,
       and_18_out, and_19_out, and_20_out, and_21_out, and_22_out, and_23_out, and_24_out, and_25_out,
       and_26_out, and_27_out, and_28_out, and_29_out, and_30_out, and_31_out, and_32_out, and_33_out,
       and_34_out, and_35_out, and_36_out, and_37_out, and_38_out, and_39_out, and_40_out, and_41_out,
       and_42_out, and_43_out, and_44_out, and_45_out, and_46_out, and_47_out, not_1_out, not_2_out,
       not_3_out, not_4_out, not_5_out, not_6_out, not_7_out, not_8_out, not_9_out, not_10_out, not_11_out,
       not_12_out, not_13_out, not_14_out, not_15_out, not_16_out, not_17_out, not_18_out, not_19_out,
       not_20_out, not_21_out, not_22_out, not_23_out, not_24_out, not_25_out, not_26_out, not_27_out,
       not_28_out, not_29_out, not_30_out, not_31_out, not_32_out, not_33_out, not_34_out, not_35_out,
       not_36_out, not_37_out, not_38_out, not_39_out, not_40_out, not_41_out, not_42_out, not_43_out,
       not_44_out, not_45_out, not_46_out, not_47_out, not_48_out, not_49_out, not_50_out, not_51_out,
       not_52_out, not_53_out, not_54_out, not_55_out, not_56_out, not_57_out, not_58_out, not_59_out,
       not_60_out, not_61_out, not_62_out, not_63_out, not_64_out, not_65_out, not_66_out, not_67_out,
       not_68_out, not_69_out, not_70_out, not_71_out, not_72_out, not_73_out, not_74_out, not_75_out,
       not_76_out, not_77_out, not_78_out, not_79_out, not_80_out, not_81_out, not_82_out, not_83_out,
       not_84_out, not_85_out, not_86_out, not_87_out, not_88_out, not_89_out, not_90_out, not_91_out,
       not_92_out, not_93_out, not_94_out, not_95_out, not_96_out, not_97_out, not_98_out, not_99_out,
       not_100_out, not_101_out, not_102_out, not_103_out, not_104_out, not_105_out, not_106_out,
       not_107_out, not_108_out, not_109_out, not_110_out, not_111_out, not_112_out, not_113_out,
       not_114_out, not_115_out, not_116_out, not_117_out, not_118_out, not_119_out, not_120_out,
       not_121_out, not_122_out, not_123_out, not_124_out, not_125_out, not_126_out, not_127_out,
       not_128_out, not_129_out, not_130_out, not_131_out, not_132_out, not_133_out, not_134_out,
       not_135_out, not_136_out, not_137_out, not_138_out, not_139_out, not_140_out, not_141_out,
       not_142_out, not_143_out, not_144_out, not_145_out, not_146_out, not_147_out, not_148_out,
       not_149_out, not_150_out, not_151_out, not_152_out, not_153_out, not_154_out, not_155_out,
       not_156_out, not_157_out, not_158_out, not_159_out, not_160_out, not_161_out, not_162_out,
       not_163_out, not_164_out, not_165_out, not_166_out, not_167_out, not_168_out, not_169_out,
       not_170_out, not_171_out, not_172_out, not_173_out, not_174_out, not_175_out, not_176_out,
       not_177_out, not_178_out, not_179_out, not_180_out, not_181_out, not_182_out, not_183_out,
       not_184_out, not_185_out, not_186_out, not_187_out, not_188_out, not_189_out, not_190_out,
       not_191_out, not_192_out, not_193_out, not_194_out, not_195_out, not_196_out, not_197_out,
       not_198_out, not_199_out, not_200_out, not_201_out, not_202_out, not_203_out, not_204_out,
       not_205_out, not_206_out, not_207_out, not_208_out, not_209_out, not_210_out, not_211_out,
       not_212_out, not_213_out, not_214_out, not_215_out, not_216_out, not_217_out, not_218_out,
       not_219_out, not_220_out, not_221_out, not_222_out, not_223_out, not_224_out, not_225_out,
       not_226_out, not_227_out, not_228_out, not_229_out, not_230_out, not_231_out, not_232_out,
       not_233_out, not_234_out, not_235_out, not_236_out, not_237_out, not_238_out, not_239_out,
       not_240_out, not_241_out, not_242_out, not_243_out, not_244_out, not_245_out, not_246_out,
       not_247_out, not_248_out, not_249_out, not_250_out, not_251_out, not_252_out, not_253_out,
       not_254_out, not_255_out, not_256_out, not_257_out, not_258_out, not_259_out, not_260_out,
       not_261_out, not_262_out, not_263_out, not_264_out, not_265_out, not_266_out, not_267_out,
       not_268_out, not_269_out, not_270_out, not_271_out, not_272_out, not_273_out, not_274_out;

  not not_1 (not_1_out, F30);
  not not_2 (not_2_out, F25);
  not not_3 (not_3_out, F14);
  not not_4 (not_4_out, F13);
  not not_5 (not_5_out, F12);
  not not_6 (not_6_out, OP6);
  not not_7 (not_7_out, OP3);
  not not_8 (not_8_out, OP2);
  not not_9 (not_9_out, F30);
  not not_10 (not_10_out, F25);
  not not_11 (not_11_out, OP6);
  not not_12 (not_12_out, OP3);
  not not_13 (not_13_out, OP2);
  not not_14 (not_14_out, F30);
  not not_15 (not_15_out, F25);
  not not_16 (not_16_out, F14);
  not not_17 (not_17_out, F12);
  not not_18 (not_18_out, OP6);
  not not_19 (not_19_out, OP3);
  not not_20 (not_20_out, OP2);
  not not_21 (not_21_out, F14);
  not not_22 (not_22_out, F13);
  not not_23 (not_23_out, F12);
  not not_24 (not_24_out, OP6);
  not not_25 (not_25_out, OP5);
  not not_26 (not_26_out, OP3);
  not not_27 (not_27_out, OP2);
  not not_28 (not_28_out, OP6);
  not not_29 (not_29_out, OP5);
  not not_30 (not_30_out, OP3);
  not not_31 (not_31_out, OP2);
  not not_32 (not_32_out, F13);
  not not_33 (not_33_out, F12);
  not not_34 (not_34_out, OP6);
  not not_35 (not_35_out, OP5);
  not not_36 (not_36_out, OP3);
  not not_37 (not_37_out, OP2);
  not not_38 (not_38_out, F14);
  not not_39 (not_39_out, F12);
  not not_40 (not_40_out, OP6);
  not not_41 (not_41_out, OP5);
  not not_42 (not_42_out, OP3);
  not not_43 (not_43_out, OP2);
  not not_44 (not_44_out, F25);
  not not_45 (not_45_out, F13);
  not not_46 (not_46_out, OP6);
  not not_47 (not_47_out, OP5);
  not not_48 (not_48_out, OP3);
  not not_49 (not_49_out, OP2);
  not not_50 (not_50_out, F14);
  not not_51 (not_51_out, F12);
  not not_52 (not_52_out, OP6);
  not not_53 (not_53_out, OP5);
  not not_54 (not_54_out, OP4);
  not not_55 (not_55_out, OP3);
  not not_56 (not_56_out, OP2);
  not not_57 (not_57_out, F14);
  not not_58 (not_58_out, F12);
  not not_59 (not_59_out, OP6);
  not not_60 (not_60_out, OP4);
  not not_61 (not_61_out, OP3);
  not not_62 (not_62_out, OP2);
  not not_63 (not_63_out, F14);
  not not_64 (not_64_out, F13);
  not not_65 (not_65_out, F12);
  not not_66 (not_66_out, OP3);
  not not_67 (not_67_out, OP2);
  not not_68 (not_68_out, F14);
  not not_69 (not_69_out, F13);
  not not_70 (not_70_out, F12);
  not not_71 (not_71_out, OP4);
  not not_72 (not_72_out, OP3);
  not not_73 (not_73_out, OP2);
  not not_74 (not_74_out, F14);
  not not_75 (not_75_out, F13);
  not not_76 (not_76_out, OP4);
  not not_77 (not_77_out, OP3);
  not not_78 (not_78_out, OP2);
  not not_79 (not_79_out, F14);
  not not_80 (not_80_out, F13);
  not not_81 (not_81_out, F12);
  not not_82 (not_82_out, OP4);
  not not_83 (not_83_out, OP3);
  not not_84 (not_84_out, F14);
  not not_85 (not_85_out, F13);
  not not_86 (not_86_out, F12);
  not not_87 (not_87_out, OP6);
  not not_88 (not_88_out, OP4);
  not not_89 (not_89_out, OP3);
  not not_90 (not_90_out, OP2);
  not not_91 (not_91_out, F25);
  not not_92 (not_92_out, F14);
  not not_93 (not_93_out, F13);
  not not_94 (not_94_out, F12);
  not not_95 (not_95_out, OP6);
  not not_96 (not_96_out, OP3);
  not not_97 (not_97_out, OP2);
  not not_98 (not_98_out, F30);
  not not_99 (not_99_out, F25);
  not not_100 (not_100_out, OP6);
  not not_101 (not_101_out, OP3);
  not not_102 (not_102_out, OP2);
  not not_103 (not_103_out, F30);
  not not_104 (not_104_out, F25);
  not not_105 (not_105_out, F14);
  not not_106 (not_106_out, F12);
  not not_107 (not_107_out, OP6);
  not not_108 (not_108_out, OP3);
  not not_109 (not_109_out, OP2);
  not not_110 (not_110_out, OP6);
  not not_111 (not_111_out, OP5);
  not not_112 (not_112_out, OP3);
  not not_113 (not_113_out, OP2);
  not not_114 (not_114_out, F14);
  not not_115 (not_115_out, F12);
  not not_116 (not_116_out, OP6);
  not not_117 (not_117_out, OP5);
  not not_118 (not_118_out, OP3);
  not not_119 (not_119_out, OP2);
  not not_120 (not_120_out, F30);
  not not_121 (not_121_out, F25);
  not not_122 (not_122_out, F13);
  not not_123 (not_123_out, OP6);
  not not_124 (not_124_out, OP5);
  not not_125 (not_125_out, OP3);
  not not_126 (not_126_out, OP2);
  not not_127 (not_127_out, F14);
  not not_128 (not_128_out, F13);
  not not_129 (not_129_out, F12);
  not not_130 (not_130_out, OP3);
  not not_131 (not_131_out, OP2);
  not not_132 (not_132_out, F14);
  not not_133 (not_133_out, F13);
  not not_134 (not_134_out, F12);
  not not_135 (not_135_out, OP4);
  not not_136 (not_136_out, OP3);
  not not_137 (not_137_out, OP2);
  not not_138 (not_138_out, F14);
  not not_139 (not_139_out, F13);
  not not_140 (not_140_out, OP4);
  not not_141 (not_141_out, OP3);
  not not_142 (not_142_out, OP2);
  not not_143 (not_143_out, F30);
  not not_144 (not_144_out, F25);
  not not_145 (not_145_out, F14);
  not not_146 (not_146_out, F13);
  not not_147 (not_147_out, F12);
  not not_148 (not_148_out, OP6);
  not not_149 (not_149_out, OP3);
  not not_150 (not_150_out, OP2);
  not not_151 (not_151_out, F25);
  not not_152 (not_152_out, F14);
  not not_153 (not_153_out, F13);
  not not_154 (not_154_out, F12);
  not not_155 (not_155_out, OP6);
  not not_156 (not_156_out, OP3);
  not not_157 (not_157_out, OP2);
  not not_158 (not_158_out, F30);
  not not_159 (not_159_out, F25);
  not not_160 (not_160_out, OP6);
  not not_161 (not_161_out, OP3);
  not not_162 (not_162_out, OP2);
  not not_163 (not_163_out, F30);
  not not_164 (not_164_out, F25);
  not not_165 (not_165_out, F14);
  not not_166 (not_166_out, OP6);
  not not_167 (not_167_out, OP3);
  not not_168 (not_168_out, OP2);
  not not_169 (not_169_out, F14);
  not not_170 (not_170_out, F13);
  not not_171 (not_171_out, F12);
  not not_172 (not_172_out, OP6);
  not not_173 (not_173_out, OP5);
  not not_174 (not_174_out, OP3);
  not not_175 (not_175_out, OP2);
  not not_176 (not_176_out, OP6);
  not not_177 (not_177_out, OP5);
  not not_178 (not_178_out, OP3);
  not not_179 (not_179_out, OP2);
  not not_180 (not_180_out, F14);
  not not_181 (not_181_out, F12);
  not not_182 (not_182_out, OP6);
  not not_183 (not_183_out, OP5);
  not not_184 (not_184_out, OP4);
  not not_185 (not_185_out, OP3);
  not not_186 (not_186_out, OP2);
  not not_187 (not_187_out, F14);
  not not_188 (not_188_out, F12);
  not not_189 (not_189_out, OP6);
  not not_190 (not_190_out, OP4);
  not not_191 (not_191_out, OP3);
  not not_192 (not_192_out, OP2);
  not not_193 (not_193_out, F14);
  not not_194 (not_194_out, F13);
  not not_195 (not_195_out, F12);
  not not_196 (not_196_out, OP4);
  not not_197 (not_197_out, OP3);
  not not_198 (not_198_out, F14);
  not not_199 (not_199_out, F13);
  not not_200 (not_200_out, F12);
  not not_201 (not_201_out, OP6);
  not not_202 (not_202_out, OP4);
  not not_203 (not_203_out, OP3);
  not not_204 (not_204_out, OP2);
  not not_205 (not_205_out, F14);
  not not_206 (not_206_out, OP6);
  not not_207 (not_207_out, OP5);
  not not_208 (not_208_out, OP3);
  not not_209 (not_209_out, OP2);
  not not_210 (not_210_out, F12);
  not not_211 (not_211_out, OP4);
  not not_212 (not_212_out, OP3);
  not not_213 (not_213_out, OP2);
  not not_214 (not_214_out, F30);
  not not_215 (not_215_out, F25);
  not not_216 (not_216_out, F12);
  not not_217 (not_217_out, OP6);
  not not_218 (not_218_out, OP3);
  not not_219 (not_219_out, OP2);
  not not_220 (not_220_out, F30);
  not not_221 (not_221_out, F25);
  not not_222 (not_222_out, F14);
  not not_223 (not_223_out, F12);
  not not_224 (not_224_out, OP6);
  not not_225 (not_225_out, OP3);
  not not_226 (not_226_out, OP2);
  not not_227 (not_227_out, F30);
  not not_228 (not_228_out, F25);
  not not_229 (not_229_out, F14);
  not not_230 (not_230_out, OP6);
  not not_231 (not_231_out, OP3);
  not not_232 (not_232_out, OP2);
  not not_233 (not_233_out, F12);
  not not_234 (not_234_out, OP6);
  not not_235 (not_235_out, OP5);
  not not_236 (not_236_out, OP3);
  not not_237 (not_237_out, OP2);
  not not_238 (not_238_out, F13);
  not not_239 (not_239_out, F12);
  not not_240 (not_240_out, OP6);
  not not_241 (not_241_out, OP5);
  not not_242 (not_242_out, OP3);
  not not_243 (not_243_out, OP2);
  not not_244 (not_244_out, F14);
  not not_245 (not_245_out, F12);
  not not_246 (not_246_out, OP6);
  not not_247 (not_247_out, OP5);
  not not_248 (not_248_out, OP3);
  not not_249 (not_249_out, OP2);
  not not_250 (not_250_out, F14);
  not not_251 (not_251_out, F13);
  not not_252 (not_252_out, F12);
  not not_253 (not_253_out, OP3);
  not not_254 (not_254_out, OP2);
  not not_255 (not_255_out, F14);
  not not_256 (not_256_out, F13);
  not not_257 (not_257_out, F12);
  not not_258 (not_258_out, OP4);
  not not_259 (not_259_out, OP3);
  not not_260 (not_260_out, OP2);
  not not_261 (not_261_out, F14);
  not not_262 (not_262_out, F13);
  not not_263 (not_263_out, OP4);
  not not_264 (not_264_out, OP3);
  not not_265 (not_265_out, OP2);
  not not_266 (not_266_out, F14);
  not not_267 (not_267_out, OP6);
  not not_268 (not_268_out, OP5);
  not not_269 (not_269_out, OP3);
  not not_270 (not_270_out, OP2);
  not not_271 (not_271_out, F12);
  not not_272 (not_272_out, OP4);
  not not_273 (not_273_out, OP3);
  not not_274 (not_274_out, OP2);
  and and_1 (and_1_out, not_1_out, not_2_out, not_3_out, not_4_out, not_5_out, not_6_out, OP5, OP4, not_7_out, not_8_out);
  and and_2 (and_2_out, not_9_out, not_10_out, F14, F13, F12, not_11_out, OP5, OP4, not_12_out, not_13_out);
  and and_3 (and_3_out, not_14_out, not_15_out, not_16_out, F13, not_17_out, not_18_out, OP5, OP4, not_19_out, not_20_out);
  and and_4 (and_4_out, not_21_out, not_22_out, not_23_out, not_24_out, not_25_out, OP4, not_26_out, not_27_out);
  and and_5 (and_5_out, F14, F13, F12, not_28_out, not_29_out, OP4, not_30_out, not_31_out);
  and and_6 (and_6_out, F14, not_32_out, not_33_out, not_34_out, not_35_out, OP4, not_36_out, not_37_out);
  and and_7 (and_7_out, not_38_out, F13, not_39_out, not_40_out, not_41_out, OP4, not_42_out, not_43_out);
  and and_8 (and_8_out, F30, not_44_out, F14, not_45_out, F12, not_46_out, not_47_out, OP4, not_48_out, not_49_out);
  and and_9 (and_9_out, not_50_out, F13, not_51_out, not_52_out, not_53_out, not_54_out, not_55_out, not_56_out);
  and and_10 (and_10_out, not_57_out, F13, not_58_out, not_59_out, OP5, not_60_out, not_61_out, not_62_out);
  and and_11 (and_11_out, not_63_out, not_64_out, not_65_out, OP6, OP5, OP4, not_66_out, not_67_out);
  and and_12 (and_12_out, not_68_out, not_69_out, not_70_out, OP6, OP5, not_71_out, not_72_out, not_73_out);
  and and_13 (and_13_out, not_74_out, not_75_out, F12, OP6, OP5, not_76_out, not_77_out, not_78_out);
  and and_14 (and_14_out, not_79_out, not_80_out, not_81_out, OP6, OP5, not_82_out, not_83_out, OP2);
  and and_15 (and_15_out, not_84_out, not_85_out, not_86_out, not_87_out, OP5, not_88_out, not_89_out, not_90_out);
  and and_16 (and_16_out, F30, not_91_out, not_92_out, not_93_out, not_94_out, not_95_out, OP5, OP4, not_96_out, not_97_out);
  and and_17 (and_17_out, not_98_out, not_99_out, F14, F13, F12, not_100_out, OP5, OP4, not_101_out, not_102_out);
  and and_18 (and_18_out, not_103_out, not_104_out, not_105_out, F13, not_106_out, not_107_out, OP5, OP4, not_108_out, not_109_out);
  and and_19 (and_19_out, F14, F13, F12, not_110_out, not_111_out, OP4, not_112_out, not_113_out);
  and and_20 (and_20_out, not_114_out, F13, not_115_out, not_116_out, not_117_out, OP4, not_118_out, not_119_out);
  and and_21 (and_21_out, not_120_out, not_121_out, F14, not_122_out, F12, not_123_out, not_124_out, OP4, not_125_out, not_126_out);
  and and_22 (and_22_out, not_127_out, not_128_out, not_129_out, OP6, OP5, OP4, not_130_out, not_131_out);
  and and_23 (and_23_out, not_132_out, not_133_out, not_134_out, OP6, OP5, not_135_out, not_136_out, not_137_out);
  and and_24 (and_24_out, not_138_out, not_139_out, F12, OP6, OP5, not_140_out, not_141_out, not_142_out);
  and and_25 (and_25_out, not_143_out, not_144_out, not_145_out, not_146_out, not_147_out, not_148_out, OP5, OP4, not_149_out, not_150_out);
  and and_26 (and_26_out, F30, not_151_out, not_152_out, not_153_out, not_154_out, not_155_out, OP5, OP4, not_156_out, not_157_out);
  and and_27 (and_27_out, not_158_out, not_159_out, F14, F13, F12, not_160_out, OP5, OP4, not_161_out, not_162_out);
  and and_28 (and_28_out, not_163_out, not_164_out, not_165_out, F13, F12, not_166_out, OP5, OP4, not_167_out, not_168_out);
  and and_29 (and_29_out, not_169_out, not_170_out, not_171_out, not_172_out, not_173_out, OP4, not_174_out, not_175_out);
  and and_30 (and_30_out, F14, F13, F12, not_176_out, not_177_out, OP4, not_178_out, not_179_out);
  and and_31 (and_31_out, not_180_out, F13, not_181_out, not_182_out, not_183_out, not_184_out, not_185_out, not_186_out);
  and and_32 (and_32_out, not_187_out, F13, not_188_out, not_189_out, OP5, not_190_out, not_191_out, not_192_out);
  and and_33 (and_33_out, not_193_out, not_194_out, not_195_out, OP6, OP5, not_196_out, not_197_out, OP2);
  and and_34 (and_34_out, not_198_out, not_199_out, not_200_out, not_201_out, OP5, not_202_out, not_203_out, not_204_out);
  and and_35 (and_35_out, not_205_out, F13, F12, not_206_out, not_207_out, OP4, not_208_out, not_209_out);
  and and_36 (and_36_out, F14, F13, not_210_out, OP6, OP5, not_211_out, not_212_out, not_213_out);
  and and_37 (and_37_out, not_214_out, not_215_out, F14, F13, not_216_out, not_217_out, OP5, OP4, not_218_out, not_219_out);
  and and_38 (and_38_out, not_220_out, not_221_out, not_222_out, F13, not_223_out, not_224_out, OP5, OP4, not_225_out, not_226_out);
  and and_39 (and_39_out, not_227_out, not_228_out, not_229_out, F13, F12, not_230_out, OP5, OP4, not_231_out, not_232_out);
  and and_40 (and_40_out, F14, F13, not_233_out, not_234_out, not_235_out, OP4, not_236_out, not_237_out);
  and and_41 (and_41_out, F14, not_238_out, not_239_out, not_240_out, not_241_out, OP4, not_242_out, not_243_out);
  and and_42 (and_42_out, not_244_out, F13, not_245_out, not_246_out, not_247_out, OP4, not_248_out, not_249_out);
  and and_43 (and_43_out, not_250_out, not_251_out, not_252_out, OP6, OP5, OP4, not_253_out, not_254_out);
  and and_44 (and_44_out, not_255_out, not_256_out, not_257_out, OP6, OP5, not_258_out, not_259_out, not_260_out);
  and and_45 (and_45_out, not_261_out, not_262_out, F12, OP6, OP5, not_263_out, not_264_out, not_265_out);
  and and_46 (and_46_out, not_266_out, F13, F12, not_267_out, not_268_out, OP4, not_269_out, not_270_out);
  and and_47 (and_47_out, F14, F13, not_271_out, OP6, OP5, not_272_out, not_273_out, not_274_out);
  or or_1 (S0, and_1_out, and_2_out, and_3_out, and_4_out, and_5_out, and_6_out, and_7_out, and_8_out, and_9_out, and_10_out, and_11_out, and_12_out, and_13_out, and_14_out, and_15_out);
  or or_2 (S1, and_16_out, and_17_out, and_18_out, and_19_out, and_20_out, and_21_out, and_22_out, and_23_out, and_24_out);
  or or_3 (S2, and_25_out, and_26_out, and_27_out, and_28_out, and_29_out, and_30_out, and_31_out, and_32_out, and_33_out, and_34_out, and_35_out, and_36_out);
  or or_4 (S3, and_37_out, and_38_out, and_39_out, and_40_out, and_41_out, and_42_out, and_43_out, and_44_out, and_45_out, and_46_out, and_47_out);
endmodule

// 控制信号生成
module \控制信号自动生成  (
  input  OP2,
  input  OP3,
  input  OP4,
  input  OP5,
  input  OP6,
  input  F12,
  input  F13,
  input  F14,
  input  F25,
  input  F30,
  output MemToReg,
  output MemWrite,
  output ALU_SRC,
  output RegWrite,
  output ecall,
  output S_Type,
  output BEQ,
  output BNE,
  output JALR,
  output JAL,
  output sb,
  output auipc,
  output bltu,
  output sltiu,
  output rs1,
  output rs2,
  output CSRRSI,
  output CSRRCI
);

  wire and_2_out, and_3_out, and_4_out, and_5_out, and_6_out, and_7_out, and_8_out, and_9_out, and_10_out,
       and_11_out, and_12_out, and_13_out, and_14_out, and_15_out, and_16_out, and_17_out, and_18_out,
       and_19_out, and_20_out, and_21_out, and_22_out, and_23_out, and_24_out, and_25_out, and_26_out,
       and_27_out, and_28_out, and_29_out, and_30_out, and_31_out, and_32_out, and_33_out, and_34_out,
       and_35_out, and_36_out, and_37_out, and_39_out, and_40_out, and_49_out, and_50_out, and_51_out,
       and_52_out, and_53_out, and_54_out, and_55_out, and_56_out, and_57_out, and_58_out, and_59_out,
       and_60_out, and_61_out, and_62_out, and_63_out, and_64_out, and_65_out, and_66_out, and_67_out,
       and_68_out, and_69_out, and_70_out, and_71_out, and_72_out, and_73_out, and_74_out, and_75_out,
       and_76_out, and_77_out, and_78_out, and_79_out, and_80_out, and_81_out, not_1_out, not_2_out,
       not_3_out, not_4_out, not_5_out, not_6_out, not_7_out, not_8_out, not_9_out, not_10_out, not_11_out,
       not_12_out, not_13_out, not_14_out, not_15_out, not_16_out, not_17_out, not_18_out, not_19_out,
       not_20_out, not_21_out, not_22_out, not_23_out, not_24_out, not_25_out, not_26_out, not_27_out,
       not_28_out, not_29_out, not_30_out, not_31_out, not_32_out, not_33_out, not_34_out, not_35_out,
       not_36_out, not_37_out, not_38_out, not_39_out, not_40_out, not_41_out, not_42_out, not_43_out,
       not_44_out, not_45_out, not_46_out, not_47_out, not_48_out, not_49_out, not_50_out, not_51_out,
       not_52_out, not_53_out, not_54_out, not_55_out, not_56_out, not_57_out, not_58_out, not_59_out,
       not_60_out, not_61_out, not_62_out, not_63_out, not_64_out, not_65_out, not_66_out, not_67_out,
       not_68_out, not_69_out, not_70_out, not_71_out, not_72_out, not_73_out, not_74_out, not_75_out,
       not_76_out, not_77_out, not_78_out, not_79_out, not_80_out, not_81_out, not_82_out, not_83_out,
       not_84_out, not_85_out, not_86_out, not_87_out, not_88_out, not_89_out, not_90_out, not_91_out,
       not_92_out, not_93_out, not_94_out, not_95_out, not_96_out, not_97_out, not_98_out, not_99_out,
       not_100_out, not_101_out, not_102_out, not_103_out, not_104_out, not_105_out, not_106_out,
       not_107_out, not_108_out, not_109_out, not_110_out, not_111_out, not_112_out, not_113_out,
       not_114_out, not_115_out, not_116_out, not_117_out, not_118_out, not_119_out, not_120_out,
       not_121_out, not_122_out, not_123_out, not_124_out, not_125_out, not_126_out, not_127_out,
       not_128_out, not_129_out, not_130_out, not_131_out, not_132_out, not_133_out, not_134_out,
       not_135_out, not_136_out, not_137_out, not_138_out, not_139_out, not_140_out, not_141_out,
       not_142_out, not_143_out, not_144_out, not_145_out, not_146_out, not_147_out, not_148_out,
       not_149_out, not_150_out, not_151_out, not_152_out, not_153_out, not_154_out, not_155_out,
       not_156_out, not_157_out, not_158_out, not_159_out, not_160_out, not_161_out, not_162_out,
       not_163_out, not_164_out, not_165_out, not_166_out, not_167_out, not_168_out, not_169_out,
       not_170_out, not_171_out, not_172_out, not_173_out, not_174_out, not_175_out, not_176_out,
       not_177_out, not_178_out, not_179_out, not_180_out, not_181_out, not_182_out, not_183_out,
       not_184_out, not_185_out, not_186_out, not_187_out, not_188_out, not_189_out, not_190_out,
       not_191_out, not_192_out, not_193_out, not_194_out, not_195_out, not_196_out, not_197_out,
       not_198_out, not_199_out, not_200_out, not_201_out, not_202_out, not_203_out, not_204_out,
       not_205_out, not_206_out, not_207_out, not_208_out, not_209_out, not_210_out, not_211_out,
       not_212_out, not_213_out, not_214_out, not_215_out, not_216_out, not_217_out, not_218_out,
       not_219_out, not_220_out, not_221_out, not_222_out, not_223_out, not_224_out, not_225_out,
       not_226_out, not_227_out, not_228_out, not_229_out, not_230_out, not_231_out, not_232_out,
       not_233_out, not_234_out, not_235_out, not_236_out, not_237_out, not_238_out, not_239_out,
       not_240_out, not_241_out, not_242_out, not_243_out, not_244_out, not_245_out, not_246_out,
       not_247_out, not_248_out, not_249_out, not_250_out, not_251_out, not_252_out, not_253_out,
       not_254_out, not_255_out, not_256_out, not_257_out, not_258_out, not_259_out, not_260_out,
       not_261_out, not_262_out, not_263_out, not_264_out, not_265_out, not_266_out, not_267_out,
       not_268_out, not_269_out, not_270_out, not_271_out, not_272_out, not_273_out, not_274_out,
       not_275_out, not_276_out, not_277_out, not_278_out, not_279_out, not_280_out, not_281_out,
       not_282_out, not_283_out, not_284_out, not_285_out, not_286_out, not_287_out, not_288_out,
       not_289_out, not_290_out, not_291_out, not_292_out, not_293_out, not_294_out, not_295_out,
       not_296_out, not_297_out, not_298_out, not_299_out, not_300_out, not_301_out, not_302_out,
       not_303_out, not_304_out, not_305_out, not_306_out, not_307_out, not_308_out, not_309_out,
       not_310_out, not_311_out, not_312_out, not_313_out, not_314_out, not_315_out, not_316_out,
       not_317_out, not_318_out, not_319_out, not_320_out, not_321_out, not_322_out, not_323_out,
       not_324_out, not_325_out, not_326_out, not_327_out, not_328_out, not_329_out, not_330_out,
       not_331_out, not_332_out, not_333_out, not_334_out, not_335_out, not_336_out, not_337_out,
       not_338_out, not_339_out, not_340_out, not_341_out, not_342_out, not_343_out, not_344_out,
       not_345_out, not_346_out, not_347_out, not_348_out, not_349_out, not_350_out, not_351_out,
       not_352_out, not_353_out, not_354_out, not_355_out, not_356_out, not_357_out, not_358_out,
       not_359_out, not_360_out, not_361_out, not_362_out, not_363_out, not_364_out, not_365_out,
       not_366_out, not_367_out, not_368_out, not_369_out, not_370_out, not_371_out, not_372_out,
       not_373_out, not_374_out, not_375_out, not_376_out, not_377_out, not_378_out, not_379_out,
       not_380_out, not_381_out, not_382_out, not_383_out, not_384_out, not_385_out, not_386_out,
       not_387_out, not_388_out, not_389_out, not_390_out, not_391_out, not_392_out, not_393_out,
       not_394_out, not_395_out, not_396_out, not_397_out, not_398_out, not_399_out, not_400_out,
       not_401_out, not_402_out, not_403_out, not_404_out, not_405_out, not_406_out, not_407_out,
       not_408_out, not_409_out, not_410_out, not_411_out, not_412_out, not_413_out, not_414_out,
       not_415_out, not_416_out, not_417_out, not_418_out, not_419_out, not_420_out, not_421_out,
       not_422_out, not_423_out, not_424_out, not_425_out, not_426_out, not_427_out, not_428_out,
       not_429_out, not_430_out, not_431_out, not_432_out, not_433_out, not_434_out, not_435_out,
       not_436_out, not_437_out, not_438_out, not_439_out, not_440_out, not_441_out, not_442_out,
       not_443_out, not_444_out, not_445_out, not_446_out, not_447_out, not_448_out, not_449_out,
       not_450_out, not_451_out, not_452_out, not_453_out, not_454_out, not_455_out, not_456_out,
       not_457_out, not_458_out, not_459_out, not_460_out, not_461_out, not_462_out, not_463_out,
       not_464_out, not_465_out, not_466_out, not_467_out, not_468_out;

  not not_1 (not_1_out, F14);
  not not_2 (not_2_out, F12);
  not not_3 (not_3_out, OP6);
  not not_4 (not_4_out, OP5);
  not not_5 (not_5_out, OP4);
  not not_6 (not_6_out, OP3);
  not not_7 (not_7_out, OP2);
  not not_8 (not_8_out, F14);
  not not_9 (not_9_out, F12);
  not not_10 (not_10_out, OP6);
  not not_11 (not_11_out, OP4);
  not not_12 (not_12_out, OP3);
  not not_13 (not_13_out, OP2);
  not not_14 (not_14_out, F14);
  not not_15 (not_15_out, F13);
  not not_16 (not_16_out, F12);
  not not_17 (not_17_out, OP6);
  not not_18 (not_18_out, OP4);
  not not_19 (not_19_out, OP3);
  not not_20 (not_20_out, OP2);
  not not_21 (not_21_out, F14);
  not not_22 (not_22_out, F13);
  not not_23 (not_23_out, F12);
  not not_24 (not_24_out, OP6);
  not not_25 (not_25_out, OP5);
  not not_26 (not_26_out, OP3);
  not not_27 (not_27_out, OP2);
  not not_28 (not_28_out, OP6);
  not not_29 (not_29_out, OP5);
  not not_30 (not_30_out, OP3);
  not not_31 (not_31_out, OP2);
  not not_32 (not_32_out, F12);
  not not_33 (not_33_out, OP6);
  not not_34 (not_34_out, OP5);
  not not_35 (not_35_out, OP3);
  not not_36 (not_36_out, OP2);
  not not_37 (not_37_out, F13);
  not not_38 (not_38_out, F12);
  not not_39 (not_39_out, OP6);
  not not_40 (not_40_out, OP5);
  not not_41 (not_41_out, OP3);
  not not_42 (not_42_out, OP2);
  not not_43 (not_43_out, F14);
  not not_44 (not_44_out, F12);
  not not_45 (not_45_out, OP6);
  not not_46 (not_46_out, OP5);
  not not_47 (not_47_out, OP3);
  not not_48 (not_48_out, OP2);
  not not_49 (not_49_out, F30);
  not not_50 (not_50_out, F25);
  not not_51 (not_51_out, F14);
  not not_52 (not_52_out, F13);
  not not_53 (not_53_out, OP6);
  not not_54 (not_54_out, OP5);
  not not_55 (not_55_out, OP3);
  not not_56 (not_56_out, OP2);
  not not_57 (not_57_out, F30);
  not not_58 (not_58_out, F25);
  not not_59 (not_59_out, F13);
  not not_60 (not_60_out, OP6);
  not not_61 (not_61_out, OP5);
  not not_62 (not_62_out, OP3);
  not not_63 (not_63_out, OP2);
  not not_64 (not_64_out, F25);
  not not_65 (not_65_out, F13);
  not not_66 (not_66_out, OP6);
  not not_67 (not_67_out, OP5);
  not not_68 (not_68_out, OP3);
  not not_69 (not_69_out, OP2);
  not not_70 (not_70_out, F14);
  not not_71 (not_71_out, F12);
  not not_72 (not_72_out, OP6);
  not not_73 (not_73_out, OP5);
  not not_74 (not_74_out, OP4);
  not not_75 (not_75_out, OP3);
  not not_76 (not_76_out, OP2);
  not not_77 (not_77_out, F14);
  not not_78 (not_78_out, F12);
  not not_79 (not_79_out, OP6);
  not not_80 (not_80_out, OP4);
  not not_81 (not_81_out, OP3);
  not not_82 (not_82_out, OP2);
  not not_83 (not_83_out, F14);
  not not_84 (not_84_out, F13);
  not not_85 (not_85_out, F12);
  not not_86 (not_86_out, OP4);
  not not_87 (not_87_out, OP3);
  not not_88 (not_88_out, F12);
  not not_89 (not_89_out, OP3);
  not not_90 (not_90_out, OP2);
  not not_91 (not_91_out, OP3);
  not not_92 (not_92_out, OP2);
  not not_93 (not_93_out, F14);
  not not_94 (not_94_out, F13);
  not not_95 (not_95_out, F12);
  not not_96 (not_96_out, OP6);
  not not_97 (not_97_out, OP4);
  not not_98 (not_98_out, OP3);
  not not_99 (not_99_out, OP2);
  not not_100 (not_100_out, F14);
  not not_101 (not_101_out, OP6);
  not not_102 (not_102_out, OP5);
  not not_103 (not_103_out, OP3);
  not not_104 (not_104_out, OP2);
  not not_105 (not_105_out, F30);
  not not_106 (not_106_out, F25);
  not not_107 (not_107_out, F14);
  not not_108 (not_108_out, F13);
  not not_109 (not_109_out, F12);
  not not_110 (not_110_out, OP6);
  not not_111 (not_111_out, OP3);
  not not_112 (not_112_out, OP2);
  not not_113 (not_113_out, F25);
  not not_114 (not_114_out, F14);
  not not_115 (not_115_out, F13);
  not not_116 (not_116_out, F12);
  not not_117 (not_117_out, OP6);
  not not_118 (not_118_out, OP3);
  not not_119 (not_119_out, OP2);
  not not_120 (not_120_out, F30);
  not not_121 (not_121_out, F25);
  not not_122 (not_122_out, OP6);
  not not_123 (not_123_out, OP3);
  not not_124 (not_124_out, OP2);
  not not_125 (not_125_out, F30);
  not not_126 (not_126_out, F25);
  not not_127 (not_127_out, F12);
  not not_128 (not_128_out, OP6);
  not not_129 (not_129_out, OP3);
  not not_130 (not_130_out, OP2);
  not not_131 (not_131_out, F30);
  not not_132 (not_132_out, F25);
  not not_133 (not_133_out, F14);
  not not_134 (not_134_out, F12);
  not not_135 (not_135_out, OP6);
  not not_136 (not_136_out, OP3);
  not not_137 (not_137_out, OP2);
  not not_138 (not_138_out, F30);
  not not_139 (not_139_out, F25);
  not not_140 (not_140_out, F14);
  not not_141 (not_141_out, OP6);
  not not_142 (not_142_out, OP3);
  not not_143 (not_143_out, OP2);
  not not_144 (not_144_out, F14);
  not not_145 (not_145_out, F13);
  not not_146 (not_146_out, F12);
  not not_147 (not_147_out, OP6);
  not not_148 (not_148_out, OP5);
  not not_149 (not_149_out, OP3);
  not not_150 (not_150_out, OP2);
  not not_151 (not_151_out, OP6);
  not not_152 (not_152_out, OP5);
  not not_153 (not_153_out, OP3);
  not not_154 (not_154_out, OP2);
  not not_155 (not_155_out, F12);
  not not_156 (not_156_out, OP6);
  not not_157 (not_157_out, OP5);
  not not_158 (not_158_out, OP3);
  not not_159 (not_159_out, OP2);
  not not_160 (not_160_out, F13);
  not not_161 (not_161_out, F12);
  not not_162 (not_162_out, OP6);
  not not_163 (not_163_out, OP5);
  not not_164 (not_164_out, OP3);
  not not_165 (not_165_out, OP2);
  not not_166 (not_166_out, F14);
  not not_167 (not_167_out, F12);
  not not_168 (not_168_out, OP6);
  not not_169 (not_169_out, OP5);
  not not_170 (not_170_out, OP3);
  not not_171 (not_171_out, OP2);
  not not_172 (not_172_out, F30);
  not not_173 (not_173_out, F25);
  not not_174 (not_174_out, F14);
  not not_175 (not_175_out, F13);
  not not_176 (not_176_out, OP6);
  not not_177 (not_177_out, OP5);
  not not_178 (not_178_out, OP3);
  not not_179 (not_179_out, OP2);
  not not_180 (not_180_out, F30);
  not not_181 (not_181_out, F25);
  not not_182 (not_182_out, F13);
  not not_183 (not_183_out, OP6);
  not not_184 (not_184_out, OP5);
  not not_185 (not_185_out, OP3);
  not not_186 (not_186_out, OP2);
  not not_187 (not_187_out, F25);
  not not_188 (not_188_out, F13);
  not not_189 (not_189_out, OP6);
  not not_190 (not_190_out, OP5);
  not not_191 (not_191_out, OP3);
  not not_192 (not_192_out, OP2);
  not not_193 (not_193_out, F14);
  not not_194 (not_194_out, F12);
  not not_195 (not_195_out, OP6);
  not not_196 (not_196_out, OP5);
  not not_197 (not_197_out, OP4);
  not not_198 (not_198_out, OP3);
  not not_199 (not_199_out, OP2);
  not not_200 (not_200_out, OP4);
  not not_201 (not_201_out, F14);
  not not_202 (not_202_out, F13);
  not not_203 (not_203_out, F12);
  not not_204 (not_204_out, OP4);
  not not_205 (not_205_out, OP3);
  not not_206 (not_206_out, OP6);
  not not_207 (not_207_out, OP5);
  not not_208 (not_208_out, OP3);
  not not_209 (not_209_out, F14);
  not not_210 (not_210_out, OP6);
  not not_211 (not_211_out, OP5);
  not not_212 (not_212_out, OP3);
  not not_213 (not_213_out, OP2);
  not not_214 (not_214_out, F14);
  not not_215 (not_215_out, F13);
  not not_216 (not_216_out, F12);
  not not_217 (not_217_out, OP3);
  not not_218 (not_218_out, OP2);
  not not_219 (not_219_out, F14);
  not not_220 (not_220_out, F12);
  not not_221 (not_221_out, OP6);
  not not_222 (not_222_out, OP4);
  not not_223 (not_223_out, OP3);
  not not_224 (not_224_out, OP2);
  not not_225 (not_225_out, F14);
  not not_226 (not_226_out, F13);
  not not_227 (not_227_out, F12);
  not not_228 (not_228_out, OP6);
  not not_229 (not_229_out, OP4);
  not not_230 (not_230_out, OP3);
  not not_231 (not_231_out, OP2);
  not not_232 (not_232_out, F14);
  not not_233 (not_233_out, F13);
  not not_234 (not_234_out, F12);
  not not_235 (not_235_out, OP4);
  not not_236 (not_236_out, OP3);
  not not_237 (not_237_out, OP2);
  not not_238 (not_238_out, F14);
  not not_239 (not_239_out, F13);
  not not_240 (not_240_out, OP4);
  not not_241 (not_241_out, OP3);
  not not_242 (not_242_out, OP2);
  not not_243 (not_243_out, F14);
  not not_244 (not_244_out, F13);
  not not_245 (not_245_out, F12);
  not not_246 (not_246_out, OP4);
  not not_247 (not_247_out, OP3);
  not not_248 (not_248_out, OP4);
  not not_249 (not_249_out, F14);
  not not_250 (not_250_out, F13);
  not not_251 (not_251_out, F12);
  not not_252 (not_252_out, OP6);
  not not_253 (not_253_out, OP4);
  not not_254 (not_254_out, OP3);
  not not_255 (not_255_out, OP2);
  not not_256 (not_256_out, OP6);
  not not_257 (not_257_out, OP5);
  not not_258 (not_258_out, OP3);
  not not_259 (not_259_out, F12);
  not not_260 (not_260_out, OP4);
  not not_261 (not_261_out, OP3);
  not not_262 (not_262_out, OP2);
  not not_263 (not_263_out, F14);
  not not_264 (not_264_out, OP6);
  not not_265 (not_265_out, OP5);
  not not_266 (not_266_out, OP3);
  not not_267 (not_267_out, OP2);
  not not_268 (not_268_out, F30);
  not not_269 (not_269_out, F25);
  not not_270 (not_270_out, F14);
  not not_271 (not_271_out, F13);
  not not_272 (not_272_out, F12);
  not not_273 (not_273_out, OP6);
  not not_274 (not_274_out, OP3);
  not not_275 (not_275_out, OP2);
  not not_276 (not_276_out, F25);
  not not_277 (not_277_out, F14);
  not not_278 (not_278_out, F13);
  not not_279 (not_279_out, F12);
  not not_280 (not_280_out, OP6);
  not not_281 (not_281_out, OP3);
  not not_282 (not_282_out, OP2);
  not not_283 (not_283_out, F30);
  not not_284 (not_284_out, F25);
  not not_285 (not_285_out, OP6);
  not not_286 (not_286_out, OP3);
  not not_287 (not_287_out, OP2);
  not not_288 (not_288_out, F30);
  not not_289 (not_289_out, F25);
  not not_290 (not_290_out, F12);
  not not_291 (not_291_out, OP6);
  not not_292 (not_292_out, OP3);
  not not_293 (not_293_out, OP2);
  not not_294 (not_294_out, F30);
  not not_295 (not_295_out, F25);
  not not_296 (not_296_out, F14);
  not not_297 (not_297_out, F12);
  not not_298 (not_298_out, OP6);
  not not_299 (not_299_out, OP3);
  not not_300 (not_300_out, OP2);
  not not_301 (not_301_out, F30);
  not not_302 (not_302_out, F25);
  not not_303 (not_303_out, F14);
  not not_304 (not_304_out, OP6);
  not not_305 (not_305_out, OP3);
  not not_306 (not_306_out, OP2);
  not not_307 (not_307_out, F14);
  not not_308 (not_308_out, F13);
  not not_309 (not_309_out, F12);
  not not_310 (not_310_out, OP6);
  not not_311 (not_311_out, OP5);
  not not_312 (not_312_out, OP3);
  not not_313 (not_313_out, OP2);
  not not_314 (not_314_out, OP6);
  not not_315 (not_315_out, OP5);
  not not_316 (not_316_out, OP3);
  not not_317 (not_317_out, OP2);
  not not_318 (not_318_out, F12);
  not not_319 (not_319_out, OP6);
  not not_320 (not_320_out, OP5);
  not not_321 (not_321_out, OP3);
  not not_322 (not_322_out, OP2);
  not not_323 (not_323_out, F13);
  not not_324 (not_324_out, F12);
  not not_325 (not_325_out, OP6);
  not not_326 (not_326_out, OP5);
  not not_327 (not_327_out, OP3);
  not not_328 (not_328_out, OP2);
  not not_329 (not_329_out, F14);
  not not_330 (not_330_out, F12);
  not not_331 (not_331_out, OP6);
  not not_332 (not_332_out, OP5);
  not not_333 (not_333_out, OP3);
  not not_334 (not_334_out, OP2);
  not not_335 (not_335_out, F30);
  not not_336 (not_336_out, F25);
  not not_337 (not_337_out, F14);
  not not_338 (not_338_out, F13);
  not not_339 (not_339_out, OP6);
  not not_340 (not_340_out, OP5);
  not not_341 (not_341_out, OP3);
  not not_342 (not_342_out, OP2);
  not not_343 (not_343_out, F30);
  not not_344 (not_344_out, F25);
  not not_345 (not_345_out, F13);
  not not_346 (not_346_out, OP6);
  not not_347 (not_347_out, OP5);
  not not_348 (not_348_out, OP3);
  not not_349 (not_349_out, OP2);
  not not_350 (not_350_out, F25);
  not not_351 (not_351_out, F13);
  not not_352 (not_352_out, OP6);
  not not_353 (not_353_out, OP5);
  not not_354 (not_354_out, OP3);
  not not_355 (not_355_out, OP2);
  not not_356 (not_356_out, F14);
  not not_357 (not_357_out, F12);
  not not_358 (not_358_out, OP6);
  not not_359 (not_359_out, OP5);
  not not_360 (not_360_out, OP4);
  not not_361 (not_361_out, OP3);
  not not_362 (not_362_out, OP2);
  not not_363 (not_363_out, F14);
  not not_364 (not_364_out, F12);
  not not_365 (not_365_out, OP6);
  not not_366 (not_366_out, OP4);
  not not_367 (not_367_out, OP3);
  not not_368 (not_368_out, OP2);
  not not_369 (not_369_out, F14);
  not not_370 (not_370_out, F13);
  not not_371 (not_371_out, F12);
  not not_372 (not_372_out, OP3);
  not not_373 (not_373_out, OP2);
  not not_374 (not_374_out, F14);
  not not_375 (not_375_out, F13);
  not not_376 (not_376_out, F12);
  not not_377 (not_377_out, OP4);
  not not_378 (not_378_out, OP3);
  not not_379 (not_379_out, OP2);
  not not_380 (not_380_out, F14);
  not not_381 (not_381_out, F13);
  not not_382 (not_382_out, OP4);
  not not_383 (not_383_out, OP3);
  not not_384 (not_384_out, OP2);
  not not_385 (not_385_out, F14);
  not not_386 (not_386_out, F13);
  not not_387 (not_387_out, F12);
  not not_388 (not_388_out, OP4);
  not not_389 (not_389_out, OP3);
  not not_390 (not_390_out, F14);
  not not_391 (not_391_out, OP6);
  not not_392 (not_392_out, OP5);
  not not_393 (not_393_out, OP3);
  not not_394 (not_394_out, OP2);
  not not_395 (not_395_out, F12);
  not not_396 (not_396_out, OP4);
  not not_397 (not_397_out, OP3);
  not not_398 (not_398_out, OP2);
  not not_399 (not_399_out, F30);
  not not_400 (not_400_out, F25);
  not not_401 (not_401_out, F14);
  not not_402 (not_402_out, F13);
  not not_403 (not_403_out, F12);
  not not_404 (not_404_out, OP6);
  not not_405 (not_405_out, OP3);
  not not_406 (not_406_out, OP2);
  not not_407 (not_407_out, F25);
  not not_408 (not_408_out, F14);
  not not_409 (not_409_out, F13);
  not not_410 (not_410_out, F12);
  not not_411 (not_411_out, OP6);
  not not_412 (not_412_out, OP3);
  not not_413 (not_413_out, OP2);
  not not_414 (not_414_out, F30);
  not not_415 (not_415_out, F25);
  not not_416 (not_416_out, OP6);
  not not_417 (not_417_out, OP3);
  not not_418 (not_418_out, OP2);
  not not_419 (not_419_out, F30);
  not not_420 (not_420_out, F25);
  not not_421 (not_421_out, F12);
  not not_422 (not_422_out, OP6);
  not not_423 (not_423_out, OP3);
  not not_424 (not_424_out, OP2);
  not not_425 (not_425_out, F30);
  not not_426 (not_426_out, F25);
  not not_427 (not_427_out, F14);
  not not_428 (not_428_out, F12);
  not not_429 (not_429_out, OP6);
  not not_430 (not_430_out, OP3);
  not not_431 (not_431_out, OP2);
  not not_432 (not_432_out, F30);
  not not_433 (not_433_out, F25);
  not not_434 (not_434_out, F14);
  not not_435 (not_435_out, OP6);
  not not_436 (not_436_out, OP3);
  not not_437 (not_437_out, OP2);
  not not_438 (not_438_out, F14);
  not not_439 (not_439_out, F12);
  not not_440 (not_440_out, OP6);
  not not_441 (not_441_out, OP4);
  not not_442 (not_442_out, OP3);
  not not_443 (not_443_out, OP2);
  not not_444 (not_444_out, F14);
  not not_445 (not_445_out, F13);
  not not_446 (not_446_out, F12);
  not not_447 (not_447_out, OP3);
  not not_448 (not_448_out, OP2);
  not not_449 (not_449_out, F14);
  not not_450 (not_450_out, F13);
  not not_451 (not_451_out, F12);
  not not_452 (not_452_out, OP4);
  not not_453 (not_453_out, OP3);
  not not_454 (not_454_out, OP2);
  not not_455 (not_455_out, F14);
  not not_456 (not_456_out, F13);
  not not_457 (not_457_out, OP4);
  not not_458 (not_458_out, OP3);
  not not_459 (not_459_out, OP2);
  not not_460 (not_460_out, F12);
  not not_461 (not_461_out, OP4);
  not not_462 (not_462_out, OP3);
  not not_463 (not_463_out, OP2);
  not not_464 (not_464_out, OP2);
  not not_465 (not_465_out, OP3);
  not not_466 (not_466_out, F12);
  not not_467 (not_467_out, OP2);
  not not_468 (not_468_out, OP3);
  and and_1 (MemToReg, not_1_out, F13, not_2_out, not_3_out, not_4_out, not_5_out, not_6_out, not_7_out);
  and and_2 (and_2_out, not_8_out, F13, not_9_out, not_10_out, OP5, not_11_out, not_12_out, not_13_out);
  and and_3 (and_3_out, not_14_out, not_15_out, not_16_out, not_17_out, OP5, not_18_out, not_19_out, not_20_out);
  and and_4 (and_4_out, not_21_out, not_22_out, not_23_out, not_24_out, not_25_out, OP4, not_26_out, not_27_out);
  and and_5 (and_5_out, F14, F13, F12, not_28_out, not_29_out, OP4, not_30_out, not_31_out);
  and and_6 (and_6_out, F14, F13, not_32_out, not_33_out, not_34_out, OP4, not_35_out, not_36_out);
  and and_7 (and_7_out, F14, not_37_out, not_38_out, not_39_out, not_40_out, OP4, not_41_out, not_42_out);
  and and_8 (and_8_out, not_43_out, F13, not_44_out, not_45_out, not_46_out, OP4, not_47_out, not_48_out);
  and and_9 (and_9_out, not_49_out, not_50_out, not_51_out, not_52_out, F12, not_53_out, not_54_out, OP4, not_55_out, not_56_out);
  and and_10 (and_10_out, not_57_out, not_58_out, F14, not_59_out, F12, not_60_out, not_61_out, OP4, not_62_out, not_63_out);
  and and_11 (and_11_out, F30, not_64_out, F14, not_65_out, F12, not_66_out, not_67_out, OP4, not_68_out, not_69_out);
  and and_12 (and_12_out, not_70_out, F13, not_71_out, not_72_out, not_73_out, not_74_out, not_75_out, not_76_out);
  and and_13 (and_13_out, not_77_out, F13, not_78_out, not_79_out, OP5, not_80_out, not_81_out, not_82_out);
  and and_14 (and_14_out, not_83_out, not_84_out, not_85_out, OP6, OP5, not_86_out, not_87_out, OP2);
  and and_15 (and_15_out, F14, F13, not_88_out, OP6, OP5, OP4, not_89_out, not_90_out);
  and and_16 (and_16_out, F14, F13, F12, OP6, OP5, OP4, not_91_out, not_92_out);
  and and_17 (and_17_out, not_93_out, not_94_out, not_95_out, not_96_out, OP5, not_97_out, not_98_out, not_99_out);
  and and_18 (and_18_out, not_100_out, F13, F12, not_101_out, not_102_out, OP4, not_103_out, not_104_out);
  and and_19 (and_19_out, not_105_out, not_106_out, not_107_out, not_108_out, not_109_out, not_110_out, OP5, OP4, not_111_out, not_112_out);
  and and_20 (and_20_out, F30, not_113_out, not_114_out, not_115_out, not_116_out, not_117_out, OP5, OP4, not_118_out, not_119_out);
  and and_21 (and_21_out, not_120_out, not_121_out, F14, F13, F12, not_122_out, OP5, OP4, not_123_out, not_124_out);
  and and_22 (and_22_out, not_125_out, not_126_out, F14, F13, not_127_out, not_128_out, OP5, OP4, not_129_out, not_130_out);
  and and_23 (and_23_out, not_131_out, not_132_out, not_133_out, F13, not_134_out, not_135_out, OP5, OP4, not_136_out, not_137_out);
  and and_24 (and_24_out, not_138_out, not_139_out, not_140_out, F13, F12, not_141_out, OP5, OP4, not_142_out, not_143_out);
  and and_25 (and_25_out, not_144_out, not_145_out, not_146_out, not_147_out, not_148_out, OP4, not_149_out, not_150_out);
  and and_26 (and_26_out, F14, F13, F12, not_151_out, not_152_out, OP4, not_153_out, not_154_out);
  and and_27 (and_27_out, F14, F13, not_155_out, not_156_out, not_157_out, OP4, not_158_out, not_159_out);
  and and_28 (and_28_out, F14, not_160_out, not_161_out, not_162_out, not_163_out, OP4, not_164_out, not_165_out);
  and and_29 (and_29_out, not_166_out, F13, not_167_out, not_168_out, not_169_out, OP4, not_170_out, not_171_out);
  and and_30 (and_30_out, not_172_out, not_173_out, not_174_out, not_175_out, F12, not_176_out, not_177_out, OP4, not_178_out, not_179_out);
  and and_31 (and_31_out, not_180_out, not_181_out, F14, not_182_out, F12, not_183_out, not_184_out, OP4, not_185_out, not_186_out);
  and and_32 (and_32_out, F30, not_187_out, F14, not_188_out, F12, not_189_out, not_190_out, OP4, not_191_out, not_192_out);
  and and_33 (and_33_out, not_193_out, F13, not_194_out, not_195_out, not_196_out, not_197_out, not_198_out, not_199_out);
  and and_34 (and_34_out, OP6, OP5, not_200_out, OP3, OP2);
  and and_35 (and_35_out, not_201_out, not_202_out, not_203_out, OP6, OP5, not_204_out, not_205_out, OP2);
  and and_36 (and_36_out, not_206_out, not_207_out, OP4, not_208_out, OP2);
  and and_37 (and_37_out, not_209_out, F13, F12, not_210_out, not_211_out, OP4, not_212_out, not_213_out);
  and and_38 (ecall, not_214_out, not_215_out, not_216_out, OP6, OP5, OP4, not_217_out, not_218_out);
  and and_39 (and_39_out, not_219_out, F13, not_220_out, not_221_out, OP5, not_222_out, not_223_out, not_224_out);
  and and_40 (and_40_out, not_225_out, not_226_out, not_227_out, not_228_out, OP5, not_229_out, not_230_out, not_231_out);
  and and_41 (BEQ, not_232_out, not_233_out, not_234_out, OP6, OP5, not_235_out, not_236_out, not_237_out);
  and and_42 (BNE, not_238_out, not_239_out, F12, OP6, OP5, not_240_out, not_241_out, not_242_out);
  and and_43 (JALR, not_243_out, not_244_out, not_245_out, OP6, OP5, not_246_out, not_247_out, OP2);
  and and_44 (JAL, OP6, OP5, not_248_out, OP3, OP2);
  and and_45 (sb, not_249_out, not_250_out, not_251_out, not_252_out, OP5, not_253_out, not_254_out, not_255_out);
  and and_46 (auipc, not_256_out, not_257_out, OP4, not_258_out, OP2);
  and and_47 (bltu, F14, F13, not_259_out, OP6, OP5, not_260_out, not_261_out, not_262_out);
  and and_48 (sltiu, not_263_out, F13, F12, not_264_out, not_265_out, OP4, not_266_out, not_267_out);
  and and_49 (and_49_out, not_268_out, not_269_out, not_270_out, not_271_out, not_272_out, not_273_out, OP5, OP4, not_274_out, not_275_out);
  and and_50 (and_50_out, F30, not_276_out, not_277_out, not_278_out, not_279_out, not_280_out, OP5, OP4, not_281_out, not_282_out);
  and and_51 (and_51_out, not_283_out, not_284_out, F14, F13, F12, not_285_out, OP5, OP4, not_286_out, not_287_out);
  and and_52 (and_52_out, not_288_out, not_289_out, F14, F13, not_290_out, not_291_out, OP5, OP4, not_292_out, not_293_out);
  and and_53 (and_53_out, not_294_out, not_295_out, not_296_out, F13, not_297_out, not_298_out, OP5, OP4, not_299_out, not_300_out);
  and and_54 (and_54_out, not_301_out, not_302_out, not_303_out, F13, F12, not_304_out, OP5, OP4, not_305_out, not_306_out);
  and and_55 (and_55_out, not_307_out, not_308_out, not_309_out, not_310_out, not_311_out, OP4, not_312_out, not_313_out);
  and and_56 (and_56_out, F14, F13, F12, not_314_out, not_315_out, OP4, not_316_out, not_317_out);
  and and_57 (and_57_out, F14, F13, not_318_out, not_319_out, not_320_out, OP4, not_321_out, not_322_out);
  and and_58 (and_58_out, F14, not_323_out, not_324_out, not_325_out, not_326_out, OP4, not_327_out, not_328_out);
  and and_59 (and_59_out, not_329_out, F13, not_330_out, not_331_out, not_332_out, OP4, not_333_out, not_334_out);
  and and_60 (and_60_out, not_335_out, not_336_out, not_337_out, not_338_out, F12, not_339_out, not_340_out, OP4, not_341_out, not_342_out);
  and and_61 (and_61_out, not_343_out, not_344_out, F14, not_345_out, F12, not_346_out, not_347_out, OP4, not_348_out, not_349_out);
  and and_62 (and_62_out, F30, not_350_out, F14, not_351_out, F12, not_352_out, not_353_out, OP4, not_354_out, not_355_out);
  and and_63 (and_63_out, not_356_out, F13, not_357_out, not_358_out, not_359_out, not_360_out, not_361_out, not_362_out);
  and and_64 (and_64_out, not_363_out, F13, not_364_out, not_365_out, OP5, not_366_out, not_367_out, not_368_out);
  and and_65 (and_65_out, not_369_out, not_370_out, not_371_out, OP6, OP5, OP4, not_372_out, not_373_out);
  and and_66 (and_66_out, not_374_out, not_375_out, not_376_out, OP6, OP5, not_377_out, not_378_out, not_379_out);
  and and_67 (and_67_out, not_380_out, not_381_out, F12, OP6, OP5, not_382_out, not_383_out, not_384_out);
  and and_68 (and_68_out, not_385_out, not_386_out, not_387_out, OP6, OP5, not_388_out, not_389_out, OP2);
  and and_69 (and_69_out, not_390_out, F13, F12, not_391_out, not_392_out, OP4, not_393_out, not_394_out);
  and and_70 (and_70_out, F14, F13, not_395_out, OP6, OP5, not_396_out, not_397_out, not_398_out);
  and and_71 (and_71_out, not_399_out, not_400_out, not_401_out, not_402_out, not_403_out, not_404_out, OP5, OP4, not_405_out, not_406_out);
  and and_72 (and_72_out, F30, not_407_out, not_408_out, not_409_out, not_410_out, not_411_out, OP5, OP4, not_412_out, not_413_out);
  and and_73 (and_73_out, not_414_out, not_415_out, F14, F13, F12, not_416_out, OP5, OP4, not_417_out, not_418_out);
  and and_74 (and_74_out, not_419_out, not_420_out, F14, F13, not_421_out, not_422_out, OP5, OP4, not_423_out, not_424_out);
  and and_75 (and_75_out, not_425_out, not_426_out, not_427_out, F13, not_428_out, not_429_out, OP5, OP4, not_430_out, not_431_out);
  and and_76 (and_76_out, not_432_out, not_433_out, not_434_out, F13, F12, not_435_out, OP5, OP4, not_436_out, not_437_out);
  and and_77 (and_77_out, not_438_out, F13, not_439_out, not_440_out, OP5, not_441_out, not_442_out, not_443_out);
  and and_78 (and_78_out, not_444_out, not_445_out, not_446_out, OP6, OP5, OP4, not_447_out, not_448_out);
  and and_79 (and_79_out, not_449_out, not_450_out, not_451_out, OP6, OP5, not_452_out, not_453_out, not_454_out);
  and and_80 (and_80_out, not_455_out, not_456_out, F12, OP6, OP5, not_457_out, not_458_out, not_459_out);
  and and_81 (and_81_out, F14, F13, not_460_out, OP6, OP5, not_461_out, not_462_out, not_463_out);
  and and_82 (CSRRSI, not_464_out, not_465_out, OP4, OP5, OP6, not_466_out, F13, F14);
  and and_83 (CSRRCI, not_467_out, not_468_out, OP4, OP5, OP6, F12, F13, F14);
  or or_1 (MemWrite, and_2_out, and_3_out);
  or or_2 (S_Type, and_39_out, and_40_out);
  or or_3 (ALU_SRC, and_4_out, and_5_out, and_6_out, and_7_out, and_8_out, and_9_out, and_10_out, and_11_out, and_12_out, and_13_out, and_14_out, and_15_out, and_16_out, and_17_out, and_18_out);
  or or_4 (RegWrite, and_19_out, and_20_out, and_21_out, and_22_out, and_23_out, and_24_out, and_25_out, and_26_out, and_27_out, and_28_out, and_29_out, and_30_out, and_31_out, and_32_out, and_33_out, and_34_out, and_35_out, and_36_out, and_37_out);
  or or_5 (rs2, and_71_out, and_72_out, and_73_out, and_74_out, and_75_out, and_76_out, and_77_out, and_78_out, and_79_out, and_80_out, and_81_out);
  or or_6 (rs1, and_49_out, and_50_out, and_51_out, and_52_out, and_53_out, and_54_out, and_55_out, and_56_out, and_57_out, and_58_out, and_59_out, and_60_out, and_61_out, and_62_out, and_63_out, and_64_out, and_65_out, and_66_out, and_67_out, and_68_out, and_69_out, and_70_out);
endmodule

module \单周期RISC_V  (
  input  IR1,
  input  IR2,
  input  IR3,
  output RegWrite,
  output MemWrite,
  output [31:0] PC,
  output [31:0] IR,
  output [31:0] RDin,
  output [31:0] MDin,
  output [31:0] LedData
);

  wire alu_1_equal, alu_1_out_6, and_1_out, and_2_out, and_3_out, and_5_out, and_6_out, auipc, bltu, Branch,
       CLK, clock_1_out, comparator_1_eq, comparator_1_lt, comparator_2_eq, d_ff_1_q, ecall, Go, halt, IR1_t,
       IR2_t, IR3_t, IRA, IRB, IRC, JAL, JALR, MemToReg, nand_1_out, not_1_out, not_2_out, not_3_out,
       not_4_out, or_4_out, or_6_out, riscv_probe_1_p2, RST, sb, sltiu, W1, W2, W3, \单周期硬布线控制器_1_alu_src ,
       \单周期硬布线控制器_1_beq , \单周期硬布线控制器_1_bne , \单周期硬布线控制器_1_s_type ;
  wire [3:0] sb_1_out_3, \单周期硬布线控制器_1_alu_op ;
  wire [4:0] multiplexer_4_out, multiplexer_5_out;
  wire [11:0] multiplexer_6_out;
  wire [12:0] CNT_num;
  wire [15:0] \总周期数 ;
  wire [31:0] adder_1_out, adder_5_out, ALU_result, bit_extender_1_out, bit_extender_2_out,
       bit_extender_3_out, bit_extender_4_out, Branch_Adress, JAL_Adress, JALR_Adress, mips_ram_1_p7,
       multiplexer_1_out, multiplexer_2_out, multiplexer_3_out, multiplexer_7_out, multiplexer_8_out,
       multiplexer_10_out, multiplexer_11_out, r1, r2, sb_1_darta, shifter_1_out, shifter_2_out,
       shifter_3_out, U_adress;

  Button \u_继续运行  (.out(Go));
  Button _1 (.out(IRA));
  Button _2 (.out(IRB));
  Button _3 (.out(IRC));
  Multiplexer #(.select(1), .width(32), .disabled("Z"), .enable("false")) multiplexer_1 (
    .in0(multiplexer_2_out), .in1(JALR_Adress), .out(multiplexer_1_out), .sel(JALR));
  Multiplexer #(.select(1), .width(32), .disabled("Z"), .enable("false")) multiplexer_2 (
    .in0(adder_1_out), .in1(Branch_Adress), .out(multiplexer_2_out), .sel(Branch));
  LED #(.active("true")) led_1 (.in(W1));
  LED #(.active("true")) led_2 (.in(W2));
  LED #(.active("true")) led_3 (.in(W3));
  Button button_1 (.out(RST));
  Multiplexer #(.select(1), .width(32), .disabled("Z"), .enable("false")) multiplexer_3 (
    .in0(multiplexer_1_out), .in1(JAL_Adress), .out(multiplexer_3_out), .sel(JAL));
  Hex_Digit_Display hex_digit_display_1 (.value(LedData[31:28]));  // open: dp
  Register #(.width(32), .trigger("rising"), .Select("low")) u_PC (
    .D(multiplexer_3_out), .en(not_1_out), .Q(PC), .clk(CLK), .clr(RST));
  not not_1 (not_1_out, halt);
  Hex_Digit_Display hex_digit_display_2 (.value(LedData[27:24]));  // open: dp
  Hex_Digit_Display hex_digit_display_3 (.value(LedData[23:20]));  // open: dp
  Hex_Digit_Display hex_digit_display_4 (.value(LedData[15:12]));  // open: dp
  Hex_Digit_Display hex_digit_display_5 (.value(LedData[19:16]));  // open: dp
  // RiscV_Probe riscv_probe_1: pin names not known; wires that end beside it: IR, riscv_probe_1_p2, ecall
  Adder #(.width(32)) adder_1 (.a(PC), .b(32'h4), .out(adder_1_out));  // open: cin, cout
  Hex_Digit_Display hex_digit_display_6 (.value(LedData[7:4]));  // open: dp
  Hex_Digit_Display hex_digit_display_7 (.value(LedData[11:8]));  // open: dp
  // Probe on \总周期数 
  ROM #(.addrWidth(10), .dataWidth(32), .Select("high")) rom_1 (.addr(PC[11:2]), .data(IR));
  Hex_Digit_Display hex_digit_display_8 (.value(LedData[3:0]));  // open: dp
  \单周期硬布线控制器  \u_单周期硬布线控制器_1  (
    .Funct({IR[30], IR[25], IR[14:12]}), .OP(IR[6:2]), .ALU_OP(\单周期硬布线控制器_1_alu_op ), .MemToReg(MemToReg),
    .MemWrite(MemWrite), .ALU_SRC(\单周期硬布线控制器_1_alu_src ), .RegWrite(RegWrite), .ecall(ecall),
    .S_type(\单周期硬布线控制器_1_s_type ), .Jalr(JALR), .Beq(\单周期硬布线控制器_1_beq ), .JAL(JAL), .Bne(\单周期硬布线控制器_1_bne ),
    .in_3(IR[21]), .uret(riscv_probe_1_p2), .sb(sb), .auipc(auipc), .bltu(bltu), .sltiu(sltiu));  // open: rs1, rs2, CSRRSI, CSRRCI
  Multiplexer #(.select(1), .width(5), .disabled("Z"), .enable("false")) multiplexer_4 (
    .in0(IR[19:15]), .in1(5'b10001), .out(multiplexer_4_out), .sel(ecall));
  Multiplexer #(.select(1), .width(5), .disabled("Z"), .enable("false")) multiplexer_5 (
    .in0(IR[24:20]), .in1(5'b01010), .out(multiplexer_5_out), .sel(ecall));
  or or_1 (IR1_t, IR1, IRA);
  Multiplexer #(.select(1), .width(12), .disabled("Z"), .enable("false")) multiplexer_6 (
    .in0(IR[31:20]), .in1({IR[31:25], IR[11:7]}), .out(multiplexer_6_out), .sel(\单周期硬布线控制器_1_s_type ));
  assign bit_extender_1_out = {{20{IR[31]}}, {IR[31], IR[7], IR[30:25], IR[11:8]}};  // Bit_Extender bit_extender_1
  assign bit_extender_2_out = {{12{IR[31]}}, {IR[31], IR[19:12], IR[20], IR[30:21]}};  // Bit_Extender bit_extender_2
  assign bit_extender_3_out = {{12{1'b0}}, IR[31:12]};  // Bit_Extender bit_extender_3
  or or_2 (IR2_t, IR2, IRB);
  assign bit_extender_4_out = {{20{multiplexer_6_out[11]}}, multiplexer_6_out};  // Bit_Extender bit_extender_4
  Multiplexer #(.select(1), .width(32), .disabled("Z"), .enable("false")) multiplexer_7 (
    .in0({32{1'b0}}), .in1(bit_extender_3_out), .out(multiplexer_7_out), .sel(auipc));
  Regifile regifile_1 (
    .Din(RDin), .Clk(CLK), .R1(r1), .R2(r2), .WE(RegWrite), .W_num(IR[11:7]), .R1_num(multiplexer_4_out),
    .R2_num(multiplexer_5_out));
  Shifter #(.width(32), .shift("ll")) shifter_1 (.in(bit_extender_1_out), .\dist (5'b00001), .out(shifter_1_out));
  Shifter #(.width(32), .shift("ll")) shifter_2 (.in(bit_extender_2_out), .\dist (5'b00001), .out(shifter_2_out));
  or or_3 (IR3_t, IR3, IRC);
  Multiplexer #(.select(1), .width(32), .disabled("Z"), .enable("false")) multiplexer_8 (
    .in0(r2), .in1(bit_extender_4_out), .out(multiplexer_8_out), .sel(\单周期硬布线控制器_1_alu_src ));
  Adder #(.width(32)) adder_2 (.a(shifter_1_out), .b(PC), .out(Branch_Adress));  // open: cin, cout
  Adder #(.width(32)) adder_3 (.a(shifter_2_out), .b(PC), .out(JAL_Adress));  // open: cin, cout
  Shifter #(.width(32), .shift("ll")) shifter_3 (.in(multiplexer_7_out), .\dist (5'b01100), .out(shifter_3_out));
  Adder #(.width(32)) adder_4 (.a(shifter_3_out), .b(PC), .out(U_adress));  // open: cin, cout
  ALU alu_1 (
    .X(r1), .Y(multiplexer_8_out), .AluOP(\单周期硬布线控制器_1_alu_op ), .Equal(alu_1_equal), .Result(ALU_result),
    .out_6(alu_1_out_6));  // open: Result_2, out_4
  sb sb_1 (.in_1(sb), .R2(r2), .out_3(sb_1_out_3), .darta(sb_1_darta));
  Multiplexer #(.select(1), .width(32), .disabled("Z"), .enable("false")) multiplexer_9 (
    .in0(r2), .in1(sb_1_darta), .out(MDin), .sel(sb));
  and and_1 (and_1_out, \单周期硬布线控制器_1_beq , alu_1_equal);
  and and_2 (and_2_out, \单周期硬布线控制器_1_bne , not_2_out);
  not not_2 (not_2_out, alu_1_equal);
  and and_3 (and_3_out, bltu, alu_1_out_6);
  D_Flip_Flop #(.trigger("high"), .Pre_Clr_Positions("LEGACY"), .NegatePresetClear("false"), .enable("true"), .NewFFLayout("false")) d_ff_1 (.Q(d_ff_1_q));  // open: clk, D, Qn, preset, en, reset
  // Probe on 13'hc
  or or_4 (or_4_out, and_1_out, and_2_out);
  // MIPS_RAM mips_ram_1: pin names not known; wires that end beside it: ALU_result[11:2], MDin, MemWrite, sb_1_out_3, CLK, RST, mips_ram_1_p7
  Comparator #(.width(13), .mode("twosComplement")) comparator_1 (
    .a(CNT_num), .b(13'hc), .eq(comparator_1_eq), .lt(comparator_1_lt));  // open: gt
  Clock #(.highDuration(1), .lowDuration(1)) clock_1 (.out(clock_1_out));
  or or_5 (Branch, or_4_out, and_3_out);
  Counter #(.width(13), .max('h1fff), .ongoal("stay"), .trigger("rising"), .behavior("old")) counter_1 (
    .count(comparator_1_lt), .Q(CNT_num), .clk(clock_1_out));  // open: load, D, carry, clr, preset
  Multiplexer #(.select(1), .width(32), .disabled("Z"), .enable("false")) multiplexer_10 (
    .in0(ALU_result), .in1(mips_ram_1_p7), .out(multiplexer_10_out), .sel(MemToReg));
  Adder #(.width(32)) adder_5 (.a(PC), .b(32'h4), .out(adder_5_out));  // open: cin, cout
  assign JALR_Adress = ALU_result & 32'hfffffffe;  // AND_Gate and_4, 32 bits wide
  nand nand_1 (nand_1_out, d_ff_1_q, comparator_1_eq);
  or or_6 (or_6_out, JAL, JALR);
  Multiplexer #(.select(1), .width(32), .disabled("Z"), .enable("false")) multiplexer_11 (
    .in0(multiplexer_10_out), .in1(adder_5_out), .out(multiplexer_11_out), .sel(or_6_out));
  Comparator #(.width(32), .mode("twosComplement")) comparator_2 (
    .a(32'h22), .b(r1), .eq(comparator_2_eq));  // open: gt, lt
  assign CLK = nand_1_out ? clock_1_out : 1'bz;  // Controlled_Buffer controlled_buffer_1
  Pull_Resistor #(.pull(1)) pull_resistor_1 (.node(CLK));
  Multiplexer #(.select(1), .width(32), .disabled("Z"), .enable("false")) multiplexer_12 (
    .in0(multiplexer_11_out), .in1(U_adress), .out(RDin), .sel(auipc));
  not not_3 (not_3_out, comparator_2_eq);
  and and_5 (and_5_out, ecall, comparator_2_eq);
  and and_6 (and_6_out, ecall, not_3_out);
  Register #(.width(32), .trigger("rising"), .Select("low")) register_1 (
    .D(MDin), .en(and_5_out), .Q(LedData), .clk(CLK), .clr(RST));
  Multiplexer #(.select(1), .width(1), .disabled("Z"), .enable("false")) multiplexer_13 (
    .in0(and_6_out), .in1(1'b0), .out(halt), .sel(Go));
  not not_4 (not_4_out, halt);
  Counter #(.width(16), .max('hffff), .ongoal("wrap"), .trigger("rising"), .behavior("new")) counter_2 (
    .count(not_4_out), .Q(\总周期数 ), .clk(CLK), .clr(RST));  // open: load, D, carry, preset, down

  // Other names for the same wires on the sheet: I_imm[11:0] = IR[31:20]

  // Notes on the sheet:
  //   中断源
  //   中断等待指示
  //   数码管输出应该用寄存器锁存，否则显示数据只能一闪而过
  //   数码管输出
  //   指令探针
  //   指令存储器
  //   contents of rom_1 (hex, n*v repeats v):
  //   100493 100006f 100493 200913 300993 100006f 100493 200913 300993 100006f 100493 200913 300993
  //   100006f 100493 200913 300993 29c000ef 100413 100493 1f49493 900533 2200893 73 24d493 48463 fedff06f
  //   900533 2200893 73 100493 249493 900533 2200893 73 48463 fedff06f 100493 1f49493 900533 2200893 73
  //   4034d493 900533 2200893 73 4044d493 900533 2200893 73 4044d493 900533 2200893 73 4044d493 900533
  //   2200893 73 4044d493 900533 2200893 73 4044d493 900533 2200893 73 4044d493 900533 2200893 73 4044d493
  //   900533 2200893 73 100413 1f41993 41f9d993 433 c00913 300b13 140413 f47413 800293 100313 499993
  //   89e9b3 1300533 2200893 73 406282b3 fe0294e3 140413 f00f93 1f47433 1c41413 800293 100313 49d993
  //   89e9b3 1300533 2200893 73 406282b3 fe0294e3 1c45413 406b0b33 b0463 f95ff06f 2b3 fff2c293 829293
  //   ff2e293 500533 2200893 73 fff00413 493 84a023 140413 448493 84a023 140413 448493 84a023 140413
  //   448493 84a023 140413 448493 84a023 140413 448493 84a023 140413 448493 84a023 140413 448493 84a023
  //   140413 448493 84a023 140413 448493 84a023 140413 448493 84a023 140413 448493 84a023 140413 448493
  //   84a023 140413 448493 84a023 140413 448493 84a023 140413 448493 84a023 140413 448493 140413 433
  //   3c00493 42983 4aa03 149a2b3 28663 134a023 1442023 ffc48493 fe9412e3 800533 2200893 73 440413 3c00493
  //   fc9416e3 a00893 73 413 140413 800533 2200893 73 240413 800533 2200893 73 340413 800533 2200893 73
  //   440413 800533 2200893 73 540413 800533 2200893 73 640413 800533 2200893 73 740413 800533 2200893 73
  //   840413 800533 2200893 2200893 73 8067
  //   指令字
  //   JAL
  //   JALR
  //   URET
  //   Beq
  //   Bne
  //   MemToReg
  //   MemWrite
  //   AluOP
  //   AluSrcB
  //   RegWrite
  //   为方便自动评测，需要输出PC，IR，寄存器堆写如数据RDin
  //   RAM写使能MemWrite、RAM写入数据MDin等信号
  //   数据存储器
  //   控制位
  //   暂停节拍，不能为0
  //   戳工具置1进入计数暂停模式，ctrl+k时钟自动运行到对应节拍暂停
  //   用这个时钟源需要去掉电路中的其他时钟源
  //   可计数暂停的时钟源
endmodule

module Regifile (
  input  [31:0] Din,
  input  Clk,
  input  WE,
  input  [4:0] R1_num,
  input  [4:0] W_num,
  input  [4:0] R2_num,
  output [31:0] R1,
  output [31:0] R2
);

  // RegisterFile registerfile_1: pin names not known; wires that end beside it: Din, Clk, WE, W_num, R1_num, R2_num, R1, R2
endmodule

// ALU
module ALU (
  input  [31:0] X,
  input  [31:0] Y,
  input  [3:0] AluOP,
  output out_4,
  output Equal,
  output out_6,
  output [31:0] Result,
  output [31:0] Result_2
);

  wire [0:0] comparator_1_lt, comparator_2_lt;
  wire [31:0] adder_1_out, AND_out, divider_1_out, divider_1_rem, multiplier_1_cout, multiplier_1_out,
       NOR_out, OR_out, shifter_1_out, shifter_2_out, shifter_3_out, subtractor_1_out, XOR_out;

  assign AND_out = X & Y;  // AND_Gate AND, 32 bits wide
  assign OR_out = X | Y;  // OR_Gate OR, 32 bits wide
  Shifter #(.width(32), .shift("ll")) shifter_1 (.in(X), .\dist (Y[4:0]), .out(shifter_1_out));
  Shifter #(.width(32), .shift("ar")) shifter_2 (.in(X), .\dist (Y[4:0]), .out(shifter_2_out));
  Shifter #(.width(32), .shift("lr")) shifter_3 (.in(X), .\dist (Y[4:0]), .out(shifter_3_out));
  Multiplier #(.width(32)) multiplier_1 (.a(X), .b(Y), .out(multiplier_1_out), .cout(multiplier_1_cout));  // open: cin
  Divider #(.width(32)) divider_1 (.a(X), .b(Y), .out(divider_1_out), .rem(divider_1_rem));  // open: upper
  Adder #(.width(32)) adder_1 (.a(X), .b(Y), .out(adder_1_out));  // open: cin, cout
  Subtractor #(.width(32)) subtractor_1 (.a(X), .b(Y), .out(subtractor_1_out));  // open: bin, bout
  assign XOR_out = X ^ Y;  // XOR_Gate XOR, 32 bits wide
  assign NOR_out = ~(X | Y);  // NOR_Gate NOR, 32 bits wide
  Comparator #(.width(32), .mode("twosComplement")) comparator_1 (
    .a(X), .b(Y), .eq(Equal), .lt(comparator_1_lt[0]));  // open: gt
  Comparator #(.width(32), .mode("unsigned")) comparator_2 (.a(X), .b(Y), .lt(comparator_2_lt[0]));  // open: gt, eq
  Multiplexer #(.select(4), .width(32), .disabled("Z"), .enable("false")) multiplexer_1 (
    .in0(shifter_1_out), .in1(shifter_2_out), .in2(shifter_3_out), .in3(multiplier_1_out),
    .in4(divider_1_out), .in5(adder_1_out), .in6(subtractor_1_out), .in7(AND_out), .in8(OR_out),
    .in9(XOR_out), .in10(NOR_out), .in11({{31{1'b0}}, comparator_1_lt[0]}),
    .in12({{31{1'b0}}, comparator_2_lt[0]}), .in13({32{1'b0}}), .in14({32{1'b0}}), .in15({32{1'b0}}),
    .out(Result), .sel(AluOP));
  Multiplexer #(.select(4), .width(32), .disabled("Z"), .enable("false")) multiplexer_2 (
    .in0({32{1'b0}}), .in1({32{1'b0}}), .in2({32{1'b0}}), .in3(multiplier_1_cout), .in4(divider_1_rem),
    .in5({32{1'b0}}), .in6({32{1'b0}}), .in7({32{1'b0}}), .in8({32{1'b0}}), .in9({32{1'b0}}),
    .in10({32{1'b0}}), .in11({32{1'b0}}), .in12({32{1'b0}}), .in13({32{1'b0}}), .in14({32{1'b0}}),
    .in15({32{1'b0}}), .out(Result_2), .sel(AluOP));
  Multiplexer #(.select(4), .width(1), .disabled("Z"), .enable("false")) multiplexer_3 (
    .in0(1'b0), .in1(1'b0), .in2(1'b0), .in3(1'b0), .in4(1'b0), .in5(1'b0), .in6(1'b0), .in7(1'b0),
    .in8(1'b0), .in9(1'b0), .in10(1'b0), .in11(comparator_1_lt[0]), .in12(comparator_2_lt[0]), .in13(1'b0),
    .in14(1'b0), .in15(1'b0), .out(out_6), .sel(AluOP));
  not not_1 (out_4, out_6);

  // Other names for the same wires on the sheet: Result2[31:0] = Result_2; S[3:0] = AluOP; tunnel = out_6;
  //   tunnel_t = out_4

  // Notes on the sheet:
  //   不要改变此引脚区域内容，也不要改变ALU封装形式
  //   输入引脚
  //   输出引脚
endmodule

module \气泡流水线  (
  output RegWrite,
  output MemWrite,
  output [31:0] IF_PC,
  output [31:0] ID_PC,
  output [31:0] EX_PC,
  output [31:0] M_PC,
  output [31:0] WB_PC,
  output [31:0] RDin,
  output [31:0] MDin,
  output [31:0] LedData
);

  wire alu_1_equal, alu_1_out_6, and_1_out, and_3_out, and_4_out, and_5_out, and_6_out, auipc, branchtaken,
       CLK, clock_1_out, comparator_1_eq, comparator_1_lt, comparator_2_eq, comparator_3_eq, d_ff_2_q,
       datahazzrd, ecall, ecallEq, ecallFB, ex_1_auipc_2, ex_1_ecall_2, ex_1_jal_2, ex_1_jalr_2,
       ex_1_memtoreg_2, ex_1_sb_2, ex_1_uret_2, EX_RegWrite, flush, Go, halt, id_1_alu_srcb_2, id_1_auipc_2,
       id_1_beq_2, id_1_bltu_2, id_1_bne_2, id_1_ecall_2, id_1_jal_2, id_1_jalr_2, id_1_memtoreg_2,
       id_1_memwrite_2, id_1_sb_2, id_1_uret_2, IR1, IR2, IR3, mem_1_jal_2, mem_1_jalr_2, MEN_MemtoReg,
       MEN_RegWrite, nand_1_out, not_1_out, not_2_out, not_3_out, not_4_out, not_5_out, not_6_out, not_7_out,
       not_8_out, or_1_out, or_2_out, or_3_out, or_5_out, or_6_out, rs1, rs2, RST, sltiu, stall, Stop, W1,
       W2, W3, WB_ecall, \单周期硬布线控制器_1_alu_src , \单周期硬布线控制器_1_auipc , \单周期硬布线控制器_1_beq , \单周期硬布线控制器_1_bltu ,
       \单周期硬布线控制器_1_bne , \单周期硬布线控制器_1_jal , \单周期硬布线控制器_1_jalr , \单周期硬布线控制器_1_memtoreg ,
       \单周期硬布线控制器_1_memwrite , \单周期硬布线控制器_1_regwrite , \单周期硬布线控制器_1_s_type , \单周期硬布线控制器_1_sb ,
       \单周期硬布线控制器_1_uret ;
  wire [3:0] id_1_alu_op_2, sb_1_out_3, \单周期硬布线控制器_1_alu_op ;
  wire [4:0] EX_RD, MEM_RD, R1_num, R2_num, WB_RD;
  wire [11:0] I_imm, multiplexer_6_out;
  wire [12:0] CNT_num;
  wire [15:0] \LoadUse次数 , \总周期数 , \插入气泡数 , \无条件分支数 , \条件分支成功数 ;
  wire [19:0] ID_IR;
  wire [31:0] adder_1_out, adder_4_out, alu_1_result, ALU_result, bit_extender_1_out, bit_extender_2_out,
       bit_extender_3_out, bit_extender_4_out, Branch_Adress, ex_1_pc_4_2, ex_1_r1_2, ex_1_r2_2, ex_1_u_2,
       EX_IR, EX_R1, EX_R2, id_1_bm_2, id_1_im_2, id_1_jm_2, id_1_pc_4_2, id_1_u_2, ID_PC_4, IF_IR,
       JAL_Adress, JALR_Adress, mem_1_alu_result_2, mem_1_mdata_2, mem_1_u_2, MEM_IR, mips_ram_1_p7,
       multiplexer_1_out, multiplexer_2_out, multiplexer_3_out, multiplexer_7_out, multiplexer_9_out,
       multiplexer_10_out, multiplexer_11_out, regifile_1_r1, regifile_1_r2, sb_1_darta, shifter_1_out,
       shifter_2_out, shifter_3_out, U_adress, WB_IR, WB_PC_4, WB_R1, WB_R2;

  Button \u_总复位  (.out(RST));
  Button _1 (.out(IR1));
  Button _2 (.out(IR2));
  Button _3 (.out(IR3));
  // Probe on \总周期数 
  // Probe on \总周期数 
  Button \u_继续运行  (.out(Go));
  LED #(.active("true")) led_1 (.in(W1));
  LED #(.active("true")) led_2 (.in(W2));
  LED #(.active("true")) led_3 (.in(W3));
  Hex_Digit_Display hex_digit_display_1 (.value(LedData[31:28]));  // open: dp
  // Probe on IF_PC[19:0]
  // RiscV_Probe riscv_probe_1: pin names not known; wires that end beside it: IF_IR
  Hex_Digit_Display hex_digit_display_2 (.value(LedData[23:20]));  // open: dp
  Hex_Digit_Display hex_digit_display_3 (.value(LedData[27:24]));  // open: dp
  // Probe on ID_PC[19:0]
  // RiscV_Probe riscv_probe_2: pin names not known; wires that end beside it: {I_imm, ID_IR}
  Hex_Digit_Display hex_digit_display_4 (.value(LedData[19:16]));  // open: dp
  Hex_Digit_Display hex_digit_display_5 (.value(LedData[15:12]));  // open: dp
  Multiplexer #(.select(1), .width(32), .disabled("Z"), .enable("false")) multiplexer_1 (
    .in0(adder_1_out), .in1(Branch_Adress), .out(multiplexer_1_out), .sel(or_5_out));
  Multiplexer #(.select(1), .width(32), .disabled("Z"), .enable("false")) multiplexer_2 (
    .in0(multiplexer_1_out), .in1(JAL_Adress), .out(multiplexer_2_out), .sel(id_1_jal_2));
  Adder #(.width(32)) adder_1 (.a(IF_PC), .b(32'h4), .out(adder_1_out));  // open: cin, cout
  datahazzard datahazzard_1 (
    .RtUsed(rs1), .Rt(R1_num), .Rt_2(R1_num), .MEN_WriteReg(MEM_RD), .MEN_Regwrite(MEN_RegWrite),
    .RtUsed_2(rs1), .Rt_3(R1_num), .Rt_4(R1_num), .EX_WriteReg(EX_RD), .EX_Regwrite(EX_RegWrite),
    .RsUsed(rs2), .Rs(R2_num), .Rs_2(R2_num), .EX_WriteReg_2(EX_RD), .EX_Regwrite_2(EX_RegWrite),
    .RsUsed_2(rs2), .Rs_3(R2_num), .Rs_4(R2_num), .MEN_WriteReg_2(MEM_RD), .MEN_Regwrite_2(MEN_RegWrite),
    .datahazzed(datahazzrd));
  Hex_Digit_Display hex_digit_display_6 (.value(LedData[11:8]));  // open: dp
  Hex_Digit_Display hex_digit_display_7 (.value(LedData[7:4]));  // open: dp
  // Probe on EX_PC[19:0]
  // RiscV_Probe riscv_probe_3: pin names not known; wires that end beside it: EX_IR
  Multiplexer #(.select(1), .width(32), .disabled("Z"), .enable("false")) multiplexer_3 (
    .in0(multiplexer_2_out), .in1(JALR_Adress), .out(multiplexer_3_out), .sel(id_1_jalr_2));
  not not_1 (not_1_out, datahazzrd);
  Hex_Digit_Display hex_digit_display_8 (.value(LedData[3:0]));  // open: dp
  Register #(.width(32), .trigger("rising"), .Select("low")) PC (
    .D(multiplexer_3_out), .en(and_1_out), .Q(IF_PC), .clk(CLK), .clr(RST));
  and and_1 (and_1_out, not_1_out, Stop);
  \气泡处理  \u_气泡处理_1  (
    .datahazzd(datahazzrd), .branch(branchtaken), .datahazzd_2(datahazzrd), .stall(stall), .flush(flush));
  // Probe on \总周期数 
  // Probe on M_PC[19:0]
  // RiscV_Probe riscv_probe_4: pin names not known; wires that end beside it: MEM_IR
  D_Flip_Flop #(.trigger("rising"), .Pre_Clr_Positions("LEGACY"), .NegatePresetClear("false"), .enable("true"), .NewFFLayout("false")) d_ff_1 (
    .Qn(Stop), .preset(halt), .reset(Go));  // open: clk, D, Q, en
  // Probe on \总周期数 
  // Probe on \无条件分支数 
  // Probe on \条件分支成功数 
  // Probe on \插入气泡数 
  // Probe on \LoadUse次数 
  // Probe on IF_PC[11:0]
  // Probe on WB_PC[19:0]
  // RiscV_Probe riscv_probe_5: pin names not known; wires that end beside it: WB_IR
  // Probe on EX_PC[11:0]
  // Probe on ID_PC[11:0]
  or or_1 (or_1_out, RST, branchtaken);
  // RiscV_Probe riscv_probe_6: pin names not known; wires that end beside it: IF_IR
  ROM #(.addrWidth(10), .dataWidth(32), .Select("high")) rom_1 (.addr(IF_PC[11:2]), .data(IF_IR));
  or or_2 (or_2_out, not_2_out, datahazzrd);
  not not_2 (not_2_out, Stop);
  // Probe on M_PC[11:0]
  D_Flip_Flop #(.trigger("high"), .Pre_Clr_Positions("LEGACY"), .NegatePresetClear("false"), .enable("true"), .NewFFLayout("false")) d_ff_2 (.Q(d_ff_2_q));  // open: clk, D, Qn, preset, en, reset
  // Probe on 13'hc
  IF if_1 (
    .CLK(CLK), .RST(or_1_out), .IR(IF_IR), .PC(IF_PC), .PC_4(adder_1_out), .IR_2({I_imm, ID_IR}),
    .PC_2(ID_PC), .PC_4_2(ID_PC_4), .flush(1'b0), .en(or_2_out));
  // Probe on WB_PC[11:0]
  Comparator #(.width(13), .mode("twosComplement")) comparator_1 (
    .a(CNT_num), .b(13'hc), .eq(comparator_1_eq), .lt(comparator_1_lt));  // open: gt
  Clock #(.highDuration(1), .lowDuration(1)) clock_1 (.out(clock_1_out));
  nand nand_1 (nand_1_out, d_ff_2_q, comparator_1_eq);
  Counter #(.width(13), .max('h1fff), .ongoal("stay"), .trigger("rising"), .behavior("old")) counter_1 (
    .count(comparator_1_lt), .Q(CNT_num), .clk(clock_1_out));  // open: load, D, carry, clr, preset
  assign CLK = nand_1_out ? clock_1_out : 1'bz;  // Controlled_Buffer controlled_buffer_1
  \单周期硬布线控制器  \u_单周期硬布线控制器_1  (
    .Funct({I_imm[10], I_imm[5], ID_IR[14:12]}), .OP(ID_IR[6:2]), .ALU_OP(\单周期硬布线控制器_1_alu_op ),
    .MemToReg(\单周期硬布线控制器_1_memtoreg ), .MemWrite(\单周期硬布线控制器_1_memwrite ), .ALU_SRC(\单周期硬布线控制器_1_alu_src ),
    .RegWrite(\单周期硬布线控制器_1_regwrite ), .ecall(ecall), .S_type(\单周期硬布线控制器_1_s_type ),
    .Jalr(\单周期硬布线控制器_1_jalr ), .Beq(\单周期硬布线控制器_1_beq ), .JAL(\单周期硬布线控制器_1_jal ), .Bne(\单周期硬布线控制器_1_bne ),
    .in_3(I_imm[1]), .uret(\单周期硬布线控制器_1_uret ), .sb(\单周期硬布线控制器_1_sb ), .auipc(\单周期硬布线控制器_1_auipc ),
    .bltu(\单周期硬布线控制器_1_bltu ), .sltiu(sltiu), .rs1(rs1), .rs2(rs2));  // open: CSRRSI, CSRRCI
  Multiplexer #(.select(1), .width(5), .disabled("Z"), .enable("false")) multiplexer_4 (
    .in0(ID_IR[19:15]), .in1(5'b10001), .out(R1_num), .sel(ecall));
  Multiplexer #(.select(1), .width(5), .disabled("Z"), .enable("false")) multiplexer_5 (
    .in0(I_imm[4:0]), .in1(5'b01010), .out(R2_num), .sel(ecall));
  Pull_Resistor #(.pull(1)) pull_resistor_1 (.node(CLK));
  Multiplexer #(.select(1), .width(12), .disabled("Z"), .enable("false")) multiplexer_6 (
    .in0(I_imm), .in1({I_imm[11:5], ID_IR[11:7]}), .out(multiplexer_6_out), .sel(\单周期硬布线控制器_1_s_type ));
  assign bit_extender_1_out = {{20{I_imm[11]}}, {I_imm[11], ID_IR[7], I_imm[10:5], ID_IR[11:8]}};  // Bit_Extender bit_extender_1
  assign bit_extender_2_out = {{12{I_imm[11]}}, {I_imm[11], ID_IR[19:12], I_imm[0], I_imm[10:1]}};  // Bit_Extender bit_extender_2
  assign bit_extender_3_out = {{12{1'b0}}, {I_imm, ID_IR[19:12]}};  // Bit_Extender bit_extender_3
  assign bit_extender_4_out = {{20{multiplexer_6_out[11]}}, multiplexer_6_out};  // Bit_Extender bit_extender_4
  Regifile regifile_1 (
    .Din(RDin), .Clk(CLK), .R1(regifile_1_r1), .R2(regifile_1_r2), .WE(RegWrite), .W_num(WB_RD),
    .R1_num(R1_num), .R2_num(R2_num));
  not not_3 (not_3_out, Stop);
  or or_3 (or_3_out, RST, branchtaken, datahazzrd);
  ID id_1 (
    .RST(or_3_out), .beq(\单周期硬布线控制器_1_beq ), .bne(\单周期硬布线控制器_1_bne ), .MemToReg(\单周期硬布线控制器_1_memtoreg ),
    .MemWrite(\单周期硬布线控制器_1_memwrite ), .ALU_OP(\单周期硬布线控制器_1_alu_op ), .ALU_SRCB(\单周期硬布线控制器_1_alu_src ),
    .RegWrite(\单周期硬布线控制器_1_regwrite ), .JAL(\单周期硬布线控制器_1_jal ), .JALR(\单周期硬布线控制器_1_jalr ),
    .URET(\单周期硬布线控制器_1_uret ), .ID_PC(ID_PC), .r1(regifile_1_r1), .r2(regifile_1_r2),
    .Bm(bit_extender_1_out), .Jm(bit_extender_2_out), .PC_4(ID_PC_4), .CLK(CLK), .beq_2(id_1_beq_2),
    .bne_2(id_1_bne_2), .MemToReg_2(id_1_memtoreg_2), .MemWrite_2(id_1_memwrite_2), .ALU_OP_2(id_1_alu_op_2),
    .ALU_SRCB_2(id_1_alu_srcb_2), .RegWrite_2(EX_RegWrite), .JAL_2(id_1_jal_2), .JALR_2(id_1_jalr_2),
    .URET_2(id_1_uret_2), .ID_PC_2(EX_PC), .r1_2(EX_R1), .r2_2(EX_R2), .Bm_2(id_1_bm_2), .Jm_2(id_1_jm_2),
    .PC_4_2(id_1_pc_4_2), .ID_IR({I_imm, ID_IR}), .ID_IR_2(EX_IR), .ecall(ecall), .ecall_2(id_1_ecall_2),
    .WRD(ID_IR[11:7]), .WRD_2(EX_RD), .Im(bit_extender_4_out), .Im_2(id_1_im_2), .halt(not_3_out),
    .auipc(\单周期硬布线控制器_1_auipc ), .bltu(\单周期硬布线控制器_1_bltu ), .sb(\单周期硬布线控制器_1_sb ), .bltu_2(id_1_bltu_2),
    .auipc_2(id_1_auipc_2), .sb_2(id_1_sb_2), .u(bit_extender_3_out), .u_2(id_1_u_2), .flush(1'b0));  // open: S_type, S_type_2, RsFoward, RtFoward, RsFoward_2, Rtfoward_2
  Shifter #(.width(32), .shift("ll")) shifter_1 (.in(id_1_bm_2), .\dist (5'b00001), .out(shifter_1_out));
  Shifter #(.width(32), .shift("ll")) shifter_2 (.in(id_1_jm_2), .\dist (5'b00001), .out(shifter_2_out));
  Multiplexer #(.select(1), .width(32), .disabled("Z"), .enable("false")) multiplexer_7 (
    .in0(EX_R2), .in1(id_1_im_2), .out(multiplexer_7_out), .sel(id_1_alu_srcb_2));
  Adder #(.width(32)) adder_2 (.a(shifter_1_out), .b(EX_PC), .out(Branch_Adress));  // open: cin, cout
  Adder #(.width(32)) adder_3 (.a(shifter_2_out), .b(EX_PC), .out(JAL_Adress));  // open: cin, cout
  ALU alu_1 (
    .X(EX_R1), .Y(multiplexer_7_out), .AluOP(id_1_alu_op_2), .Equal(alu_1_equal), .Result(alu_1_result),
    .out_6(alu_1_out_6));  // open: Result_2, out_4
  assign JALR_Adress = alu_1_result & 32'hfffffffe;  // AND_Gate and_2, 32 bits wide
  or or_4 (branchtaken, id_1_jalr_2, id_1_jal_2, or_5_out);
  or or_5 (or_5_out, and_5_out, and_3_out, and_4_out);
  and and_3 (and_3_out, not_4_out, id_1_bne_2);
  and and_4 (and_4_out, id_1_beq_2, alu_1_equal);
  and and_5 (and_5_out, id_1_bltu_2, alu_1_out_6);
  not not_4 (not_4_out, alu_1_equal);
  not not_5 (not_5_out, Stop);
  EX ex_1 (
    .RST(RST), .JAL(id_1_jal_2), .JALR(id_1_jalr_2), .URET(id_1_uret_2), .MemToReg(id_1_memtoreg_2),
    .MenWrite(id_1_memwrite_2), .ecall(id_1_ecall_2), .RegWirte(EX_RegWrite), .Write(EX_RD),
    .ALU_Result(alu_1_result), .EX_PC(EX_PC), .EX_IR(EX_IR), .PC_4(id_1_pc_4_2), .R1(EX_R1), .R2(EX_R2),
    .halt(not_5_out), .CLK(CLK), .JAL_2(ex_1_jal_2), .JALR_2(ex_1_jalr_2), .URET_2(ex_1_uret_2),
    .MemToReg_2(ex_1_memtoreg_2), .MemWrite(MemWrite), .ecall_2(ex_1_ecall_2), .RegWirte_2(MEN_RegWrite),
    .Write_2(MEM_RD), .ALU_Result_2(ALU_result), .MEN_PC(M_PC), .MEN_IR(MEM_IR), .PC_4_2(ex_1_pc_4_2),
    .R1_2(ex_1_r1_2), .R2_2(ex_1_r2_2), .sb(id_1_sb_2), .auipc(id_1_auipc_2), .sb_2(ex_1_sb_2),
    .auipc_2(ex_1_auipc_2), .U(id_1_u_2), .U_2(ex_1_u_2), .flush(1'b0));
  sb sb_1 (.in_1(ex_1_sb_2), .R2(ex_1_r2_2), .out_3(sb_1_out_3), .darta(sb_1_darta));
  not not_6 (not_6_out, ex_1_sb_2);
  Multiplexer #(.select(1), .width(32), .disabled("Z"), .enable("false")) multiplexer_8 (
    .in0(sb_1_darta), .in1(ex_1_r2_2), .out(MDin), .sel(not_6_out));
  // MIPS_RAM mips_ram_1: pin names not known; wires that end beside it: MDin, ALU_result[11:2], MemWrite, sb_1_out_3, CLK, RST, mips_ram_1_p7
  not not_7 (not_7_out, Stop);
  Mem mem_1 (
    .RST(RST), .JAL(ex_1_jal_2), .JALR(ex_1_jalr_2), .URET(ex_1_uret_2), .MemToReg(ex_1_memtoreg_2),
    .MenWrite(MemWrite), .ecall(ex_1_ecall_2), .RegWirte(MEN_RegWrite), .Write(MEM_RD),
    .ALU_Result(ALU_result), .Mem_PC(M_PC), .Mem_IR(MEM_IR), .PC_4(ex_1_pc_4_2), .R1(ex_1_r1_2),
    .R2(ex_1_r2_2), .CLK(CLK), .JAL_2(mem_1_jal_2), .JALR_2(mem_1_jalr_2), .MemToReg_2(MEN_MemtoReg),
    .ecall_2(WB_ecall), .RegWirte_2(RegWrite), .Write_2(WB_RD), .ALU_Result_2(mem_1_alu_result_2),
    .Mem_PC_2(WB_PC), .Mem_IR_2(WB_IR), .PC_4_2(WB_PC_4), .R1_2(WB_R1), .R2_2(WB_R2), .MData(mips_ram_1_p7),
    .halt(not_7_out), .Mdata_2(mem_1_mdata_2), .sb(ex_1_sb_2), .auipc(ex_1_auipc_2), .auipc_2(auipc),
    .u(ex_1_u_2), .u_2(mem_1_u_2), .flush(1'b0));  // open: URET_2, MemWrite, sb_2
  Multiplexer #(.select(1), .width(32), .disabled("Z"), .enable("false")) multiplexer_9 (
    .in0({32{1'b0}}), .in1(mem_1_u_2), .out(multiplexer_9_out), .sel(auipc));
  Multiplexer #(.select(1), .width(32), .disabled("Z"), .enable("false")) multiplexer_10 (
    .in0(mem_1_alu_result_2), .in1(mem_1_mdata_2), .out(multiplexer_10_out), .sel(MEN_MemtoReg));
  Adder #(.width(32)) adder_4 (.a(WB_PC), .b(32'h4), .out(adder_4_out));  // open: cin, cout
  or or_6 (or_6_out, mem_1_jalr_2, mem_1_jal_2);
  Multiplexer #(.select(1), .width(32), .disabled("Z"), .enable("false")) multiplexer_11 (
    .in0(multiplexer_10_out), .in1(adder_4_out), .out(multiplexer_11_out), .sel(or_6_out));
  Shifter #(.width(32), .shift("ll")) shifter_3 (.in(multiplexer_9_out), .\dist (5'b01100), .out(shifter_3_out));
  Multiplexer #(.select(1), .width(32), .disabled("Z"), .enable("false")) multiplexer_12 (
    .in0(multiplexer_11_out), .in1(U_adress), .out(RDin), .sel(auipc));
  Adder #(.width(32)) adder_5 (.a(shifter_3_out), .b(WB_PC), .out(U_adress));  // open: cin, cout
  Comparator #(.width(32), .mode("twosComplement")) comparator_2 (
    .a(WB_R1), .b(32'ha), .eq(comparator_2_eq));  // open: gt, lt
  not not_8 (not_8_out, halt);
  and and_6 (and_6_out, Go, halt);
  Comparator #(.width(32), .mode("twosComplement")) comparator_3 (
    .a(WB_R1), .b(32'h22), .eq(comparator_3_eq));  // open: gt, lt
  Register #(.width(32), .trigger("rising"), .Select("low")) register_1 (
    .D(WB_R2), .en(ecallEq), .Q(LedData), .clk(CLK), .clr(RST));
  Counter #(.width(16), .max('hffff), .ongoal("wrap"), .trigger("rising"), .behavior("new")) counter_2 (
    .count(not_8_out), .Q(\总周期数 ), .clk(CLK), .clr(RST));  // open: load, D, carry, preset, down
  Counter #(.width(1), .max('h1), .ongoal("stay"), .trigger("rising"), .behavior("new")) counter_3 (
    .D(and_6_out), .count(Stop), .Q(ecallFB), .clk(and_6_out), .clr(RST));  // open: load, carry, preset, down
  and and_7 (ecallEq, WB_ecall, comparator_3_eq);
  and and_8 (halt, WB_ecall, comparator_2_eq);

  // Other names for the same wires on the sheet: WDin[4:0] = ID_IR[11:7]; ID_IR[31:20] = I_imm; MEM_PC[31:0] = M_PC

  // Notes on the sheet:
  //   中断源
  //   中断等待指示
  //   数码管输出
  //   指令存储器
  //   控制位
  //   contents of rom_1 (hex, n*v repeats v):
  //   100493 100006f 100493 200913 300993 100006f 100493 200913 300993 100006f 100493 200913 300993
  //   100006f 100493 200913 300993 3e4000ef 100413 100493 1f49493 900533 2200893 73 24d493 48463 fedff06f
  //   900533 2200893 73 100493 249493 900533 2200893 73 48463 fedff06f 100493 1f49493 900533 2200893 73
  //   4034d493 900533 2200893 73 4044d493 900533 2200893 73 4044d493 900533 2200893 73 4044d493 900533
  //   2200893 73 4044d493 900533 2200893 73 4044d493 900533 2200893 73 4044d493 900533 2200893 73 4044d493
  //   900533 2200893 73 100413 1f41993 41f9d993 433 c00913 300b13 140413 f47413 800293 100313 499993
  //   89e9b3 1300533 2200893 73 406282b3 fe0294e3 140413 f00f93 1f47433 1c41413 800293 100313 49d993
  //   89e9b3 1300533 2200893 73 406282b3 fe0294e3 1c45413 406b0b33 b0463 f95ff06f 2b3 fff2c293 829293
  //   ff2e293 500533 2200893 73 fff00413 493 84a023 140413 448493 84a023 140413 448493 84a023 140413
  //   448493 84a023 140413 448493 84a023 140413 448493 84a023 140413 448493 84a023 140413 448493 84a023
  //   140413 448493 84a023 140413 448493 84a023 140413 448493 84a023 140413 448493 84a023 140413 448493
  //   84a023 140413 448493 84a023 140413 448493 84a023 140413 448493 84a023 140413 448493 140413 433
  //   3c00493 42983 4aa03 149a2b3 28663 134a023 1442023 ffc48493 fe9412e3 800533 2200893 73 440413 3c00493
  //   fc9416e3 a00893 73 313 2000e13 493 100913 930023 900533 2200893 73 12484b3 130313 fffe0e13 fe0e12e3
  //   800e13 313 32483 900533 2200893 73 430313 fffe0e13 fe0e14e3 a00893 73 13 430497 900533 2200893 73
  //   430497 900533 2200893 73 430497 900533 2200893 73 430497 900533 2200893 73 430497 900533 2200893 73
  //   430497 900533 2200893 73 430497 900533 2200893 73 430497 900533 2200893 73 a00893 73 fff00293 313
  //   1900413 841413 9700493 940533 2200893 73 5484b3 494b313 fe0306e3 a00893 73 ff100493 900533 2200893
  //   73 148493 fe9068e3 900533 2200893 73 a00893 73 413 140413 800533 2200893 73 240413 800533 2200893 73
  //   340413 800533 2200893 73 440413 800533 2200893 73 540413 800533 2200893 73 640413 800533 2200893 73
  //   740413 800533 2200893 73 840413 800533 2200893 2200893 73 8067
  //   流水调试日志用
  //   暂停节拍，不能为0
  //   可计数暂停的时钟源
  //   Beq
  //   Bne
  //   AluOP
  //   AluSrcB
  //   RegWrite
  //   MemToReg
  //   MemWrite
  //   为方便自动评测，需要输出流水线各段保存的PC值，注意是PC不是PC+4，另外ID段寄存器写入信息，Mem段内存写入信息也要输出
  //   数据存储器
  //   ecall比较$a7=?34
  //   ecallLED显示$a0
  //   ecall暂停
  //   ecall等待go按键
endmodule
module \重定向流水线  (
  output RegWrite,
  output MemWrite,
  output [31:0] IF_PC,
  output [31:0] ID_PC,
  output [31:0] EX_PC,
  output [31:0] M_PC,
  output [31:0] WB_PC,
  output [31:0] RDin,
  output [31:0] MDin,
  output [31:0] LedData
);

  wire alu_1_equal, alu_1_out_6, and_1_out, and_2_out, and_4_out, and_5_out, and_6_out, and_7_out, auipc,
       branchtaken, CLK, clock_1_out, comparator_1_eq, comparator_1_lt, comparator_2_eq, comparator_3_eq,
       comparator_4_eq, d_ff_1_q, datahazzrd, ecall, ecallEq, ex_1_auipc_2, ex_1_ecall_2, ex_1_jal_2,
       ex_1_jalr_2, ex_1_sb_2, ex_1_uret_2, EX_auipc, EX_ecall, EX_MemToReg, EX_RegWrite, flush, Go, GOOD,
       halt, id_1_alu_srcb_2, id_1_beq_2, id_1_bltu_2, id_1_bne_2, id_1_jal_2, id_1_jalr_2, id_1_memwrite_2,
       id_1_sb_2, id_1_uret_2, IR1, IR2, IR3, LoadUse, mem_1_jal_2, mem_1_jalr_2, MEN_MemToReg,
       MEN_MemtoReg_t, MEN_RegWrite, multiplexer_1_out, nand_1_out, not_1_out, not_2_out, not_3_out,
       not_4_out, not_5_out, not_6_out, not_7_out, not_8_out, not_9_out, not_10_out, or_1_out, or_2_out,
       or_4_out, or_5_out, rs1, rs2, RST, sltiu, stall, W1, W2, W3, WB_ecall, \单周期硬布线控制器_1_alu_src ,
       \单周期硬布线控制器_1_auipc , \单周期硬布线控制器_1_beq , \单周期硬布线控制器_1_bltu , \单周期硬布线控制器_1_bne , \单周期硬布线控制器_1_jal ,
       \单周期硬布线控制器_1_jalr , \单周期硬布线控制器_1_memtoreg , \单周期硬布线控制器_1_memwrite , \单周期硬布线控制器_1_regwrite ,
       \单周期硬布线控制器_1_s_type , \单周期硬布线控制器_1_sb , \单周期硬布线控制器_1_uret ;
  wire [1:0] id_1_rsfoward_2, id_1_rtfoward_2, RSfoward, RTfoward;
  wire [3:0] id_1_alu_op_2, sb_1_out_3, \单周期硬布线控制器_1_alu_op ;
  wire [4:0] EX_RD, MEM_RD, R1_num, R2_num, WB_RD;
  wire [11:0] I_imm, multiplexer_7_out;
  wire [12:0] CNT_num;
  wire [15:0] \LoadUse次数 , \总周期数 , \插入气泡数 , \无条件分支数 , \条件分支成功数 ;
  wire [19:0] ID_IR;
  wire [31:0] adder_1_out, adder_4_out, alu_1_result, ALU_result, bit_extender_1_out, bit_extender_2_out,
       bit_extender_3_out, bit_extender_4_out, Branch_Adress, ex_1_pc_4_2, ex_1_r1_2, ex_1_r2_2, ex_1_u_2,
       EX_IR, EX_R1, EX_R2, id_1_bm_2, id_1_im_2, id_1_jm_2, id_1_pc_4_2, id_1_u_2, ID_PC_4, IF_IR,
       JAL_Adress, JALR_Adress, mem_1_alu_result_2, mem_1_mdata_2, mem_1_u_2, MEM_IR, mips_ram_1_p7,
       multiplexer_2_out, multiplexer_3_out, multiplexer_4_out, multiplexer_10_out, multiplexer_12_out,
       multiplexer_13_out, multiplexer_14_out, re_R1, re_R2, regifile_1_r1, regifile_1_r2, sb_1_darta,
       shifter_1_out, shifter_2_out, shifter_3_out, U_adress, WB_IR, WB_PC_4, WB_R1, WB_R2;

  Button \u_总复位  (.out(RST));
  Button _1 (.out(IR1));
  Button _2 (.out(IR2));
  Button _3 (.out(IR3));
  // Probe on \总周期数 
  // Probe on \总周期数 
  Button \u_继续运行  (.out(Go));
  LED #(.active("true")) led_1 (.in(W1));
  LED #(.active("true")) led_2 (.in(W2));
  LED #(.active("true")) led_3 (.in(W3));
  not not_1 (not_1_out, EX_auipc);
  Multiplexer #(.select(1), .width(1), .disabled("Z"), .enable("false")) multiplexer_1 (
    .in0(EX_RegWrite), .in1(EX_MemToReg), .out(multiplexer_1_out), .sel(not_1_out));
  Hex_Digit_Display hex_digit_display_1 (.value(LedData[31:28]));  // open: dp
  // Probe on IF_PC[19:0]
  // RiscV_Probe riscv_probe_1: pin names not known; wires that end beside it: IF_IR
  foward foward_1 (
    .EX_WriteReg(EX_RD), .rs(R1_num), .EX_RegWrite(EX_RegWrite), .rsused(rs1), .EX_WriteReg_2(EX_RD),
    .MEM_WriteReg(MEM_RD), .rt(R2_num), .rs_2(R1_num), .EX_RegWrite_2(EX_RegWrite),
    .MEM_RegWrite(MEN_RegWrite), .rtused(rs2), .rsused_2(EX_RegWrite), .MEM_WriteReg_2(MEM_RD),
    .rt_2(R2_num), .MEM_RegWrite_2(MEN_RegWrite), .rtused_2(rs2), .RSFoward(RSfoward), .RTFoward(RTfoward));
  Hex_Digit_Display hex_digit_display_2 (.value(LedData[23:20]));  // open: dp
  Hex_Digit_Display hex_digit_display_3 (.value(LedData[27:24]));  // open: dp
  // Probe on ID_PC[19:0]
  // RiscV_Probe riscv_probe_2: pin names not known; wires that end beside it: {I_imm, ID_IR}
  Hex_Digit_Display hex_digit_display_4 (.value(LedData[19:16]));  // open: dp
  Hex_Digit_Display hex_digit_display_5 (.value(LedData[15:12]));  // open: dp
  loaduse loaduse_1 (
    .rsused(rs1), .rs(R1_num), .EX_WriteReg(EX_RD), .EX_MemRead(multiplexer_1_out), .rtused(rs2),
    .rt(R2_num), .EX_WriteReg_2(EX_RD), .EX_MemRead_2(multiplexer_1_out), .LoadUse(LoadUse));
  Hex_Digit_Display hex_digit_display_6 (.value(LedData[11:8]));  // open: dp
  Hex_Digit_Display hex_digit_display_7 (.value(LedData[7:4]));  // open: dp
  // Probe on EX_PC[19:0]
  // RiscV_Probe riscv_probe_3: pin names not known; wires that end beside it: EX_IR
  Hex_Digit_Display hex_digit_display_8 (.value(LedData[3:0]));  // open: dp
  // Probe on \总周期数 
  // Probe on M_PC[19:0]
  // RiscV_Probe riscv_probe_4: pin names not known; wires that end beside it: MEM_IR
  // Probe on \总周期数 
  // Probe on \无条件分支数 
  // Probe on \条件分支成功数 
  // Probe on \插入气泡数 
  // Probe on \LoadUse次数 
  // Probe on IF_PC[11:0]
  // Probe on WB_PC[19:0]
  // RiscV_Probe riscv_probe_5: pin names not known; wires that end beside it: WB_IR
  Multiplexer #(.select(1), .width(32), .disabled("Z"), .enable("false")) multiplexer_2 (
    .in0(adder_1_out), .in1(Branch_Adress), .out(multiplexer_2_out), .sel(or_4_out));
  // Probe on ID_PC[11:0]
  // Probe on EX_PC[11:0]
  // Probe on RDin
  Multiplexer #(.select(1), .width(32), .disabled("Z"), .enable("false")) multiplexer_3 (
    .in0(multiplexer_2_out), .in1(JAL_Adress), .out(multiplexer_3_out), .sel(id_1_jal_2));
  Adder #(.width(32)) adder_1 (.a(IF_PC), .b(32'h4), .out(adder_1_out));  // open: cin, cout
  datahazzard datahazzard_1 (
    .RtUsed(rs1), .Rt(R1_num), .Rt_2(R1_num), .MEN_WriteReg(MEM_RD), .MEN_Regwrite(MEN_RegWrite),
    .RtUsed_2(rs1), .Rt_3(R1_num), .Rt_4(R1_num), .EX_WriteReg(EX_RD), .EX_Regwrite(EX_RegWrite),
    .RsUsed(rs2), .Rs(R2_num), .Rs_2(R2_num), .EX_WriteReg_2(EX_RD), .EX_Regwrite_2(EX_RegWrite),
    .RsUsed_2(rs2), .Rs_3(R2_num), .Rs_4(R2_num), .MEN_WriteReg_2(MEM_RD), .MEN_Regwrite_2(MEN_RegWrite),
    .datahazzed(datahazzrd));
  // Probe on M_PC[11:0]
  D_Flip_Flop #(.trigger("high"), .Pre_Clr_Positions("LEGACY"), .NegatePresetClear("false"), .enable("true"), .NewFFLayout("false")) d_ff_1 (.Q(d_ff_1_q));  // open: clk, D, Qn, preset, en, reset
  // Probe on 13'ha8e
  Multiplexer #(.select(1), .width(32), .disabled("Z"), .enable("false")) multiplexer_4 (
    .in0(multiplexer_3_out), .in1(JALR_Adress), .out(multiplexer_4_out), .sel(id_1_jalr_2));
  and and_1 (and_1_out, not_3_out, not_2_out);
  not not_2 (not_2_out, LoadUse);
  not not_3 (not_3_out, halt);
  // Probe on WB_PC[11:0]
  Comparator #(.width(13), .mode("twosComplement")) comparator_1 (
    .a(CNT_num), .b(13'ha8e), .eq(comparator_1_eq), .lt(comparator_1_lt));  // open: gt
  Clock #(.highDuration(1), .lowDuration(1)) clock_1 (.out(clock_1_out));
  Register #(.width(32), .trigger("rising"), .Select("low")) PC (
    .D(multiplexer_4_out), .en(and_1_out), .Q(IF_PC), .clk(CLK), .clr(RST));
  \气泡处理  \u_气泡处理_1  (
    .datahazzd(datahazzrd), .branch(branchtaken), .datahazzd_2(datahazzrd), .stall(stall), .flush(flush));
  nand nand_1 (nand_1_out, d_ff_1_q, comparator_1_eq);
  Counter #(.width(13), .max('h1fff), .ongoal("stay"), .trigger("rising"), .behavior("old")) counter_1 (
    .count(comparator_1_lt), .Q(CNT_num), .clk(clock_1_out));  // open: load, D, carry, clr, preset
  assign CLK = nand_1_out ? clock_1_out : 1'bz;  // Controlled_Buffer controlled_buffer_1
  Pull_Resistor #(.pull(1)) pull_resistor_1 (.node(CLK));
  ROM #(.addrWidth(10), .dataWidth(32), .Select("high")) rom_1 (.addr(IF_PC[11:2]), .data(IF_IR));
  not not_4 (not_4_out, halt);
  or or_1 (or_1_out, RST, branchtaken);
  // RiscV_Probe riscv_probe_6: pin names not known; wires that end beside it: IF_IR
  IF if_1 (
    .CLK(CLK), .RST(or_1_out), .IR(IF_IR), .PC(IF_PC), .PC_4(adder_1_out), .IR_2({I_imm, ID_IR}),
    .PC_2(ID_PC), .PC_4_2(ID_PC_4), .flush(1'b0), .en(and_2_out));
  and and_2 (and_2_out, not_4_out, not_5_out);
  not not_5 (not_5_out, LoadUse);
  \单周期硬布线控制器  \u_单周期硬布线控制器_1  (
    .Funct({I_imm[10], I_imm[5], ID_IR[14:12]}), .OP(ID_IR[6:2]), .ALU_OP(\单周期硬布线控制器_1_alu_op ),
    .MemToReg(\单周期硬布线控制器_1_memtoreg ), .MemWrite(\单周期硬布线控制器_1_memwrite ), .ALU_SRC(\单周期硬布线控制器_1_alu_src ),
    .RegWrite(\单周期硬布线控制器_1_regwrite ), .ecall(ecall), .S_type(\单周期硬布线控制器_1_s_type ),
    .Jalr(\单周期硬布线控制器_1_jalr ), .Beq(\单周期硬布线控制器_1_beq ), .JAL(\单周期硬布线控制器_1_jal ), .Bne(\单周期硬布线控制器_1_bne ),
    .in_3(I_imm[1]), .uret(\单周期硬布线控制器_1_uret ), .sb(\单周期硬布线控制器_1_sb ), .auipc(\单周期硬布线控制器_1_auipc ),
    .bltu(\单周期硬布线控制器_1_bltu ), .sltiu(sltiu), .rs1(rs1), .rs2(rs2));  // open: CSRRSI, CSRRCI
  Multiplexer #(.select(1), .width(5), .disabled("Z"), .enable("false")) multiplexer_5 (
    .in0(ID_IR[19:15]), .in1(5'b10001), .out(R1_num), .sel(ecall));
  Multiplexer #(.select(1), .width(5), .disabled("Z"), .enable("false")) multiplexer_6 (
    .in0(I_imm[4:0]), .in1(5'b01010), .out(R2_num), .sel(ecall));
  Multiplexer #(.select(1), .width(12), .disabled("Z"), .enable("false")) multiplexer_7 (
    .in0(I_imm), .in1({I_imm[11:5], ID_IR[11:7]}), .out(multiplexer_7_out), .sel(\单周期硬布线控制器_1_s_type ));
  assign bit_extender_1_out = {{20{I_imm[11]}}, {I_imm[11], ID_IR[7], I_imm[10:5], ID_IR[11:8]}};  // Bit_Extender bit_extender_1
  assign bit_extender_2_out = {{12{I_imm[11]}}, {I_imm[11], ID_IR[19:12], I_imm[0], I_imm[10:1]}};  // Bit_Extender bit_extender_2
  assign bit_extender_3_out = {{12{1'b0}}, {I_imm, ID_IR[19:12]}};  // Bit_Extender bit_extender_3
  Regifile regifile_1 (
    .Din(RDin), .Clk(CLK), .R1(regifile_1_r1), .R2(regifile_1_r2), .WE(RegWrite), .W_num(WB_RD),
    .R1_num(R1_num), .R2_num(R2_num));
  assign bit_extender_4_out = {{20{multiplexer_7_out[11]}}, multiplexer_7_out};  // Bit_Extender bit_extender_4
  or or_2 (or_2_out, RST, branchtaken, LoadUse);
  ID id_1 (
    .RST(or_2_out), .beq(\单周期硬布线控制器_1_beq ), .bne(\单周期硬布线控制器_1_bne ), .MemToReg(\单周期硬布线控制器_1_memtoreg ),
    .MemWrite(\单周期硬布线控制器_1_memwrite ), .ALU_OP(\单周期硬布线控制器_1_alu_op ), .ALU_SRCB(\单周期硬布线控制器_1_alu_src ),
    .RegWrite(\单周期硬布线控制器_1_regwrite ), .JAL(\单周期硬布线控制器_1_jal ), .JALR(\单周期硬布线控制器_1_jalr ),
    .URET(\单周期硬布线控制器_1_uret ), .ID_PC(ID_PC), .r1(regifile_1_r1), .r2(regifile_1_r2),
    .Bm(bit_extender_1_out), .Jm(bit_extender_2_out), .PC_4(ID_PC_4), .CLK(CLK), .beq_2(id_1_beq_2),
    .bne_2(id_1_bne_2), .MemToReg_2(EX_MemToReg), .MemWrite_2(id_1_memwrite_2), .ALU_OP_2(id_1_alu_op_2),
    .ALU_SRCB_2(id_1_alu_srcb_2), .RegWrite_2(EX_RegWrite), .JAL_2(id_1_jal_2), .JALR_2(id_1_jalr_2),
    .URET_2(id_1_uret_2), .ID_PC_2(EX_PC), .r1_2(EX_R1), .r2_2(EX_R2), .Bm_2(id_1_bm_2), .Jm_2(id_1_jm_2),
    .PC_4_2(id_1_pc_4_2), .ID_IR({I_imm, ID_IR}), .ID_IR_2(EX_IR), .ecall(ecall), .ecall_2(EX_ecall),
    .WRD(ID_IR[11:7]), .WRD_2(EX_RD), .Im(bit_extender_4_out), .Im_2(id_1_im_2), .halt(halt),
    .auipc(\单周期硬布线控制器_1_auipc ), .bltu(\单周期硬布线控制器_1_bltu ), .sb(\单周期硬布线控制器_1_sb ), .bltu_2(id_1_bltu_2),
    .auipc_2(EX_auipc), .sb_2(id_1_sb_2), .u(bit_extender_3_out), .u_2(id_1_u_2), .flush(1'b0),
    .RsFoward(RSfoward), .RtFoward(RTfoward), .RsFoward_2(id_1_rsfoward_2), .Rtfoward_2(id_1_rtfoward_2));  // open: S_type, S_type_2
  Multiplexer #(.select(2), .width(32), .disabled("Z"), .enable("false")) multiplexer_8 (
    .in0(EX_R1), .in1(RDin), .in2(ALU_result), .out(re_R1), .sel(id_1_rsfoward_2));  // open: in3
  Multiplexer #(.select(2), .width(32), .disabled("Z"), .enable("false")) multiplexer_9 (
    .in0(EX_R2), .in1(RDin), .in2(ALU_result), .out(re_R2), .sel(id_1_rtfoward_2));  // open: in3
  Shifter #(.width(32), .shift("ll")) shifter_1 (.in(id_1_bm_2), .\dist (5'b00001), .out(shifter_1_out));
  Shifter #(.width(32), .shift("ll")) shifter_2 (.in(id_1_jm_2), .\dist (5'b00001), .out(shifter_2_out));
  Adder #(.width(32)) adder_2 (.a(shifter_1_out), .b(EX_PC), .out(Branch_Adress));  // open: cin, cout
  Adder #(.width(32)) adder_3 (.a(shifter_2_out), .b(EX_PC), .out(JAL_Adress));  // open: cin, cout
  Multiplexer #(.select(1), .width(32), .disabled("Z"), .enable("false")) multiplexer_10 (
    .in0(re_R2), .in1(id_1_im_2), .out(multiplexer_10_out), .sel(id_1_alu_srcb_2));
  ALU alu_1 (
    .X(re_R1), .Y(multiplexer_10_out), .AluOP(id_1_alu_op_2), .Equal(alu_1_equal), .Result(alu_1_result),
    .out_6(alu_1_out_6));  // open: Result_2, out_4
  assign JALR_Adress = alu_1_result & 32'hfffffffe;  // AND_Gate and_3, 32 bits wide
  or or_3 (branchtaken, id_1_jalr_2, id_1_jal_2, or_4_out);
  and and_4 (and_4_out, id_1_bltu_2, alu_1_out_6);
  not not_6 (not_6_out, alu_1_equal);
  or or_4 (or_4_out, and_4_out, and_6_out, and_5_out);
  and and_5 (and_5_out, id_1_beq_2, alu_1_equal);
  and and_6 (and_6_out, not_6_out, id_1_bne_2);
  not not_7 (not_7_out, halt);
  EX ex_1 (
    .RST(RST), .JAL(id_1_jal_2), .JALR(id_1_jalr_2), .URET(id_1_uret_2), .MemToReg(EX_MemToReg),
    .MenWrite(id_1_memwrite_2), .ecall(EX_ecall), .RegWirte(EX_RegWrite), .Write(EX_RD),
    .ALU_Result(alu_1_result), .EX_PC(EX_PC), .EX_IR(EX_IR), .PC_4(id_1_pc_4_2), .R1(re_R1), .R2(re_R2),
    .halt(not_7_out), .CLK(CLK), .JAL_2(ex_1_jal_2), .JALR_2(ex_1_jalr_2), .URET_2(ex_1_uret_2),
    .MemToReg_2(MEN_MemToReg), .MemWrite(MemWrite), .ecall_2(ex_1_ecall_2), .RegWirte_2(MEN_RegWrite),
    .Write_2(MEM_RD), .ALU_Result_2(ALU_result), .MEN_PC(M_PC), .MEN_IR(MEM_IR), .PC_4_2(ex_1_pc_4_2),
    .R1_2(ex_1_r1_2), .R2_2(ex_1_r2_2), .sb(id_1_sb_2), .auipc(EX_auipc), .sb_2(ex_1_sb_2),
    .auipc_2(ex_1_auipc_2), .U(id_1_u_2), .U_2(ex_1_u_2), .flush(1'b0));
  sb sb_1 (.in_1(ex_1_sb_2), .R2(ex_1_r2_2), .out_3(sb_1_out_3), .darta(sb_1_darta));
  not not_8 (not_8_out, ex_1_sb_2);
  Multiplexer #(.select(1), .width(32), .disabled("Z"), .enable("false")) multiplexer_11 (
    .in0(sb_1_darta), .in1(ex_1_r2_2), .out(MDin), .sel(not_8_out));
  // MIPS_RAM mips_ram_1: pin names not known; wires that end beside it: MDin, ALU_result[11:2], MemWrite, sb_1_out_3, CLK, RST, mips_ram_1_p7
  and and_7 (and_7_out, ~Go, halt);  // AND_Gate
  Mem mem_1 (
    .RST(RST), .JAL(ex_1_jal_2), .JALR(ex_1_jalr_2), .URET(ex_1_uret_2), .MemToReg(MEN_MemToReg),
    .MenWrite(MemWrite), .ecall(ex_1_ecall_2), .RegWirte(MEN_RegWrite), .Write(MEM_RD),
    .ALU_Result(ALU_result), .Mem_PC(M_PC), .Mem_IR(MEM_IR), .PC_4(ex_1_pc_4_2), .R1(ex_1_r1_2),
    .R2(ex_1_r2_2), .CLK(CLK), .JAL_2(mem_1_jal_2), .JALR_2(mem_1_jalr_2), .MemToReg_2(MEN_MemtoReg_t),
    .ecall_2(WB_ecall), .RegWirte_2(RegWrite), .Write_2(WB_RD), .ALU_Result_2(mem_1_alu_result_2),
    .Mem_PC_2(WB_PC), .Mem_IR_2(WB_IR), .PC_4_2(WB_PC_4), .R1_2(WB_R1), .R2_2(WB_R2), .MData(mips_ram_1_p7),
    .halt(and_7_out), .Mdata_2(mem_1_mdata_2), .sb(ex_1_sb_2), .auipc(ex_1_auipc_2), .auipc_2(auipc),
    .u(ex_1_u_2), .u_2(mem_1_u_2), .flush(1'b0));  // open: URET_2, MemWrite, sb_2
  Adder #(.width(32)) adder_4 (.a(WB_PC), .b(32'h4), .out(adder_4_out));  // open: cin, cout
  Multiplexer #(.select(1), .width(32), .disabled("Z"), .enable("false")) multiplexer_12 (
    .in0({32{1'b0}}), .in1(mem_1_u_2), .out(multiplexer_12_out), .sel(auipc));
  Multiplexer #(.select(1), .width(32), .disabled("Z"), .enable("false")) multiplexer_13 (
    .in0(mem_1_alu_result_2), .in1(mem_1_mdata_2), .out(multiplexer_13_out), .sel(MEN_MemtoReg_t));
  Shifter #(.width(32), .shift("ll")) shifter_3 (.in(multiplexer_12_out), .\dist (5'b01100), .out(shifter_3_out));
  or or_5 (or_5_out, mem_1_jalr_2, mem_1_jal_2);
  Multiplexer #(.select(1), .width(32), .disabled("Z"), .enable("false")) multiplexer_14 (
    .in0(multiplexer_13_out), .in1(adder_4_out), .out(multiplexer_14_out), .sel(or_5_out));
  Multiplexer #(.select(1), .width(32), .disabled("Z"), .enable("false")) multiplexer_15 (
    .in0(multiplexer_14_out), .in1(U_adress), .out(RDin), .sel(auipc));
  Adder #(.width(32)) adder_5 (.a(shifter_3_out), .b(WB_PC), .out(U_adress));  // open: cin, cout
  not not_9 (not_9_out, Go);
  Comparator #(.width(32), .mode("twosComplement")) comparator_2 (
    .a(WB_R1), .b(32'h22), .eq(comparator_2_eq));  // open: gt, lt
  Comparator #(.width(32), .mode("twosComplement")) comparator_3 (
    .a(WB_R1), .b(32'ha), .eq(comparator_3_eq));  // open: gt, lt
  Register #(.width(32), .trigger("rising"), .Select("low")) register_1 (
    .D(re_R2), .en(ecallEq), .Q(LedData), .clk(CLK), .clr(RST));
  not not_10 (not_10_out, halt);
  Counter #(.width(16), .max('hffff), .ongoal("wrap"), .trigger("rising"), .behavior("new")) counter_2 (
    .count(not_10_out), .Q(\总周期数 ), .clk(CLK), .clr(RST));  // open: load, D, carry, preset, down
  and and_8 (GOOD, WB_ecall, comparator_2_eq);
  and and_9 (halt, WB_ecall, not_9_out, comparator_3_eq);
  Comparator #(.width(32), .mode("twosComplement")) comparator_4 (
    .a(re_R1), .b(32'h22), .eq(comparator_4_eq));  // open: gt, lt
  and and_10 (ecallEq, EX_ecall, comparator_4_eq);

  // Other names for the same wires on the sheet: WDin[4:0] = ID_IR[11:7]; ID_IR[31:20] = I_imm; MEM_PC[31:0] = M_PC

  // Notes on the sheet:
  //   中断源
  //   时空图监测，可删除
  //   当使用regwrite时能通过auipc
  //   中断等待指示
  //   数码管输出
  //   控制位
  //   流水调试日志用
  //   暂停节拍，不能为0
  //   戳工具置1进入计数暂停模式，ctrl+k时钟自动运行到对应节拍暂停
  //   ctrl+k关闭时钟连续运行，将控制位置零，进入单步调试模式调试
  //   可计数暂停的时钟源
  //   指令存储器
  //   contents of rom_1 (hex, n*v repeats v):
  //   100493 100006f 100493 200913 300993 100006f 100493 200913 300993 100006f 100493 200913 300993
  //   100006f 100493 200913 300993 3e4000ef 100413 100493 1f49493 900533 2200893 73 24d493 48463 fedff06f
  //   900533 2200893 73 100493 249493 900533 2200893 73 48463 fedff06f 100493 1f49493 900533 2200893 73
  //   4034d493 900533 2200893 73 4044d493 900533 2200893 73 4044d493 900533 2200893 73 4044d493 900533
  //   2200893 73 4044d493 900533 2200893 73 4044d493 900533 2200893 73 4044d493 900533 2200893 73 4044d493
  //   900533 2200893 73 100413 1f41993 41f9d993 433 c00913 300b13 140413 f47413 800293 100313 499993
  //   89e9b3 1300533 2200893 73 406282b3 fe0294e3 140413 f00f93 1f47433 1c41413 800293 100313 49d993
  //   89e9b3 1300533 2200893 73 406282b3 fe0294e3 1c45413 406b0b33 b0463 f95ff06f 2b3 fff2c293 829293
  //   ff2e293 500533 2200893 73 fff00413 493 84a023 140413 448493 84a023 140413 448493 84a023 140413
  //   448493 84a023 140413 448493 84a023 140413 448493 84a023 140413 448493 84a023 140413 448493 84a023
  //   140413 448493 84a023 140413 448493 84a023 140413 448493 84a023 140413 448493 84a023 140413 448493
  //   84a023 140413 448493 84a023 140413 448493 84a023 140413 448493 84a023 140413 448493 140413 433
  //   3c00493 42983 4aa03 149a2b3 28663 134a023 1442023 ffc48493 fe9412e3 800533 2200893 73 440413 3c00493
  //   fc9416e3 a00893 73 313 2000e13 493 100913 930023 900533 2200893 73 12484b3 130313 fffe0e13 fe0e12e3
  //   800e13 313 32483 900533 2200893 73 430313 fffe0e13 fe0e14e3 a00893 73 13 430497 900533 2200893 73
  //   430497 900533 2200893 73 430497 900533 2200893 73 430497 900533 2200893 73 430497 900533 2200893 73
  //   430497 900533 2200893 73 430497 900533 2200893 73 430497 900533 2200893 73 a00893 73 fff00293 313
  //   1900413 841413 9700493 940533 2200893 73 5484b3 494b313 fe0306e3 a00893 73 ff100493 900533 2200893
  //   73 148493 fe9068e3 900533 2200893 73 a00893 73 413 140413 800533 2200893 73 240413 800533 2200893 73
  //   340413 800533 2200893 73 440413 800533 2200893 73 540413 800533 2200893 73 640413 800533 2200893 73
  //   740413 800533 2200893 73 840413 800533 2200893 2200893 73 8067
  //   为方便自动评测，需要输出流水线各段保存的PC值，注意是PC不是PC+4，另外ID段寄存器写入信息，Mem段内存写入信息也要输出
  //   Beq
  //   Bne
  //   MemToReg
  //   MemWrite
  //   AluOP
  //   AluSrcB
  //   RegWrite
  //   数据存储器
  //   ecall暂停
  //   ecall比较$a7=?34
  //   ecallLED显示$a0
endmodule

module \动态分支流水线  (
  input  IR1,
  input  IR2,
  input  IR3,
  output RegWrite,
  output MemWrite,
  output [31:0] IF_PC,
  output [31:0] ID_PC,
  output [31:0] EX_PC,
  output [31:0] M_PC,
  output [31:0] WB_PC,
  output [31:0] RDin,
  output [31:0] MDin,
  output [31:0] LedData
);

  wire and_1_out, and_2_out, and_4_out, and_5_out, and_6_out, and_7_out, and_8_out, and_9_out, and_10_out,
       and_11_out, and_12_out, and_13_out, and_15_out, and_16_out, and_17_out, blow, BLTU, Branch,
       BranchTaken, CLK, clock_1_out, comparator_1_eq, comparator_1_lt, comparator_2_eq, comparator_3_eq,
       d_ff_1_q, d_ff_2_q, d_ff_3_q, d_ff_4_q, decoder_1_out1, decoder_1_out2, decoder_1_out3, ecall, EN,
       equal, EX_Beq, EX_BLTU, EX_Bne, EX_ecall, EX_LHU, ex_mem_1_bltuout, ex_mem_1_haltout,
       ex_mem_1_jampout, ex_mem_1_lhuout, ex_mem_1_luiout, ex_mem_1_memtoregout, ex_mem_1_uretout,
       EX_PredictErr, EX_PredictJump, EX_RegWrite_num, EXlode, Go, halt, id_ex_1_alusrcbout, id_ex_1_luiout,
       id_ex_1_memtoregout, id_ex_1_memwriteout, id_ex_1_s_typeout, id_ex_1_uretout, ID_JAL, ID_JALR,
       ID_PredictJump, ID_URET, IE_q, Inter1, Inter2, Inter3, Interr, Interrupt, IR1_t, IR2_t, IR3_t, IRA,
       IRB, IRC, JAL, JALR, LHU, Load_Use, LUI, MEM_RegWrite_num, mem_wb_1_haltout, mem_wb_1_jampout,
       mem_wb_1_memtoregout, nand_1_out, not_1_out, not_2_out, not_3_out, not_4_out, not_5_out, not_6_out,
       not_7_out, not_8_out, not_10_out, not_11_out, not_12_out, not_13_out, not_15_out, not_16_out,
       or_2_out, or_3_out, or_4_out, or_8_out, or_11_out, or_12_out, or_14_out, or_15_out, or_18_out,
       or_19_out, or_20_out, or_21_out, PredictJump, Ret1, Ret2, Ret3, RST, RST_num, URET, W1, W2, W3, \冲突 ,
       \单周期硬布线控制器_1_alu_src , \单周期硬布线控制器_1_auipc , \单周期硬布线控制器_1_beq , \单周期硬布线控制器_1_bltu , \单周期硬布线控制器_1_bne ,
       \单周期硬布线控制器_1_memtoreg , \单周期硬布线控制器_1_memwrite , \单周期硬布线控制器_1_regwrite , \单周期硬布线控制器_1_s_type ,
       \单周期硬布线控制器_1_sb ;
  wire [1:0] id_ex_1_r1forwardout, id_ex_1_r2forwardout, priority_encoder_1_out, R1Forward, R2Forward,
       \中断号_q ;
  wire [3:0] id_ex_1_aluopout, \单周期硬布线控制器_1_alu_op ;
  wire [4:0] EX_W_num, ID_Funct, ID_R1_num, ID_R2_num, MEM_W_num, W_num;
  wire [12:0] CNT_num;
  wire [15:0] adder_3_out, \LoadUse次数 , shifter_4_out, \分支预测成功数 , \总周期数 , \插入气泡数 , \无条件分支数 , \条件分支成功数 ;
  wire [31:0] adder_1_out, adder_4_out, adder_5_out, adder_7_out, and_3_out, and_14_out, bit_extender_1_out,
       bit_extender_2_out, bit_extender_3_out, bit_extender_4_out, bit_extender_5_out, BranchAddr, EPC,
       EX_IR, ex_mem_1_imm_lui_out, EX_R1, EX_R2, id_ex_1_imm_b_out, id_ex_1_imm_i_out, id_ex_1_imm_j_out,
       id_ex_1_imm_lui_out, id_ex_1_imm_s_out, id_ex_1_r1out, id_ex_1_r2out, ID_IR, ID_R1, ID_R2, IF_IR,
       IF_PC_4, Imm_lui, InterAddr, MEM_IR, MEM_Result, mem_wb_1_resultout, mem_wb_1_rmdataout,
       multiplexer_1_out, multiplexer_2_out, multiplexer_7_out, multiplexer_8_out, multiplexer_9_out,
       multiplexer_10_out, multiplexer_12_out, multiplexer_14_out, multiplexer_15_out, multiplexer_16_out,
       multiplexer_17_out, PCout, ram_1_data, Result, shifter_1_out, shifter_2_out, shifter_3_out, WB_IR;

  Button \u_总复位  (.out(RST));
  Button _1 (.out(IRA));
  Button _2 (.out(IRB));
  Button _3 (.out(IRC));
  // Probe on \总周期数 
  // Probe on \总周期数 
  Button \u_继续运行  (.out(Go));
  LED #(.active("true")) led_1 (.in(W1));
  LED #(.active("true")) led_2 (.in(W2));
  LED #(.active("true")) led_3 (.in(W3));
  Hex_Digit_Display hex_digit_display_1 (.value(LedData[31:28]));  // open: dp
  // Probe on IF_PC[19:0]
  // RiscV_Probe riscv_probe_1: pin names not known; wires that end beside it: IF_IR
  Hex_Digit_Display hex_digit_display_2 (.value(LedData[23:20]));  // open: dp
  Hex_Digit_Display hex_digit_display_3 (.value(LedData[27:24]));  // open: dp
  // Probe on ID_PC[19:0]
  // RiscV_Probe riscv_probe_2: pin names not known; wires that end beside it: {ID_IR[31], ID_Funct[4], ID_IR[29:26], ID_Funct[3], ID_IR[24:15], ID_Funct[2:0], ID_IR[11:0]}
  or or_1 (IR1_t, IR1, IRA);
  Adder #(.width(32)) adder_1 (.a(EX_PC), .b(32'h4), .out(adder_1_out));  // open: cin, cout
  or or_2 (or_2_out, BranchTaken, and_1_out);
  and and_1 (and_1_out, JAL, ~JALR);  // AND_Gate
  and and_2 (and_2_out, JAL, ~JALR);  // AND_Gate
  Hex_Digit_Display hex_digit_display_4 (.value(LedData[19:16]));  // open: dp
  Hex_Digit_Display hex_digit_display_5 (.value(LedData[15:12]));  // open: dp
  or or_3 (or_3_out, Branch, JAL, JALR);
  assign and_3_out = Result & 32'hfffffffe;  // AND_Gate and_3, 32 bits wide
  \分支预测  \u_分支预测_1  (
    .CLK(CLK), .EX_Jalr(JALR), .PC(IF_PC), .EX_PC(EX_PC), .EX_jalrAddr(and_3_out), .en(EN),
    .EX_GuessJ(EX_PredictJump), .PC_4(IF_PC_4), .EX_PC_4(adder_1_out), .EX_JumpAddr(BranchAddr),
    .EX_BranchTaken(or_2_out), .EX_Branch(or_4_out), .IR(IF_IR), .PCout(PCout), .GuessJ(PredictJump),
    .Ex_PredictErr(EX_PredictErr));
  or or_4 (or_4_out, Branch, and_2_out);
  Hex_Digit_Display hex_digit_display_6 (.value(LedData[11:8]));  // open: dp
  Hex_Digit_Display hex_digit_display_7 (.value(LedData[7:4]));  // open: dp
  // Probe on EX_PC[19:0]
  // RiscV_Probe riscv_probe_3: pin names not known; wires that end beside it: EX_IR
  and and_4 (and_4_out, or_3_out, ~EX_PredictErr);  // AND_Gate
  or or_5 (IR2_t, IR2, IRB);
  Multiplexer #(.select(1), .width(32), .disabled("Z"), .enable("false")) multiplexer_1 (
    .in0(multiplexer_2_out), .in1(EPC), .out(multiplexer_1_out), .sel(URET));
  Multiplexer #(.select(1), .width(32), .disabled("Z"), .enable("false")) multiplexer_2 (
    .in0(PCout), .in1(InterAddr), .out(multiplexer_2_out), .sel(Interrupt));
  Hex_Digit_Display hex_digit_display_8 (.value(LedData[3:0]));  // open: dp
  // Probe on \分支预测成功数 
  Counter #(.width(16), .max('hffff), .ongoal("wrap"), .trigger("rising"), .behavior("new")) counter_1 (
    .count(and_4_out), .Q(\分支预测成功数 ), .clk(CLK), .clr(RST));  // open: load, D, carry, preset, down
  // Probe on \总周期数 
  // Probe on M_PC[19:0]
  // RiscV_Probe riscv_probe_4: pin names not known; wires that end beside it: MEM_IR
  or or_6 (IR3_t, IR3, IRC);
  // Probe on \总周期数 
  // Probe on \无条件分支数 
  // Probe on \条件分支成功数 
  // Probe on \插入气泡数 
  // Probe on \LoadUse次数 
  // Probe on IF_PC[11:0]
  // Probe on WB_PC[19:0]
  // RiscV_Probe riscv_probe_5: pin names not known; wires that end beside it: WB_IR
  // Probe on RDin
  Register #(.width(32), .trigger("rising"), .Select("low")) PC (
    .D(multiplexer_1_out), .en(and_5_out), .Q(IF_PC), .clk(CLK), .clr(RST));
  and and_5 (and_5_out, not_1_out, not_2_out);
  not not_1 (not_1_out, Load_Use);
  not not_2 (not_2_out, halt);
  // Probe on ID_PC[11:0]
  // Probe on EX_PC[11:0]
  D_Flip_Flop #(.trigger("rising"), .Pre_Clr_Positions("LEGACY"), .NegatePresetClear("false"), .enable("true"), .NewFFLayout("false")) d_ff_1 (
    .clk(IR1_t), .D(1'b1), .Q(d_ff_1_q), .reset(Inter1));  // open: Qn, preset, en
  or or_7 (W1, Inter1, d_ff_1_q);
  // Probe on M_PC[11:0]
  D_Flip_Flop #(.trigger("high"), .Pre_Clr_Positions("LEGACY"), .NegatePresetClear("false"), .enable("true"), .NewFFLayout("false")) d_ff_2 (.Q(d_ff_2_q));  // open: clk, D, Qn, preset, en, reset
  // Probe on 13'hc
  or or_8 (or_8_out, d_ff_1_q, Inter1);
  Adder #(.width(32)) adder_2 (.a(IF_PC), .b(32'h4), .out(IF_PC_4));  // open: cin, cout
  // Probe on WB_PC[11:0]
  Comparator #(.width(13), .mode("twosComplement")) comparator_1 (
    .a(CNT_num), .b(13'hc), .eq(comparator_1_eq), .lt(comparator_1_lt));  // open: gt
  Clock #(.highDuration(1), .lowDuration(1)) clock_1 (.out(clock_1_out));
  and and_6 (and_6_out, or_8_out, ~Ret1);  // AND_Gate
  // Probe on multiplexer_1_out[11:2]
  nand nand_1 (nand_1_out, d_ff_2_q, comparator_1_eq);
  Counter #(.width(13), .max('h1fff), .ongoal("stay"), .trigger("rising"), .behavior("old")) counter_2 (
    .count(comparator_1_lt), .Q(CNT_num), .clk(clock_1_out), .clr(RST));  // open: load, D, carry, preset
  D_Flip_Flop #(.trigger("rising"), .Pre_Clr_Positions("LEGACY"), .NegatePresetClear("false"), .enable("true"), .NewFFLayout("false")) u_IR1 (
    .clk(CLK), .D(and_6_out), .Q(Inter1), .en(EXlode), .reset(RST));  // open: Qn, preset
  \冲突处理逻辑_重定向  \u_冲突处理逻辑_重定向_1  (
    .ID_R1_num(ID_R1_num), .EX_W_num(EX_W_num), .EX_RegWrite(EX_RegWrite_num), .EX_OP(EX_IR[6:2]),
    .ID_R2_num(ID_R2_num), .MEM_W_num(MEM_W_num), .MEM_RegWrite(MEM_RegWrite_num), .OP(ID_IR[6:2]),
    .Funct(ID_Funct), .\数据冲突 (\冲突 ), .R1Forward(R1Forward), .Load_Use(Load_Use), .R2Forward(R2Forward));
  ROM #(.addrWidth(10), .dataWidth(32), .Select("high")) rom_1 (.addr(IF_PC[11:2]), .data(IF_IR));
  not not_3 (not_3_out, Load_Use);
  assign CLK = nand_1_out ? clock_1_out : 1'bz;  // Controlled_Buffer controlled_buffer_1
  or or_9 (RST_num, RST, Interrupt, URET, JALR, EX_PredictErr);
  IF_ID if_id_1 (
    .PCin(IF_PC), .IRin(IF_IR), .PredictJumpin(PredictJump), .PCout(ID_PC),
    .IRout({ID_IR[31], ID_Funct[4], ID_IR[29:26], ID_Funct[3], ID_IR[24:15], ID_Funct[2:0], ID_IR[11:0]}),
    .PredictJumpout(ID_PredictJump), .RST(RST_num), .EN(and_7_out), .CLK(CLK), .RST_num(RST));
  and and_7 (and_7_out, not_3_out, EN);
  Pull_Resistor #(.pull(1)) pull_resistor_1 (.node(CLK));
  or or_10 (W2, Inter2, d_ff_3_q);
  // RiscV_Probe riscv_probe_6: pin names not known; wires that end beside it: {ID_IR[31], ID_Funct[4], ID_IR[29:26], ID_Funct[3], ID_IR[24:15], ID_Funct[2:0], ID_IR[11:0]}
  D_Flip_Flop #(.trigger("rising"), .Pre_Clr_Positions("LEGACY"), .NegatePresetClear("false"), .enable("true"), .NewFFLayout("false")) d_ff_3 (
    .clk(IR2_t), .D(1'b1), .Q(d_ff_3_q), .reset(Inter2));  // open: Qn, preset, en
  or or_11 (or_11_out, d_ff_3_q, Inter2);
  assign bit_extender_1_out = {{20{ID_IR[31]}}, {ID_IR[31], ID_Funct[4], ID_IR[29:26], ID_Funct[3], ID_IR[24:20]}};  // Bit_Extender bit_extender_1
  assign bit_extender_2_out = {{20{ID_IR[31]}}, {ID_IR[31], ID_Funct[4], ID_IR[29:26], ID_Funct[3], ID_IR[11:7]}};  // Bit_Extender bit_extender_2
  assign bit_extender_3_out = {{12{ID_IR[31]}}, {ID_IR[31], ID_Funct[4], ID_IR[29:26], ID_Funct[3], ID_IR[24:15], ID_Funct[2:0]}};  // Bit_Extender bit_extender_3
  Counter #(.width(16), .max('hffff), .ongoal("wrap"), .trigger("rising"), .behavior("new")) counter_3 (
    .count(Branch), .Q(\条件分支成功数 ), .clk(CLK), .clr(RST));  // open: load, D, carry, preset, down
  and and_8 (and_8_out, or_11_out, ~Ret2);  // AND_Gate
  \单周期硬布线控制器  \u_单周期硬布线控制器_1  (
    .Funct(ID_Funct), .OP(ID_IR[6:2]), .ALU_OP(\单周期硬布线控制器_1_alu_op ), .MemToReg(\单周期硬布线控制器_1_memtoreg ),
    .MemWrite(\单周期硬布线控制器_1_memwrite ), .ALU_SRC(\单周期硬布线控制器_1_alu_src ), .RegWrite(\单周期硬布线控制器_1_regwrite ),
    .ecall(ecall), .S_type(\单周期硬布线控制器_1_s_type ), .Jalr(ID_JALR), .Beq(\单周期硬布线控制器_1_beq ), .JAL(ID_JAL),
    .Bne(\单周期硬布线控制器_1_bne ), .in_3(ID_IR[21]), .uret(ID_URET), .sb(\单周期硬布线控制器_1_sb ),
    .auipc(\单周期硬布线控制器_1_auipc ), .bltu(\单周期硬布线控制器_1_bltu ));  // open: sltiu, rs1, rs2, CSRRSI, CSRRCI
  Multiplexer #(.select(1), .width(5), .disabled("Z"), .enable("false")) multiplexer_3 (
    .in0(ID_IR[19:15]), .in1(5'b10001), .out(ID_R1_num), .sel(ecall));
  Multiplexer #(.select(1), .width(5), .disabled("Z"), .enable("false")) multiplexer_4 (
    .in0(ID_IR[24:20]), .in1(5'b01010), .out(ID_R2_num), .sel(ecall));
  assign bit_extender_4_out = {{20{ID_IR[31]}}, {ID_IR[31], ID_IR[7], ID_Funct[4], ID_IR[29:26], ID_Funct[3], ID_IR[11:8]}};  // Bit_Extender bit_extender_4
  assign bit_extender_5_out = {{12{ID_IR[31]}}, {ID_IR[31], ID_IR[19:15], ID_Funct[2:0], ID_IR[20], ID_Funct[4], ID_IR[29:26], ID_Funct[3], ID_IR[24:21]}};  // Bit_Extender bit_extender_5
  Shifter #(.width(32), .shift("ll")) shifter_1 (.in(bit_extender_3_out), .\dist (5'b01100), .out(shifter_1_out));
  D_Flip_Flop #(.trigger("rising"), .Pre_Clr_Positions("LEGACY"), .NegatePresetClear("false"), .enable("true"), .NewFFLayout("false")) u_IR2 (
    .clk(CLK), .D(and_8_out), .Q(Inter2), .en(EXlode), .reset(RST));  // open: Qn, preset
  Shifter #(.width(32), .shift("ll")) shifter_2 (.in(bit_extender_4_out), .\dist (5'b00001), .out(shifter_2_out));
  Shifter #(.width(32), .shift("ll")) shifter_3 (.in(bit_extender_5_out), .\dist (5'b00001), .out(shifter_3_out));
  or or_12 (or_12_out, JAL, JALR);
  not not_4 (not_4_out, CLK);
  Regifile regifile_1 (
    .Din(RDin), .Clk(not_4_out), .R1(ID_R1), .R2(ID_R2), .WE(RegWrite), .W_num(W_num), .R1_num(ID_R1_num),
    .R2_num(ID_R2_num));
  Counter #(.width(16), .max('hffff), .ongoal("wrap"), .trigger("rising"), .behavior("new")) counter_4 (
    .count(or_12_out), .Q(\无条件分支数 ), .clk(CLK), .clr(RST));  // open: load, D, carry, preset, down
  D_Flip_Flop #(.trigger("rising"), .Pre_Clr_Positions("LEGACY"), .NegatePresetClear("false"), .enable("true"), .NewFFLayout("false")) d_ff_4 (
    .clk(IR3_t), .D(1'b1), .Q(d_ff_4_q), .reset(Inter3));  // open: Qn, preset, en
  or or_13 (W3, Inter3, d_ff_4_q);
  or or_14 (or_14_out, Load_Use, RST_num);
  or or_15 (or_15_out, d_ff_4_q, Inter3);
  ID_EX id_ex_1 (
    .Beqin(\单周期硬布线控制器_1_beq ), .PCin(ID_PC), .Bnein(\单周期硬布线控制器_1_bne ),
    .IRin({ID_IR[31], ID_Funct[4], ID_IR[29:26], ID_Funct[3], ID_IR[24:15], ID_Funct[2:0], ID_IR[11:0]}),
    .MemToRegin(\单周期硬布线控制器_1_memtoreg ), .MemWritein(\单周期硬布线控制器_1_memwrite ), .Imm_I_in(bit_extender_1_out),
    .AluSrcBin(\单周期硬布线控制器_1_alu_src ), .Imm_S_in(bit_extender_2_out), .RegWritein(\单周期硬布线控制器_1_regwrite ),
    .Imm_B_in(shifter_2_out), .S_typein(\单周期硬布线控制器_1_s_type ), .Jalin(ID_JAL), .Imm_J_in(shifter_3_out),
    .Jalrin(ID_JALR), .R1in(ID_R1), .R2in(ID_R2), .W_in(ID_IR[11:7]), .Imm_lui_in(shifter_1_out),
    .LUIin(\单周期硬布线控制器_1_sb ), .LHUin(\单周期硬布线控制器_1_auipc ), .BLTUin(\单周期硬布线控制器_1_bltu ),
    .R1Forwardin(R1Forward), .R2Forwardin(R2Forward), .Ecallin(ecall), .Uretlin(ID_URET),
    .PredictJumpin(ID_PredictJump), .AluOpin(\单周期硬布线控制器_1_alu_op ), .Beqout(EX_Beq), .PCout(EX_PC),
    .Bneout(EX_Bne), .IRout(EX_IR), .MemToRegout(id_ex_1_memtoregout), .MemWriteout(id_ex_1_memwriteout),
    .Imm_I_out(id_ex_1_imm_i_out), .AluSrcBout(id_ex_1_alusrcbout), .Imm_S_out(id_ex_1_imm_s_out),
    .RegWriteout(EX_RegWrite_num), .Imm_B_out(id_ex_1_imm_b_out), .S_Typeout(id_ex_1_s_typeout),
    .Jalout(JAL), .Imm_J_out(id_ex_1_imm_j_out), .Jalrout(JALR), .R1out(id_ex_1_r1out),
    .R2out(id_ex_1_r2out), .W_out(EX_W_num), .Imm_lui_out(id_ex_1_imm_lui_out), .LUIout(id_ex_1_luiout),
    .LHUout(EX_LHU), .BLTUout(EX_BLTU), .R1Forwardout(id_ex_1_r1forwardout),
    .R2Forwardout(id_ex_1_r2forwardout), .Ecallout(EX_ecall), .Uretout(id_ex_1_uretout),
    .PredictJumpout(EX_PredictJump), .AluOpout(id_ex_1_aluopout), .RST(or_14_out), .EN(EN), .CLK(CLK),
    .RST_num(RST));  // open: Haltin, Haltout
  and and_9 (and_9_out, or_15_out, ~Ret3);  // AND_Gate
  Adder #(.width(16)) adder_3 (.a(\无条件分支数 ), .b(\条件分支成功数 ), .out(adder_3_out));  // open: cin, cout
  not not_5 (not_5_out, halt);
  and and_10 (and_10_out, not_5_out, Load_Use);
  D_Flip_Flop #(.trigger("rising"), .Pre_Clr_Positions("LEGACY"), .NegatePresetClear("false"), .enable("true"), .NewFFLayout("false")) u_IR3 (
    .clk(CLK), .D(and_9_out), .Q(Inter3), .en(EXlode), .reset(RST));  // open: Qn, preset
  Multiplexer #(.select(2), .width(32), .disabled("Z"), .enable("false")) multiplexer_5 (
    .in0(id_ex_1_r1out), .in1(RDin), .in2(MEM_Result), .out(EX_R1), .sel(id_ex_1_r1forwardout));  // open: in3
  Multiplexer #(.select(2), .width(32), .disabled("Z"), .enable("false")) multiplexer_6 (
    .in0(id_ex_1_r2out), .in1(RDin), .in2(MEM_Result), .out(EX_R2), .sel(id_ex_1_r2forwardout));  // open: in3
  Adder #(.width(32)) adder_4 (.a(id_ex_1_imm_j_out), .b(EX_PC), .out(adder_4_out));  // open: cin, cout
  Adder #(.width(32)) adder_5 (.a(id_ex_1_imm_lui_out), .b(EX_PC), .out(adder_5_out));  // open: cin, cout
  Shifter #(.width(16), .shift("ll")) shifter_4 (.in(adder_3_out), .\dist (4'b0001), .out(shifter_4_out));
  Counter #(.width(16), .max('hffff), .ongoal("wrap"), .trigger("rising"), .behavior("new")) counter_5 (
    .count(and_10_out), .Q(\LoadUse次数 ), .clk(CLK), .clr(RST));  // open: load, D, carry, preset, down
  or or_16 (Branch, EX_Bne, EX_Beq, EX_BLTU);
  and and_11 (and_11_out, EX_BLTU, blow);
  and and_12 (and_12_out, EX_Beq, equal);
  not not_6 (not_6_out, equal);
  and and_13 (and_13_out, not_6_out, EX_Bne);
  Multiplexer #(.select(1), .width(32), .disabled("Z"), .enable("false")) multiplexer_7 (
    .in0(adder_5_out), .in1(IF_PC_4), .out(multiplexer_7_out), .sel(not_7_out));
  not not_7 (not_7_out, JAL);
  Adder #(.width(16)) adder_6 (.a(shifter_4_out), .b(\LoadUse次数 ), .out(\插入气泡数 ));  // open: cin, cout
  or or_17 (BranchTaken, and_11_out, and_12_out, and_13_out);
  Multiplexer #(.select(1), .width(32), .disabled("Z"), .enable("false")) multiplexer_8 (
    .in0(id_ex_1_imm_i_out), .in1(id_ex_1_imm_s_out), .out(multiplexer_8_out), .sel(id_ex_1_s_typeout));
  assign and_14_out = Result & 32'hfffffffe;  // AND_Gate and_14, 32 bits wide
  or or_18 (or_18_out, JALR, JAL);
  Multiplexer #(.select(1), .width(32), .disabled("Z"), .enable("false")) multiplexer_9 (
    .in0(multiplexer_8_out), .in1(id_ex_1_imm_i_out), .out(multiplexer_9_out), .sel(EX_LHU));
  not not_8 (not_8_out, Branch);
  Multiplexer #(.select(1), .width(32), .disabled("Z"), .enable("false")) multiplexer_10 (
    .in0(multiplexer_7_out), .in1(and_14_out), .out(multiplexer_10_out), .sel(JALR));
  Comparator #(.width(32), .mode("twosComplement")) comparator_2 (
    .a(EX_PC), .b({32{1'b0}}), .eq(comparator_2_eq));  // open: gt, lt
  not not_9 (EXlode, comparator_2_eq);
  Multiplexer #(.select(1), .width(32), .disabled("Z"), .enable("false")) multiplexer_11 (
    .in0(adder_4_out), .in1(multiplexer_10_out), .out(BranchAddr), .sel(not_8_out));
  and and_15 (and_15_out, Interrupt, EXlode);
  Comparator #(.width(32), .mode("twosComplement")) comparator_3 (
    .a(EX_R1), .b(32'ha), .eq(comparator_3_eq));  // open: gt, lt
  Priority_Encoder #(.select(2), .disabled("Z")) priority_encoder_1 (
    .in0(1'b0), .in1(Inter1), .in2(Inter2), .in3(Inter3), .out(priority_encoder_1_out), .gs(Interr));  // open: en_out, en_in
  Register #(.width(32), .trigger("rising"), .Select("low")) u_EPC (
    .D(M_PC), .en(and_15_out), .Q(EPC), .clk(CLK), .clr(RST));
  Multiplexer #(.select(1), .width(32), .disabled("Z"), .enable("false")) multiplexer_12 (
    .in0(EX_R2), .in1(multiplexer_9_out), .out(multiplexer_12_out), .sel(id_ex_1_alusrcbout));
  not not_10 (not_10_out, comparator_3_eq);
  ALU alu_1 (
    .X(EX_R1), .Y(multiplexer_12_out), .AluOP(id_ex_1_aluopout), .Equal(equal), .Result(Result), .out_6(blow));  // open: Result_2, out_4
  and and_16 (and_16_out, comparator_3_eq, EX_ecall);
  Register #(.width(32), .trigger("rising"), .Select("low")) register_1 (
    .D(EX_R2), .en(and_17_out), .Q(LedData), .clk(CLK), .clr(RST));
  and and_17 (and_17_out, not_10_out, EX_ecall);
  Multiplexer #(.select(2), .width(32), .disabled("Z"), .enable("false")) multiplexer_13 (
    .in1(32'h30ac), .in2(32'h3158), .in3(32'h3204), .out(InterAddr), .sel(priority_encoder_1_out));  // open: in0
  or or_19 (or_19_out, Interrupt, URET);
  Register #(.width(2), .trigger("rising"), .Select("low")) \u_中断号  (
    .D(priority_encoder_1_out), .en(Interrupt), .Q(\中断号_q ), .clk(CLK), .clr(RST));
  Register #(.width(1), .trigger("rising"), .Select("low")) IE (
    .D(Interrupt), .en(or_19_out), .Q(IE_q), .clk(CLK), .clr(RST));
  not not_11 (not_11_out, IE_q);
  or or_20 (or_20_out, URET, Interrupt, RST);
  EX_MEM ex_mem_1 (
    .MemToRegin(id_ex_1_memtoregout), .PCin(EX_PC), .MemWritein(id_ex_1_memwriteout), .IRin(EX_IR),
    .JAMPin(or_18_out), .RegWritein(EX_RegWrite_num), .Resultin(Result), .Haltin(and_16_out),
    .MDatain(EX_R2), .W_in(EX_W_num), .Imm_lui_in(id_ex_1_imm_b_out), .LUIin(EX_LHU), .LHUin(id_ex_1_luiout),
    .BLTUin(EX_BLTU), .Uretlin(id_ex_1_uretout), .MemToRegout(ex_mem_1_memtoregout), .PCout(M_PC),
    .MemWriteout(MemWrite), .IRout(MEM_IR), .JAMPout(ex_mem_1_jampout), .RegWriteout(MEM_RegWrite_num),
    .Resultout(MEM_Result), .Haltout(ex_mem_1_haltout), .Mdataout(MDin), .W_out(MEM_W_num),
    .Imm_lui_out(ex_mem_1_imm_lui_out), .LUIout(ex_mem_1_luiout), .LHUout(ex_mem_1_lhuout),
    .BLTUout(ex_mem_1_bltuout), .Uretout(ex_mem_1_uretout), .RST(or_20_out), .EN_H(EN), .CLK(CLK),
    .RST_num(RST));
  Decoder #(.select(2), .tristate("false"), .disabled("Z"), .enable("false")) decoder_1 (
    .out1(decoder_1_out1), .out2(decoder_1_out2), .out3(decoder_1_out3), .sel(\中断号_q ));  // open: out0
  and and_18 (Interrupt, not_11_out, Interr);
  not not_12 (not_12_out, halt);
  and and_19 (Ret1, URET, decoder_1_out1);
  and and_20 (Ret2, decoder_1_out2, URET);
  and and_21 (Ret3, decoder_1_out3, URET);
  Counter #(.width(16), .max('hffff), .ongoal("wrap"), .trigger("rising"), .behavior("new")) counter_6 (
    .count(not_12_out), .Q(\总周期数 ), .clk(CLK), .clr(RST));  // open: load, D, carry, preset, down
  RAM #(.addrWidth(10), .dataWidth(32), .bus("separate"), .Select("high")) ram_1 (
    .addr(MEM_Result[11:2]), .din(MDin), .data(ram_1_data), .str(MemWrite), .clk(CLK),
    .ld(ex_mem_1_memtoregout), .clr(RST));  // open: sel
  or or_21 (or_21_out, URET, RST);
  MEM_WB mem_wb_1 (
    .MemToRegin(ex_mem_1_memtoregout), .PCin(M_PC), .JAMPin(ex_mem_1_jampout), .IRin(MEM_IR),
    .RegWritein(MEM_RegWrite_num), .Resultin(MEM_Result), .Haltin(ex_mem_1_haltout), .RMDatain(ram_1_data),
    .W_in(MEM_W_num), .LUIin(ex_mem_1_lhuout), .Imm_lui_in(ex_mem_1_imm_lui_out), .LHUin(ex_mem_1_luiout),
    .BLTUin(ex_mem_1_bltuout), .Uretlin(ex_mem_1_uretout), .MemToRegout(mem_wb_1_memtoregout), .PCout(WB_PC),
    .JAMPout(mem_wb_1_jampout), .IRout(WB_IR), .RegWriteout(RegWrite), .Resultout(mem_wb_1_resultout),
    .Haltout(mem_wb_1_haltout), .RMdataout(mem_wb_1_rmdataout), .W_out(W_num), .LUIout(LUI),
    .Imm_lui_out(Imm_lui), .LHUout(LHU), .BLTUout(BLTU), .Uretout(URET), .RST(or_21_out), .EN_H(EN),
    .CLK(CLK), .RST_num(RST));
  Multiplexer #(.select(1), .width(32), .disabled("Z"), .enable("false")) multiplexer_14 (
    .in0(mem_wb_1_resultout), .in1(mem_wb_1_rmdataout), .out(multiplexer_14_out), .sel(mem_wb_1_memtoregout));
  not not_13 (not_13_out, Go);
  and and_22 (halt, not_13_out, mem_wb_1_haltout);
  Adder #(.width(32)) adder_7 (.a(WB_PC), .b(32'h4), .out(adder_7_out));  // open: cin, cout
  not not_14 (EN, halt);
  Multiplexer #(.select(1), .width(32), .disabled("Z"), .enable("false")) multiplexer_15 (
    .in0({{16{1'b0}}, mem_wb_1_rmdataout[15:0]}), .in1({{16{1'b0}}, mem_wb_1_rmdataout[31:16]}),
    .out(multiplexer_15_out), .sel(mem_wb_1_resultout[1]));
  not not_15 (not_15_out, LHU);
  Multiplexer #(.select(1), .width(32), .disabled("Z"), .enable("false")) multiplexer_16 (
    .in0(multiplexer_15_out), .in1(multiplexer_14_out), .out(multiplexer_16_out), .sel(not_15_out));
  not not_16 (not_16_out, mem_wb_1_jampout);
  Multiplexer #(.select(1), .width(32), .disabled("Z"), .enable("false")) multiplexer_17 (
    .in0(adder_7_out), .in1(multiplexer_16_out), .out(multiplexer_17_out), .sel(not_16_out));
  Multiplexer #(.select(1), .width(32), .disabled("Z"), .enable("false")) multiplexer_18 (
    .in0(multiplexer_17_out), .in1(Imm_lui), .out(RDin), .sel(LUI));

  // Other names for the same wires on the sheet: IR[31:0] = {ID_IR[31], ID_Funct[4], ID_IR[29:26], ID_Funct[3], ID_IR[24:15], ID_Funct[2:0], ID_IR[11:0]};
  //   RD_num[4:0] = ID_IR[11:7]; ID_IR (some bits) = ID_Funct; ID_ecall = ecall; ID_OP[4:0] = ID_IR[6:2];
  //   MEM_PC[31:0] = M_PC

  // Notes on the sheet:
  //   中断源
  //   时空图监测，可删除
  //   中断等待指示
  //   数码管输出
  //   控制位
  //   流水调试日志用
  //   暂停节拍，不能为0
  //   戳工具置1进入计数暂停模式，ctrl+k时钟自动运行到对应节拍暂停
  //   ctrl+k关闭时钟连续运行，将控制位置零，进入单步调试模式调试
  //   指令存储器
  //   Reset 
  //   contents of rom_1 (hex, n*v repeats v):
  //   100493 100006f 100493 200913 300993 100006f 100493 200913 300993 100006f 100493 200913 300993
  //   100006f 100493 200913 300993 3dc000ef 100413 100493 1f49493 900533 2200893 73 24d493 48463 fedff06f
  //   900533 2200893 73 100493 249493 900533 2200893 73 48463 fedff06f 100493 1f49493 900533 2200893 73
  //   4034d493 900533 2200893 73 4044d493 900533 2200893 73 4044d493 900533 2200893 73 4044d493 900533
  //   2200893 73 4044d493 900533 2200893 73 4044d493 900533 2200893 73 4044d493 900533 2200893 73 4044d493
  //   900533 2200893 73 100413 1f41993 41f9d993 433 c00913 300b13 140413 f47413 800293 100313 499993
  //   89e9b3 1300533 2200893 73 406282b3 fe0294e3 140413 f00f93 1f47433 1c41413 800293 100313 49d993
  //   89e9b3 1300533 2200893 73 406282b3 fe0294e3 1c45413 406b0b33 b0463 f95ff06f 2b3 fff2c293 829293
  //   ff2e293 500533 2200893 73 fff00413 493 84a023 140413 448493 84a023 140413 448493 84a023 140413
  //   448493 84a023 140413 448493 84a023 140413 448493 84a023 140413 448493 84a023 140413 448493 84a023
  //   140413 448493 84a023 140413 448493 84a023 140413 448493 84a023 140413 448493 84a023 140413 448493
  //   84a023 140413 448493 84a023 140413 448493 84a023 140413 448493 84a023 140413 448493 140413 433
  //   3c00493 42983 4aa03 149a2b3 28663 134a023 1442023 ffc48493 fe9412e3 800533 2200893 73 440413 3c00493
  //   fc9416e3 a00893 73 fff00293 7700493 849493 7748493 900533 2200893 73 1000e13 54c4b3 900533 2200893
  //   73 fffe0e13 fe0e16e3 a00893 73 800e13 fedc04b7 fff00413 1045413 84e4b3 900533 2200893 73 ba984b7
  //   900533 73 76544b7 900533 73 32104b7 900533 73 fffe0e13 fa0e1ee3 a00893 73 313 1000e13 8400493 849493
  //   8348493 400913 891913 490913 849493 8248493 849493 8148493 891913 490913 891913 490913 932023
  //   12484b3 430313 fffe0e13 fe0e18e3 2000e13 313 35483 900533 2200893 73 230313 fffe0e13 fe0e14e3 a00893
  //   73 ff100493 900533 2200893 73 148493 fe9068e3 900533 2200893 73 a00893 73 413 140413 800533 2200893
  //   73 240413 800533 2200893 73 340413 800533 2200893 73 440413 800533 2200893 73 540413 800533 2200893
  //   73 640413 800533 2200893 73 740413 800533 2200893 73 840413 800533 2200893 2200893 73 8067
  //   可计数暂停的时钟源
  //   指令探针
  //   JAL
  //   指令字
  //   为方便自动评测，需要输出流水线各段保存的PC值，注意是PC不是PC+4，另外ID段寄存器写入信息，Mem段内存写入信息也要输出
  //   JALR
  //   Reset 
  //   Beq
  //   Bne
  //   MemToReg
  //   MemWrite
  //   AluOP
  //   AluSrcB
  //   RegWrite
  //   S_type
  //   Reset 
  //   数据存储器
endmodule

module \理想流水线  (
  output RegWrite,
  output MemWrite,
  output [31:0] IF_PC,
  output [31:0] ID_PC,
  output [31:0] EX_PC,
  output [31:0] M_PC,
  output [31:0] WB_PC,
  output [31:0] RDin,
  output [31:0] MDin,
  output [31:0] LedData
);

  wire alu_1_equal, alu_1_out_6, and_3_out, and_4_out, and_5_out, and_6_out, CLK, clock_1_out,
       comparator_1_eq, comparator_1_lt, comparator_2_eq, d_ff_1_q, ecall, ecallEq, ecallFB, ex_1_auipc_2,
       ex_1_ecall_2, ex_1_jal_2, ex_1_jalr_2, ex_1_memtoreg_2, ex_1_memwrite, ex_1_regwirte_2, ex_1_sb_2,
       ex_1_uret_2, Go, halt, id_1_alu_srcb_2, id_1_auipc_2, id_1_beq_2, id_1_bltu_2, id_1_bne_2,
       id_1_ecall_2, id_1_jal_2, id_1_jalr_2, id_1_memtoreg_2, id_1_memwrite_2, id_1_regwrite_2, id_1_sb_2,
       id_1_uret_2, IR1, IR2, IR3, mem_1_jal_2, mem_1_jalr_2, mem_1_sb_2, MEN_MemtoReg, MEN_RegWrite,
       nand_1_out, not_1_out, not_2_out, not_3_out, not_4_out, or_1_out, or_2_out, RST, sltiu, W1, W2, W3,
       WB_ecall, \单周期硬布线控制器_1_alu_src , \单周期硬布线控制器_1_auipc , \单周期硬布线控制器_1_beq , \单周期硬布线控制器_1_bltu ,
       \单周期硬布线控制器_1_bne , \单周期硬布线控制器_1_ecall , \单周期硬布线控制器_1_jal , \单周期硬布线控制器_1_jalr , \单周期硬布线控制器_1_memtoreg ,
       \单周期硬布线控制器_1_memwrite , \单周期硬布线控制器_1_regwrite , \单周期硬布线控制器_1_s_type , \单周期硬布线控制器_1_sb ,
       \单周期硬布线控制器_1_uret ;
  wire [3:0] id_1_alu_op_2, \单周期硬布线控制器_1_alu_op ;
  wire [4:0] ex_1_write_2, id_1_wrd_2, multiplexer_4_out, multiplexer_5_out, WB_RD;
  wire [11:0] I_imm, multiplexer_6_out;
  wire [12:0] CNT_num;
  wire [15:0] \LoadUse次数 , \总周期数 , \插入气泡数 , \无条件分支数 , \条件分支成功数 ;
  wire [19:0] ID_IR;
  wire [31:0] adder_1_out, adder_4_out, alu_1_result, ALU_result, bit_extender_1_out, bit_extender_2_out,
       bit_extender_3_out, bit_extender_4_out, Branch_Adress, ex_1_pc_4_2, ex_1_r1_2, ex_1_u_2, EX_IR, EX_R1,
       EX_R2, id_1_bm_2, id_1_im_2, id_1_jm_2, id_1_pc_4_2, id_1_u_2, ID_PC_4, IF_IR, JAL_Adress,
       JALR_Adress, mem_1_alu_result_2, mem_1_mdata_2, mem_1_u_2, MEM_IR, MEN_PC, mips_ram_1_p6,
       multiplexer_1_out, multiplexer_2_out, multiplexer_3_out, multiplexer_7_out, multiplexer_8_out,
       multiplexer_9_out, multiplexer_10_out, regifile_1_r1, regifile_1_r2, shifter_1_out, shifter_2_out,
       shifter_3_out, U_adress, WB_IR, WB_PC_4, WB_R1, WB_R2;

  Button \u_总复位  (.out(RST));
  Button _1 (.out(IR1));
  Button _2 (.out(IR2));
  Button _3 (.out(IR3));
  // Probe on \总周期数 
  // Probe on \总周期数 
  Button \u_继续运行  (.out(Go));
  LED #(.active("true")) led_1 (.in(W1));
  LED #(.active("true")) led_2 (.in(W2));
  LED #(.active("true")) led_3 (.in(W3));
  Hex_Digit_Display hex_digit_display_1 (.value(LedData[31:28]));  // open: dp
  // Probe on IF_PC[19:0]
  // RiscV_Probe riscv_probe_1: pin names not known; wires that end beside it: IF_IR
  Multiplexer #(.select(1), .width(32), .disabled("Z"), .enable("false")) multiplexer_1 (
    .in0(adder_1_out), .in1(Branch_Adress), .out(multiplexer_1_out), .sel(or_1_out));
  Adder #(.width(32)) adder_1 (.a(IF_PC), .b(32'h4), .out(adder_1_out));  // open: cin, cout
  Hex_Digit_Display hex_digit_display_2 (.value(LedData[27:24]));  // open: dp
  Hex_Digit_Display hex_digit_display_3 (.value(LedData[23:20]));  // open: dp
  // Probe on ID_PC[19:0]
  // RiscV_Probe riscv_probe_2: pin names not known; wires that end beside it: {I_imm, ID_IR}
  Multiplexer #(.select(1), .width(32), .disabled("Z"), .enable("false")) multiplexer_2 (
    .in0(multiplexer_1_out), .in1(JAL_Adress), .out(multiplexer_2_out), .sel(id_1_jal_2));
  Hex_Digit_Display hex_digit_display_4 (.value(LedData[19:16]));  // open: dp
  Hex_Digit_Display hex_digit_display_5 (.value(LedData[15:12]));  // open: dp
  Multiplexer #(.select(1), .width(32), .disabled("Z"), .enable("false")) multiplexer_3 (
    .in0(multiplexer_2_out), .in1(JALR_Adress), .out(multiplexer_3_out), .sel(id_1_jalr_2));
  Register #(.width(32), .trigger("rising"), .Select("low")) PC (
    .D(multiplexer_3_out), .en(not_1_out), .Q(IF_PC), .clk(CLK), .clr(RST));
  not not_1 (not_1_out, halt);
  Hex_Digit_Display hex_digit_display_6 (.value(LedData[11:8]));  // open: dp
  Hex_Digit_Display hex_digit_display_7 (.value(LedData[7:4]));  // open: dp
  // Probe on EX_PC[19:0]
  // RiscV_Probe riscv_probe_3: pin names not known; wires that end beside it: EX_IR
  Hex_Digit_Display hex_digit_display_8 (.value(LedData[3:0]));  // open: dp
  // Probe on \总周期数 
  // Probe on M_PC[19:0]
  // RiscV_Probe riscv_probe_4: pin names not known; wires that end beside it: MEM_IR
  // Probe on \总周期数 
  // Probe on \无条件分支数 
  // Probe on \条件分支成功数 
  // Probe on \插入气泡数 
  // Probe on \LoadUse次数 
  // RiscV_Probe riscv_probe_5: pin names not known; wires that end beside it: IF_IR
  ROM #(.addrWidth(10), .dataWidth(32), .Select("high")) rom_1 (.addr(IF_PC[11:2]), .data(IF_IR));
  // Probe on IF_PC[11:0]
  // Probe on WB_PC[19:0]
  // RiscV_Probe riscv_probe_6: pin names not known; wires that end beside it: WB_IR
  IF if_1 (
    .CLK(CLK), .RST(RST), .IR(IF_IR), .PC(IF_PC), .PC_4(adder_1_out), .IR_2({I_imm, ID_IR}), .PC_2(ID_PC),
    .PC_4_2(ID_PC_4), .flush(halt));  // open: en
  // Probe on ID_PC[11:0]
  // Probe on EX_PC[11:0]
  and and_1 (ecall, ~ecallFB, \单周期硬布线控制器_1_ecall );  // AND_Gate
  // Probe on M_PC[11:0]
  D_Flip_Flop #(.trigger("high"), .Pre_Clr_Positions("LEGACY"), .NegatePresetClear("false"), .enable("true"), .NewFFLayout("false")) d_ff_1 (.Q(d_ff_1_q));  // open: clk, D, Qn, preset, en, reset
  // Probe on 13'hc
  // Probe on WB_PC[11:0]
  Comparator #(.width(13), .mode("twosComplement")) comparator_1 (
    .a(CNT_num), .b(13'hc), .eq(comparator_1_eq), .lt(comparator_1_lt));  // open: gt
  Clock #(.highDuration(1), .lowDuration(1)) clock_1 (.out(clock_1_out));
  \单周期硬布线控制器  \u_单周期硬布线控制器_1  (
    .Funct({I_imm[10], I_imm[5], ID_IR[14:12]}), .OP(ID_IR[6:2]), .ALU_OP(\单周期硬布线控制器_1_alu_op ),
    .MemToReg(\单周期硬布线控制器_1_memtoreg ), .MemWrite(\单周期硬布线控制器_1_memwrite ), .ALU_SRC(\单周期硬布线控制器_1_alu_src ),
    .RegWrite(\单周期硬布线控制器_1_regwrite ), .ecall(\单周期硬布线控制器_1_ecall ), .S_type(\单周期硬布线控制器_1_s_type ),
    .Jalr(\单周期硬布线控制器_1_jalr ), .Beq(\单周期硬布线控制器_1_beq ), .JAL(\单周期硬布线控制器_1_jal ), .Bne(\单周期硬布线控制器_1_bne ),
    .in_3(I_imm[1]), .uret(\单周期硬布线控制器_1_uret ), .sb(\单周期硬布线控制器_1_sb ), .auipc(\单周期硬布线控制器_1_auipc ),
    .bltu(\单周期硬布线控制器_1_bltu ), .sltiu(sltiu));  // open: rs1, rs2, CSRRSI, CSRRCI
  Multiplexer #(.select(1), .width(5), .disabled("Z"), .enable("false")) multiplexer_4 (
    .in0(ID_IR[19:15]), .in1(5'b10001), .out(multiplexer_4_out), .sel(ecall));
  Multiplexer #(.select(1), .width(5), .disabled("Z"), .enable("false")) multiplexer_5 (
    .in0(I_imm[4:0]), .in1(5'b01010), .out(multiplexer_5_out), .sel(ecall));
  nand nand_1 (nand_1_out, d_ff_1_q, comparator_1_eq);
  Counter #(.width(13), .max('h1fff), .ongoal("stay"), .trigger("rising"), .behavior("old")) counter_1 (
    .count(comparator_1_lt), .Q(CNT_num), .clk(clock_1_out));  // open: load, D, carry, clr, preset
  Multiplexer #(.select(1), .width(12), .disabled("Z"), .enable("false")) multiplexer_6 (
    .in0(I_imm), .in1({I_imm[11:5], ID_IR[11:7]}), .out(multiplexer_6_out), .sel(\单周期硬布线控制器_1_s_type ));
  assign bit_extender_1_out = {{12{1'b0}}, {I_imm, ID_IR[19:12]}};  // Bit_Extender bit_extender_1
  assign CLK = nand_1_out ? clock_1_out : 1'bz;  // Controlled_Buffer controlled_buffer_1
  assign bit_extender_2_out = {{20{I_imm[11]}}, {I_imm[11], ID_IR[7], I_imm[10:5], ID_IR[11:8]}};  // Bit_Extender bit_extender_2
  assign bit_extender_3_out = {{12{I_imm[11]}}, {I_imm[11], ID_IR[19:12], I_imm[0], I_imm[10:1]}};  // Bit_Extender bit_extender_3
  Pull_Resistor #(.pull(1)) pull_resistor_1 (.node(CLK));
  Regifile regifile_1 (
    .Din(RDin), .Clk(CLK), .R1(regifile_1_r1), .R2(regifile_1_r2), .WE(MEN_RegWrite), .W_num(WB_RD),
    .R1_num(multiplexer_4_out), .R2_num(multiplexer_5_out));
  assign bit_extender_4_out = {{20{multiplexer_6_out[11]}}, multiplexer_6_out};  // Bit_Extender bit_extender_4
  ID id_1 (
    .RST(RST), .beq(\单周期硬布线控制器_1_beq ), .bne(\单周期硬布线控制器_1_bne ), .MemToReg(\单周期硬布线控制器_1_memtoreg ),
    .MemWrite(\单周期硬布线控制器_1_memwrite ), .ALU_OP(\单周期硬布线控制器_1_alu_op ), .ALU_SRCB(\单周期硬布线控制器_1_alu_src ),
    .RegWrite(\单周期硬布线控制器_1_regwrite ), .JAL(\单周期硬布线控制器_1_jal ), .JALR(\单周期硬布线控制器_1_jalr ),
    .URET(\单周期硬布线控制器_1_uret ), .ID_PC(ID_PC), .r1(regifile_1_r1), .r2(regifile_1_r2),
    .Bm(bit_extender_2_out), .Jm(bit_extender_3_out), .PC_4(ID_PC_4), .CLK(CLK), .beq_2(id_1_beq_2),
    .bne_2(id_1_bne_2), .MemToReg_2(id_1_memtoreg_2), .MemWrite_2(id_1_memwrite_2), .ALU_OP_2(id_1_alu_op_2),
    .ALU_SRCB_2(id_1_alu_srcb_2), .RegWrite_2(id_1_regwrite_2), .JAL_2(id_1_jal_2), .JALR_2(id_1_jalr_2),
    .URET_2(id_1_uret_2), .ID_PC_2(EX_PC), .r1_2(EX_R1), .r2_2(EX_R2), .Bm_2(id_1_bm_2), .Jm_2(id_1_jm_2),
    .PC_4_2(id_1_pc_4_2), .ID_IR({I_imm, ID_IR}), .ID_IR_2(EX_IR), .ecall(ecall), .ecall_2(id_1_ecall_2),
    .WRD(ID_IR[11:7]), .WRD_2(id_1_wrd_2), .Im(bit_extender_4_out), .Im_2(id_1_im_2), .halt(halt),
    .auipc(\单周期硬布线控制器_1_auipc ), .bltu(\单周期硬布线控制器_1_bltu ), .sb(\单周期硬布线控制器_1_sb ), .bltu_2(id_1_bltu_2),
    .auipc_2(id_1_auipc_2), .sb_2(id_1_sb_2), .u(bit_extender_1_out), .u_2(id_1_u_2), .flush(1'b0));  // open: S_type, S_type_2, RsFoward, RtFoward, RsFoward_2, Rtfoward_2
  Shifter #(.width(32), .shift("ll")) shifter_1 (.in(id_1_bm_2), .\dist (5'b00001), .out(shifter_1_out));
  Shifter #(.width(32), .shift("ll")) shifter_2 (.in(id_1_jm_2), .\dist (5'b00001), .out(shifter_2_out));
  Adder #(.width(32)) adder_2 (.a(shifter_1_out), .b(EX_PC), .out(Branch_Adress));  // open: cin, cout
  Adder #(.width(32)) adder_3 (.a(shifter_2_out), .b(EX_PC), .out(JAL_Adress));  // open: cin, cout
  Multiplexer #(.select(1), .width(32), .disabled("Z"), .enable("false")) multiplexer_7 (
    .in0(EX_R2), .in1(id_1_im_2), .out(multiplexer_7_out), .sel(id_1_alu_srcb_2));
  ALU alu_1 (
    .X(EX_R1), .Y(multiplexer_7_out), .AluOP(id_1_alu_op_2), .Equal(alu_1_equal), .Result(alu_1_result),
    .out_6(alu_1_out_6));  // open: Result_2, out_4
  assign JALR_Adress = alu_1_result & 32'hfffffffe;  // AND_Gate and_2, 32 bits wide
  or or_1 (or_1_out, and_3_out, and_5_out, and_4_out);
  and and_3 (and_3_out, id_1_bltu_2, alu_1_out_6);
  and and_4 (and_4_out, id_1_beq_2, alu_1_equal);
  and and_5 (and_5_out, not_2_out, id_1_bne_2);
  not not_2 (not_2_out, alu_1_equal);
  EX ex_1 (
    .RST(RST), .JAL(id_1_jal_2), .JALR(id_1_jalr_2), .URET(id_1_uret_2), .MemToReg(id_1_memtoreg_2),
    .MenWrite(id_1_memwrite_2), .ecall(id_1_ecall_2), .RegWirte(id_1_regwrite_2), .Write(id_1_wrd_2),
    .ALU_Result(alu_1_result), .EX_PC(EX_PC), .EX_IR(EX_IR), .PC_4(id_1_pc_4_2), .R1(EX_R1), .R2(EX_R2),
    .halt(halt), .CLK(CLK), .JAL_2(ex_1_jal_2), .JALR_2(ex_1_jalr_2), .URET_2(ex_1_uret_2),
    .MemToReg_2(ex_1_memtoreg_2), .MemWrite(ex_1_memwrite), .ecall_2(ex_1_ecall_2),
    .RegWirte_2(ex_1_regwirte_2), .Write_2(ex_1_write_2), .ALU_Result_2(ALU_result), .MEN_PC(M_PC),
    .MEN_IR(MEM_IR), .PC_4_2(ex_1_pc_4_2), .R1_2(ex_1_r1_2), .R2_2(MDin), .sb(id_1_sb_2),
    .auipc(id_1_auipc_2), .sb_2(ex_1_sb_2), .auipc_2(ex_1_auipc_2), .U(id_1_u_2), .U_2(ex_1_u_2), .flush(1'b0));
  // MIPS_RAM mips_ram_1: pin names not known; wires that end beside it: ALU_result[11:2], MDin, ex_1_memwrite, CLK, RST, mips_ram_1_p6
  Mem mem_1 (
    .RST(RST), .JAL(ex_1_jal_2), .JALR(ex_1_jalr_2), .URET(ex_1_uret_2), .MemToReg(ex_1_memtoreg_2),
    .MenWrite(ex_1_memwrite), .ecall(ex_1_ecall_2), .RegWirte(ex_1_regwirte_2), .Write(ex_1_write_2),
    .ALU_Result(ALU_result), .Mem_PC(M_PC), .Mem_IR(MEM_IR), .PC_4(ex_1_pc_4_2), .R1(ex_1_r1_2), .R2(MDin),
    .CLK(CLK), .JAL_2(mem_1_jal_2), .JALR_2(mem_1_jalr_2), .MemToReg_2(MEN_MemtoReg), .ecall_2(WB_ecall),
    .RegWirte_2(MEN_RegWrite), .Write_2(WB_RD), .ALU_Result_2(mem_1_alu_result_2), .Mem_PC_2(WB_PC),
    .Mem_IR_2(WB_IR), .PC_4_2(WB_PC_4), .R1_2(WB_R1), .R2_2(WB_R2), .MData(mips_ram_1_p6),
    .Mdata_2(mem_1_mdata_2), .sb(ex_1_sb_2), .auipc(ex_1_auipc_2), .sb_2(mem_1_sb_2), .u(ex_1_u_2),
    .u_2(mem_1_u_2), .flush(1'b0));  // open: URET_2, MemWrite, halt, auipc_2
  Multiplexer #(.select(1), .width(32), .disabled("Z"), .enable("false")) multiplexer_8 (
    .in0({32{1'b0}}), .in1(mem_1_u_2), .out(multiplexer_8_out));  // open: sel
  Multiplexer #(.select(1), .width(32), .disabled("Z"), .enable("false")) multiplexer_9 (
    .in0(mem_1_alu_result_2), .in1(mem_1_mdata_2), .out(multiplexer_9_out), .sel(MEN_MemtoReg));
  Adder #(.width(32)) adder_4 (.a(WB_PC), .b(32'h4), .out(adder_4_out));  // open: cin, cout
  or or_2 (or_2_out, mem_1_jalr_2, mem_1_jal_2);
  Multiplexer #(.select(1), .width(32), .disabled("Z"), .enable("false")) multiplexer_10 (
    .in0(multiplexer_9_out), .in1(adder_4_out), .out(multiplexer_10_out), .sel(or_2_out));
  Shifter #(.width(32), .shift("ll")) shifter_3 (.in(multiplexer_8_out), .\dist (5'b01100), .out(shifter_3_out));
  Multiplexer #(.select(1), .width(32), .disabled("Z"), .enable("false")) multiplexer_11 (
    .in0(multiplexer_10_out), .in1(U_adress), .out(RDin), .sel(mem_1_sb_2));
  Adder #(.width(32)) adder_5 (.a(shifter_3_out), .b(MEN_PC), .out(U_adress));  // open: cin, cout
  not not_3 (not_3_out, halt);
  and and_6 (and_6_out, Go, halt);
  Comparator #(.width(32), .mode("twosComplement")) comparator_2 (
    .a(WB_R1), .b(32'h22), .eq(comparator_2_eq));  // open: gt, lt
  Register #(.width(32), .trigger("rising"), .Select("low")) register_1 (
    .D(WB_R2), .en(ecallEq), .Q(LedData), .clk(CLK), .clr(RST));
  Counter #(.width(16), .max('hffff), .ongoal("wrap"), .trigger("rising"), .behavior("new")) counter_2 (
    .count(not_3_out), .Q(\总周期数 ), .clk(CLK), .clr(RST));  // open: load, D, carry, preset, down
  Counter #(.width(1), .max('h1), .ongoal("stay"), .trigger("rising"), .behavior("new")) counter_3 (
    .D(and_6_out), .Q(ecallFB), .clk(and_6_out), .clr(RST));  // open: load, count, carry, preset, down
  and and_7 (ecallEq, WB_ecall, comparator_2_eq);
  and and_8 (halt, WB_ecall, not_4_out);
  not not_4 (not_4_out, comparator_2_eq);

  // Other names for the same wires on the sheet: WDin[4:0] = ID_IR[11:7]; ID_IR[31:20] = I_imm; MEM_PC[31:0] = M_PC

  // Notes on the sheet:
  //   中断源
  //   时空图监测，可删除
  //   中断等待指示
  //   数码管输出
  //   指令存储器
  //   contents of rom_1 (hex, n*v repeats v):
  //   100493 100006f 100493 200913 300993 100006f 100493 200913 300993 100006f 100493 200913 300993
  //   100006f 100493 200913 300993 29c000ef 100413 100493 1f49493 900533 2200893 73 24d493 48463 fedff06f
  //   900533 2200893 73 100493 249493 900533 2200893 73 48463 fedff06f 100493 1f49493 900533 2200893 73
  //   4034d493 900533 2200893 73 4044d493 900533 2200893 73 4044d493 900533 2200893 73 4044d493 900533
  //   2200893 73 4044d493 900533 2200893 73 4044d493 900533 2200893 73 4044d493 900533 2200893 73 4044d493
  //   900533 2200893 73 100413 1f41993 41f9d993 433 c00913 300b13 140413 f47413 800293 100313 499993
  //   89e9b3 1300533 2200893 73 406282b3 fe0294e3 140413 f00f93 1f47433 1c41413 800293 100313 49d993
  //   89e9b3 1300533 2200893 73 406282b3 fe0294e3 1c45413 406b0b33 b0463 f95ff06f 2b3 fff2c293 829293
  //   ff2e293 500533 2200893 73 fff00413 493 84a023 140413 448493 84a023 140413 448493 84a023 140413
  //   448493 84a023 140413 448493 84a023 140413 448493 84a023 140413 448493 84a023 140413 448493 84a023
  //   140413 448493 84a023 140413 448493 84a023 140413 448493 84a023 140413 448493 84a023 140413 448493
  //   84a023 140413 448493 84a023 140413 448493 84a023 140413 448493 84a023 140413 448493 140413 433
  //   3c00493 42983 4aa03 149a2b3 28663 134a023 1442023 ffc48493 fe9412e3 800533 2200893 73 440413 3c00493
  //   fc9416e3 a00893 73 413 140413 800533 2200893 73 240413 800533 2200893 73 340413 800533 2200893 73
  //   440413 800533 2200893 73 540413 800533 2200893 73 640413 800533 2200893 73 740413 800533 2200893 73
  //   840413 800533 2200893 2200893 73 8067
  //   控制位
  //   流水调试日志用
  //   暂停节拍，不能为0
  //   Beq
  //   Bne
  //   MemToReg
  //   MemWrite
  //   AluOP
  //   AluSrcB
  //   RegWrite
  //   可计数暂停的时钟源
  //   为方便自动评测，需要输出流水线各段保存的PC值，注意是PC不是PC+4，另外ID段寄存器写入信息，Mem段内存写入信息也要输出
  //   数据存储器
  //   ecall比较$a7=?34
  //   ecallLED显示$a0
  //   ecall暂停
  //   ecall等待go按键
endmodule

module \中断按键参考电路  (
  input  \同步清零信号 ,
  output \与中断屏蔽位与 
);

  wire \_1号中断_out , and_1_out, clock_1_out, d_ff_1_q, or_1_out, or_2_out;

  Clock #(.highDuration(1), .lowDuration(1)) clock_1 (.out(clock_1_out));
  Button \_1号中断  (.out(\_1号中断_out ));
  or or_1 (or_1_out, \与中断屏蔽位与 , d_ff_1_q);
  LED #(.active("true")) \_1号中断等待指示灯  (.in(or_1_out));
  D_Flip_Flop #(.trigger("rising"), .Pre_Clr_Positions("LEGACY"), .NegatePresetClear("false"), .enable("true"), .NewFFLayout("false")) d_ff_1 (
    .clk(\_1号中断_out ), .D(1'b1), .Q(d_ff_1_q), .reset(\与中断屏蔽位与 ));  // open: Qn, preset, en
  or or_2 (or_2_out, d_ff_1_q, \与中断屏蔽位与 );
  and and_1 (and_1_out, or_2_out, ~\同步清零信号 );  // AND_Gate
  D_Flip_Flop #(.trigger("rising"), .Pre_Clr_Positions("LEGACY"), .NegatePresetClear("false"), .enable("true"), .NewFFLayout("false")) IR1 (
    .clk(clock_1_out), .D(and_1_out), .Q(\与中断屏蔽位与 ));  // open: Qn, preset, en, reset

  // Notes on the sheet:
  //   中断信号采样参考电路
  //   Reset 
endmodule

module \单周期_单级中断  (
  input  IR1,
  input  IR2,
  input  IR3,
  output RegWrite,
  output MemWrite,
  output [31:0] PC,
  output [31:0] IR,
  output [31:0] RDin,
  output [31:0] MDin,
  output [31:0] LedData
);

  wire alu_1_equal, alu_1_out_6, and_1_out, and_2_out, and_3_out, and_4_out, and_6_out, and_7_out, and_8_out,
       and_13_out, and_14_out, auipc, bltu, Branch, ClearA, ClearB, ClearC, CLK, clock_1_out,
       comparator_1_eq, comparator_2_eq, comparator_3_eq, comparator_4_eq, comparator_5_eq, comparator_5_lt,
       comparator_6_eq, d_ff_1_q, decoder_1_out1, decoder_1_out2, decoder_1_out3, ecall, Go, halt, IE, INT,
       IR1_t, IR2_t, IR3_t, IRA, IRB, IRC, JAL, JALR, MemToReg, nand_1_out, not_1_out, not_2_out, not_3_out,
       not_4_out, or_2_out, or_8_out, or_9_out, or_10_out, or_11_out, or_12_out, or_13_out, or_14_out,
       or_16_out, register_1_q, register_2_q, register_3_q, register_4_q, register_5_q, register_6_q, RST,
       sb, sltiu, URET, W1, W2, W3, \中断信号 , \单周期硬布线控制器_1_alu_src , \单周期硬布线控制器_1_beq , \单周期硬布线控制器_1_bne ,
       \单周期硬布线控制器_1_s_type ;
  wire [1:0] register_7_q, \中断号 ;
  wire [3:0] sb_1_out_3, \单周期硬布线控制器_1_alu_op ;
  wire [4:0] multiplexer_6_out, multiplexer_7_out;
  wire [11:0] multiplexer_8_out;
  wire [12:0] CNT_num;
  wire [15:0] \总周期数 ;
  wire [31:0] adder_1_out, adder_5_out, ALU_result, bit_extender_1_out, bit_extender_2_out,
       bit_extender_3_out, bit_extender_4_out, Branch_Adress, INTPC, JAL_Adress, JALR_Adress, LocalPC,
       mips_ram_1_p7, multiplexer_1_out, multiplexer_3_out, multiplexer_4_out, multiplexer_5_out,
       multiplexer_9_out, multiplexer_10_out, multiplexer_13_out, multiplexer_14_out, r1, r2, RETPC,
       sb_1_darta, shifter_1_out, shifter_2_out, shifter_3_out, U_adress;

  Button \u_继续运行  (.out(Go));
  Button _1 ();  // open: out
  Button _2 ();  // open: out
  Button _3 ();  // open: out
  LED #(.active("true")) led_1 (.in(W1));
  LED #(.active("true")) led_2 (.in(W2));
  LED #(.active("true")) led_3 (.in(W3));
  Multiplexer #(.select(1), .width(32), .disabled("Z"), .enable("false")) multiplexer_1 (
    .in0(adder_1_out), .in1(Branch_Adress), .out(multiplexer_1_out), .sel(Branch));
  Hex_Digit_Display hex_digit_display_1 (.value(LedData[31:28]));  // open: dp
  Multiplexer #(.select(1), .width(32), .disabled("Z"), .enable("false")) multiplexer_2 (
    .in0(multiplexer_3_out), .in1(JAL_Adress), .out(LocalPC), .sel(JAL));
  Multiplexer #(.select(1), .width(32), .disabled("Z"), .enable("false")) multiplexer_3 (
    .in0(multiplexer_1_out), .in1(JALR_Adress), .out(multiplexer_3_out), .sel(JALR));
  Hex_Digit_Display hex_digit_display_2 (.value(LedData[23:20]));  // open: dp
  Hex_Digit_Display hex_digit_display_3 (.value(LedData[27:24]));  // open: dp
  Hex_Digit_Display hex_digit_display_4 (.value(LedData[19:16]));  // open: dp
  Hex_Digit_Display hex_digit_display_5 (.value(LedData[15:12]));  // open: dp
  Multiplexer #(.select(1), .width(32), .disabled("Z"), .enable("false")) multiplexer_4 (
    .in0(LocalPC), .in1(RETPC), .out(multiplexer_4_out), .sel(URET));
  Hex_Digit_Display hex_digit_display_6 (.value(LedData[11:8]));  // open: dp
  Hex_Digit_Display hex_digit_display_7 (.value(LedData[7:4]));  // open: dp
  // Probe on \总周期数 
  Multiplexer #(.select(1), .width(32), .disabled("Z"), .enable("false")) multiplexer_5 (
    .in0(multiplexer_4_out), .in1(INTPC), .out(multiplexer_5_out), .sel(INT));
  Hex_Digit_Display hex_digit_display_8 (.value(LedData[3:0]));  // open: dp
  Button button_1 (.out(RST));
  not not_1 (not_1_out, halt);
  Register #(.width(32), .trigger("rising"), .Select("low")) u_PC (
    .D(multiplexer_5_out), .en(not_1_out), .Q(PC), .clk(CLK), .clr(RST));
  Adder #(.width(32)) adder_1 (.a(PC), .b(32'h4), .out(adder_1_out));  // open: cin, cout
  Comparator #(.width(16), .mode("twosComplement")) comparator_1 (
    .a(16'h23b), .b(\总周期数 ), .eq(comparator_1_eq));  // open: gt, lt
  Comparator #(.width(16), .mode("twosComplement")) comparator_2 (
    .a(\总周期数 ), .b(16'h1), .eq(comparator_2_eq));  // open: gt, lt
  Comparator #(.width(16), .mode("twosComplement")) comparator_3 (
    .a(\总周期数 ), .b(16'h4), .eq(comparator_3_eq));  // open: gt, lt
  Comparator #(.width(16), .mode("twosComplement")) comparator_4 (
    .a(\总周期数 ), .b(16'h7), .eq(comparator_4_eq));  // open: gt, lt
  or or_1 (IR1_t, IR1, IRA);
  or or_2 (or_2_out, comparator_1_eq, comparator_2_eq);
  Pull_Resistor #(.pull(0)) pull_resistor_1 (.node(IRA));
  assign IRA = or_2_out ? ~CLK : 1'bz;  // Controlled_Inverter controlled_inverter_1
  Pull_Resistor #(.pull(0)) pull_resistor_2 (.node(IRB));
  assign IRB = comparator_3_eq ? ~CLK : 1'bz;  // Controlled_Inverter controlled_inverter_2
  Pull_Resistor #(.pull(0)) pull_resistor_3 (.node(IRC));
  assign IRC = comparator_4_eq ? ~CLK : 1'bz;  // Controlled_Inverter controlled_inverter_3
  or or_3 (IR2_t, IR2, IRB);
  // RiscV_Probe riscv_probe_1: pin names not known; wires that end beside it: Branch, IR, ecall
  ROM #(.addrWidth(10), .dataWidth(32), .Select("high")) rom_1 (.addr(PC[11:2]), .data(IR));
  or or_4 (IR3_t, IR3, IRC);
  Multiplexer #(.select(1), .width(5), .disabled("Z"), .enable("false")) multiplexer_6 (
    .in0(IR[19:15]), .in1(5'b10001), .out(multiplexer_6_out), .sel(ecall));
  Multiplexer #(.select(1), .width(5), .disabled("Z"), .enable("false")) multiplexer_7 (
    .in0(IR[24:20]), .in1(5'b01010), .out(multiplexer_7_out), .sel(ecall));
  or or_5 (W1, register_4_q, register_1_q);
  or or_6 (W2, register_5_q, register_2_q);
  or or_7 (W3, register_6_q, register_3_q);
  \单周期硬布线控制器  \u_单周期硬布线控制器_1  (
    .Funct({IR[30], IR[25], IR[14:12]}), .OP(IR[6:2]), .ALU_OP(\单周期硬布线控制器_1_alu_op ), .MemToReg(MemToReg),
    .MemWrite(MemWrite), .ALU_SRC(\单周期硬布线控制器_1_alu_src ), .RegWrite(RegWrite), .ecall(ecall),
    .S_type(\单周期硬布线控制器_1_s_type ), .Jalr(JALR), .Beq(\单周期硬布线控制器_1_beq ), .JAL(JAL), .Bne(\单周期硬布线控制器_1_bne ),
    .in_3(IR[21]), .uret(URET), .sb(sb), .auipc(auipc), .bltu(bltu), .sltiu(sltiu));  // open: rs1, rs2, CSRRSI, CSRRCI
  Multiplexer #(.select(1), .width(12), .disabled("Z"), .enable("false")) multiplexer_8 (
    .in0(IR[31:20]), .in1({IR[31:25], IR[11:7]}), .out(multiplexer_8_out), .sel(\单周期硬布线控制器_1_s_type ));
  Register #(.width(1), .trigger("rising"), .Select("low")) register_1 (
    .D(1'b1), .Q(register_1_q), .clk(IRA), .clr(or_8_out));  // open: en
  or or_8 (or_8_out, register_4_q, RST);
  Register #(.width(1), .trigger("rising"), .Select("low")) register_2 (
    .D(1'b1), .Q(register_2_q), .clk(IRB), .clr(or_9_out));  // open: en
  or or_9 (or_9_out, register_5_q, RST);
  Register #(.width(1), .trigger("rising"), .Select("low")) register_3 (
    .D(1'b1), .Q(register_3_q), .clk(IRC), .clr(or_10_out));  // open: en
  or or_10 (or_10_out, register_6_q, RST);
  assign bit_extender_1_out = {{20{IR[31]}}, {IR[31], IR[7], IR[30:25], IR[11:8]}};  // Bit_Extender bit_extender_1
  assign bit_extender_2_out = {{12{IR[31]}}, {IR[31], IR[19:12], IR[20], IR[30:21]}};  // Bit_Extender bit_extender_2
  assign bit_extender_3_out = {{12{1'b0}}, IR[31:12]};  // Bit_Extender bit_extender_3
  or or_11 (or_11_out, register_1_q, register_4_q);
  or or_12 (or_12_out, register_2_q, register_5_q);
  or or_13 (or_13_out, register_3_q, register_6_q);
  Regifile regifile_1 (
    .Din(RDin), .Clk(CLK), .R1(r1), .R2(r2), .WE(RegWrite), .W_num(IR[11:7]), .R1_num(multiplexer_6_out),
    .R2_num(multiplexer_7_out));
  assign bit_extender_4_out = {{20{multiplexer_8_out[11]}}, multiplexer_8_out};  // Bit_Extender bit_extender_4
  Shifter #(.width(32), .shift("ll")) shifter_1 (.in(bit_extender_1_out), .\dist (5'b00001), .out(shifter_1_out));
  Shifter #(.width(32), .shift("ll")) shifter_2 (.in(bit_extender_2_out), .\dist (5'b00001), .out(shifter_2_out));
  Multiplexer #(.select(1), .width(32), .disabled("Z"), .enable("false")) multiplexer_9 (
    .in0({32{1'b0}}), .in1(bit_extender_3_out), .out(multiplexer_9_out), .sel(auipc));
  and and_1 (and_1_out, or_11_out, ~ClearA);  // AND_Gate
  and and_2 (and_2_out, or_12_out, ~ClearB);  // AND_Gate
  and and_3 (and_3_out, or_13_out, ~ClearC);  // AND_Gate
  Adder #(.width(32)) adder_2 (.a(shifter_1_out), .b(PC), .out(Branch_Adress));  // open: cin, cout
  Adder #(.width(32)) adder_3 (.a(shifter_2_out), .b(PC), .out(JAL_Adress));  // open: cin, cout
  Shifter #(.width(32), .shift("ll")) shifter_3 (.in(multiplexer_9_out), .\dist (5'b01100), .out(shifter_3_out));
  Register #(.width(1), .trigger("rising"), .Select("low")) register_4 (
    .D(and_1_out), .Q(register_4_q), .clk(CLK), .clr(RST));  // open: en
  Register #(.width(1), .trigger("rising"), .Select("low")) register_5 (
    .D(and_2_out), .Q(register_5_q), .clk(CLK), .clr(RST));  // open: en
  Register #(.width(1), .trigger("rising"), .Select("low")) register_6 (
    .D(and_3_out), .Q(register_6_q), .clk(CLK), .clr(RST));  // open: en
  Multiplexer #(.select(1), .width(32), .disabled("Z"), .enable("false")) multiplexer_10 (
    .in0(r2), .in1(bit_extender_4_out), .out(multiplexer_10_out), .sel(\单周期硬布线控制器_1_alu_src ));
  Adder #(.width(32)) adder_4 (.a(shifter_3_out), .b(PC), .out(U_adress));  // open: cin, cout
  Priority_Encoder #(.select(2), .disabled("Z")) priority_encoder_1 (
    .in1(register_4_q), .in2(register_5_q), .in3(register_6_q), .out(\中断号 ), .gs(\中断信号 ));  // open: in0, en_out, en_in
  D_Flip_Flop #(.trigger("high"), .Pre_Clr_Positions("LEGACY"), .NegatePresetClear("false"), .enable("true"), .NewFFLayout("false")) d_ff_1 (.Q(d_ff_1_q));  // open: clk, D, Qn, preset, en, reset
  // Probe on 13'hc
  Comparator #(.width(13), .mode("twosComplement")) comparator_5 (
    .a(CNT_num), .b(13'hc), .eq(comparator_5_eq), .lt(comparator_5_lt));  // open: gt
  Clock #(.highDuration(1), .lowDuration(1)) clock_1 (.out(clock_1_out));
  Register #(.width(2), .trigger("rising"), .Select("low")) register_7 (
    .D(\中断号 ), .en(INT), .Q(register_7_q), .clk(CLK), .clr(RST));
  Counter #(.width(13), .max('h1fff), .ongoal("stay"), .trigger("rising"), .behavior("old")) counter_1 (
    .count(comparator_5_lt), .Q(CNT_num), .clk(clock_1_out));  // open: load, D, carry, clr, preset
  not not_2 (not_2_out, alu_1_equal);
  ALU alu_1 (
    .X(r1), .Y(multiplexer_10_out), .AluOP(\单周期硬布线控制器_1_alu_op ), .Equal(alu_1_equal), .Result(ALU_result),
    .out_6(alu_1_out_6));  // open: Result_2, out_4
  sb sb_1 (.in_1(sb), .R2(r2), .out_3(sb_1_out_3), .darta(sb_1_darta));
  Multiplexer #(.select(1), .width(32), .disabled("Z"), .enable("false")) multiplexer_11 (
    .in0(r2), .in1(sb_1_darta), .out(MDin), .sel(sb));
  and and_4 (and_4_out, \中断信号 , ~URET);  // AND_Gate
  and and_5 (INT, \中断信号 , IE);
  Register #(.width(32), .trigger("falling"), .Select("low")) mEPC (
    .D(LocalPC), .en(INT), .Q(RETPC), .clk(CLK), .clr(RST));
  Decoder #(.select(2), .tristate("false"), .disabled("Z"), .enable("false")) decoder_1 (
    .out1(decoder_1_out1), .out2(decoder_1_out2), .out3(decoder_1_out3), .sel(register_7_q));  // open: out0
  nand nand_1 (nand_1_out, d_ff_1_q, comparator_5_eq);
  and and_6 (and_6_out, \单周期硬布线控制器_1_beq , alu_1_equal);
  and and_7 (and_7_out, \单周期硬布线控制器_1_bne , not_2_out);
  and and_8 (and_8_out, bltu, alu_1_out_6);
  D_Flip_Flop #(.trigger("rising"), .Pre_Clr_Positions("ABOVE_BELOW"), .NegatePresetClear("false"), .enable("false"), .NewFFLayout("true")) u_IE (
    .clk(CLK), .D(and_4_out), .Qn(IE), .reset(RST));  // open: Q, preset
  Multiplexer #(.select(2), .width(32), .disabled("Z"), .enable("false")) multiplexer_12 (
    .in1(32'h30ac), .in2(32'h3150), .in3(32'h31f4), .out(INTPC), .sel(\中断号 ));  // open: in0
  and and_9 (ClearA, URET, decoder_1_out1);
  and and_10 (ClearB, URET, decoder_1_out2);
  and and_11 (ClearC, decoder_1_out3, URET);
  assign CLK = nand_1_out ? clock_1_out : 1'bz;  // Controlled_Buffer controlled_buffer_1
  Pull_Resistor #(.pull(1)) pull_resistor_4 (.node(CLK));
  or or_14 (or_14_out, and_6_out, and_7_out);
  // MIPS_RAM mips_ram_1: pin names not known; wires that end beside it: ALU_result[11:2], MDin, MemWrite, sb_1_out_3, CLK, RST, mips_ram_1_p7
  or or_15 (Branch, or_14_out, and_8_out);
  Adder #(.width(32)) adder_5 (.a(PC), .b(32'h4), .out(adder_5_out));  // open: cin, cout
  Multiplexer #(.select(1), .width(32), .disabled("Z"), .enable("false")) multiplexer_13 (
    .in0(ALU_result), .in1(mips_ram_1_p7), .out(multiplexer_13_out), .sel(MemToReg));
  assign JALR_Adress = ALU_result & 32'hfffffffe;  // AND_Gate and_12, 32 bits wide
  or or_16 (or_16_out, JAL, JALR);
  Multiplexer #(.select(1), .width(32), .disabled("Z"), .enable("false")) multiplexer_14 (
    .in0(multiplexer_13_out), .in1(adder_5_out), .out(multiplexer_14_out), .sel(or_16_out));
  Comparator #(.width(32), .mode("twosComplement")) comparator_6 (
    .a(32'h22), .b(r1), .eq(comparator_6_eq));  // open: gt, lt
  Multiplexer #(.select(1), .width(32), .disabled("Z"), .enable("false")) multiplexer_15 (
    .in0(multiplexer_14_out), .in1(U_adress), .out(RDin), .sel(auipc));
  and and_13 (and_13_out, ecall, comparator_6_eq);
  and and_14 (and_14_out, ecall, not_3_out);
  not not_3 (not_3_out, comparator_6_eq);
  Multiplexer #(.select(1), .width(1), .disabled("Z"), .enable("false")) multiplexer_16 (
    .in0(and_14_out), .in1(1'b0), .out(halt), .sel(Go));
  Register #(.width(32), .trigger("rising"), .Select("low")) register_8 (
    .D(MDin), .en(and_13_out), .Q(LedData), .clk(CLK), .clr(RST));
  not not_4 (not_4_out, halt);
  Counter #(.width(16), .max('hffff), .ongoal("wrap"), .trigger("rising"), .behavior("new")) counter_2 (
    .count(not_4_out), .Q(\总周期数 ), .clk(CLK), .clr(RST));  // open: load, D, carry, preset, down

  // Other names for the same wires on the sheet: I_imm[11:0] = IR[31:20]

  // Notes on the sheet:
  //   中断源
  //   中断等待指示
  //   总复位信号应将除ROM以外所有存储组件全部清零
  //   数码管输出
  //   数码管输出应该用寄存器锁存，否则显示数据只能一闪而过
  //   数码管输出应该用寄存器锁存，否则显示数据只能一闪而过
  //   单级中断测试信号模拟器
  //   中断信号采样参考电路
  //   指令探针
  //   指令存储器
  //   contents of rom_1 (hex, n*v repeats v):
  //   7d000113 100413 1f41993 41f9d993 433 c00913 800b13 140413 f47413 800293 100313 499993 89e9b3 1300533
  //   2200893 73 406282b3 fe0294e3 140413 f00f93 1f47433 1c41413 800293 100313 49d993 89e9b3 1300533
  //   2200893 73 406282b3 fe0294e3 1c45413 406b0b33 b0463 f95ff06f 2b3 fff2c293 1029293 fff2e293 500533
  //   2200893 73 f5dff06f 1112023 410113 a12023 410113 812023 410113 1312023 410113 1412023 410113 1512023
  //   410113 1612023 410113 100b13 300a13 100a93 1600433 441413 14469b3 1300533 2200893 73 fe0416e3
  //   415a0a33 fe0a10e3 ffc10113 12b03 ffc10113 12a83 ffc10113 12a03 ffc10113 12983 ffc10113 12403
  //   ffc10113 12503 ffc10113 12883 200073 1112023 410113 a12023 410113 812023 410113 1312023 410113
  //   1412023 410113 1512023 410113 1612023 410113 200b13 300a13 100a93 1600433 441413 14469b3 1300533
  //   2200893 73 fe0416e3 415a0a33 fe0a10e3 ffc10113 12b03 ffc10113 12a83 ffc10113 12a03 ffc10113 12983
  //   ffc10113 12403 ffc10113 12503 ffc10113 12883 200073 1112023 410113 a12023 410113 812023 410113
  //   1312023 410113 1412023 410113 1512023 410113 1612023 410113 300b13 300a13 100a93 1600433 441413
  //   14469b3 1300533 2200893 73 fe0416e3 415a0a33 fe0a10e3 ffc10113 12b03 ffc10113 12a83 ffc10113 12a03
  //   ffc10113 12983 ffc10113 12403 ffc10113 12503 ffc10113 12883 200073
  //   指令字
  //   JAL
  //   JALR
  //   URET
  //   Beq
  //   Bne
  //   MemToReg
  //   MemWrite
  //   AluOP
  //   AluSrcB
  //   RegWrite
  //   为方便自动评测，需要输出PC，IR，寄存器堆写如数据RDin
  //   RAM写使能MemWrite、RAM写入数据MDin等信号
  //   控制位
  //   暂停节拍，不能为0
  //   戳工具置1进入计数暂停模式，ctrl+k时钟自动运行到对应节拍暂停
  //   ctrl+k关闭时钟连续运行，将控制位置零，进入单步调试模式调试
  //   数据存储器
  //   可计数暂停的时钟源
  //   用这个时钟源需要去掉电路中的其他时钟源
endmodule

module \单周期_多级中断  (
  input  IR1,
  input  IR2,
  input  IR3,
  output RegWrite,
  output MemWrite,
  output [31:0] PC,
  output [31:0] IR,
  output [31:0] RDin,
  output [31:0] MDin,
  output [31:0] LedData
);

  wire alu_1_equal, alu_1_out_6, and_1_out, and_2_out, and_3_out, and_8_out, and_9_out, and_10_out,
       and_11_out, and_12_out, and_13_out, and_14_out, and_15_out, and_16_out, and_17_out, and_18_out,
       and_19_out, and_20_out, and_21_out, auipc, bltu, Branch, ClearA, ClearB, ClearC, CLK, clock_1_out,
       comparator_1_eq, comparator_2_eq, comparator_3_eq, comparator_4_eq, comparator_5_eq, comparator_6_eq,
       comparator_6_lt, comparator_7_eq, comparator_8_gt, counter_3_q, CSRRCI, CSRRSI, d_ff_1_q,
       decoder_1_out1, decoder_1_out2, decoder_1_out3, decoder_2_out1, decoder_2_out2, decoder_2_out3,
       decoder_3_out1, decoder_3_out2, decoder_3_out3, ecall, EPC1_q, EPC2_q, EPC3_q, Go, halt, IE, INT,
       IR1_t, IR2_t, IR3_t, IRA, IRB, IRC, JAL, JALR, MemToReg, nand_1_out, not_1_out, not_2_out, not_3_out,
       not_4_out, not_5_out, or_1_out, or_2_out, or_6_out, or_8_out, or_9_out, or_13_out, or_14_out,
       or_15_out, or_16_out, or_17_out, or_18_out, or_20_out, or_21_out, register_2_q, register_3_q,
       register_4_q, register_5_q, register_6_q, register_7_q, RST, sb, sltiu, URET, W1, W2, W3, \中断信号 ,
       \优先中断 , \单周期硬布线控制器_1_alu_src , \单周期硬布线控制器_1_beq , \单周期硬布线控制器_1_bne , \单周期硬布线控制器_1_s_type ;
  wire [1:0] \中断号 , \当前中断号 ;
  wire [3:0] sb_1_out_3, \单周期硬布线控制器_1_alu_op ;
  wire [4:0] multiplexer_6_out, multiplexer_7_out;
  wire [11:0] multiplexer_8_out;
  wire [12:0] CNT_num;
  wire [15:0] \总周期数 ;
  wire [31:0] adder_1_out, adder_5_out, ALU_result, bit_extender_1_out, bit_extender_2_out,
       bit_extender_3_out, bit_extender_4_out, Branch_Adress, INTPC, JAL_Adress, JALR_Adress, LocalPC,
       mEPC1_q, mEPC2_q, mEPC3_q, mips_ram_1_p7, multiplexer_1_out, multiplexer_3_out, multiplexer_4_out,
       multiplexer_5_out, multiplexer_9_out, multiplexer_10_out, multiplexer_12_out, multiplexer_13_out, r1,
       r2, RETPC, sb_1_darta, shifter_1_out, shifter_2_out, shifter_3_out, U_adress;

  Button \u_继续运行  (.out(Go));
  Button _1 (.out(IRA));
  Button _2 (.out(IRB));
  Button _3 (.out(IRC));
  LED #(.active("true")) led_1 (.in(W1));
  LED #(.active("true")) led_2 (.in(W2));
  LED #(.active("true")) led_3 (.in(W3));
  Multiplexer #(.select(1), .width(32), .disabled("Z"), .enable("false")) multiplexer_1 (
    .in0(adder_1_out), .in1(Branch_Adress), .out(multiplexer_1_out), .sel(Branch));
  Hex_Digit_Display hex_digit_display_1 (.value(LedData[31:28]));  // open: dp
  Comparator #(.width(16), .mode("twosComplement")) comparator_1 (
    .a(\总周期数 ), .b(16'h7), .eq(comparator_1_eq));  // open: gt, lt
  Comparator #(.width(16), .mode("twosComplement")) comparator_2 (
    .a(\总周期数 ), .b(16'h241), .eq(comparator_2_eq));  // open: gt, lt
  Multiplexer #(.select(1), .width(32), .disabled("Z"), .enable("false")) multiplexer_2 (
    .in0(multiplexer_3_out), .in1(JAL_Adress), .out(LocalPC), .sel(JAL));
  Multiplexer #(.select(1), .width(32), .disabled("Z"), .enable("false")) multiplexer_3 (
    .in0(multiplexer_1_out), .in1(JALR_Adress), .out(multiplexer_3_out), .sel(JALR));
  Hex_Digit_Display hex_digit_display_2 (.value(LedData[27:24]));  // open: dp
  Hex_Digit_Display hex_digit_display_3 (.value(LedData[23:20]));  // open: dp
  Comparator #(.width(16), .mode("twosComplement")) comparator_3 (
    .a(16'h258), .b(\总周期数 ), .eq(comparator_3_eq));  // open: gt, lt
  or or_1 (or_1_out, comparator_3_eq, comparator_4_eq);
  Comparator #(.width(16), .mode("twosComplement")) comparator_4 (
    .a(\总周期数 ), .b(16'h1), .eq(comparator_4_eq));  // open: gt, lt
  Comparator #(.width(16), .mode("twosComplement")) comparator_5 (
    .a(\总周期数 ), .b(16'h4), .eq(comparator_5_eq));  // open: gt, lt
  or or_2 (or_2_out, comparator_1_eq, comparator_2_eq);
  Hex_Digit_Display hex_digit_display_4 (.value(LedData[19:16]));  // open: dp
  Hex_Digit_Display hex_digit_display_5 (.value(LedData[15:12]));  // open: dp
  Pull_Resistor #(.pull(0)) pull_resistor_1 (.node(IRA));
  assign IRA = or_1_out ? ~CLK : 1'bz;  // Controlled_Inverter controlled_inverter_1
  Pull_Resistor #(.pull(0)) pull_resistor_2 (.node(IRB));
  assign IRB = comparator_5_eq ? ~CLK : 1'bz;  // Controlled_Inverter controlled_inverter_2
  Pull_Resistor #(.pull(0)) pull_resistor_3 (.node(IRC));
  assign IRC = or_2_out ? ~CLK : 1'bz;  // Controlled_Inverter controlled_inverter_3
  Multiplexer #(.select(1), .width(32), .disabled("Z"), .enable("false")) multiplexer_4 (
    .in0(LocalPC), .in1(RETPC), .out(multiplexer_4_out), .sel(URET));
  Hex_Digit_Display hex_digit_display_6 (.value(LedData[7:4]));  // open: dp
  Hex_Digit_Display hex_digit_display_7 (.value(LedData[11:8]));  // open: dp
  // Probe on \总周期数 
  Multiplexer #(.select(1), .width(32), .disabled("Z"), .enable("false")) multiplexer_5 (
    .in0(multiplexer_4_out), .in1(INTPC), .out(multiplexer_5_out), .sel(INT));
  Hex_Digit_Display hex_digit_display_8 (.value(LedData[3:0]));  // open: dp
  Button button_1 (.out(RST));
  not not_1 (not_1_out, halt);
  Register #(.width(32), .trigger("rising"), .Select("low")) u_PC (
    .D(multiplexer_5_out), .en(not_1_out), .Q(PC), .clk(CLK), .clr(RST));
  Adder #(.width(32)) adder_1 (.a(PC), .b(32'h4), .out(adder_1_out));  // open: cin, cout
  or or_3 (IR1_t, IR1, IRA);
  or or_4 (IR2_t, IR2, IRB);
  // RiscV_Probe riscv_probe_1: pin names not known; wires that end beside it: Branch, IR, ecall
  ROM #(.addrWidth(10), .dataWidth(32), .Select("high")) rom_1 (.addr(PC[11:2]), .data(IR));
  or or_5 (IR3_t, IR3, IRC);
  Multiplexer #(.select(1), .width(5), .disabled("Z"), .enable("false")) multiplexer_6 (
    .in0(IR[19:15]), .in1(5'b10001), .out(multiplexer_6_out), .sel(ecall));
  Multiplexer #(.select(1), .width(5), .disabled("Z"), .enable("false")) multiplexer_7 (
    .in0(IR[24:20]), .in1(5'b01010), .out(multiplexer_7_out), .sel(ecall));
  \单周期硬布线控制器  \u_单周期硬布线控制器_1  (
    .Funct({IR[30], IR[25], IR[14:12]}), .OP(IR[6:2]), .ALU_OP(\单周期硬布线控制器_1_alu_op ), .MemToReg(MemToReg),
    .MemWrite(MemWrite), .ALU_SRC(\单周期硬布线控制器_1_alu_src ), .RegWrite(RegWrite), .ecall(ecall),
    .S_type(\单周期硬布线控制器_1_s_type ), .Jalr(JALR), .Beq(\单周期硬布线控制器_1_beq ), .JAL(JAL), .Bne(\单周期硬布线控制器_1_bne ),
    .in_3(IR[21]), .uret(URET), .sb(sb), .auipc(auipc), .bltu(bltu), .sltiu(sltiu), .CSRRSI(CSRRSI),
    .CSRRCI(CSRRCI));  // open: rs1, rs2
  Multiplexer #(.select(1), .width(12), .disabled("Z"), .enable("false")) multiplexer_8 (
    .in0(IR[31:20]), .in1({IR[31:25], IR[11:7]}), .out(multiplexer_8_out), .sel(\单周期硬布线控制器_1_s_type ));
  assign bit_extender_1_out = {{20{IR[31]}}, {IR[31], IR[7], IR[30:25], IR[11:8]}};  // Bit_Extender bit_extender_1
  assign bit_extender_2_out = {{12{IR[31]}}, {IR[31], IR[19:12], IR[20], IR[30:21]}};  // Bit_Extender bit_extender_2
  assign bit_extender_3_out = {{12{1'b0}}, IR[31:12]};  // Bit_Extender bit_extender_3
  Regifile regifile_1 (
    .Din(RDin), .Clk(CLK), .R1(r1), .R2(r2), .WE(RegWrite), .W_num(IR[11:7]), .R1_num(multiplexer_6_out),
    .R2_num(multiplexer_7_out));
  assign bit_extender_4_out = {{20{multiplexer_8_out[11]}}, multiplexer_8_out};  // Bit_Extender bit_extender_4
  Shifter #(.width(32), .shift("ll")) shifter_1 (.in(bit_extender_1_out), .\dist (5'b00001), .out(shifter_1_out));
  Shifter #(.width(32), .shift("ll")) shifter_2 (.in(bit_extender_2_out), .\dist (5'b00001), .out(shifter_2_out));
  Multiplexer #(.select(1), .width(32), .disabled("Z"), .enable("false")) multiplexer_9 (
    .in0({32{1'b0}}), .in1(bit_extender_3_out), .out(multiplexer_9_out), .sel(auipc));
  Adder #(.width(32)) adder_2 (.a(shifter_1_out), .b(PC), .out(Branch_Adress));  // open: cin, cout
  Adder #(.width(32)) adder_3 (.a(shifter_2_out), .b(PC), .out(JAL_Adress));  // open: cin, cout
  Shifter #(.width(32), .shift("ll")) shifter_3 (.in(multiplexer_9_out), .\dist (5'b01100), .out(shifter_3_out));
  Multiplexer #(.select(1), .width(32), .disabled("Z"), .enable("false")) multiplexer_10 (
    .in0(r2), .in1(bit_extender_4_out), .out(multiplexer_10_out), .sel(\单周期硬布线控制器_1_alu_src ));
  Adder #(.width(32)) adder_4 (.a(shifter_3_out), .b(PC), .out(U_adress));  // open: cin, cout
  D_Flip_Flop #(.trigger("high"), .Pre_Clr_Positions("LEGACY"), .NegatePresetClear("false"), .enable("true"), .NewFFLayout("false")) d_ff_1 (.Q(d_ff_1_q));  // open: clk, D, Qn, preset, en, reset
  // Probe on 13'hc
  Comparator #(.width(13), .mode("twosComplement")) comparator_6 (
    .a(CNT_num), .b(13'hc), .eq(comparator_6_eq), .lt(comparator_6_lt));  // open: gt
  Clock #(.highDuration(1), .lowDuration(1)) clock_1 (.out(clock_1_out));
  Counter #(.width(13), .max('h1fff), .ongoal("stay"), .trigger("rising"), .behavior("old")) counter_1 (
    .count(comparator_6_lt), .Q(CNT_num), .clk(clock_1_out));  // open: load, D, carry, clr, preset
  not not_2 (not_2_out, alu_1_equal);
  ALU alu_1 (
    .X(r1), .Y(multiplexer_10_out), .AluOP(\单周期硬布线控制器_1_alu_op ), .Equal(alu_1_equal), .Result(ALU_result),
    .out_6(alu_1_out_6));  // open: Result_2, out_4
  sb sb_1 (.in_1(sb), .R2(r2), .out_3(sb_1_out_3), .darta(sb_1_darta));
  Multiplexer #(.select(1), .width(32), .disabled("Z"), .enable("false")) multiplexer_11 (
    .in0(r2), .in1(sb_1_darta), .out(MDin), .sel(sb));
  nand nand_1 (nand_1_out, d_ff_1_q, comparator_6_eq);
  and and_1 (and_1_out, \单周期硬布线控制器_1_beq , alu_1_equal);
  and and_2 (and_2_out, \单周期硬布线控制器_1_bne , not_2_out);
  and and_3 (and_3_out, bltu, alu_1_out_6);
  assign CLK = nand_1_out ? clock_1_out : 1'bz;  // Controlled_Buffer controlled_buffer_1
  Pull_Resistor #(.pull(1)) pull_resistor_4 (.node(CLK));
  or or_6 (or_6_out, and_1_out, and_2_out);
  // MIPS_RAM mips_ram_1: pin names not known; wires that end beside it: ALU_result[11:2], MDin, MemWrite, sb_1_out_3, CLK, RST, mips_ram_1_p7
  or or_7 (Branch, or_6_out, and_3_out);
  Adder #(.width(32)) adder_5 (.a(PC), .b(32'h4), .out(adder_5_out));  // open: cin, cout
  Decoder #(.select(2), .tristate("false"), .disabled("Z"), .enable("false")) decoder_1 (
    .out1(decoder_1_out1), .out2(decoder_1_out2), .out3(decoder_1_out3), .sel(\当前中断号 ));  // open: out0
  Multiplexer #(.select(1), .width(32), .disabled("Z"), .enable("false")) multiplexer_12 (
    .in0(ALU_result), .in1(mips_ram_1_p7), .out(multiplexer_12_out), .sel(MemToReg));
  assign JALR_Adress = ALU_result & 32'hfffffffe;  // AND_Gate and_4, 32 bits wide
  and and_5 (ClearA, URET, decoder_1_out1);
  and and_6 (ClearB, URET, decoder_1_out2);
  and and_7 (ClearC, decoder_1_out3, URET);
  or or_8 (or_8_out, JAL, JALR);
  Multiplexer #(.select(1), .width(32), .disabled("Z"), .enable("false")) multiplexer_13 (
    .in0(multiplexer_12_out), .in1(adder_5_out), .out(multiplexer_13_out), .sel(or_8_out));
  Comparator #(.width(32), .mode("twosComplement")) comparator_7 (
    .a(32'h22), .b(r1), .eq(comparator_7_eq));  // open: gt, lt
  Multiplexer #(.select(1), .width(32), .disabled("Z"), .enable("false")) multiplexer_14 (
    .in0(multiplexer_13_out), .in1(U_adress), .out(RDin), .sel(auipc));
  and and_8 (and_8_out, ecall, comparator_7_eq);
  and and_9 (and_9_out, ecall, not_3_out);
  not not_3 (not_3_out, comparator_7_eq);
  or or_9 (or_9_out, URET, IE);
  Decoder #(.select(2), .tristate("false"), .disabled("Z"), .enable("false")) decoder_2 (
    .out1(decoder_2_out1), .out2(decoder_2_out2), .out3(decoder_2_out3), .sel(\中断号 ));  // open: out0
  Multiplexer #(.select(1), .width(1), .disabled("Z"), .enable("false")) multiplexer_15 (
    .in0(and_9_out), .in1(1'b0), .out(halt), .sel(Go));
  Decoder #(.select(2), .tristate("false"), .disabled("Z"), .enable("false")) decoder_3 (
    .out1(decoder_3_out1), .out2(decoder_3_out2), .out3(decoder_3_out3), .sel(\中断号 ));  // open: out0
  Register #(.width(32), .trigger("rising"), .Select("low")) register_1 (
    .D(MDin), .en(and_8_out), .Q(LedData), .clk(CLK), .clr(RST));
  not not_4 (not_4_out, halt);
  Counter #(.width(16), .max('hffff), .ongoal("wrap"), .trigger("rising"), .behavior("new")) counter_2 (
    .count(not_4_out), .Q(\总周期数 ), .clk(CLK), .clr(RST));  // open: load, D, carry, preset, down
  and and_10 (and_10_out, \优先中断 , decoder_3_out1);
  and and_11 (and_11_out, decoder_3_out2, \优先中断 );
  and and_12 (and_12_out, decoder_3_out3, \优先中断 );
  and and_13 (and_13_out, or_9_out, decoder_2_out1);
  and and_14 (and_14_out, decoder_2_out2, or_9_out);
  and and_15 (and_15_out, decoder_2_out3, or_9_out);
  Register #(.width(32), .trigger("rising"), .Select("low")) mEPC1 (
    .D(LocalPC), .en(and_10_out), .Q(mEPC1_q), .clk(CLK), .clr(RST));
  Register #(.width(1), .trigger("rising"), .Select("low")) EPC1 (
    .D(and_16_out), .en(and_13_out), .Q(EPC1_q), .clk(CLK), .clr(RST));
  and and_16 (and_16_out, ~ClearA, 1'b1);  // AND_Gate
  Register #(.width(32), .trigger("rising"), .Select("low")) mEPC2 (
    .D(LocalPC), .en(and_11_out), .Q(mEPC2_q), .clk(CLK), .clr(RST));
  Register #(.width(32), .trigger("rising"), .Select("low")) mEPC3 (
    .D(LocalPC), .en(and_12_out), .Q(mEPC3_q), .clk(CLK), .clr(RST));
  and and_17 (and_17_out, ~ClearB, 1'b1);  // AND_Gate
  Register #(.width(1), .trigger("rising"), .Select("low")) EPC2 (
    .D(and_17_out), .en(and_14_out), .Q(EPC2_q), .clk(CLK), .clr(RST));
  and and_18 (and_18_out, ~ClearC, 1'b1);  // AND_Gate
  Multiplexer #(.select(2), .width(32), .disabled("Z"), .enable("false")) multiplexer_16 (
    .in1(mEPC1_q), .in2(mEPC2_q), .in3(mEPC3_q), .out(RETPC), .sel(\当前中断号 ));  // open: in0
  Register #(.width(1), .trigger("rising"), .Select("low")) EPC3 (
    .D(and_18_out), .en(and_15_out), .Q(EPC3_q), .clk(CLK), .clr(RST));
  Priority_Encoder #(.select(2), .disabled("Z")) priority_encoder_1 (
    .in0(1'b1), .in1(EPC1_q), .in2(EPC2_q), .in3(EPC3_q), .out(\当前中断号 ));  // open: gs, en_out, en_in
  or or_10 (W1, register_5_q, register_2_q);
  or or_11 (W2, register_6_q, register_3_q);
  or or_12 (W3, register_7_q, register_4_q);
  or or_13 (or_13_out, register_5_q, RST);
  or or_14 (or_14_out, register_6_q, RST);
  or or_15 (or_15_out, register_7_q, RST);
  Register #(.width(1), .trigger("rising"), .Select("low")) register_2 (
    .D(1'b1), .Q(register_2_q), .clk(IR1_t), .clr(or_13_out));  // open: en
  Register #(.width(1), .trigger("rising"), .Select("low")) register_3 (
    .D(1'b1), .Q(register_3_q), .clk(IR2_t), .clr(or_14_out));  // open: en
  Register #(.width(1), .trigger("rising"), .Select("low")) register_4 (
    .D(1'b1), .Q(register_4_q), .clk(IR3_t), .clr(or_15_out));  // open: en
  or or_16 (or_16_out, register_2_q, register_5_q);
  or or_17 (or_17_out, register_3_q, register_6_q);
  or or_18 (or_18_out, register_4_q, register_7_q);
  and and_19 (and_19_out, or_16_out, ~ClearA);  // AND_Gate
  and and_20 (and_20_out, or_17_out, ~ClearB);  // AND_Gate
  and and_21 (and_21_out, or_18_out, ~ClearC);  // AND_Gate
  Register #(.width(1), .trigger("rising"), .Select("low")) register_5 (
    .D(and_19_out), .Q(register_5_q), .clk(CLK), .clr(RST));  // open: en
  Register #(.width(1), .trigger("rising"), .Select("low")) register_6 (
    .D(and_20_out), .Q(register_6_q), .clk(CLK), .clr(RST));  // open: en
  Register #(.width(1), .trigger("rising"), .Select("low")) register_7 (
    .D(and_21_out), .Q(register_7_q), .clk(CLK), .clr(RST));  // open: en
  Priority_Encoder #(.select(2), .disabled("Z")) priority_encoder_2 (
    .in0(1'b1), .in1(register_5_q), .in2(register_6_q), .in3(register_7_q), .out(\中断号 ));  // open: gs, en_out, en_in
  or or_19 (\中断信号 , register_5_q, register_6_q, register_7_q);
  Comparator #(.width(2), .mode("unsigned")) comparator_8 (
    .a(\中断号 ), .b(\当前中断号 ), .gt(comparator_8_gt));  // open: eq, lt
  Counter #(.width(1), .max('h1), .ongoal("stay"), .trigger("rising"), .behavior("new")) counter_3 (
    .Q(counter_3_q), .clk(or_20_out), .clr(or_21_out));  // open: load, D, count, carry, preset, down
  or or_20 (or_20_out, CSRRCI, \优先中断 );
  or or_21 (or_21_out, CSRRSI, URET);
  and and_22 (INT, IE, \优先中断 );
  Multiplexer #(.select(2), .width(32), .disabled("Z"), .enable("false")) multiplexer_17 (
    .in1(32'h30ac), .in2(32'h3158), .in3(32'h3204), .out(INTPC), .sel(\中断号 ));  // open: in0
  and and_23 (\优先中断 , \中断信号 , comparator_8_gt);
  not not_5 (not_5_out, counter_3_q);
  Register #(.width(1), .trigger("rising"), .Select("low")) register_8 (
    .D(not_5_out), .Q(IE), .clk(CLK));  // open: en, clr

  // Other names for the same wires on the sheet: I_imm[11:0] = IR[31:20]

  // Notes on the sheet:
  //   中断源
  //   中断等待指示
  //   总复位信号应将除ROM以外所有存储组件全部清零
  //   多级中断测试信号模拟器
  //   数码管输出
  //   数码管输出应该用寄存器锁存，否则显示数据只能一闪而过
  //   数码管输出应该用寄存器锁存，否则显示数据只能一闪而过
  //   中断信号采样参考电路
  //   指令探针
  //   指令存储器
  //   contents of rom_1 (hex, n*v repeats v):
  //   7d000113 100413 1f41993 41f9d993 433 c00913 800b13 140413 f47413 800293 100313 499993 89e9b3 1300533
  //   2200893 73 406282b3 fe0294e3 140413 f00f93 1f47433 1c41413 800293 100313 49d993 89e9b3 1300533
  //   2200893 73 406282b3 fe0294e3 1c45413 406b0b33 b0463 f95ff06f 2b3 fff2c293 1029293 fff2e293 500533
  //   2200893 73 f5dff06f 1112023 410113 a12023 410113 812023 410113 1312023 410113 1412023 410113 1512023
  //   410113 1612023 410113 40e073 100b13 300a13 100a93 1600433 441413 14469b3 1300533 2200893 73 fe0416e3
  //   415a0a33 fe0a10e3 40f073 ffc10113 12b03 ffc10113 12a83 ffc10113 12a03 ffc10113 12983 ffc10113 12403
  //   ffc10113 12503 ffc10113 12883 200073 1112023 410113 a12023 410113 812023 410113 1312023 410113
  //   1412023 410113 1512023 410113 1612023 410113 40e073 200b13 300a13 100a93 1600433 441413 14469b3
  //   1300533 2200893 73 fe0416e3 415a0a33 fe0a10e3 40f073 ffc10113 12b03 ffc10113 12a83 ffc10113 12a03
  //   ffc10113 12983 ffc10113 12403 ffc10113 12503 ffc10113 12883 200073 1112023 410113 a12023 410113
  //   812023 410113 1312023 410113 1412023 410113 1512023 410113 1612023 410113 40e073 300b13 300a13
  //   100a93 1600433 441413 14469b3 1300533 2200893 73 fe0416e3 415a0a33 fe0a10e3 40f073 ffc10113 12b03
  //   ffc10113 12a83 ffc10113 12a03 ffc10113 12983 ffc10113 12403 ffc10113 12503 ffc10113 12883 200073
  //   指令字
  //   JAL
  //   JALR
  //   URET
  //   Beq
  //   Bne
  //   MemToReg
  //   MemWrite
  //   AluOP
  //   AluSrcB
  //   RegWrite
  //   为方便自动评测，需要输出PC，IR，寄存器堆写如数据RDin
  //   RAM写使能MemWrite、RAM写入数据MDin等信号
  //   控制位
  //   暂停节拍，不能为0
  //   戳工具置1进入计数暂停模式，ctrl+k时钟自动运行到对应节拍暂停
  //   ctrl+k关闭时钟连续运行，将控制位置零，进入单步调试模式调试
  //   数据存储器
  //   可计数暂停的时钟源
  //   用这个时钟源需要去掉电路中的其他时钟源
  //   保护现场，保存返回地址
  //   当前中断号
  //   高优先级中断判断
  //   中断使能寄存器IE
endmodule

module \封装正确性测试  (
);

  wire IR1, IR2, IR3, MemW, RegW;
  wire [31:0] EX_PC, ID_PC, IF_PC, IR, LED, MDin, MDinr, MEM_PC, PC, RDin, RDinr, WB_PC;

  \单周期RISC_V  \u_单周期risc_v_1  (
    .IR1(IR1), .IR2(IR2), .IR3(IR3), .RegWrite(RegW), .MemWrite(MemW), .PC(PC), .IR(IR), .RDin(RDin),
    .MDin(MDin), .LedData(LED));
  \气泡流水线  \u_气泡流水线_1  (
    .RegWrite(RegW), .MemWrite(MemW), .IF_PC(IF_PC), .ID_PC(ID_PC), .EX_PC(EX_PC), .M_PC(MEM_PC),
    .WB_PC(WB_PC), .RDin(RDinr), .MDin(MDinr), .LedData(LED));
  \单周期_单级中断  \u_单周期_单级中断_1  (
    .IR1(IR1), .IR2(IR2), .IR3(IR3), .RegWrite(RegW), .MemWrite(MemW), .PC(PC), .IR(IR), .RDin(RDin),
    .MDin(MDin), .LedData(LED));
  \理想流水线  \u_理想流水线_1  (
    .RegWrite(RegW), .MemWrite(MemW), .IF_PC(IF_PC), .ID_PC(ID_PC), .EX_PC(EX_PC), .M_PC(MEM_PC),
    .WB_PC(WB_PC), .RDin(RDinr), .MDin(MDinr), .LedData(LED));
  \重定向流水线  \u_重定向流水线_1  (
    .RegWrite(RegW), .MemWrite(MemW), .IF_PC(IF_PC), .ID_PC(ID_PC), .EX_PC(EX_PC), .M_PC(MEM_PC),
    .WB_PC(WB_PC), .RDin(RDinr), .MDin(MDinr), .LedData(LED));
  \单周期_多级中断  \u_单周期_多级中断_1  (
    .IR1(IR1), .IR2(IR2), .IR3(IR3), .RegWrite(RegW), .MemWrite(MemW), .PC(PC), .IR(IR), .RDin(RDin),
    .MDin(MDin), .LedData(LED));

  // Notes on the sheet:
  //   单周期封装测试
  //   气泡流水封装测试
  //   单周期+单级中断封装测试
  //   请检查上面封装有无位宽不匹配，引脚标签是否和连接的标签相对应，否则无法在educoder平台上正确测试
  //   理想流水封装测试
  //   重定向流水封装测试
  //   单周期+多级中断封装测试
endmodule
module IF (
  input  RST,
  input  CLK,
  input  flush,
  input  [31:0] IR,
  input  [31:0] PC,
  input  [31:0] PC_4,
  input  en,
  output [31:0] IR_2,
  output [31:0] PC_2,
  output [31:0] PC_4_2
);

  wire not_1_out, or_1_out;
  wire [31:0] multiplexer_1_out, multiplexer_2_out, multiplexer_3_out;

  or or_1 (or_1_out, RST, flush);
  Multiplexer #(.select(1), .width(32), .disabled("Z"), .enable("false")) multiplexer_1 (
    .in0(IR), .in1({32{1'b0}}), .out(multiplexer_1_out), .sel(or_1_out));
  Multiplexer #(.select(1), .width(32), .disabled("Z"), .enable("false")) multiplexer_2 (
    .in0(PC), .in1({32{1'b0}}), .out(multiplexer_2_out), .sel(or_1_out));
  Multiplexer #(.select(1), .width(32), .disabled("Z"), .enable("false")) multiplexer_3 (
    .in0(PC_4), .in1({32{1'b0}}), .out(multiplexer_3_out), .sel(or_1_out));
  Register #(.width(32), .trigger("rising"), .Select("low")) register_1 (
    .D(multiplexer_1_out), .en(not_1_out), .Q(IR_2), .clk(CLK));  // open: clr
  Register #(.width(32), .trigger("rising"), .Select("low")) register_2 (
    .D(multiplexer_2_out), .en(not_1_out), .Q(PC_2), .clk(CLK));  // open: clr
  Register #(.width(32), .trigger("rising"), .Select("low")) register_3 (
    .D(multiplexer_3_out), .en(not_1_out), .Q(PC_4_2), .clk(CLK));  // open: clr
  not not_1 (not_1_out, en);
endmodule

module ID (
  input  RST,
  input  halt,
  input  flush,
  input  beq,
  input  bne,
  input  MemToReg,
  input  MemWrite,
  input  [3:0] ALU_OP,
  input  ALU_SRCB,
  input  RegWrite,
  input  S_type,
  input  JAL,
  input  JALR,
  input  URET,
  input  ecall,
  input  [31:0] ID_PC,
  input  [31:0] r1,
  input  [31:0] r2,
  input  [31:0] Im,
  input  [31:0] Bm,
  input  [31:0] Jm,
  input  [31:0] PC_4,
  input  [31:0] ID_IR,
  input  [4:0] WRD,
  input  bltu,
  input  auipc,
  input  sb,
  input  [31:0] u,
  input  [1:0] RsFoward,
  input  [1:0] RtFoward,
  input  CLK,
  output beq_2,
  output bne_2,
  output MemToReg_2,
  output MemWrite_2,
  output [3:0] ALU_OP_2,
  output ALU_SRCB_2,
  output RegWrite_2,
  output S_type_2,
  output JAL_2,
  output JALR_2,
  output URET_2,
  output ecall_2,
  output [31:0] ID_PC_2,
  output [31:0] r1_2,
  output [31:0] r2_2,
  output [31:0] Im_2,
  output [31:0] Bm_2,
  output [31:0] Jm_2,
  output [31:0] PC_4_2,
  output [31:0] ID_IR_2,
  output [4:0] WRD_2,
  output bltu_2,
  output auipc_2,
  output sb_2,
  output [31:0] u_2,
  output [1:0] RsFoward_2,
  output [1:0] Rtfoward_2
);

  wire multiplexer_1_out, multiplexer_2_out, multiplexer_3_out, multiplexer_4_out, multiplexer_6_out,
       multiplexer_7_out, multiplexer_8_out, multiplexer_9_out, multiplexer_10_out, multiplexer_11_out,
       multiplexer_12_out, multiplexer_16_out, multiplexer_17_out, multiplexer_18_out, not_1_out, or_1_out,
       undriven;
  wire [1:0] multiplexer_20_out, multiplexer_21_out;
  wire [3:0] multiplexer_5_out;
  wire [4:0] multiplexer_27_out;
  wire [31:0] multiplexer_13_out, multiplexer_14_out, multiplexer_15_out, multiplexer_19_out,
       multiplexer_22_out, multiplexer_23_out, multiplexer_24_out, multiplexer_25_out, multiplexer_26_out;

  or or_1 (or_1_out, RST, flush);
  Multiplexer #(.select(1), .width(1), .disabled("Z"), .enable("false")) multiplexer_1 (
    .in0(beq), .in1(1'b0), .out(multiplexer_1_out), .sel(or_1_out));
  Multiplexer #(.select(1), .width(1), .disabled("Z"), .enable("false")) multiplexer_2 (
    .in0(bne), .in1(1'b0), .out(multiplexer_2_out), .sel(or_1_out));
  Multiplexer #(.select(1), .width(1), .disabled("Z"), .enable("false")) multiplexer_3 (
    .in0(MemToReg), .in1(1'b0), .out(multiplexer_3_out), .sel(or_1_out));
  Multiplexer #(.select(1), .width(1), .disabled("Z"), .enable("false")) multiplexer_4 (
    .in0(MemWrite), .in1(1'b0), .out(multiplexer_4_out), .sel(or_1_out));
  Multiplexer #(.select(1), .width(4), .disabled("Z"), .enable("false")) multiplexer_5 (
    .in0(ALU_OP), .in1(4'b0000), .out(multiplexer_5_out), .sel(or_1_out));
  Multiplexer #(.select(1), .width(1), .disabled("Z"), .enable("false")) multiplexer_6 (
    .in0(ALU_SRCB), .in1(1'b0), .out(multiplexer_6_out), .sel(or_1_out));
  Multiplexer #(.select(1), .width(1), .disabled("Z"), .enable("false")) multiplexer_7 (
    .in0(RegWrite), .in1(1'b0), .out(multiplexer_7_out), .sel(or_1_out));
  Multiplexer #(.select(1), .width(1), .disabled("Z"), .enable("false")) multiplexer_8 (
    .in0(S_type), .in1(1'b0), .out(multiplexer_8_out), .sel(or_1_out));
  Multiplexer #(.select(1), .width(1), .disabled("Z"), .enable("false")) multiplexer_9 (
    .in0(JAL), .in1(1'b0), .out(multiplexer_9_out), .sel(or_1_out));
  Multiplexer #(.select(1), .width(1), .disabled("Z"), .enable("false")) multiplexer_10 (
    .in0(JALR), .in1(1'b0), .out(multiplexer_10_out), .sel(or_1_out));
  Multiplexer #(.select(1), .width(1), .disabled("Z"), .enable("false")) multiplexer_11 (
    .in0(URET), .in1(1'b0), .out(multiplexer_11_out), .sel(or_1_out));
  Multiplexer #(.select(1), .width(1), .disabled("Z"), .enable("false")) multiplexer_12 (
    .in0(ecall), .in1(1'b0), .out(multiplexer_12_out), .sel(or_1_out));
  Multiplexer #(.select(1), .width(32), .disabled("Z"), .enable("false")) multiplexer_13 (
    .in0(ID_PC), .in1({32{1'b0}}), .out(multiplexer_13_out), .sel(or_1_out));
  Multiplexer #(.select(1), .width(32), .disabled("Z"), .enable("false")) multiplexer_14 (
    .in0(r1), .in1({32{1'b0}}), .out(multiplexer_14_out), .sel(or_1_out));
  Multiplexer #(.select(1), .width(32), .disabled("Z"), .enable("false")) multiplexer_15 (
    .in0(r2), .in1({32{1'b0}}), .out(multiplexer_15_out), .sel(or_1_out));
  Multiplexer #(.select(1), .width(1), .disabled("Z"), .enable("false")) multiplexer_16 (
    .in0(bltu), .in1(1'b0), .out(multiplexer_16_out), .sel(or_1_out));
  Multiplexer #(.select(1), .width(1), .disabled("Z"), .enable("false")) multiplexer_17 (
    .in0(auipc), .in1(1'b0), .out(multiplexer_17_out), .sel(or_1_out));
  Multiplexer #(.select(1), .width(1), .disabled("Z"), .enable("false")) multiplexer_18 (
    .in0(sb), .in1(1'b0), .out(multiplexer_18_out), .sel(or_1_out));
  Multiplexer #(.select(1), .width(32), .disabled("Z"), .enable("false")) multiplexer_19 (
    .in0(u), .in1({32{1'b0}}), .out(multiplexer_19_out), .sel(or_1_out));
  Multiplexer #(.select(1), .width(2), .disabled("Z"), .enable("false")) multiplexer_20 (
    .in0(RsFoward), .in1(2'b00), .out(multiplexer_20_out), .sel(or_1_out));
  Multiplexer #(.select(1), .width(2), .disabled("Z"), .enable("false")) multiplexer_21 (
    .in0(RtFoward), .in1(2'b00), .out(multiplexer_21_out), .sel(or_1_out));
  Multiplexer #(.select(1), .width(32), .disabled("Z"), .enable("false")) multiplexer_22 (
    .in0(Im), .in1({32{1'b0}}), .out(multiplexer_22_out), .sel(or_1_out));
  Multiplexer #(.select(1), .width(32), .disabled("Z"), .enable("false")) multiplexer_23 (
    .in0(Bm), .in1({32{1'b0}}), .out(multiplexer_23_out), .sel(or_1_out));
  Multiplexer #(.select(1), .width(32), .disabled("Z"), .enable("false")) multiplexer_24 (
    .in0(Jm), .in1({32{1'b0}}), .out(multiplexer_24_out), .sel(or_1_out));
  Multiplexer #(.select(1), .width(32), .disabled("Z"), .enable("false")) multiplexer_25 (
    .in0(PC_4), .in1({32{1'b0}}), .out(multiplexer_25_out), .sel(or_1_out));
  Multiplexer #(.select(1), .width(32), .disabled("Z"), .enable("false")) multiplexer_26 (
    .in0(ID_IR), .in1({32{1'b0}}), .out(multiplexer_26_out), .sel(or_1_out));
  Multiplexer #(.select(1), .width(5), .disabled("Z"), .enable("false")) multiplexer_27 (
    .in0(WRD), .in1({5{1'b0}}), .out(multiplexer_27_out), .sel(or_1_out));
  not not_1 (not_1_out, halt);
  Register #(.width(1), .trigger("rising"), .Select("low")) register_1 (
    .D(multiplexer_1_out), .en(not_1_out), .Q(beq_2), .clk(CLK));  // open: clr
  Register #(.width(1), .trigger("rising"), .Select("low")) register_2 (
    .D(multiplexer_2_out), .en(not_1_out), .Q(bne_2), .clk(CLK));  // open: clr
  Register #(.width(1), .trigger("rising"), .Select("low")) register_3 (
    .D(multiplexer_3_out), .en(not_1_out), .Q(MemToReg_2), .clk(CLK));  // open: clr
  Register #(.width(1), .trigger("rising"), .Select("low")) register_4 (
    .D(multiplexer_4_out), .en(not_1_out), .Q(MemWrite_2), .clk(CLK), .clr(undriven));
  Register #(.width(4), .trigger("rising"), .Select("low")) register_5 (
    .D(multiplexer_5_out), .en(not_1_out), .Q(ALU_OP_2), .clk(CLK));  // open: clr
  Register #(.width(1), .trigger("rising"), .Select("low")) register_6 (
    .D(multiplexer_6_out), .en(not_1_out), .Q(ALU_SRCB_2), .clk(CLK));  // open: clr
  Register #(.width(1), .trigger("rising"), .Select("low")) register_7 (
    .D(multiplexer_7_out), .en(not_1_out), .Q(RegWrite_2), .clk(CLK));  // open: clr
  Register #(.width(1), .trigger("rising"), .Select("low")) register_8 (
    .D(multiplexer_8_out), .en(not_1_out), .Q(S_type_2), .clk(CLK));  // open: clr
  Register #(.width(1), .trigger("rising"), .Select("low")) register_9 (
    .D(multiplexer_9_out), .en(not_1_out), .Q(JAL_2), .clk(CLK));  // open: clr
  Register #(.width(1), .trigger("rising"), .Select("low")) register_10 (
    .D(multiplexer_10_out), .en(not_1_out), .Q(JALR_2), .clk(CLK));  // open: clr
  Register #(.width(1), .trigger("rising"), .Select("low")) register_11 (
    .D(multiplexer_11_out), .en(not_1_out), .Q(URET_2), .clk(CLK));  // open: clr
  Register #(.width(1), .trigger("rising"), .Select("low")) register_12 (
    .D(multiplexer_12_out), .en(not_1_out), .Q(ecall_2), .clk(CLK));  // open: clr
  Register #(.width(32), .trigger("rising"), .Select("low")) register_13 (
    .D(multiplexer_13_out), .en(not_1_out), .Q(ID_PC_2), .clk(CLK));  // open: clr
  Register #(.width(32), .trigger("rising"), .Select("low")) register_14 (
    .D(multiplexer_14_out), .en(not_1_out), .Q(r1_2), .clk(CLK));  // open: clr
  Register #(.width(32), .trigger("rising"), .Select("low")) register_15 (
    .D(multiplexer_15_out), .en(not_1_out), .Q(r2_2), .clk(CLK));  // open: clr
  Register #(.width(32), .trigger("rising"), .Select("low")) register_16 (
    .D(multiplexer_22_out), .en(not_1_out), .Q(Im_2), .clk(CLK));  // open: clr
  Register #(.width(32), .trigger("rising"), .Select("low")) register_17 (
    .D(multiplexer_23_out), .en(not_1_out), .Q(Bm_2), .clk(CLK));  // open: clr
  Register #(.width(32), .trigger("rising"), .Select("low")) register_18 (
    .D(multiplexer_24_out), .en(not_1_out), .Q(Jm_2), .clk(CLK));  // open: clr
  Register #(.width(32), .trigger("rising"), .Select("low")) register_19 (
    .D(multiplexer_25_out), .en(not_1_out), .Q(PC_4_2), .clk(CLK));  // open: clr
  Register #(.width(32), .trigger("rising"), .Select("low")) register_20 (
    .D(multiplexer_26_out), .en(not_1_out), .Q(ID_IR_2), .clk(CLK));  // open: clr
  Register #(.width(5), .trigger("rising"), .Select("low")) register_21 (
    .D(multiplexer_27_out), .en(not_1_out), .Q(WRD_2), .clk(CLK));  // open: clr
  Register #(.width(1), .trigger("rising"), .Select("low")) register_22 (
    .D(multiplexer_16_out), .en(not_1_out), .Q(bltu_2), .clk(CLK));  // open: clr
  Register #(.width(1), .trigger("rising"), .Select("low")) register_23 (
    .D(multiplexer_17_out), .en(not_1_out), .Q(auipc_2), .clk(CLK));  // open: clr
  Register #(.width(1), .trigger("rising"), .Select("low")) register_24 (
    .D(multiplexer_18_out), .en(not_1_out), .Q(sb_2), .clk(CLK));  // open: clr
  Register #(.width(32), .trigger("rising"), .Select("low")) register_25 (
    .D(multiplexer_19_out), .en(not_1_out), .Q(u_2), .clk(CLK));  // open: clr
  Register #(.width(2), .trigger("rising"), .Select("low")) register_26 (
    .D(multiplexer_20_out), .en(not_1_out), .Q(RsFoward_2), .clk(CLK));  // open: clr
  Register #(.width(2), .trigger("rising"), .Select("low")) register_27 (
    .D(multiplexer_21_out), .en(not_1_out), .Q(Rtfoward_2), .clk(CLK));  // open: clr
  Pull_Resistor #(.pull(0)) pull_resistor_1 (.node(not_1_out));
endmodule

module EX (
  input  sb,
  input  auipc,
  input  RST,
  input  flush,
  input  JAL,
  input  JALR,
  input  URET,
  input  MemToReg,
  input  MenWrite,
  input  ecall,
  input  RegWirte,
  input  [4:0] Write,
  input  [31:0] ALU_Result,
  input  [31:0] EX_PC,
  input  [31:0] EX_IR,
  input  [31:0] PC_4,
  input  [31:0] R1,
  input  [31:0] R2,
  input  halt,
  input  CLK,
  input  [31:0] U,
  output sb_2,
  output auipc_2,
  output JAL_2,
  output JALR_2,
  output URET_2,
  output MemToReg_2,
  output MemWrite,
  output ecall_2,
  output RegWirte_2,
  output [4:0] Write_2,
  output [31:0] ALU_Result_2,
  output [31:0] MEN_PC,
  output [31:0] MEN_IR,
  output [31:0] PC_4_2,
  output [31:0] R1_2,
  output [31:0] R2_2,
  output [31:0] U_2
);

  wire multiplexer_1_out, multiplexer_2_out, multiplexer_3_out, multiplexer_4_out, multiplexer_5_out,
       multiplexer_6_out, multiplexer_7_out, multiplexer_8_out, multiplexer_9_out, not_1_out, or_1_out;
  wire [4:0] multiplexer_10_out;
  wire [31:0] multiplexer_11_out, multiplexer_12_out, multiplexer_13_out, multiplexer_14_out,
       multiplexer_15_out, multiplexer_16_out, multiplexer_17_out;

  or or_1 (or_1_out, RST, flush);
  Multiplexer #(.select(1), .width(1), .disabled("Z"), .enable("false")) multiplexer_1 (
    .in0(sb), .in1(1'b0), .out(multiplexer_1_out), .sel(or_1_out));
  Multiplexer #(.select(1), .width(1), .disabled("Z"), .enable("false")) multiplexer_2 (
    .in0(auipc), .in1(1'b0), .out(multiplexer_2_out), .sel(or_1_out));
  Multiplexer #(.select(1), .width(1), .disabled("Z"), .enable("false")) multiplexer_3 (
    .in0(JAL), .in1(1'b0), .out(multiplexer_3_out), .sel(or_1_out));
  Multiplexer #(.select(1), .width(1), .disabled("Z"), .enable("false")) multiplexer_4 (
    .in0(JALR), .in1(1'b0), .out(multiplexer_4_out), .sel(or_1_out));
  Multiplexer #(.select(1), .width(1), .disabled("Z"), .enable("false")) multiplexer_5 (
    .in0(URET), .in1(1'b0), .out(multiplexer_5_out), .sel(or_1_out));
  Multiplexer #(.select(1), .width(1), .disabled("Z"), .enable("false")) multiplexer_6 (
    .in0(MemToReg), .in1(1'b0), .out(multiplexer_6_out), .sel(or_1_out));
  Multiplexer #(.select(1), .width(1), .disabled("Z"), .enable("false")) multiplexer_7 (
    .in0(MenWrite), .in1(1'b0), .out(multiplexer_7_out), .sel(or_1_out));
  Multiplexer #(.select(1), .width(1), .disabled("Z"), .enable("false")) multiplexer_8 (
    .in0(ecall), .in1(1'b0), .out(multiplexer_8_out), .sel(or_1_out));
  Multiplexer #(.select(1), .width(1), .disabled("Z"), .enable("false")) multiplexer_9 (
    .in0(RegWirte), .in1(1'b0), .out(multiplexer_9_out), .sel(or_1_out));
  Multiplexer #(.select(1), .width(5), .disabled("Z"), .enable("false")) multiplexer_10 (
    .in0(Write), .in1({5{1'b0}}), .out(multiplexer_10_out), .sel(or_1_out));
  Multiplexer #(.select(1), .width(32), .disabled("Z"), .enable("false")) multiplexer_11 (
    .in0(ALU_Result), .in1({32{1'b0}}), .out(multiplexer_11_out), .sel(or_1_out));
  Multiplexer #(.select(1), .width(32), .disabled("Z"), .enable("false")) multiplexer_12 (
    .in0(EX_PC), .in1({32{1'b0}}), .out(multiplexer_12_out), .sel(or_1_out));
  Multiplexer #(.select(1), .width(32), .disabled("Z"), .enable("false")) multiplexer_13 (
    .in0(EX_IR), .in1({32{1'b0}}), .out(multiplexer_13_out), .sel(or_1_out));
  Multiplexer #(.select(1), .width(32), .disabled("Z"), .enable("false")) multiplexer_14 (
    .in0(PC_4), .in1({32{1'b0}}), .out(multiplexer_14_out), .sel(or_1_out));
  Multiplexer #(.select(1), .width(32), .disabled("Z"), .enable("false")) multiplexer_15 (
    .in0(R1), .in1({32{1'b0}}), .out(multiplexer_15_out), .sel(or_1_out));
  Multiplexer #(.select(1), .width(32), .disabled("Z"), .enable("false")) multiplexer_16 (
    .in0(R2), .in1({32{1'b0}}), .out(multiplexer_16_out), .sel(or_1_out));
  not not_1 (not_1_out, halt);
  Multiplexer #(.select(1), .width(32), .disabled("Z"), .enable("false")) multiplexer_17 (
    .in0(U), .in1({32{1'b0}}), .out(multiplexer_17_out), .sel(or_1_out));
  Register #(.width(1), .trigger("rising"), .Select("low")) register_1 (
    .D(multiplexer_1_out), .en(not_1_out), .Q(sb_2), .clk(CLK));  // open: clr
  Register #(.width(1), .trigger("rising"), .Select("low")) register_2 (
    .D(multiplexer_2_out), .en(not_1_out), .Q(auipc_2), .clk(CLK));  // open: clr
  Register #(.width(1), .trigger("rising"), .Select("low")) register_3 (
    .D(multiplexer_3_out), .en(not_1_out), .Q(JAL_2), .clk(CLK));  // open: clr
  Register #(.width(1), .trigger("rising"), .Select("low")) register_4 (
    .D(multiplexer_4_out), .en(not_1_out), .Q(JALR_2), .clk(CLK));  // open: clr
  Register #(.width(1), .trigger("rising"), .Select("low")) register_5 (
    .D(multiplexer_5_out), .en(not_1_out), .Q(URET_2), .clk(CLK));  // open: clr
  Register #(.width(1), .trigger("rising"), .Select("low")) register_6 (
    .D(multiplexer_6_out), .en(not_1_out), .Q(MemToReg_2), .clk(CLK));  // open: clr
  Register #(.width(1), .trigger("rising"), .Select("low")) register_7 (
    .D(multiplexer_7_out), .en(not_1_out), .Q(MemWrite), .clk(CLK));  // open: clr
  Register #(.width(1), .trigger("rising"), .Select("low")) register_8 (
    .D(multiplexer_8_out), .en(not_1_out), .Q(ecall_2), .clk(CLK));  // open: clr
  Register #(.width(1), .trigger("rising"), .Select("low")) register_9 (
    .D(multiplexer_9_out), .en(not_1_out), .Q(RegWirte_2), .clk(CLK));  // open: clr
  Register #(.width(5), .trigger("rising"), .Select("low")) register_10 (
    .D(multiplexer_10_out), .en(not_1_out), .Q(Write_2), .clk(CLK));  // open: clr
  Register #(.width(32), .trigger("rising"), .Select("low")) register_11 (
    .D(multiplexer_11_out), .en(not_1_out), .Q(ALU_Result_2), .clk(CLK));  // open: clr
  Register #(.width(32), .trigger("rising"), .Select("low")) register_12 (
    .D(multiplexer_12_out), .en(not_1_out), .Q(MEN_PC), .clk(CLK));  // open: clr
  Register #(.width(32), .trigger("rising"), .Select("low")) register_13 (
    .D(multiplexer_13_out), .en(not_1_out), .Q(MEN_IR), .clk(CLK));  // open: clr
  Register #(.width(32), .trigger("rising"), .Select("low")) register_14 (
    .D(multiplexer_14_out), .en(not_1_out), .Q(PC_4_2), .clk(CLK));  // open: clr
  Register #(.width(32), .trigger("rising"), .Select("low")) register_15 (
    .D(multiplexer_15_out), .en(not_1_out), .Q(R1_2), .clk(CLK));  // open: clr
  Register #(.width(32), .trigger("rising"), .Select("low")) register_16 (
    .D(multiplexer_16_out), .en(not_1_out), .Q(R2_2), .clk(CLK));  // open: clr
  Register #(.width(32), .trigger("rising"), .Select("low")) register_17 (
    .D(multiplexer_17_out), .en(not_1_out), .Q(U_2), .clk(CLK));  // open: clr
  Pull_Resistor #(.pull(0)) pull_resistor_1 (.node(not_1_out));
endmodule

module Mem (
  input  auipc,
  input  sb,
  input  RST,
  input  flush,
  input  JAL,
  input  JALR,
  input  URET,
  input  MemToReg,
  input  MenWrite,
  input  ecall,
  input  RegWirte,
  input  [4:0] Write,
  input  [31:0] ALU_Result,
  input  [31:0] Mem_PC,
  input  [31:0] Mem_IR,
  input  [31:0] PC_4,
  input  [31:0] R1,
  input  [31:0] R2,
  input  [31:0] MData,
  input  CLK,
  input  halt,
  input  [31:0] u,
  output auipc_2,
  output sb_2,
  output JAL_2,
  output JALR_2,
  output URET_2,
  output MemToReg_2,
  output MemWrite,
  output ecall_2,
  output RegWirte_2,
  output [4:0] Write_2,
  output [31:0] ALU_Result_2,
  output [31:0] Mem_PC_2,
  output [31:0] Mem_IR_2,
  output [31:0] PC_4_2,
  output [31:0] R1_2,
  output [31:0] R2_2,
  output [31:0] Mdata_2,
  output [31:0] u_2
);

  wire multiplexer_1_out, multiplexer_2_out, multiplexer_3_out, multiplexer_4_out, multiplexer_5_out,
       multiplexer_6_out, multiplexer_7_out, multiplexer_17_out, multiplexer_18_out, not_1_out, or_1_out;
  wire [4:0] multiplexer_8_out;
  wire [31:0] multiplexer_9_out, multiplexer_10_out, multiplexer_11_out, multiplexer_12_out,
       multiplexer_13_out, multiplexer_14_out, multiplexer_15_out, multiplexer_16_out;

  or or_1 (or_1_out, RST, flush);
  not not_1 (not_1_out, halt);
  Multiplexer #(.select(1), .width(1), .disabled("Z"), .enable("false")) multiplexer_1 (
    .in0(JAL), .in1(1'b0), .out(multiplexer_1_out), .sel(or_1_out));
  Multiplexer #(.select(1), .width(1), .disabled("Z"), .enable("false")) multiplexer_2 (
    .in0(JALR), .in1(1'b0), .out(multiplexer_2_out), .sel(or_1_out));
  Multiplexer #(.select(1), .width(1), .disabled("Z"), .enable("false")) multiplexer_3 (
    .in0(URET), .in1(1'b0), .out(multiplexer_3_out), .sel(or_1_out));
  Multiplexer #(.select(1), .width(1), .disabled("Z"), .enable("false")) multiplexer_4 (
    .in0(MemToReg), .in1(1'b0), .out(multiplexer_4_out), .sel(or_1_out));
  Multiplexer #(.select(1), .width(1), .disabled("Z"), .enable("false")) multiplexer_5 (
    .in0(MenWrite), .in1(1'b0), .out(multiplexer_5_out), .sel(or_1_out));
  Multiplexer #(.select(1), .width(1), .disabled("Z"), .enable("false")) multiplexer_6 (
    .in0(ecall), .in1(1'b0), .out(multiplexer_6_out), .sel(or_1_out));
  Multiplexer #(.select(1), .width(1), .disabled("Z"), .enable("false")) multiplexer_7 (
    .in0(RegWirte), .in1(1'b0), .out(multiplexer_7_out), .sel(or_1_out));
  Multiplexer #(.select(1), .width(5), .disabled("Z"), .enable("false")) multiplexer_8 (
    .in0(Write), .in1({5{1'b0}}), .out(multiplexer_8_out), .sel(or_1_out));
  Multiplexer #(.select(1), .width(32), .disabled("Z"), .enable("false")) multiplexer_9 (
    .in0(ALU_Result), .in1({32{1'b0}}), .out(multiplexer_9_out), .sel(or_1_out));
  Multiplexer #(.select(1), .width(32), .disabled("Z"), .enable("false")) multiplexer_10 (
    .in0(Mem_PC), .in1({32{1'b0}}), .out(multiplexer_10_out), .sel(or_1_out));
  Multiplexer #(.select(1), .width(32), .disabled("Z"), .enable("false")) multiplexer_11 (
    .in0(Mem_IR), .in1({32{1'b0}}), .out(multiplexer_11_out), .sel(or_1_out));
  Multiplexer #(.select(1), .width(32), .disabled("Z"), .enable("false")) multiplexer_12 (
    .in0(PC_4), .in1({32{1'b0}}), .out(multiplexer_12_out), .sel(or_1_out));
  Multiplexer #(.select(1), .width(32), .disabled("Z"), .enable("false")) multiplexer_13 (
    .in0(R1), .in1({32{1'b0}}), .out(multiplexer_13_out), .sel(or_1_out));
  Multiplexer #(.select(1), .width(32), .disabled("Z"), .enable("false")) multiplexer_14 (
    .in0(R2), .in1({32{1'b0}}), .out(multiplexer_14_out), .sel(or_1_out));
  Multiplexer #(.select(1), .width(32), .disabled("Z"), .enable("false")) multiplexer_15 (
    .in0(MData), .in1({32{1'b0}}), .out(multiplexer_15_out), .sel(or_1_out));
  Multiplexer #(.select(1), .width(32), .disabled("Z"), .enable("false")) multiplexer_16 (
    .in0(u), .in1({32{1'b0}}), .out(multiplexer_16_out), .sel(or_1_out));
  Multiplexer #(.select(1), .width(1), .disabled("Z"), .enable("false")) multiplexer_17 (
    .in0(auipc), .in1(1'b0), .out(multiplexer_17_out), .sel(or_1_out));
  Multiplexer #(.select(1), .width(1), .disabled("Z"), .enable("false")) multiplexer_18 (
    .in0(sb), .in1(1'b0), .out(multiplexer_18_out), .sel(or_1_out));
  Register #(.width(1), .trigger("rising"), .Select("low")) register_1 (
    .D(multiplexer_17_out), .en(not_1_out), .Q(auipc_2), .clk(CLK));  // open: clr
  Register #(.width(1), .trigger("rising"), .Select("low")) register_2 (
    .D(multiplexer_18_out), .en(not_1_out), .Q(sb_2), .clk(CLK));  // open: clr
  Register #(.width(1), .trigger("rising"), .Select("low")) register_3 (
    .D(multiplexer_1_out), .en(not_1_out), .Q(JAL_2), .clk(CLK));  // open: clr
  Register #(.width(1), .trigger("rising"), .Select("low")) register_4 (
    .D(multiplexer_2_out), .en(not_1_out), .Q(JALR_2), .clk(CLK));  // open: clr
  Register #(.width(1), .trigger("rising"), .Select("low")) register_5 (
    .D(multiplexer_3_out), .en(not_1_out), .Q(URET_2), .clk(CLK));  // open: clr
  Register #(.width(1), .trigger("rising"), .Select("low")) register_6 (
    .D(multiplexer_4_out), .en(not_1_out), .Q(MemToReg_2), .clk(CLK));  // open: clr
  Register #(.width(1), .trigger("rising"), .Select("low")) register_7 (
    .D(multiplexer_5_out), .en(not_1_out), .Q(MemWrite), .clk(CLK));  // open: clr
  Register #(.width(1), .trigger("rising"), .Select("low")) register_8 (
    .D(multiplexer_6_out), .en(not_1_out), .Q(ecall_2), .clk(CLK));  // open: clr
  Register #(.width(1), .trigger("rising"), .Select("low")) register_9 (
    .D(multiplexer_7_out), .en(not_1_out), .Q(RegWirte_2), .clk(CLK));  // open: clr
  Register #(.width(5), .trigger("rising"), .Select("low")) register_10 (
    .D(multiplexer_8_out), .en(not_1_out), .Q(Write_2), .clk(CLK));  // open: clr
  Register #(.width(32), .trigger("rising"), .Select("low")) register_11 (
    .D(multiplexer_9_out), .en(not_1_out), .Q(ALU_Result_2), .clk(CLK));  // open: clr
  Register #(.width(32), .trigger("rising"), .Select("low")) register_12 (
    .D(multiplexer_10_out), .en(not_1_out), .Q(Mem_PC_2), .clk(CLK));  // open: clr
  Register #(.width(32), .trigger("rising"), .Select("low")) register_13 (
    .D(multiplexer_11_out), .en(not_1_out), .Q(Mem_IR_2), .clk(CLK));  // open: clr
  Register #(.width(32), .trigger("rising"), .Select("low")) register_14 (
    .D(multiplexer_12_out), .en(not_1_out), .Q(PC_4_2), .clk(CLK));  // open: clr
  Register #(.width(32), .trigger("rising"), .Select("low")) register_15 (
    .D(multiplexer_13_out), .en(not_1_out), .Q(R1_2), .clk(CLK));  // open: clr
  Register #(.width(32), .trigger("rising"), .Select("low")) register_16 (
    .D(multiplexer_14_out), .en(not_1_out), .Q(R2_2), .clk(CLK));  // open: clr
  Register #(.width(32), .trigger("rising"), .Select("low")) register_17 (
    .D(multiplexer_15_out), .en(not_1_out), .Q(Mdata_2), .clk(CLK));  // open: clr
  Register #(.width(32), .trigger("rising"), .Select("low")) register_18 (
    .D(multiplexer_16_out), .en(not_1_out), .Q(u_2), .clk(CLK));  // open: clr
  Pull_Resistor #(.pull(0)) pull_resistor_1 (.node(not_1_out));
endmodule

module sb (
  input  in_1,
  input  [31:0] R2,
  output [3:0] out_3,
  output [31:0] darta
);

  wire [3:0] multiplexer_1_out;

  Multiplexer #(.select(2), .width(4), .disabled("Z"), .enable("false")) multiplexer_1 (
    .in0(4'b0001), .in1(4'b0010), .in2(4'b0100), .in3(4'b1000), .out(multiplexer_1_out), .sel(R2[1:0]));
  Demultiplexer #(.select(2), .width(8), .tristate("false"), .disabled("Z"), .enable("false")) demultiplexer_1 (
    .out0(darta[7:0]), .out1(darta[15:8]), .out2(darta[23:16]), .out3(darta[31:24]), .in(R2[7:0]),
    .sel(R2[1:0]));
  Multiplexer #(.select(1), .width(4), .disabled("Z"), .enable("false")) multiplexer_2 (
    .in0(4'b1111), .in1(multiplexer_1_out), .out(out_3), .sel(in_1));
endmodule

module datahazzard (
  input  RtUsed,
  input  [4:0] Rt,
  input  [4:0] Rt_2,
  input  [4:0] MEN_WriteReg,
  input  MEN_Regwrite,
  input  RtUsed_2,
  input  [4:0] Rt_3,
  input  [4:0] Rt_4,
  input  [4:0] EX_WriteReg,
  input  EX_Regwrite,
  input  RsUsed,
  input  [4:0] Rs,
  input  [4:0] Rs_2,
  input  [4:0] EX_WriteReg_2,
  input  EX_Regwrite_2,
  input  RsUsed_2,
  input  [4:0] Rs_3,
  input  [4:0] Rs_4,
  input  [4:0] MEN_WriteReg_2,
  input  MEN_Regwrite_2,
  output datahazzed
);

  wire and_1_out, and_2_out, and_3_out, and_4_out, and_5_out, and_6_out, and_7_out, and_8_out, and_9_out,
       and_10_out, and_11_out, and_12_out, comparator_1_eq, comparator_2_eq, comparator_3_eq,
       comparator_4_eq, comparator_5_eq, comparator_6_eq, comparator_7_eq, comparator_8_eq, not_1_out,
       not_2_out, not_3_out, not_4_out, or_1_out, or_2_out;

  not not_1 (not_1_out, comparator_1_eq);
  Comparator #(.width(5), .mode("unsigned")) comparator_1 (
    .a(Rt), .b({5{1'b0}}), .eq(comparator_1_eq));  // open: gt, lt
  Comparator #(.width(5), .mode("unsigned")) comparator_2 (
    .a(Rt_2), .b(MEN_WriteReg), .eq(comparator_2_eq));  // open: gt, lt
  Comparator #(.width(5), .mode("unsigned")) comparator_3 (
    .a(Rt_3), .b({5{1'b0}}), .eq(comparator_3_eq));  // open: gt, lt
  not not_2 (not_2_out, comparator_3_eq);
  Comparator #(.width(5), .mode("unsigned")) comparator_4 (
    .a(Rt_4), .b(EX_WriteReg), .eq(comparator_4_eq));  // open: gt, lt
  not not_3 (not_3_out, comparator_5_eq);
  Comparator #(.width(5), .mode("unsigned")) comparator_5 (
    .a(Rs), .b({5{1'b0}}), .eq(comparator_5_eq));  // open: gt, lt
  Comparator #(.width(5), .mode("unsigned")) comparator_6 (
    .a(Rs_2), .b(EX_WriteReg_2), .eq(comparator_6_eq));  // open: gt, lt
  not not_4 (not_4_out, comparator_7_eq);
  Comparator #(.width(5), .mode("unsigned")) comparator_7 (
    .a(Rs_3), .b({5{1'b0}}), .eq(comparator_7_eq));  // open: gt, lt
  Comparator #(.width(5), .mode("unsigned")) comparator_8 (
    .a(Rs_4), .b(MEN_WriteReg_2), .eq(comparator_8_eq));  // open: gt, lt
  and and_1 (and_1_out, RtUsed, not_1_out);
  and and_2 (and_2_out, comparator_2_eq, MEN_Regwrite);
  and and_3 (and_3_out, RtUsed_2, not_2_out);
  and and_4 (and_4_out, comparator_4_eq, EX_Regwrite);
  and and_5 (and_5_out, RsUsed, not_3_out);
  and and_6 (and_6_out, comparator_6_eq, EX_Regwrite_2);
  and and_7 (and_7_out, RsUsed_2, not_4_out);
  and and_8 (and_8_out, comparator_8_eq, MEN_Regwrite_2);
  and and_9 (and_9_out, and_1_out, and_2_out);
  and and_10 (and_10_out, and_3_out, and_4_out);
  and and_11 (and_11_out, and_5_out, and_6_out);
  and and_12 (and_12_out, and_7_out, and_8_out);
  or or_1 (or_1_out, and_9_out, and_10_out);
  or or_2 (or_2_out, and_11_out, and_12_out);
  or or_3 (datahazzed, or_1_out, or_2_out);
endmodule

module \气泡处理  (
  input  datahazzd,
  input  branch,
  input  datahazzd_2,
  output stall,
  output flush
);

  or or_1 (flush, branch, datahazzd_2);

  assign stall = datahazzd;
endmodule

module loaduse (
  input  rsused,
  input  [4:0] rs,
  input  [4:0] EX_WriteReg,
  input  EX_MemRead,
  input  rtused,
  input  [4:0] rt,
  input  [4:0] EX_WriteReg_2,
  input  EX_MemRead_2,
  output LoadUse
);

  wire and_1_out, and_2_out, comparator_1_eq, comparator_2_eq, comparator_3_eq, comparator_4_eq, not_1_out,
       not_2_out;

  not not_1 (not_1_out, comparator_1_eq);
  Comparator #(.width(5), .mode("twosComplement")) comparator_1 (
    .a(rs), .b({5{1'b0}}), .eq(comparator_1_eq));  // open: gt, lt
  Comparator #(.width(5), .mode("twosComplement")) comparator_2 (
    .a(rs), .b(EX_WriteReg), .eq(comparator_2_eq));  // open: gt, lt
  Comparator #(.width(5), .mode("twosComplement")) comparator_3 (
    .a(rt), .b({5{1'b0}}), .eq(comparator_3_eq));  // open: gt, lt
  not not_2 (not_2_out, comparator_3_eq);
  Comparator #(.width(5), .mode("twosComplement")) comparator_4 (
    .a(rt), .b(EX_WriteReg_2), .eq(comparator_4_eq));  // open: gt, lt
  and and_1 (and_1_out, rsused, not_1_out, comparator_2_eq, EX_MemRead);
  and and_2 (and_2_out, rtused, not_2_out, comparator_4_eq, EX_MemRead_2);
  or or_1 (LoadUse, and_1_out, and_2_out);
endmodule

module foward (
  input  [4:0] EX_WriteReg,
  input  [4:0] rs,
  input  EX_RegWrite,
  input  rsused,
  input  [4:0] EX_WriteReg_2,
  input  [4:0] MEM_WriteReg,
  input  [4:0] rt,
  input  [4:0] rs_2,
  input  EX_RegWrite_2,
  input  MEM_RegWrite,
  input  rtused,
  input  rsused_2,
  input  [4:0] MEM_WriteReg_2,
  input  [4:0] rt_2,
  input  MEM_RegWrite_2,
  input  rtused_2,
  output [1:0] RSFoward,
  output [1:0] RTFoward
);

  wire comparator_1_eq, comparator_2_eq, comparator_3_eq, comparator_4_eq, comparator_5_eq, comparator_6_eq,
       comparator_7_eq, comparator_8_eq, not_1_out, not_2_out, not_3_out, not_4_out;
  wire [1:0] and_1_out, and_3_out;

  Comparator #(.width(5), .mode("twosComplement")) comparator_1 (
    .a(rs), .b({5{1'b0}}), .eq(comparator_1_eq));  // open: gt, lt
  Comparator #(.width(5), .mode("twosComplement")) comparator_2 (
    .a(rs_2), .b({5{1'b0}}), .eq(comparator_2_eq));  // open: gt, lt
  Comparator #(.width(5), .mode("twosComplement")) comparator_3 (
    .a(EX_WriteReg), .b(rs), .eq(comparator_3_eq));  // open: gt, lt
  not not_1 (not_1_out, comparator_1_eq);
  Comparator #(.width(5), .mode("twosComplement")) comparator_4 (
    .a(MEM_WriteReg), .b(rs_2), .eq(comparator_4_eq));  // open: gt, lt
  not not_2 (not_2_out, comparator_2_eq);
  and and_1 (and_1_out[0], comparator_3_eq, not_1_out, EX_RegWrite, rsused);
  and and_2 (and_1_out[1], comparator_4_eq, not_2_out, MEM_RegWrite, rsused_2);
  Multiplexer #(.select(2), .width(2), .disabled("Z"), .enable("false")) multiplexer_1 (
    .in0(2'b00), .in1(2'b10), .in2(2'b01), .in3(2'b10), .out(RSFoward), .sel(and_1_out));
  Comparator #(.width(5), .mode("twosComplement")) comparator_5 (
    .a(EX_WriteReg_2), .b(rt), .eq(comparator_5_eq));  // open: gt, lt
  not not_3 (not_3_out, comparator_6_eq);
  Comparator #(.width(5), .mode("twosComplement")) comparator_6 (
    .a(rt), .b({5{1'b0}}), .eq(comparator_6_eq));  // open: gt, lt
  Comparator #(.width(5), .mode("twosComplement")) comparator_7 (
    .a(MEM_WriteReg_2), .b(rt_2), .eq(comparator_7_eq));  // open: gt, lt
  Comparator #(.width(5), .mode("twosComplement")) comparator_8 (
    .a(rt_2), .b({5{1'b0}}), .eq(comparator_8_eq));  // open: gt, lt
  not not_4 (not_4_out, comparator_8_eq);
  and and_3 (and_3_out[0], comparator_5_eq, not_3_out, EX_RegWrite_2, rtused);
  and and_4 (and_3_out[1], comparator_7_eq, not_4_out, MEM_RegWrite_2, rtused_2);
  Multiplexer #(.select(2), .width(2), .disabled("Z"), .enable("false")) multiplexer_2 (
    .in0(2'b00), .in1(2'b10), .in2(2'b01), .in3(2'b10), .out(RTFoward), .sel(and_3_out));
endmodule

module IF_ID (
  input  [31:0] PCin,
  input  [31:0] IRin,
  input  PredictJumpin,
  input  RST,
  input  EN,
  input  CLK,
  input  RST_num,
  output [31:0] PCout,
  output [31:0] IRout,
  output PredictJumpout
);

  wire multiplexer_3_out;
  wire [31:0] multiplexer_1_out, multiplexer_2_out;

  Multiplexer #(.select(1), .width(32), .disabled("Z"), .enable("false")) multiplexer_1 (
    .in0(PCin), .in1({32{1'b0}}), .out(multiplexer_1_out), .sel(RST));
  Multiplexer #(.select(1), .width(32), .disabled("Z"), .enable("false")) multiplexer_2 (
    .in0(IRin), .in1({32{1'b0}}), .out(multiplexer_2_out), .sel(RST));
  Multiplexer #(.select(1), .width(1), .disabled("Z"), .enable("false")) multiplexer_3 (
    .in0(PredictJumpin), .in1(1'b0), .out(multiplexer_3_out), .sel(RST));
  Register #(.width(32), .trigger("rising"), .Select("low")) register_1 (
    .D(multiplexer_1_out), .en(EN), .Q(PCout), .clk(CLK), .clr(RST_num));
  Register #(.width(32), .trigger("rising"), .Select("low")) register_2 (
    .D(multiplexer_2_out), .en(EN), .Q(IRout), .clk(CLK), .clr(RST_num));
  Register #(.width(1), .trigger("rising"), .Select("low")) register_3 (
    .D(multiplexer_3_out), .en(EN), .Q(PredictJumpout), .clk(CLK), .clr(RST_num));
endmodule

module ID_EX (
  input  Beqin,
  input  [31:0] PCin,
  input  Bnein,
  input  [31:0] IRin,
  input  MemToRegin,
  input  MemWritein,
  input  [31:0] Imm_I_in,
  input  AluSrcBin,
  input  [31:0] Imm_S_in,
  input  RegWritein,
  input  [31:0] Imm_B_in,
  input  S_typein,
  input  Jalin,
  input  [31:0] Imm_J_in,
  input  Jalrin,
  input  [31:0] R1in,
  input  Haltin,
  input  [31:0] R2in,
  input  [4:0] W_in,
  input  [31:0] Imm_lui_in,
  input  LUIin,
  input  LHUin,
  input  BLTUin,
  input  [1:0] R1Forwardin,
  input  [1:0] R2Forwardin,
  input  Ecallin,
  input  Uretlin,
  input  PredictJumpin,
  input  [3:0] AluOpin,
  input  RST_num,
  input  RST,
  input  EN,
  input  CLK,
  output Beqout,
  output [31:0] PCout,
  output Bneout,
  output [31:0] IRout,
  output MemToRegout,
  output MemWriteout,
  output [31:0] Imm_I_out,
  output AluSrcBout,
  output [31:0] Imm_S_out,
  output RegWriteout,
  output [31:0] Imm_B_out,
  output S_Typeout,
  output Jalout,
  output [31:0] Imm_J_out,
  output Jalrout,
  output [31:0] R1out,
  output Haltout,
  output [31:0] R2out,
  output [4:0] W_out,
  output [31:0] Imm_lui_out,
  output LUIout,
  output LHUout,
  output BLTUout,
  output [1:0] R1Forwardout,
  output [1:0] R2Forwardout,
  output Ecallout,
  output Uretout,
  output PredictJumpout,
  output [3:0] AluOpout
);

  wire multiplexer_11_out, multiplexer_12_out, multiplexer_13_out, multiplexer_14_out, multiplexer_15_out,
       multiplexer_16_out, multiplexer_17_out, multiplexer_18_out, multiplexer_19_out, multiplexer_20_out,
       multiplexer_22_out, multiplexer_23_out, multiplexer_24_out, multiplexer_27_out, multiplexer_28_out,
       multiplexer_29_out;
  wire [1:0] multiplexer_25_out, multiplexer_26_out;
  wire [3:0] multiplexer_10_out;
  wire [4:0] multiplexer_21_out;
  wire [31:0] multiplexer_1_out, multiplexer_2_out, multiplexer_3_out, multiplexer_4_out, multiplexer_5_out,
       multiplexer_6_out, multiplexer_7_out, multiplexer_8_out, multiplexer_9_out;

  Multiplexer #(.select(1), .width(32), .disabled("Z"), .enable("false")) multiplexer_1 (
    .in0(PCin), .in1({32{1'b0}}), .out(multiplexer_1_out), .sel(RST));
  Multiplexer #(.select(1), .width(32), .disabled("Z"), .enable("false")) multiplexer_2 (
    .in0(IRin), .in1({32{1'b0}}), .out(multiplexer_2_out), .sel(RST));
  Multiplexer #(.select(1), .width(32), .disabled("Z"), .enable("false")) multiplexer_3 (
    .in0(Imm_I_in), .in1({32{1'b0}}), .out(multiplexer_3_out), .sel(RST));
  Multiplexer #(.select(1), .width(32), .disabled("Z"), .enable("false")) multiplexer_4 (
    .in0(Imm_S_in), .in1({32{1'b0}}), .out(multiplexer_4_out), .sel(RST));
  Multiplexer #(.select(1), .width(32), .disabled("Z"), .enable("false")) multiplexer_5 (
    .in0(Imm_B_in), .in1({32{1'b0}}), .out(multiplexer_5_out), .sel(RST));
  Multiplexer #(.select(1), .width(32), .disabled("Z"), .enable("false")) multiplexer_6 (
    .in0(Imm_J_in), .in1({32{1'b0}}), .out(multiplexer_6_out), .sel(RST));
  Multiplexer #(.select(1), .width(32), .disabled("Z"), .enable("false")) multiplexer_7 (
    .in0(R1in), .in1({32{1'b0}}), .out(multiplexer_7_out), .sel(RST));
  Multiplexer #(.select(1), .width(32), .disabled("Z"), .enable("false")) multiplexer_8 (
    .in0(R2in), .in1({32{1'b0}}), .out(multiplexer_8_out), .sel(RST));
  Multiplexer #(.select(1), .width(32), .disabled("Z"), .enable("false")) multiplexer_9 (
    .in0(Imm_lui_in), .in1({32{1'b0}}), .out(multiplexer_9_out), .sel(RST));
  Multiplexer #(.select(1), .width(4), .disabled("Z"), .enable("false")) multiplexer_10 (
    .in0(AluOpin), .in1(4'b0000), .out(multiplexer_10_out), .sel(RST));
  Register #(.width(32), .trigger("rising"), .Select("low")) register_1 (
    .D(multiplexer_1_out), .en(EN), .Q(PCout), .clk(CLK), .clr(RST_num));
  Register #(.width(32), .trigger("rising"), .Select("low")) register_2 (
    .D(multiplexer_2_out), .en(EN), .Q(IRout), .clk(CLK), .clr(RST_num));
  Register #(.width(32), .trigger("rising"), .Select("low")) register_3 (
    .D(multiplexer_3_out), .en(EN), .Q(Imm_I_out), .clk(CLK), .clr(RST_num));
  Register #(.width(32), .trigger("rising"), .Select("low")) register_4 (
    .D(multiplexer_4_out), .en(EN), .Q(Imm_S_out), .clk(CLK), .clr(RST_num));
  Register #(.width(32), .trigger("rising"), .Select("low")) register_5 (
    .D(multiplexer_5_out), .en(EN), .Q(Imm_B_out), .clk(CLK), .clr(RST_num));
  Register #(.width(32), .trigger("rising"), .Select("low")) register_6 (
    .D(multiplexer_6_out), .en(EN), .Q(Imm_J_out), .clk(CLK), .clr(RST_num));
  Register #(.width(32), .trigger("rising"), .Select("low")) register_7 (
    .D(multiplexer_7_out), .en(EN), .Q(R1out), .clk(CLK), .clr(RST_num));
  Register #(.width(32), .trigger("rising"), .Select("low")) register_8 (
    .D(multiplexer_8_out), .en(EN), .Q(R2out), .clk(CLK), .clr(RST_num));
  Register #(.width(32), .trigger("rising"), .Select("low")) register_9 (
    .D(multiplexer_9_out), .en(EN), .Q(Imm_lui_out), .clk(CLK), .clr(RST_num));
  Register #(.width(4), .trigger("rising"), .Select("low")) register_10 (
    .D(multiplexer_10_out), .en(EN), .Q(AluOpout), .clk(CLK), .clr(RST_num));
  Multiplexer #(.select(1), .width(1), .disabled("Z"), .enable("false")) multiplexer_11 (
    .in0(Beqin), .in1(1'b0), .out(multiplexer_11_out), .sel(RST));
  Multiplexer #(.select(1), .width(1), .disabled("Z"), .enable("false")) multiplexer_12 (
    .in0(Bnein), .in1(1'b0), .out(multiplexer_12_out), .sel(RST));
  Multiplexer #(.select(1), .width(1), .disabled("Z"), .enable("false")) multiplexer_13 (
    .in0(MemToRegin), .in1(1'b0), .out(multiplexer_13_out), .sel(RST));
  Multiplexer #(.select(1), .width(1), .disabled("Z"), .enable("false")) multiplexer_14 (
    .in0(MemWritein), .in1(1'b0), .out(multiplexer_14_out), .sel(RST));
  Multiplexer #(.select(1), .width(1), .disabled("Z"), .enable("false")) multiplexer_15 (
    .in0(AluSrcBin), .in1(1'b0), .out(multiplexer_15_out), .sel(RST));
  Multiplexer #(.select(1), .width(1), .disabled("Z"), .enable("false")) multiplexer_16 (
    .in0(RegWritein), .in1(1'b0), .out(multiplexer_16_out), .sel(RST));
  Multiplexer #(.select(1), .width(1), .disabled("Z"), .enable("false")) multiplexer_17 (
    .in0(S_typein), .in1(1'b0), .out(multiplexer_17_out), .sel(RST));
  Multiplexer #(.select(1), .width(1), .disabled("Z"), .enable("false")) multiplexer_18 (
    .in0(Jalin), .in1(1'b0), .out(multiplexer_18_out), .sel(RST));
  Multiplexer #(.select(1), .width(1), .disabled("Z"), .enable("false")) multiplexer_19 (
    .in0(Jalrin), .in1(1'b0), .out(multiplexer_19_out), .sel(RST));
  Multiplexer #(.select(1), .width(1), .disabled("Z"), .enable("false")) multiplexer_20 (
    .in0(Haltin), .in1(1'b0), .out(multiplexer_20_out), .sel(RST));
  Multiplexer #(.select(1), .width(5), .disabled("Z"), .enable("false")) multiplexer_21 (
    .in0(W_in), .in1({5{1'b0}}), .out(multiplexer_21_out), .sel(RST));
  Multiplexer #(.select(1), .width(1), .disabled("Z"), .enable("false")) multiplexer_22 (
    .in0(LUIin), .in1(1'b0), .out(multiplexer_22_out), .sel(RST));
  Multiplexer #(.select(1), .width(1), .disabled("Z"), .enable("false")) multiplexer_23 (
    .in0(LHUin), .in1(1'b0), .out(multiplexer_23_out), .sel(RST));
  Multiplexer #(.select(1), .width(1), .disabled("Z"), .enable("false")) multiplexer_24 (
    .in0(BLTUin), .in1(1'b0), .out(multiplexer_24_out), .sel(RST));
  Multiplexer #(.select(1), .width(2), .disabled("Z"), .enable("false")) multiplexer_25 (
    .in0(R1Forwardin), .in1(2'b00), .out(multiplexer_25_out), .sel(RST));
  Multiplexer #(.select(1), .width(2), .disabled("Z"), .enable("false")) multiplexer_26 (
    .in0(R2Forwardin), .in1(2'b00), .out(multiplexer_26_out), .sel(RST));
  Multiplexer #(.select(1), .width(1), .disabled("Z"), .enable("false")) multiplexer_27 (
    .in0(Ecallin), .in1(1'b0), .out(multiplexer_27_out), .sel(RST));
  Multiplexer #(.select(1), .width(1), .disabled("Z"), .enable("false")) multiplexer_28 (
    .in0(Uretlin), .in1(1'b0), .out(multiplexer_28_out), .sel(RST));
  Multiplexer #(.select(1), .width(1), .disabled("Z"), .enable("false")) multiplexer_29 (
    .in0(PredictJumpin), .in1(1'b0), .out(multiplexer_29_out), .sel(RST));
  Register #(.width(1), .trigger("rising"), .Select("low")) register_11 (
    .D(multiplexer_11_out), .en(EN), .Q(Beqout), .clk(CLK), .clr(RST_num));
  Register #(.width(1), .trigger("rising"), .Select("low")) register_12 (
    .D(multiplexer_12_out), .en(EN), .Q(Bneout), .clk(CLK), .clr(RST_num));
  Register #(.width(1), .trigger("rising"), .Select("low")) register_13 (
    .D(multiplexer_13_out), .en(EN), .Q(MemToRegout), .clk(CLK), .clr(RST_num));
  Register #(.width(1), .trigger("rising"), .Select("low")) register_14 (
    .D(multiplexer_14_out), .en(EN), .Q(MemWriteout), .clk(CLK), .clr(RST_num));
  Register #(.width(1), .trigger("rising"), .Select("low")) register_15 (
    .D(multiplexer_15_out), .en(EN), .Q(AluSrcBout), .clk(CLK), .clr(RST_num));
  Register #(.width(1), .trigger("rising"), .Select("low")) register_16 (
    .D(multiplexer_16_out), .en(EN), .Q(RegWriteout), .clk(CLK), .clr(RST_num));
  Register #(.width(1), .trigger("rising"), .Select("low")) register_17 (
    .D(multiplexer_17_out), .en(EN), .Q(S_Typeout), .clk(CLK), .clr(RST_num));
  Register #(.width(1), .trigger("rising"), .Select("low")) register_18 (
    .D(multiplexer_18_out), .en(EN), .Q(Jalout), .clk(CLK), .clr(RST_num));
  Register #(.width(1), .trigger("rising"), .Select("low")) register_19 (
    .D(multiplexer_19_out), .en(EN), .Q(Jalrout), .clk(CLK), .clr(RST_num));
  Register #(.width(1), .trigger("rising"), .Select("low")) register_20 (
    .D(multiplexer_20_out), .en(EN), .Q(Haltout), .clk(CLK), .clr(RST_num));
  Register #(.width(5), .trigger("rising"), .Select("low")) register_21 (
    .D(multiplexer_21_out), .en(EN), .Q(W_out), .clk(CLK), .clr(RST_num));
  Register #(.width(1), .trigger("rising"), .Select("low")) register_22 (
    .D(multiplexer_22_out), .en(EN), .Q(LUIout), .clk(CLK), .clr(RST_num));
  Register #(.width(1), .trigger("rising"), .Select("low")) register_23 (
    .D(multiplexer_23_out), .en(EN), .Q(LHUout), .clk(CLK), .clr(RST_num));
  Register #(.width(1), .trigger("rising"), .Select("low")) register_24 (
    .D(multiplexer_24_out), .en(EN), .Q(BLTUout), .clk(CLK), .clr(RST_num));
  Register #(.width(2), .trigger("rising"), .Select("low")) register_25 (
    .D(multiplexer_25_out), .en(EN), .Q(R1Forwardout), .clk(CLK), .clr(RST_num));
  Register #(.width(2), .trigger("rising"), .Select("low")) register_26 (
    .D(multiplexer_26_out), .en(EN), .Q(R2Forwardout), .clk(CLK), .clr(RST_num));
  Register #(.width(1), .trigger("rising"), .Select("low")) register_27 (
    .D(multiplexer_27_out), .en(EN), .Q(Ecallout), .clk(CLK), .clr(RST_num));
  Register #(.width(1), .trigger("rising"), .Select("low")) register_28 (
    .D(multiplexer_28_out), .en(EN), .Q(Uretout), .clk(CLK), .clr(RST_num));
  Register #(.width(1), .trigger("rising"), .Select("low")) register_29 (
    .D(multiplexer_29_out), .en(EN), .Q(PredictJumpout), .clk(CLK), .clr(RST_num));
endmodule

module EX_MEM (
  input  MemToRegin,
  input  [31:0] PCin,
  input  MemWritein,
  input  [31:0] IRin,
  input  JAMPin,
  input  RegWritein,
  input  [31:0] Resultin,
  input  Haltin,
  input  [31:0] MDatain,
  input  [4:0] W_in,
  input  [31:0] Imm_lui_in,
  input  LUIin,
  input  LHUin,
  input  BLTUin,
  input  Uretlin,
  input  RST,
  input  EN_H,
  input  CLK,
  input  RST_num,
  output MemToRegout,
  output [31:0] PCout,
  output MemWriteout,
  output [31:0] IRout,
  output JAMPout,
  output RegWriteout,
  output [31:0] Resultout,
  output Haltout,
  output [31:0] Mdataout,
  output [4:0] W_out,
  output [31:0] Imm_lui_out,
  output LUIout,
  output LHUout,
  output BLTUout,
  output Uretout
);

  wire multiplexer_6_out, multiplexer_7_out, multiplexer_8_out, multiplexer_9_out, multiplexer_10_out,
       multiplexer_12_out, multiplexer_13_out, multiplexer_14_out, multiplexer_15_out;
  wire [4:0] multiplexer_11_out;
  wire [31:0] multiplexer_1_out, multiplexer_2_out, multiplexer_3_out, multiplexer_4_out, multiplexer_5_out;

  Multiplexer #(.select(1), .width(32), .disabled("Z"), .enable("false")) multiplexer_1 (
    .in0(IRin), .in1({32{1'b0}}), .out(multiplexer_1_out), .sel(RST));
  Multiplexer #(.select(1), .width(32), .disabled("Z"), .enable("false")) multiplexer_2 (
    .in0(Resultin), .in1({32{1'b0}}), .out(multiplexer_2_out), .sel(RST));
  Multiplexer #(.select(1), .width(32), .disabled("Z"), .enable("false")) multiplexer_3 (
    .in0(MDatain), .in1({32{1'b0}}), .out(multiplexer_3_out), .sel(RST));
  Multiplexer #(.select(1), .width(32), .disabled("Z"), .enable("false")) multiplexer_4 (
    .in0(PCin), .in1({32{1'b0}}), .out(multiplexer_4_out), .sel(RST));
  Multiplexer #(.select(1), .width(32), .disabled("Z"), .enable("false")) multiplexer_5 (
    .in0(Imm_lui_in), .in1({32{1'b0}}), .out(multiplexer_5_out), .sel(RST));
  Register #(.width(32), .trigger("rising"), .Select("low")) register_1 (
    .D(multiplexer_5_out), .en(EN_H), .Q(Imm_lui_out), .clk(CLK), .clr(RST_num));
  Register #(.width(32), .trigger("rising"), .Select("low")) register_2 (
    .D(multiplexer_4_out), .en(EN_H), .Q(PCout), .clk(CLK), .clr(RST_num));
  Register #(.width(32), .trigger("rising"), .Select("low")) register_3 (
    .D(multiplexer_1_out), .en(EN_H), .Q(IRout), .clk(CLK), .clr(RST_num));
  Register #(.width(32), .trigger("rising"), .Select("low")) register_4 (
    .D(multiplexer_2_out), .en(EN_H), .Q(Resultout), .clk(CLK), .clr(RST_num));
  Register #(.width(32), .trigger("rising"), .Select("low")) register_5 (
    .D(multiplexer_3_out), .en(EN_H), .Q(Mdataout), .clk(CLK), .clr(RST_num));
  Multiplexer #(.select(1), .width(1), .disabled("Z"), .enable("false")) multiplexer_6 (
    .in0(MemToRegin), .in1(1'b0), .out(multiplexer_6_out), .sel(RST));
  Multiplexer #(.select(1), .width(1), .disabled("Z"), .enable("false")) multiplexer_7 (
    .in0(MemWritein), .in1(1'b0), .out(multiplexer_7_out), .sel(RST));
  Multiplexer #(.select(1), .width(1), .disabled("Z"), .enable("false")) multiplexer_8 (
    .in0(JAMPin), .in1(1'b0), .out(multiplexer_8_out), .sel(RST));
  Multiplexer #(.select(1), .width(1), .disabled("Z"), .enable("false")) multiplexer_9 (
    .in0(RegWritein), .in1(1'b0), .out(multiplexer_9_out), .sel(RST));
  Multiplexer #(.select(1), .width(1), .disabled("Z"), .enable("false")) multiplexer_10 (
    .in0(Haltin), .in1(1'b0), .out(multiplexer_10_out), .sel(RST));
  Multiplexer #(.select(1), .width(5), .disabled("Z"), .enable("false")) multiplexer_11 (
    .in0(W_in), .in1({5{1'b0}}), .out(multiplexer_11_out), .sel(RST));
  Multiplexer #(.select(1), .width(1), .disabled("Z"), .enable("false")) multiplexer_12 (
    .in0(LUIin), .in1(1'b0), .out(multiplexer_12_out), .sel(RST));
  Multiplexer #(.select(1), .width(1), .disabled("Z"), .enable("false")) multiplexer_13 (
    .in0(LHUin), .in1(1'b0), .out(multiplexer_13_out), .sel(RST));
  Multiplexer #(.select(1), .width(1), .disabled("Z"), .enable("false")) multiplexer_14 (
    .in0(BLTUin), .in1(1'b0), .out(multiplexer_14_out), .sel(RST));
  Multiplexer #(.select(1), .width(1), .disabled("Z"), .enable("false")) multiplexer_15 (
    .in0(Uretlin), .in1(1'b0), .out(multiplexer_15_out), .sel(RST));
  Register #(.width(1), .trigger("rising"), .Select("low")) register_6 (
    .D(multiplexer_6_out), .en(EN_H), .Q(MemToRegout), .clk(CLK), .clr(RST_num));
  Register #(.width(1), .trigger("rising"), .Select("low")) register_7 (
    .D(multiplexer_7_out), .en(EN_H), .Q(MemWriteout), .clk(CLK), .clr(RST_num));
  Register #(.width(1), .trigger("rising"), .Select("low")) register_8 (
    .D(multiplexer_8_out), .en(EN_H), .Q(JAMPout), .clk(CLK), .clr(RST_num));
  Register #(.width(1), .trigger("rising"), .Select("low")) register_9 (
    .D(multiplexer_9_out), .en(EN_H), .Q(RegWriteout), .clk(CLK), .clr(RST_num));
  Register #(.width(1), .trigger("rising"), .Select("low")) register_10 (
    .D(multiplexer_10_out), .en(EN_H), .Q(Haltout), .clk(CLK), .clr(RST_num));
  Register #(.width(5), .trigger("rising"), .Select("low")) register_11 (
    .D(multiplexer_11_out), .en(EN_H), .Q(W_out), .clk(CLK), .clr(RST_num));
  Register #(.width(1), .trigger("rising"), .Select("low")) register_12 (
    .D(multiplexer_12_out), .en(EN_H), .Q(LUIout), .clk(CLK), .clr(RST_num));
  Register #(.width(1), .trigger("rising"), .Select("low")) register_13 (
    .D(multiplexer_13_out), .en(EN_H), .Q(LHUout), .clk(CLK), .clr(RST_num));
  Register #(.width(1), .trigger("rising"), .Select("low")) register_14 (
    .D(multiplexer_14_out), .en(EN_H), .Q(BLTUout), .clk(CLK), .clr(RST_num));
  Register #(.width(1), .trigger("rising"), .Select("low")) register_15 (
    .D(multiplexer_15_out), .en(EN_H), .Q(Uretout), .clk(CLK), .clr(RST_num));
endmodule

module MEM_WB (
  input  MemToRegin,
  input  [31:0] PCin,
  input  JAMPin,
  input  [31:0] IRin,
  input  RegWritein,
  input  [31:0] Resultin,
  input  Haltin,
  input  [31:0] RMDatain,
  input  [4:0] W_in,
  input  LUIin,
  input  [31:0] Imm_lui_in,
  input  LHUin,
  input  BLTUin,
  input  Uretlin,
  input  RST,
  input  EN_H,
  input  CLK,
  input  RST_num,
  output MemToRegout,
  output [31:0] PCout,
  output JAMPout,
  output [31:0] IRout,
  output RegWriteout,
  output [31:0] Resultout,
  output Haltout,
  output [31:0] RMdataout,
  output [4:0] W_out,
  output LUIout,
  output [31:0] Imm_lui_out,
  output LHUout,
  output BLTUout,
  output Uretout
);

  wire multiplexer_6_out, multiplexer_7_out, multiplexer_8_out, multiplexer_9_out, multiplexer_11_out,
       multiplexer_12_out, multiplexer_13_out, multiplexer_14_out;
  wire [4:0] multiplexer_10_out;
  wire [31:0] multiplexer_1_out, multiplexer_2_out, multiplexer_3_out, multiplexer_4_out, multiplexer_5_out;

  Multiplexer #(.select(1), .width(32), .disabled("Z"), .enable("false")) multiplexer_1 (
    .in0(PCin), .in1({32{1'b0}}), .out(multiplexer_1_out), .sel(RST));
  Multiplexer #(.select(1), .width(32), .disabled("Z"), .enable("false")) multiplexer_2 (
    .in0(IRin), .in1({32{1'b0}}), .out(multiplexer_2_out), .sel(RST));
  Multiplexer #(.select(1), .width(32), .disabled("Z"), .enable("false")) multiplexer_3 (
    .in0(Resultin), .in1({32{1'b0}}), .out(multiplexer_3_out), .sel(RST));
  Multiplexer #(.select(1), .width(32), .disabled("Z"), .enable("false")) multiplexer_4 (
    .in0(RMDatain), .in1({32{1'b0}}), .out(multiplexer_4_out), .sel(RST));
  Multiplexer #(.select(1), .width(32), .disabled("Z"), .enable("false")) multiplexer_5 (
    .in0(Imm_lui_in), .in1({32{1'b0}}), .out(multiplexer_5_out), .sel(RST));
  Register #(.width(32), .trigger("rising"), .Select("low")) register_1 (
    .D(multiplexer_1_out), .en(EN_H), .Q(PCout), .clk(CLK), .clr(RST_num));
  Register #(.width(32), .trigger("rising"), .Select("low")) register_2 (
    .D(multiplexer_2_out), .en(EN_H), .Q(IRout), .clk(CLK), .clr(RST_num));
  Register #(.width(32), .trigger("rising"), .Select("low")) register_3 (
    .D(multiplexer_3_out), .en(EN_H), .Q(Resultout), .clk(CLK), .clr(RST_num));
  Register #(.width(32), .trigger("rising"), .Select("low")) register_4 (
    .D(multiplexer_4_out), .en(EN_H), .Q(RMdataout), .clk(CLK), .clr(RST_num));
  Register #(.width(32), .trigger("rising"), .Select("low")) register_5 (
    .D(multiplexer_5_out), .en(EN_H), .Q(Imm_lui_out), .clk(CLK), .clr(RST_num));
  Multiplexer #(.select(1), .width(1), .disabled("Z"), .enable("false")) multiplexer_6 (
    .in0(MemToRegin), .in1(1'b0), .out(multiplexer_6_out), .sel(RST));
  Multiplexer #(.select(1), .width(1), .disabled("Z"), .enable("false")) multiplexer_7 (
    .in0(JAMPin), .in1(1'b0), .out(multiplexer_7_out), .sel(RST));
  Multiplexer #(.select(1), .width(1), .disabled("Z"), .enable("false")) multiplexer_8 (
    .in0(RegWritein), .in1(1'b0), .out(multiplexer_8_out), .sel(RST));
  Multiplexer #(.select(1), .width(1), .disabled("Z"), .enable("false")) multiplexer_9 (
    .in0(Haltin), .in1(1'b0), .out(multiplexer_9_out), .sel(RST));
  Multiplexer #(.select(1), .width(5), .disabled("Z"), .enable("false")) multiplexer_10 (
    .in0(W_in), .in1({5{1'b0}}), .out(multiplexer_10_out), .sel(RST));
  Multiplexer #(.select(1), .width(1), .disabled("Z"), .enable("false")) multiplexer_11 (
    .in0(LUIin), .in1(1'b0), .out(multiplexer_11_out), .sel(RST));
  Multiplexer #(.select(1), .width(1), .disabled("Z"), .enable("false")) multiplexer_12 (
    .in0(LHUin), .in1(1'b0), .out(multiplexer_12_out), .sel(RST));
  Multiplexer #(.select(1), .width(1), .disabled("Z"), .enable("false")) multiplexer_13 (
    .in0(BLTUin), .in1(1'b0), .out(multiplexer_13_out), .sel(RST));
  Multiplexer #(.select(1), .width(1), .disabled("Z"), .enable("false")) multiplexer_14 (
    .in0(Uretlin), .in1(1'b0), .out(multiplexer_14_out), .sel(RST));
  Register #(.width(1), .trigger("rising"), .Select("low")) register_6 (
    .D(multiplexer_6_out), .en(EN_H), .Q(MemToRegout), .clk(CLK), .clr(RST_num));
  Register #(.width(1), .trigger("rising"), .Select("low")) register_7 (
    .D(multiplexer_7_out), .en(EN_H), .Q(JAMPout), .clk(CLK), .clr(RST_num));
  Register #(.width(1), .trigger("rising"), .Select("low")) register_8 (
    .D(multiplexer_8_out), .en(EN_H), .Q(RegWriteout), .clk(CLK), .clr(RST_num));
  Register #(.width(1), .trigger("rising"), .Select("low")) register_9 (
    .D(multiplexer_9_out), .en(EN_H), .Q(Haltout), .clk(CLK), .clr(RST_num));
  Register #(.width(5), .trigger("rising"), .Select("low")) register_10 (
    .D(multiplexer_10_out), .en(EN_H), .Q(W_out), .clk(CLK), .clr(RST_num));
  Register #(.width(1), .trigger("rising"), .Select("low")) register_11 (
    .D(multiplexer_11_out), .en(EN_H), .Q(LUIout), .clk(CLK), .clr(RST_num));
  Register #(.width(1), .trigger("rising"), .Select("low")) register_12 (
    .D(multiplexer_12_out), .en(EN_H), .Q(LHUout), .clk(CLK), .clr(RST_num));
  Register #(.width(1), .trigger("rising"), .Select("low")) register_13 (
    .D(multiplexer_13_out), .en(EN_H), .Q(BLTUout), .clk(CLK), .clr(RST_num));
  Register #(.width(1), .trigger("rising"), .Select("low")) register_14 (
    .D(multiplexer_14_out), .en(EN_H), .Q(Uretout), .clk(CLK), .clr(RST_num));
endmodule

module BTB (
  input  CLK,
  input  [1:0] NewJumpStat,
  input  En,
  input  [1:0] JumpStat,
  input  [31:0] EX_PC,
  input  [31:0] BranchAddr,
  input  [31:0] PC,
  input  PCReady,
  input  StatReady,
  output [1:0] PredictJump,
  output Hit,
  output [1:0] EX_PredictJump,
  output Miss,
  output EX_Hit,
  output [31:0] JumpAddr
);

  wire and_1_out, and_2_out, and_3_out, and_4_out, and_13_out, and_14_out, and_15_out, and_16_out,
       and_17_out, and_18_out, and_19_out, and_20_out, and_21_out, and_22_out, and_31_out, and_32_out,
       and_33_out, and_34_out, and_35_out, and_36_out, and_37_out, and_38_out, and_39_out, and_40_out,
       and_41_out, and_42_out, comparator_1_eq, comparator_2_eq, comparator_3_eq, comparator_4_eq,
       comparator_5_eq, comparator_6_eq, comparator_7_eq, comparator_8_eq, comparator_9_eq, comparator_10_eq,
       comparator_11_eq, comparator_12_eq, comparator_13_eq, comparator_14_eq, comparator_15_eq,
       comparator_16_eq, E0, E1, E2, E3, E4, E5, E6, E7, EX_Miss, L0, L1, L2, L3, L4, L5, L6, L7, not_1_out,
       or_1_out, or_2_out, or_3_out, or_4_out, or_6_out, or_7_out, or_8_out, or_9_out, or_11_out, or_12_out,
       or_13_out, or_14_out, or_15_out, or_16_out, or_17_out, or_18_out, priority_encoder_1_en_out, S0, S1,
       S2, S3, S4, S5, S6, S7, V0, V1, V2, V3, V4, V5, V6, V7, W0, W1, W2, W3, W4, W5, W6, W7;
  wire [1:0] JumpState0, JumpState1, JumpState2, JumpState3, JumpState4, JumpState5, JumpState6, JumpState7,
       multiplexer_1_out, multiplexer_2_out, multiplexer_3_out, multiplexer_4_out, multiplexer_5_out,
       multiplexer_6_out, multiplexer_7_out, multiplexer_8_out, NewJumpState0, NewJumpState1, NewJumpState2,
       NewJumpState3, NewJumpState4, NewJumpState5, NewJumpState6, NewJumpState7, \分支预测历史位_2_q ,
       \分支预测历史位_3_q , \分支预测历史位_4_q , \分支预测历史位_5_q , \分支预测历史位_6_q , \分支预测历史位_7_q , \分支预测历史位_8_q , \分支预测历史位_q ;
  wire [2:0] max2_1_max_num, max2_2_max_num, max2_3_max_num, max2_4_max_num, max2_5_max_num, max2_6_max_num,
       max2_7_max_num, priority_encoder_1_out;
  wire [15:0] C0, C1, C2, C3, C4, C5, C6, C7, max2_1_max, max2_2_max, max2_3_max, max2_4_max, max2_5_max,
       max2_6_max;
  wire [31:0] Tag0, Tag1, Tag2, Tag3, Tag4, Tag5, Tag6, Tag7, \分支目标地址_2_q , \分支目标地址_3_q , \分支目标地址_4_q ,
       \分支目标地址_5_q , \分支目标地址_6_q , \分支目标地址_7_q , \分支目标地址_8_q , \分支目标地址_q ;

  and and_1 (and_1_out, W0, En);
  and and_2 (and_2_out, W1, En);
  and and_3 (and_3_out, W2, En);
  and and_4 (and_4_out, W3, En);
  Register #(.width(1), .trigger("rising"), .Select("low")) Valid (
    .D(1'b1), .en(and_1_out), .Q(V0), .clk(CLK));  // open: clr
  Register #(.width(1), .trigger("rising"), .Select("low")) Valid_2 (
    .D(1'b1), .en(and_2_out), .Q(V1), .clk(CLK));  // open: clr
  Register #(.width(1), .trigger("rising"), .Select("low")) Valid_3 (
    .D(1'b1), .en(and_3_out), .Q(V2), .clk(CLK));  // open: clr
  Register #(.width(1), .trigger("rising"), .Select("low")) Valid_4 (
    .D(1'b1), .en(and_4_out), .Q(V3), .clk(CLK));  // open: clr
  MAX2 max2_1 (.Y(C1), .X(C0), .Y_num(3'b001), .X_num(3'b000), .MAX(max2_1_max), .MAX_num(max2_1_max_num));
  MAX2 max2_2 (.Y(C3), .X(C2), .Y_num(3'b011), .X_num(3'b010), .MAX(max2_2_max), .MAX_num(max2_2_max_num));
  MAX2 max2_3 (.Y(C5), .X(C4), .Y_num(3'b101), .X_num(3'b100), .MAX(max2_3_max), .MAX_num(max2_3_max_num));
  MAX2 max2_4 (.Y(C7), .X(C6), .Y_num(3'b111), .X_num(3'b110), .MAX(max2_4_max), .MAX_num(max2_4_max_num));
  Register #(.width(32), .trigger("rising"), .Select("low")) \u_分支指令地址  (
    .D(PC), .en(and_1_out), .Q(Tag0), .clk(CLK));  // open: clr
  Register #(.width(32), .trigger("rising"), .Select("low")) \u_分支指令地址_2  (
    .D(PC), .en(and_2_out), .Q(Tag1), .clk(CLK));  // open: clr
  Register #(.width(32), .trigger("rising"), .Select("low")) \u_分支指令地址_3  (
    .D(PC), .en(and_3_out), .Q(Tag2), .clk(CLK));  // open: clr
  Register #(.width(32), .trigger("rising"), .Select("low")) \u_分支指令地址_4  (
    .D(PC), .en(and_4_out), .Q(Tag3), .clk(CLK));  // open: clr
  Comparator #(.width(32), .mode("unsigned")) comparator_1 (.a(PC), .b(Tag0), .eq(comparator_1_eq));  // open: gt, lt
  Comparator #(.width(32), .mode("unsigned")) comparator_2 (.a(PC), .b(Tag1), .eq(comparator_2_eq));  // open: gt, lt
  Comparator #(.width(32), .mode("unsigned")) comparator_3 (.a(PC), .b(Tag2), .eq(comparator_3_eq));  // open: gt, lt
  Comparator #(.width(32), .mode("unsigned")) comparator_4 (.a(PC), .b(Tag3), .eq(comparator_4_eq));  // open: gt, lt
  Comparator #(.width(32), .mode("unsigned")) comparator_5 (.a(PC), .b(Tag4), .eq(comparator_5_eq));  // open: gt, lt
  Comparator #(.width(32), .mode("unsigned")) comparator_6 (.a(PC), .b(Tag5), .eq(comparator_6_eq));  // open: gt, lt
  Comparator #(.width(32), .mode("unsigned")) comparator_7 (.a(PC), .b(Tag6), .eq(comparator_7_eq));  // open: gt, lt
  Comparator #(.width(32), .mode("unsigned")) comparator_8 (.a(PC), .b(Tag7), .eq(comparator_8_eq));  // open: gt, lt
  MAX2 max2_5 (
    .Y(max2_2_max), .X(max2_1_max), .Y_num(max2_2_max_num), .X_num(max2_1_max_num), .MAX(max2_5_max),
    .MAX_num(max2_5_max_num));
  MAX2 max2_6 (
    .Y(max2_4_max), .X(max2_3_max), .Y_num(max2_4_max_num), .X_num(max2_3_max_num), .MAX(max2_6_max),
    .MAX_num(max2_6_max_num));
  not not_1 (not_1_out, priority_encoder_1_en_out);
  Priority_Encoder #(.select(3), .disabled("Z")) priority_encoder_1 (
    .in0(E0), .in1(E1), .in2(E2), .in3(E3), .in4(E4), .in5(E5), .in6(E6), .in7(E7),
    .out(priority_encoder_1_out), .en_out(priority_encoder_1_en_out), .en_in(1'b1));  // open: gs
  and and_5 (L0, comparator_1_eq, V0);
  and and_6 (L1, comparator_2_eq, V1);
  and and_7 (L2, comparator_3_eq, V2);
  and and_8 (L3, comparator_4_eq, V3);
  and and_9 (L4, comparator_5_eq, V4);
  and and_10 (L5, comparator_6_eq, V5);
  and and_11 (L6, comparator_7_eq, V6);
  and and_12 (L7, comparator_8_eq, V7);
  MAX2 max2_7 (
    .Y(max2_6_max), .X(max2_5_max), .Y_num(max2_6_max_num), .X_num(max2_5_max_num), .MAX_num(max2_7_max_num));  // open: MAX
  or or_1 (or_1_out, ~V0, Hit);  // OR_Gate
  or or_2 (or_2_out, ~V1, Hit);  // OR_Gate
  or or_3 (or_3_out, ~V2, Hit);  // OR_Gate
  or or_4 (or_4_out, ~V3, Hit);  // OR_Gate
  and and_13 (and_13_out, EX_Hit, En, StatReady);
  Counter #(.width(16), .max('hffff), .ongoal("wrap"), .trigger("falling"), .behavior("old")) \u_淘汰记数  (
    .count(or_1_out), .Q(C0), .clk(CLK), .clr(and_14_out));  // open: load, D, carry, preset
  and and_14 (and_14_out, L0, En);
  Counter #(.width(16), .max('hffff), .ongoal("wrap"), .trigger("falling"), .behavior("old")) \u_淘汰记数_2  (
    .count(or_2_out), .Q(C1), .clk(CLK), .clr(and_15_out));  // open: load, D, carry, preset
  and and_15 (and_15_out, L1, En);
  Counter #(.width(16), .max('hffff), .ongoal("wrap"), .trigger("falling"), .behavior("old")) \u_淘汰记数_3  (
    .count(or_3_out), .Q(C2), .clk(CLK), .clr(and_16_out));  // open: load, D, carry, preset
  and and_16 (and_16_out, L2, En);
  Counter #(.width(16), .max('hffff), .ongoal("wrap"), .trigger("falling"), .behavior("old")) \u_淘汰记数_4  (
    .count(or_4_out), .Q(C3), .clk(CLK), .clr(and_17_out));  // open: load, D, carry, preset
  and and_17 (and_17_out, L3, En);
  or or_5 (Hit, L0, L1, L2, L3, L4, L5, L6, L7);
  Demultiplexer #(.select(3), .width(1), .tristate("false"), .disabled("Z"), .enable("false")) demultiplexer_1 (
    .out0(W0), .out1(W1), .out2(W2), .out3(W3), .out4(W4), .out5(W5), .out6(W6), .out7(W7), .in(and_18_out),
    .sel(max2_7_max_num));
  and and_18 (and_18_out, Miss, En, PCReady);
  Demultiplexer #(.select(3), .width(1), .tristate("false"), .disabled(0), .enable("true")) demultiplexer_2 (
    .out0(S0), .out1(S1), .out2(S2), .out3(S3), .out4(S4), .out5(S5), .out6(S6), .out7(S7), .in(and_13_out),
    .sel(priority_encoder_1_out), .en(not_1_out));
  not not_2 (Miss, Hit);
  Register #(.width(32), .trigger("rising"), .Select("low")) \u_分支目标地址  (
    .D(BranchAddr), .en(and_1_out), .Q(\分支目标地址_q ), .clk(CLK));  // open: clr
  Register #(.width(32), .trigger("rising"), .Select("low")) \u_分支目标地址_2  (
    .D(BranchAddr), .en(and_2_out), .Q(\分支目标地址_2_q ), .clk(CLK));  // open: clr
  Register #(.width(32), .trigger("rising"), .Select("low")) \u_分支目标地址_3  (
    .D(BranchAddr), .en(and_3_out), .Q(\分支目标地址_3_q ), .clk(CLK));  // open: clr
  Register #(.width(32), .trigger("rising"), .Select("low")) \u_分支目标地址_4  (
    .D(BranchAddr), .en(and_4_out), .Q(\分支目标地址_4_q ), .clk(CLK));  // open: clr
  assign JumpAddr = L0 ? \分支目标地址_q  : 32'bz;  // Controlled_Buffer controlled_buffer_1
  assign JumpAddr = L1 ? \分支目标地址_2_q  : 32'bz;  // Controlled_Buffer controlled_buffer_2
  assign JumpAddr = L2 ? \分支目标地址_3_q  : 32'bz;  // Controlled_Buffer controlled_buffer_3
  assign JumpAddr = L3 ? \分支目标地址_4_q  : 32'bz;  // Controlled_Buffer controlled_buffer_4
  Demultiplexer #(.select(3), .width(2), .tristate("false"), .disabled("Z"), .enable("false")) demultiplexer_3 (
    .out0(NewJumpState0), .out1(NewJumpState1), .out2(NewJumpState2), .out3(NewJumpState3),
    .out4(NewJumpState4), .out5(NewJumpState5), .out6(NewJumpState6), .out7(NewJumpState7), .in(NewJumpStat),
    .sel(max2_7_max_num));
  Demultiplexer #(.select(3), .width(2), .tristate("false"), .disabled(0), .enable("true")) demultiplexer_4 (
    .out0(JumpState0), .out1(JumpState1), .out2(JumpState2), .out3(JumpState3), .out4(JumpState4),
    .out5(JumpState5), .out6(JumpState6), .out7(JumpState7), .in(JumpStat), .sel(priority_encoder_1_out),
    .en(not_1_out));
  and and_19 (and_19_out, S0, En);
  and and_20 (and_20_out, S1, En);
  and and_21 (and_21_out, S2, En);
  and and_22 (and_22_out, S3, En);
  Comparator #(.width(32), .mode("unsigned")) comparator_9 (.a(EX_PC), .b(Tag0), .eq(comparator_9_eq));  // open: gt, lt
  Comparator #(.width(32), .mode("unsigned")) comparator_10 (
    .a(EX_PC), .b(Tag1), .eq(comparator_10_eq));  // open: gt, lt
  Comparator #(.width(32), .mode("unsigned")) comparator_11 (
    .a(EX_PC), .b(Tag2), .eq(comparator_11_eq));  // open: gt, lt
  Comparator #(.width(32), .mode("unsigned")) comparator_12 (
    .a(EX_PC), .b(Tag3), .eq(comparator_12_eq));  // open: gt, lt
  Comparator #(.width(32), .mode("unsigned")) comparator_13 (
    .a(EX_PC), .b(Tag4), .eq(comparator_13_eq));  // open: gt, lt
  Comparator #(.width(32), .mode("unsigned")) comparator_14 (
    .a(EX_PC), .b(Tag5), .eq(comparator_14_eq));  // open: gt, lt
  Comparator #(.width(32), .mode("unsigned")) comparator_15 (
    .a(EX_PC), .b(Tag6), .eq(comparator_15_eq));  // open: gt, lt
  Comparator #(.width(32), .mode("unsigned")) comparator_16 (
    .a(EX_PC), .b(Tag7), .eq(comparator_16_eq));  // open: gt, lt
  Multiplexer #(.select(1), .width(2), .disabled("Z"), .enable("false")) multiplexer_1 (
    .in0(NewJumpState0), .in1(JumpState0), .out(multiplexer_1_out), .sel(S0));
  or or_6 (or_6_out, and_19_out, and_1_out);
  Multiplexer #(.select(1), .width(2), .disabled("Z"), .enable("false")) multiplexer_2 (
    .in0(NewJumpState1), .in1(JumpState1), .out(multiplexer_2_out), .sel(S1));
  Register #(.width(2), .trigger("rising"), .Select("low")) \u_分支预测历史位  (
    .D(multiplexer_2_out), .en(or_7_out), .Q(\分支预测历史位_q ), .clk(CLK));  // open: clr
  or or_7 (or_7_out, and_20_out, and_2_out);
  Multiplexer #(.select(1), .width(2), .disabled("Z"), .enable("false")) multiplexer_3 (
    .in0(NewJumpState2), .in1(JumpState2), .out(multiplexer_3_out), .sel(S2));
  Register #(.width(2), .trigger("rising"), .Select("low")) \u_分支预测历史位_2  (
    .D(multiplexer_3_out), .en(or_8_out), .Q(\分支预测历史位_2_q ), .clk(CLK));  // open: clr
  or or_8 (or_8_out, and_21_out, and_3_out);
  Multiplexer #(.select(1), .width(2), .disabled("Z"), .enable("false")) multiplexer_4 (
    .in0(NewJumpState3), .in1(JumpState3), .out(multiplexer_4_out), .sel(S3));
  Register #(.width(2), .trigger("rising"), .Select("low")) \u_分支预测历史位_3  (
    .D(multiplexer_4_out), .en(or_9_out), .Q(\分支预测历史位_3_q ), .clk(CLK));  // open: clr
  or or_9 (or_9_out, and_22_out, and_4_out);
  and and_23 (E0, comparator_9_eq, V0);
  and and_24 (E1, comparator_10_eq, V1);
  and and_25 (E2, comparator_11_eq, V2);
  and and_26 (E3, comparator_12_eq, V3);
  and and_27 (E4, comparator_13_eq, V4);
  and and_28 (E5, comparator_14_eq, V5);
  and and_29 (E6, comparator_15_eq, V6);
  and and_30 (E7, comparator_16_eq, V7);
  assign PredictJump = L0 ? \分支预测历史位_4_q  : 2'bz;  // Controlled_Buffer controlled_buffer_5
  Register #(.width(2), .trigger("rising"), .Select("low")) \u_分支预测历史位_4  (
    .D(multiplexer_1_out), .en(or_6_out), .Q(\分支预测历史位_4_q ), .clk(CLK));  // open: clr
  assign EX_PredictJump = E0 ? \分支预测历史位_4_q  : 2'bz;  // Controlled_Buffer controlled_buffer_6
  assign PredictJump = L1 ? \分支预测历史位_q  : 2'bz;  // Controlled_Buffer controlled_buffer_7
  assign EX_PredictJump = E1 ? \分支预测历史位_q  : 2'bz;  // Controlled_Buffer controlled_buffer_8
  assign PredictJump = L2 ? \分支预测历史位_2_q  : 2'bz;  // Controlled_Buffer controlled_buffer_9
  assign EX_PredictJump = E2 ? \分支预测历史位_2_q  : 2'bz;  // Controlled_Buffer controlled_buffer_10
  assign PredictJump = L3 ? \分支预测历史位_3_q  : 2'bz;  // Controlled_Buffer controlled_buffer_11
  assign EX_PredictJump = E3 ? \分支预测历史位_3_q  : 2'bz;  // Controlled_Buffer controlled_buffer_12
  or or_10 (EX_Hit, E0, E1, E2, E3, E4, E5, E6, E7);
  not not_3 (EX_Miss, EX_Hit);
  and and_31 (and_31_out, W4, En);
  Register #(.width(1), .trigger("rising"), .Select("low")) Valid_5 (
    .D(1'b1), .en(and_32_out), .Q(V5), .clk(CLK));  // open: clr
  and and_32 (and_32_out, W5, En);
  Register #(.width(1), .trigger("rising"), .Select("low")) Valid_6 (
    .D(1'b1), .en(and_33_out), .Q(V6), .clk(CLK));  // open: clr
  and and_33 (and_33_out, W6, En);
  Register #(.width(1), .trigger("rising"), .Select("low")) Valid_7 (
    .D(1'b1), .en(and_34_out), .Q(V7), .clk(CLK));  // open: clr
  and and_34 (and_34_out, W7, En);
  Register #(.width(1), .trigger("rising"), .Select("low")) Valid_8 (
    .D(1'b1), .en(and_31_out), .Q(V4), .clk(CLK));  // open: clr
  Register #(.width(32), .trigger("rising"), .Select("low")) \u_分支指令地址_5  (
    .D(PC), .en(and_31_out), .Q(Tag4), .clk(CLK));  // open: clr
  Register #(.width(32), .trigger("rising"), .Select("low")) \u_分支指令地址_6  (
    .D(PC), .en(and_32_out), .Q(Tag5), .clk(CLK));  // open: clr
  Register #(.width(32), .trigger("rising"), .Select("low")) \u_分支指令地址_7  (
    .D(PC), .en(and_33_out), .Q(Tag6), .clk(CLK));  // open: clr
  Register #(.width(32), .trigger("rising"), .Select("low")) \u_分支指令地址_8  (
    .D(PC), .en(and_34_out), .Q(Tag7), .clk(CLK));  // open: clr
  or or_11 (or_11_out, ~V4, Hit);  // OR_Gate
  Counter #(.width(16), .max('hffff), .ongoal("wrap"), .trigger("falling"), .behavior("old")) \u_淘汰记数_5  (
    .count(or_12_out), .Q(C5), .clk(CLK), .clr(and_36_out));  // open: load, D, carry, preset
  or or_12 (or_12_out, ~V5, Hit);  // OR_Gate
  Counter #(.width(16), .max('hffff), .ongoal("wrap"), .trigger("falling"), .behavior("old")) \u_淘汰记数_6  (
    .count(or_13_out), .Q(C6), .clk(CLK), .clr(and_37_out));  // open: load, D, carry, preset
  or or_13 (or_13_out, ~V6, Hit);  // OR_Gate
  Counter #(.width(16), .max('hffff), .ongoal("wrap"), .trigger("falling"), .behavior("old")) \u_淘汰记数_7  (
    .count(or_14_out), .Q(C7), .clk(CLK), .clr(and_38_out));  // open: load, D, carry, preset
  or or_14 (or_14_out, ~V7, Hit);  // OR_Gate
  Counter #(.width(16), .max('hffff), .ongoal("wrap"), .trigger("falling"), .behavior("old")) \u_淘汰记数_8  (
    .count(or_11_out), .Q(C4), .clk(CLK), .clr(and_35_out));  // open: load, D, carry, preset
  and and_35 (and_35_out, L4, En);
  and and_36 (and_36_out, L5, En);
  and and_37 (and_37_out, L6, En);
  and and_38 (and_38_out, L7, En);
  Register #(.width(32), .trigger("rising"), .Select("low")) \u_分支目标地址_5  (
    .D(BranchAddr), .en(and_31_out), .Q(\分支目标地址_5_q ), .clk(CLK));  // open: clr
  Register #(.width(32), .trigger("rising"), .Select("low")) \u_分支目标地址_6  (
    .D(BranchAddr), .en(and_32_out), .Q(\分支目标地址_6_q ), .clk(CLK));  // open: clr
  Register #(.width(32), .trigger("rising"), .Select("low")) \u_分支目标地址_7  (
    .D(BranchAddr), .en(and_33_out), .Q(\分支目标地址_7_q ), .clk(CLK));  // open: clr
  Register #(.width(32), .trigger("rising"), .Select("low")) \u_分支目标地址_8  (
    .D(BranchAddr), .en(and_34_out), .Q(\分支目标地址_8_q ), .clk(CLK));  // open: clr
  assign JumpAddr = L4 ? \分支目标地址_5_q  : 32'bz;  // Controlled_Buffer controlled_buffer_13
  assign JumpAddr = L5 ? \分支目标地址_6_q  : 32'bz;  // Controlled_Buffer controlled_buffer_14
  assign JumpAddr = L6 ? \分支目标地址_7_q  : 32'bz;  // Controlled_Buffer controlled_buffer_15
  assign JumpAddr = L7 ? \分支目标地址_8_q  : 32'bz;  // Controlled_Buffer controlled_buffer_16
  Multiplexer #(.select(1), .width(2), .disabled("Z"), .enable("false")) multiplexer_5 (
    .in0(NewJumpState4), .in1(JumpState4), .out(multiplexer_5_out), .sel(S4));
  and and_39 (and_39_out, S4, En);
  or or_15 (or_15_out, and_39_out, and_31_out);
  Multiplexer #(.select(1), .width(2), .disabled("Z"), .enable("false")) multiplexer_6 (
    .in0(NewJumpState5), .in1(JumpState5), .out(multiplexer_6_out), .sel(S5));
  and and_40 (and_40_out, S5, En);
  or or_16 (or_16_out, and_40_out, and_32_out);
  Multiplexer #(.select(1), .width(2), .disabled("Z"), .enable("false")) multiplexer_7 (
    .in0(NewJumpState0), .in1(JumpState0), .out(multiplexer_7_out), .sel(S6));
  and and_41 (and_41_out, S6, En);
  or or_17 (or_17_out, and_41_out, and_33_out);
  Multiplexer #(.select(1), .width(2), .disabled("Z"), .enable("false")) multiplexer_8 (
    .in0(NewJumpState7), .in1(JumpState7), .out(multiplexer_8_out), .sel(S7));
  and and_42 (and_42_out, S7, En);
  or or_18 (or_18_out, and_42_out, and_34_out);
  Register #(.width(2), .trigger("rising"), .Select("low")) \u_分支预测历史位_5  (
    .D(multiplexer_5_out), .en(or_15_out), .Q(\分支预测历史位_5_q ), .clk(CLK));  // open: clr
  Register #(.width(2), .trigger("rising"), .Select("low")) \u_分支预测历史位_6  (
    .D(multiplexer_6_out), .en(or_16_out), .Q(\分支预测历史位_6_q ), .clk(CLK));  // open: clr
  Register #(.width(2), .trigger("rising"), .Select("low")) \u_分支预测历史位_7  (
    .D(multiplexer_7_out), .en(or_17_out), .Q(\分支预测历史位_7_q ), .clk(CLK));  // open: clr
  Register #(.width(2), .trigger("rising"), .Select("low")) \u_分支预测历史位_8  (
    .D(multiplexer_8_out), .en(or_18_out), .Q(\分支预测历史位_8_q ), .clk(CLK));  // open: clr
  assign PredictJump = L4 ? \分支预测历史位_5_q  : 2'bz;  // Controlled_Buffer controlled_buffer_17
  assign EX_PredictJump = E4 ? \分支预测历史位_5_q  : 2'bz;  // Controlled_Buffer controlled_buffer_18
  assign PredictJump = L5 ? \分支预测历史位_6_q  : 2'bz;  // Controlled_Buffer controlled_buffer_19
  assign EX_PredictJump = E5 ? \分支预测历史位_6_q  : 2'bz;  // Controlled_Buffer controlled_buffer_20
  assign PredictJump = L6 ? \分支预测历史位_7_q  : 2'bz;  // Controlled_Buffer controlled_buffer_21
  assign EX_PredictJump = E6 ? \分支预测历史位_7_q  : 2'bz;  // Controlled_Buffer controlled_buffer_22
  assign PredictJump = L7 ? \分支预测历史位_8_q  : 2'bz;  // Controlled_Buffer controlled_buffer_23
  assign EX_PredictJump = E7 ? \分支预测历史位_8_q  : 2'bz;  // Controlled_Buffer controlled_buffer_24

  // Other names for the same wires on the sheet: JumpState[1:0] = JumpStat; NewJumpState[1:0] = NewJumpStat
endmodule

module BHT (
  input  X1,
  input  X0,
  input  JumpSuccess,
  output Y1,
  output Y0
);

  wire and_1_out, and_2_out, and_3_out, and_4_out, not_1_out, not_2_out, not_3_out, not_4_out, not_5_out;

  not not_1 (not_1_out, X0);
  not not_2 (not_2_out, X1);
  not not_3 (not_3_out, X0);
  not not_4 (not_4_out, X0);
  not not_5 (not_5_out, JumpSuccess);
  and and_1 (and_1_out, X0, JumpSuccess);
  and and_2 (and_2_out, X1, not_1_out);
  and and_3 (and_3_out, not_2_out, not_3_out, JumpSuccess);
  and and_4 (and_4_out, X1, not_4_out, not_5_out);
  or or_1 (Y1, and_1_out, and_2_out);
  or or_2 (Y0, and_3_out, and_4_out);
endmodule

module MAX2 (
  input  [15:0] Y,
  input  [15:0] X,
  input  [2:0] Y_num,
  input  [2:0] X_num,
  output [15:0] MAX,
  output [2:0] MAX_num
);

  wire comparator_1_eq, comparator_1_gt, or_1_out;

  Comparator #(.width(16), .mode("unsigned")) comparator_1 (
    .a(X), .b(Y), .gt(comparator_1_gt), .eq(comparator_1_eq));  // open: lt
  Multiplexer #(.select(1), .width(16), .disabled("Z"), .enable("false")) multiplexer_1 (
    .in0(Y), .in1(X), .out(MAX), .sel(or_1_out));
  or or_1 (or_1_out, comparator_1_gt, comparator_1_eq);
  Multiplexer #(.select(1), .width(3), .disabled("Z"), .enable("false")) multiplexer_2 (
    .in0(Y_num), .in1(X_num), .out(MAX_num), .sel(or_1_out));
endmodule

module \分支预测  (
  input  CLK,
  input  EX_Jalr,
  input  [31:0] PC,
  input  [31:0] EX_PC,
  input  [31:0] EX_jalrAddr,
  input  en,
  input  EX_GuessJ,
  input  [31:0] PC_4,
  input  [31:0] EX_PC_4,
  input  [31:0] EX_JumpAddr,
  input  EX_BranchTaken,
  input  EX_Branch,
  input  [31:0] IR,
  output [31:0] PCout,
  output GuessJ,
  output Ex_PredictErr
);

  wire and_3_out, and_4_out, and_5_out, and_6_out, and_7_out, and_8_out, and_9_out, B, EX_Hit, Hit, J, Miss,
       multiplexer_3_out, or_1_out, or_2_out, or_3_out, or_4_out, or_7_out;
  wire [1:0] and_1_out, bht_1_y0, EX_PredictJump, PredictJump;
  wire [31:0] multiplexer_1_out, multiplexer_4_out, multiplexer_5_out, multiplexer_6_out, multiplexer_7_out,
       PredictAddr, PredictToPC, \分支超前_1_b_addr , \分支超前_1_j_addr ;

  \分支超前  \u_分支超前_1  (.PC(PC), .IR(IR), .B(B), .B_Addr(\分支超前_1_b_addr ), .J(J), .J_Addr(\分支超前_1_j_addr ));
  Multiplexer #(.select(1), .width(32), .disabled("Z"), .enable("false")) multiplexer_1 (
    .in0(PC_4), .in1(\分支超前_1_b_addr ), .out(multiplexer_1_out), .sel(B));
  Multiplexer #(.select(1), .width(32), .disabled("Z"), .enable("false")) multiplexer_2 (
    .in0(multiplexer_1_out), .in1(\分支超前_1_j_addr ), .out(PredictAddr), .sel(J));
  or or_1 (or_1_out, J, B);
  or or_2 (or_2_out, B, J);
  and and_1 (and_1_out[0], or_1_out, Miss);
  and and_2 (and_1_out[1], Miss, or_2_out);
  or or_3 (or_3_out, B, J);
  BHT bht_1 (
    .X1(EX_PredictJump[1]), .X0(EX_PredictJump[0]), .JumpSuccess(EX_BranchTaken), .Y1(bht_1_y0[1]),
    .Y0(bht_1_y0[0]));
  or or_4 (or_4_out, B, J);
  and and_3 (and_3_out, or_3_out, Miss);
  Multiplexer #(.select(1), .width(1), .disabled("Z"), .enable("false")) multiplexer_3 (
    .in0(1'b0), .in1(PredictJump[1]), .out(multiplexer_3_out), .sel(Hit));
  and and_4 (and_4_out, or_4_out, Miss);
  BTB btb_1 (
    .CLK(CLK), .NewJumpStat(and_1_out), .En(en), .JumpStat(bht_1_y0), .EX_PC(EX_PC),
    .BranchAddr(PredictAddr), .PC(PC), .PCReady(and_3_out), .StatReady(EX_Branch), .PredictJump(PredictJump),
    .Hit(Hit), .EX_PredictJump(EX_PredictJump), .Miss(Miss), .EX_Hit(EX_Hit), .JumpAddr(PredictToPC));
  or or_5 (GuessJ, multiplexer_3_out, and_4_out);
  and and_5 (and_5_out, EX_GuessJ, ~EX_BranchTaken);  // AND_Gate
  or or_6 (Ex_PredictErr, and_5_out, and_6_out);
  and and_6 (and_6_out, EX_BranchTaken, ~EX_GuessJ);  // AND_Gate
  or or_7 (or_7_out, B, J);
  and and_7 (and_7_out, or_7_out, Miss);
  Multiplexer #(.select(1), .width(32), .disabled("Z"), .enable("false")) multiplexer_4 (
    .in0(PC_4), .in1(PredictAddr), .out(multiplexer_4_out), .sel(and_7_out));
  and and_8 (and_8_out, Hit, GuessJ);
  Multiplexer #(.select(1), .width(32), .disabled("Z"), .enable("false")) multiplexer_5 (
    .in0(multiplexer_4_out), .in1(PredictToPC), .out(multiplexer_5_out), .sel(and_8_out));
  Multiplexer #(.select(1), .width(32), .disabled("Z"), .enable("false")) multiplexer_6 (
    .in0(EX_JumpAddr), .in1(EX_PC_4), .out(multiplexer_6_out), .sel(and_9_out));
  and and_9 (and_9_out, EX_GuessJ, ~EX_BranchTaken);  // AND_Gate
  Multiplexer #(.select(1), .width(32), .disabled("Z"), .enable("false")) multiplexer_7 (
    .in0(multiplexer_5_out), .in1(multiplexer_6_out), .out(multiplexer_7_out), .sel(Ex_PredictErr));
  Multiplexer #(.select(1), .width(32), .disabled("Z"), .enable("false")) multiplexer_8 (
    .in0(multiplexer_7_out), .in1(EX_jalrAddr), .out(PCout), .sel(EX_Jalr));
endmodule

module \分支超前  (
  input  [31:0] PC,
  input  [31:0] IR,
  output B,
  output [31:0] B_Addr,
  output J,
  output [31:0] J_Addr
);

  wire \单周期硬布线控制器_1_beq , \单周期硬布线控制器_1_bltu , \单周期硬布线控制器_1_bne , \单周期硬布线控制器_1_jal , \单周期硬布线控制器_1_jalr ;
  wire [11:0] shifter_1_out;
  wire [19:0] shifter_2_out;
  wire [31:0] bit_extender_1_out, bit_extender_2_out;

  and and_1 (J, \单周期硬布线控制器_1_jal , ~\单周期硬布线控制器_1_jalr );  // AND_Gate
  \单周期硬布线控制器  \u_单周期硬布线控制器_1  (
    .Funct({IR[30], IR[25], IR[14:12]}), .OP(IR[6:2]), .Jalr(\单周期硬布线控制器_1_jalr ), .Beq(\单周期硬布线控制器_1_beq ),
    .JAL(\单周期硬布线控制器_1_jal ), .Bne(\单周期硬布线控制器_1_bne ), .bltu(\单周期硬布线控制器_1_bltu ));  // open: ALU_OP, MemToReg, MemWrite, ALU_SRC, RegWrite, ecall, S_type, in_3, uret, sb, auipc, sltiu, rs1, rs2, CSRRSI, CSRRCI
  Shifter #(.width(12), .shift("ll")) shifter_1 (
    .in({IR[31], IR[7], IR[30:25], IR[11:8]}), .\dist (4'b0001), .out(shifter_1_out));
  Shifter #(.width(20), .shift("ll")) shifter_2 (
    .in({IR[31], IR[19:12], IR[20], IR[30:21]}), .\dist (5'b00001), .out(shifter_2_out));
  or or_1 (B, \单周期硬布线控制器_1_beq , \单周期硬布线控制器_1_bne , \单周期硬布线控制器_1_bltu );
  assign bit_extender_1_out = {{20{shifter_1_out[11]}}, shifter_1_out};  // Bit_Extender bit_extender_1
  assign bit_extender_2_out = {{12{shifter_2_out[19]}}, shifter_2_out};  // Bit_Extender bit_extender_2
  Adder #(.width(32)) adder_1 (.a(bit_extender_2_out), .b(PC), .out(J_Addr));  // open: cin, cout
  Adder #(.width(32)) adder_2 (.a(bit_extender_1_out), .b(PC), .out(B_Addr));  // open: cin, cout
endmodule

module \冲突处理逻辑_气泡  (
  input  [4:0] ID_R1_num,
  input  [4:0] EX_W_num,
  input  EX_RegWrite,
  input  [4:0] ID_R2_num,
  input  [4:0] MEM_W_num,
  input  MEM_RegWrite,
  input  [4:0] OP,
  input  [4:0] Funct,
  output \数据冲突 
);

  wire and_1_out, and_2_out, and_3_out, and_4_out, and_5_out, and_6_out, comparator_1_eq, comparator_2_eq,
       comparator_3_eq, comparator_4_eq, comparator_5_eq, comparator_6_eq, comparator_7_eq, comparator_8_eq,
       or_1_out, or_2_out, \寄存器使用情况_1_r1 , \寄存器使用情况_1_r2 ;

  \寄存器使用情况  \u_寄存器使用情况_1  (
    .OP2(OP[0]), .OP3(OP[1]), .OP4(OP[2]), .OP5(OP[3]), .OP6(OP[4]), .F12(Funct[0]), .F13(Funct[1]),
    .F14(Funct[2]), .F25(Funct[3]), .F30(Funct[4]), .R1(\寄存器使用情况_1_r1 ), .R2(\寄存器使用情况_1_r2 ));
  Comparator #(.width(5), .mode("twosComplement")) comparator_1 (
    .a(ID_R1_num), .b(EX_W_num), .eq(comparator_1_eq));  // open: gt, lt
  Comparator #(.width(5), .mode("twosComplement")) comparator_2 (
    .a(EX_W_num), .b({5{1'b0}}), .eq(comparator_2_eq));  // open: gt, lt
  Comparator #(.width(5), .mode("twosComplement")) comparator_3 (
    .a(ID_R2_num), .b(EX_W_num), .eq(comparator_3_eq));  // open: gt, lt
  Comparator #(.width(5), .mode("twosComplement")) comparator_4 (
    .a(EX_W_num), .b({5{1'b0}}), .eq(comparator_4_eq));  // open: gt, lt
  and and_1 (and_1_out, comparator_1_eq, EX_RegWrite, ~comparator_2_eq);  // AND_Gate
  and and_2 (and_2_out, comparator_3_eq, EX_RegWrite, ~comparator_4_eq);  // AND_Gate
  Comparator #(.width(5), .mode("twosComplement")) comparator_5 (
    .a(ID_R1_num), .b(MEM_W_num), .eq(comparator_5_eq));  // open: gt, lt
  Comparator #(.width(5), .mode("twosComplement")) comparator_6 (
    .a(MEM_W_num), .b({5{1'b0}}), .eq(comparator_6_eq));  // open: gt, lt
  Comparator #(.width(5), .mode("twosComplement")) comparator_7 (
    .a(ID_R2_num), .b(MEM_W_num), .eq(comparator_7_eq));  // open: gt, lt
  Comparator #(.width(5), .mode("twosComplement")) comparator_8 (
    .a(MEM_W_num), .b({5{1'b0}}), .eq(comparator_8_eq));  // open: gt, lt
  and and_3 (and_3_out, comparator_5_eq, MEM_RegWrite, ~comparator_6_eq);  // AND_Gate
  and and_4 (and_4_out, comparator_7_eq, MEM_RegWrite, ~comparator_8_eq);  // AND_Gate
  or or_1 (or_1_out, and_3_out, and_1_out);
  or or_2 (or_2_out, and_2_out, and_4_out);
  and and_5 (and_5_out, or_1_out, \寄存器使用情况_1_r1 );
  and and_6 (and_6_out, \寄存器使用情况_1_r2 , or_2_out);
  or or_3 (\数据冲突 , and_5_out, and_6_out);
endmodule

module \冲突处理逻辑_重定向  (
  input  [4:0] ID_R1_num,
  input  [4:0] EX_W_num,
  input  EX_RegWrite,
  input  [4:0] EX_OP,
  input  [4:0] ID_R2_num,
  input  [4:0] MEM_W_num,
  input  MEM_RegWrite,
  input  [4:0] OP,
  input  [4:0] Funct,
  output \数据冲突 ,
  output [1:0] R1Forward,
  output Load_Use,
  output [1:0] R2Forward
);

  wire and_3_out, and_4_out, and_5_out, and_6_out, and_9_out, and_10_out, and_11_out, and_12_out,
       comparator_1_eq, comparator_2_eq, comparator_3_eq, comparator_4_eq, comparator_5_eq, comparator_6_eq,
       comparator_7_eq, comparator_8_eq, comparator_9_eq, comparator_10_eq, \EX_R1冲突 , \EX_R2冲突 , \MEM_R1冲突 ,
       \MEM_R2冲突 , or_1_out, or_2_out, or_4_out, or_5_out, \R1使用 , \R2使用 ;

  \寄存器使用情况  \u_寄存器使用情况_1  (
    .OP2(OP[0]), .OP3(OP[1]), .OP4(OP[2]), .OP5(OP[3]), .OP6(OP[4]), .F12(Funct[0]), .F13(Funct[1]),
    .F14(Funct[2]), .F25(Funct[3]), .F30(Funct[4]), .R1(\R1使用 ), .R2(\R2使用 ));
  Comparator #(.width(5), .mode("twosComplement")) comparator_1 (
    .a(ID_R1_num), .b(EX_W_num), .eq(comparator_1_eq));  // open: gt, lt
  Comparator #(.width(5), .mode("twosComplement")) comparator_2 (
    .a(EX_W_num), .b({5{1'b0}}), .eq(comparator_2_eq));  // open: gt, lt
  Comparator #(.width(5), .mode("twosComplement")) comparator_3 (
    .a(ID_R2_num), .b(EX_W_num), .eq(comparator_3_eq));  // open: gt, lt
  Comparator #(.width(5), .mode("twosComplement")) comparator_4 (
    .a(EX_W_num), .b({5{1'b0}}), .eq(comparator_4_eq));  // open: gt, lt
  and and_1 (\EX_R1冲突 , comparator_1_eq, EX_RegWrite, ~comparator_2_eq);  // AND_Gate
  and and_2 (\EX_R2冲突 , comparator_3_eq, EX_RegWrite, ~comparator_4_eq);  // AND_Gate
  and and_3 (and_3_out, \R1使用 , \MEM_R1冲突 );
  and and_4 (and_4_out, \R1使用 , \EX_R1冲突 );
  and and_5 (and_5_out, \R2使用 , \MEM_R2冲突 );
  and and_6 (and_6_out, \R2使用 , \EX_R2冲突 );
  Priority_Encoder #(.select(2), .disabled("Z")) priority_encoder_1 (
    .in0(1'b1), .in1(and_3_out), .in2(and_4_out), .out(R1Forward));  // open: in3, gs, en_out, en_in
  Priority_Encoder #(.select(2), .disabled("Z")) priority_encoder_2 (
    .in0(1'b1), .in1(and_5_out), .in2(and_6_out), .out(R2Forward));  // open: in3, gs, en_out, en_in
  Comparator #(.width(5), .mode("twosComplement")) comparator_5 (
    .a(ID_R1_num), .b(MEM_W_num), .eq(comparator_5_eq));  // open: gt, lt
  Comparator #(.width(5), .mode("twosComplement")) comparator_6 (
    .a(MEM_W_num), .b({5{1'b0}}), .eq(comparator_6_eq));  // open: gt, lt
  Comparator #(.width(5), .mode("twosComplement")) comparator_7 (
    .a(ID_R2_num), .b(MEM_W_num), .eq(comparator_7_eq));  // open: gt, lt
  Comparator #(.width(5), .mode("twosComplement")) comparator_8 (
    .a(MEM_W_num), .b({5{1'b0}}), .eq(comparator_8_eq));  // open: gt, lt
  and and_7 (\MEM_R1冲突 , comparator_5_eq, MEM_RegWrite, ~comparator_6_eq);  // AND_Gate
  and and_8 (\MEM_R2冲突 , comparator_7_eq, MEM_RegWrite, ~comparator_8_eq);  // AND_Gate
  or or_1 (or_1_out, \MEM_R1冲突 , \EX_R1冲突 );
  or or_2 (or_2_out, \EX_R2冲突 , \MEM_R2冲突 );
  and and_9 (and_9_out, or_1_out, \R1使用 );
  and and_10 (and_10_out, \R2使用 , or_2_out);
  and and_11 (and_11_out, \R1使用 , \EX_R1冲突 );
  and and_12 (and_12_out, \EX_R2冲突 , \R2使用 );
  Comparator #(.width(5), .mode("twosComplement")) comparator_9 (
    .a(EX_OP), .b({5{1'b0}}), .eq(comparator_9_eq));  // open: gt, lt
  Comparator #(.width(5), .mode("twosComplement")) comparator_10 (
    .a(EX_OP), .b(5'b01101), .eq(comparator_10_eq));  // open: gt, lt
  or or_3 (\数据冲突 , and_9_out, and_10_out);
  or or_4 (or_4_out, and_11_out, and_12_out);
  or or_5 (or_5_out, comparator_9_eq, comparator_10_eq);
  and and_13 (Load_Use, or_4_out, or_5_out);

  // Notes on the sheet:
  //   lw、lhu
  //   lui
endmodule
module \寄存器使用情况  (
  input  OP2,
  input  OP3,
  input  OP4,
  input  OP5,
  input  OP6,
  input  F12,
  input  F13,
  input  F14,
  input  F25,
  input  F30,
  output R1,
  output R2
);

  wire and_1_out, and_2_out, and_3_out, and_4_out, and_5_out, and_6_out, and_7_out, and_8_out, and_9_out,
       and_10_out, and_11_out, and_12_out, and_13_out, and_14_out, and_15_out, and_16_out, and_17_out,
       and_18_out, and_19_out, and_20_out, and_21_out, and_22_out, and_23_out, and_24_out, and_25_out,
       and_26_out, and_27_out, and_28_out, and_29_out, and_30_out, and_31_out, and_32_out, and_33_out,
       and_34_out, and_35_out, not_1_out, not_2_out, not_3_out, not_4_out, not_5_out, not_6_out, not_7_out,
       not_8_out, not_9_out, not_10_out, not_11_out, not_12_out, not_13_out, not_14_out, not_15_out,
       not_16_out, not_17_out, not_18_out, not_19_out, not_20_out, not_21_out, not_22_out, not_23_out,
       not_24_out, not_25_out, not_26_out, not_27_out, not_28_out, not_29_out, not_30_out, not_31_out,
       not_32_out, not_33_out, not_34_out, not_35_out, not_36_out, not_37_out, not_38_out, not_39_out,
       not_40_out, not_41_out, not_42_out, not_43_out, not_44_out, not_45_out, not_46_out, not_47_out,
       not_48_out, not_49_out, not_50_out, not_51_out, not_52_out, not_53_out, not_54_out, not_55_out,
       not_56_out, not_57_out, not_58_out, not_59_out, not_60_out, not_61_out, not_62_out, not_63_out,
       not_64_out, not_65_out, not_66_out, not_67_out, not_68_out, not_69_out, not_70_out, not_71_out,
       not_72_out, not_73_out, not_74_out, not_75_out, not_76_out, not_77_out, not_78_out, not_79_out,
       not_80_out, not_81_out, not_82_out, not_83_out, not_84_out, not_85_out, not_86_out, not_87_out,
       not_88_out, not_89_out, not_90_out, not_91_out, not_92_out, not_93_out, not_94_out, not_95_out,
       not_96_out, not_97_out, not_98_out, not_99_out, not_100_out, not_101_out, not_102_out, not_103_out,
       not_104_out, not_105_out, not_106_out, not_107_out, not_108_out, not_109_out, not_110_out,
       not_111_out, not_112_out, not_113_out, not_114_out, not_115_out, not_116_out, not_117_out,
       not_118_out, not_119_out, not_120_out, not_121_out, not_122_out, not_123_out, not_124_out,
       not_125_out, not_126_out, not_127_out, not_128_out, not_129_out, not_130_out, not_131_out,
       not_132_out, not_133_out, not_134_out, not_135_out, not_136_out, not_137_out, not_138_out,
       not_139_out, not_140_out, not_141_out, not_142_out, not_143_out, not_144_out, not_145_out,
       not_146_out, not_147_out, not_148_out, not_149_out, not_150_out, not_151_out, not_152_out,
       not_153_out, not_154_out, not_155_out, not_156_out, not_157_out, not_158_out, not_159_out,
       not_160_out, not_161_out, not_162_out, not_163_out, not_164_out, not_165_out, not_166_out,
       not_167_out, not_168_out, not_169_out, not_170_out, not_171_out, not_172_out, not_173_out,
       not_174_out, not_175_out, not_176_out, not_177_out, not_178_out, not_179_out, not_180_out,
       not_181_out, not_182_out, not_183_out, not_184_out, not_185_out, not_186_out, not_187_out,
       not_188_out, not_189_out, not_190_out, not_191_out, not_192_out, not_193_out, not_194_out,
       not_195_out, not_196_out, not_197_out, not_198_out, not_199_out, not_200_out, not_201_out,
       not_202_out, not_203_out, not_204_out, not_205_out, not_206_out, not_207_out, not_208_out,
       not_209_out, not_210_out, not_211_out, not_212_out, not_213_out, not_214_out, not_215_out;

  not not_1 (not_1_out, F30);
  not not_2 (not_2_out, F25);
  not not_3 (not_3_out, F14);
  not not_4 (not_4_out, F13);
  not not_5 (not_5_out, F12);
  not not_6 (not_6_out, OP6);
  not not_7 (not_7_out, OP3);
  not not_8 (not_8_out, OP2);
  not not_9 (not_9_out, F25);
  not not_10 (not_10_out, F14);
  not not_11 (not_11_out, F13);
  not not_12 (not_12_out, F12);
  not not_13 (not_13_out, OP6);
  not not_14 (not_14_out, OP3);
  not not_15 (not_15_out, OP2);
  not not_16 (not_16_out, F30);
  not not_17 (not_17_out, F25);
  not not_18 (not_18_out, OP6);
  not not_19 (not_19_out, OP3);
  not not_20 (not_20_out, OP2);
  not not_21 (not_21_out, F30);
  not not_22 (not_22_out, F25);
  not not_23 (not_23_out, F12);
  not not_24 (not_24_out, OP6);
  not not_25 (not_25_out, OP3);
  not not_26 (not_26_out, OP2);
  not not_27 (not_27_out, F30);
  not not_28 (not_28_out, F25);
  not not_29 (not_29_out, F14);
  not not_30 (not_30_out, F12);
  not not_31 (not_31_out, OP6);
  not not_32 (not_32_out, OP3);
  not not_33 (not_33_out, OP2);
  not not_34 (not_34_out, F30);
  not not_35 (not_35_out, F25);
  not not_36 (not_36_out, F14);
  not not_37 (not_37_out, OP6);
  not not_38 (not_38_out, OP3);
  not not_39 (not_39_out, OP2);
  not not_40 (not_40_out, F14);
  not not_41 (not_41_out, F13);
  not not_42 (not_42_out, F12);
  not not_43 (not_43_out, OP6);
  not not_44 (not_44_out, OP5);
  not not_45 (not_45_out, OP3);
  not not_46 (not_46_out, OP2);
  not not_47 (not_47_out, OP6);
  not not_48 (not_48_out, OP5);
  not not_49 (not_49_out, OP3);
  not not_50 (not_50_out, OP2);
  not not_51 (not_51_out, F12);
  not not_52 (not_52_out, OP6);
  not not_53 (not_53_out, OP5);
  not not_54 (not_54_out, OP3);
  not not_55 (not_55_out, OP2);
  not not_56 (not_56_out, F13);
  not not_57 (not_57_out, F12);
  not not_58 (not_58_out, OP6);
  not not_59 (not_59_out, OP5);
  not not_60 (not_60_out, OP3);
  not not_61 (not_61_out, OP2);
  not not_62 (not_62_out, F14);
  not not_63 (not_63_out, F12);
  not not_64 (not_64_out, OP6);
  not not_65 (not_65_out, OP5);
  not not_66 (not_66_out, OP3);
  not not_67 (not_67_out, OP2);
  not not_68 (not_68_out, F30);
  not not_69 (not_69_out, F25);
  not not_70 (not_70_out, F14);
  not not_71 (not_71_out, F13);
  not not_72 (not_72_out, OP6);
  not not_73 (not_73_out, OP5);
  not not_74 (not_74_out, OP3);
  not not_75 (not_75_out, OP2);
  not not_76 (not_76_out, F30);
  not not_77 (not_77_out, F25);
  not not_78 (not_78_out, F13);
  not not_79 (not_79_out, OP6);
  not not_80 (not_80_out, OP5);
  not not_81 (not_81_out, OP3);
  not not_82 (not_82_out, OP2);
  not not_83 (not_83_out, F25);
  not not_84 (not_84_out, F13);
  not not_85 (not_85_out, OP6);
  not not_86 (not_86_out, OP5);
  not not_87 (not_87_out, OP3);
  not not_88 (not_88_out, OP2);
  not not_89 (not_89_out, F14);
  not not_90 (not_90_out, F12);
  not not_91 (not_91_out, OP6);
  not not_92 (not_92_out, OP5);
  not not_93 (not_93_out, OP4);
  not not_94 (not_94_out, OP3);
  not not_95 (not_95_out, OP2);
  not not_96 (not_96_out, F14);
  not not_97 (not_97_out, F12);
  not not_98 (not_98_out, OP6);
  not not_99 (not_99_out, OP4);
  not not_100 (not_100_out, OP3);
  not not_101 (not_101_out, OP2);
  not not_102 (not_102_out, F30);
  not not_103 (not_103_out, F25);
  not not_104 (not_104_out, F14);
  not not_105 (not_105_out, F13);
  not not_106 (not_106_out, F12);
  not not_107 (not_107_out, OP3);
  not not_108 (not_108_out, OP2);
  not not_109 (not_109_out, F14);
  not not_110 (not_110_out, F13);
  not not_111 (not_111_out, F12);
  not not_112 (not_112_out, OP4);
  not not_113 (not_113_out, OP3);
  not not_114 (not_114_out, OP2);
  not not_115 (not_115_out, F14);
  not not_116 (not_116_out, F13);
  not not_117 (not_117_out, OP4);
  not not_118 (not_118_out, OP3);
  not not_119 (not_119_out, OP2);
  not not_120 (not_120_out, F14);
  not not_121 (not_121_out, F13);
  not not_122 (not_122_out, F12);
  not not_123 (not_123_out, OP4);
  not not_124 (not_124_out, OP3);
  not not_125 (not_125_out, F30);
  not not_126 (not_126_out, F25);
  not not_127 (not_127_out, F13);
  not not_128 (not_128_out, F12);
  not not_129 (not_129_out, OP6);
  not not_130 (not_130_out, OP3);
  not not_131 (not_131_out, OP2);
  not not_132 (not_132_out, F13);
  not not_133 (not_133_out, OP6);
  not not_134 (not_134_out, OP5);
  not not_135 (not_135_out, OP4);
  not not_136 (not_136_out, OP3);
  not not_137 (not_137_out, OP2);
  not not_138 (not_138_out, F12);
  not not_139 (not_139_out, OP4);
  not not_140 (not_140_out, OP3);
  not not_141 (not_141_out, OP2);
  not not_142 (not_142_out, F30);
  not not_143 (not_143_out, F25);
  not not_144 (not_144_out, F14);
  not not_145 (not_145_out, F13);
  not not_146 (not_146_out, F12);
  not not_147 (not_147_out, OP6);
  not not_148 (not_148_out, OP3);
  not not_149 (not_149_out, OP2);
  not not_150 (not_150_out, F25);
  not not_151 (not_151_out, F14);
  not not_152 (not_152_out, F13);
  not not_153 (not_153_out, F12);
  not not_154 (not_154_out, OP6);
  not not_155 (not_155_out, OP3);
  not not_156 (not_156_out, OP2);
  not not_157 (not_157_out, F30);
  not not_158 (not_158_out, F25);
  not not_159 (not_159_out, OP6);
  not not_160 (not_160_out, OP3);
  not not_161 (not_161_out, OP2);
  not not_162 (not_162_out, F30);
  not not_163 (not_163_out, F25);
  not not_164 (not_164_out, F12);
  not not_165 (not_165_out, OP6);
  not not_166 (not_166_out, OP3);
  not not_167 (not_167_out, OP2);
  not not_168 (not_168_out, F30);
  not not_169 (not_169_out, F25);
  not not_170 (not_170_out, F14);
  not not_171 (not_171_out, F12);
  not not_172 (not_172_out, OP6);
  not not_173 (not_173_out, OP3);
  not not_174 (not_174_out, OP2);
  not not_175 (not_175_out, F30);
  not not_176 (not_176_out, F25);
  not not_177 (not_177_out, F14);
  not not_178 (not_178_out, OP6);
  not not_179 (not_179_out, OP3);
  not not_180 (not_180_out, OP2);
  not not_181 (not_181_out, F14);
  not not_182 (not_182_out, F12);
  not not_183 (not_183_out, OP6);
  not not_184 (not_184_out, OP4);
  not not_185 (not_185_out, OP3);
  not not_186 (not_186_out, OP2);
  not not_187 (not_187_out, F30);
  not not_188 (not_188_out, F25);
  not not_189 (not_189_out, F14);
  not not_190 (not_190_out, F13);
  not not_191 (not_191_out, F12);
  not not_192 (not_192_out, OP3);
  not not_193 (not_193_out, OP2);
  not not_194 (not_194_out, F14);
  not not_195 (not_195_out, F13);
  not not_196 (not_196_out, F12);
  not not_197 (not_197_out, OP4);
  not not_198 (not_198_out, OP3);
  not not_199 (not_199_out, OP2);
  not not_200 (not_200_out, F14);
  not not_201 (not_201_out, F13);
  not not_202 (not_202_out, OP4);
  not not_203 (not_203_out, OP3);
  not not_204 (not_204_out, OP2);
  not not_205 (not_205_out, F30);
  not not_206 (not_206_out, F25);
  not not_207 (not_207_out, F13);
  not not_208 (not_208_out, F12);
  not not_209 (not_209_out, OP6);
  not not_210 (not_210_out, OP3);
  not not_211 (not_211_out, OP2);
  not not_212 (not_212_out, F12);
  not not_213 (not_213_out, OP4);
  not not_214 (not_214_out, OP3);
  not not_215 (not_215_out, OP2);
  and and_1 (and_1_out, not_1_out, not_2_out, not_3_out, not_4_out, not_5_out, not_6_out, OP5, OP4, not_7_out, not_8_out);
  and and_2 (and_2_out, F30, not_9_out, not_10_out, not_11_out, not_12_out, not_13_out, OP5, OP4, not_14_out, not_15_out);
  and and_3 (and_3_out, not_16_out, not_17_out, F14, F13, F12, not_18_out, OP5, OP4, not_19_out, not_20_out);
  and and_4 (and_4_out, not_21_out, not_22_out, F14, F13, not_23_out, not_24_out, OP5, OP4, not_25_out, not_26_out);
  and and_5 (and_5_out, not_27_out, not_28_out, not_29_out, F13, not_30_out, not_31_out, OP5, OP4, not_32_out, not_33_out);
  and and_6 (and_6_out, not_34_out, not_35_out, not_36_out, F13, F12, not_37_out, OP5, OP4, not_38_out, not_39_out);
  and and_7 (and_7_out, not_40_out, not_41_out, not_42_out, not_43_out, not_44_out, OP4, not_45_out, not_46_out);
  and and_8 (and_8_out, F14, F13, F12, not_47_out, not_48_out, OP4, not_49_out, not_50_out);
  and and_9 (and_9_out, F14, F13, not_51_out, not_52_out, not_53_out, OP4, not_54_out, not_55_out);
  and and_10 (and_10_out, F14, not_56_out, not_57_out, not_58_out, not_59_out, OP4, not_60_out, not_61_out);
  and and_11 (and_11_out, not_62_out, F13, not_63_out, not_64_out, not_65_out, OP4, not_66_out, not_67_out);
  and and_12 (and_12_out, not_68_out, not_69_out, not_70_out, not_71_out, F12, not_72_out, not_73_out, OP4, not_74_out, not_75_out);
  and and_13 (and_13_out, not_76_out, not_77_out, F14, not_78_out, F12, not_79_out, not_80_out, OP4, not_81_out, not_82_out);
  and and_14 (and_14_out, F30, not_83_out, F14, not_84_out, F12, not_85_out, not_86_out, OP4, not_87_out, not_88_out);
  and and_15 (and_15_out, not_89_out, F13, not_90_out, not_91_out, not_92_out, not_93_out, not_94_out, not_95_out);
  and and_16 (and_16_out, not_96_out, F13, not_97_out, not_98_out, OP5, not_99_out, not_100_out, not_101_out);
  and and_17 (and_17_out, not_102_out, not_103_out, not_104_out, not_105_out, not_106_out, OP6, OP5, OP4, not_107_out, not_108_out);
  and and_18 (and_18_out, not_109_out, not_110_out, not_111_out, OP6, OP5, not_112_out, not_113_out, not_114_out);
  and and_19 (and_19_out, not_115_out, not_116_out, F12, OP6, OP5, not_117_out, not_118_out, not_119_out);
  and and_20 (and_20_out, not_120_out, not_121_out, not_122_out, OP6, OP5, not_123_out, not_124_out, OP2);
  and and_21 (and_21_out, not_125_out, not_126_out, F14, not_127_out, not_128_out, not_129_out, OP5, OP4, not_130_out, not_131_out);
  and and_22 (and_22_out, F14, not_132_out, F12, not_133_out, not_134_out, not_135_out, not_136_out, not_137_out);
  and and_23 (and_23_out, F14, F13, not_138_out, OP6, OP5, not_139_out, not_140_out, not_141_out);
  and and_24 (and_24_out, not_142_out, not_143_out, not_144_out, not_145_out, not_146_out, not_147_out, OP5, OP4, not_148_out, not_149_out);
  and and_25 (and_25_out, F30, not_150_out, not_151_out, not_152_out, not_153_out, not_154_out, OP5, OP4, not_155_out, not_156_out);
  and and_26 (and_26_out, not_157_out, not_158_out, F14, F13, F12, not_159_out, OP5, OP4, not_160_out, not_161_out);
  and and_27 (and_27_out, not_162_out, not_163_out, F14, F13, not_164_out, not_165_out, OP5, OP4, not_166_out, not_167_out);
  and and_28 (and_28_out, not_168_out, not_169_out, not_170_out, F13, not_171_out, not_172_out, OP5, OP4, not_173_out, not_174_out);
  and and_29 (and_29_out, not_175_out, not_176_out, not_177_out, F13, F12, not_178_out, OP5, OP4, not_179_out, not_180_out);
  and and_30 (and_30_out, not_181_out, F13, not_182_out, not_183_out, OP5, not_184_out, not_185_out, not_186_out);
  and and_31 (and_31_out, not_187_out, not_188_out, not_189_out, not_190_out, not_191_out, OP6, OP5, OP4, not_192_out, not_193_out);
  and and_32 (and_32_out, not_194_out, not_195_out, not_196_out, OP6, OP5, not_197_out, not_198_out, not_199_out);
  and and_33 (and_33_out, not_200_out, not_201_out, F12, OP6, OP5, not_202_out, not_203_out, not_204_out);
  and and_34 (and_34_out, not_205_out, not_206_out, F14, not_207_out, not_208_out, not_209_out, OP5, OP4, not_210_out, not_211_out);
  and and_35 (and_35_out, F14, F13, not_212_out, OP6, OP5, not_213_out, not_214_out, not_215_out);
  or or_1 (R2, and_24_out, and_25_out, and_26_out, and_27_out, and_28_out, and_29_out, and_30_out, and_31_out, and_32_out, and_33_out, and_34_out, and_35_out);
  or or_2 (R1, and_1_out, and_2_out, and_3_out, and_4_out, and_5_out, and_6_out, and_7_out, and_8_out, and_9_out, and_10_out, and_11_out, and_12_out, and_13_out, and_14_out, and_15_out, and_16_out, and_17_out, and_18_out, and_19_out, and_20_out, and_21_out, and_22_out, and_23_out);
endmodule
